// Logisim project cpu21-riscv -单周期24+4ccab指令(me).circ as structural Verilog: 19 circuits, main circuit ◇单周期RISC-V
// 单周期硬布线控制器
module \单周期硬布线控制器  (
  input  [4:0] OP,
  input  [4:0] Funct,
  input  in_3,
  output [3:0] ALU_OP,
  output uret,
  output MemToReg,
  output ecall,
  output MemWrite,
  output ALU_SRC,
  output RegWrite,
  output S_type,
  output Beq,
  output Bne,
  output Jalr,
  output JAL,
  output csr,
  output U_Type,
  output u1,
  output u2,
  output LB,
  output BLTU
);

  wire \控制信号自动生成_1_ecall ;

  \运算控制器自动生成  \u_运算控制器自动生成_1  (
    .OP2(OP[0]), .OP3(OP[1]), .OP4(OP[2]), .OP5(OP[3]), .OP6(OP[4]), .F12(Funct[0]), .F13(Funct[1]),
    .F14(Funct[2]), .F25(Funct[3]), .F30(Funct[4]), .S0(ALU_OP[0]), .S1(ALU_OP[1]), .S2(ALU_OP[2]),
    .S3(ALU_OP[3]));
  \控制信号自动生成  \u_控制信号自动生成_1  (
    .OP2(OP[0]), .OP3(OP[1]), .MemToReg(MemToReg), .OP4(OP[2]), .OP5(OP[3]), .OP6(OP[4]), .F12(Funct[0]),
    .MemWrite(MemWrite), .F13(Funct[1]), .F14(Funct[2]), .F25(Funct[3]), .F30(Funct[4]), .ALU_SRC(ALU_SRC),
    .RegWrite(RegWrite), .ecall(\控制信号自动生成_1_ecall ), .S_Type(S_type), .BEQ(Beq), .BNE(Bne), .JALR(Jalr),
    .JAL(JAL), .csr(csr), .BLTU(BLTU), .U_Type(U_Type), .u1(u1), .u2(u2), .LB(LB));
  and and_1 (uret, in_3, \控制信号自动生成_1_ecall );
  and and_2 (ecall, ~in_3, \控制信号自动生成_1_ecall );  // AND_Gate

  // Other names for the same wires on the sheet: IR21 = in_3; OP_CODE[4:0] = OP

  // Notes on the sheet:
  //   控制信号生成，产生数据通路需要的其他控制信号
  //   运算器控制器，根据指令生成运算器功能选择信号
endmodule

// 运算器控制器
module \运算控制器自动生成  (
  input  OP2,
  input  OP3,
  input  OP4,
  input  OP5,
  input  OP6,
  input  F12,
  input  F13,
  input  F14,
  input  F25,
  input  F30,
  output S0,
  output S1,
  output S2,
  output S3
);

  wire and_1_out, and_2_out, and_3_out, and_4_out, and_5_out, and_6_out, and_7_out, and_8_out, and_9_out,
       and_10_out, and_11_out, and_12_out, and_13_out, and_14_out, and_15_out, and_16_out, and_17_out,
       and_18_out, and_19_out, and_20_out, and_21_out, and_22_out, and_23_out, and_24_out, and_25_out,
       and_26_out, and_27_out, and_28_out, and_29_out, and_30_out, and_31_out, and_32_out, and_33_out,
       and_34_out, and_35_out, and_36_out, and_37_out, and_38_out, and_39_out, and_40_out, and_41_out,
       and_42_out, and_43_out, and_44_out, and_45_out, and_46_out, and_47_out, not_1_out, not_2_out,
       not_3_out, not_4_out, not_5_out, not_6_out, not_7_out, not_8_out, not_9_out, not_10_out, not_11_out,
       not_12_out, not_13_out, not_14_out, not_15_out, not_16_out, not_17_out, not_18_out, not_19_out,
       not_20_out, not_21_out, not_22_out, not_23_out, not_24_out, not_25_out, not_26_out, not_27_out,
       not_28_out, not_29_out, not_30_out, not_31_out, not_32_out, not_33_out, not_34_out, not_35_out,
       not_36_out, not_37_out, not_38_out, not_39_out, not_40_out, not_41_out, not_42_out, not_43_out,
       not_44_out, not_45_out, not_46_out, not_47_out, not_48_out, not_49_out, not_50_out, not_51_out,
       not_52_out, not_53_out, not_54_out, not_55_out, not_56_out, not_57_out, not_58_out, not_59_out,
       not_60_out, not_61_out, not_62_out, not_63_out, not_64_out, not_65_out, not_66_out, not_67_out,
       not_68_out, not_69_out, not_70_out, not_71_out, not_72_out, not_73_out, not_74_out, not_75_out,
       not_76_out, not_77_out, not_78_out, not_79_out, not_80_out, not_81_out, not_82_out, not_83_out,
       not_84_out, not_85_out, not_86_out, not_87_out, not_88_out, not_89_out, not_90_out, not_91_out,
       not_92_out, not_93_out, not_94_out, not_95_out, not_96_out, not_97_out, not_98_out, not_99_out,
       not_100_out, not_101_out, not_102_out, not_103_out, not_104_out, not_105_out, not_106_out,
       not_107_out, not_108_out, not_109_out, not_110_out, not_111_out, not_112_out, not_113_out,
       not_114_out, not_115_out, not_116_out, not_117_out, not_118_out, not_119_out, not_120_out,
       not_121_out, not_122_out, not_123_out, not_124_out, not_125_out, not_126_out, not_127_out,
       not_128_out, not_129_out, not_130_out, not_131_out, not_132_out, not_133_out, not_134_out,
       not_135_out, not_136_out, not_137_out, not_138_out, not_139_out, not_140_out, not_141_out,
       not_142_out, not_143_out, not_144_out, not_145_out, not_146_out, not_147_out, not_148_out,
       not_149_out, not_150_out, not_151_out, not_152_out, not_153_out, not_154_out, not_155_out,
       not_156_out, not_157_out, not_158_out, not_159_out, not_160_out, not_161_out, not_162_out,
       not_163_out, not_164_out, not_165_out, not_166_out, not_167_out, not_168_out, not_169_out,
       not_170_out, not_171_out, not_172_out, not_173_out, not_174_out, not_175_out, not_176_out,
       not_177_out, not_178_out, not_179_out, not_180_out, not_181_out, not_182_out, not_183_out,
       not_184_out, not_185_out, not_186_out, not_187_out, not_188_out, not_189_out, not_190_out,
       not_191_out, not_192_out, not_193_out, not_194_out, not_195_out, not_196_out, not_197_out,
       not_198_out, not_199_out, not_200_out, not_201_out, not_202_out, not_203_out, not_204_out,
       not_205_out, not_206_out, not_207_out, not_208_out, not_209_out, not_210_out, not_211_out,
       not_212_out, not_213_out, not_214_out, not_215_out, not_216_out, not_217_out, not_218_out,
       not_219_out, not_220_out, not_221_out, not_222_out, not_223_out, not_224_out, not_225_out,
       not_226_out, not_227_out, not_228_out, not_229_out, not_230_out, not_231_out, not_232_out,
       not_233_out, not_234_out, not_235_out, not_236_out, not_237_out, not_238_out, not_239_out,
       not_240_out, not_241_out, not_242_out, not_243_out, not_244_out, not_245_out, not_246_out,
       not_247_out, not_248_out, not_249_out, not_250_out, not_251_out, not_252_out, not_253_out,
       not_254_out, not_255_out, not_256_out, not_257_out, not_258_out;

  not not_1 (not_1_out, F30);
  not not_2 (not_2_out, F25);
  not not_3 (not_3_out, F14);
  not not_4 (not_4_out, F13);
  not not_5 (not_5_out, F12);
  not not_6 (not_6_out, OP6);
  not not_7 (not_7_out, OP3);
  not not_8 (not_8_out, OP2);
  not not_9 (not_9_out, F30);
  not not_10 (not_10_out, F25);
  not not_11 (not_11_out, OP6);
  not not_12 (not_12_out, OP3);
  not not_13 (not_13_out, OP2);
  not not_14 (not_14_out, F30);
  not not_15 (not_15_out, F25);
  not not_16 (not_16_out, F14);
  not not_17 (not_17_out, F12);
  not not_18 (not_18_out, OP6);
  not not_19 (not_19_out, OP3);
  not not_20 (not_20_out, OP2);
  not not_21 (not_21_out, F14);
  not not_22 (not_22_out, F13);
  not not_23 (not_23_out, F12);
  not not_24 (not_24_out, OP6);
  not not_25 (not_25_out, OP5);
  not not_26 (not_26_out, OP3);
  not not_27 (not_27_out, OP2);
  not not_28 (not_28_out, OP6);
  not not_29 (not_29_out, OP5);
  not not_30 (not_30_out, OP3);
  not not_31 (not_31_out, OP2);
  not not_32 (not_32_out, F13);
  not not_33 (not_33_out, F12);
  not not_34 (not_34_out, OP6);
  not not_35 (not_35_out, OP5);
  not not_36 (not_36_out, OP3);
  not not_37 (not_37_out, OP2);
  not not_38 (not_38_out, F14);
  not not_39 (not_39_out, F12);
  not not_40 (not_40_out, OP6);
  not not_41 (not_41_out, OP5);
  not not_42 (not_42_out, OP3);
  not not_43 (not_43_out, OP2);
  not not_44 (not_44_out, F25);
  not not_45 (not_45_out, F13);
  not not_46 (not_46_out, OP6);
  not not_47 (not_47_out, OP5);
  not not_48 (not_48_out, OP3);
  not not_49 (not_49_out, OP2);
  not not_50 (not_50_out, F14);
  not not_51 (not_51_out, F12);
  not not_52 (not_52_out, OP6);
  not not_53 (not_53_out, OP5);
  not not_54 (not_54_out, OP4);
  not not_55 (not_55_out, OP3);
  not not_56 (not_56_out, OP2);
  not not_57 (not_57_out, F14);
  not not_58 (not_58_out, F12);
  not not_59 (not_59_out, OP6);
  not not_60 (not_60_out, OP4);
  not not_61 (not_61_out, OP3);
  not not_62 (not_62_out, OP2);
  not not_63 (not_63_out, OP3);
  not not_64 (not_64_out, OP2);
  not not_65 (not_65_out, F25);
  not not_66 (not_66_out, F13);
  not not_67 (not_67_out, OP6);
  not not_68 (not_68_out, OP3);
  not not_69 (not_69_out, OP2);
  not not_70 (not_70_out, OP6);
  not not_71 (not_71_out, OP3);
  not not_72 (not_72_out, F14);
  not not_73 (not_73_out, F13);
  not not_74 (not_74_out, F12);
  not not_75 (not_75_out, OP6);
  not not_76 (not_76_out, OP5);
  not not_77 (not_77_out, OP4);
  not not_78 (not_78_out, OP3);
  not not_79 (not_79_out, OP2);
  not not_80 (not_80_out, F25);
  not not_81 (not_81_out, F14);
  not not_82 (not_82_out, F13);
  not not_83 (not_83_out, F12);
  not not_84 (not_84_out, OP6);
  not not_85 (not_85_out, OP3);
  not not_86 (not_86_out, OP2);
  not not_87 (not_87_out, F30);
  not not_88 (not_88_out, F25);
  not not_89 (not_89_out, OP6);
  not not_90 (not_90_out, OP3);
  not not_91 (not_91_out, OP2);
  not not_92 (not_92_out, F30);
  not not_93 (not_93_out, F25);
  not not_94 (not_94_out, F14);
  not not_95 (not_95_out, F12);
  not not_96 (not_96_out, OP6);
  not not_97 (not_97_out, OP3);
  not not_98 (not_98_out, OP2);
  not not_99 (not_99_out, OP6);
  not not_100 (not_100_out, OP5);
  not not_101 (not_101_out, OP3);
  not not_102 (not_102_out, OP2);
  not not_103 (not_103_out, F14);
  not not_104 (not_104_out, F12);
  not not_105 (not_105_out, OP6);
  not not_106 (not_106_out, OP5);
  not not_107 (not_107_out, OP3);
  not not_108 (not_108_out, OP2);
  not not_109 (not_109_out, F30);
  not not_110 (not_110_out, F25);
  not not_111 (not_111_out, F13);
  not not_112 (not_112_out, OP6);
  not not_113 (not_113_out, OP5);
  not not_114 (not_114_out, OP3);
  not not_115 (not_115_out, OP2);
  not not_116 (not_116_out, F14);
  not not_117 (not_117_out, F13);
  not not_118 (not_118_out, F12);
  not not_119 (not_119_out, OP4);
  not not_120 (not_120_out, OP3);
  not not_121 (not_121_out, OP2);
  not not_122 (not_122_out, F14);
  not not_123 (not_123_out, F13);
  not not_124 (not_124_out, OP4);
  not not_125 (not_125_out, OP3);
  not not_126 (not_126_out, OP2);
  not not_127 (not_127_out, F14);
  not not_128 (not_128_out, F13);
  not not_129 (not_129_out, F12);
  not not_130 (not_130_out, OP4);
  not not_131 (not_131_out, OP3);
  not not_132 (not_132_out, OP3);
  not not_133 (not_133_out, OP2);
  not not_134 (not_134_out, F30);
  not not_135 (not_135_out, F25);
  not not_136 (not_136_out, F14);
  not not_137 (not_137_out, F13);
  not not_138 (not_138_out, F12);
  not not_139 (not_139_out, OP6);
  not not_140 (not_140_out, OP3);
  not not_141 (not_141_out, OP2);
  not not_142 (not_142_out, F25);
  not not_143 (not_143_out, F14);
  not not_144 (not_144_out, F13);
  not not_145 (not_145_out, F12);
  not not_146 (not_146_out, OP6);
  not not_147 (not_147_out, OP3);
  not not_148 (not_148_out, OP2);
  not not_149 (not_149_out, F30);
  not not_150 (not_150_out, F25);
  not not_151 (not_151_out, OP6);
  not not_152 (not_152_out, OP3);
  not not_153 (not_153_out, OP2);
  not not_154 (not_154_out, F30);
  not not_155 (not_155_out, F25);
  not not_156 (not_156_out, F14);
  not not_157 (not_157_out, OP6);
  not not_158 (not_158_out, OP3);
  not not_159 (not_159_out, OP2);
  not not_160 (not_160_out, F14);
  not not_161 (not_161_out, F13);
  not not_162 (not_162_out, F12);
  not not_163 (not_163_out, OP6);
  not not_164 (not_164_out, OP5);
  not not_165 (not_165_out, OP3);
  not not_166 (not_166_out, OP2);
  not not_167 (not_167_out, OP6);
  not not_168 (not_168_out, OP5);
  not not_169 (not_169_out, OP3);
  not not_170 (not_170_out, OP2);
  not not_171 (not_171_out, F14);
  not not_172 (not_172_out, F12);
  not not_173 (not_173_out, OP6);
  not not_174 (not_174_out, OP5);
  not not_175 (not_175_out, OP4);
  not not_176 (not_176_out, OP3);
  not not_177 (not_177_out, OP2);
  not not_178 (not_178_out, F14);
  not not_179 (not_179_out, F12);
  not not_180 (not_180_out, OP6);
  not not_181 (not_181_out, OP4);
  not not_182 (not_182_out, OP3);
  not not_183 (not_183_out, OP2);
  not not_184 (not_184_out, F14);
  not not_185 (not_185_out, F13);
  not not_186 (not_186_out, F12);
  not not_187 (not_187_out, OP4);
  not not_188 (not_188_out, OP3);
  not not_189 (not_189_out, OP2);
  not not_190 (not_190_out, F14);
  not not_191 (not_191_out, F13);
  not not_192 (not_192_out, OP4);
  not not_193 (not_193_out, OP3);
  not not_194 (not_194_out, OP2);
  not not_195 (not_195_out, F14);
  not not_196 (not_196_out, F13);
  not not_197 (not_197_out, F12);
  not not_198 (not_198_out, OP4);
  not not_199 (not_199_out, OP3);
  not not_200 (not_200_out, OP3);
  not not_201 (not_201_out, OP2);
  not not_202 (not_202_out, OP6);
  not not_203 (not_203_out, OP3);
  not not_204 (not_204_out, F14);
  not not_205 (not_205_out, F13);
  not not_206 (not_206_out, F12);
  not not_207 (not_207_out, OP6);
  not not_208 (not_208_out, OP5);
  not not_209 (not_209_out, OP4);
  not not_210 (not_210_out, OP3);
  not not_211 (not_211_out, OP2);
  not not_212 (not_212_out, F12);
  not not_213 (not_213_out, OP4);
  not not_214 (not_214_out, OP3);
  not not_215 (not_215_out, OP2);
  not not_216 (not_216_out, F30);
  not not_217 (not_217_out, F25);
  not not_218 (not_218_out, F12);
  not not_219 (not_219_out, OP6);
  not not_220 (not_220_out, OP3);
  not not_221 (not_221_out, OP2);
  not not_222 (not_222_out, F30);
  not not_223 (not_223_out, F25);
  not not_224 (not_224_out, F14);
  not not_225 (not_225_out, F12);
  not not_226 (not_226_out, OP6);
  not not_227 (not_227_out, OP3);
  not not_228 (not_228_out, OP2);
  not not_229 (not_229_out, F30);
  not not_230 (not_230_out, F25);
  not not_231 (not_231_out, F14);
  not not_232 (not_232_out, OP6);
  not not_233 (not_233_out, OP3);
  not not_234 (not_234_out, OP2);
  not not_235 (not_235_out, F12);
  not not_236 (not_236_out, OP6);
  not not_237 (not_237_out, OP5);
  not not_238 (not_238_out, OP3);
  not not_239 (not_239_out, OP2);
  not not_240 (not_240_out, F13);
  not not_241 (not_241_out, F12);
  not not_242 (not_242_out, OP6);
  not not_243 (not_243_out, OP5);
  not not_244 (not_244_out, OP3);
  not not_245 (not_245_out, OP2);
  not not_246 (not_246_out, F14);
  not not_247 (not_247_out, F12);
  not not_248 (not_248_out, OP6);
  not not_249 (not_249_out, OP5);
  not not_250 (not_250_out, OP3);
  not not_251 (not_251_out, OP2);
  not not_252 (not_252_out, F12);
  not not_253 (not_253_out, OP3);
  not not_254 (not_254_out, OP2);
  not not_255 (not_255_out, F12);
  not not_256 (not_256_out, OP4);
  not not_257 (not_257_out, OP3);
  not not_258 (not_258_out, OP2);
  and and_1 (and_1_out, not_1_out, not_2_out, not_3_out, not_4_out, not_5_out, not_6_out, OP5, OP4, not_7_out, not_8_out);
  and and_2 (and_2_out, not_9_out, not_10_out, F14, F13, F12, not_11_out, OP5, OP4, not_12_out, not_13_out);
  and and_3 (and_3_out, not_14_out, not_15_out, not_16_out, F13, not_17_out, not_18_out, OP5, OP4, not_19_out, not_20_out);
  and and_4 (and_4_out, not_21_out, not_22_out, not_23_out, not_24_out, not_25_out, OP4, not_26_out, not_27_out);
  and and_5 (and_5_out, F14, F13, F12, not_28_out, not_29_out, OP4, not_30_out, not_31_out);
  and and_6 (and_6_out, F14, not_32_out, not_33_out, not_34_out, not_35_out, OP4, not_36_out, not_37_out);
  and and_7 (and_7_out, not_38_out, F13, not_39_out, not_40_out, not_41_out, OP4, not_42_out, not_43_out);
  and and_8 (and_8_out, F30, not_44_out, F14, not_45_out, F12, not_46_out, not_47_out, OP4, not_48_out, not_49_out);
  and and_9 (and_9_out, not_50_out, F13, not_51_out, not_52_out, not_53_out, not_54_out, not_55_out, not_56_out);
  and and_10 (and_10_out, not_57_out, F13, not_58_out, not_59_out, OP5, not_60_out, not_61_out, not_62_out);
  and and_11 (and_11_out, F14, F13, F12, OP6, OP5, OP4, not_63_out, not_64_out);
  and and_12 (and_12_out, F30, not_65_out, F14, not_66_out, F12, not_67_out, OP5, OP4, not_68_out, not_69_out);
  and and_13 (and_13_out, not_70_out, OP5, OP4, not_71_out, OP2);
  and and_14 (and_14_out, not_72_out, not_73_out, not_74_out, not_75_out, not_76_out, not_77_out, not_78_out, not_79_out);
  and and_15 (and_15_out, F30, not_80_out, not_81_out, not_82_out, not_83_out, not_84_out, OP5, OP4, not_85_out, not_86_out);
  and and_16 (and_16_out, not_87_out, not_88_out, F14, F13, F12, not_89_out, OP5, OP4, not_90_out, not_91_out);
  and and_17 (and_17_out, not_92_out, not_93_out, not_94_out, F13, not_95_out, not_96_out, OP5, OP4, not_97_out, not_98_out);
  and and_18 (and_18_out, F14, F13, F12, not_99_out, not_100_out, OP4, not_101_out, not_102_out);
  and and_19 (and_19_out, not_103_out, F13, not_104_out, not_105_out, not_106_out, OP4, not_107_out, not_108_out);
  and and_20 (and_20_out, not_109_out, not_110_out, F14, not_111_out, F12, not_112_out, not_113_out, OP4, not_114_out, not_115_out);
  and and_21 (and_21_out, not_116_out, not_117_out, not_118_out, OP6, OP5, not_119_out, not_120_out, not_121_out);
  and and_22 (and_22_out, not_122_out, not_123_out, F12, OP6, OP5, not_124_out, not_125_out, not_126_out);
  and and_23 (and_23_out, not_127_out, not_128_out, not_129_out, OP6, OP5, not_130_out, not_131_out, OP2);
  and and_24 (and_24_out, F14, F13, F12, OP6, OP5, OP4, not_132_out, not_133_out);
  and and_25 (and_25_out, not_134_out, not_135_out, not_136_out, not_137_out, not_138_out, not_139_out, OP5, OP4, not_140_out, not_141_out);
  and and_26 (and_26_out, F30, not_142_out, not_143_out, not_144_out, not_145_out, not_146_out, OP5, OP4, not_147_out, not_148_out);
  and and_27 (and_27_out, not_149_out, not_150_out, F14, F13, F12, not_151_out, OP5, OP4, not_152_out, not_153_out);
  and and_28 (and_28_out, not_154_out, not_155_out, not_156_out, F13, F12, not_157_out, OP5, OP4, not_158_out, not_159_out);
  and and_29 (and_29_out, not_160_out, not_161_out, not_162_out, not_163_out, not_164_out, OP4, not_165_out, not_166_out);
  and and_30 (and_30_out, F14, F13, F12, not_167_out, not_168_out, OP4, not_169_out, not_170_out);
  and and_31 (and_31_out, not_171_out, F13, not_172_out, not_173_out, not_174_out, not_175_out, not_176_out, not_177_out);
  and and_32 (and_32_out, not_178_out, F13, not_179_out, not_180_out, OP5, not_181_out, not_182_out, not_183_out);
  and and_33 (and_33_out, not_184_out, not_185_out, not_186_out, OP6, OP5, not_187_out, not_188_out, not_189_out);
  and and_34 (and_34_out, not_190_out, not_191_out, F12, OP6, OP5, not_192_out, not_193_out, not_194_out);
  and and_35 (and_35_out, not_195_out, not_196_out, not_197_out, OP6, OP5, not_198_out, not_199_out, OP2);
  and and_36 (and_36_out, F14, F13, F12, OP6, OP5, OP4, not_200_out, not_201_out);
  and and_37 (and_37_out, not_202_out, OP5, OP4, not_203_out, OP2);
  and and_38 (and_38_out, not_204_out, not_205_out, not_206_out, not_207_out, not_208_out, not_209_out, not_210_out, not_211_out);
  and and_39 (and_39_out, F14, F13, not_212_out, OP6, OP5, not_213_out, not_214_out, not_215_out);
  and and_40 (and_40_out, not_216_out, not_217_out, F14, F13, not_218_out, not_219_out, OP5, OP4, not_220_out, not_221_out);
  and and_41 (and_41_out, not_222_out, not_223_out, not_224_out, F13, not_225_out, not_226_out, OP5, OP4, not_227_out, not_228_out);
  and and_42 (and_42_out, not_229_out, not_230_out, not_231_out, F13, F12, not_232_out, OP5, OP4, not_233_out, not_234_out);
  and and_43 (and_43_out, F14, F13, not_235_out, not_236_out, not_237_out, OP4, not_238_out, not_239_out);
  and and_44 (and_44_out, F14, not_240_out, not_241_out, not_242_out, not_243_out, OP4, not_244_out, not_245_out);
  and and_45 (and_45_out, not_246_out, F13, not_247_out, not_248_out, not_249_out, OP4, not_250_out, not_251_out);
  and and_46 (and_46_out, F14, F13, not_252_out, OP6, OP5, OP4, not_253_out, not_254_out);
  and and_47 (and_47_out, F14, F13, not_255_out, OP6, OP5, not_256_out, not_257_out, not_258_out);
  or or_1 (S0, and_1_out, and_2_out, and_3_out, and_4_out, and_5_out, and_6_out, and_7_out, and_8_out, and_9_out, and_10_out, and_11_out, and_12_out, and_13_out, and_14_out);
  or or_2 (S1, and_15_out, and_16_out, and_17_out, and_18_out, and_19_out, and_20_out, and_21_out, and_22_out, and_23_out, and_24_out);
  or or_3 (S2, and_25_out, and_26_out, and_27_out, and_28_out, and_29_out, and_30_out, and_31_out, and_32_out, and_33_out, and_34_out, and_35_out, and_36_out, and_37_out, and_38_out, and_39_out);
  or or_4 (S3, and_40_out, and_41_out, and_42_out, and_43_out, and_44_out, and_45_out, and_46_out, and_47_out);
endmodule

module \单周期RISC_V  (
  input  IR1,
  input  IR2,
  input  IR3,
  output RegWrite,
  output MemWrite,
  output [31:0] PC,
  output [31:0] IR,
  output [31:0] RDin,
  output [31:0] MDin,
  output [31:0] LedData
);

  wire ALUequal, ALUge, ALUl, and_1_out, and_2_out, and_3_out, and_5_out, Beq, Bne, CLK, clock_1_out,
       comparator_1_eq, comparator_2_eq, comparator_2_lt, d_ff_1_q, ecall, Go, halt, IR1_t, IR2_t, IR3_t,
       IRA, IRB, IRC, jal, jalr, LB, MemToReg, nand_1_out, not_1_out, not_2_out, not_3_out, not_4_out,
       or_1_out, or_2_out, riscv_probe_1_p2, RST, Stype, Utype, W1, W2, W3, \单周期硬布线控制器_1_alu_src ,
       \单周期硬布线控制器_1_bltu ;
  wire [1:0] or_6_out, priority_encoder_1_out;
  wire [3:0] \单周期硬布线控制器_1_alu_op ;
  wire [4:0] multiplexer_2_out, multiplexer_3_out;
  wire [7:0] multiplexer_8_out;
  wire [11:0] multiplexer_4_out;
  wire [12:0] CNT_num;
  wire [15:0] \总周期数 ;
  wire [31:0] adder_2_out, adder_3_out, ALUresult, bit_extender_1_out, bit_extender_2_out,
       bit_extender_3_out, bit_extender_4_out, LBData, multiplexer_1_out, multiplexer_5_out,
       multiplexer_6_out, PC_4, ram_1_data, regifile_1_r1, shifter_1_out, shifter_2_out, shifter_3_out;

  Button \u_继续运行  (.out(Go));
  Button _1 (.out(IRA));
  Button _2 (.out(IRB));
  Button _3 (.out(IRC));
  LED #(.active("true")) led_1 (.in(W1));
  LED #(.active("true")) led_2 (.in(W2));
  LED #(.active("true")) led_3 (.in(W3));
  Priority_Encoder #(.select(2), .disabled("Z")) priority_encoder_1 (
    .in0(1'b1), .in1(jalr), .in2(jal), .in3(or_1_out), .out(priority_encoder_1_out), .en_in(1'b1));  // open: gs, en_out
  Multiplexer #(.select(2), .width(32), .disabled("Z"), .enable("false")) multiplexer_1 (
    .in0(PC_4), .in1(ALUresult), .in2(adder_3_out), .in3(adder_2_out), .out(multiplexer_1_out),
    .sel(priority_encoder_1_out));
  not not_1 (not_1_out, halt);
  Hex_Digit_Display hex_digit_display_1 (.value(LedData[31:28]));  // open: dp
  not not_2 (not_2_out, ALUequal);
  and and_1 (and_1_out, Beq, ALUequal);
  or or_1 (or_1_out, and_1_out, and_2_out, and_3_out);
  Register #(.width(32), .trigger("rising"), .Select("low")) u_PC (
    .D(multiplexer_1_out), .en(or_2_out), .Q(PC), .clk(CLK), .clr(RST));
  or or_2 (or_2_out, not_1_out, Go);
  Hex_Digit_Display hex_digit_display_2 (.value(LedData[23:20]));  // open: dp
  Hex_Digit_Display hex_digit_display_3 (.value(LedData[27:24]));  // open: dp
  and and_2 (and_2_out, not_2_out, Bne);
  Hex_Digit_Display hex_digit_display_4 (.value(LedData[19:16]));  // open: dp
  Hex_Digit_Display hex_digit_display_5 (.value(LedData[15:12]));  // open: dp
  and and_3 (and_3_out, ALUl, \单周期硬布线控制器_1_bltu );
  // RiscV_Probe riscv_probe_1: pin names not known; wires that end beside it: IR, riscv_probe_1_p2
  Adder #(.width(32)) adder_1 (.a(PC), .b(32'h4), .out(PC_4));  // open: cin, cout
  Hex_Digit_Display hex_digit_display_6 (.value(LedData[11:8]));  // open: dp
  Hex_Digit_Display hex_digit_display_7 (.value(LedData[7:4]));  // open: dp
  // Probe on \总周期数 
  ROM #(.addrWidth(10), .dataWidth(32), .Select("high")) rom_1 (.addr(PC[11:2]), .data(IR));
  Hex_Digit_Display hex_digit_display_8 (.value(LedData[3:0]));  // open: dp
  \单周期硬布线控制器  \u_单周期硬布线控制器_1  (
    .Funct({IR[30], IR[25], IR[14:12]}), .OP(IR[6:2]), .ALU_OP(\单周期硬布线控制器_1_alu_op ), .MemToReg(MemToReg),
    .MemWrite(MemWrite), .ALU_SRC(\单周期硬布线控制器_1_alu_src ), .RegWrite(RegWrite), .ecall(ecall), .S_type(Stype),
    .Jalr(jalr), .Beq(Beq), .JAL(jal), .Bne(Bne), .in_3(IR[21]), .uret(riscv_probe_1_p2), .U_Type(Utype),
    .BLTU(\单周期硬布线控制器_1_bltu ), .LB(LB));  // open: u2, u1, csr
  Multiplexer #(.select(1), .width(5), .disabled("Z"), .enable("false")) multiplexer_2 (
    .in0(IR[19:15]), .in1(5'b10001), .out(multiplexer_2_out), .sel(ecall));
  Multiplexer #(.select(1), .width(5), .disabled("Z"), .enable("false")) multiplexer_3 (
    .in0(IR[24:20]), .in1(5'b01010), .out(multiplexer_3_out), .sel(ecall));
  Multiplexer #(.select(1), .width(12), .disabled("Z"), .enable("false")) multiplexer_4 (
    .in0(IR[31:20]), .in1({IR[31:25], IR[11:7]}), .out(multiplexer_4_out), .sel(Stype));
  or or_3 (IR1_t, IR1, IRA);
  assign bit_extender_1_out = {{20{multiplexer_4_out[11]}}, multiplexer_4_out};  // Bit_Extender bit_extender_1
  assign bit_extender_2_out = {{12{IR[31]}}, IR[31:12]};  // Bit_Extender bit_extender_2
  assign bit_extender_3_out = {{20{IR[31]}}, {IR[31], IR[7], IR[30:25], IR[11:8]}};  // Bit_Extender bit_extender_3
  assign bit_extender_4_out = {{12{IR[31]}}, {IR[31], IR[19:12], IR[20], IR[30:21]}};  // Bit_Extender bit_extender_4
  or or_4 (IR2_t, IR2, IRB);
  Regifile regifile_1 (
    .Din(RDin), .Clk(CLK), .R1(regifile_1_r1), .R2(MDin), .WE(RegWrite), .W_num(IR[11:7]),
    .R1_num(multiplexer_2_out), .R2_num(multiplexer_3_out));
  Shifter #(.width(32), .shift("ll")) shifter_1 (.in(bit_extender_2_out), .\dist (5'b01100), .out(shifter_1_out));
  Shifter #(.width(32), .shift("ll")) shifter_2 (.in(bit_extender_3_out), .\dist (5'b00001), .out(shifter_2_out));
  Shifter #(.width(32), .shift("ll")) shifter_3 (.in(bit_extender_4_out), .\dist (5'b00001), .out(shifter_3_out));
  Multiplexer #(.select(1), .width(32), .disabled("Z"), .enable("false")) multiplexer_5 (
    .in0(MDin), .in1(bit_extender_1_out), .out(multiplexer_5_out), .sel(\单周期硬布线控制器_1_alu_src ));
  Adder #(.width(32)) adder_2 (.a(shifter_2_out), .b(PC), .out(adder_2_out));  // open: cin, cout
  Adder #(.width(32)) adder_3 (.a(shifter_3_out), .b(PC), .out(adder_3_out));  // open: cin, cout
  or or_5 (IR3_t, IR3, IRC);
  ALU alu_1 (
    .X(regifile_1_r1), .Y(multiplexer_5_out), .AluOP(\单周期硬布线控制器_1_alu_op ), .Equal(ALUequal),
    .Result(ALUresult), .out_4(ALUge), .out_6(ALUl));  // open: Result_2
  not not_3 (not_3_out, halt);
  not not_4 (not_4_out, comparator_1_eq);
  Comparator #(.width(32), .mode("twosComplement")) comparator_1 (
    .a(regifile_1_r1), .b(32'h22), .eq(comparator_1_eq));  // open: gt, lt
  Counter #(.width(16), .max('hffff), .ongoal("wrap"), .trigger("rising"), .behavior("new")) counter_1 (
    .load(1'b0), .D({16{1'b0}}), .count(not_3_out), .Q(\总周期数 ), .clk(CLK), .clr(1'b0), .down(1'b0));  // open: carry, preset
  and and_4 (halt, ecall, not_4_out);
  and and_5 (and_5_out, comparator_1_eq, ecall);
  RAM #(.addrWidth(10), .dataWidth(32), .bus("separate"), .Select("high")) ram_1 (
    .addr(ALUresult[11:2]), .din(MDin), .data(ram_1_data), .str(MemWrite), .sel(1'b1), .clk(CLK), .ld(1'b1));  // open: clr
  Register #(.width(32), .trigger("rising"), .Select("low")) register_1 (
    .D(MDin), .en(and_5_out), .Q(LedData), .clk(CLK));  // open: clr
  Multiplexer #(.select(1), .width(32), .disabled("Z"), .enable("false")) multiplexer_6 (
    .in0(ram_1_data), .in1(LBData), .out(multiplexer_6_out), .sel(LB));
  D_Flip_Flop #(.trigger("high"), .Pre_Clr_Positions("LEGACY"), .NegatePresetClear("false"), .enable("true"), .NewFFLayout("false")) d_ff_1 (.Q(d_ff_1_q));  // open: clk, D, Qn, preset, en, reset
  // Probe on 13'h609
  or or_6 (or_6_out[0], Utype, MemToReg);
  Comparator #(.width(13), .mode("twosComplement")) comparator_2 (
    .a(CNT_num), .b(13'h609), .eq(comparator_2_eq), .lt(comparator_2_lt));  // open: gt
  Clock #(.highDuration(1), .lowDuration(1)) clock_1 (.out(clock_1_out));
  or or_7 (or_6_out[1], Utype, jal, jalr);
  Multiplexer #(.select(2), .width(32), .disabled("Z"), .enable("false")) multiplexer_7 (
    .in0(ALUresult), .in1(multiplexer_6_out), .in2(PC_4), .in3(shifter_1_out), .out(RDin), .sel(or_6_out));
  Multiplexer #(.select(2), .width(8), .disabled("Z"), .enable("false")) multiplexer_8 (
    .in0(ram_1_data[7:0]), .in1(ram_1_data[15:8]), .in2(ram_1_data[23:16]), .in3(ram_1_data[31:24]),
    .out(multiplexer_8_out), .sel(ALUresult[1:0]));
  Counter #(.width(13), .max('h1fff), .ongoal("stay"), .trigger("rising"), .behavior("old")) counter_2 (
    .count(comparator_2_lt), .Q(CNT_num), .clk(clock_1_out));  // open: load, D, carry, clr, preset
  assign LBData = {{24{multiplexer_8_out[7]}}, multiplexer_8_out};  // Bit_Extender bit_extender_5
  nand nand_1 (nand_1_out, d_ff_1_q, comparator_2_eq);
  assign CLK = nand_1_out ? clock_1_out : 1'bz;  // Controlled_Buffer controlled_buffer_1
  Pull_Resistor #(.pull(1)) pull_resistor_1 (.node(CLK));

  // Notes on the sheet:
  //   中断源
  //   中断等待指示
  //   数码管输出应该用寄存器锁存，否则显示数据只能一闪而过
  //   数码管输出
  //   指令探针
  //   指令存储器
  //   指令字
  //   contents of rom_1 (hex, n*v repeats v):
  //   100493 100006f 100493 200913 300993 100006f 100493 200913 300993 100006f 100493 200913 300993
  //   100006f 100493 200913 300993 3ec000ef 100413 100493 1f49493 900533 2200893 73 24d493 48463 fedff06f
  //   900533 2200893 73 100493 249493 900533 2200893 73 48463 fedff06f 100493 1f49493 900533 2200893 73
  //   4034d493 900533 2200893 73 4044d493 900533 2200893 73 4044d493 900533 2200893 73 4044d493 900533
  //   2200893 73 4044d493 900533 2200893 73 4044d493 900533 2200893 73 4044d493 900533 2200893 73 4044d493
  //   900533 2200893 73 100413 1f41993 41f9d993 433 c00913 300b13 140413 f47413 800293 100313 499993
  //   89e9b3 1300533 2200893 73 406282b3 fe0294e3 140413 f00f93 1f47433 1c41413 800293 100313 49d993
  //   89e9b3 1300533 2200893 73 406282b3 fe0294e3 1c45413 406b0b33 b0463 f95ff06f 2b3 fff2c293 829293
  //   ff2e293 500533 2200893 73 fff00413 493 84a023 140413 448493 84a023 140413 448493 84a023 140413
  //   448493 84a023 140413 448493 84a023 140413 448493 84a023 140413 448493 84a023 140413 448493 84a023
  //   140413 448493 84a023 140413 448493 84a023 140413 448493 84a023 140413 448493 84a023 140413 448493
  //   84a023 140413 448493 84a023 140413 448493 84a023 140413 448493 84a023 140413 448493 140413 433
  //   3c00493 42983 4aa03 149a2b3 28663 134a023 1442023 ffc48493 fe9412e3 800533 2200893 73 440413 3c00493
  //   fc9416e3 a00893 73 100293 300313 800493 849493 7648493 1449493 900533 2200893 73 800e13 4054d4b3
  //   4064d4b3 900533 2200893 73 fffe0e13 fe0e14e3 a00893 73 800e13 fedc04b7 fff00413 1045413 84e4b3
  //   900533 2200893 73 ba984b7 900533 73 76544b7 900533 73 32104b7 900533 73 fffe0e13 fa0e1ee3 a00893 73
  //   313 1000e13 13 8400493 849493 8348493 400913 891913 490913 849493 8248493 849493 8148493 891913
  //   490913 891913 490913 932023 12484b3 430313 fffe0e13 fe0e18e3 2000e13 313 30483 900533 2200893 73
  //   130313 fffe0e13 fe0e14e3 a00893 73 ff100493 900533 2200893 73 148493 fe9068e3 900533 2200893 73
  //   a00893 73 413 140413 800533 2200893 73 240413 800533 2200893 73 340413 800533 2200893 73 440413
  //   800533 2200893 73 540413 800533 2200893 73 640413 800533 2200893 73 740413 800533 2200893 73 840413
  //   800533 2200893 2200893 73 8067
  //   JAL
  //   JALR
  //   URET
  //   BLTU
  //   CSR
  //   rs1
  //   rs2
  //   rd
  //   I指令
  //   S指令
  //   U指令
  //   B指令
  //   J指令
  //   Beq
  //   Bne
  //   MemToReg
  //   MemWrite
  //   AluOP
  //   AluSrcB
  //   RegWrite
  //   为方便自动评测，需要输出PC，IR，寄存器堆写如数据RDin
  //   RAM写使能MemWrite、RAM写入数据MDin等信号
  //   数据存储器
  //   控制位
  //   暂停节拍，不能为0
  //   戳工具置1进入计数暂停模式，ctrl+k时钟自动运行到对应节拍暂停
  //   ctrl+k关闭时钟连续运行，将控制位置零，进入单步调试模式调试
  //   用这个时钟源需要去掉电路中的其他时钟源
  //   可计数暂停的时钟源
endmodule

// 控制信号生成
module \控制信号自动生成  (
  input  OP2,
  input  OP3,
  input  OP4,
  input  OP5,
  input  OP6,
  input  F12,
  input  F13,
  input  F14,
  input  F25,
  input  F30,
  output MemToReg,
  output MemWrite,
  output ALU_SRC,
  output RegWrite,
  output ecall,
  output S_Type,
  output BEQ,
  output BNE,
  output JALR,
  output JAL,
  output csr,
  output BLTU,
  output U_Type,
  output u1,
  output u2,
  output LB
);

  wire and_3_out, and_4_out, and_5_out, and_6_out, and_7_out, and_8_out, and_9_out, and_10_out, and_11_out,
       and_12_out, and_13_out, and_14_out, and_15_out, and_16_out, and_17_out, and_18_out, and_19_out,
       and_20_out, and_21_out, and_31_out, and_32_out, and_33_out, and_34_out, and_35_out, and_36_out,
       and_37_out, and_38_out, and_39_out, and_40_out, and_41_out, and_42_out, and_43_out, and_44_out,
       and_45_out, and_46_out, and_47_out, and_48_out, not_1_out, not_2_out, not_3_out, not_4_out, not_5_out,
       not_6_out, not_7_out, not_8_out, not_9_out, not_10_out, not_11_out, not_12_out, not_13_out,
       not_14_out, not_15_out, not_16_out, not_17_out, not_18_out, not_19_out, not_20_out, not_21_out,
       not_22_out, not_23_out, not_24_out, not_25_out, not_26_out, not_27_out, not_28_out, not_29_out,
       not_30_out, not_31_out, not_32_out, not_33_out, not_34_out, not_35_out, not_36_out, not_37_out,
       not_38_out, not_39_out, not_40_out, not_41_out, not_42_out, not_43_out, not_44_out, not_45_out,
       not_46_out, not_47_out, not_48_out, not_49_out, not_50_out, not_51_out, not_52_out, not_53_out,
       not_54_out, not_55_out, not_56_out, not_57_out, not_58_out, not_59_out, not_60_out, not_61_out,
       not_62_out, not_63_out, not_64_out, not_65_out, not_66_out, not_67_out, not_68_out, not_69_out,
       not_70_out, not_71_out, not_72_out, not_73_out, not_74_out, not_75_out, not_76_out, not_77_out,
       not_78_out, not_79_out, not_80_out, not_81_out, not_82_out, not_83_out, not_84_out, not_85_out,
       not_86_out, not_87_out, not_88_out, not_89_out, not_90_out, not_91_out, not_92_out, not_93_out,
       not_94_out, not_95_out, not_96_out, not_97_out, not_98_out, not_99_out, not_100_out, not_101_out,
       not_102_out, not_103_out, not_104_out, not_105_out, not_106_out, not_107_out, not_108_out,
       not_109_out, not_110_out, not_111_out, not_112_out, not_113_out, not_114_out, not_115_out,
       not_116_out, not_117_out, not_118_out, not_119_out, not_120_out, not_121_out, not_122_out,
       not_123_out, not_124_out, not_125_out, not_126_out, not_127_out, not_128_out, not_129_out,
       not_130_out, not_131_out, not_132_out, not_133_out, not_134_out, not_135_out, not_136_out,
       not_137_out, not_138_out, not_139_out, not_140_out, not_141_out, not_142_out, not_143_out,
       not_144_out, not_145_out, not_146_out, not_147_out, not_148_out, not_149_out, not_150_out,
       not_151_out, not_152_out, not_153_out, not_154_out, not_155_out, not_156_out, not_157_out,
       not_158_out, not_159_out, not_160_out, not_161_out, not_162_out, not_163_out, not_164_out,
       not_165_out, not_166_out, not_167_out, not_168_out, not_169_out, not_170_out, not_171_out,
       not_172_out, not_173_out, not_174_out, not_175_out, not_176_out, not_177_out, not_178_out,
       not_179_out, not_180_out, not_181_out, not_182_out, not_183_out, not_184_out, not_185_out,
       not_186_out, not_187_out, not_188_out, not_189_out, not_190_out, not_191_out, not_192_out,
       not_193_out, not_194_out, not_195_out, not_196_out, not_197_out, not_198_out, not_199_out,
       not_200_out, not_201_out, not_202_out, not_203_out, not_204_out, not_205_out, not_206_out,
       not_207_out, not_208_out, not_209_out, not_210_out, not_211_out, not_212_out, not_213_out,
       not_214_out, not_215_out, not_216_out, not_217_out, not_218_out, not_219_out, not_220_out,
       not_221_out, not_222_out, not_223_out, not_224_out, not_225_out, not_226_out, not_227_out,
       not_228_out, not_229_out, not_230_out, not_231_out, not_232_out, not_233_out, not_234_out,
       not_235_out, not_236_out, not_237_out, not_238_out, or_1_p3, SLL_decode_p11;

  not not_1 (not_1_out, OP2);
  not not_2 (not_2_out, OP3);
  not not_3 (not_3_out, OP4);
  not not_4 (not_4_out, OP5);
  not not_5 (not_5_out, OP6);
  not not_6 (not_6_out, F12);
  not not_7 (not_7_out, F14);
  not not_8 (not_8_out, OP2);
  not not_9 (not_9_out, OP3);
  not not_10 (not_10_out, OP4);
  not not_11 (not_11_out, OP6);
  not not_12 (not_12_out, F12);
  not not_13 (not_13_out, F14);
  not not_14 (not_14_out, OP2);
  not not_15 (not_15_out, OP3);
  not not_16 (not_16_out, OP5);
  not not_17 (not_17_out, OP6);
  not not_18 (not_18_out, F12);
  not not_19 (not_19_out, F14);
  not not_20 (not_20_out, OP2);
  not not_21 (not_21_out, OP3);
  not not_22 (not_22_out, OP4);
  not not_23 (not_23_out, OP6);
  not not_24 (not_24_out, F12);
  not not_25 (not_25_out, F14);
  not not_26 (not_26_out, OP2);
  not not_27 (not_27_out, OP3);
  not not_28 (not_28_out, OP5);
  not not_29 (not_29_out, OP6);
  not not_30 (not_30_out, F12);
  not not_31 (not_31_out, OP2);
  not not_32 (not_32_out, OP3);
  not not_33 (not_33_out, OP5);
  not not_34 (not_34_out, OP6);
  not not_35 (not_35_out, F13);
  not not_36 (not_36_out, F25);
  not not_37 (not_37_out, F30);
  not not_38 (not_38_out, OP2);
  not not_39 (not_39_out, OP3);
  not not_40 (not_40_out, OP5);
  not not_41 (not_41_out, OP6);
  not not_42 (not_42_out, F25);
  not not_43 (not_43_out, OP2);
  not not_44 (not_44_out, OP3);
  not not_45 (not_45_out, OP5);
  not not_46 (not_46_out, OP6);
  not not_47 (not_47_out, OP2);
  not not_48 (not_48_out, OP3);
  not not_49 (not_49_out, OP3);
  not not_50 (not_50_out, OP4);
  not not_51 (not_51_out, F12);
  not not_52 (not_52_out, F13);
  not not_53 (not_53_out, F14);
  not not_54 (not_54_out, OP3);
  not not_55 (not_55_out, OP6);
  not not_56 (not_56_out, OP2);
  not not_57 (not_57_out, OP3);
  not not_58 (not_58_out, OP5);
  not not_59 (not_59_out, OP6);
  not not_60 (not_60_out, F12);
  not not_61 (not_61_out, F14);
  not not_62 (not_62_out, OP2);
  not not_63 (not_63_out, OP3);
  not not_64 (not_64_out, OP5);
  not not_65 (not_65_out, OP6);
  not not_66 (not_66_out, F12);
  not not_67 (not_67_out, OP2);
  not not_68 (not_68_out, OP3);
  not not_69 (not_69_out, OP5);
  not not_70 (not_70_out, OP6);
  not not_71 (not_71_out, F13);
  not not_72 (not_72_out, F25);
  not not_73 (not_73_out, F30);
  not not_74 (not_74_out, OP2);
  not not_75 (not_75_out, OP3);
  not not_76 (not_76_out, OP6);
  not not_77 (not_77_out, F12);
  not not_78 (not_78_out, F13);
  not not_79 (not_79_out, F14);
  not not_80 (not_80_out, F25);
  not not_81 (not_81_out, OP2);
  not not_82 (not_82_out, OP3);
  not not_83 (not_83_out, OP5);
  not not_84 (not_84_out, OP6);
  not not_85 (not_85_out, OP2);
  not not_86 (not_86_out, OP3);
  not not_87 (not_87_out, OP6);
  not not_88 (not_88_out, F13);
  not not_89 (not_89_out, F25);
  not not_90 (not_90_out, OP3);
  not not_91 (not_91_out, OP6);
  not not_92 (not_92_out, F25);
  not not_93 (not_93_out, F30);
  not not_94 (not_94_out, OP4);
  not not_95 (not_95_out, F12);
  not not_96 (not_96_out, F13);
  not not_97 (not_97_out, F14);
  not not_98 (not_98_out, OP3);
  not not_99 (not_99_out, OP6);
  not not_100 (not_100_out, OP4);
  not not_101 (not_101_out, OP2);
  not not_102 (not_102_out, OP3);
  not not_103 (not_103_out, F12);
  not not_104 (not_104_out, F13);
  not not_105 (not_105_out, F14);
  not not_106 (not_106_out, F25);
  not not_107 (not_107_out, F30);
  not not_108 (not_108_out, OP2);
  not not_109 (not_109_out, OP3);
  not not_110 (not_110_out, OP4);
  not not_111 (not_111_out, OP6);
  not not_112 (not_112_out, F12);
  not not_113 (not_113_out, F14);
  not not_114 (not_114_out, OP2);
  not not_115 (not_115_out, OP3);
  not not_116 (not_116_out, OP4);
  not not_117 (not_117_out, F12);
  not not_118 (not_118_out, F13);
  not not_119 (not_119_out, F14);
  not not_120 (not_120_out, OP2);
  not not_121 (not_121_out, OP3);
  not not_122 (not_122_out, OP4);
  not not_123 (not_123_out, F13);
  not not_124 (not_124_out, F14);
  not not_125 (not_125_out, OP3);
  not not_126 (not_126_out, OP4);
  not not_127 (not_127_out, F12);
  not not_128 (not_128_out, F13);
  not not_129 (not_129_out, F14);
  not not_130 (not_130_out, OP4);
  not not_131 (not_131_out, OP2);
  not not_132 (not_132_out, OP3);
  not not_133 (not_133_out, F12);
  not not_134 (not_134_out, OP4);
  not not_135 (not_135_out, OP3);
  not not_136 (not_136_out, OP2);
  not not_137 (not_137_out, OP3);
  not not_138 (not_138_out, OP6);
  not not_139 (not_139_out, OP2);
  not not_140 (not_140_out, OP3);
  not not_141 (not_141_out, OP5);
  not not_142 (not_142_out, OP6);
  not not_143 (not_143_out, F12);
  not not_144 (not_144_out, F14);
  not not_145 (not_145_out, OP2);
  not not_146 (not_146_out, OP3);
  not not_147 (not_147_out, OP4);
  not not_148 (not_148_out, OP6);
  not not_149 (not_149_out, F12);
  not not_150 (not_150_out, F14);
  not not_151 (not_151_out, OP2);
  not not_152 (not_152_out, OP3);
  not not_153 (not_153_out, OP4);
  not not_154 (not_154_out, F13);
  not not_155 (not_155_out, F14);
  not not_156 (not_156_out, OP3);
  not not_157 (not_157_out, OP4);
  not not_158 (not_158_out, F12);
  not not_159 (not_159_out, F13);
  not not_160 (not_160_out, F14);
  not not_161 (not_161_out, OP2);
  not not_162 (not_162_out, OP3);
  not not_163 (not_163_out, OP4);
  not not_164 (not_164_out, F12);
  not not_165 (not_165_out, OP2);
  not not_166 (not_166_out, OP3);
  not not_167 (not_167_out, OP5);
  not not_168 (not_168_out, OP6);
  not not_169 (not_169_out, F12);
  not not_170 (not_170_out, OP2);
  not not_171 (not_171_out, OP3);
  not not_172 (not_172_out, OP5);
  not not_173 (not_173_out, OP6);
  not not_174 (not_174_out, F13);
  not not_175 (not_175_out, F25);
  not not_176 (not_176_out, F30);
  not not_177 (not_177_out, OP2);
  not not_178 (not_178_out, OP3);
  not not_179 (not_179_out, OP6);
  not not_180 (not_180_out, F12);
  not not_181 (not_181_out, F13);
  not not_182 (not_182_out, F14);
  not not_183 (not_183_out, F25);
  not not_184 (not_184_out, OP2);
  not not_185 (not_185_out, OP3);
  not not_186 (not_186_out, OP5);
  not not_187 (not_187_out, OP6);
  not not_188 (not_188_out, OP2);
  not not_189 (not_189_out, OP3);
  not not_190 (not_190_out, OP6);
  not not_191 (not_191_out, F13);
  not not_192 (not_192_out, F25);
  not not_193 (not_193_out, OP3);
  not not_194 (not_194_out, OP6);
  not not_195 (not_195_out, F25);
  not not_196 (not_196_out, F30);
  not not_197 (not_197_out, OP3);
  not not_198 (not_198_out, OP6);
  not not_199 (not_199_out, OP2);
  not not_200 (not_200_out, OP3);
  not not_201 (not_201_out, OP4);
  not not_202 (not_202_out, OP6);
  not not_203 (not_203_out, F12);
  not not_204 (not_204_out, F14);
  not not_205 (not_205_out, OP2);
  not not_206 (not_206_out, OP3);
  not not_207 (not_207_out, OP4);
  not not_208 (not_208_out, F13);
  not not_209 (not_209_out, F14);
  not not_210 (not_210_out, OP2);
  not not_211 (not_211_out, OP3);
  not not_212 (not_212_out, OP4);
  not not_213 (not_213_out, F12);
  not not_214 (not_214_out, OP2);
  not not_215 (not_215_out, OP3);
  not not_216 (not_216_out, OP6);
  not not_217 (not_217_out, F12);
  not not_218 (not_218_out, F13);
  not not_219 (not_219_out, F14);
  not not_220 (not_220_out, F25);
  not not_221 (not_221_out, OP2);
  not not_222 (not_222_out, OP3);
  not not_223 (not_223_out, OP6);
  not not_224 (not_224_out, F25);
  not not_225 (not_225_out, F30);
  not not_226 (not_226_out, OP2);
  not not_227 (not_227_out, OP3);
  not not_228 (not_228_out, OP6);
  not not_229 (not_229_out, F13);
  not not_230 (not_230_out, F25);
  not not_231 (not_231_out, OP2);
  not not_232 (not_232_out, OP3);
  not not_233 (not_233_out, OP4);
  not not_234 (not_234_out, OP5);
  not not_235 (not_235_out, OP6);
  not not_236 (not_236_out, F12);
  not not_237 (not_237_out, F13);
  not not_238 (not_238_out, F14);
  and and_1 (MemToReg, not_1_out, not_2_out, not_3_out, not_4_out, not_5_out, not_6_out, not_7_out);
  and and_2 (MemWrite, not_8_out, not_9_out, not_10_out, OP5, not_11_out, not_12_out, F13, not_13_out);
  and and_3 (and_3_out, not_14_out, not_15_out, not_16_out, not_17_out, not_18_out, not_19_out);
  and and_4 (and_4_out, not_20_out, not_21_out, not_22_out, not_23_out, not_24_out, F13, not_25_out);
  and and_5 (and_5_out, not_26_out, not_27_out, OP4, not_28_out, not_29_out, not_30_out);
  and and_6 (and_6_out, not_31_out, not_32_out, OP4, not_33_out, not_34_out, not_35_out, not_36_out, not_37_out);
  and and_7 (and_7_out, not_38_out, not_39_out, OP4, not_40_out, not_41_out, F14, not_42_out);
  and and_8 (and_8_out, not_43_out, not_44_out, OP4, not_45_out, not_46_out, F13, F14);
  and and_9 (and_9_out, not_47_out, not_48_out, OP4, OP5, OP6, F13, F14);
  and and_10 (and_10_out, OP2, not_49_out, not_50_out, OP5, OP6, not_51_out, not_52_out, not_53_out);
  and and_11 (and_11_out, OP2, not_54_out, OP4, OP5, not_55_out);
  and and_12 (and_12_out, not_56_out, not_57_out, not_58_out, not_59_out, not_60_out, not_61_out);
  and and_13 (and_13_out, not_62_out, not_63_out, OP4, not_64_out, not_65_out, not_66_out);
  and and_14 (and_14_out, not_67_out, not_68_out, OP4, not_69_out, not_70_out, not_71_out, not_72_out, not_73_out);
  and and_15 (and_15_out, not_74_out, not_75_out, OP4, not_76_out, not_77_out, not_78_out, not_79_out, not_80_out);
  and and_16 (and_16_out, not_81_out, not_82_out, OP4, not_83_out, not_84_out, F13, F14);
  and and_17 (and_17_out, not_85_out, not_86_out, OP4, not_87_out, F12, not_88_out, F14, not_89_out, F30);
  and and_18 (and_18_out, not_90_out, OP4, OP5, not_91_out, F13, not_92_out, not_93_out);
  and and_19 (and_19_out, OP2, not_94_out, OP5, OP6, not_95_out, not_96_out, not_97_out);
  and and_20 (and_20_out, OP2, not_98_out, OP4, OP5, not_99_out);
  and and_21 (and_21_out, OP2, OP3, not_100_out, OP5, OP6);
  and and_22 (ecall, not_101_out, not_102_out, OP4, OP5, OP6, not_103_out, not_104_out, not_105_out, not_106_out, not_107_out);
  and and_23 (S_Type, not_108_out, not_109_out, not_110_out, OP5, not_111_out, not_112_out, F13, not_113_out);
  and and_24 (BEQ, not_114_out, not_115_out, not_116_out, OP5, OP6, not_117_out, not_118_out, not_119_out);
  and and_25 (BNE, not_120_out, not_121_out, not_122_out, OP5, OP6, F12, not_123_out, not_124_out);
  and and_26 (JALR, OP2, not_125_out, not_126_out, OP5, OP6, not_127_out, not_128_out, not_129_out);
  and and_27 (JAL, OP2, OP3, not_130_out, OP5, OP6);
  and and_28 (csr, not_131_out, not_132_out, OP4, OP5, OP6, F13, F14);
  and and_29 (BLTU, F14, F13, not_133_out, OP6, OP5, not_134_out, not_135_out, not_136_out);
  and and_30 (U_Type, OP2, not_137_out, OP4, OP5, not_138_out);
  and and_31 (and_31_out, not_139_out, not_140_out, not_141_out, not_142_out, not_143_out, not_144_out);
  and and_32 (and_32_out, not_145_out, not_146_out, not_147_out, not_148_out, not_149_out, F13, not_150_out);
  and and_33 (and_33_out, not_151_out, not_152_out, not_153_out, OP5, OP6, not_154_out, not_155_out);
  and and_34 (and_34_out, not_156_out, not_157_out, OP5, OP6, not_158_out, not_159_out, not_160_out);
  and and_35 (and_35_out, not_161_out, not_162_out, not_163_out, OP5, OP6, not_164_out, F13, F14);
  and and_36 (and_36_out, not_165_out, not_166_out, OP4, not_167_out, not_168_out, not_169_out);
  and and_37 (and_37_out, not_170_out, not_171_out, OP4, not_172_out, not_173_out, not_174_out, not_175_out, not_176_out);
  and and_38 (and_38_out, not_177_out, not_178_out, OP4, not_179_out, not_180_out, not_181_out, not_182_out, not_183_out);
  and and_39 (and_39_out, not_184_out, not_185_out, OP4, not_186_out, not_187_out, F13, F14);
  and and_40 (and_40_out, not_188_out, not_189_out, OP4, not_190_out, F12, not_191_out, F14, not_192_out, F30);
  and and_41 (and_41_out, not_193_out, OP4, OP5, not_194_out, F13, not_195_out, not_196_out);
  and and_42 (and_42_out, OP2, not_197_out, OP4, OP5, not_198_out);
  and and_43 (and_43_out, not_199_out, not_200_out, not_201_out, OP5, not_202_out, not_203_out, F13, not_204_out);
  and and_44 (and_44_out, not_205_out, not_206_out, not_207_out, OP5, OP6, not_208_out, not_209_out);
  and and_45 (and_45_out, not_210_out, not_211_out, not_212_out, OP5, OP6, not_213_out, F13, F14);
  and and_46 (and_46_out, not_214_out, not_215_out, OP4, OP5, not_216_out, not_217_out, not_218_out, not_219_out, not_220_out);
  and and_47 (and_47_out, not_221_out, not_222_out, OP4, OP5, not_223_out, F13, not_224_out, not_225_out);
  and and_48 (and_48_out, not_226_out, not_227_out, OP4, OP5, not_228_out, F12, not_229_out, F14, not_230_out, F30);
  and and_49 (LB, not_231_out, not_232_out, not_233_out, not_234_out, not_235_out, not_236_out, not_237_out, not_238_out);
  // AND_Gate #(.width(1), .out(01)) SLL_decode: pin names not known; wires that end beside it: OP2, OP3, OP4, OP5, OP6, F12, F13, F14, F25, F30, SLL_decode_p11
  // OR_Gate #(.width(1), .out(01)) or_1: pin names not known; wires that end beside it: SLL_decode_p11, and_21_out, or_1_p3
  or or_2 (ALU_SRC, and_3_out, and_4_out, and_5_out, and_6_out, and_7_out, and_8_out, and_9_out, and_10_out, and_11_out);
  or or_3 (RegWrite, and_12_out, and_13_out, and_14_out, and_15_out, and_16_out, and_17_out, and_18_out, and_19_out, and_20_out, or_1_p3);
  or or_4 (u1, and_31_out, and_32_out, and_33_out, and_34_out, and_35_out, and_36_out, and_37_out, and_38_out, and_39_out, and_40_out, and_41_out, and_42_out);
  or or_5 (u2, and_43_out, and_44_out, and_45_out, and_46_out, and_47_out, and_48_out);
endmodule

// ALU
module ALU (
  input  [31:0] X,
  input  [31:0] Y,
  input  [3:0] AluOP,
  output out_4,
  output Equal,
  output out_6,
  output [31:0] Result,
  output [31:0] Result_2
);

  wire [0:0] comparator_1_lt, comparator_2_lt;
  wire [31:0] adder_1_out, AND_out, divider_1_out, divider_1_rem, multiplier_1_cout, multiplier_1_out,
       NOR_out, OR_out, shifter_1_out, shifter_2_out, shifter_3_out, subtractor_1_out, XOR_out;

  assign AND_out = X & Y;  // AND_Gate AND, 32 bits wide
  assign OR_out = X | Y;  // OR_Gate OR, 32 bits wide
  Shifter #(.width(32), .shift("ll")) shifter_1 (.in(X), .\dist (Y[4:0]), .out(shifter_1_out));
  Shifter #(.width(32), .shift("ar")) shifter_2 (.in(X), .\dist (Y[4:0]), .out(shifter_2_out));
  Shifter #(.width(32), .shift("lr")) shifter_3 (.in(X), .\dist (Y[4:0]), .out(shifter_3_out));
  Multiplier #(.width(32)) multiplier_1 (.a(X), .b(Y), .out(multiplier_1_out), .cout(multiplier_1_cout));  // open: cin
  Divider #(.width(32)) divider_1 (.a(X), .b(Y), .out(divider_1_out), .rem(divider_1_rem));  // open: upper
  Adder #(.width(32)) adder_1 (.a(X), .b(Y), .out(adder_1_out));  // open: cin, cout
  Subtractor #(.width(32)) subtractor_1 (.a(X), .b(Y), .out(subtractor_1_out));  // open: bin, bout
  assign XOR_out = X ^ Y;  // XOR_Gate XOR, 32 bits wide
  assign NOR_out = ~(X | Y);  // NOR_Gate NOR, 32 bits wide
  Comparator #(.width(32), .mode("twosComplement")) comparator_1 (
    .a(X), .b(Y), .eq(Equal), .lt(comparator_1_lt[0]));  // open: gt
  Comparator #(.width(32), .mode("unsigned")) comparator_2 (.a(X), .b(Y), .lt(comparator_2_lt[0]));  // open: gt, eq
  Multiplexer #(.select(4), .width(32), .disabled("Z"), .enable("false")) multiplexer_1 (
    .in0(shifter_1_out), .in1(shifter_2_out), .in2(shifter_3_out), .in3(multiplier_1_out),
    .in4(divider_1_out), .in5(adder_1_out), .in6(subtractor_1_out), .in7(AND_out), .in8(OR_out),
    .in9(XOR_out), .in10(NOR_out), .in11({{31{1'b0}}, comparator_1_lt[0]}),
    .in12({{31{1'b0}}, comparator_2_lt[0]}), .in13({32{1'b0}}), .in14({32{1'b0}}), .in15({32{1'b0}}),
    .out(Result), .sel(AluOP));
  Multiplexer #(.select(4), .width(32), .disabled("Z"), .enable("false")) multiplexer_2 (
    .in0({32{1'b0}}), .in1({32{1'b0}}), .in2({32{1'b0}}), .in3(multiplier_1_cout), .in4(divider_1_rem),
    .in5({32{1'b0}}), .in6({32{1'b0}}), .in7({32{1'b0}}), .in8({32{1'b0}}), .in9({32{1'b0}}),
    .in10({32{1'b0}}), .in11({32{1'b0}}), .in12({32{1'b0}}), .in13({32{1'b0}}), .in14({32{1'b0}}),
    .in15({32{1'b0}}), .out(Result_2), .sel(AluOP));
  Multiplexer #(.select(4), .width(1), .disabled("Z"), .enable("false")) multiplexer_3 (
    .in0(1'b0), .in1(1'b0), .in2(1'b0), .in3(1'b0), .in4(1'b0), .in5(1'b0), .in6(1'b0), .in7(1'b0),
    .in8(1'b0), .in9(1'b0), .in10(1'b0), .in11(comparator_1_lt[0]), .in12(comparator_2_lt[0]), .in13(1'b0),
    .in14(1'b0), .in15(1'b0), .out(out_6), .sel(AluOP));
  not not_1 (out_4, out_6);

  // Other names for the same wires on the sheet: Result2[31:0] = Result_2; S[3:0] = AluOP; tunnel = out_6;
  //   tunnel_t = out_4

  // Notes on the sheet:
  //   不要改变此引脚区域内容，也不要改变ALU封装形式
  //   输入引脚
  //   输出引脚
endmodule

module Regifile (
  input  [31:0] Din,
  input  Clk,
  input  WE,
  input  [4:0] R1_num,
  input  [4:0] W_num,
  input  [4:0] R2_num,
  output [31:0] R1,
  output [31:0] R2
);

  // RegisterFile registerfile_1: pin names not known; wires that end beside it: Din, Clk, WE, W_num, R1_num, R2_num, R1, R2
endmodule

module \理想流水线  (
  output RegWrite,
  output MemWrite,
  output [31:0] IF_PC,
  output [31:0] ID_PC,
  output [31:0] EX_PC,
  output [31:0] M_PC,
  output [31:0] WB_PC,
  output [31:0] RDin,
  output [31:0] MDin,
  output [31:0] LedData
);

  wire ALUequal, ALUge, ALUl, and_1_out, and_2_out, and_3_out, and_4_out, CLK, clock_1_out, comparator_1_eq,
       comparator_1_lt, comparator_2_eq, d_ff_1_q, EX_ecall, ex_mem_1_halt_2, ex_mem_1_jal_2,
       ex_mem_1_jalr_2, ex_mem_1_lb_2, ex_mem_1_memtoreg_2, ex_mem_1_regwrite_2, ex_mem_1_uret_2, exhalt, Go,
       halt, ID_ecall, id_ex_1_alusrcb_2, id_ex_1_beq_2, id_ex_1_bltu_2, id_ex_1_bne_2, id_ex_1_jal_2,
       id_ex_1_lb_2, id_ex_1_memtoreg_2, id_ex_1_memwrite_2, id_ex_1_regwrite_2, id_ex_1_uret_2, IR1, IR2,
       IR3, jal, mem_wb_1_halt_2, mem_wb_1_jal_2, mem_wb_1_jalr_2, nand_1_out, not_1_out, not_2_out,
       not_3_out, or_1_out, or_2_out, RST, Stype, Utype, W1, W2, W3, \单周期硬布线控制器_1_alu_src ,
       \单周期硬布线控制器_1_beq , \单周期硬布线控制器_1_bltu , \单周期硬布线控制器_1_bne , \单周期硬布线控制器_1_csr , \单周期硬布线控制器_1_jalr ,
       \单周期硬布线控制器_1_lb , \单周期硬布线控制器_1_memtoreg , \单周期硬布线控制器_1_memwrite , \单周期硬布线控制器_1_regwrite ,
       \单周期硬布线控制器_1_uret ;
  wire [1:0] id_ex_1_jalr_2, mem_wb_1_memtoreg_2;
  wire [3:0] id_ex_1_aluop_2, \单周期硬布线控制器_1_alu_op ;
  wire [4:0] ex_mem_1_rd_2, id_ex_1_rd_2, multiplexer_2_out, multiplexer_3_out, \WB地址 ;
  wire [11:0] multiplexer_4_out;
  wire [12:0] CNT_num;
  wire [15:0] \LoadUse次数 , \总周期数 , \插入气泡数 , \无条件分支数 , \条件分支成功数 ;
  wire [31:0] ALUresult, bit_extender_1_out, bit_extender_2_out, bit_extender_3_out, EX_IR, ex_mem_1_pc_4_2,
       ex_mem_1_result_2, id_ex_1_imm_1_2, id_ex_1_imm_2_2, id_ex_1_pc_4_2, id_ex_1_r1_2, id_ex_1_r2_2,
       ID_IR, if_id_1_pc_4_2, IF_IR, IR, Jaddress, MEM_IR, mem_wb_1_aluresult_2, mem_wb_1_memdata_2,
       mem_wb_1_pc_4_2, multiplexer_1_out, multiplexer_5_out, multiplexer_6_out, PC_4, ram_1_data,
       regifile_1_r1, regifile_1_r2, shifter_1_out, WB_IR;

  Button \u_总复位  (.out(RST));
  Button _1 (.out(IR1));
  Button _2 (.out(IR2));
  Button _3 (.out(IR3));
  // Probe on \总周期数 
  // Probe on \总周期数 
  Button \u_继续运行  (.out(Go));
  LED #(.active("true")) led_1 (.in(W1));
  LED #(.active("true")) led_2 (.in(W2));
  LED #(.active("true")) led_3 (.in(W3));
  Multiplexer #(.select(2), .width(32), .disabled("Z"), .enable("false")) multiplexer_1 (
    .in0(PC_4), .in1(ALUresult), .in2(Jaddress), .out(multiplexer_1_out), .sel(id_ex_1_jalr_2));  // open: in3
  Hex_Digit_Display hex_digit_display_1 (.value(LedData[31:28]));  // open: dp
  // Probe on IF_PC[19:0]
  // RiscV_Probe riscv_probe_1: pin names not known; wires that end beside it: IF_IR
  or or_1 (or_1_out, not_1_out, Go);
  not not_1 (not_1_out, halt);
  Hex_Digit_Display hex_digit_display_2 (.value(LedData[23:20]));  // open: dp
  Hex_Digit_Display hex_digit_display_3 (.value(LedData[27:24]));  // open: dp
  // Probe on ID_PC[19:0]
  // RiscV_Probe riscv_probe_2: pin names not known; wires that end beside it: ID_IR
  Register #(.width(32), .trigger("rising"), .Select("low")) PC (
    .D(multiplexer_1_out), .en(or_1_out), .Q(IF_PC), .clk(CLK), .clr(RST));
  Hex_Digit_Display hex_digit_display_4 (.value(LedData[15:12]));  // open: dp
  Hex_Digit_Display hex_digit_display_5 (.value(LedData[19:16]));  // open: dp
  Adder #(.width(32)) adder_1 (.a(IF_PC), .b(32'h4), .out(PC_4));  // open: cin, cout
  Hex_Digit_Display hex_digit_display_6 (.value(LedData[7:4]));  // open: dp
  Hex_Digit_Display hex_digit_display_7 (.value(LedData[11:8]));  // open: dp
  // Probe on EX_PC[19:0]
  // RiscV_Probe riscv_probe_3: pin names not known; wires that end beside it: EX_IR
  // RiscV_Probe riscv_probe_4: pin names not known; wires that end beside it: IR
  ROM #(.addrWidth(10), .dataWidth(32), .Select("high")) rom_1 (.addr(IF_PC[11:2]), .data(IR));
  Hex_Digit_Display hex_digit_display_8 (.value(LedData[3:0]));  // open: dp
  or or_2 (or_2_out, id_ex_1_jalr_2[0], id_ex_1_jalr_2[1]);
  // Probe on \总周期数 
  // Probe on M_PC[19:0]
  // RiscV_Probe riscv_probe_5: pin names not known; wires that end beside it: MEM_IR
  IF_ID if_id_1 (
    .PC(IF_PC), .PC_4(PC_4), .IR(IR), .PC_2(ID_PC), .PC_4_2(if_id_1_pc_4_2), .IR_2(ID_IR), .reset(1'b0),
    .flush(or_2_out), .en(1'b1), .CLK(CLK));
  // Probe on \总周期数 
  // Probe on \无条件分支数 
  // Probe on \条件分支成功数 
  // Probe on \插入气泡数 
  // Probe on \LoadUse次数 
  // Probe on IF_PC[11:0]
  // Probe on WB_PC[19:0]
  // RiscV_Probe riscv_probe_6: pin names not known; wires that end beside it: WB_IR
  \单周期硬布线控制器  \u_单周期硬布线控制器_1  (
    .Funct({ID_IR[30], ID_IR[25], ID_IR[14:12]}), .OP(ID_IR[6:2]), .ALU_OP(\单周期硬布线控制器_1_alu_op ),
    .MemToReg(\单周期硬布线控制器_1_memtoreg ), .MemWrite(\单周期硬布线控制器_1_memwrite ), .ALU_SRC(\单周期硬布线控制器_1_alu_src ),
    .RegWrite(\单周期硬布线控制器_1_regwrite ), .ecall(ID_ecall), .S_type(Stype), .Jalr(\单周期硬布线控制器_1_jalr ),
    .Beq(\单周期硬布线控制器_1_beq ), .JAL(jal), .Bne(\单周期硬布线控制器_1_bne ), .in_3(ID_IR[21]), .uret(\单周期硬布线控制器_1_uret ),
    .csr(\单周期硬布线控制器_1_csr ), .U_Type(Utype), .BLTU(\单周期硬布线控制器_1_bltu ), .LB(\单周期硬布线控制器_1_lb ));  // open: u2, u1
  Multiplexer #(.select(1), .width(5), .disabled("Z"), .enable("false")) multiplexer_2 (
    .in0(ID_IR[19:15]), .in1(5'b10001), .out(multiplexer_2_out), .sel(ID_ecall));
  Multiplexer #(.select(1), .width(5), .disabled("Z"), .enable("false")) multiplexer_3 (
    .in0(ID_IR[24:20]), .in1(5'b01010), .out(multiplexer_3_out), .sel(ID_ecall));
  Multiplexer #(.select(1), .width(12), .disabled("Z"), .enable("false")) multiplexer_4 (
    .in0(ID_IR[31:20]), .in1({ID_IR[31:25], ID_IR[11:7]}), .out(multiplexer_4_out), .sel(Stype));
  // Probe on EX_PC[11:0]
  // Probe on ID_PC[11:0]
  assign bit_extender_1_out = {{20{multiplexer_4_out[11]}}, multiplexer_4_out};  // Bit_Extender bit_extender_1
  assign bit_extender_2_out = {{20{ID_IR[31]}}, {ID_IR[31], ID_IR[7], ID_IR[30:25], ID_IR[11:8]}};  // Bit_Extender bit_extender_2
  Multiplexer #(.select(1), .width(32), .disabled("Z"), .enable("false")) multiplexer_5 (
    .in0(bit_extender_2_out), .in1(bit_extender_3_out), .out(multiplexer_5_out), .sel(jal));
  assign bit_extender_3_out = {{12{ID_IR[31]}}, {ID_IR[31], ID_IR[19:12], ID_IR[20], ID_IR[30:21]}};  // Bit_Extender bit_extender_3
  // Probe on M_PC[11:0]
  D_Flip_Flop #(.trigger("high"), .Pre_Clr_Positions("LEGACY"), .NegatePresetClear("false"), .enable("true"), .NewFFLayout("false")) d_ff_1 (.Q(d_ff_1_q));  // open: clk, D, Qn, preset, en, reset
  // Probe on 13'hc
  Regifile regifile_1 (
    .Din(RDin), .Clk(CLK), .R1(regifile_1_r1), .R2(regifile_1_r2), .WE(RegWrite), .W_num(\WB地址 ),
    .R1_num(multiplexer_2_out), .R2_num(multiplexer_3_out));
  // Probe on WB_PC[11:0]
  Comparator #(.width(13), .mode("twosComplement")) comparator_1 (
    .a(CNT_num), .b(13'hc), .eq(comparator_1_eq), .lt(comparator_1_lt));  // open: gt
  Clock #(.highDuration(1), .lowDuration(1)) clock_1 (.out(clock_1_out));
  nand nand_1 (nand_1_out, d_ff_1_q, comparator_1_eq);
  Counter #(.width(13), .max('h1fff), .ongoal("stay"), .trigger("rising"), .behavior("old")) counter_1 (
    .count(comparator_1_lt), .Q(CNT_num), .clk(clock_1_out));  // open: load, D, carry, clr, preset
  ID_EX id_ex_1 (
    .Beq(\单周期硬布线控制器_1_beq ), .Beq_2(id_ex_1_beq_2), .Bne(\单周期硬布线控制器_1_bne ), .Bne_2(id_ex_1_bne_2),
    .MemToReg(\单周期硬布线控制器_1_memtoreg ), .MemToReg_2(id_ex_1_memtoreg_2), .MemWrite(\单周期硬布线控制器_1_memwrite ),
    .MemWrite_2(id_ex_1_memwrite_2), .AluSrcB(\单周期硬布线控制器_1_alu_src ), .AluSrcB_2(id_ex_1_alusrcb_2),
    .RegWrite(\单周期硬布线控制器_1_regwrite ), .RegWrite_2(id_ex_1_regwrite_2), .JAL(jal), .JAL_2(id_ex_1_jal_2),
    .JALR(\单周期硬布线控制器_1_jalr ), .JALR_2(id_ex_1_jalr_2[0]), .URET(\单周期硬布线控制器_1_uret ),
    .URET_2(id_ex_1_uret_2), .S_type(Stype), .U_type(Utype), .BLTU(\单周期硬布线控制器_1_bltu ),
    .BLTU_2(id_ex_1_bltu_2), .csr(\单周期硬布线控制器_1_csr ), .LB(\单周期硬布线控制器_1_lb ), .LB_2(id_ex_1_lb_2),
    .ecall(ID_ecall), .ecall_2(EX_ecall), .AluOP(\单周期硬布线控制器_1_alu_op ), .AluOP_2(id_ex_1_aluop_2),
    .rd(ID_IR[11:7]), .rd_2(id_ex_1_rd_2), .R1(regifile_1_r1), .R1_2(id_ex_1_r1_2), .R2(regifile_1_r2),
    .R2_2(id_ex_1_r2_2), .imm_1(bit_extender_1_out), .imm_1_2(id_ex_1_imm_1_2), .imm_2(multiplexer_5_out),
    .imm_2_2(id_ex_1_imm_2_2), .PC(ID_PC), .PC_2(EX_PC), .PC_4(if_id_1_pc_4_2), .PC_4_2(id_ex_1_pc_4_2),
    .IR(ID_IR), .IR_2(EX_IR), .reset(1'b0), .flush(1'b0), .en(1'b1), .CLK(CLK));  // open: S_type_2, U_type_2, csr_2, imm_3, imm_3_2, rs1f, rs1f_2, rs2f, rs2f_2, 预测跳转, 预测跳转_2
  assign CLK = nand_1_out ? clock_1_out : 1'bz;  // Controlled_Buffer controlled_buffer_1
  or or_3 (id_ex_1_jalr_2[1], and_1_out, and_3_out, and_2_out);
  and and_1 (and_1_out, id_ex_1_beq_2, ALUequal);
  Pull_Resistor #(.pull(1)) pull_resistor_1 (.node(CLK));
  and and_2 (and_2_out, id_ex_1_bne_2, ~ALUequal);  // AND_Gate
  Multiplexer #(.select(1), .width(32), .disabled("Z"), .enable("false")) multiplexer_6 (
    .in0(id_ex_1_r2_2), .in1(id_ex_1_imm_1_2), .out(multiplexer_6_out), .sel(id_ex_1_alusrcb_2));
  Shifter #(.width(32), .shift("ll")) shifter_1 (.in(id_ex_1_imm_2_2), .\dist (5'b00001), .out(shifter_1_out));
  Comparator #(.width(32), .mode("twosComplement")) comparator_2 (
    .a(id_ex_1_r1_2), .b(32'h22), .eq(comparator_2_eq));  // open: gt, lt
  and and_3 (and_3_out, id_ex_1_bltu_2, ALUl);
  ALU alu_1 (
    .X(id_ex_1_r1_2), .Y(multiplexer_6_out), .AluOP(id_ex_1_aluop_2), .Equal(ALUequal), .Result(ALUresult),
    .out_4(ALUge), .out_6(ALUl));  // open: Result_2
  Adder #(.width(32)) adder_2 (.a(shifter_1_out), .b(EX_PC), .out(Jaddress), .cin(1'b0));  // open: cout
  not not_2 (not_2_out, comparator_2_eq);
  and and_4 (and_4_out, comparator_2_eq, EX_ecall);
  not not_3 (not_3_out, halt);
  and and_5 (exhalt, EX_ecall, not_2_out);
  Counter #(.width(16), .max('hffff), .ongoal("wrap"), .trigger("rising"), .behavior("new")) counter_2 (
    .load(1'b0), .D({16{1'b0}}), .count(not_3_out), .Q(\总周期数 ), .clk(CLK), .clr(1'b0), .down(1'b0));  // open: carry, preset
  Register #(.width(32), .trigger("rising"), .Select("low")) register_1 (
    .D(id_ex_1_r2_2), .en(and_4_out), .Q(LedData), .clk(CLK));  // open: clr
  EX_MEM ex_mem_1 (
    .MemToReg(id_ex_1_memtoreg_2), .MemWrite(id_ex_1_memwrite_2), .RegWrite(id_ex_1_regwrite_2),
    .JAL(id_ex_1_jal_2), .JALR(id_ex_1_jalr_2[0]), .URET(id_ex_1_uret_2), .LB(id_ex_1_lb_2), .halt(exhalt),
    .rd(id_ex_1_rd_2), .result(ALUresult), .R2(id_ex_1_r2_2), .PC(EX_PC), .PC_4(id_ex_1_pc_4_2), .IR(EX_IR),
    .MemToReg_2(ex_mem_1_memtoreg_2), .MemWrite_2(MemWrite), .RegWrite_2(ex_mem_1_regwrite_2),
    .JAL_2(ex_mem_1_jal_2), .JALR_2(ex_mem_1_jalr_2), .URET_2(ex_mem_1_uret_2), .LB_2(ex_mem_1_lb_2),
    .halt_2(ex_mem_1_halt_2), .rd_2(ex_mem_1_rd_2), .result_2(ex_mem_1_result_2), .R2_2(MDin), .PC_2(M_PC),
    .PC_4_2(ex_mem_1_pc_4_2), .IR_2(MEM_IR), .reset(1'b0), .flush(1'b0), .en(1'b1), .CLK(CLK));  // open: Uimm, Uimm_2, U_type, U_type_2
  RAM #(.addrWidth(10), .dataWidth(32), .bus("separate"), .Select("high")) ram_1 (
    .addr(ex_mem_1_result_2[11:2]), .din(MDin), .data(ram_1_data), .str(MemWrite), .sel(1'b1), .clk(CLK),
    .ld(1'b1));  // open: clr
  MEM_WB mem_wb_1 (
    .LB(ex_mem_1_lb_2), .MemToReg(ex_mem_1_memtoreg_2), .RegWrite(ex_mem_1_regwrite_2), .JAL(ex_mem_1_jal_2),
    .JALR(ex_mem_1_jalr_2), .URET(ex_mem_1_uret_2), .halt(ex_mem_1_halt_2), .rd(ex_mem_1_rd_2),
    .ALUresult(ex_mem_1_result_2), .MemData(ram_1_data), .PC(M_PC), .PC_4(ex_mem_1_pc_4_2), .IR(MEM_IR),
    .MemToReg_2(mem_wb_1_memtoreg_2[0]), .RegWrite_2(RegWrite), .JAL_2(mem_wb_1_jal_2),
    .JALR_2(mem_wb_1_jalr_2), .halt_2(mem_wb_1_halt_2), .rd_2(\WB地址 ), .ALUresult_2(mem_wb_1_aluresult_2),
    .MemData_2(mem_wb_1_memdata_2), .PC_2(WB_PC), .PC_4_2(mem_wb_1_pc_4_2), .IR_2(WB_IR), .reset(1'b0),
    .flush(1'b0), .en(1'b1), .CLK(CLK));  // open: LB_2, URET_2, Uimm, Uimm_2, U_type, U_type_2
  or or_4 (mem_wb_1_memtoreg_2[1], mem_wb_1_jal_2, mem_wb_1_jalr_2);
  Multiplexer #(.select(2), .width(32), .disabled("Z"), .enable("false")) multiplexer_7 (
    .in0(mem_wb_1_aluresult_2), .in1(mem_wb_1_memdata_2), .in2(mem_wb_1_pc_4_2), .out(RDin),
    .sel(mem_wb_1_memtoreg_2));  // open: in3
  D_Flip_Flop #(.trigger("rising"), .Pre_Clr_Positions("ABOVE_BELOW"), .NegatePresetClear("false"), .enable("true"), .NewFFLayout("true")) d_ff_2 (
    .clk(mem_wb_1_halt_2), .D(1'b1), .Q(halt), .preset(1'b0), .en(1'b1), .reset(Go));  // open: Qn

  // Other names for the same wires on the sheet: MEM_PC[31:0] = M_PC

  // Notes on the sheet:
  //   中断源
  //   时空图监测，可删除
  //   中断等待指示
  //   数码管输出
  //   指令探针
  //   指令存储器
  //   contents of rom_1 (hex, n*v repeats v):
  //   413 493 913 993 46413 14e493 296913 39e993 842023 942223 1242423 1342623 a00893 493 913 993 73
  //   JAL
  //   JALR
  //   CSR
  //   rs1
  //   rs2
  //   rd
  //   I指令
  //   S指令
  //   B指令
  //   J指令
  //   Beq
  //   Bne
  //   MemToReg
  //   MemWrite
  //   AluOP
  //   AluSrcB
  //   RegWrite
  //   控制位
  //   流水调试日志用
  //   暂停节拍，不能为0
  //   戳工具置1进入计数暂停模式，ctrl+k时钟自动运行到对应节拍暂停
  //   R1
  //   R2
  //   rd
  //   imm1
  //   imm2
  //   可计数暂停的时钟源
  //   为方便自动评测，需要输出流水线各段保存的PC值，注意是PC不是PC+4，另外ID段寄存器写入信息，Mem段内存写入信息也要输出
  //   ALUresult
  //   ReegWrite
  //   数据存储器
  //   MemtoReg
  //   JAL
  //   JALR
  //   LBU
endmodule

module \气泡流水线  (
  output RegWrite,
  output MemWrite,
  output [31:0] IF_PC,
  output [31:0] ID_PC,
  output [31:0] EX_PC,
  output [31:0] M_PC,
  output [31:0] WB_PC,
  output [31:0] RDin,
  output [31:0] MDin,
  output [31:0] LedData
);

  wire ALUequal, ALUge, ALUl, and_1_out, and_2_out, and_3_out, and_4_out, and_5_out, and_6_out, branch, CLK,
       clock_1_out, comparator_1_eq, comparator_1_lt, comparator_2_eq, d_ff_1_q, EX_ecall, ex_mem_1_halt_2,
       ex_mem_1_jal_2, ex_mem_1_jalr_2, ex_mem_1_lb_2, ex_mem_1_memtoreg_2, ex_mem_1_regwrite_2,
       ex_mem_1_uret_2, exhalt, flush, Go, halt, ID_ecall, id_ex_1_p28, id_ex_1_p30, id_ex_1_p31,
       id_ex_1_p32, id_ex_1_p34, id_ex_1_p35, id_ex_1_p36, id_ex_1_p37, id_ex_1_p39, id_ex_1_p40,
       id_ex_1_p42, IR1, IR2, IR3, jal, mem_wb_1_halt_2, mem_wb_1_jal_2, mem_wb_1_jalr_2, nand_1_out,
       not_1_out, not_2_out, not_3_out, not_4_out, not_5_out, not_6_out, not_7_out, or_1_out, or_3_out,
       or_5_out, RST, Stype, Utype, W1, W2, W3, \冲突 , \单周期硬布线控制器_1_alu_src , \单周期硬布线控制器_1_beq ,
       \单周期硬布线控制器_1_bltu , \单周期硬布线控制器_1_bne , \单周期硬布线控制器_1_csr , \单周期硬布线控制器_1_jalr , \单周期硬布线控制器_1_lb ,
       \单周期硬布线控制器_1_memtoreg , \单周期硬布线控制器_1_memwrite , \单周期硬布线控制器_1_regwrite , \单周期硬布线控制器_1_u1 ,
       \单周期硬布线控制器_1_u2 , \单周期硬布线控制器_1_uret ;
  wire [1:0] id_ex_1_p33, mem_wb_1_memtoreg_2;
  wire [3:0] id_ex_1_p38, \单周期硬布线控制器_1_alu_op ;
  wire [4:0] EX_rd, MEM_rd, multiplexer_2_out, multiplexer_3_out, \WB地址 ;
  wire [11:0] multiplexer_4_out;
  wire [12:0] CNT_num;
  wire [15:0] \LoadUse次数 , \总周期数 , \插入气泡数 , \无条件分支数 , \条件分支成功数 ;
  wire [31:0] ALUresult, bit_extender_1_out, bit_extender_2_out, bit_extender_3_out, EX_IR, ex_mem_1_pc_4_2,
       ex_mem_1_result_2, id_ex_1_p44, id_ex_1_p45, id_ex_1_p47, id_ex_1_p48, id_ex_1_p50, ID_IR,
       if_id_1_pc_4_2, IF_IR, IR, Jaddress, MEM_IR, mem_wb_1_aluresult_2, mem_wb_1_memdata_2,
       mem_wb_1_pc_4_2, multiplexer_1_out, multiplexer_5_out, multiplexer_6_out, PC_4, ram_1_data,
       regifile_1_r1, regifile_1_r2, shifter_1_out, WB_IR;

  Button \u_总复位  (.out(RST));
  Button _1 (.out(IR1));
  Button _2 (.out(IR2));
  Button _3 (.out(IR3));
  // Probe on \总周期数 
  // Probe on \总周期数 
  Button \u_继续运行  (.out(Go));
  LED #(.active("true")) led_1 (.in(W1));
  LED #(.active("true")) led_2 (.in(W2));
  LED #(.active("true")) led_3 (.in(W3));
  Hex_Digit_Display hex_digit_display_1 (.value(LedData[31:28]));  // open: dp
  // Probe on IF_PC[19:0]
  // RiscV_Probe riscv_probe_1: pin names not known; wires that end beside it: IF_IR
  Hex_Digit_Display hex_digit_display_2 (.value(LedData[23:20]));  // open: dp
  Hex_Digit_Display hex_digit_display_3 (.value(LedData[27:24]));  // open: dp
  // Probe on ID_PC[19:0]
  // RiscV_Probe riscv_probe_2: pin names not known; wires that end beside it: ID_IR
  Multiplexer #(.select(2), .width(32), .disabled("Z"), .enable("false")) multiplexer_1 (
    .in0(PC_4), .in1(ALUresult), .in2(Jaddress), .out(multiplexer_1_out), .sel(id_ex_1_p33));  // open: in3
  not not_1 (not_1_out, \冲突 );
  not not_2 (not_2_out, halt);
  Hex_Digit_Display hex_digit_display_4 (.value(LedData[19:16]));  // open: dp
  Hex_Digit_Display hex_digit_display_5 (.value(LedData[15:12]));  // open: dp
  and and_1 (and_1_out, not_1_out, or_1_out);
  or or_1 (or_1_out, not_2_out, Go);
  Hex_Digit_Display hex_digit_display_6 (.value(LedData[7:4]));  // open: dp
  Hex_Digit_Display hex_digit_display_7 (.value(LedData[11:8]));  // open: dp
  // Probe on EX_PC[19:0]
  // RiscV_Probe riscv_probe_3: pin names not known; wires that end beside it: EX_IR
  Register #(.width(32), .trigger("rising"), .Select("low")) PC (
    .D(multiplexer_1_out), .en(and_1_out), .Q(IF_PC), .clk(CLK), .clr(RST));
  Hex_Digit_Display hex_digit_display_8 (.value(LedData[3:0]));  // open: dp
  Adder #(.width(32)) adder_1 (.a(IF_PC), .b(32'h4), .out(PC_4));  // open: cin, cout
  // Probe on \总周期数 
  // Probe on M_PC[19:0]
  // RiscV_Probe riscv_probe_4: pin names not known; wires that end beside it: MEM_IR
  // RiscV_Probe riscv_probe_5: pin names not known; wires that end beside it: IR
  ROM #(.addrWidth(10), .dataWidth(32), .Select("high")) rom_1 (.addr(IF_PC[11:2]), .data(IR));
  // Probe on \总周期数 
  // Probe on \无条件分支数 
  // Probe on \条件分支成功数 
  // Probe on \插入气泡数 
  // Probe on \LoadUse次数 
  or or_2 (branch, id_ex_1_p33[0], id_ex_1_p33[1]);
  not not_3 (not_3_out, halt);
  // Probe on IF_PC[11:0]
  // Probe on WB_PC[19:0]
  // RiscV_Probe riscv_probe_6: pin names not known; wires that end beside it: WB_IR
  IF_ID if_id_1 (
    .PC(IF_PC), .PC_4(PC_4), .IR(IR), .PC_2(ID_PC), .PC_4_2(if_id_1_pc_4_2), .IR_2(ID_IR), .reset(1'b0),
    .flush(branch), .en(and_2_out), .CLK(CLK));
  and and_2 (and_2_out, or_3_out, not_4_out);
  or or_3 (or_3_out, not_3_out, Go);
  not not_4 (not_4_out, \冲突 );
  // Probe on ID_PC[11:0]
  // Probe on EX_PC[11:0]
  \气泡流水线子电路  \u_气泡流水线子电路_1  (
    .IR(ID_IR), .u1(\单周期硬布线控制器_1_u1 ), .EX_RegWrite(id_ex_1_p40), .u2(\单周期硬布线控制器_1_u2 ),
    .MEM_RegWrite(ex_mem_1_regwrite_2), .EX_rd(EX_rd), .branch(branch), .MEM_rd(MEM_rd), .ecall(ID_ecall),
    .\冲突 (\冲突 ), .flush(flush));
  // Probe on M_PC[11:0]
  D_Flip_Flop #(.trigger("high"), .Pre_Clr_Positions("LEGACY"), .NegatePresetClear("false"), .enable("true"), .NewFFLayout("false")) d_ff_1 (.Q(d_ff_1_q));  // open: clk, D, Qn, preset, en, reset
  // Probe on 13'hc
  \单周期硬布线控制器  \u_单周期硬布线控制器_1  (
    .Funct({ID_IR[30], ID_IR[25], ID_IR[14:12]}), .OP(ID_IR[6:2]), .ALU_OP(\单周期硬布线控制器_1_alu_op ),
    .MemToReg(\单周期硬布线控制器_1_memtoreg ), .MemWrite(\单周期硬布线控制器_1_memwrite ), .ALU_SRC(\单周期硬布线控制器_1_alu_src ),
    .RegWrite(\单周期硬布线控制器_1_regwrite ), .ecall(ID_ecall), .S_type(Stype), .Jalr(\单周期硬布线控制器_1_jalr ),
    .Beq(\单周期硬布线控制器_1_beq ), .JAL(jal), .Bne(\单周期硬布线控制器_1_bne ), .in_3(ID_IR[21]), .uret(\单周期硬布线控制器_1_uret ),
    .u2(\单周期硬布线控制器_1_u2 ), .u1(\单周期硬布线控制器_1_u1 ), .csr(\单周期硬布线控制器_1_csr ), .U_Type(Utype),
    .BLTU(\单周期硬布线控制器_1_bltu ), .LB(\单周期硬布线控制器_1_lb ));
  Multiplexer #(.select(1), .width(5), .disabled("Z"), .enable("false")) multiplexer_2 (
    .in0(ID_IR[19:15]), .in1(5'b10001), .out(multiplexer_2_out), .sel(ID_ecall));
  Multiplexer #(.select(1), .width(5), .disabled("Z"), .enable("false")) multiplexer_3 (
    .in0(ID_IR[24:20]), .in1(5'b01010), .out(multiplexer_3_out), .sel(ID_ecall));
  Multiplexer #(.select(1), .width(12), .disabled("Z"), .enable("false")) multiplexer_4 (
    .in0(ID_IR[31:20]), .in1({ID_IR[31:25], ID_IR[11:7]}), .out(multiplexer_4_out), .sel(Stype));
  assign bit_extender_1_out = {{20{ID_IR[31]}}, {ID_IR[31], ID_IR[7], ID_IR[30:25], ID_IR[11:8]}};  // Bit_Extender bit_extender_1
  assign bit_extender_2_out = {{12{ID_IR[31]}}, {ID_IR[31], ID_IR[19:12], ID_IR[20], ID_IR[30:21]}};  // Bit_Extender bit_extender_2
  // Probe on WB_PC[11:0]
  Comparator #(.width(13), .mode("twosComplement")) comparator_1 (
    .a(CNT_num), .b(13'hc), .eq(comparator_1_eq), .lt(comparator_1_lt));  // open: gt
  Clock #(.highDuration(1), .lowDuration(1)) clock_1 (.out(clock_1_out));
  assign bit_extender_3_out = {{20{multiplexer_4_out[11]}}, multiplexer_4_out};  // Bit_Extender bit_extender_3
  Multiplexer #(.select(1), .width(32), .disabled("Z"), .enable("false")) multiplexer_5 (
    .in0(bit_extender_1_out), .in1(bit_extender_2_out), .out(multiplexer_5_out), .sel(jal));
  nand nand_1 (nand_1_out, d_ff_1_q, comparator_1_eq);
  Counter #(.width(13), .max('h1fff), .ongoal("stay"), .trigger("rising"), .behavior("old")) counter_1 (
    .count(comparator_1_lt), .Q(CNT_num), .clk(clock_1_out));  // open: load, D, carry, clr, preset
  Regifile regifile_1 (
    .Din(RDin), .Clk(not_5_out), .R1(regifile_1_r1), .R2(regifile_1_r2), .WE(RegWrite), .W_num(\WB地址 ),
    .R1_num(multiplexer_2_out), .R2_num(multiplexer_3_out));
  not not_5 (not_5_out, CLK);
  assign CLK = nand_1_out ? clock_1_out : 1'bz;  // Controlled_Buffer controlled_buffer_1
  Pull_Resistor #(.pull(1)) pull_resistor_1 (.node(CLK));
  // ID_EX id_ex_1: pin names not known; wires that end beside it: \单周期硬布线控制器_1_beq , jal, \单周期硬布线控制器_1_bne , \单周期硬布线控制器_1_jalr , \单周期硬布线控制器_1_memtoreg , \单周期硬布线控制器_1_uret , \单周期硬布线控制器_1_memwrite , \单周期硬布线控制器_1_bltu , \单周期硬布线控制器_1_alu_op , \单周期硬布线控制器_1_csr , Utype, \单周期硬布线控制器_1_lb , \单周期硬布线控制器_1_regwrite , ID_ecall, Stype, \单周期硬布线控制器_1_alu_src , regifile_1_r1, regifile_1_r2, ID_IR[11:7], bit_extender_3_out, multiplexer_5_out, ID_PC, if_id_1_pc_4_2, ID_IR, flush, 1'b0, CLK, id_ex_1_p28, or_3_out, id_ex_1_p30, id_ex_1_p31, id_ex_1_p32, id_ex_1_p33[0], id_ex_1_p34, id_ex_1_p35, id_ex_1_p36, id_ex_1_p37, id_ex_1_p38, id_ex_1_p39, id_ex_1_p40, EX_ecall, id_ex_1_p42, id_ex_1_p28, id_ex_1_p44, id_ex_1_p45, EX_rd, id_ex_1_p47, id_ex_1_p48, EX_PC, id_ex_1_p50, EX_IR
  or or_4 (id_ex_1_p33[1], id_ex_1_p31, or_5_out);
  or or_5 (or_5_out, and_3_out, and_5_out, and_4_out);
  and and_3 (and_3_out, id_ex_1_p30, ALUequal);
  Multiplexer #(.select(1), .width(32), .disabled("Z"), .enable("false")) multiplexer_6 (
    .in0(id_ex_1_p45), .in1(id_ex_1_p47), .out(multiplexer_6_out), .sel(id_ex_1_p42));
  not not_6 (not_6_out, halt);
  and and_4 (and_4_out, id_ex_1_p32, ~ALUequal);  // AND_Gate
  Shifter #(.width(32), .shift("ll")) shifter_1 (.in(id_ex_1_p48), .\dist (5'b00001), .out(shifter_1_out));
  Comparator #(.width(32), .mode("twosComplement")) comparator_2 (
    .a(id_ex_1_p44), .b(32'h22), .eq(comparator_2_eq));  // open: gt, lt
  Counter #(.width(16), .max('hffff), .ongoal("wrap"), .trigger("rising"), .behavior("new")) counter_2 (
    .load(1'b0), .D({16{1'b0}}), .count(not_6_out), .Q(\总周期数 ), .clk(CLK), .clr(1'b0), .down(1'b0));  // open: carry, preset
  and and_5 (and_5_out, id_ex_1_p37, ALUl);
  ALU alu_1 (
    .X(id_ex_1_p44), .Y(multiplexer_6_out), .AluOP(id_ex_1_p38), .Equal(ALUequal), .Result(ALUresult),
    .out_4(ALUge), .out_6(ALUl));  // open: Result_2
  Adder #(.width(32)) adder_2 (.a(shifter_1_out), .b(EX_PC), .out(Jaddress), .cin(1'b0));  // open: cout
  not not_7 (not_7_out, comparator_2_eq);
  and and_6 (and_6_out, comparator_2_eq, EX_ecall);
  and and_7 (exhalt, EX_ecall, not_7_out);
  EX_MEM ex_mem_1 (
    .MemToReg(id_ex_1_p34), .MemWrite(id_ex_1_p36), .RegWrite(id_ex_1_p40), .JAL(id_ex_1_p31),
    .JALR(id_ex_1_p33[0]), .URET(id_ex_1_p35), .LB(id_ex_1_p39), .halt(exhalt), .rd(EX_rd),
    .result(ALUresult), .R2(id_ex_1_p45), .PC(EX_PC), .PC_4(id_ex_1_p50), .IR(EX_IR),
    .MemToReg_2(ex_mem_1_memtoreg_2), .MemWrite_2(MemWrite), .RegWrite_2(ex_mem_1_regwrite_2),
    .JAL_2(ex_mem_1_jal_2), .JALR_2(ex_mem_1_jalr_2), .URET_2(ex_mem_1_uret_2), .LB_2(ex_mem_1_lb_2),
    .halt_2(ex_mem_1_halt_2), .rd_2(MEM_rd), .result_2(ex_mem_1_result_2), .R2_2(MDin), .PC_2(M_PC),
    .PC_4_2(ex_mem_1_pc_4_2), .IR_2(MEM_IR), .reset(1'b0), .flush(1'b0), .en(or_3_out), .CLK(CLK));  // open: Uimm, Uimm_2, U_type, U_type_2
  Register #(.width(32), .trigger("rising"), .Select("low")) register_1 (
    .D(id_ex_1_p45), .en(and_6_out), .Q(LedData), .clk(CLK));  // open: clr
  RAM #(.addrWidth(10), .dataWidth(32), .bus("separate"), .Select("high")) ram_1 (
    .addr(ex_mem_1_result_2[11:2]), .din(MDin), .data(ram_1_data), .str(MemWrite), .sel(1'b1), .clk(CLK),
    .ld(1'b1));  // open: clr
  MEM_WB mem_wb_1 (
    .LB(ex_mem_1_lb_2), .MemToReg(ex_mem_1_memtoreg_2), .RegWrite(ex_mem_1_regwrite_2), .JAL(ex_mem_1_jal_2),
    .JALR(ex_mem_1_jalr_2), .URET(ex_mem_1_uret_2), .halt(ex_mem_1_halt_2), .rd(MEM_rd),
    .ALUresult(ex_mem_1_result_2), .MemData(ram_1_data), .PC(M_PC), .PC_4(ex_mem_1_pc_4_2), .IR(MEM_IR),
    .MemToReg_2(mem_wb_1_memtoreg_2[0]), .RegWrite_2(RegWrite), .JAL_2(mem_wb_1_jal_2),
    .JALR_2(mem_wb_1_jalr_2), .halt_2(mem_wb_1_halt_2), .rd_2(\WB地址 ), .ALUresult_2(mem_wb_1_aluresult_2),
    .MemData_2(mem_wb_1_memdata_2), .PC_2(WB_PC), .PC_4_2(mem_wb_1_pc_4_2), .IR_2(WB_IR), .reset(1'b0),
    .flush(1'b0), .en(or_3_out), .CLK(CLK));  // open: LB_2, URET_2, Uimm, Uimm_2, U_type, U_type_2
  or or_6 (mem_wb_1_memtoreg_2[1], mem_wb_1_jal_2, mem_wb_1_jalr_2);
  Multiplexer #(.select(2), .width(32), .disabled("Z"), .enable("false")) multiplexer_7 (
    .in0(mem_wb_1_aluresult_2), .in1(mem_wb_1_memdata_2), .in2(mem_wb_1_pc_4_2), .out(RDin),
    .sel(mem_wb_1_memtoreg_2));  // open: in3
  D_Flip_Flop #(.trigger("rising"), .Pre_Clr_Positions("ABOVE_BELOW"), .NegatePresetClear("false"), .enable("true"), .NewFFLayout("true")) d_ff_2 (
    .clk(mem_wb_1_halt_2), .D(1'b1), .Q(halt), .preset(1'b0), .en(1'b1), .reset(Go));  // open: Qn

  // Other names for the same wires on the sheet: MEM_PC[31:0] = M_PC

  // Notes on the sheet:
  //   中断源
  //   时空图监测，可删除
  //   中断等待指示
  //   数码管输出
  //   指令存储器
  //   指令探针
  //   contents of rom_1 (hex, n*v repeats v):
  //   100493 100006f 100493 200913 300993 100006f 100493 200913 300993 100006f 100493 200913 300993
  //   100006f 100493 200913 300993 29c000ef 100413 100493 1f49493 900533 2200893 73 24d493 48463 fedff06f
  //   900533 2200893 73 100493 249493 900533 2200893 73 48463 fedff06f 100493 1f49493 900533 2200893 73
  //   4034d493 900533 2200893 73 4044d493 900533 2200893 73 4044d493 900533 2200893 73 4044d493 900533
  //   2200893 73 4044d493 900533 2200893 73 4044d493 900533 2200893 73 4044d493 900533 2200893 73 4044d493
  //   900533 2200893 73 100413 1f41993 41f9d993 433 c00913 300b13 140413 f47413 800293 100313 499993
  //   89e9b3 1300533 2200893 73 406282b3 fe0294e3 140413 f00f93 1f47433 1c41413 800293 100313 49d993
  //   89e9b3 1300533 2200893 73 406282b3 fe0294e3 1c45413 406b0b33 b0463 f95ff06f 2b3 fff2c293 829293
  //   ff2e293 500533 2200893 73 fff00413 493 84a023 140413 448493 84a023 140413 448493 84a023 140413
  //   448493 84a023 140413 448493 84a023 140413 448493 84a023 140413 448493 84a023 140413 448493 84a023
  //   140413 448493 84a023 140413 448493 84a023 140413 448493 84a023 140413 448493 84a023 140413 448493
  //   84a023 140413 448493 84a023 140413 448493 84a023 140413 448493 84a023 140413 448493 140413 433
  //   3c00493 42983 4aa03 149a2b3 28663 134a023 1442023 ffc48493 fe9412e3 800533 2200893 73 440413 3c00493
  //   fc9416e3 a00893 73 413 140413 800533 2200893 73 240413 800533 2200893 73 340413 800533 2200893 73
  //   440413 800533 2200893 73 540413 800533 2200893 73 640413 800533 2200893 73 740413 800533 2200893 73
  //   840413 800533 2200893 2200893 73 8067
  //   控制位
  //   JAL
  //   JALR
  //   CSR
  //   rs1
  //   rs2
  //   rd
  //   I指令
  //   S指令
  //   B指令
  //   J指令
  //   流水调试日志用
  //   暂停节拍，不能为0
  //   Beq
  //   Bne
  //   MemToReg
  //   MemWrite
  //   AluOP
  //   AluSrcB
  //   RegWrite
  //   戳工具置1进入计数暂停模式，ctrl+k时钟自动运行到对应节拍暂停
  //   ctrl+k关闭时钟连续运行，将控制位置零，进入单步调试模式调试
  //   可计数暂停的时钟源
  //   R1
  //   R2
  //   rd
  //   imm1
  //   imm2
  //   为方便自动评测，需要输出流水线各段保存的PC值，注意是PC不是PC+4，另外ID段寄存器写入信息，Mem段内存写入信息也要输出
  //   ALUresult
  //   ReegWrite
  //   数据存储器
  //   MemtoReg
  //   JAL
  //   JALR
  //   LBU
endmodule

module \重定向流水线  (
  output RegWrite,
  output MemWrite,
  output [31:0] IF_PC,
  output [31:0] ID_PC,
  output [31:0] EX_PC,
  output [31:0] M_PC,
  output [31:0] WB_PC,
  output [31:0] RDin,
  output [31:0] MDin,
  output [31:0] LedData
);

  wire ALUequal, ALUge, ALUI, and_1_out, and_2_out, and_3_out, and_4_out, and_5_out, and_6_out, branch, CLK,
       clock_1_out, comparator_1_eq, comparator_1_lt, comparator_2_eq, d_ff_1_q, EX_ecall, ex_mem_1_halt_2,
       ex_mem_1_jal_2, ex_mem_1_jalr_2, ex_mem_1_lb_2, ex_mem_1_memtoreg_2, ex_mem_1_regwrite_2,
       ex_mem_1_uret_2, exhalt, flush, Go, halt, ID_ecall, id_ex_1_p25, id_ex_1_p34, id_ex_1_p35,
       id_ex_1_p36, id_ex_1_p38, id_ex_1_p39, id_ex_1_p40, id_ex_1_p41, id_ex_1_p43, id_ex_1_p44,
       id_ex_1_p45, id_ex_1_p47, IR1, IR2, IR3, jal, mem_wb_1_halt_2, mem_wb_1_jal_2, mem_wb_1_jalr_2,
       mem_wb_1_lb_2, mem_wb_1_memtoreg_2, mem_wb_1_u_type_2, MemUtype, nand_1_out, not_1_out, not_2_out,
       not_3_out, not_4_out, not_5_out, not_6_out, not_7_out, or_1_out, or_3_out, or_5_out, RST, Stype,
       Utype, W1, W2, W3, \冲突 , \单周期硬布线控制器_1_alu_src , \单周期硬布线控制器_1_beq , \单周期硬布线控制器_1_bltu ,
       \单周期硬布线控制器_1_bne , \单周期硬布线控制器_1_csr , \单周期硬布线控制器_1_jalr , \单周期硬布线控制器_1_lb , \单周期硬布线控制器_1_memtoreg ,
       \单周期硬布线控制器_1_memwrite , \单周期硬布线控制器_1_regwrite , \单周期硬布线控制器_1_u1 , \单周期硬布线控制器_1_u2 , \单周期硬布线控制器_1_uret ;
  wire [1:0] id_ex_1_p37, id_ex_1_p54, id_ex_1_p55, multiplexer_8_out, or_7_out, r1_forward, r2_forward;
  wire [3:0] id_ex_1_p42, \单周期硬布线控制器_1_alu_op ;
  wire [4:0] EX_rd, MEM_rd, multiplexer_2_out, multiplexer_3_out, \WB地址 ;
  wire [7:0] multiplexer_12_out;
  wire [11:0] multiplexer_4_out;
  wire [12:0] CNT_num;
  wire [15:0] \LoadUse次数 , \总周期数 , \插入气泡数 , \无条件分支数 , \条件分支成功数 ;
  wire [31:0] ALUresult, bit_extender_1_out, bit_extender_2_out, bit_extender_3_out, bit_extender_4_out,
       EX_IR, ex_mem_1_pc_4_2, EX_R1, EX_R2, id_ex_1_p51, id_ex_1_p52, id_ex_1_p53, id_ex_1_p57, ID_IR,
       if_id_1_pc_4_2, IF_IR, Jaddress, LBData, MEM_AluResult, MEM_IR, MEM_Uimm, mem_wb_1_aluresult_2,
       mem_wb_1_memdata_2, mem_wb_1_pc_4_2, mem_wb_1_uimm_2, multiplexer_1_out, multiplexer_5_out,
       multiplexer_7_out, multiplexer_10_out, newr1, newr2, PC_4, ram_1_data, regifile_1_r1, regifile_1_r2,
       shifter_1_out, shifter_2_out, WB_IR;

  Button \u_总复位  (.out(RST));
  Button _1 (.out(IR1));
  Button _2 (.out(IR2));
  Button _3 (.out(IR3));
  // Probe on \总周期数 
  // Probe on \总周期数 
  Button \u_继续运行  (.out(Go));
  LED #(.active("true")) led_1 (.in(W1));
  LED #(.active("true")) led_2 (.in(W2));
  LED #(.active("true")) led_3 (.in(W3));
  not not_1 (not_1_out, halt);
  Hex_Digit_Display hex_digit_display_1 (.value(LedData[31:28]));  // open: dp
  // Probe on IF_PC[19:0]
  // RiscV_Probe riscv_probe_1: pin names not known; wires that end beside it: IF_IR
  and and_1 (and_1_out, or_1_out, not_2_out);
  Multiplexer #(.select(2), .width(32), .disabled("Z"), .enable("false")) multiplexer_1 (
    .in0(PC_4), .in1(ALUresult), .in2(Jaddress), .out(multiplexer_1_out), .sel(id_ex_1_p37));  // open: in3
  or or_1 (or_1_out, not_1_out, Go);
  not not_2 (not_2_out, \冲突 );
  Hex_Digit_Display hex_digit_display_2 (.value(LedData[23:20]));  // open: dp
  Hex_Digit_Display hex_digit_display_3 (.value(LedData[27:24]));  // open: dp
  // Probe on ID_PC[19:0]
  // RiscV_Probe riscv_probe_2: pin names not known; wires that end beside it: ID_IR
  Register #(.width(32), .trigger("rising"), .Select("low")) PC (
    .D(multiplexer_1_out), .en(and_1_out), .Q(IF_PC), .clk(CLK), .clr(RST));
  Hex_Digit_Display hex_digit_display_4 (.value(LedData[15:12]));  // open: dp
  Hex_Digit_Display hex_digit_display_5 (.value(LedData[19:16]));  // open: dp
  Adder #(.width(32)) adder_1 (.a(IF_PC), .b(32'h4), .out(PC_4));  // open: cin, cout
  Hex_Digit_Display hex_digit_display_6 (.value(LedData[11:8]));  // open: dp
  Hex_Digit_Display hex_digit_display_7 (.value(LedData[7:4]));  // open: dp
  // Probe on EX_PC[19:0]
  // RiscV_Probe riscv_probe_3: pin names not known; wires that end beside it: EX_IR
  // RiscV_Probe riscv_probe_4: pin names not known; wires that end beside it: IF_IR
  Hex_Digit_Display hex_digit_display_8 (.value(LedData[3:0]));  // open: dp
  ROM #(.addrWidth(10), .dataWidth(32), .Select("high")) rom_1 (.addr(IF_PC[11:2]), .data(IF_IR));
  not not_3 (not_3_out, halt);
  // Probe on \总周期数 
  // Probe on M_PC[19:0]
  // RiscV_Probe riscv_probe_5: pin names not known; wires that end beside it: MEM_IR
  or or_2 (branch, id_ex_1_p37[0], id_ex_1_p37[1]);
  IF_ID if_id_1 (
    .PC(IF_PC), .PC_4(PC_4), .IR(IF_IR), .PC_2(ID_PC), .PC_4_2(if_id_1_pc_4_2), .IR_2(ID_IR), .reset(1'b0),
    .flush(branch), .en(and_2_out), .CLK(CLK));
  and and_2 (and_2_out, or_3_out, not_4_out);
  not not_4 (not_4_out, \冲突 );
  or or_3 (or_3_out, not_3_out, Go);
  // Probe on \总周期数 
  // Probe on \无条件分支数 
  // Probe on \条件分支成功数 
  // Probe on \插入气泡数 
  // Probe on \LoadUse次数 
  // Probe on IF_PC[11:0]
  // Probe on WB_PC[19:0]
  // RiscV_Probe riscv_probe_6: pin names not known; wires that end beside it: WB_IR
  \单周期硬布线控制器  \u_单周期硬布线控制器_1  (
    .Funct({ID_IR[30], ID_IR[25], ID_IR[14:12]}), .OP(ID_IR[6:2]), .ALU_OP(\单周期硬布线控制器_1_alu_op ),
    .MemToReg(\单周期硬布线控制器_1_memtoreg ), .MemWrite(\单周期硬布线控制器_1_memwrite ), .ALU_SRC(\单周期硬布线控制器_1_alu_src ),
    .RegWrite(\单周期硬布线控制器_1_regwrite ), .ecall(ID_ecall), .S_type(Stype), .Jalr(\单周期硬布线控制器_1_jalr ),
    .Beq(\单周期硬布线控制器_1_beq ), .JAL(jal), .Bne(\单周期硬布线控制器_1_bne ), .in_3(ID_IR[21]), .uret(\单周期硬布线控制器_1_uret ),
    .u2(\单周期硬布线控制器_1_u2 ), .u1(\单周期硬布线控制器_1_u1 ), .csr(\单周期硬布线控制器_1_csr ), .U_Type(Utype),
    .BLTU(\单周期硬布线控制器_1_bltu ), .LB(\单周期硬布线控制器_1_lb ));
  Multiplexer #(.select(1), .width(5), .disabled("Z"), .enable("false")) multiplexer_2 (
    .in0(ID_IR[19:15]), .in1(5'b10001), .out(multiplexer_2_out), .sel(ID_ecall));
  Multiplexer #(.select(1), .width(5), .disabled("Z"), .enable("false")) multiplexer_3 (
    .in0(ID_IR[24:20]), .in1(5'b01010), .out(multiplexer_3_out), .sel(ID_ecall));
  Multiplexer #(.select(1), .width(12), .disabled("Z"), .enable("false")) multiplexer_4 (
    .in0(ID_IR[31:20]), .in1({ID_IR[31:25], ID_IR[11:7]}), .out(multiplexer_4_out), .sel(Stype));
  assign bit_extender_1_out = {{12{ID_IR[31]}}, ID_IR[31:12]};  // Bit_Extender bit_extender_1
  Shifter #(.width(32), .shift("ll")) shifter_1 (.in(bit_extender_1_out), .\dist (5'b01100), .out(shifter_1_out));
  // Probe on EX_PC[11:0]
  // Probe on ID_PC[11:0]
  assign bit_extender_2_out = {{20{multiplexer_4_out[11]}}, multiplexer_4_out};  // Bit_Extender bit_extender_2
  assign bit_extender_3_out = {{20{ID_IR[31]}}, {ID_IR[31], ID_IR[7], ID_IR[30:25], ID_IR[11:8]}};  // Bit_Extender bit_extender_3
  assign bit_extender_4_out = {{12{ID_IR[31]}}, {ID_IR[31], ID_IR[19:12], ID_IR[20], ID_IR[30:21]}};  // Bit_Extender bit_extender_4
  // Probe on M_PC[11:0]
  D_Flip_Flop #(.trigger("high"), .Pre_Clr_Positions("LEGACY"), .NegatePresetClear("false"), .enable("true"), .NewFFLayout("false")) d_ff_1 (.Q(d_ff_1_q));  // open: clk, D, Qn, preset, en, reset
  // Probe on 13'hc
  Regifile regifile_1 (
    .Din(RDin), .Clk(not_5_out), .R1(regifile_1_r1), .R2(regifile_1_r2), .WE(RegWrite), .W_num(\WB地址 ),
    .R1_num(multiplexer_2_out), .R2_num(multiplexer_3_out));
  not not_5 (not_5_out, CLK);
  Multiplexer #(.select(1), .width(32), .disabled("Z"), .enable("false")) multiplexer_5 (
    .in0(bit_extender_3_out), .in1(bit_extender_4_out), .out(multiplexer_5_out), .sel(jal));
  // Probe on WB_PC[11:0]
  Comparator #(.width(13), .mode("twosComplement")) comparator_1 (
    .a(CNT_num), .b(13'hc), .eq(comparator_1_eq), .lt(comparator_1_lt));  // open: gt
  Clock #(.highDuration(1), .lowDuration(1)) clock_1 (.out(clock_1_out));
  nand nand_1 (nand_1_out, d_ff_1_q, comparator_1_eq);
  Counter #(.width(13), .max('h1fff), .ongoal("stay"), .trigger("rising"), .behavior("old")) counter_1 (
    .count(comparator_1_lt), .Q(CNT_num), .clk(clock_1_out));  // open: load, D, carry, clr, preset
  // ID_EX id_ex_1: pin names not known; wires that end beside it: \单周期硬布线控制器_1_beq , jal, \单周期硬布线控制器_1_bne , \单周期硬布线控制器_1_jalr , \单周期硬布线控制器_1_memtoreg , \单周期硬布线控制器_1_uret , \单周期硬布线控制器_1_memwrite , \单周期硬布线控制器_1_bltu , \单周期硬布线控制器_1_alu_op , \单周期硬布线控制器_1_csr , Utype, \单周期硬布线控制器_1_lb , \单周期硬布线控制器_1_regwrite , ID_ecall, Stype, \单周期硬布线控制器_1_alu_src , regifile_1_r1, regifile_1_r2, ID_IR[11:7], bit_extender_2_out, multiplexer_5_out, shifter_1_out, r1_forward, r2_forward, id_ex_1_p25, ID_PC, if_id_1_pc_4_2, ID_IR, flush, id_ex_1_p25, 1'b0, CLK, or_3_out, id_ex_1_p34, id_ex_1_p35, id_ex_1_p36, id_ex_1_p37[0], id_ex_1_p38, id_ex_1_p39, id_ex_1_p40, id_ex_1_p41, id_ex_1_p42, id_ex_1_p43, id_ex_1_p44, id_ex_1_p45, EX_ecall, id_ex_1_p47, EX_R1, EX_R2, EX_rd, id_ex_1_p51, id_ex_1_p52, id_ex_1_p53, id_ex_1_p54, id_ex_1_p55, EX_PC, id_ex_1_p57, EX_IR
  Multiplexer #(.select(2), .width(32), .disabled("Z"), .enable("false")) multiplexer_6 (
    .in0(EX_R1), .in1(RDin), .in2(MEM_AluResult), .out(newr1), .sel(id_ex_1_p54));  // open: in3
  assign CLK = nand_1_out ? clock_1_out : 1'bz;  // Controlled_Buffer controlled_buffer_1
  \重定向流水线处理  \u_重定向流水线处理_1  (
    .IR(ID_IR), .u1(\单周期硬布线控制器_1_u1 ), .EX_RegWrite(id_ex_1_p45), .u2(\单周期硬布线控制器_1_u2 ),
    .MEM_RegWrite(ex_mem_1_regwrite_2), .EX_rd(EX_rd), .branch(branch), .EX_MemToReg(id_ex_1_p38),
    .MEM_rd(MEM_rd), .ecall(ID_ecall), .\冲突 (\冲突 ), .flush(flush), .RS1_Forward(r1_forward),
    .RS2_Forward(r2_forward));
  or or_4 (id_ex_1_p37[1], id_ex_1_p35, or_5_out);
  and and_3 (and_3_out, id_ex_1_p34, ALUequal);
  Pull_Resistor #(.pull(1)) pull_resistor_1 (.node(CLK));
  or or_5 (or_5_out, and_3_out, and_5_out, and_4_out);
  and and_4 (and_4_out, id_ex_1_p36, ~ALUequal);  // AND_Gate
  Multiplexer #(.select(1), .width(32), .disabled("Z"), .enable("false")) multiplexer_7 (
    .in0(newr2), .in1(id_ex_1_p51), .out(multiplexer_7_out), .sel(id_ex_1_p47));
  Shifter #(.width(32), .shift("ll")) shifter_2 (.in(id_ex_1_p52), .\dist (5'b00001), .out(shifter_2_out));
  Comparator #(.width(32), .mode("twosComplement")) comparator_2 (
    .a(newr1), .b(32'h22), .eq(comparator_2_eq));  // open: gt, lt
  Multiplexer #(.select(1), .width(2), .disabled("Z"), .enable("false")) multiplexer_8 (
    .in0(id_ex_1_p55), .in1(2'b11), .out(multiplexer_8_out), .sel(MemUtype));
  Multiplexer #(.select(2), .width(32), .disabled("Z"), .enable("false")) multiplexer_9 (
    .in0(EX_R2), .in1(RDin), .in2(MEM_AluResult), .in3(MEM_Uimm), .out(newr2), .sel(multiplexer_8_out));
  and and_5 (and_5_out, id_ex_1_p41, ALUI);
  ALU alu_1 (
    .X(newr1), .Y(multiplexer_7_out), .AluOP(id_ex_1_p42), .Equal(ALUequal), .Result(ALUresult),
    .out_4(ALUge), .out_6(ALUI));  // open: Result_2
  Adder #(.width(32)) adder_2 (.a(shifter_2_out), .b(EX_PC), .out(Jaddress), .cin(1'b0));  // open: cout
  not not_6 (not_6_out, comparator_2_eq);
  and and_6 (and_6_out, comparator_2_eq, EX_ecall);
  not not_7 (not_7_out, halt);
  and and_7 (exhalt, EX_ecall, not_6_out);
  Counter #(.width(16), .max('hffff), .ongoal("wrap"), .trigger("rising"), .behavior("new")) counter_2 (
    .load(1'b0), .D({16{1'b0}}), .count(not_7_out), .Q(\总周期数 ), .clk(CLK), .clr(1'b0), .down(1'b0));  // open: carry, preset
  Register #(.width(32), .trigger("rising"), .Select("low")) register_1 (
    .D(newr2), .en(and_6_out), .Q(LedData), .clk(CLK));  // open: clr
  EX_MEM ex_mem_1 (
    .MemToReg(id_ex_1_p38), .MemWrite(id_ex_1_p40), .RegWrite(id_ex_1_p45), .JAL(id_ex_1_p35),
    .JALR(id_ex_1_p37[0]), .URET(id_ex_1_p39), .LB(id_ex_1_p44), .halt(exhalt), .rd(EX_rd),
    .result(ALUresult), .R2(newr2), .PC(EX_PC), .PC_4(id_ex_1_p57), .IR(EX_IR),
    .MemToReg_2(ex_mem_1_memtoreg_2), .MemWrite_2(MemWrite), .RegWrite_2(ex_mem_1_regwrite_2),
    .JAL_2(ex_mem_1_jal_2), .JALR_2(ex_mem_1_jalr_2), .URET_2(ex_mem_1_uret_2), .LB_2(ex_mem_1_lb_2),
    .halt_2(ex_mem_1_halt_2), .rd_2(MEM_rd), .result_2(MEM_AluResult), .R2_2(MDin), .PC_2(M_PC),
    .PC_4_2(ex_mem_1_pc_4_2), .IR_2(MEM_IR), .reset(1'b0), .flush(1'b0), .en(or_3_out), .CLK(CLK),
    .Uimm(id_ex_1_p53), .Uimm_2(MEM_Uimm), .U_type(id_ex_1_p43), .U_type_2(MemUtype));
  RAM #(.addrWidth(10), .dataWidth(32), .bus("separate"), .Select("high")) ram_1 (
    .addr(MEM_AluResult[11:2]), .din(MDin), .data(ram_1_data), .str(MemWrite), .sel(1'b1), .clk(CLK),
    .ld(1'b1));  // open: clr
  MEM_WB mem_wb_1 (
    .LB(ex_mem_1_lb_2), .MemToReg(ex_mem_1_memtoreg_2), .RegWrite(ex_mem_1_regwrite_2), .JAL(ex_mem_1_jal_2),
    .JALR(ex_mem_1_jalr_2), .URET(ex_mem_1_uret_2), .halt(ex_mem_1_halt_2), .rd(MEM_rd),
    .ALUresult(MEM_AluResult), .MemData(ram_1_data), .PC(M_PC), .PC_4(ex_mem_1_pc_4_2), .IR(MEM_IR),
    .LB_2(mem_wb_1_lb_2), .MemToReg_2(mem_wb_1_memtoreg_2), .RegWrite_2(RegWrite), .JAL_2(mem_wb_1_jal_2),
    .JALR_2(mem_wb_1_jalr_2), .halt_2(mem_wb_1_halt_2), .rd_2(\WB地址 ), .ALUresult_2(mem_wb_1_aluresult_2),
    .MemData_2(mem_wb_1_memdata_2), .PC_2(WB_PC), .PC_4_2(mem_wb_1_pc_4_2), .IR_2(WB_IR), .reset(1'b0),
    .flush(1'b0), .en(or_3_out), .CLK(CLK), .Uimm(MEM_Uimm), .Uimm_2(mem_wb_1_uimm_2), .U_type(MemUtype),
    .U_type_2(mem_wb_1_u_type_2));  // open: URET_2
  or or_6 (or_7_out[1], mem_wb_1_jal_2, mem_wb_1_u_type_2, mem_wb_1_jalr_2);
  or or_7 (or_7_out[0], mem_wb_1_memtoreg_2, mem_wb_1_u_type_2);
  Multiplexer #(.select(1), .width(32), .disabled("Z"), .enable("false")) multiplexer_10 (
    .in0(mem_wb_1_memdata_2), .in1(LBData), .out(multiplexer_10_out), .sel(mem_wb_1_lb_2));
  Multiplexer #(.select(2), .width(32), .disabled("Z"), .enable("false")) multiplexer_11 (
    .in0(mem_wb_1_aluresult_2), .in1(multiplexer_10_out), .in2(mem_wb_1_pc_4_2), .in3(mem_wb_1_uimm_2),
    .out(RDin), .sel(or_7_out));
  D_Flip_Flop #(.trigger("rising"), .Pre_Clr_Positions("ABOVE_BELOW"), .NegatePresetClear("false"), .enable("true"), .NewFFLayout("true")) d_ff_2 (
    .clk(mem_wb_1_halt_2), .D(1'b1), .Q(halt), .preset(1'b0), .en(1'b1), .reset(Go));  // open: Qn
  Multiplexer #(.select(2), .width(8), .disabled("Z"), .enable("false")) multiplexer_12 (
    .in0(mem_wb_1_memdata_2[7:0]), .in1(mem_wb_1_memdata_2[15:8]), .in2(mem_wb_1_memdata_2[23:16]),
    .in3(mem_wb_1_memdata_2[31:24]), .out(multiplexer_12_out), .sel(mem_wb_1_aluresult_2[1:0]));
  assign LBData = {{24{multiplexer_12_out[7]}}, multiplexer_12_out};  // Bit_Extender bit_extender_5

  // Other names for the same wires on the sheet: MEM_PC[31:0] = M_PC

  // Notes on the sheet:
  //   中断源
  //   时空图监测，可删除
  //   中断等待指示
  //   数码管输出
  //   IF
  //   指令探针
  //   指令存储器
  //   contents of rom_1 (hex, n*v repeats v):
  //   100493 100006f 100493 200913 300993 100006f 100493 200913 300993 100006f 100493 200913 300993
  //   100006f 100493 200913 300993 3ec000ef 100413 100493 1f49493 900533 2200893 73 24d493 48463 fedff06f
  //   900533 2200893 73 100493 249493 900533 2200893 73 48463 fedff06f 100493 1f49493 900533 2200893 73
  //   4034d493 900533 2200893 73 4044d493 900533 2200893 73 4044d493 900533 2200893 73 4044d493 900533
  //   2200893 73 4044d493 900533 2200893 73 4044d493 900533 2200893 73 4044d493 900533 2200893 73 4044d493
  //   900533 2200893 73 100413 1f41993 41f9d993 433 c00913 300b13 140413 f47413 800293 100313 499993
  //   89e9b3 1300533 2200893 73 406282b3 fe0294e3 140413 f00f93 1f47433 1c41413 800293 100313 49d993
  //   89e9b3 1300533 2200893 73 406282b3 fe0294e3 1c45413 406b0b33 b0463 f95ff06f 2b3 fff2c293 829293
  //   ff2e293 500533 2200893 73 fff00413 493 84a023 140413 448493 84a023 140413 448493 84a023 140413
  //   448493 84a023 140413 448493 84a023 140413 448493 84a023 140413 448493 84a023 140413 448493 84a023
  //   140413 448493 84a023 140413 448493 84a023 140413 448493 84a023 140413 448493 84a023 140413 448493
  //   84a023 140413 448493 84a023 140413 448493 84a023 140413 448493 84a023 140413 448493 140413 433
  //   3c00493 42983 4aa03 149a2b3 28663 134a023 1442023 ffc48493 fe9412e3 800533 2200893 73 440413 3c00493
  //   fc9416e3 a00893 73 100293 300313 800493 849493 7648493 1449493 900533 2200893 73 800e13 4054d4b3
  //   4064d4b3 900533 2200893 73 fffe0e13 fe0e14e3 a00893 73 800e13 fedc04b7 fff00413 1045413 84e4b3
  //   900533 2200893 73 ba984b7 900533 73 76544b7 900533 73 32104b7 900533 73 fffe0e13 fa0e1ee3 a00893 73
  //   313 1000e13 13 8400493 849493 8348493 400913 891913 490913 849493 8248493 849493 8148493 891913
  //   490913 891913 490913 932023 12484b3 430313 fffe0e13 fe0e18e3 2000e13 313 30483 900533 2200893 73
  //   130313 fffe0e13 fe0e14e3 a00893 73 ff100493 900533 2200893 73 148493 fe9068e3 900533 2200893 73
  //   a00893 73 413 140413 800533 2200893 73 240413 800533 2200893 73 340413 800533 2200893 73 440413
  //   800533 2200893 73 540413 800533 2200893 73 640413 800533 2200893 73 740413 800533 2200893 73 840413
  //   800533 2200893 2200893 73 8067
  //   JAL
  //   JALR
  //   CSR
  //   rs1
  //   rs2
  //   rd
  //   I指令
  //   S指令
  //   B指令
  //   U指令
  //   J指令
  //   ID
  //   Beq
  //   Bne
  //   MemToReg
  //   MemWrite
  //   AluOP
  //   AluSrcB
  //   RegWrite
  //   控制位
  //   流水调试日志用
  //   暂停节拍，不能为0
  //   戳工具置1进入计数暂停模式，ctrl+k时钟自动运行到对应节拍暂停
  //   ctrl+k关闭时钟连续运行，将控制位置零，进入单步调试模式调试
  //   R1
  //   R2
  //   rd
  //   imm1
  //   imm2
  //   可计数暂停的时钟源
  //   EX
  //   为方便自动评测，需要输出流水线各段保存的PC值，注意是PC不是PC+4，另外ID段寄存器写入信息，Mem段内存写入信息也要输出
  //   ALUresult
  //   RegWrite
  //   MEM
  //   数据存储器
  //   MemtoReg
  //   JAL
  //   JALR
  //   LB
  //   WB
endmodule

module \中断按键参考电路  (
  input  \同步清零信号 ,
  output \与中断屏蔽位与 
);

  wire \_1号中断_out , and_1_out, clock_1_out, d_ff_1_q, or_1_out, or_2_out;

  Clock #(.highDuration(1), .lowDuration(1)) clock_1 (.out(clock_1_out));
  Button \_1号中断  (.out(\_1号中断_out ));
  or or_1 (or_1_out, \与中断屏蔽位与 , d_ff_1_q);
  LED #(.active("true")) \_1号中断等待指示灯  (.in(or_1_out));
  D_Flip_Flop #(.trigger("rising"), .Pre_Clr_Positions("LEGACY"), .NegatePresetClear("false"), .enable("true"), .NewFFLayout("false")) d_ff_1 (
    .clk(\_1号中断_out ), .D(1'b1), .Q(d_ff_1_q), .reset(\与中断屏蔽位与 ));  // open: Qn, preset, en
  or or_2 (or_2_out, d_ff_1_q, \与中断屏蔽位与 );
  and and_1 (and_1_out, or_2_out, ~\同步清零信号 );  // AND_Gate
  D_Flip_Flop #(.trigger("rising"), .Pre_Clr_Positions("LEGACY"), .NegatePresetClear("false"), .enable("true"), .NewFFLayout("false")) IR1 (
    .clk(clock_1_out), .D(and_1_out), .Q(\与中断屏蔽位与 ));  // open: Qn, preset, en, reset

  // Notes on the sheet:
  //   中断信号采样参考电路
  //   Reset 
endmodule
module \单周期_单级中断  (
  input  IR1,
  input  IR2,
  input  IR3,
  output RegWrite,
  output MemWrite,
  output [31:0] PC,
  output [31:0] IR,
  output [31:0] RDin,
  output [31:0] MDin,
  output [31:0] LedData
);

  wire ALUequal, ALUge, ALUl, and_1_out, and_2_out, and_3_out, and_4_out, and_5_out, and_6_out, and_8_out,
       Beq, Bne, CLK, clock_1_out, comparator_1_eq, comparator_2_eq, comparator_3_eq, comparator_4_eq,
       comparator_5_eq, comparator_6_eq, comparator_6_lt, csr, d_ff_1_q, d_ff_2_q, d_ff_3_q, d_ff_7_q, ecall,
       Go, halt, IE, IR1_t, IR2_t, IR3_t, IRA, IRB, IRC, jal, jalr, LB, MemToReg, nand_1_out, not_1_out,
       not_2_out, not_3_out, not_4_out, or_4_out, or_5_out, or_6_out, or_7_out, or_8_out, or_9_out,
       or_13_out, RESET1, RESET2, RESET3, RST, Stype, uret, Utype, W1, W2, W3, \中断 , \中断1 , \中断2 , \中断3 ,
       \中断产生 , \单周期硬布线控制器_1_alu_src , \单周期硬布线控制器_1_bltu ;
  wire [1:0] or_14_out, priority_encoder_1_out, \中断号 , \中断号_q ;
  wire [3:0] \单周期硬布线控制器_1_alu_op ;
  wire [4:0] multiplexer_2_out, multiplexer_3_out;
  wire [7:0] multiplexer_10_out;
  wire [11:0] multiplexer_4_out;
  wire [12:0] CNT_num;
  wire [15:0] \总周期数 ;
  wire [31:0] adder_2_out, adder_3_out, adder_4_out, ALUresult, bit_extender_1_out, bit_extender_2_out,
       bit_extender_3_out, bit_extender_4_out, EPC, LBData, multiplexer_5_out, multiplexer_8_out, PC_4,
       ram_1_data, regifile_1_r1, shifter_1_out, shifter_2_out, shifter_3_out, \中断地址 , \新PC , \老PC ;

  Button \u_继续运行  (.out(Go));
  Button _1 (.out(IRA));
  Button _2 (.out(IRB));
  Button _3 (.out(IRC));
  LED #(.active("true")) led_1 (.in(W1));
  LED #(.active("true")) led_2 (.in(W2));
  LED #(.active("true")) led_3 (.in(W3));
  Hex_Digit_Display hex_digit_display_1 (.value(LedData[31:28]));  // open: dp
  Comparator #(.width(16), .mode("twosComplement")) comparator_1 (
    .a(16'h23b), .b(\总周期数 ), .eq(comparator_1_eq));  // open: gt, lt
  Comparator #(.width(16), .mode("twosComplement")) comparator_2 (
    .a(\总周期数 ), .b(16'h1), .eq(comparator_2_eq));  // open: gt, lt
  Comparator #(.width(16), .mode("twosComplement")) comparator_3 (
    .a(\总周期数 ), .b(16'h4), .eq(comparator_3_eq));  // open: gt, lt
  Comparator #(.width(16), .mode("twosComplement")) comparator_4 (
    .a(\总周期数 ), .b(16'h7), .eq(comparator_4_eq));  // open: gt, lt
  D_Flip_Flop #(.trigger("rising"), .Pre_Clr_Positions("LEGACY"), .NegatePresetClear("false"), .enable("true"), .NewFFLayout("false")) d_ff_1 (
    .clk(IR1_t), .D(1'b1), .Q(d_ff_1_q), .en(1'b1), .reset(\中断1 ));  // open: Qn, preset
  or or_1 (W1, \中断1 , d_ff_1_q);
  D_Flip_Flop #(.trigger("rising"), .Pre_Clr_Positions("LEGACY"), .NegatePresetClear("false"), .enable("true"), .NewFFLayout("false")) d_ff_2 (
    .clk(IR2_t), .D(1'b1), .Q(d_ff_2_q), .en(1'b1), .reset(\中断2 ));  // open: Qn, preset
  or or_2 (W2, \中断2 , d_ff_2_q);
  D_Flip_Flop #(.trigger("rising"), .Pre_Clr_Positions("LEGACY"), .NegatePresetClear("false"), .enable("true"), .NewFFLayout("false")) d_ff_3 (
    .clk(IR3_t), .D(1'b1), .Q(d_ff_3_q), .en(1'b1), .reset(\中断3 ));  // open: Qn, preset
  or or_3 (W3, \中断3 , d_ff_3_q);
  Priority_Encoder #(.select(2), .disabled("Z")) priority_encoder_1 (
    .in0(1'b1), .in1(jalr), .in2(jal), .in3(or_8_out), .out(priority_encoder_1_out), .en_in(1'b1));  // open: gs, en_out
  Multiplexer #(.select(2), .width(32), .disabled("Z"), .enable("false")) multiplexer_1 (
    .in0(PC_4), .in1(ALUresult), .in2(adder_3_out), .in3(adder_2_out), .out(\老PC ),
    .sel(priority_encoder_1_out));
  not not_1 (not_1_out, halt);
  Hex_Digit_Display hex_digit_display_2 (.value(LedData[23:20]));  // open: dp
  Hex_Digit_Display hex_digit_display_3 (.value(LedData[27:24]));  // open: dp
  or or_4 (or_4_out, comparator_1_eq, comparator_2_eq);
  assign IRA = or_4_out ? ~CLK : 1'bz;  // Controlled_Inverter controlled_inverter_1
  assign IRB = comparator_3_eq ? ~CLK : 1'bz;  // Controlled_Inverter controlled_inverter_2
  assign IRC = comparator_4_eq ? ~CLK : 1'bz;  // Controlled_Inverter controlled_inverter_3
  or or_5 (or_5_out, d_ff_1_q, \中断1 );
  or or_6 (or_6_out, d_ff_2_q, \中断2 );
  or or_7 (or_7_out, d_ff_3_q, \中断3 );
  not not_2 (not_2_out, ALUequal);
  and and_1 (and_1_out, Beq, ALUequal);
  or or_8 (or_8_out, and_1_out, and_5_out, and_6_out);
  Register #(.width(32), .trigger("rising"), .Select("low")) u_PC (
    .D(\新PC ), .en(or_9_out), .Q(PC), .clk(CLK), .clr(RST));
  or or_9 (or_9_out, not_1_out, Go);
  Hex_Digit_Display hex_digit_display_4 (.value(LedData[19:16]));  // open: dp
  Hex_Digit_Display hex_digit_display_5 (.value(LedData[15:12]));  // open: dp
  Pull_Resistor #(.pull(0)) pull_resistor_1 (.node(IRA));
  Pull_Resistor #(.pull(0)) pull_resistor_2 (.node(IRB));
  Pull_Resistor #(.pull(0)) pull_resistor_3 (.node(IRC));
  and and_2 (and_2_out, or_5_out, ~RESET1);  // AND_Gate
  and and_3 (and_3_out, or_6_out, ~RESET2);  // AND_Gate
  and and_4 (and_4_out, or_7_out, ~RESET3);  // AND_Gate
  and and_5 (and_5_out, not_2_out, Bne);
  Hex_Digit_Display hex_digit_display_6 (.value(LedData[7:4]));  // open: dp
  Hex_Digit_Display hex_digit_display_7 (.value(LedData[11:8]));  // open: dp
  // Probe on \总周期数 
  D_Flip_Flop #(.trigger("rising"), .Pre_Clr_Positions("LEGACY"), .NegatePresetClear("false"), .enable("true"), .NewFFLayout("false")) d_ff_4 (
    .clk(CLK), .D(and_2_out), .Q(\中断1 ), .en(1'b1));  // open: Qn, preset, reset
  D_Flip_Flop #(.trigger("rising"), .Pre_Clr_Positions("LEGACY"), .NegatePresetClear("false"), .enable("true"), .NewFFLayout("false")) d_ff_5 (
    .clk(CLK), .D(and_3_out), .Q(\中断2 ), .en(1'b1));  // open: Qn, preset, reset
  D_Flip_Flop #(.trigger("rising"), .Pre_Clr_Positions("LEGACY"), .NegatePresetClear("false"), .enable("true"), .NewFFLayout("false")) d_ff_6 (
    .clk(CLK), .D(and_4_out), .Q(\中断3 ), .en(1'b1));  // open: Qn, preset, reset
  and and_6 (and_6_out, ALUl, \单周期硬布线控制器_1_bltu );
  // RiscV_Probe riscv_probe_1: pin names not known; wires that end beside it: IR
  Adder #(.width(32)) adder_1 (.a(PC), .b(32'h4), .out(PC_4));  // open: cin, cout
  Hex_Digit_Display hex_digit_display_8 (.value(LedData[3:0]));  // open: dp
  ROM #(.addrWidth(10), .dataWidth(32), .Select("high")) rom_1 (.addr(PC[11:2]), .data(IR));
  or or_10 (IR1_t, IR1, IRA);
  \单周期硬布线控制器  \u_单周期硬布线控制器_1  (
    .Funct({IR[30], IR[25], IR[14:12]}), .OP(IR[6:2]), .ALU_OP(\单周期硬布线控制器_1_alu_op ), .MemToReg(MemToReg),
    .MemWrite(MemWrite), .ALU_SRC(\单周期硬布线控制器_1_alu_src ), .RegWrite(RegWrite), .ecall(ecall), .S_type(Stype),
    .Jalr(jalr), .Beq(Beq), .JAL(jal), .Bne(Bne), .in_3(IR[21]), .uret(uret), .csr(csr), .U_Type(Utype),
    .BLTU(\单周期硬布线控制器_1_bltu ), .LB(LB));  // open: u2, u1
  Multiplexer #(.select(1), .width(5), .disabled("Z"), .enable("false")) multiplexer_2 (
    .in0(IR[19:15]), .in1(5'b10001), .out(multiplexer_2_out), .sel(ecall));
  Multiplexer #(.select(1), .width(5), .disabled("Z"), .enable("false")) multiplexer_3 (
    .in0(IR[24:20]), .in1(5'b01010), .out(multiplexer_3_out), .sel(ecall));
  Multiplexer #(.select(1), .width(12), .disabled("Z"), .enable("false")) multiplexer_4 (
    .in0(IR[31:20]), .in1({IR[31:25], IR[11:7]}), .out(multiplexer_4_out), .sel(Stype));
  or or_11 (IR2_t, IR2, IRB);
  assign bit_extender_1_out = {{20{multiplexer_4_out[11]}}, multiplexer_4_out};  // Bit_Extender bit_extender_1
  assign bit_extender_2_out = {{12{IR[31]}}, IR[31:12]};  // Bit_Extender bit_extender_2
  assign bit_extender_3_out = {{20{IR[31]}}, {IR[31], IR[7], IR[30:25], IR[11:8]}};  // Bit_Extender bit_extender_3
  assign bit_extender_4_out = {{12{IR[31]}}, {IR[31], IR[19:12], IR[20], IR[30:21]}};  // Bit_Extender bit_extender_4
  Priority_Encoder #(.select(2), .disabled("Z")) priority_encoder_2 (
    .in1(\中断1 ), .in2(\中断2 ), .in3(\中断3 ), .out(\中断号 ), .gs(\中断产生 ));  // open: in0, en_out, en_in
  Regifile regifile_1 (
    .Din(RDin), .Clk(CLK), .R1(regifile_1_r1), .R2(MDin), .WE(RegWrite), .W_num(IR[11:7]),
    .R1_num(multiplexer_2_out), .R2_num(multiplexer_3_out));
  Shifter #(.width(32), .shift("ll")) shifter_1 (.in(bit_extender_2_out), .\dist (5'b01100), .out(shifter_1_out));
  Shifter #(.width(32), .shift("ll")) shifter_2 (.in(bit_extender_3_out), .\dist (5'b00001), .out(shifter_2_out));
  Shifter #(.width(32), .shift("ll")) shifter_3 (.in(bit_extender_4_out), .\dist (5'b00001), .out(shifter_3_out));
  or or_12 (IR3_t, IR3, IRC);
  Multiplexer #(.select(1), .width(32), .disabled("Z"), .enable("false")) multiplexer_5 (
    .in0(MDin), .in1(bit_extender_1_out), .out(multiplexer_5_out), .sel(\单周期硬布线控制器_1_alu_src ));
  Adder #(.width(32)) adder_2 (.a(shifter_2_out), .b(PC), .out(adder_2_out));  // open: cin, cout
  Adder #(.width(32)) adder_3 (.a(shifter_3_out), .b(PC), .out(adder_3_out));  // open: cin, cout
  Multiplexer #(.select(2), .width(32), .disabled("Z"), .enable("false")) multiplexer_6 (
    .in0(\老PC ), .in1(EPC), .in2(\中断地址 ), .in3(EPC), .out(\新PC ), .sel({\中断 , uret}));
  Multiplexer #(.select(2), .width(32), .disabled("Z"), .enable("false")) multiplexer_7 (
    .in1(32'h30ac), .in2(32'h3150), .in3(32'h31f4), .out(\中断地址 ), .sel(\中断号 ));  // open: in0
  ALU alu_1 (
    .X(regifile_1_r1), .Y(multiplexer_5_out), .AluOP(\单周期硬布线控制器_1_alu_op ), .Equal(ALUequal),
    .Result(ALUresult), .out_4(ALUge), .out_6(ALUl));  // open: Result_2
  Demultiplexer #(.select(2), .width(1), .tristate("false"), .disabled("Z"), .enable("false")) demultiplexer_1 (
    .out1(RESET1), .out2(RESET2), .out3(RESET3), .in(uret), .sel(\中断号_q ));  // open: out0
  Register #(.width(2), .trigger("rising"), .Select("low")) \u_中断号  (
    .D(\中断号 ), .en(\中断 ), .Q(\中断号_q ), .clk(CLK));  // open: clr
  not not_3 (not_3_out, halt);
  Adder #(.width(32)) adder_4 (.a(shifter_1_out), .b(PC), .out(adder_4_out));  // open: cin, cout
  Register #(.width(32), .trigger("rising"), .Select("low")) u_EPC (
    .D(\老PC ), .en(\中断 ), .Q(EPC), .clk(CLK));  // open: clr
  Comparator #(.width(32), .mode("twosComplement")) comparator_5 (
    .a(regifile_1_r1), .b(32'h22), .eq(comparator_5_eq));  // open: gt, lt
  not not_4 (not_4_out, comparator_5_eq);
  Pull_Resistor #(.pull(0)) pull_resistor_4 (.node(RESET1));
  Counter #(.width(16), .max('hffff), .ongoal("wrap"), .trigger("rising"), .behavior("new")) counter_1 (
    .load(1'b0), .D({16{1'b0}}), .count(not_3_out), .Q(\总周期数 ), .clk(CLK), .clr(1'b0), .down(1'b0));  // open: carry, preset
  and and_7 (halt, ecall, not_4_out);
  and and_8 (and_8_out, comparator_5_eq, ecall);
  and and_9 (\中断 , \中断产生 , IE);
  Pull_Resistor #(.pull(0)) pull_resistor_5 (.node(RESET2));
  RAM #(.addrWidth(10), .dataWidth(32), .bus("separate"), .Select("high")) ram_1 (
    .addr(ALUresult[11:2]), .din(MDin), .data(ram_1_data), .str(MemWrite), .sel(1'b1), .clk(CLK), .ld(1'b1));  // open: clr
  Register #(.width(32), .trigger("rising"), .Select("low")) register_1 (
    .D(MDin), .en(and_8_out), .Q(LedData), .clk(CLK));  // open: clr
  D_Flip_Flop #(.trigger("high"), .Pre_Clr_Positions("LEGACY"), .NegatePresetClear("false"), .enable("true"), .NewFFLayout("false")) d_ff_7 (.Q(d_ff_7_q));  // open: clk, D, Qn, preset, en, reset
  // Probe on 13'hc
  D_Flip_Flop #(.trigger("rising"), .Pre_Clr_Positions("LEGACY"), .NegatePresetClear("false"), .enable("true"), .NewFFLayout("false")) d_ff_8 (
    .clk(CLK), .D(\中断 ), .Qn(IE), .en(or_13_out));  // open: Q, preset, reset
  or or_13 (or_13_out, \中断 , uret);
  Multiplexer #(.select(1), .width(32), .disabled("Z"), .enable("false")) multiplexer_8 (
    .in0(ram_1_data), .in1(LBData), .out(multiplexer_8_out), .sel(LB));
  Comparator #(.width(13), .mode("twosComplement")) comparator_6 (
    .a(CNT_num), .b(13'hc), .eq(comparator_6_eq), .lt(comparator_6_lt));  // open: gt
  Clock #(.highDuration(1), .lowDuration(1)) clock_1 (.out(clock_1_out));
  Pull_Resistor #(.pull(0)) pull_resistor_6 (.node(RESET3));
  or or_14 (or_14_out[0], Utype, MemToReg);
  Counter #(.width(13), .max('h1fff), .ongoal("stay"), .trigger("rising"), .behavior("old")) counter_2 (
    .count(comparator_6_lt), .Q(CNT_num), .clk(clock_1_out));  // open: load, D, carry, clr, preset
  or or_15 (or_14_out[1], Utype, jal, jalr);
  Multiplexer #(.select(2), .width(32), .disabled("Z"), .enable("false")) multiplexer_9 (
    .in0(ALUresult), .in1(multiplexer_8_out), .in2(PC_4), .in3(adder_4_out), .out(RDin), .sel(or_14_out));
  Multiplexer #(.select(2), .width(8), .disabled("Z"), .enable("false")) multiplexer_10 (
    .in0(ram_1_data[7:0]), .in1(ram_1_data[15:8]), .in2(ram_1_data[23:16]), .in3(ram_1_data[31:24]),
    .out(multiplexer_10_out), .sel(ALUresult[1:0]));
  nand nand_1 (nand_1_out, d_ff_7_q, comparator_6_eq);
  assign LBData = {{24{multiplexer_10_out[7]}}, multiplexer_10_out};  // Bit_Extender bit_extender_5
  assign CLK = nand_1_out ? clock_1_out : 1'bz;  // Controlled_Buffer controlled_buffer_1
  Pull_Resistor #(.pull(1)) pull_resistor_7 (.node(CLK));

  // Notes on the sheet:
  //   中断源
  //   中断等待指示
  //   总复位信号应将除ROM以外所有存储组件全部清零
  //   单级中断测试信号模拟器
  //   数码管输出
  //   数码管输出应该用寄存器锁存，否则显示数据只能一闪而过
  //   指令探针
  //   指令存储器
  //   指令字
  //   contents of rom_1 (hex, n*v repeats v):
  //   7d000113 100413 1f41993 41f9d993 433 c00913 800b13 140413 f47413 800293 100313 499993 89e9b3 1300533
  //   2200893 73 406282b3 fe0294e3 140413 f00f93 1f47433 1c41413 800293 100313 49d993 89e9b3 1300533
  //   2200893 73 406282b3 fe0294e3 1c45413 406b0b33 b0463 f95ff06f 2b3 fff2c293 1029293 fff2e293 500533
  //   2200893 73 f5dff06f 1112023 410113 a12023 410113 812023 410113 1312023 410113 1412023 410113 1512023
  //   410113 1612023 410113 100b13 300a13 100a93 1600433 441413 14469b3 1300533 2200893 73 fe0416e3
  //   415a0a33 fe0a10e3 ffc10113 12b03 ffc10113 12a83 ffc10113 12a03 ffc10113 12983 ffc10113 12403
  //   ffc10113 12503 ffc10113 12883 200073 1112023 410113 a12023 410113 812023 410113 1312023 410113
  //   1412023 410113 1512023 410113 1612023 410113 200b13 300a13 100a93 1600433 441413 14469b3 1300533
  //   2200893 73 fe0416e3 415a0a33 fe0a10e3 ffc10113 12b03 ffc10113 12a83 ffc10113 12a03 ffc10113 12983
  //   ffc10113 12403 ffc10113 12503 ffc10113 12883 200073 1112023 410113 a12023 410113 812023 410113
  //   1312023 410113 1412023 410113 1512023 410113 1612023 410113 300b13 300a13 100a93 1600433 441413
  //   14469b3 1300533 2200893 73 fe0416e3 415a0a33 fe0a10e3 ffc10113 12b03 ffc10113 12a83 ffc10113 12a03
  //   ffc10113 12983 ffc10113 12403 ffc10113 12503 ffc10113 12883 200073
  //   JAL
  //   JALR
  //   URET
  //   BLTU
  //   CSR
  //   rs1
  //   rs2
  //   rd
  //   I指令
  //   S指令
  //   U指令
  //   B指令
  //   J指令
  //   Beq
  //   Bne
  //   MemToReg
  //   MemWrite
  //   AluOP
  //   AluSrcB
  //   RegWrite
  //   为方便自动评测，需要输出PC，IR，寄存器堆写如数据RDin
  //   RAM写使能MemWrite、RAM写入数据MDin等信号
  //   数据存储器
  //   控制位
  //   暂停节拍，不能为0
  //   戳工具置1进入计数暂停模式，ctrl+k时钟自动运行到对应节拍暂停
  //   ctrl+k关闭时钟连续运行，将控制位置零，进入单步调试模式调试
  //   可计数暂停的时钟源
endmodule

module \单周期_多级中断  (
  input  IR1,
  input  IR2,
  input  IR3,
  output RegWrite,
  output MemWrite,
  output [31:0] PC,
  output [31:0] IR,
  output [31:0] RDin,
  output [31:0] MDin,
  output [31:0] LedData
);

  wire ALUequal, ALUge, ALUl, and_1_out, and_2_out, and_3_out, and_4_out, and_5_out, and_6_out, and_10_out,
       Beq, Bne, CLK, clock_1_out, comparator_1_eq, comparator_2_eq, comparator_3_eq, comparator_4_eq,
       comparator_5_eq, comparator_7_eq, comparator_8_eq, comparator_9_eq, comparator_10_eq,
       comparator_10_lt, csr, csrrci, csrrsi, d_ff_1_q, d_ff_2_q, d_ff_3_q, d_ff_8_q, demultiplexer_1_out0,
       demultiplexer_1_out1, demultiplexer_1_out2, demultiplexer_2_out0, demultiplexer_2_out1,
       demultiplexer_2_out2, ecall, Go, halt, IE, IR1_t, IR2_t, IR3_t, IRA, IRB, IRC, jal, jalr, LB,
       MemToReg, nand_1_out, not_1_out, not_2_out, not_3_out, not_4_out, or_4_out, or_5_out, or_6_out,
       or_7_out, or_8_out, or_9_out, or_10_out, or_14_out, or_15_out, or_16_out, priority_encoder_2_gs,
       RESET1, RESET2, RESET3, RST, Stype, uret, Utype, W1, W2, W3, \中断 , \中断1 , \中断2 , \中断3 , \中断优先 ,
       \单周期硬布线控制器_1_alu_src , \单周期硬布线控制器_1_bltu ;
  wire [1:0] EPC_4_q, EPC_5_q, EPC_6_q, or_17_out, priority_encoder_1_out, \中断号 , \中断计数 , \前中断号 ;
  wire [3:0] \单周期硬布线控制器_1_alu_op ;
  wire [4:0] multiplexer_2_out, multiplexer_3_out;
  wire [7:0] multiplexer_10_out;
  wire [11:0] multiplexer_5_out;
  wire [12:0] CNT_num;
  wire [15:0] \总周期数 ;
  wire [31:0] adder_2_out, adder_3_out, adder_4_out, ALUresult, bit_extender_1_out, bit_extender_2_out,
       bit_extender_3_out, bit_extender_4_out, EPC, EPC_2_q, EPC_3_q, EPC_q, LBData, multiplexer_6_out,
       multiplexer_8_out, PC_4, ram_1_data, regifile_1_r1, shifter_1_out, shifter_2_out, shifter_3_out,
       \中断地址 , \新PC , \老PC ;

  Button \u_继续运行  (.out(Go));
  Button _1 (.out(IRA));
  Button _2 (.out(IRB));
  Button _3 (.out(IRC));
  LED #(.active("true")) led_1 (.in(W1));
  LED #(.active("true")) led_2 (.in(W2));
  LED #(.active("true")) led_3 (.in(W3));
  Hex_Digit_Display hex_digit_display_1 (.value(LedData[31:28]));  // open: dp
  Comparator #(.width(16), .mode("twosComplement")) comparator_1 (
    .a(\总周期数 ), .b(16'h7), .eq(comparator_1_eq));  // open: gt, lt
  Comparator #(.width(16), .mode("twosComplement")) comparator_2 (
    .a(\总周期数 ), .b(16'h241), .eq(comparator_2_eq));  // open: gt, lt
  or or_1 (W1, \中断1 , d_ff_1_q);
  or or_2 (W2, \中断2 , d_ff_2_q);
  or or_3 (W3, \中断3 , d_ff_3_q);
  Hex_Digit_Display hex_digit_display_2 (.value(LedData[23:20]));  // open: dp
  Hex_Digit_Display hex_digit_display_3 (.value(LedData[27:24]));  // open: dp
  Comparator #(.width(16), .mode("twosComplement")) comparator_3 (
    .a(16'h258), .b(\总周期数 ), .eq(comparator_3_eq));  // open: gt, lt
  or or_4 (or_4_out, comparator_3_eq, comparator_4_eq);
  Comparator #(.width(16), .mode("twosComplement")) comparator_4 (
    .a(\总周期数 ), .b(16'h1), .eq(comparator_4_eq));  // open: gt, lt
  Comparator #(.width(16), .mode("twosComplement")) comparator_5 (
    .a(\总周期数 ), .b(16'h4), .eq(comparator_5_eq));  // open: gt, lt
  or or_5 (or_5_out, comparator_1_eq, comparator_2_eq);
  D_Flip_Flop #(.trigger("rising"), .Pre_Clr_Positions("LEGACY"), .NegatePresetClear("false"), .enable("true"), .NewFFLayout("false")) d_ff_1 (
    .clk(IR1_t), .D(1'b1), .Q(d_ff_1_q), .en(1'b1), .reset(\中断1 ));  // open: Qn, preset
  D_Flip_Flop #(.trigger("rising"), .Pre_Clr_Positions("LEGACY"), .NegatePresetClear("false"), .enable("true"), .NewFFLayout("false")) d_ff_2 (
    .clk(IR2_t), .D(1'b1), .Q(d_ff_2_q), .en(1'b1), .reset(\中断2 ));  // open: Qn, preset
  D_Flip_Flop #(.trigger("rising"), .Pre_Clr_Positions("LEGACY"), .NegatePresetClear("false"), .enable("true"), .NewFFLayout("false")) d_ff_3 (
    .clk(IR3_t), .D(1'b1), .Q(d_ff_3_q), .en(1'b1), .reset(\中断3 ));  // open: Qn, preset
  Priority_Encoder #(.select(2), .disabled("Z")) priority_encoder_1 (
    .in0(1'b1), .in1(jalr), .in2(jal), .in3(or_10_out), .out(priority_encoder_1_out), .en_in(1'b1));  // open: gs, en_out
  Hex_Digit_Display hex_digit_display_4 (.value(LedData[19:16]));  // open: dp
  Hex_Digit_Display hex_digit_display_5 (.value(LedData[15:12]));  // open: dp
  Pull_Resistor #(.pull(0)) pull_resistor_1 (.node(IRA));
  assign IRA = or_4_out ? ~CLK : 1'bz;  // Controlled_Inverter controlled_inverter_1
  Pull_Resistor #(.pull(0)) pull_resistor_2 (.node(IRB));
  assign IRB = comparator_5_eq ? ~CLK : 1'bz;  // Controlled_Inverter controlled_inverter_2
  Pull_Resistor #(.pull(0)) pull_resistor_3 (.node(IRC));
  assign IRC = or_5_out ? ~CLK : 1'bz;  // Controlled_Inverter controlled_inverter_3
  or or_6 (or_6_out, d_ff_1_q, \中断1 );
  or or_7 (or_7_out, d_ff_2_q, \中断2 );
  or or_8 (or_8_out, d_ff_3_q, \中断3 );
  and and_1 (and_1_out, Beq, ALUequal);
  Multiplexer #(.select(2), .width(32), .disabled("Z"), .enable("false")) multiplexer_1 (
    .in0(PC_4), .in1(ALUresult), .in2(adder_3_out), .in3(adder_2_out), .out(\老PC ),
    .sel(priority_encoder_1_out));
  or or_9 (or_9_out, not_1_out, Go);
  not not_1 (not_1_out, halt);
  Hex_Digit_Display hex_digit_display_6 (.value(LedData[11:8]));  // open: dp
  Hex_Digit_Display hex_digit_display_7 (.value(LedData[7:4]));  // open: dp
  // Probe on \总周期数 
  D_Flip_Flop #(.trigger("rising"), .Pre_Clr_Positions("LEGACY"), .NegatePresetClear("false"), .enable("true"), .NewFFLayout("false")) d_ff_4 (
    .clk(CLK), .D(and_2_out), .Q(\中断1 ), .en(1'b1));  // open: Qn, preset, reset
  and and_2 (and_2_out, or_6_out, ~RESET1);  // AND_Gate
  D_Flip_Flop #(.trigger("rising"), .Pre_Clr_Positions("LEGACY"), .NegatePresetClear("false"), .enable("true"), .NewFFLayout("false")) d_ff_5 (
    .clk(CLK), .D(and_3_out), .Q(\中断2 ), .en(1'b1));  // open: Qn, preset, reset
  and and_3 (and_3_out, or_7_out, ~RESET2);  // AND_Gate
  D_Flip_Flop #(.trigger("rising"), .Pre_Clr_Positions("LEGACY"), .NegatePresetClear("false"), .enable("true"), .NewFFLayout("false")) d_ff_6 (
    .clk(CLK), .D(and_4_out), .Q(\中断3 ), .en(1'b1));  // open: Qn, preset, reset
  and and_4 (and_4_out, or_8_out, ~RESET3);  // AND_Gate
  not not_2 (not_2_out, ALUequal);
  and and_5 (and_5_out, not_2_out, Bne);
  or or_10 (or_10_out, and_1_out, and_5_out, and_6_out);
  Register #(.width(32), .trigger("rising"), .Select("low")) u_PC (
    .D(\新PC ), .en(or_9_out), .Q(PC), .clk(CLK), .clr(RST));
  Hex_Digit_Display hex_digit_display_8 (.value(LedData[3:0]));  // open: dp
  and and_6 (and_6_out, ALUl, \单周期硬布线控制器_1_bltu );
  Adder #(.width(32)) adder_1 (.a(PC), .b(32'h4), .out(PC_4));  // open: cin, cout
  // RiscV_Probe riscv_probe_1: pin names not known; wires that end beside it: IR
  or or_11 (IR1_t, IR1, IRA);
  ROM #(.addrWidth(10), .dataWidth(32), .Select("high")) rom_1 (.addr(PC[11:2]), .data(IR));
  or or_12 (IR2_t, IR2, IRB);
  Multiplexer #(.select(1), .width(5), .disabled("Z"), .enable("false")) multiplexer_2 (
    .in0(IR[19:15]), .in1(5'b10001), .out(multiplexer_2_out), .sel(ecall));
  Multiplexer #(.select(1), .width(5), .disabled("Z"), .enable("false")) multiplexer_3 (
    .in0(IR[24:20]), .in1(5'b01010), .out(multiplexer_3_out), .sel(ecall));
  Multiplexer #(.select(2), .width(32), .disabled("Z"), .enable("false")) multiplexer_4 (
    .in0(\老PC ), .in1(EPC), .in2(\中断地址 ), .in3(EPC), .out(\新PC ), .sel({\中断 , uret}));
  Priority_Encoder #(.select(2), .disabled("Z")) priority_encoder_2 (
    .in1(\中断1 ), .in2(\中断2 ), .in3(\中断3 ), .out(\中断号 ), .gs(priority_encoder_2_gs));  // open: in0, en_out, en_in
  \单周期硬布线控制器  \u_单周期硬布线控制器_1  (
    .Funct({IR[30], IR[25], IR[14:12]}), .OP(IR[6:2]), .ALU_OP(\单周期硬布线控制器_1_alu_op ), .MemToReg(MemToReg),
    .MemWrite(MemWrite), .ALU_SRC(\单周期硬布线控制器_1_alu_src ), .RegWrite(RegWrite), .ecall(ecall), .S_type(Stype),
    .Jalr(jalr), .Beq(Beq), .JAL(jal), .Bne(Bne), .in_3(IR[21]), .uret(uret), .csr(csr), .U_Type(Utype),
    .BLTU(\单周期硬布线控制器_1_bltu ), .LB(LB));  // open: u2, u1
  Multiplexer #(.select(1), .width(12), .disabled("Z"), .enable("false")) multiplexer_5 (
    .in0(IR[31:20]), .in1({IR[31:25], IR[11:7]}), .out(multiplexer_5_out), .sel(Stype));
  assign bit_extender_1_out = {{12{IR[31]}}, IR[31:12]};  // Bit_Extender bit_extender_1
  or or_13 (IR3_t, IR3, IRC);
  assign bit_extender_2_out = {{20{multiplexer_5_out[11]}}, multiplexer_5_out};  // Bit_Extender bit_extender_2
  Shifter #(.width(32), .shift("ll")) shifter_1 (.in(bit_extender_1_out), .\dist (5'b01100), .out(shifter_1_out));
  assign bit_extender_3_out = {{20{IR[31]}}, {IR[31], IR[7], IR[30:25], IR[11:8]}};  // Bit_Extender bit_extender_3
  assign bit_extender_4_out = {{12{IR[31]}}, {IR[31], IR[19:12], IR[20], IR[30:21]}};  // Bit_Extender bit_extender_4
  and and_7 (\中断 , priority_encoder_2_gs, \中断优先 , IE);
  Comparator #(.width(2), .mode("unsigned")) comparator_6 (.a(\前中断号 ), .b(\中断号 ), .lt(\中断优先 ));  // open: gt, eq
  Pull_Resistor #(.pull(1)) pull_resistor_4 (.node(\中断优先 ));
  Comparator #(.width(3), .mode("twosComplement")) comparator_7 (
    .a(3'b110), .b(IR[14:12]), .eq(comparator_7_eq));  // open: gt, lt
  Comparator #(.width(3), .mode("twosComplement")) comparator_8 (
    .a(IR[14:12]), .b(3'b111), .eq(comparator_8_eq));  // open: gt, lt
  Regifile regifile_1 (
    .Din(RDin), .Clk(CLK), .R1(regifile_1_r1), .R2(MDin), .WE(RegWrite), .W_num(IR[11:7]),
    .R1_num(multiplexer_2_out), .R2_num(multiplexer_3_out));
  Shifter #(.width(32), .shift("ll")) shifter_2 (.in(bit_extender_3_out), .\dist (5'b00001), .out(shifter_2_out));
  Shifter #(.width(32), .shift("ll")) shifter_3 (.in(bit_extender_4_out), .\dist (5'b00001), .out(shifter_3_out));
  and and_8 (csrrsi, comparator_7_eq, csr);
  and and_9 (csrrci, csr, comparator_8_eq);
  Multiplexer #(.select(1), .width(32), .disabled("Z"), .enable("false")) multiplexer_6 (
    .in0(MDin), .in1(bit_extender_2_out), .out(multiplexer_6_out), .sel(\单周期硬布线控制器_1_alu_src ));
  Adder #(.width(32)) adder_2 (.a(shifter_2_out), .b(PC), .out(adder_2_out));  // open: cin, cout
  Adder #(.width(32)) adder_3 (.a(shifter_3_out), .b(PC), .out(adder_3_out));  // open: cin, cout
  or or_14 (or_14_out, \中断 , uret);
  Multiplexer #(.select(2), .width(32), .disabled("Z"), .enable("false")) multiplexer_7 (
    .in1(32'h30ac), .in2(32'h3158), .in3(32'h3204), .out(\中断地址 ), .sel(\中断号 ));  // open: in0
  ALU alu_1 (
    .X(regifile_1_r1), .Y(multiplexer_6_out), .AluOP(\单周期硬布线控制器_1_alu_op ), .Equal(ALUequal),
    .Result(ALUresult), .out_4(ALUge), .out_6(ALUl));  // open: Result_2
  Counter #(.width(2), .max('h3), .ongoal("wrap"), .trigger("rising"), .behavior("new")) counter_1 (
    .count(or_14_out), .Q(\中断计数 ), .clk(CLK), .down(uret));  // open: load, D, carry, clr, preset
  or or_15 (or_15_out, \中断 , csrrci);
  Adder #(.width(32)) adder_4 (.a(shifter_1_out), .b(PC), .out(adder_4_out));  // open: cin, cout
  or or_16 (or_16_out, \中断 , csrrci, csrrsi, uret);
  not not_3 (not_3_out, halt);
  Comparator #(.width(32), .mode("twosComplement")) comparator_9 (
    .a(regifile_1_r1), .b(32'h22), .eq(comparator_9_eq));  // open: gt, lt
  D_Flip_Flop #(.trigger("rising"), .Pre_Clr_Positions("LEGACY"), .NegatePresetClear("false"), .enable("true"), .NewFFLayout("false")) d_ff_7 (
    .clk(CLK), .D(or_15_out), .Qn(IE), .en(or_16_out));  // open: Q, preset, reset
  Counter #(.width(16), .max('hffff), .ongoal("wrap"), .trigger("rising"), .behavior("new")) counter_2 (
    .load(1'b0), .D({16{1'b0}}), .count(not_3_out), .Q(\总周期数 ), .clk(CLK), .clr(1'b0), .down(1'b0));  // open: carry, preset
  not not_4 (not_4_out, comparator_9_eq);
  and and_10 (and_10_out, comparator_9_eq, ecall);
  D_Flip_Flop #(.trigger("high"), .Pre_Clr_Positions("LEGACY"), .NegatePresetClear("false"), .enable("true"), .NewFFLayout("false")) d_ff_8 (.Q(d_ff_8_q));  // open: clk, D, Qn, preset, en, reset
  // Probe on 13'hc
  Demultiplexer #(.select(2), .width(1), .tristate("false"), .disabled("Z"), .enable("false")) demultiplexer_1 (
    .out0(demultiplexer_1_out0), .out1(demultiplexer_1_out1), .out2(demultiplexer_1_out2), .in(\中断 ),
    .sel(\中断计数 ));  // open: out3
  and and_11 (halt, ecall, not_4_out);
  Comparator #(.width(13), .mode("twosComplement")) comparator_10 (
    .a(CNT_num), .b(13'hc), .eq(comparator_10_eq), .lt(comparator_10_lt));  // open: gt
  Clock #(.highDuration(1), .lowDuration(1)) clock_1 (.out(clock_1_out));
  Demultiplexer #(.select(2), .width(1), .tristate("false"), .disabled("Z"), .enable("false")) demultiplexer_2 (
    .out0(demultiplexer_2_out0), .out1(demultiplexer_2_out1), .out2(demultiplexer_2_out2), .in(\中断 ),
    .sel(\中断计数 ));  // open: out3
  RAM #(.addrWidth(10), .dataWidth(32), .bus("separate"), .Select("high")) ram_1 (
    .addr(ALUresult[11:2]), .din(MDin), .data(ram_1_data), .str(MemWrite), .sel(1'b1), .clk(CLK), .ld(1'b1));  // open: clr
  Register #(.width(32), .trigger("rising"), .Select("low")) register_1 (
    .D(MDin), .en(and_10_out), .Q(LedData), .clk(CLK));  // open: clr
  Counter #(.width(13), .max('h1fff), .ongoal("stay"), .trigger("rising"), .behavior("old")) counter_3 (
    .count(comparator_10_lt), .Q(CNT_num), .clk(clock_1_out));  // open: load, D, carry, clr, preset
  Demultiplexer #(.select(2), .width(1), .tristate("false"), .disabled("Z"), .enable("false")) demultiplexer_3 (
    .out1(RESET1), .out2(RESET2), .out3(RESET3), .in(uret), .sel(\前中断号 ));  // open: out0
  or or_17 (or_17_out[0], Utype, MemToReg);
  Multiplexer #(.select(1), .width(32), .disabled("Z"), .enable("false")) multiplexer_8 (
    .in0(ram_1_data), .in1(LBData), .out(multiplexer_8_out), .sel(LB));
  nand nand_1 (nand_1_out, d_ff_8_q, comparator_10_eq);
  Register #(.width(32), .trigger("rising"), .Select("low")) u_EPC (
    .D(\老PC ), .en(demultiplexer_1_out0), .Q(EPC_q), .clk(CLK));  // open: clr
  Register #(.width(32), .trigger("rising"), .Select("low")) EPC_2 (
    .D(\老PC ), .en(demultiplexer_1_out1), .Q(EPC_2_q), .clk(CLK));  // open: clr
  Register #(.width(32), .trigger("rising"), .Select("low")) EPC_3 (
    .D(\老PC ), .en(demultiplexer_1_out2), .Q(EPC_3_q), .clk(CLK));  // open: clr
  Pull_Resistor #(.pull(0)) pull_resistor_5 (.node(RESET1));
  Multiplexer #(.select(2), .width(32), .disabled("Z"), .enable("false")) multiplexer_9 (
    .in0(ALUresult), .in1(multiplexer_8_out), .in2(PC_4), .in3(adder_4_out), .out(RDin), .sel(or_17_out));
  assign CLK = nand_1_out ? clock_1_out : 1'bz;  // Controlled_Buffer controlled_buffer_1
  Pull_Resistor #(.pull(1)) pull_resistor_6 (.node(CLK));
  Register #(.width(2), .trigger("rising"), .Select("low")) EPC_4 (
    .D(\中断号 ), .en(demultiplexer_2_out0), .Q(EPC_4_q), .clk(CLK));  // open: clr
  Register #(.width(2), .trigger("rising"), .Select("low")) EPC_5 (
    .D(\中断号 ), .en(demultiplexer_2_out1), .Q(EPC_5_q), .clk(CLK));  // open: clr
  Register #(.width(2), .trigger("rising"), .Select("low")) EPC_6 (
    .D(\中断号 ), .en(demultiplexer_2_out2), .Q(EPC_6_q), .clk(CLK));  // open: clr
  or or_18 (or_17_out[1], Utype, jal, jalr);
  Multiplexer #(.select(2), .width(8), .disabled("Z"), .enable("false")) multiplexer_10 (
    .in0(ram_1_data[7:0]), .in1(ram_1_data[15:8]), .in2(ram_1_data[23:16]), .in3(ram_1_data[31:24]),
    .out(multiplexer_10_out), .sel(ALUresult[1:0]));
  Multiplexer #(.select(2), .width(32), .disabled("Z"), .enable("false")) multiplexer_11 (
    .in1(EPC_q), .in2(EPC_2_q), .in3(EPC_3_q), .out(EPC), .sel(\中断计数 ));  // open: in0
  Multiplexer #(.select(2), .width(2), .disabled("Z"), .enable("false")) multiplexer_12 (
    .in1(EPC_4_q), .in2(EPC_5_q), .in3(EPC_6_q), .out(\前中断号 ), .sel(\中断计数 ));  // open: in0
  Pull_Resistor #(.pull(0)) pull_resistor_7 (.node(RESET2));
  assign LBData = {{24{multiplexer_10_out[7]}}, multiplexer_10_out};  // Bit_Extender bit_extender_5
  Pull_Resistor #(.pull(0)) pull_resistor_8 (.node(RESET3));

  // Notes on the sheet:
  //   中断源
  //   中断等待指示
  //   总复位信号应将除ROM以外所有存储组件全部清零
  //   多级中断测试信号模拟器
  //   数码管输出
  //   数码管输出应该用寄存器锁存，否则显示数据只能一闪而过
  //   指令探针
  //   指令存储器
  //   rs1
  //   rs2
  //   指令字
  //   contents of rom_1 (hex, n*v repeats v):
  //   7d000113 100413 1f41993 41f9d993 433 c00913 800b13 140413 f47413 800293 100313 499993 89e9b3 1300533
  //   2200893 73 406282b3 fe0294e3 140413 f00f93 1f47433 1c41413 800293 100313 49d993 89e9b3 1300533
  //   2200893 73 406282b3 fe0294e3 1c45413 406b0b33 b0463 f95ff06f 2b3 fff2c293 1029293 fff2e293 500533
  //   2200893 73 f5dff06f 1112023 410113 a12023 410113 812023 410113 1312023 410113 1412023 410113 1512023
  //   410113 1612023 410113 40e073 100b13 300a13 100a93 1600433 441413 14469b3 1300533 2200893 73 fe0416e3
  //   415a0a33 fe0a10e3 40f073 ffc10113 12b03 ffc10113 12a83 ffc10113 12a03 ffc10113 12983 ffc10113 12403
  //   ffc10113 12503 ffc10113 12883 200073 1112023 410113 a12023 410113 812023 410113 1312023 410113
  //   1412023 410113 1512023 410113 1612023 410113 40e073 200b13 300a13 100a93 1600433 441413 14469b3
  //   1300533 2200893 73 fe0416e3 415a0a33 fe0a10e3 40f073 ffc10113 12b03 ffc10113 12a83 ffc10113 12a03
  //   ffc10113 12983 ffc10113 12403 ffc10113 12503 ffc10113 12883 200073 1112023 410113 a12023 410113
  //   812023 410113 1312023 410113 1412023 410113 1512023 410113 1612023 410113 40e073 300b13 300a13
  //   100a93 1600433 441413 14469b3 1300533 2200893 73 fe0416e3 415a0a33 fe0a10e3 40f073 ffc10113 12b03
  //   ffc10113 12a83 ffc10113 12a03 ffc10113 12983 ffc10113 12403 ffc10113 12503 ffc10113 12883 200073
  //   rd
  //   I指令
  //   S指令
  //   PC更新
  //   JAL
  //   JALR
  //   URET
  //   BLTU
  //   CSR
  //   U指令
  //   B指令
  //   J指令
  //   Beq
  //   Bne
  //   MemToReg
  //   MemWrite
  //   AluOP
  //   AluSrcB
  //   RegWrite
  //   中断使能
  //   为方便自动评测，需要输出PC，IR，寄存器堆写如数据RDin
  //   RAM写使能MemWrite、RAM写入数据MDin等信号
  //   中断计数
  //   控制位
  //   暂停节拍，不能为0
  //   数据存储器
  //   戳工具置1进入计数暂停模式，ctrl+k时钟自动运行到对应节拍暂停
  //   ctrl+k关闭时钟连续运行，将控制位置零，进入单步调试模式调试
  //   保存中断号
  //   堆栈保存EPC
  //   可计数暂停的时钟源
endmodule

module \封装正确性测试  (
);

  wire IR1, IR2, IR3, MemW, RegW;
  wire [31:0] EX_PC, ID_PC, IF_PC, IR, LED, MDin, MDinr, MEM_PC, PC, RDin, RDinr, WB_PC;

  \单周期RISC_V  \u_单周期risc_v_1  (
    .IR1(IR1), .IR2(IR2), .IR3(IR3), .RegWrite(RegW), .MemWrite(MemW), .PC(PC), .IR(IR), .RDin(RDin),
    .MDin(MDin), .LedData(LED));
  \气泡流水线  \u_气泡流水线_1  (
    .RegWrite(RegW), .MemWrite(MemW), .IF_PC(IF_PC), .ID_PC(ID_PC), .EX_PC(EX_PC), .M_PC(MEM_PC),
    .WB_PC(WB_PC), .RDin(RDinr), .MDin(MDinr), .LedData(LED));
  \单周期_单级中断  \u_单周期_单级中断_1  (
    .IR1(IR1), .IR2(IR2), .IR3(IR3), .RegWrite(RegW), .MemWrite(MemW), .PC(PC), .IR(IR), .RDin(RDin),
    .MDin(MDin), .LedData(LED));
  \理想流水线  \u_理想流水线_1  (
    .RegWrite(RegW), .MemWrite(MemW), .IF_PC(IF_PC), .ID_PC(ID_PC), .EX_PC(EX_PC), .M_PC(MEM_PC),
    .WB_PC(WB_PC), .RDin(RDinr), .MDin(MDinr), .LedData(LED));
  \重定向流水线  \u_重定向流水线_1  (
    .RegWrite(RegW), .MemWrite(MemW), .IF_PC(IF_PC), .ID_PC(ID_PC), .EX_PC(EX_PC), .M_PC(MEM_PC),
    .WB_PC(WB_PC), .RDin(RDinr), .MDin(MDinr), .LedData(LED));
  \单周期_多级中断  \u_单周期_多级中断_1  (
    .IR1(IR1), .IR2(IR2), .IR3(IR3), .RegWrite(RegW), .MemWrite(MemW), .PC(PC), .IR(IR), .RDin(RDin),
    .MDin(MDin), .LedData(LED));

  // Notes on the sheet:
  //   单周期封装测试
  //   气泡流水封装测试
  //   单周期+单级中断封装测试
  //   请检查上面封装有无位宽不匹配，引脚标签是否和连接的标签相对应，否则无法在educoder平台上正确测试
  //   理想流水封装测试
  //   重定向流水封装测试
  //   单周期+多级中断封装测试
endmodule

module IF_ID (
  input  [31:0] PC,
  input  [31:0] PC_4,
  input  [31:0] IR,
  input  en,
  input  CLK,
  input  reset,
  input  flush,
  output [31:0] PC_2,
  output [31:0] PC_4_2,
  output [31:0] IR_2
);

  wire or_1_out;
  wire [31:0] multiplexer_1_out, multiplexer_2_out, multiplexer_3_out;

  Multiplexer #(.select(1), .width(32), .disabled("Z"), .enable("false")) multiplexer_1 (
    .in0(PC), .in1({32{1'b0}}), .out(multiplexer_1_out), .sel(or_1_out));
  Multiplexer #(.select(1), .width(32), .disabled("Z"), .enable("false")) multiplexer_2 (
    .in0(PC_4), .in1({32{1'b0}}), .out(multiplexer_2_out), .sel(or_1_out));
  Multiplexer #(.select(1), .width(32), .disabled("Z"), .enable("false")) multiplexer_3 (
    .in0(IR), .in1({32{1'b0}}), .out(multiplexer_3_out), .sel(or_1_out));
  or or_1 (or_1_out, reset, flush);
  Register #(.width(32), .trigger("rising"), .Select("low")) register_1 (
    .D(multiplexer_1_out), .en(en), .Q(PC_2), .clk(CLK));  // open: clr
  Register #(.width(32), .trigger("rising"), .Select("low")) register_2 (
    .D(multiplexer_2_out), .en(en), .Q(PC_4_2), .clk(CLK));  // open: clr
  Register #(.width(32), .trigger("rising"), .Select("low")) register_3 (
    .D(multiplexer_3_out), .en(en), .Q(IR_2), .clk(CLK));  // open: clr
endmodule

module ID_EX (
  input  Beq,
  input  Bne,
  input  MemToReg,
  input  MemWrite,
  input  AluSrcB,
  input  RegWrite,
  input  JAL,
  input  JALR,
  input  URET,
  input  S_type,
  input  U_type,
  input  BLTU,
  input  csr,
  input  LB,
  input  ecall,
  input  [3:0] AluOP,
  input  [4:0] rd,
  input  [31:0] R1,
  input  [31:0] R2,
  input  [31:0] imm_1,
  input  [31:0] imm_2,
  input  [31:0] imm_3,
  input  [31:0] PC,
  input  [31:0] PC_4,
  input  [31:0] IR,
  input  [1:0] rs1f,
  input  [1:0] rs2f,
  input  \预测跳转 ,
  input  reset,
  input  flush,
  input  en,
  input  CLK,
  output Beq_2,
  output Bne_2,
  output MemToReg_2,
  output MemWrite_2,
  output AluSrcB_2,
  output RegWrite_2,
  output JAL_2,
  output JALR_2,
  output URET_2,
  output S_type_2,
  output U_type_2,
  output BLTU_2,
  output csr_2,
  output LB_2,
  output ecall_2,
  output [3:0] AluOP_2,
  output [4:0] rd_2,
  output [31:0] R1_2,
  output [31:0] R2_2,
  output [31:0] imm_1_2,
  output [31:0] imm_2_2,
  output [31:0] imm_3_2,
  output [31:0] PC_2,
  output [31:0] PC_4_2,
  output [31:0] IR_2,
  output [1:0] rs1f_2,
  output [1:0] rs2f_2,
  output \预测跳转_2 
);

  wire and_1_out, multiplexer_1_out, multiplexer_2_out, multiplexer_3_out, multiplexer_4_out,
       multiplexer_5_out, multiplexer_6_out, multiplexer_7_out, multiplexer_8_out, multiplexer_9_out,
       multiplexer_10_out, multiplexer_11_out, multiplexer_12_out, multiplexer_13_out, multiplexer_14_out,
       multiplexer_15_out, not_1_out, or_1_out;
  wire [1:0] multiplexer_26_out, multiplexer_27_out;
  wire [3:0] multiplexer_16_out;
  wire [4:0] multiplexer_17_out;
  wire [31:0] multiplexer_18_out, multiplexer_19_out, multiplexer_20_out, multiplexer_21_out,
       multiplexer_22_out, multiplexer_23_out, multiplexer_24_out, multiplexer_25_out;

  Multiplexer #(.select(1), .width(1), .disabled("Z"), .enable("false")) multiplexer_1 (
    .in0(Beq), .in1(1'b0), .out(multiplexer_1_out), .sel(or_1_out));
  Multiplexer #(.select(1), .width(1), .disabled("Z"), .enable("false")) multiplexer_2 (
    .in0(Bne), .in1(1'b0), .out(multiplexer_2_out), .sel(or_1_out));
  Multiplexer #(.select(1), .width(1), .disabled("Z"), .enable("false")) multiplexer_3 (
    .in0(MemToReg), .in1(1'b0), .out(multiplexer_3_out), .sel(or_1_out));
  Multiplexer #(.select(1), .width(1), .disabled("Z"), .enable("false")) multiplexer_4 (
    .in0(MemWrite), .in1(1'b0), .out(multiplexer_4_out), .sel(or_1_out));
  Multiplexer #(.select(1), .width(1), .disabled("Z"), .enable("false")) multiplexer_5 (
    .in0(AluSrcB), .in1(1'b0), .out(multiplexer_5_out), .sel(or_1_out));
  Multiplexer #(.select(1), .width(1), .disabled("Z"), .enable("false")) multiplexer_6 (
    .in0(RegWrite), .in1(1'b0), .out(multiplexer_6_out), .sel(or_1_out));
  Multiplexer #(.select(1), .width(1), .disabled("Z"), .enable("false")) multiplexer_7 (
    .in0(JAL), .in1(1'b0), .out(multiplexer_7_out), .sel(or_1_out));
  Multiplexer #(.select(1), .width(1), .disabled("Z"), .enable("false")) multiplexer_8 (
    .in0(JALR), .in1(1'b0), .out(multiplexer_8_out), .sel(or_1_out));
  Multiplexer #(.select(1), .width(1), .disabled("Z"), .enable("false")) multiplexer_9 (
    .in0(URET), .in1(1'b0), .out(multiplexer_9_out), .sel(or_1_out));
  Multiplexer #(.select(1), .width(1), .disabled("Z"), .enable("false")) multiplexer_10 (
    .in0(S_type), .in1(1'b0), .out(multiplexer_10_out), .sel(or_1_out));
  Multiplexer #(.select(1), .width(1), .disabled("Z"), .enable("false")) multiplexer_11 (
    .in0(U_type), .in1(1'b0), .out(multiplexer_11_out), .sel(or_1_out));
  Multiplexer #(.select(1), .width(1), .disabled("Z"), .enable("false")) multiplexer_12 (
    .in0(BLTU), .in1(1'b0), .out(multiplexer_12_out), .sel(or_1_out));
  Multiplexer #(.select(1), .width(1), .disabled("Z"), .enable("false")) multiplexer_13 (
    .in0(csr), .in1(1'b0), .out(multiplexer_13_out), .sel(or_1_out));
  Multiplexer #(.select(1), .width(1), .disabled("Z"), .enable("false")) multiplexer_14 (
    .in0(LB), .in1(1'b0), .out(multiplexer_14_out), .sel(or_1_out));
  Multiplexer #(.select(1), .width(1), .disabled("Z"), .enable("false")) multiplexer_15 (
    .in0(ecall), .in1(1'b0), .out(multiplexer_15_out), .sel(or_1_out));
  Multiplexer #(.select(1), .width(4), .disabled("Z"), .enable("false")) multiplexer_16 (
    .in0(AluOP), .in1(4'b0000), .out(multiplexer_16_out), .sel(or_1_out));
  Multiplexer #(.select(1), .width(5), .disabled("Z"), .enable("false")) multiplexer_17 (
    .in0(rd), .in1({5{1'b0}}), .out(multiplexer_17_out), .sel(or_1_out));
  Multiplexer #(.select(1), .width(32), .disabled("Z"), .enable("false")) multiplexer_18 (
    .in0(R1), .in1({32{1'b0}}), .out(multiplexer_18_out), .sel(or_1_out));
  Multiplexer #(.select(1), .width(32), .disabled("Z"), .enable("false")) multiplexer_19 (
    .in0(R2), .in1({32{1'b0}}), .out(multiplexer_19_out), .sel(or_1_out));
  Multiplexer #(.select(1), .width(32), .disabled("Z"), .enable("false")) multiplexer_20 (
    .in0(imm_1), .in1({32{1'b0}}), .out(multiplexer_20_out), .sel(or_1_out));
  Multiplexer #(.select(1), .width(32), .disabled("Z"), .enable("false")) multiplexer_21 (
    .in0(imm_2), .in1({32{1'b0}}), .out(multiplexer_21_out), .sel(or_1_out));
  Multiplexer #(.select(1), .width(32), .disabled("Z"), .enable("false")) multiplexer_22 (
    .in0(imm_3), .in1({32{1'b0}}), .out(multiplexer_22_out), .sel(or_1_out));
  Multiplexer #(.select(1), .width(32), .disabled("Z"), .enable("false")) multiplexer_23 (
    .in0(PC), .in1({32{1'b0}}), .out(multiplexer_23_out), .sel(or_1_out));
  Multiplexer #(.select(1), .width(32), .disabled("Z"), .enable("false")) multiplexer_24 (
    .in0(PC_4), .in1({32{1'b0}}), .out(multiplexer_24_out), .sel(or_1_out));
  Multiplexer #(.select(1), .width(32), .disabled("Z"), .enable("false")) multiplexer_25 (
    .in0(IR), .in1({32{1'b0}}), .out(multiplexer_25_out), .sel(or_1_out));
  Multiplexer #(.select(1), .width(2), .disabled("Z"), .enable("false")) multiplexer_26 (
    .in0(rs1f), .in1(2'b00), .out(multiplexer_26_out), .sel(or_1_out));
  Multiplexer #(.select(1), .width(2), .disabled("Z"), .enable("false")) multiplexer_27 (
    .in0(rs2f), .in1(2'b00), .out(multiplexer_27_out), .sel(or_1_out));
  or or_1 (or_1_out, reset, flush);
  not not_1 (not_1_out, or_1_out);
  and and_1 (and_1_out, \预测跳转 , not_1_out);
  Register #(.width(1), .trigger("rising"), .Select("low")) register_1 (
    .D(multiplexer_1_out), .en(en), .Q(Beq_2), .clk(CLK));  // open: clr
  Register #(.width(1), .trigger("rising"), .Select("low")) register_2 (
    .D(multiplexer_2_out), .en(en), .Q(Bne_2), .clk(CLK));  // open: clr
  Register #(.width(1), .trigger("rising"), .Select("low")) register_3 (
    .D(multiplexer_3_out), .en(en), .Q(MemToReg_2), .clk(CLK));  // open: clr
  Register #(.width(1), .trigger("rising"), .Select("low")) register_4 (
    .D(multiplexer_4_out), .en(en), .Q(MemWrite_2), .clk(CLK));  // open: clr
  Register #(.width(1), .trigger("rising"), .Select("low")) register_5 (
    .D(multiplexer_5_out), .en(en), .Q(AluSrcB_2), .clk(CLK));  // open: clr
  Register #(.width(1), .trigger("rising"), .Select("low")) register_6 (
    .D(multiplexer_6_out), .en(en), .Q(RegWrite_2), .clk(CLK));  // open: clr
  Register #(.width(1), .trigger("rising"), .Select("low")) register_7 (
    .D(multiplexer_7_out), .en(en), .Q(JAL_2), .clk(CLK));  // open: clr
  Register #(.width(1), .trigger("rising"), .Select("low")) register_8 (
    .D(multiplexer_8_out), .en(en), .Q(JALR_2), .clk(CLK));  // open: clr
  Register #(.width(1), .trigger("rising"), .Select("low")) register_9 (
    .D(multiplexer_9_out), .en(en), .Q(URET_2), .clk(CLK));  // open: clr
  Register #(.width(1), .trigger("rising"), .Select("low")) register_10 (
    .D(multiplexer_10_out), .en(en), .Q(S_type_2), .clk(CLK));  // open: clr
  Register #(.width(1), .trigger("rising"), .Select("low")) register_11 (
    .D(multiplexer_11_out), .en(en), .Q(U_type_2), .clk(CLK));  // open: clr
  Register #(.width(1), .trigger("rising"), .Select("low")) register_12 (
    .D(multiplexer_12_out), .en(en), .Q(BLTU_2), .clk(CLK));  // open: clr
  Register #(.width(1), .trigger("rising"), .Select("low")) register_13 (
    .D(multiplexer_13_out), .en(en), .Q(csr_2), .clk(CLK));  // open: clr
  Register #(.width(1), .trigger("rising"), .Select("low")) register_14 (
    .D(multiplexer_14_out), .en(en), .Q(LB_2), .clk(CLK));  // open: clr
  Register #(.width(1), .trigger("rising"), .Select("low")) register_15 (
    .D(multiplexer_15_out), .en(en), .Q(ecall_2), .clk(CLK));  // open: clr
  Register #(.width(4), .trigger("rising"), .Select("low")) register_16 (
    .D(multiplexer_16_out), .en(en), .Q(AluOP_2), .clk(CLK));  // open: clr
  Register #(.width(5), .trigger("rising"), .Select("low")) register_17 (
    .D(multiplexer_17_out), .en(en), .Q(rd_2), .clk(CLK));  // open: clr
  Register #(.width(32), .trigger("rising"), .Select("low")) register_18 (
    .D(multiplexer_18_out), .en(en), .Q(R1_2), .clk(CLK));  // open: clr
  Register #(.width(32), .trigger("rising"), .Select("low")) register_19 (
    .D(multiplexer_19_out), .en(en), .Q(R2_2), .clk(CLK));  // open: clr
  Register #(.width(32), .trigger("rising"), .Select("low")) register_20 (
    .D(multiplexer_20_out), .en(en), .Q(imm_1_2), .clk(CLK));  // open: clr
  Register #(.width(32), .trigger("rising"), .Select("low")) register_21 (
    .D(multiplexer_21_out), .en(en), .Q(imm_2_2), .clk(CLK));  // open: clr
  Register #(.width(32), .trigger("rising"), .Select("low")) register_22 (
    .D(multiplexer_22_out), .en(en), .Q(imm_3_2), .clk(CLK));  // open: clr
  Register #(.width(32), .trigger("rising"), .Select("low")) register_23 (
    .D(multiplexer_23_out), .en(en), .Q(PC_2), .clk(CLK));  // open: clr
  Register #(.width(32), .trigger("rising"), .Select("low")) register_24 (
    .D(multiplexer_24_out), .en(en), .Q(PC_4_2), .clk(CLK));  // open: clr
  Register #(.width(32), .trigger("rising"), .Select("low")) register_25 (
    .D(multiplexer_25_out), .en(en), .Q(IR_2), .clk(CLK));  // open: clr
  Register #(.width(2), .trigger("rising"), .Select("low")) register_26 (
    .D(multiplexer_26_out), .en(en), .Q(rs1f_2), .clk(CLK));  // open: clr
  Register #(.width(2), .trigger("rising"), .Select("low")) register_27 (
    .D(multiplexer_27_out), .en(en), .Q(rs2f_2), .clk(CLK));  // open: clr
  Register #(.width(1), .trigger("rising"), .Select("low")) register_28 (
    .D(and_1_out), .en(en), .Q(\预测跳转_2 ), .clk(CLK));  // open: clr
endmodule

module EX_MEM (
  input  U_type,
  input  MemToReg,
  input  MemWrite,
  input  RegWrite,
  input  JAL,
  input  JALR,
  input  URET,
  input  LB,
  input  halt,
  input  [4:0] rd,
  input  [31:0] result,
  input  [31:0] Uimm,
  input  [31:0] R2,
  input  [31:0] PC,
  input  [31:0] PC_4,
  input  [31:0] IR,
  input  reset,
  input  flush,
  input  en,
  input  CLK,
  output U_type_2,
  output MemToReg_2,
  output MemWrite_2,
  output RegWrite_2,
  output JAL_2,
  output JALR_2,
  output URET_2,
  output LB_2,
  output halt_2,
  output [4:0] rd_2,
  output [31:0] result_2,
  output [31:0] Uimm_2,
  output [31:0] R2_2,
  output [31:0] PC_2,
  output [31:0] PC_4_2,
  output [31:0] IR_2
);

  wire multiplexer_1_out, multiplexer_2_out, multiplexer_3_out, multiplexer_4_out, multiplexer_5_out,
       multiplexer_6_out, multiplexer_7_out, multiplexer_8_out, multiplexer_9_out, or_1_out;
  wire [4:0] multiplexer_10_out;
  wire [31:0] multiplexer_11_out, multiplexer_12_out, multiplexer_13_out, multiplexer_14_out,
       multiplexer_15_out, multiplexer_16_out;

  Multiplexer #(.select(1), .width(1), .disabled("Z"), .enable("false")) multiplexer_1 (
    .in0(U_type), .in1(1'b0), .out(multiplexer_1_out), .sel(or_1_out));
  Multiplexer #(.select(1), .width(1), .disabled("Z"), .enable("false")) multiplexer_2 (
    .in0(MemToReg), .in1(1'b0), .out(multiplexer_2_out), .sel(or_1_out));
  Multiplexer #(.select(1), .width(1), .disabled("Z"), .enable("false")) multiplexer_3 (
    .in0(MemWrite), .in1(1'b0), .out(multiplexer_3_out), .sel(or_1_out));
  Multiplexer #(.select(1), .width(1), .disabled("Z"), .enable("false")) multiplexer_4 (
    .in0(RegWrite), .in1(1'b0), .out(multiplexer_4_out), .sel(or_1_out));
  Multiplexer #(.select(1), .width(1), .disabled("Z"), .enable("false")) multiplexer_5 (
    .in0(JAL), .in1(1'b0), .out(multiplexer_5_out), .sel(or_1_out));
  Multiplexer #(.select(1), .width(1), .disabled("Z"), .enable("false")) multiplexer_6 (
    .in0(JALR), .in1(1'b0), .out(multiplexer_6_out), .sel(or_1_out));
  Multiplexer #(.select(1), .width(1), .disabled("Z"), .enable("false")) multiplexer_7 (
    .in0(URET), .in1(1'b0), .out(multiplexer_7_out));  // open: sel
  Multiplexer #(.select(1), .width(1), .disabled("Z"), .enable("false")) multiplexer_8 (
    .in0(LB), .in1(1'b0), .out(multiplexer_8_out), .sel(or_1_out));
  Multiplexer #(.select(1), .width(1), .disabled("Z"), .enable("false")) multiplexer_9 (
    .in0(halt), .in1(1'b0), .out(multiplexer_9_out), .sel(or_1_out));
  Multiplexer #(.select(1), .width(5), .disabled("Z"), .enable("false")) multiplexer_10 (
    .in0(rd), .in1({5{1'b0}}), .out(multiplexer_10_out), .sel(or_1_out));
  Multiplexer #(.select(1), .width(32), .disabled("Z"), .enable("false")) multiplexer_11 (
    .in0(result), .in1({32{1'b0}}), .out(multiplexer_11_out), .sel(or_1_out));
  Multiplexer #(.select(1), .width(32), .disabled("Z"), .enable("false")) multiplexer_12 (
    .in0(Uimm), .in1({32{1'b0}}), .out(multiplexer_12_out), .sel(or_1_out));
  Multiplexer #(.select(1), .width(32), .disabled("Z"), .enable("false")) multiplexer_13 (
    .in0(R2), .in1({32{1'b0}}), .out(multiplexer_13_out), .sel(or_1_out));
  Multiplexer #(.select(1), .width(32), .disabled("Z"), .enable("false")) multiplexer_14 (
    .in0(PC), .in1({32{1'b0}}), .out(multiplexer_14_out), .sel(or_1_out));
  Multiplexer #(.select(1), .width(32), .disabled("Z"), .enable("false")) multiplexer_15 (
    .in0(PC_4), .in1({32{1'b0}}), .out(multiplexer_15_out), .sel(or_1_out));
  Multiplexer #(.select(1), .width(32), .disabled("Z"), .enable("false")) multiplexer_16 (
    .in0(IR), .in1({32{1'b0}}), .out(multiplexer_16_out), .sel(or_1_out));
  or or_1 (or_1_out, reset, flush);
  Register #(.width(1), .trigger("rising"), .Select("low")) register_1 (
    .D(multiplexer_1_out), .en(en), .Q(U_type_2), .clk(CLK));  // open: clr
  Register #(.width(1), .trigger("rising"), .Select("low")) register_2 (
    .D(multiplexer_2_out), .en(en), .Q(MemToReg_2), .clk(CLK));  // open: clr
  Register #(.width(1), .trigger("rising"), .Select("low")) register_3 (
    .D(multiplexer_3_out), .en(en), .Q(MemWrite_2), .clk(CLK));  // open: clr
  Register #(.width(1), .trigger("rising"), .Select("low")) register_4 (
    .D(multiplexer_4_out), .en(en), .Q(RegWrite_2), .clk(CLK));  // open: clr
  Register #(.width(1), .trigger("rising"), .Select("low")) register_5 (
    .D(multiplexer_5_out), .en(en), .Q(JAL_2), .clk(CLK));  // open: clr
  Register #(.width(1), .trigger("rising"), .Select("low")) register_6 (
    .D(multiplexer_6_out), .en(en), .Q(JALR_2), .clk(CLK));  // open: clr
  Register #(.width(1), .trigger("rising"), .Select("low")) register_7 (
    .D(multiplexer_7_out), .en(en), .Q(URET_2));  // open: clk, clr
  Register #(.width(1), .trigger("rising"), .Select("low")) register_8 (
    .D(multiplexer_8_out), .en(en), .Q(LB_2), .clk(CLK));  // open: clr
  Register #(.width(1), .trigger("rising"), .Select("low")) register_9 (
    .D(multiplexer_9_out), .en(en), .Q(halt_2), .clk(CLK));  // open: clr
  Register #(.width(5), .trigger("rising"), .Select("low")) register_10 (
    .D(multiplexer_10_out), .en(en), .Q(rd_2), .clk(CLK));  // open: clr
  Register #(.width(32), .trigger("rising"), .Select("low")) register_11 (
    .D(multiplexer_11_out), .en(en), .Q(result_2), .clk(CLK));  // open: clr
  Register #(.width(32), .trigger("rising"), .Select("low")) register_12 (
    .D(multiplexer_12_out), .en(en), .Q(Uimm_2), .clk(CLK));  // open: clr
  Register #(.width(32), .trigger("rising"), .Select("low")) register_13 (
    .D(multiplexer_13_out), .en(en), .Q(R2_2), .clk(CLK));  // open: clr
  Register #(.width(32), .trigger("rising"), .Select("low")) register_14 (
    .D(multiplexer_14_out), .en(en), .Q(PC_2), .clk(CLK));  // open: clr
  Register #(.width(32), .trigger("rising"), .Select("low")) register_15 (
    .D(multiplexer_15_out), .en(en), .Q(PC_4_2), .clk(CLK));  // open: clr
  Register #(.width(32), .trigger("rising"), .Select("low")) register_16 (
    .D(multiplexer_16_out), .en(en), .Q(IR_2), .clk(CLK));  // open: clr
endmodule

module MEM_WB (
  input  U_type,
  input  LB,
  input  MemToReg,
  input  RegWrite,
  input  JAL,
  input  JALR,
  input  URET,
  input  halt,
  input  [4:0] rd,
  input  [31:0] ALUresult,
  input  [31:0] MemData,
  input  [31:0] Uimm,
  input  [31:0] PC,
  input  [31:0] PC_4,
  input  [31:0] IR,
  input  [31:0] IR_2,
  input  reset,
  input  flush,
  input  en,
  input  CLK,
  output U_type_2,
  output LB_2,
  output MemToReg_2,
  output RegWrite_2,
  output JAL_2,
  output JALR_2,
  output URET_2,
  output halt_2,
  output [4:0] rd_2,
  output [31:0] ALUresult_2,
  output [31:0] MemData_2,
  output [31:0] Uimm_2,
  output [31:0] PC_2,
  output [31:0] PC_4_2
);

  wire multiplexer_1_out, multiplexer_2_out, multiplexer_3_out, multiplexer_4_out, multiplexer_5_out,
       multiplexer_6_out, multiplexer_7_out, multiplexer_8_out, or_1_out;
  wire [4:0] multiplexer_9_out;
  wire [31:0] multiplexer_10_out, multiplexer_11_out, multiplexer_12_out, multiplexer_13_out,
       multiplexer_14_out, multiplexer_15_out;

  Multiplexer #(.select(1), .width(1), .disabled("Z"), .enable("false")) multiplexer_1 (
    .in0(U_type), .in1(1'b0), .out(multiplexer_1_out), .sel(or_1_out));
  Multiplexer #(.select(1), .width(1), .disabled("Z"), .enable("false")) multiplexer_2 (
    .in0(LB), .in1(1'b0), .out(multiplexer_2_out), .sel(or_1_out));
  Multiplexer #(.select(1), .width(1), .disabled("Z"), .enable("false")) multiplexer_3 (
    .in0(MemToReg), .in1(1'b0), .out(multiplexer_3_out), .sel(or_1_out));
  Multiplexer #(.select(1), .width(1), .disabled("Z"), .enable("false")) multiplexer_4 (
    .in0(RegWrite), .in1(1'b0), .out(multiplexer_4_out), .sel(or_1_out));
  Multiplexer #(.select(1), .width(1), .disabled("Z"), .enable("false")) multiplexer_5 (
    .in0(JAL), .in1(1'b0), .out(multiplexer_5_out), .sel(or_1_out));
  Multiplexer #(.select(1), .width(1), .disabled("Z"), .enable("false")) multiplexer_6 (
    .in0(JALR), .in1(1'b0), .out(multiplexer_6_out), .sel(or_1_out));
  Multiplexer #(.select(1), .width(1), .disabled("Z"), .enable("false")) multiplexer_7 (
    .in0(URET), .in1(1'b0), .out(multiplexer_7_out), .sel(or_1_out));
  Multiplexer #(.select(1), .width(1), .disabled("Z"), .enable("false")) multiplexer_8 (
    .in0(halt), .in1(1'b0), .out(multiplexer_8_out), .sel(or_1_out));
  Multiplexer #(.select(1), .width(5), .disabled("Z"), .enable("false")) multiplexer_9 (
    .in0(rd), .in1({5{1'b0}}), .out(multiplexer_9_out), .sel(or_1_out));
  Multiplexer #(.select(1), .width(32), .disabled("Z"), .enable("false")) multiplexer_10 (
    .in0(ALUresult), .in1({32{1'b0}}), .out(multiplexer_10_out), .sel(or_1_out));
  Multiplexer #(.select(1), .width(32), .disabled("Z"), .enable("false")) multiplexer_11 (
    .in0(MemData), .in1({32{1'b0}}), .out(multiplexer_11_out), .sel(or_1_out));
  Multiplexer #(.select(1), .width(32), .disabled("Z"), .enable("false")) multiplexer_12 (
    .in0(Uimm), .in1({32{1'b0}}), .out(multiplexer_12_out), .sel(or_1_out));
  Multiplexer #(.select(1), .width(32), .disabled("Z"), .enable("false")) multiplexer_13 (
    .in0(PC), .in1({32{1'b0}}), .out(multiplexer_13_out), .sel(or_1_out));
  Multiplexer #(.select(1), .width(32), .disabled("Z"), .enable("false")) multiplexer_14 (
    .in0(PC_4), .in1({32{1'b0}}), .out(multiplexer_14_out), .sel(or_1_out));
  Multiplexer #(.select(1), .width(32), .disabled("Z"), .enable("false")) multiplexer_15 (
    .in0(IR), .in1({32{1'b0}}), .out(multiplexer_15_out), .sel(or_1_out));
  or or_1 (or_1_out, reset, flush);
  Register #(.width(1), .trigger("rising"), .Select("low")) register_1 (
    .D(multiplexer_1_out), .en(en), .Q(U_type_2), .clk(CLK));  // open: clr
  Register #(.width(1), .trigger("rising"), .Select("low")) register_2 (
    .D(multiplexer_2_out), .en(en), .Q(LB_2), .clk(CLK));  // open: clr
  Register #(.width(1), .trigger("rising"), .Select("low")) register_3 (
    .D(multiplexer_3_out), .en(en), .Q(MemToReg_2), .clk(CLK));  // open: clr
  Register #(.width(1), .trigger("rising"), .Select("low")) register_4 (
    .D(multiplexer_4_out), .en(en), .Q(RegWrite_2), .clk(CLK));  // open: clr
  Register #(.width(1), .trigger("rising"), .Select("low")) register_5 (
    .D(multiplexer_5_out), .en(en), .Q(JAL_2), .clk(CLK));  // open: clr
  Register #(.width(1), .trigger("rising"), .Select("low")) register_6 (
    .D(multiplexer_6_out), .en(en), .Q(JALR_2), .clk(CLK));  // open: clr
  Register #(.width(1), .trigger("rising"), .Select("low")) register_7 (
    .D(multiplexer_7_out), .en(en), .Q(URET_2));  // open: clk, clr
  Register #(.width(1), .trigger("rising"), .Select("low")) register_8 (
    .D(multiplexer_8_out), .en(en), .Q(halt_2), .clk(CLK));  // open: clr
  Register #(.width(5), .trigger("rising"), .Select("low")) register_9 (
    .D(multiplexer_9_out), .en(en), .Q(rd_2), .clk(CLK));  // open: clr
  Register #(.width(32), .trigger("rising"), .Select("low")) register_10 (
    .D(multiplexer_10_out), .en(en), .Q(ALUresult_2), .clk(CLK));  // open: clr
  Register #(.width(32), .trigger("rising"), .Select("low")) register_11 (
    .D(multiplexer_11_out), .en(en), .Q(MemData_2), .clk(CLK));  // open: clr
  Register #(.width(32), .trigger("rising"), .Select("low")) register_12 (
    .D(multiplexer_12_out), .en(en), .Q(Uimm_2), .clk(CLK));  // open: clr
  Register #(.width(32), .trigger("rising"), .Select("low")) register_13 (
    .D(multiplexer_13_out), .en(en), .Q(PC_2), .clk(CLK));  // open: clr
  Register #(.width(32), .trigger("rising"), .Select("low")) register_14 (
    .D(multiplexer_14_out), .en(en), .Q(PC_4_2), .clk(CLK));  // open: clr
  Register #(.width(32), .trigger("rising"), .Select("low")) register_15 (
    .D(multiplexer_15_out), .en(en), .Q(IR_2), .clk(CLK));  // open: clr
endmodule

module \气泡流水线子电路  (
  input  [31:0] IR,
  input  u1,
  input  EX_RegWrite,
  input  u2,
  input  MEM_RegWrite,
  input  [4:0] EX_rd,
  input  branch,
  input  [4:0] MEM_rd,
  input  ecall,
  output \冲突 ,
  output flush
);

  wire and_1_out, and_2_out, and_3_out, and_4_out, and_5_out, comparator_1_eq, comparator_2_eq,
       comparator_3_eq, comparator_4_eq, comparator_5_eq, comparator_6_eq, comparator_7_eq, comparator_8_eq,
       comparator_9_eq, comparator_10_eq, comparator_11_eq, comparator_12_eq, not_1_out, not_2_out,
       not_3_out, not_4_out, or_1_out;

  Comparator #(.width(5), .mode("twosComplement")) comparator_1 (
    .a(5'b10001), .b(EX_rd), .eq(comparator_1_eq));  // open: gt, lt
  Comparator #(.width(5), .mode("twosComplement")) comparator_2 (
    .a(EX_rd), .b(5'b01010), .eq(comparator_2_eq));  // open: gt, lt
  Comparator #(.width(5), .mode("twosComplement")) comparator_3 (
    .a(5'b10001), .b(MEM_rd), .eq(comparator_3_eq));  // open: gt, lt
  Comparator #(.width(5), .mode("twosComplement")) comparator_4 (
    .a(MEM_rd), .b(5'b01010), .eq(comparator_4_eq));  // open: gt, lt
  Comparator #(.width(5), .mode("twosComplement")) comparator_5 (
    .a(EX_rd), .b(IR[24:20]), .eq(comparator_5_eq));  // open: gt, lt
  not not_1 (not_1_out, comparator_6_eq);
  Comparator #(.width(5), .mode("twosComplement")) comparator_6 (
    .a(IR[24:20]), .b({5{1'b0}}), .eq(comparator_6_eq));  // open: gt, lt
  Comparator #(.width(5), .mode("twosComplement")) comparator_7 (
    .a(EX_rd), .b(IR[19:15]), .eq(comparator_7_eq));  // open: gt, lt
  Comparator #(.width(5), .mode("twosComplement")) comparator_8 (
    .a(IR[19:15]), .b({5{1'b0}}), .eq(comparator_8_eq));  // open: gt, lt
  Comparator #(.width(5), .mode("twosComplement")) comparator_9 (
    .a(MEM_rd), .b(IR[24:20]), .eq(comparator_9_eq));  // open: gt, lt
  Comparator #(.width(5), .mode("twosComplement")) comparator_10 (
    .a(IR[24:20]), .b({5{1'b0}}), .eq(comparator_10_eq));  // open: gt, lt
  Comparator #(.width(5), .mode("twosComplement")) comparator_11 (
    .a(MEM_rd), .b(IR[19:15]), .eq(comparator_11_eq));  // open: gt, lt
  Comparator #(.width(5), .mode("twosComplement")) comparator_12 (
    .a(IR[19:15]), .b({5{1'b0}}), .eq(comparator_12_eq));  // open: gt, lt
  not not_2 (not_2_out, comparator_8_eq);
  not not_3 (not_3_out, comparator_10_eq);
  not not_4 (not_4_out, comparator_12_eq);
  or or_1 (or_1_out, comparator_1_eq, comparator_2_eq, comparator_3_eq, comparator_4_eq);
  and and_1 (and_1_out, EX_RegWrite, u2, comparator_5_eq, not_1_out);
  and and_2 (and_2_out, EX_RegWrite, u1, comparator_7_eq, not_2_out);
  and and_3 (and_3_out, MEM_RegWrite, u2, comparator_9_eq, not_3_out);
  and and_4 (and_4_out, MEM_RegWrite, u1, comparator_11_eq, not_4_out);
  and and_5 (and_5_out, or_1_out, ecall);
  or or_2 (\冲突 , and_5_out, and_1_out, and_2_out, and_3_out, and_4_out);
  or or_3 (flush, \冲突 , branch);

  // Other names for the same wires on the sheet: RS1[4:0] = IR[19:15]; RS2[4:0] = IR[24:20]
endmodule

module \重定向流水线处理  (
  input  [31:0] IR,
  input  u1,
  input  EX_RegWrite,
  input  u2,
  input  MEM_RegWrite,
  input  [4:0] EX_rd,
  input  branch,
  input  EX_MemToReg,
  input  [4:0] MEM_rd,
  input  ecall,
  output \冲突 ,
  output flush,
  output [1:0] RS1_Forward,
  output [1:0] RS2_Forward
);

  wire and_1_out, and_2_out, and_3_out, and_4_out, and_5_out, and_6_out, and_8_out, and_9_out, and_10_out,
       and_11_out, comparator_1_eq, comparator_2_eq, comparator_3_eq, comparator_4_eq, comparator_5_eq,
       comparator_6_eq, comparator_7_eq, comparator_8_eq, comparator_9_eq, comparator_10_eq,
       comparator_11_eq, comparator_12_eq, comparator_13_eq, comparator_14_eq, comparator_15_eq,
       comparator_16_eq, not_1_out, not_2_out, not_3_out, not_4_out, not_5_out, not_6_out, not_7_out,
       not_8_out, or_3_out, or_6_out;

  Comparator #(.width(5), .mode("twosComplement")) comparator_1 (
    .a(EX_rd), .b(IR[24:20]), .eq(comparator_1_eq));  // open: gt, lt
  not not_1 (not_1_out, comparator_2_eq);
  Comparator #(.width(5), .mode("twosComplement")) comparator_2 (
    .a(IR[24:20]), .b({5{1'b0}}), .eq(comparator_2_eq));  // open: gt, lt
  Comparator #(.width(5), .mode("twosComplement")) comparator_3 (
    .a(EX_rd), .b(IR[19:15]), .eq(comparator_3_eq));  // open: gt, lt
  not not_2 (not_2_out, comparator_4_eq);
  Comparator #(.width(5), .mode("twosComplement")) comparator_4 (
    .a(IR[19:15]), .b({5{1'b0}}), .eq(comparator_4_eq));  // open: gt, lt
  Comparator #(.width(5), .mode("twosComplement")) comparator_5 (
    .a(EX_rd), .b(IR[19:15]), .eq(comparator_5_eq));  // open: gt, lt
  Comparator #(.width(5), .mode("twosComplement")) comparator_6 (
    .a(IR[19:15]), .b({5{1'b0}}), .eq(comparator_6_eq));  // open: gt, lt
  not not_3 (not_3_out, comparator_6_eq);
  Comparator #(.width(5), .mode("twosComplement")) comparator_7 (
    .a(EX_rd), .b(5'b10001), .eq(comparator_7_eq));  // open: gt, lt
  Comparator #(.width(5), .mode("twosComplement")) comparator_8 (
    .a(MEM_rd), .b(IR[19:15]), .eq(comparator_8_eq));  // open: gt, lt
  not not_4 (not_4_out, comparator_9_eq);
  Comparator #(.width(5), .mode("twosComplement")) comparator_9 (
    .a(IR[19:15]), .b({5{1'b0}}), .eq(comparator_9_eq));  // open: gt, lt
  Comparator #(.width(5), .mode("twosComplement")) comparator_10 (
    .a(MEM_rd), .b(5'b10001), .eq(comparator_10_eq));  // open: gt, lt
  and and_1 (and_1_out, comparator_7_eq, EX_RegWrite, ecall);
  and and_2 (and_2_out, comparator_10_eq, MEM_RegWrite, ecall);
  and and_3 (and_3_out, EX_MemToReg, u2, comparator_1_eq, not_1_out);
  and and_4 (and_4_out, EX_MemToReg, u1, comparator_3_eq, not_2_out);
  and and_5 (and_5_out, EX_RegWrite, u1, comparator_5_eq, not_3_out);
  and and_6 (and_6_out, MEM_RegWrite, u1, comparator_8_eq, not_4_out);
  or or_1 (\冲突 , and_3_out, and_4_out);
  or or_2 (RS1_Forward[1], and_5_out, and_1_out);
  or or_3 (or_3_out, and_6_out, and_2_out);
  or or_4 (flush, \冲突 , branch);
  not not_5 (not_5_out, RS1_Forward[1]);
  and and_7 (RS1_Forward[0], not_5_out, or_3_out);
  Comparator #(.width(5), .mode("twosComplement")) comparator_11 (
    .a(EX_rd), .b(IR[24:20]), .eq(comparator_11_eq));  // open: gt, lt
  not not_6 (not_6_out, comparator_12_eq);
  Comparator #(.width(5), .mode("twosComplement")) comparator_12 (
    .a(IR[24:20]), .b({5{1'b0}}), .eq(comparator_12_eq));  // open: gt, lt
  Comparator #(.width(5), .mode("twosComplement")) comparator_13 (
    .a(EX_rd), .b(5'b01010), .eq(comparator_13_eq));  // open: gt, lt
  Comparator #(.width(5), .mode("twosComplement")) comparator_14 (
    .a(MEM_rd), .b(IR[24:20]), .eq(comparator_14_eq));  // open: gt, lt
  not not_7 (not_7_out, comparator_15_eq);
  Comparator #(.width(5), .mode("twosComplement")) comparator_15 (
    .a(IR[24:20]), .b({5{1'b0}}), .eq(comparator_15_eq));  // open: gt, lt
  Comparator #(.width(5), .mode("twosComplement")) comparator_16 (
    .a(MEM_rd), .b(5'b01010), .eq(comparator_16_eq));  // open: gt, lt
  and and_8 (and_8_out, comparator_13_eq, EX_RegWrite, ecall);
  and and_9 (and_9_out, comparator_16_eq, MEM_RegWrite, ecall);
  and and_10 (and_10_out, EX_RegWrite, u2, comparator_11_eq, not_6_out);
  and and_11 (and_11_out, MEM_RegWrite, u2, comparator_14_eq, not_7_out);
  or or_5 (RS2_Forward[1], and_10_out, and_8_out);
  or or_6 (or_6_out, and_11_out, and_9_out);
  not not_8 (not_8_out, RS2_Forward[1]);
  and and_12 (RS2_Forward[0], not_8_out, or_6_out);

  // Other names for the same wires on the sheet: RS1[4:0] = IR[19:15]; RS2[4:0] = IR[24:20]
endmodule
