// Logisim project cpu21-riscv(answer).circ as structural Verilog: 24 circuits, main circuit ◇单周期RISC-V
module \单周期RISC_V  (
  input  IR1,
  input  IR2,
  input  IR3,
  output RegWrite,
  output MemWrite,
  output [31:0] PC,
  output [31:0] IR,
  output [31:0] RDin,
  output [31:0] MDin,
  output [31:0] LedData
);

  wire AluSrcB, and_1_out, and_2_out, and_3_out, and_4_out, and_5_out, B, Beq, Blt, Bne, CLK, clock_1_out,
       comparator_1_eq, comparator_2_eq, comparator_3_eq, comparator_3_lt, d_ff_1_q, ecall, equal, Go, halt,
       IR1_t, IR2_t, IR3_t, IRA, IRB, IRC, J, JAL, JALR, less, MemToReg, nand_1_out, not_1_out, not_2_out,
       not_3_out, not_4_out, not_5_out, riscv_probe_1_p2, S_Type, Sb, W1, W2, W3;
  wire [3:0] AluOP, ByteSelect, multiplexer_10_out;
  wire [4:0] multiplexer_4_out, multiplexer_5_out, multiplexer_11_out;
  wire [11:0] multiplexer_6_out, shifter_1_out;
  wire [12:0] CNT_num;
  wire [15:0] \总周期数 ;
  wire [19:0] shifter_2_out;
  wire [31:0] adder_2_out, adder_3_out, bit_extender_1_out, bit_extender_2_out, bit_extender_3_out,
       mips_ram_1_p7, multiplexer_1_out, multiplexer_2_out, multiplexer_8_out, multiplexer_9_out, PC_4, PCin,
       R1, R2, Result, shifter_3_out;

  Button \u_继续运行  (.out(Go));
  Button _1 (.out(IRA));
  Button _2 (.out(IRB));
  Button _3 (.out(IRC));
  LED #(.active("true")) led_1 (.in(W1));
  LED #(.active("true")) led_2 (.in(W2));
  LED #(.active("true")) led_3 (.in(W3));
  Comparator #(.width(32), .mode("twosComplement")) comparator_1 (
    .a(R2), .b(32'h22), .eq(comparator_1_eq));  // open: gt, lt
  Hex_Digit_Display hex_digit_display_1 (.value(LedData[31:28]));  // open: dp
  Comparator #(.width(32), .mode("twosComplement")) comparator_2 (
    .a(R2), .b(32'h22), .eq(comparator_2_eq));  // open: gt, lt
  not not_1 (not_1_out, comparator_1_eq);
  Register #(.width(32), .trigger("rising"), .Select("low")) u_PC (
    .D(PCin), .en(not_2_out), .Q(PC), .clk(CLK));  // open: clr
  not not_2 (not_2_out, halt);
  Hex_Digit_Display hex_digit_display_2 (.value(LedData[27:24]));  // open: dp
  Hex_Digit_Display hex_digit_display_3 (.value(LedData[23:20]));  // open: dp
  and and_1 (and_1_out, ecall, comparator_2_eq);
  and and_2 (and_2_out, ecall, not_1_out);
  Hex_Digit_Display hex_digit_display_4 (.value(LedData[19:16]));  // open: dp
  Hex_Digit_Display hex_digit_display_5 (.value(LedData[15:12]));  // open: dp
  Register #(.width(32), .trigger("rising"), .Select("low")) register_1 (
    .D(R1), .en(and_1_out), .Q(LedData), .clk(CLK));  // open: clr
  Register #(.width(1), .trigger("falling"), .Select("low")) register_2 (
    .D(and_2_out), .Q(halt), .clk(CLK), .clr(Go));  // open: en
  Hex_Digit_Display hex_digit_display_6 (.value(LedData[7:4]));  // open: dp
  Hex_Digit_Display hex_digit_display_7 (.value(LedData[11:8]));  // open: dp
  // Probe on \总周期数 
  not not_3 (not_3_out, halt);
  Counter #(.width(16), .max('hffff), .ongoal("wrap"), .trigger("rising"), .behavior("new")) counter_1 (
    .count(not_3_out), .Q(\总周期数 ), .clk(CLK));  // open: load, D, carry, clr, preset, down
  ROM #(.addrWidth(10), .dataWidth(32), .Select("high")) rom_1 (.addr(PC[11:2]), .data(IR));
  Hex_Digit_Display hex_digit_display_8 (.value(LedData[3:0]));  // open: dp
  Shifter #(.width(12), .shift("ll")) shifter_1 (
    .in({IR[31], IR[7], IR[30:25], IR[11:8]}), .\dist (4'b0001), .out(shifter_1_out));
  Shifter #(.width(20), .shift("ll")) shifter_2 (
    .in({IR[31], IR[19:12], IR[20], IR[30:21]}), .\dist (5'b00001), .out(shifter_2_out));
  and and_3 (and_3_out, Beq, equal);
  not not_4 (not_4_out, equal);
  and and_4 (and_4_out, not_4_out, Bne);
  and and_5 (and_5_out, less, Blt);
  assign bit_extender_1_out = {{20{shifter_1_out[11]}}, shifter_1_out};  // Bit_Extender bit_extender_1
  assign bit_extender_2_out = {{12{shifter_2_out[19]}}, shifter_2_out};  // Bit_Extender bit_extender_2
  or or_1 (IR1_t, IR1, IRA);
  Adder #(.width(32)) adder_1 (.a(PC), .b(32'h4), .out(PC_4));  // open: cin, cout
  Multiplexer #(.select(1), .width(32), .disabled("Z"), .enable("false")) multiplexer_1 (
    .in0(PC_4), .in1(adder_2_out), .out(multiplexer_1_out), .sel(B));
  Adder #(.width(32)) adder_2 (.a(bit_extender_1_out), .b(PC), .out(adder_2_out));  // open: cin, cout
  Adder #(.width(32)) adder_3 (.a(bit_extender_2_out), .b(PC), .out(adder_3_out));  // open: cin, cout
  or or_2 (IR2_t, IR2, IRB);
  // RiscV_Probe riscv_probe_1: pin names not known; wires that end beside it: IR, riscv_probe_1_p2, ecall, IR[24:20]
  or or_3 (B, and_3_out, and_4_out, and_5_out);
  Multiplexer #(.select(1), .width(32), .disabled("Z"), .enable("false")) multiplexer_2 (
    .in0(multiplexer_1_out), .in1(adder_3_out), .out(multiplexer_2_out), .sel(JAL));
  Multiplexer #(.select(1), .width(32), .disabled("Z"), .enable("false")) multiplexer_3 (
    .in0(multiplexer_2_out), .in1(Result), .out(PCin), .sel(JALR));
  or or_4 (IR3_t, IR3, IRC);
  \单周期硬布线控制器  \u_单周期硬布线控制器_1  (
    .Funct({IR[30], IR[25], IR[14:12]}), .OP(IR[6:2]), .ALU_OP(AluOP), .MemToReg(MemToReg),
    .MemWrite(MemWrite), .ALU_SRC(AluSrcB), .RegWrite(RegWrite), .ecall(ecall), .S_type(S_Type), .Jalr(JALR),
    .Beq(Beq), .JAL(JAL), .Bne(Bne), .in_3(IR[21]), .uret(riscv_probe_1_p2), .Blt(Blt), .Sb(Sb));  // open: CSRRCI, CSRRSI
  Multiplexer #(.select(1), .width(5), .disabled("Z"), .enable("false")) multiplexer_4 (
    .in0(IR[19:15]), .in1(5'b01010), .out(multiplexer_4_out), .sel(ecall));
  Multiplexer #(.select(1), .width(5), .disabled("Z"), .enable("false")) multiplexer_5 (
    .in0(IR[24:20]), .in1(5'b10001), .out(multiplexer_5_out), .sel(ecall));
  Multiplexer #(.select(1), .width(12), .disabled("Z"), .enable("false")) multiplexer_6 (
    .in0(IR[31:20]), .in1({IR[31:25], IR[11:7]}), .out(multiplexer_6_out), .sel(S_Type));
  assign bit_extender_3_out = {{20{multiplexer_6_out[11]}}, multiplexer_6_out};  // Bit_Extender bit_extender_3
  Multiplexer #(.select(1), .width(32), .disabled("Z"), .enable("false")) multiplexer_7 (
    .in0(multiplexer_9_out), .in1(PC_4), .out(RDin), .sel(J));
  or or_5 (J, JAL, JALR);
  Regifile regifile_1 (
    .Din(RDin), .Clk(CLK), .R1(R1), .R2(R2), .WE(RegWrite), .W_num(IR[11:7]), .R1_num(multiplexer_4_out),
    .R2_num(multiplexer_5_out));
  Multiplexer #(.select(1), .width(32), .disabled("Z"), .enable("false")) multiplexer_8 (
    .in0(R2), .in1(bit_extender_3_out), .out(multiplexer_8_out), .sel(AluSrcB));
  Multiplexer #(.select(1), .width(32), .disabled("Z"), .enable("false")) multiplexer_9 (
    .in0(Result), .in1(mips_ram_1_p7), .out(multiplexer_9_out), .sel(MemToReg));
  ALU alu_1 (
    .X(R1), .Y(multiplexer_8_out), .AluOP(AluOP), .Equal(equal), .Result(Result), .out_6(less));  // open: Result_2, out_4
  D_Flip_Flop #(.trigger("high"), .Pre_Clr_Positions("LEGACY"), .NegatePresetClear("false"), .enable("true"), .NewFFLayout("false")) d_ff_1 (.Q(d_ff_1_q));  // open: clk, D, Qn, preset, en, reset
  // Probe on 13'hc
  Multiplexer #(.select(2), .width(4), .disabled("Z"), .enable("false")) multiplexer_10 (
    .in0(4'b0001), .in1(4'b0010), .in2(4'b0100), .in3(4'b1000), .out(multiplexer_10_out), .sel(Result[1:0]));
  Multiplexer #(.select(2), .width(5), .disabled("Z"), .enable("false")) multiplexer_11 (
    .in0({5{1'b0}}), .in1(5'b01000), .in2(5'b10000), .in3(5'b11000), .out(multiplexer_11_out),
    .sel(Result[1:0]));
  not not_5 (not_5_out, MemWrite);
  Comparator #(.width(13), .mode("twosComplement")) comparator_3 (
    .a(CNT_num), .b(13'hc), .eq(comparator_3_eq), .lt(comparator_3_lt));  // open: gt
  Clock #(.highDuration(1), .lowDuration(1)) clock_1 (.out(clock_1_out));
  // MIPS_RAM mips_ram_1: pin names not known; wires that end beside it: Result[11:2], MDin, MemWrite, ByteSelect, CLK, not_5_out, mips_ram_1_p7
  Counter #(.width(13), .max('h1fff), .ongoal("stay"), .trigger("rising"), .behavior("old")) counter_2 (
    .count(comparator_3_lt), .Q(CNT_num), .clk(clock_1_out));  // open: load, D, carry, clr, preset
  Multiplexer #(.select(1), .width(4), .disabled("Z"), .enable("false")) multiplexer_12 (
    .in0(4'b1111), .in1(multiplexer_10_out), .out(ByteSelect), .sel(Sb));
  Shifter #(.width(32), .shift("ll")) shifter_3 (.in(R2), .\dist (multiplexer_11_out), .out(shifter_3_out));
  nand nand_1 (nand_1_out, d_ff_1_q, comparator_3_eq);
  Multiplexer #(.select(1), .width(32), .disabled("Z"), .enable("false")) multiplexer_13 (
    .in0(R2), .in1(shifter_3_out), .out(MDin), .sel(Sb));
  assign CLK = nand_1_out ? clock_1_out : 1'bz;  // Controlled_Buffer controlled_buffer_1
  Pull_Resistor #(.pull(1)) pull_resistor_1 (.node(CLK));

  // Notes on the sheet:
  //   中断源
  //   中断等待指示
  //   数码管输出应该用寄存器锁存，否则显示数据只能一闪而过
  //   数码管输出
  //   指令存储器
  //   contents of rom_1 (hex, n*v repeats v):
  //   100493 100006f 100493 200913 300993 100006f 100493 200913 300993 100006f 100493 200913 300993
  //   100006f 100493 200913 300993 3b8000ef 100413 100493 1f49493 900533 2200893 73 24d493 48463 fedff06f
  //   900533 2200893 73 100493 249493 900533 2200893 73 48463 fedff06f 100493 1f49493 900533 2200893 73
  //   4034d493 900533 2200893 73 4044d493 900533 2200893 73 4044d493 900533 2200893 73 4044d493 900533
  //   2200893 73 4044d493 900533 2200893 73 4044d493 900533 2200893 73 4044d493 900533 2200893 73 4044d493
  //   900533 2200893 73 100413 1f41993 41f9d993 433 c00913 300b13 140413 f47413 800293 100313 499993
  //   89e9b3 1300533 2200893 73 406282b3 fe0294e3 140413 f00f93 1f47433 1c41413 800293 100313 49d993
  //   89e9b3 1300533 2200893 73 406282b3 fe0294e3 1c45413 406b0b33 b0463 f95ff06f 2b3 fff2c293 829293
  //   ff2e293 500533 2200893 73 fff00413 493 84a023 140413 448493 84a023 140413 448493 84a023 140413
  //   448493 84a023 140413 448493 84a023 140413 448493 84a023 140413 448493 84a023 140413 448493 84a023
  //   140413 448493 84a023 140413 448493 84a023 140413 448493 84a023 140413 448493 84a023 140413 448493
  //   84a023 140413 448493 84a023 140413 448493 84a023 140413 448493 84a023 140413 448493 140413 433
  //   3c00493 42983 4aa03 149a2b3 28663 134a023 1442023 ffc48493 fe9412e3 800533 2200893 73 440413 3c00493
  //   fc9416e3 3200893 73 100293 300313 800493 849493 7648493 1449493 900533 2200893 73 800e13 54d4b3
  //   64d4b3 900533 2200893 73 fffe0e13 fe0e14e3 a00893 73 100293 300313 800493 849493 7648493 1449493
  //   900533 2200893 73 800e13 4054d4b3 4064d4b3 900533 2200893 73 fffe0e13 fe0e14e3 a00893 73 313 2000e13
  //   493 100913 930023 900533 2200893 73 12484b3 130313 fffe0e13 fe0e12e3 800e13 313 32483 900533 2200893
  //   73 430313 fffe0e13 fe0e14e3 a00893 73 ff100493 900533 2200893 73 148493 fe04c8e3 a00893 73 a00893 73
  //   413 140413 800533 2200893 73 240413 800533 2200893 73 340413 800533 2200893 73 440413 800533 2200893
  //   73 540413 800533 2200893 73 640413 800533 2200893 73 740413 800533 2200893 73 840413 800533 2200893
  //   2200893 73 8067
  //   b型imm
  //   j型imm
  //   指令探针
  //   JAL
  //   JALR
  //   func
  //   rs1
  //   rs2
  //   指令字
  //   rd
  //   s型imm
  //   Beq
  //   Bne
  //   Blt
  //   URET
  //   I型imm
  //   MemToReg
  //   MemWrite
  //   AluOP
  //   AluSrcB
  //   RegWrite
  //   S_Type
  //   为方便自动评测，需要输出PC，IR，寄存器堆写如数据RDin
  //   RAM写使能MemWrite、RAM写入数据MDin等信号
  //   控制位
  //   暂停节拍，不能为0
  //   数据存储器
  //   戳工具置1进入计数暂停模式，ctrl+k时钟自动运行到对应节拍暂停
  //   ctrl+k关闭时钟连续运行，将控制位置零，进入单步调试模式调试
  //   用这个时钟源需要去掉电路中的其他时钟源
  //   可计数暂停的时钟源
endmodule

// 单周期硬布线控制器
module \单周期硬布线控制器  (
  input  [4:0] OP,
  input  [4:0] Funct,
  input  in_3,
  output [3:0] ALU_OP,
  output uret,
  output MemToReg,
  output ecall,
  output MemWrite,
  output CSRRSI,
  output CSRRCI,
  output Sb,
  output ALU_SRC,
  output RegWrite,
  output Blt,
  output S_type,
  output Beq,
  output Bne,
  output Jalr,
  output JAL
);

  wire \控制信号自动生成_1_ecall ;

  \运算控制器自动生成  \u_运算控制器自动生成_1  (
    .OP2(OP[0]), .OP3(OP[1]), .OP4(OP[2]), .OP5(OP[3]), .OP6(OP[4]), .F12(Funct[0]), .F13(Funct[1]),
    .F14(Funct[2]), .F25(Funct[3]), .F30(Funct[4]), .S0(ALU_OP[0]), .S1(ALU_OP[1]), .S2(ALU_OP[2]),
    .S3(ALU_OP[3]));
  \控制信号自动生成  \u_控制信号自动生成_1  (
    .OP2(OP[0]), .OP3(OP[1]), .MemToReg(MemToReg), .OP4(OP[2]), .OP5(OP[3]), .OP6(OP[4]), .F12(Funct[0]),
    .MemWrite(MemWrite), .F13(Funct[1]), .F14(Funct[2]), .F25(Funct[3]), .CSRRSI(CSRRSI), .F30(Funct[4]),
    .CSRRCI(CSRRCI), .Sb(Sb), .ALU_SRC(ALU_SRC), .RegWrite(RegWrite), .Blt(Blt), .ecall(\控制信号自动生成_1_ecall ),
    .S_Type(S_type), .BEQ(Beq), .BNE(Bne), .JALR(Jalr), .JAL(JAL));
  and and_1 (uret, in_3, \控制信号自动生成_1_ecall );
  and and_2 (ecall, ~in_3, \控制信号自动生成_1_ecall );  // AND_Gate

  // Other names for the same wires on the sheet: IR21 = in_3; OP_CODE[4:0] = OP

  // Notes on the sheet:
  //   运算器控制器，根据指令生成运算器功能选择信号
  //   控制信号生成，产生数据通路需要的其他控制信号
endmodule

// 运算器控制器
module \运算控制器自动生成  (
  input  OP2,
  input  OP3,
  input  OP4,
  input  OP5,
  input  OP6,
  input  F12,
  input  F13,
  input  F14,
  input  F25,
  input  F30,
  output S0,
  output S1,
  output S2,
  output S3
);

  wire and_1_out, and_2_out, and_3_out, and_4_out, and_5_out, and_6_out, and_7_out, and_8_out, and_9_out,
       and_10_out, and_11_out, and_12_out, and_13_out, and_14_out, and_15_out, and_16_out, and_17_out,
       and_18_out, and_19_out, and_20_out, and_21_out, and_22_out, and_23_out, and_24_out, and_25_out,
       and_26_out, and_27_out, and_28_out, and_29_out, and_30_out, and_31_out, and_32_out, and_33_out,
       and_34_out, and_35_out, and_36_out, and_37_out, and_38_out, and_39_out, not_1_out, not_2_out,
       not_3_out, not_4_out, not_5_out, not_6_out, not_7_out, not_8_out, not_9_out, not_10_out, not_11_out,
       not_12_out, not_13_out, not_14_out, not_15_out, not_16_out, not_17_out, not_18_out, not_19_out,
       not_20_out, not_21_out, not_22_out, not_23_out, not_24_out, not_25_out, not_26_out, not_27_out,
       not_28_out, not_29_out, not_30_out, not_31_out, not_32_out, not_33_out, not_34_out, not_35_out,
       not_36_out, not_37_out, not_38_out, not_39_out, not_40_out, not_41_out, not_42_out, not_43_out,
       not_44_out, not_45_out, not_46_out, not_47_out, not_48_out, not_49_out, not_50_out, not_51_out,
       not_52_out, not_53_out, not_54_out, not_55_out, not_56_out, not_57_out, not_58_out, not_59_out,
       not_60_out, not_61_out, not_62_out, not_63_out, not_64_out, not_65_out, not_66_out, not_67_out,
       not_68_out, not_69_out, not_70_out, not_71_out, not_72_out, not_73_out, not_74_out, not_75_out,
       not_76_out, not_77_out, not_78_out, not_79_out, not_80_out, not_81_out, not_82_out, not_83_out,
       not_84_out, not_85_out, not_86_out, not_87_out, not_88_out, not_89_out, not_90_out, not_91_out,
       not_92_out, not_93_out, not_94_out, not_95_out, not_96_out, not_97_out, not_98_out, not_99_out,
       not_100_out, not_101_out, not_102_out, not_103_out, not_104_out, not_105_out, not_106_out,
       not_107_out, not_108_out, not_109_out, not_110_out, not_111_out, not_112_out, not_113_out,
       not_114_out, not_115_out, not_116_out, not_117_out, not_118_out, not_119_out, not_120_out,
       not_121_out, not_122_out, not_123_out, not_124_out, not_125_out, not_126_out, not_127_out,
       not_128_out, not_129_out, not_130_out, not_131_out, not_132_out, not_133_out, not_134_out,
       not_135_out, not_136_out, not_137_out, not_138_out, not_139_out, not_140_out, not_141_out,
       not_142_out, not_143_out, not_144_out, not_145_out, not_146_out, not_147_out, not_148_out,
       not_149_out, not_150_out, not_151_out, not_152_out, not_153_out, not_154_out, not_155_out,
       not_156_out, not_157_out, not_158_out, not_159_out, not_160_out, not_161_out, not_162_out,
       not_163_out, not_164_out, not_165_out, not_166_out, not_167_out, not_168_out, not_169_out,
       not_170_out, not_171_out, not_172_out, not_173_out, not_174_out, not_175_out, not_176_out,
       not_177_out, not_178_out, not_179_out, not_180_out, not_181_out, not_182_out, not_183_out,
       not_184_out, not_185_out, not_186_out, not_187_out, not_188_out, not_189_out, not_190_out,
       not_191_out, not_192_out, not_193_out, not_194_out, not_195_out, not_196_out, not_197_out,
       not_198_out, not_199_out, not_200_out, not_201_out, not_202_out, not_203_out, not_204_out,
       not_205_out, not_206_out, not_207_out, not_208_out, not_209_out, not_210_out, not_211_out,
       not_212_out, not_213_out, not_214_out, not_215_out, not_216_out, not_217_out, not_218_out,
       not_219_out, not_220_out, not_221_out, not_222_out, not_223_out, not_224_out, not_225_out,
       not_226_out, not_227_out, not_228_out, not_229_out, not_230_out, not_231_out, not_232_out,
       not_233_out, not_234_out, not_235_out, not_236_out, not_237_out, not_238_out, not_239_out, not_240_out;

  not not_1 (not_1_out, F30);
  not not_2 (not_2_out, F25);
  not not_3 (not_3_out, F14);
  not not_4 (not_4_out, F13);
  not not_5 (not_5_out, F12);
  not not_6 (not_6_out, OP6);
  not not_7 (not_7_out, OP3);
  not not_8 (not_8_out, OP2);
  not not_9 (not_9_out, F30);
  not not_10 (not_10_out, F25);
  not not_11 (not_11_out, OP6);
  not not_12 (not_12_out, OP3);
  not not_13 (not_13_out, OP2);
  not not_14 (not_14_out, F30);
  not not_15 (not_15_out, F25);
  not not_16 (not_16_out, F14);
  not not_17 (not_17_out, F12);
  not not_18 (not_18_out, OP6);
  not not_19 (not_19_out, OP3);
  not not_20 (not_20_out, OP2);
  not not_21 (not_21_out, F14);
  not not_22 (not_22_out, F13);
  not not_23 (not_23_out, F12);
  not not_24 (not_24_out, OP6);
  not not_25 (not_25_out, OP5);
  not not_26 (not_26_out, OP3);
  not not_27 (not_27_out, OP2);
  not not_28 (not_28_out, OP6);
  not not_29 (not_29_out, OP5);
  not not_30 (not_30_out, OP3);
  not not_31 (not_31_out, OP2);
  not not_32 (not_32_out, F13);
  not not_33 (not_33_out, F12);
  not not_34 (not_34_out, OP6);
  not not_35 (not_35_out, OP5);
  not not_36 (not_36_out, OP3);
  not not_37 (not_37_out, OP2);
  not not_38 (not_38_out, F30);
  not not_39 (not_39_out, F25);
  not not_40 (not_40_out, F14);
  not not_41 (not_41_out, F12);
  not not_42 (not_42_out, OP6);
  not not_43 (not_43_out, OP5);
  not not_44 (not_44_out, OP3);
  not not_45 (not_45_out, OP2);
  not not_46 (not_46_out, F25);
  not not_47 (not_47_out, F13);
  not not_48 (not_48_out, OP6);
  not not_49 (not_49_out, OP5);
  not not_50 (not_50_out, OP3);
  not not_51 (not_51_out, OP2);
  not not_52 (not_52_out, F14);
  not not_53 (not_53_out, F12);
  not not_54 (not_54_out, OP6);
  not not_55 (not_55_out, OP5);
  not not_56 (not_56_out, OP4);
  not not_57 (not_57_out, OP3);
  not not_58 (not_58_out, OP2);
  not not_59 (not_59_out, F14);
  not not_60 (not_60_out, F12);
  not not_61 (not_61_out, OP6);
  not not_62 (not_62_out, OP4);
  not not_63 (not_63_out, OP3);
  not not_64 (not_64_out, OP2);
  not not_65 (not_65_out, F14);
  not not_66 (not_66_out, F13);
  not not_67 (not_67_out, F12);
  not not_68 (not_68_out, OP4);
  not not_69 (not_69_out, OP3);
  not not_70 (not_70_out, F25);
  not not_71 (not_71_out, F13);
  not not_72 (not_72_out, OP6);
  not not_73 (not_73_out, OP3);
  not not_74 (not_74_out, OP2);
  not not_75 (not_75_out, F14);
  not not_76 (not_76_out, F13);
  not not_77 (not_77_out, F12);
  not not_78 (not_78_out, OP6);
  not not_79 (not_79_out, OP4);
  not not_80 (not_80_out, OP3);
  not not_81 (not_81_out, OP2);
  not not_82 (not_82_out, F13);
  not not_83 (not_83_out, F12);
  not not_84 (not_84_out, OP4);
  not not_85 (not_85_out, OP3);
  not not_86 (not_86_out, OP2);
  not not_87 (not_87_out, F25);
  not not_88 (not_88_out, F14);
  not not_89 (not_89_out, F13);
  not not_90 (not_90_out, F12);
  not not_91 (not_91_out, OP6);
  not not_92 (not_92_out, OP3);
  not not_93 (not_93_out, OP2);
  not not_94 (not_94_out, F30);
  not not_95 (not_95_out, F25);
  not not_96 (not_96_out, OP6);
  not not_97 (not_97_out, OP3);
  not not_98 (not_98_out, OP2);
  not not_99 (not_99_out, F30);
  not not_100 (not_100_out, F25);
  not not_101 (not_101_out, F14);
  not not_102 (not_102_out, F12);
  not not_103 (not_103_out, OP6);
  not not_104 (not_104_out, OP3);
  not not_105 (not_105_out, OP2);
  not not_106 (not_106_out, OP6);
  not not_107 (not_107_out, OP5);
  not not_108 (not_108_out, OP3);
  not not_109 (not_109_out, OP2);
  not not_110 (not_110_out, F30);
  not not_111 (not_111_out, F25);
  not not_112 (not_112_out, F14);
  not not_113 (not_113_out, F12);
  not not_114 (not_114_out, OP6);
  not not_115 (not_115_out, OP5);
  not not_116 (not_116_out, OP3);
  not not_117 (not_117_out, OP2);
  not not_118 (not_118_out, F30);
  not not_119 (not_119_out, F25);
  not not_120 (not_120_out, F13);
  not not_121 (not_121_out, OP6);
  not not_122 (not_122_out, OP5);
  not not_123 (not_123_out, OP3);
  not not_124 (not_124_out, OP2);
  not not_125 (not_125_out, F30);
  not not_126 (not_126_out, F25);
  not not_127 (not_127_out, F13);
  not not_128 (not_128_out, OP6);
  not not_129 (not_129_out, OP3);
  not not_130 (not_130_out, OP2);
  not not_131 (not_131_out, F13);
  not not_132 (not_132_out, F12);
  not not_133 (not_133_out, OP4);
  not not_134 (not_134_out, OP3);
  not not_135 (not_135_out, OP2);
  not not_136 (not_136_out, F30);
  not not_137 (not_137_out, F25);
  not not_138 (not_138_out, F14);
  not not_139 (not_139_out, F13);
  not not_140 (not_140_out, F12);
  not not_141 (not_141_out, OP6);
  not not_142 (not_142_out, OP3);
  not not_143 (not_143_out, OP2);
  not not_144 (not_144_out, F25);
  not not_145 (not_145_out, F14);
  not not_146 (not_146_out, F13);
  not not_147 (not_147_out, F12);
  not not_148 (not_148_out, OP6);
  not not_149 (not_149_out, OP3);
  not not_150 (not_150_out, OP2);
  not not_151 (not_151_out, F30);
  not not_152 (not_152_out, F25);
  not not_153 (not_153_out, OP6);
  not not_154 (not_154_out, OP3);
  not not_155 (not_155_out, OP2);
  not not_156 (not_156_out, F30);
  not not_157 (not_157_out, F25);
  not not_158 (not_158_out, F14);
  not not_159 (not_159_out, OP6);
  not not_160 (not_160_out, OP3);
  not not_161 (not_161_out, OP2);
  not not_162 (not_162_out, F14);
  not not_163 (not_163_out, F13);
  not not_164 (not_164_out, F12);
  not not_165 (not_165_out, OP6);
  not not_166 (not_166_out, OP5);
  not not_167 (not_167_out, OP3);
  not not_168 (not_168_out, OP2);
  not not_169 (not_169_out, OP6);
  not not_170 (not_170_out, OP5);
  not not_171 (not_171_out, OP3);
  not not_172 (not_172_out, OP2);
  not not_173 (not_173_out, F14);
  not not_174 (not_174_out, F12);
  not not_175 (not_175_out, OP6);
  not not_176 (not_176_out, OP5);
  not not_177 (not_177_out, OP4);
  not not_178 (not_178_out, OP3);
  not not_179 (not_179_out, OP2);
  not not_180 (not_180_out, F14);
  not not_181 (not_181_out, F12);
  not not_182 (not_182_out, OP6);
  not not_183 (not_183_out, OP4);
  not not_184 (not_184_out, OP3);
  not not_185 (not_185_out, OP2);
  not not_186 (not_186_out, F14);
  not not_187 (not_187_out, F13);
  not not_188 (not_188_out, F12);
  not not_189 (not_189_out, OP4);
  not not_190 (not_190_out, OP3);
  not not_191 (not_191_out, F14);
  not not_192 (not_192_out, F13);
  not not_193 (not_193_out, F12);
  not not_194 (not_194_out, OP6);
  not not_195 (not_195_out, OP4);
  not not_196 (not_196_out, OP3);
  not not_197 (not_197_out, OP2);
  not not_198 (not_198_out, F30);
  not not_199 (not_199_out, F25);
  not not_200 (not_200_out, F12);
  not not_201 (not_201_out, OP6);
  not not_202 (not_202_out, OP3);
  not not_203 (not_203_out, OP2);
  not not_204 (not_204_out, F30);
  not not_205 (not_205_out, F25);
  not not_206 (not_206_out, F14);
  not not_207 (not_207_out, F12);
  not not_208 (not_208_out, OP6);
  not not_209 (not_209_out, OP3);
  not not_210 (not_210_out, OP2);
  not not_211 (not_211_out, F30);
  not not_212 (not_212_out, F25);
  not not_213 (not_213_out, F14);
  not not_214 (not_214_out, OP6);
  not not_215 (not_215_out, OP3);
  not not_216 (not_216_out, OP2);
  not not_217 (not_217_out, F12);
  not not_218 (not_218_out, OP6);
  not not_219 (not_219_out, OP5);
  not not_220 (not_220_out, OP3);
  not not_221 (not_221_out, OP2);
  not not_222 (not_222_out, F13);
  not not_223 (not_223_out, F12);
  not not_224 (not_224_out, OP6);
  not not_225 (not_225_out, OP5);
  not not_226 (not_226_out, OP3);
  not not_227 (not_227_out, OP2);
  not not_228 (not_228_out, F30);
  not not_229 (not_229_out, F25);
  not not_230 (not_230_out, F14);
  not not_231 (not_231_out, F12);
  not not_232 (not_232_out, OP6);
  not not_233 (not_233_out, OP5);
  not not_234 (not_234_out, OP3);
  not not_235 (not_235_out, OP2);
  not not_236 (not_236_out, F13);
  not not_237 (not_237_out, F12);
  not not_238 (not_238_out, OP4);
  not not_239 (not_239_out, OP3);
  not not_240 (not_240_out, OP2);
  and and_1 (and_1_out, not_1_out, not_2_out, not_3_out, not_4_out, not_5_out, not_6_out, OP5, OP4, not_7_out, not_8_out);
  and and_2 (and_2_out, not_9_out, not_10_out, F14, F13, F12, not_11_out, OP5, OP4, not_12_out, not_13_out);
  and and_3 (and_3_out, not_14_out, not_15_out, not_16_out, F13, not_17_out, not_18_out, OP5, OP4, not_19_out, not_20_out);
  and and_4 (and_4_out, not_21_out, not_22_out, not_23_out, not_24_out, not_25_out, OP4, not_26_out, not_27_out);
  and and_5 (and_5_out, F14, F13, F12, not_28_out, not_29_out, OP4, not_30_out, not_31_out);
  and and_6 (and_6_out, F14, not_32_out, not_33_out, not_34_out, not_35_out, OP4, not_36_out, not_37_out);
  and and_7 (and_7_out, not_38_out, not_39_out, not_40_out, F13, not_41_out, not_42_out, not_43_out, OP4, not_44_out, not_45_out);
  and and_8 (and_8_out, F30, not_46_out, F14, not_47_out, F12, not_48_out, not_49_out, OP4, not_50_out, not_51_out);
  and and_9 (and_9_out, not_52_out, F13, not_53_out, not_54_out, not_55_out, not_56_out, not_57_out, not_58_out);
  and and_10 (and_10_out, not_59_out, F13, not_60_out, not_61_out, OP5, not_62_out, not_63_out, not_64_out);
  and and_11 (and_11_out, not_65_out, not_66_out, not_67_out, OP6, OP5, not_68_out, not_69_out, OP2);
  and and_12 (and_12_out, F30, not_70_out, F14, not_71_out, F12, not_72_out, OP5, OP4, not_73_out, not_74_out);
  and and_13 (and_13_out, not_75_out, not_76_out, not_77_out, not_78_out, OP5, not_79_out, not_80_out, not_81_out);
  and and_14 (and_14_out, F14, not_82_out, not_83_out, OP6, OP5, not_84_out, not_85_out, not_86_out);
  and and_15 (and_15_out, F30, not_87_out, not_88_out, not_89_out, not_90_out, not_91_out, OP5, OP4, not_92_out, not_93_out);
  and and_16 (and_16_out, not_94_out, not_95_out, F14, F13, F12, not_96_out, OP5, OP4, not_97_out, not_98_out);
  and and_17 (and_17_out, not_99_out, not_100_out, not_101_out, F13, not_102_out, not_103_out, OP5, OP4, not_104_out, not_105_out);
  and and_18 (and_18_out, F14, F13, F12, not_106_out, not_107_out, OP4, not_108_out, not_109_out);
  and and_19 (and_19_out, not_110_out, not_111_out, not_112_out, F13, not_113_out, not_114_out, not_115_out, OP4, not_116_out, not_117_out);
  and and_20 (and_20_out, not_118_out, not_119_out, F14, not_120_out, F12, not_121_out, not_122_out, OP4, not_123_out, not_124_out);
  and and_21 (and_21_out, not_125_out, not_126_out, F14, not_127_out, F12, not_128_out, OP5, OP4, not_129_out, not_130_out);
  and and_22 (and_22_out, F14, not_131_out, not_132_out, OP6, OP5, not_133_out, not_134_out, not_135_out);
  and and_23 (and_23_out, not_136_out, not_137_out, not_138_out, not_139_out, not_140_out, not_141_out, OP5, OP4, not_142_out, not_143_out);
  and and_24 (and_24_out, F30, not_144_out, not_145_out, not_146_out, not_147_out, not_148_out, OP5, OP4, not_149_out, not_150_out);
  and and_25 (and_25_out, not_151_out, not_152_out, F14, F13, F12, not_153_out, OP5, OP4, not_154_out, not_155_out);
  and and_26 (and_26_out, not_156_out, not_157_out, not_158_out, F13, F12, not_159_out, OP5, OP4, not_160_out, not_161_out);
  and and_27 (and_27_out, not_162_out, not_163_out, not_164_out, not_165_out, not_166_out, OP4, not_167_out, not_168_out);
  and and_28 (and_28_out, F14, F13, F12, not_169_out, not_170_out, OP4, not_171_out, not_172_out);
  and and_29 (and_29_out, not_173_out, F13, not_174_out, not_175_out, not_176_out, not_177_out, not_178_out, not_179_out);
  and and_30 (and_30_out, not_180_out, F13, not_181_out, not_182_out, OP5, not_183_out, not_184_out, not_185_out);
  and and_31 (and_31_out, not_186_out, not_187_out, not_188_out, OP6, OP5, not_189_out, not_190_out, OP2);
  and and_32 (and_32_out, not_191_out, not_192_out, not_193_out, not_194_out, OP5, not_195_out, not_196_out, not_197_out);
  and and_33 (and_33_out, not_198_out, not_199_out, F14, F13, not_200_out, not_201_out, OP5, OP4, not_202_out, not_203_out);
  and and_34 (and_34_out, not_204_out, not_205_out, not_206_out, F13, not_207_out, not_208_out, OP5, OP4, not_209_out, not_210_out);
  and and_35 (and_35_out, not_211_out, not_212_out, not_213_out, F13, F12, not_214_out, OP5, OP4, not_215_out, not_216_out);
  and and_36 (and_36_out, F14, F13, not_217_out, not_218_out, not_219_out, OP4, not_220_out, not_221_out);
  and and_37 (and_37_out, F14, not_222_out, not_223_out, not_224_out, not_225_out, OP4, not_226_out, not_227_out);
  and and_38 (and_38_out, not_228_out, not_229_out, not_230_out, F13, not_231_out, not_232_out, not_233_out, OP4, not_234_out, not_235_out);
  and and_39 (and_39_out, F14, not_236_out, not_237_out, OP6, OP5, not_238_out, not_239_out, not_240_out);
  or or_1 (S0, and_1_out, and_2_out, and_3_out, and_4_out, and_5_out, and_6_out, and_7_out, and_8_out, and_9_out, and_10_out, and_11_out, and_12_out, and_13_out, and_14_out);
  or or_2 (S1, and_15_out, and_16_out, and_17_out, and_18_out, and_19_out, and_20_out, and_21_out, and_22_out);
  or or_3 (S2, and_23_out, and_24_out, and_25_out, and_26_out, and_27_out, and_28_out, and_29_out, and_30_out, and_31_out, and_32_out);
  or or_4 (S3, and_33_out, and_34_out, and_35_out, and_36_out, and_37_out, and_38_out, and_39_out);
endmodule

// 控制信号生成
module \控制信号自动生成  (
  input  OP2,
  input  OP3,
  input  OP4,
  input  OP5,
  input  OP6,
  input  F12,
  input  F13,
  input  F14,
  input  F25,
  input  F30,
  output MemToReg,
  output MemWrite,
  output CSRRSI,
  output CSRRCI,
  output Sb,
  output ALU_SRC,
  output RegWrite,
  output Blt,
  output ecall,
  output S_Type,
  output BEQ,
  output BNE,
  output JALR,
  output JAL
);

  wire and_6_out, and_7_out, and_8_out, and_9_out, and_10_out, and_11_out, and_12_out, and_13_out,
       and_14_out, and_15_out, and_16_out, and_17_out, and_18_out, and_19_out, and_20_out, and_21_out,
       and_22_out, and_23_out, not_1_out, not_2_out, not_3_out, not_4_out, not_5_out, not_6_out, not_7_out,
       not_8_out, not_9_out, not_10_out, not_11_out, not_12_out, not_13_out, not_14_out, not_15_out,
       not_16_out, not_17_out, not_18_out, not_19_out, not_20_out, not_21_out, not_22_out, not_23_out,
       not_24_out, not_25_out, not_26_out, not_27_out, not_28_out, not_29_out, not_30_out, not_31_out,
       not_32_out, not_33_out, not_34_out, not_35_out, not_36_out, not_37_out, not_38_out, not_39_out,
       not_40_out, not_41_out, not_42_out, not_43_out, not_44_out, not_45_out, not_46_out, not_47_out,
       not_48_out, not_49_out, not_50_out, not_51_out, not_52_out, not_53_out, not_54_out, not_55_out,
       not_56_out, not_57_out, not_58_out, not_59_out, not_60_out, not_61_out, not_62_out, not_63_out,
       not_64_out, not_65_out, not_66_out, not_67_out, not_68_out, not_69_out, not_70_out, not_71_out,
       not_72_out, not_73_out, not_74_out, not_75_out, not_76_out, not_77_out, not_78_out, not_79_out,
       not_80_out, not_81_out, not_82_out, not_83_out, not_84_out, not_85_out, not_86_out, not_87_out,
       not_88_out, not_89_out, not_90_out, not_91_out, not_92_out, not_93_out, not_94_out, not_95_out,
       not_96_out, not_97_out, not_98_out, not_99_out, not_100_out, not_101_out, not_102_out, not_103_out,
       not_104_out, not_105_out, not_106_out, not_107_out, not_108_out, not_109_out, not_110_out,
       not_111_out, not_112_out, not_113_out, not_114_out, not_115_out, not_116_out, not_117_out,
       not_118_out, not_119_out, not_120_out, not_121_out, not_122_out, not_123_out, not_124_out,
       not_125_out, not_126_out, not_127_out, not_128_out, not_129_out, not_130_out, not_131_out,
       not_132_out, not_133_out, not_134_out, not_135_out, not_136_out, not_137_out, not_138_out,
       not_139_out, not_140_out, not_141_out, not_142_out, not_143_out, not_144_out, not_145_out,
       not_146_out, not_147_out, not_148_out, not_149_out, not_150_out, not_151_out, not_152_out,
       not_153_out, not_154_out, not_155_out, not_156_out, not_157_out, not_158_out, not_159_out;

  not not_1 (not_1_out, OP2);
  not not_2 (not_2_out, OP3);
  not not_3 (not_3_out, OP4);
  not not_4 (not_4_out, OP5);
  not not_5 (not_5_out, OP6);
  not not_6 (not_6_out, F12);
  not not_7 (not_7_out, F14);
  not not_8 (not_8_out, OP2);
  not not_9 (not_9_out, OP3);
  not not_10 (not_10_out, OP4);
  not not_11 (not_11_out, OP6);
  not not_12 (not_12_out, F12);
  not not_13 (not_13_out, F14);
  not not_14 (not_14_out, F12);
  not not_15 (not_15_out, OP3);
  not not_16 (not_16_out, OP2);
  not not_17 (not_17_out, OP3);
  not not_18 (not_18_out, OP2);
  not not_19 (not_19_out, OP2);
  not not_20 (not_20_out, OP3);
  not not_21 (not_21_out, OP4);
  not not_22 (not_22_out, OP6);
  not not_23 (not_23_out, F12);
  not not_24 (not_24_out, F13);
  not not_25 (not_25_out, F14);
  not not_26 (not_26_out, OP2);
  not not_27 (not_27_out, OP3);
  not not_28 (not_28_out, OP4);
  not not_29 (not_29_out, OP6);
  not not_30 (not_30_out, F12);
  not not_31 (not_31_out, F14);
  not not_32 (not_32_out, OP2);
  not not_33 (not_33_out, OP3);
  not not_34 (not_34_out, OP4);
  not not_35 (not_35_out, OP6);
  not not_36 (not_36_out, F12);
  not not_37 (not_37_out, F14);
  not not_38 (not_38_out, OP2);
  not not_39 (not_39_out, OP3);
  not not_40 (not_40_out, OP5);
  not not_41 (not_41_out, OP6);
  not not_42 (not_42_out, F12);
  not not_43 (not_43_out, F13);
  not not_44 (not_44_out, OP2);
  not not_45 (not_45_out, OP3);
  not not_46 (not_46_out, OP5);
  not not_47 (not_47_out, OP6);
  not not_48 (not_48_out, F12);
  not not_49 (not_49_out, F25);
  not not_50 (not_50_out, F30);
  not not_51 (not_51_out, OP2);
  not not_52 (not_52_out, OP3);
  not not_53 (not_53_out, OP5);
  not not_54 (not_54_out, OP6);
  not not_55 (not_55_out, F13);
  not not_56 (not_56_out, F25);
  not not_57 (not_57_out, F30);
  not not_58 (not_58_out, OP2);
  not not_59 (not_59_out, OP3);
  not not_60 (not_60_out, OP5);
  not not_61 (not_61_out, OP6);
  not not_62 (not_62_out, F25);
  not not_63 (not_63_out, OP2);
  not not_64 (not_64_out, OP3);
  not not_65 (not_65_out, OP5);
  not not_66 (not_66_out, OP6);
  not not_67 (not_67_out, OP3);
  not not_68 (not_68_out, OP4);
  not not_69 (not_69_out, F12);
  not not_70 (not_70_out, F13);
  not not_71 (not_71_out, F14);
  not not_72 (not_72_out, OP2);
  not not_73 (not_73_out, OP3);
  not not_74 (not_74_out, OP4);
  not not_75 (not_75_out, OP5);
  not not_76 (not_76_out, OP6);
  not not_77 (not_77_out, F12);
  not not_78 (not_78_out, F14);
  not not_79 (not_79_out, OP2);
  not not_80 (not_80_out, OP3);
  not not_81 (not_81_out, OP5);
  not not_82 (not_82_out, OP6);
  not not_83 (not_83_out, F12);
  not not_84 (not_84_out, F13);
  not not_85 (not_85_out, OP2);
  not not_86 (not_86_out, OP3);
  not not_87 (not_87_out, OP5);
  not not_88 (not_88_out, OP6);
  not not_89 (not_89_out, F13);
  not not_90 (not_90_out, F25);
  not not_91 (not_91_out, F30);
  not not_92 (not_92_out, OP2);
  not not_93 (not_93_out, OP3);
  not not_94 (not_94_out, OP6);
  not not_95 (not_95_out, F12);
  not not_96 (not_96_out, F13);
  not not_97 (not_97_out, F14);
  not not_98 (not_98_out, F25);
  not not_99 (not_99_out, OP2);
  not not_100 (not_100_out, OP3);
  not not_101 (not_101_out, OP6);
  not not_102 (not_102_out, F12);
  not not_103 (not_103_out, F14);
  not not_104 (not_104_out, F25);
  not not_105 (not_105_out, F30);
  not not_106 (not_106_out, OP2);
  not not_107 (not_107_out, OP3);
  not not_108 (not_108_out, OP5);
  not not_109 (not_109_out, OP6);
  not not_110 (not_110_out, OP2);
  not not_111 (not_111_out, OP3);
  not not_112 (not_112_out, OP6);
  not not_113 (not_113_out, F13);
  not not_114 (not_114_out, F25);
  not not_115 (not_115_out, OP2);
  not not_116 (not_116_out, OP3);
  not not_117 (not_117_out, OP6);
  not not_118 (not_118_out, F25);
  not not_119 (not_119_out, F30);
  not not_120 (not_120_out, OP4);
  not not_121 (not_121_out, F12);
  not not_122 (not_122_out, F13);
  not not_123 (not_123_out, F14);
  not not_124 (not_124_out, OP4);
  not not_125 (not_125_out, OP2);
  not not_126 (not_126_out, OP3);
  not not_127 (not_127_out, OP4);
  not not_128 (not_128_out, F12);
  not not_129 (not_129_out, F13);
  not not_130 (not_130_out, OP2);
  not not_131 (not_131_out, OP3);
  not not_132 (not_132_out, F12);
  not not_133 (not_133_out, F13);
  not not_134 (not_134_out, F14);
  not not_135 (not_135_out, F25);
  not not_136 (not_136_out, F30);
  not not_137 (not_137_out, OP2);
  not not_138 (not_138_out, OP3);
  not not_139 (not_139_out, OP4);
  not not_140 (not_140_out, OP6);
  not not_141 (not_141_out, F12);
  not not_142 (not_142_out, F14);
  not not_143 (not_143_out, OP2);
  not not_144 (not_144_out, OP3);
  not not_145 (not_145_out, OP4);
  not not_146 (not_146_out, F12);
  not not_147 (not_147_out, F13);
  not not_148 (not_148_out, F14);
  not not_149 (not_149_out, OP2);
  not not_150 (not_150_out, OP3);
  not not_151 (not_151_out, OP4);
  not not_152 (not_152_out, F13);
  not not_153 (not_153_out, F14);
  not not_154 (not_154_out, OP3);
  not not_155 (not_155_out, OP4);
  not not_156 (not_156_out, F12);
  not not_157 (not_157_out, F13);
  not not_158 (not_158_out, F14);
  not not_159 (not_159_out, OP4);
  and and_1 (MemToReg, not_1_out, not_2_out, not_3_out, not_4_out, not_5_out, not_6_out, F13, not_7_out);
  and and_2 (MemWrite, not_8_out, not_9_out, not_10_out, OP5, not_11_out, not_12_out, not_13_out);
  and and_3 (CSRRSI, F14, F13, not_14_out, OP6, OP5, OP4, not_15_out, not_16_out);
  and and_4 (CSRRCI, F14, F13, F12, OP6, OP5, OP4, not_17_out, not_18_out);
  and and_5 (Sb, not_19_out, not_20_out, not_21_out, OP5, not_22_out, not_23_out, not_24_out, not_25_out);
  and and_6 (and_6_out, not_26_out, not_27_out, not_28_out, not_29_out, not_30_out, F13, not_31_out);
  and and_7 (and_7_out, not_32_out, not_33_out, not_34_out, OP5, not_35_out, not_36_out, not_37_out);
  and and_8 (and_8_out, not_38_out, not_39_out, OP4, not_40_out, not_41_out, not_42_out, not_43_out);
  and and_9 (and_9_out, not_44_out, not_45_out, OP4, not_46_out, not_47_out, not_48_out, not_49_out, not_50_out);
  and and_10 (and_10_out, not_51_out, not_52_out, OP4, not_53_out, not_54_out, not_55_out, not_56_out, not_57_out);
  and and_11 (and_11_out, not_58_out, not_59_out, OP4, not_60_out, not_61_out, F14, not_62_out);
  and and_12 (and_12_out, not_63_out, not_64_out, OP4, not_65_out, not_66_out, F13, F14);
  and and_13 (and_13_out, OP2, not_67_out, not_68_out, OP5, OP6, not_69_out, not_70_out, not_71_out);
  and and_14 (and_14_out, not_72_out, not_73_out, not_74_out, not_75_out, not_76_out, not_77_out, F13, not_78_out);
  and and_15 (and_15_out, not_79_out, not_80_out, OP4, not_81_out, not_82_out, not_83_out, not_84_out);
  and and_16 (and_16_out, not_85_out, not_86_out, OP4, not_87_out, not_88_out, not_89_out, not_90_out, not_91_out);
  and and_17 (and_17_out, not_92_out, not_93_out, OP4, not_94_out, not_95_out, not_96_out, not_97_out, not_98_out);
  and and_18 (and_18_out, not_99_out, not_100_out, OP4, not_101_out, not_102_out, not_103_out, not_104_out, not_105_out);
  and and_19 (and_19_out, not_106_out, not_107_out, OP4, not_108_out, not_109_out, F13, F14);
  and and_20 (and_20_out, not_110_out, not_111_out, OP4, not_112_out, F12, not_113_out, F14, not_114_out);
  and and_21 (and_21_out, not_115_out, not_116_out, OP4, OP5, not_117_out, F13, not_118_out, not_119_out);
  and and_22 (and_22_out, OP2, not_120_out, OP5, OP6, not_121_out, not_122_out, not_123_out);
  and and_23 (and_23_out, OP2, OP3, not_124_out, OP5, OP6);
  and and_24 (Blt, not_125_out, not_126_out, not_127_out, OP5, OP6, not_128_out, not_129_out, F14);
  and and_25 (ecall, not_130_out, not_131_out, OP4, OP5, OP6, not_132_out, not_133_out, not_134_out, not_135_out, not_136_out);
  and and_26 (S_Type, not_137_out, not_138_out, not_139_out, OP5, not_140_out, not_141_out, not_142_out);
  and and_27 (BEQ, not_143_out, not_144_out, not_145_out, OP5, OP6, not_146_out, not_147_out, not_148_out);
  and and_28 (BNE, not_149_out, not_150_out, not_151_out, OP5, OP6, F12, not_152_out, not_153_out);
  and and_29 (JALR, OP2, not_154_out, not_155_out, OP5, OP6, not_156_out, not_157_out, not_158_out);
  and and_30 (JAL, OP2, OP3, not_159_out, OP5, OP6);
  or or_1 (ALU_SRC, and_6_out, and_7_out, and_8_out, and_9_out, and_10_out, and_11_out, and_12_out, and_13_out);
  or or_2 (RegWrite, and_14_out, and_15_out, and_16_out, and_17_out, and_18_out, and_19_out, and_20_out, and_21_out, and_22_out, and_23_out);
endmodule

// ALU
module ALU (
  input  [31:0] X,
  input  [31:0] Y,
  input  [3:0] AluOP,
  output out_4,
  output Equal,
  output out_6,
  output [31:0] Result,
  output [31:0] Result_2
);

  wire [0:0] comparator_1_lt, comparator_2_lt;
  wire [31:0] adder_1_out, AND_out, divider_1_out, divider_1_rem, multiplier_1_cout, multiplier_1_out,
       NOR_out, OR_out, shifter_1_out, shifter_2_out, shifter_3_out, subtractor_1_out, XOR_out;

  assign AND_out = X & Y;  // AND_Gate AND, 32 bits wide
  assign OR_out = X | Y;  // OR_Gate OR, 32 bits wide
  Shifter #(.width(32), .shift("ll")) shifter_1 (.in(X), .\dist (Y[4:0]), .out(shifter_1_out));
  Shifter #(.width(32), .shift("ar")) shifter_2 (.in(X), .\dist (Y[4:0]), .out(shifter_2_out));
  Shifter #(.width(32), .shift("lr")) shifter_3 (.in(X), .\dist (Y[4:0]), .out(shifter_3_out));
  Multiplier #(.width(32)) multiplier_1 (.a(X), .b(Y), .out(multiplier_1_out), .cout(multiplier_1_cout));  // open: cin
  Divider #(.width(32)) divider_1 (.a(X), .b(Y), .out(divider_1_out), .rem(divider_1_rem));  // open: upper
  Adder #(.width(32)) adder_1 (.a(X), .b(Y), .out(adder_1_out));  // open: cin, cout
  Subtractor #(.width(32)) subtractor_1 (.a(X), .b(Y), .out(subtractor_1_out));  // open: bin, bout
  assign XOR_out = X ^ Y;  // XOR_Gate XOR, 32 bits wide
  assign NOR_out = ~(X | Y);  // NOR_Gate NOR, 32 bits wide
  Comparator #(.width(32), .mode("twosComplement")) comparator_1 (
    .a(X), .b(Y), .eq(Equal), .lt(comparator_1_lt[0]));  // open: gt
  Comparator #(.width(32), .mode("unsigned")) comparator_2 (.a(X), .b(Y), .lt(comparator_2_lt[0]));  // open: gt, eq
  Multiplexer #(.select(4), .width(32), .disabled("Z"), .enable("false")) multiplexer_1 (
    .in0(shifter_1_out), .in1(shifter_2_out), .in2(shifter_3_out), .in3(multiplier_1_out),
    .in4(divider_1_out), .in5(adder_1_out), .in6(subtractor_1_out), .in7(AND_out), .in8(OR_out),
    .in9(XOR_out), .in10(NOR_out), .in11({{31{1'b0}}, comparator_1_lt[0]}),
    .in12({{31{1'b0}}, comparator_2_lt[0]}), .in13({32{1'b0}}), .in14({32{1'b0}}), .in15({32{1'b0}}),
    .out(Result), .sel(AluOP));
  Multiplexer #(.select(4), .width(32), .disabled("Z"), .enable("false")) multiplexer_2 (
    .in0({32{1'b0}}), .in1({32{1'b0}}), .in2({32{1'b0}}), .in3(multiplier_1_cout), .in4(divider_1_rem),
    .in5({32{1'b0}}), .in6({32{1'b0}}), .in7({32{1'b0}}), .in8({32{1'b0}}), .in9({32{1'b0}}),
    .in10({32{1'b0}}), .in11({32{1'b0}}), .in12({32{1'b0}}), .in13({32{1'b0}}), .in14({32{1'b0}}),
    .in15({32{1'b0}}), .out(Result_2), .sel(AluOP));
  Multiplexer #(.select(4), .width(1), .disabled("Z"), .enable("false")) multiplexer_3 (
    .in0(1'b0), .in1(1'b0), .in2(1'b0), .in3(1'b0), .in4(1'b0), .in5(1'b0), .in6(1'b0), .in7(1'b0),
    .in8(1'b0), .in9(1'b0), .in10(1'b0), .in11(comparator_1_lt[0]), .in12(comparator_2_lt[0]), .in13(1'b0),
    .in14(1'b0), .in15(1'b0), .out(out_6), .sel(AluOP));
  not not_1 (out_4, out_6);

  // Other names for the same wires on the sheet: Result2[31:0] = Result_2; S[3:0] = AluOP; tunnel = out_6;
  //   tunnel_t = out_4

  // Notes on the sheet:
  //   不要改变此引脚区域内容，也不要改变ALU封装形式
  //   输入引脚
  //   输出引脚
endmodule

module Regifile (
  input  [31:0] Din,
  input  Clk,
  input  WE,
  input  [4:0] R1_num,
  input  [4:0] W_num,
  input  [4:0] R2_num,
  output [31:0] R1,
  output [31:0] R2
);

  // RegisterFile registerfile_1: pin names not known; wires that end beside it: Din, Clk, WE, W_num, R1_num, R2_num, R1, R2
endmodule

module \理想流水线  (
  output RegWrite,
  output MemWrite,
  output [31:0] IF_PC,
  output [31:0] ID_PC,
  output [31:0] EX_PC,
  output [31:0] M_PC,
  output [31:0] WB_PC,
  output [31:0] RDin,
  output [31:0] MDin,
  output [31:0] LedData
);

  wire and_1_out, and_2_out, and_3_out, and_4_out, and_5_out, B, CLK, clock_1_out, comparator_1_eq,
       comparator_2_eq, comparator_3_eq, comparator_3_lt, d_ff_1_q, ecall, en, equal, ex_mem_1_haltout,
       ex_mem_1_jout, ex_mem_1_memtoregout, ex_mem_1_regwriteout, Go, halt, id_ex_1_p1, id_ex_1_p21,
       id_ex_1_p29, id_ex_1_p30, id_ex_1_p31, id_ex_1_p32, id_ex_1_p33, id_ex_1_p34, id_ex_1_p36,
       id_ex_1_p37, id_ex_1_p38, id_ex_1_p41, id_ex_1_p50, id_ex_1_p54, IR1, IR2, IR3, J, JAL, JALR, less,
       mem_wb_1_haltout, mem_wb_1_memtoregout, nand_1_out, not_1_out, not_2_out, not_3_out, not_4_out,
       not_5_out, or_2_out, riscv_probe_5_p2, riscv_probe_5_p5, riscv_probe_5_p6, RST, S_Type, W1, W2, W3,
       \单周期硬布线控制器_1_alu_src , \单周期硬布线控制器_1_beq , \单周期硬布线控制器_1_blt , \单周期硬布线控制器_1_bne , \单周期硬布线控制器_1_jal ,
       \单周期硬布线控制器_1_jalr , \单周期硬布线控制器_1_memtoreg , \单周期硬布线控制器_1_memwrite , \单周期硬布线控制器_1_regwrite ,
       \单周期硬布线控制器_1_sb ;
  wire [3:0] ByteSelect, ex_mem_1_byteselectout, id_ex_1_p35, multiplexer_7_out, \单周期硬布线控制器_1_alu_op ;
  wire [4:0] ex_mem_1_w_out, id_ex_1_p43, multiplexer_4_out, multiplexer_5_out, multiplexer_8_out, W_num;
  wire [11:0] id_ex_1_p45, id_ex_1_p46, multiplexer_6_out, shifter_1_out;
  wire [12:0] CNT_num;
  wire [15:0] \LoadUse次数 , \总周期数 , \插入气泡数 , \无条件分支数 , \条件分支成功数 ;
  wire [19:0] shifter_2_out;
  wire [31:0] adder_1_out, adder_4_out, bit_extender_1_out, bit_extender_2_out, bit_extender_3_out, BPC,
       EX_IR, ex_mem_1_rrsultout, id_ex_1_p39, id_ex_1_p48, id_ex_1_p52, ID_IR, IF_IR, JPC, MEM_IR,
       mem_wb_1_memdateout, mem_wb_1_resultout, mips_ram_1_p8, multiplexer_1_out, multiplexer_2_out,
       multiplexer_9_out, multiplexer_11_out, multiplexer_12_out, PCin, R1, R2, R2Sel, Result, shifter_3_out,
       WB_IR;

  Button \u_总复位  (.out(RST));
  Button _1 (.out(IR1));
  Button _2 (.out(IR2));
  Button _3 (.out(IR3));
  // Probe on \总周期数 
  // Probe on \总周期数 
  Button \u_继续运行  (.out(Go));
  LED #(.active("true")) led_1 (.in(W1));
  LED #(.active("true")) led_2 (.in(W2));
  LED #(.active("true")) led_3 (.in(W3));
  not not_1 (not_1_out, halt);
  Hex_Digit_Display hex_digit_display_1 (.value(LedData[31:28]));  // open: dp
  // Probe on IF_PC[19:0]
  // RiscV_Probe riscv_probe_1: pin names not known; wires that end beside it: IF_IR
  Register #(.width(32), .trigger("rising"), .Select("low")) PC (
    .D(PCin), .en(not_1_out), .Q(IF_PC), .clk(CLK));  // open: clr
  Hex_Digit_Display hex_digit_display_2 (.value(LedData[27:24]));  // open: dp
  Hex_Digit_Display hex_digit_display_3 (.value(LedData[23:20]));  // open: dp
  // Probe on ID_PC[19:0]
  // RiscV_Probe riscv_probe_2: pin names not known; wires that end beside it: ID_IR
  Adder #(.width(32)) adder_1 (.a(IF_PC), .b(32'h4), .out(adder_1_out));  // open: cin, cout
  Multiplexer #(.select(1), .width(32), .disabled("Z"), .enable("false")) multiplexer_1 (
    .in0(adder_1_out), .in1(BPC), .out(multiplexer_1_out), .sel(B));
  Hex_Digit_Display hex_digit_display_4 (.value(LedData[15:12]));  // open: dp
  Hex_Digit_Display hex_digit_display_5 (.value(LedData[19:16]));  // open: dp
  ROM #(.addrWidth(10), .dataWidth(32), .Select("high")) rom_1 (.addr(IF_PC[11:2]), .data(IF_IR));
  Multiplexer #(.select(1), .width(32), .disabled("Z"), .enable("false")) multiplexer_2 (
    .in0(multiplexer_1_out), .in1(JPC), .out(multiplexer_2_out), .sel(JAL));
  Hex_Digit_Display hex_digit_display_6 (.value(LedData[7:4]));  // open: dp
  Hex_Digit_Display hex_digit_display_7 (.value(LedData[11:8]));  // open: dp
  // Probe on EX_PC[19:0]
  // RiscV_Probe riscv_probe_3: pin names not known; wires that end beside it: EX_IR
  not not_2 (not_2_out, halt);
  Counter #(.width(16), .max('hffff), .ongoal("wrap"), .trigger("rising"), .behavior("new")) counter_1 (
    .count(not_2_out), .Q(\总周期数 ), .clk(CLK));  // open: load, D, carry, clr, preset, down
  Multiplexer #(.select(1), .width(32), .disabled("Z"), .enable("false")) multiplexer_3 (
    .in0(multiplexer_2_out), .in1(Result), .out(PCin), .sel(JALR));
  Hex_Digit_Display hex_digit_display_8 (.value(LedData[3:0]));  // open: dp
  IF_ID if_id_1 (
    .IRin(IF_IR), .PCin(IF_PC), .RST(RST), .EN(en), .CLK(CLK), .IRout(ID_IR), .PCout(ID_PC));  // open: PredictJumpin, PredictJumpout
  // Probe on \总周期数 
  // Probe on M_PC[19:0]
  // RiscV_Probe riscv_probe_4: pin names not known; wires that end beside it: MEM_IR
  // RiscV_Probe riscv_probe_5: pin names not known; wires that end beside it: ID_IR, riscv_probe_5_p2, riscv_probe_5_p2, {ID_IR[31:25], ID_IR[11:7]}, riscv_probe_5_p5, riscv_probe_5_p6, riscv_probe_5_p5
  // Probe on \总周期数 
  // Probe on \无条件分支数 
  // Probe on \条件分支成功数 
  // Probe on \插入气泡数 
  // Probe on \LoadUse次数 
  // Probe on IF_PC[11:0]
  // Probe on WB_PC[19:0]
  // RiscV_Probe riscv_probe_6: pin names not known; wires that end beside it: WB_IR
  Comparator #(.width(32), .mode("twosComplement")) comparator_1 (
    .a(R2), .b(32'h22), .eq(comparator_1_eq));  // open: gt, lt
  Comparator #(.width(32), .mode("twosComplement")) comparator_2 (
    .a(R2), .b(32'h22), .eq(comparator_2_eq));  // open: gt, lt
  // Probe on EX_PC[11:0]
  // Probe on ID_PC[11:0]
  \单周期硬布线控制器  \u_单周期硬布线控制器_1  (
    .Funct({ID_IR[30], ID_IR[25], ID_IR[14:12]}), .OP(ID_IR[6:2]), .ALU_OP(\单周期硬布线控制器_1_alu_op ),
    .MemToReg(\单周期硬布线控制器_1_memtoreg ), .MemWrite(\单周期硬布线控制器_1_memwrite ), .ALU_SRC(\单周期硬布线控制器_1_alu_src ),
    .RegWrite(\单周期硬布线控制器_1_regwrite ), .ecall(ecall), .S_type(S_Type), .Jalr(\单周期硬布线控制器_1_jalr ),
    .Beq(\单周期硬布线控制器_1_beq ), .JAL(\单周期硬布线控制器_1_jal ), .Bne(\单周期硬布线控制器_1_bne ), .in_3(ID_IR[21]),
    .uret(riscv_probe_5_p6), .Blt(\单周期硬布线控制器_1_blt ), .Sb(\单周期硬布线控制器_1_sb ));  // open: CSRRCI, CSRRSI
  Shifter #(.width(12), .shift("ll")) shifter_1 (
    .in({ID_IR[31], ID_IR[7], ID_IR[30:25], ID_IR[11:8]}), .\dist (4'b0001), .out(shifter_1_out));
  Shifter #(.width(20), .shift("ll")) shifter_2 (
    .in({ID_IR[31], ID_IR[19:12], ID_IR[20], ID_IR[30:21]}), .\dist (5'b00001), .out(shifter_2_out));
  and and_1 (and_1_out, ecall, not_3_out);
  not not_3 (not_3_out, comparator_1_eq);
  and and_2 (and_2_out, ecall, comparator_2_eq);
  // Probe on M_PC[11:0]
  D_Flip_Flop #(.trigger("high"), .Pre_Clr_Positions("LEGACY"), .NegatePresetClear("false"), .enable("true"), .NewFFLayout("false")) d_ff_1 (.Q(d_ff_1_q));  // open: clk, D, Qn, preset, en, reset
  // Probe on 13'hc
  Multiplexer #(.select(1), .width(5), .disabled("Z"), .enable("false")) multiplexer_4 (
    .in0(ID_IR[19:15]), .in1(5'b01010), .out(multiplexer_4_out), .sel(ecall));
  Multiplexer #(.select(1), .width(5), .disabled("Z"), .enable("false")) multiplexer_5 (
    .in0(ID_IR[24:20]), .in1(5'b10001), .out(multiplexer_5_out), .sel(ecall));
  assign bit_extender_1_out = {{20{shifter_1_out[11]}}, shifter_1_out};  // Bit_Extender bit_extender_1
  assign bit_extender_2_out = {{12{shifter_2_out[19]}}, shifter_2_out};  // Bit_Extender bit_extender_2
  Register #(.width(32), .trigger("rising"), .Select("low")) register_1 (
    .D(R1), .en(and_2_out), .Q(LedData), .clk(CLK));  // open: clr
  // Probe on WB_PC[11:0]
  Comparator #(.width(13), .mode("twosComplement")) comparator_3 (
    .a(CNT_num), .b(13'hc), .eq(comparator_3_eq), .lt(comparator_3_lt));  // open: gt
  Clock #(.highDuration(1), .lowDuration(1)) clock_1 (.out(clock_1_out));
  nand nand_1 (nand_1_out, d_ff_1_q, comparator_3_eq);
  Counter #(.width(13), .max('h1fff), .ongoal("stay"), .trigger("rising"), .behavior("old")) counter_2 (
    .count(comparator_3_lt), .Q(CNT_num), .clk(clock_1_out));  // open: load, D, carry, clr, preset
  Regifile regifile_1 (
    .Din(RDin), .Clk(CLK), .R1(R1), .R2(R2), .WE(RegWrite), .W_num(W_num), .R1_num(multiplexer_4_out),
    .R2_num(multiplexer_5_out));
  assign CLK = nand_1_out ? clock_1_out : 1'bz;  // Controlled_Buffer controlled_buffer_1
  Pull_Resistor #(.pull(1)) pull_resistor_1 (.node(CLK));
  // ID_EX id_ex_1: pin names not known; wires that end beside it: id_ex_1_p1, \单周期硬布线控制器_1_sb , \单周期硬布线控制器_1_beq , \单周期硬布线控制器_1_bne , \单周期硬布线控制器_1_blt , \单周期硬布线控制器_1_memtoreg , \单周期硬布线控制器_1_memwrite , \单周期硬布线控制器_1_alu_op , \单周期硬布线控制器_1_alu_src , \单周期硬布线控制器_1_regwrite , S_Type, R1, R2, ID_IR[11:7], ID_IR, ID_IR[31:20], {ID_IR[31:25], ID_IR[11:7]}, ID_PC, bit_extender_1_out, \单周期硬布线控制器_1_jal , id_ex_1_p21, id_ex_1_p21, bit_extender_2_out, \单周期硬布线控制器_1_jalr , and_1_out, CLK, en, RST, id_ex_1_p29, id_ex_1_p30, id_ex_1_p31, id_ex_1_p32, id_ex_1_p33, id_ex_1_p34, id_ex_1_p35, id_ex_1_p36, id_ex_1_p37, id_ex_1_p38, id_ex_1_p39, R2Sel, id_ex_1_p41, id_ex_1_p41, id_ex_1_p43, EX_IR, id_ex_1_p45, id_ex_1_p46, EX_PC, id_ex_1_p48, JAL, id_ex_1_p50, id_ex_1_p50, id_ex_1_p52, JALR, id_ex_1_p54
  Multiplexer #(.select(1), .width(12), .disabled("Z"), .enable("false")) multiplexer_6 (
    .in0(id_ex_1_p45), .in1(id_ex_1_p46), .out(multiplexer_6_out), .sel(id_ex_1_p38));
  assign bit_extender_3_out = {{20{multiplexer_6_out[11]}}, multiplexer_6_out};  // Bit_Extender bit_extender_3
  Multiplexer #(.select(2), .width(4), .disabled("Z"), .enable("false")) multiplexer_7 (
    .in0(4'b0001), .in1(4'b0010), .in2(4'b0100), .in3(4'b1000), .out(multiplexer_7_out), .sel(Result[1:0]));
  Multiplexer #(.select(2), .width(5), .disabled("Z"), .enable("false")) multiplexer_8 (
    .in0({5{1'b0}}), .in1(5'b01000), .in2(5'b10000), .in3(5'b11000), .out(multiplexer_8_out),
    .sel(Result[1:0]));
  and and_3 (and_3_out, id_ex_1_p30, equal);
  not not_4 (not_4_out, equal);
  and and_4 (and_4_out, not_4_out, id_ex_1_p31);
  and and_5 (and_5_out, less, id_ex_1_p32);
  Multiplexer #(.select(1), .width(32), .disabled("Z"), .enable("false")) multiplexer_9 (
    .in0(R2Sel), .in1(bit_extender_3_out), .out(multiplexer_9_out), .sel(id_ex_1_p36));
  Adder #(.width(32)) adder_2 (.a(EX_PC), .b(id_ex_1_p48), .out(BPC));  // open: cin, cout
  Adder #(.width(32)) adder_3 (.a(EX_PC), .b(id_ex_1_p52), .out(JPC));  // open: cin, cout
  Multiplexer #(.select(1), .width(4), .disabled("Z"), .enable("false")) multiplexer_10 (
    .in0(4'b1111), .in1(multiplexer_7_out), .out(ByteSelect), .sel(id_ex_1_p29));
  Shifter #(.width(32), .shift("ll")) shifter_3 (.in(R2Sel), .\dist (multiplexer_8_out), .out(shifter_3_out));
  or or_1 (B, and_3_out, and_4_out, and_5_out);
  ALU alu_1 (
    .X(id_ex_1_p39), .Y(multiplexer_9_out), .AluOP(id_ex_1_p35), .Equal(equal), .Result(Result), .out_6(less));  // open: Result_2, out_4
  Multiplexer #(.select(1), .width(32), .disabled("Z"), .enable("false")) multiplexer_11 (
    .in0(R2Sel), .in1(shifter_3_out), .out(multiplexer_11_out), .sel(id_ex_1_p29));
  // Probe on Result
  or or_2 (or_2_out, JAL, JALR);
  EX_MEM ex_mem_1 (
    .MemToRegin(id_ex_1_p33), .MemWritein(id_ex_1_p34), .Jin(or_2_out), .RegWritein(id_ex_1_p37),
    .ByteSelectin(ByteSelect), .MDin(multiplexer_11_out), .W_in(id_ex_1_p43), .PCin(EX_PC),
    .MemToRegout(ex_mem_1_memtoregout), .MemWriteout(MemWrite), .Jout(ex_mem_1_jout),
    .RegWriteout(ex_mem_1_regwriteout), .ByteSelectout(ex_mem_1_byteselectout), .MDout(MDin),
    .W_out(ex_mem_1_w_out), .PCout(M_PC), .RST(RST), .EN_H(en), .CLK(CLK), .Resultin(Result),
    .Rrsultout(ex_mem_1_rrsultout), .IRin(EX_IR), .IRout(MEM_IR), .Haltout(ex_mem_1_haltout),
    .Haltin(id_ex_1_p54));
  // Probe on ex_mem_1_rrsultout
  not not_5 (not_5_out, MemWrite);
  // MIPS_RAM mips_ram_1: pin names not known; wires that end beside it: ex_mem_1_rrsultout[11:2], MDin, MemWrite, ex_mem_1_byteselectout, CLK, not_5_out, MemWrite, mips_ram_1_p8
  MEM_WB mem_wb_1 (
    .MemToRegin(ex_mem_1_memtoregout), .Jin(ex_mem_1_jout), .RegWritein(ex_mem_1_regwriteout),
    .W_in(ex_mem_1_w_out), .IRin(MEM_IR), .PCin(M_PC), .MemToRegout(mem_wb_1_memtoregout), .Jout(J),
    .RegWriteout(RegWrite), .W_out(W_num), .IRout(WB_IR), .PCout(WB_PC), .RST(RST), .EN_H(en), .CLK(CLK),
    .Memdatein(mips_ram_1_p8), .Memdateout(mem_wb_1_memdateout), .Resultin(ex_mem_1_rrsultout),
    .Resultout(mem_wb_1_resultout), .Haltin(ex_mem_1_haltout), .Haltout(mem_wb_1_haltout));
  Multiplexer #(.select(1), .width(32), .disabled("Z"), .enable("false")) multiplexer_12 (
    .in0(mem_wb_1_resultout), .in1(mem_wb_1_memdateout), .out(multiplexer_12_out), .sel(mem_wb_1_memtoregout));
  Adder #(.width(32)) adder_4 (.a(32'h4), .b(WB_PC), .out(adder_4_out));  // open: cin, cout
  and and_6 (halt, mem_wb_1_haltout, ~Go);  // AND_Gate
  not not_6 (en, halt);
  Multiplexer #(.select(1), .width(32), .disabled("Z"), .enable("false")) multiplexer_13 (
    .in0(multiplexer_12_out), .in1(adder_4_out), .out(RDin), .sel(J));

  // Other names for the same wires on the sheet: IR[31:0] = ID_IR; MEM_PC[31:0] = M_PC

  // Notes on the sheet:
  //   中断源
  //   时空图监测，可删除
  //   中断等待指示
  //   指令存储器
  //   数码管输出
  //   contents of rom_1 (hex, n*v repeats v):
  //   413 493 913 993 46413 14e493 296913 39e993 842023 942223 1242423 1342623 a00893 493 913 993 73
  //   IR
  //   PC
  //   指令探针
  //   指令字
  //   JAL
  //   JALR
  //   URET
  //   func
  //   rs1
  //   rs2
  //   rd
  //   I型imm
  //   s型imm
  //   b型imm
  //   j型imm
  //   控制位
  //   Beq
  //   Bne
  //   Blt
  //   MemToReg
  //   MemWrite
  //   AluOP
  //   AluSrcB
  //   RegWrite
  //   S_Type
  //   流水调试日志用
  //   暂停节拍，不能为0
  //   戳工具置1进入计数暂停模式，ctrl+k时钟自动运行到对应节拍暂停
  //   ctrl+k关闭时钟连续运行，将控制位置零，进入单步调试模式调试
  //   用这个时钟源需要去掉电路中的其他时钟源
  //   可计数暂停的时钟源
  //   为方便自动评测，需要输出流水线各段保存的PC值，注意是PC不是PC+4，另外ID段寄存器写入信息，Mem段内存写入信息也要输出
  //   数据存储器
endmodule

module \气泡流水线  (
  output RegWrite,
  output MemWrite,
  output [31:0] IF_PC,
  output [31:0] ID_PC,
  output [31:0] EX_PC,
  output [31:0] M_PC,
  output [31:0] WB_PC,
  output [31:0] RDin,
  output [31:0] MDin,
  output [31:0] LedData
);

  wire and_1_out, and_2_out, and_3_out, and_4_out, and_5_out, and_6_out, and_7_out, and_8_out, B, CLK,
       clock_1_out, comparator_1_eq, comparator_2_eq, comparator_3_eq, comparator_3_lt, d_ff_1_q,
       DataHazzard, ecall, en, equal, ex_mem_1_haltout, ex_mem_1_jout, ex_mem_1_memtoregout, EX_RegWrite_num,
       Go, halt, id_ex_1_alusrcbout, id_ex_1_beqout, id_ex_1_bltout, id_ex_1_bneout, id_ex_1_haltout,
       id_ex_1_memtoregout, id_ex_1_memwriteout, id_ex_1_s_typeout, id_ex_1_sbout, IR1, IR2, IR3, J, JAL,
       JALR, less, MEM_RegWrite_num, mem_wb_1_haltout, mem_wb_1_memtoregout, nand_1_out, not_1_out,
       not_2_out, not_3_out, not_4_out, not_5_out, not_6_out, not_7_out, not_8_out, or_1_out, or_2_out,
       or_3_out, or_5_out, riscv_probe_5_p3, RST, S_Type, Sb, W1, W2, W3, \单周期硬布线控制器_1_alu_src ,
       \单周期硬布线控制器_1_beq , \单周期硬布线控制器_1_blt , \单周期硬布线控制器_1_bne , \单周期硬布线控制器_1_jal , \单周期硬布线控制器_1_jalr ,
       \单周期硬布线控制器_1_memtoreg , \单周期硬布线控制器_1_memwrite , \单周期硬布线控制器_1_regwrite ;
  wire [3:0] ByteSelect, ex_mem_1_byteselectout, id_ex_1_aluopout, multiplexer_7_out, \单周期硬布线控制器_1_alu_op ;
  wire [4:0] EX_W_num, ID_Funct, ID_R1_num, ID_R2_num, MEM_W_num, multiplexer_8_out, W_num;
  wire [11:0] id_ex_1_imm_i_out, id_ex_1_imm_s_out, multiplexer_6_out, shifter_1_out;
  wire [12:0] CNT_num;
  wire [15:0] adder_2_out, counter_5_q, \LoadUse次数 , shifter_3_out, \总周期数 , \插入气泡数 , \无条件分支数 , \条件分支成功数 ;
  wire [19:0] shifter_2_out;
  wire [31:0] adder_1_out, adder_6_out, bit_extender_1_out, bit_extender_2_out, bit_extender_3_out, BPC,
       EX_IR, ex_mem_1_rrsultout, id_ex_1_imm_b_out, id_ex_1_imm_j_out, id_ex_1_r1out, ID_IR, IF_IR, JPC,
       MEM_IR, mem_wb_1_memdateout, mem_wb_1_resultout, mips_ram_1_p8, multiplexer_1_out, multiplexer_2_out,
       multiplexer_9_out, multiplexer_11_out, multiplexer_12_out, PCin, R1, R2, R2Sel, Result, shifter_4_out,
       WB_IR;

  Button \u_总复位  (.out(RST));
  Button _1 (.out(IR1));
  Button _2 (.out(IR2));
  Button _3 (.out(IR3));
  // Probe on \总周期数 
  // Probe on \总周期数 
  Button \u_继续运行  (.out(Go));
  LED #(.active("true")) led_1 (.in(W1));
  LED #(.active("true")) led_2 (.in(W2));
  LED #(.active("true")) led_3 (.in(W3));
  not not_1 (not_1_out, DataHazzard);
  and and_1 (and_1_out, not_1_out, en);
  Hex_Digit_Display hex_digit_display_1 (.value(LedData[31:28]));  // open: dp
  // Probe on IF_PC[19:0]
  // RiscV_Probe riscv_probe_1: pin names not known; wires that end beside it: IF_IR
  not not_2 (not_2_out, halt);
  Counter #(.width(16), .max('hffff), .ongoal("wrap"), .trigger("rising"), .behavior("new")) counter_1 (
    .count(not_2_out), .Q(\总周期数 ), .clk(CLK));  // open: load, D, carry, clr, preset, down
  Register #(.width(32), .trigger("rising"), .Select("low")) PC (
    .D(PCin), .en(and_1_out), .Q(IF_PC), .clk(CLK));  // open: clr
  Hex_Digit_Display hex_digit_display_2 (.value(LedData[23:20]));  // open: dp
  Hex_Digit_Display hex_digit_display_3 (.value(LedData[27:24]));  // open: dp
  // Probe on ID_PC[19:0]
  // RiscV_Probe riscv_probe_2: pin names not known; wires that end beside it: {ID_IR[31], ID_Funct[4], ID_IR[29:26], ID_Funct[3], ID_IR[24:15], ID_Funct[2:0], ID_IR[11:0]}, ID_IR[6:2], ID_Funct, ID_R1_num
  Adder #(.width(32)) adder_1 (.a(IF_PC), .b(32'h4), .out(adder_1_out));  // open: cin, cout
  Hex_Digit_Display hex_digit_display_4 (.value(LedData[19:16]));  // open: dp
  Hex_Digit_Display hex_digit_display_5 (.value(LedData[15:12]));  // open: dp
  \数据相关检测逻辑  \u_数据相关检测逻辑_1  (
    .ID_R1_num(ID_R1_num), .EX_W_num(EX_W_num), .EX_RegWrite(EX_RegWrite_num), .ID_R2_num(ID_R2_num),
    .MEM_W_num(MEM_W_num), .MEM_RegWrite(MEM_RegWrite_num), .OP(ID_IR[6:2]), .Funct(ID_Funct),
    .DataHazzard(DataHazzard));
  Multiplexer #(.select(1), .width(32), .disabled("Z"), .enable("false")) multiplexer_1 (
    .in0(adder_1_out), .in1(BPC), .out(multiplexer_1_out), .sel(B));
  Multiplexer #(.select(1), .width(32), .disabled("Z"), .enable("false")) multiplexer_2 (
    .in0(multiplexer_1_out), .in1(JPC), .out(multiplexer_2_out), .sel(JAL));
  Hex_Digit_Display hex_digit_display_6 (.value(LedData[11:8]));  // open: dp
  Hex_Digit_Display hex_digit_display_7 (.value(LedData[7:4]));  // open: dp
  // Probe on EX_PC[19:0]
  // RiscV_Probe riscv_probe_3: pin names not known; wires that end beside it: EX_IR
  Counter #(.width(16), .max('hffff), .ongoal("wrap"), .trigger("rising"), .behavior("new")) counter_2 (
    .count(B), .Q(\条件分支成功数 ), .clk(CLK), .clr(RST));  // open: load, D, carry, preset, down
  ROM #(.addrWidth(10), .dataWidth(32), .Select("high")) rom_1 (.addr(IF_PC[11:2]), .data(IF_IR));
  Multiplexer #(.select(1), .width(32), .disabled("Z"), .enable("false")) multiplexer_3 (
    .in0(multiplexer_2_out), .in1(Result), .out(PCin), .sel(JALR));
  not not_3 (not_3_out, DataHazzard);
  and and_2 (and_2_out, not_3_out, en);
  Hex_Digit_Display hex_digit_display_8 (.value(LedData[3:0]));  // open: dp
  IF_ID if_id_1 (
    .IRin(IF_IR), .PCin(IF_PC), .RST(or_1_out), .EN(and_2_out), .CLK(CLK),
    .IRout({ID_IR[31], ID_Funct[4], ID_IR[29:26], ID_Funct[3], ID_IR[24:15], ID_Funct[2:0], ID_IR[11:0]}),
    .PCout(ID_PC));  // open: PredictJumpin, PredictJumpout
  or or_1 (or_1_out, JALR, JAL, B, RST);
  // Probe on \总周期数 
  // Probe on M_PC[19:0]
  // RiscV_Probe riscv_probe_4: pin names not known; wires that end beside it: MEM_IR
  or or_2 (or_2_out, JAL, JALR);
  // Probe on \总周期数 
  // Probe on \无条件分支数 
  // Probe on \条件分支成功数 
  // Probe on \插入气泡数 
  // Probe on \LoadUse次数 
  Counter #(.width(16), .max('hffff), .ongoal("wrap"), .trigger("rising"), .behavior("new")) counter_3 (
    .count(or_2_out), .Q(\无条件分支数 ), .clk(CLK), .clr(RST));  // open: load, D, carry, preset, down
  // RiscV_Probe riscv_probe_5: pin names not known; wires that end beside it: {ID_IR[31], ID_Funct[4], ID_IR[29:26], ID_Funct[3], ID_IR[24:15], ID_Funct[2:0], ID_IR[11:0]}, {ID_IR[31], ID_Funct[4], ID_IR[29:26], ID_Funct[3], ID_IR[11:7]}, riscv_probe_5_p3
  // Probe on IF_PC[11:0]
  // Probe on WB_PC[19:0]
  // RiscV_Probe riscv_probe_6: pin names not known; wires that end beside it: WB_IR
  // Probe on EX_PC[11:0]
  // Probe on ID_PC[11:0]
  \单周期硬布线控制器  \u_单周期硬布线控制器_1  (
    .Funct(ID_Funct), .OP(ID_IR[6:2]), .ALU_OP(\单周期硬布线控制器_1_alu_op ), .MemToReg(\单周期硬布线控制器_1_memtoreg ),
    .MemWrite(\单周期硬布线控制器_1_memwrite ), .ALU_SRC(\单周期硬布线控制器_1_alu_src ), .RegWrite(\单周期硬布线控制器_1_regwrite ),
    .ecall(ecall), .S_type(S_Type), .Jalr(\单周期硬布线控制器_1_jalr ), .Beq(\单周期硬布线控制器_1_beq ),
    .JAL(\单周期硬布线控制器_1_jal ), .Bne(\单周期硬布线控制器_1_bne ), .in_3(ID_IR[21]), .uret(riscv_probe_5_p3),
    .Blt(\单周期硬布线控制器_1_blt ), .Sb(Sb));  // open: CSRRCI, CSRRSI
  Shifter #(.width(12), .shift("ll")) shifter_1 (
    .in({ID_IR[31], ID_IR[7], ID_Funct[4], ID_IR[29:26], ID_Funct[3], ID_IR[11:8]}), .\dist (4'b0001),
    .out(shifter_1_out));
  Shifter #(.width(20), .shift("ll")) shifter_2 (
    .in({ID_IR[31], ID_IR[19:15], ID_Funct[2:0], ID_IR[20], ID_Funct[4], ID_IR[29:26], ID_Funct[3], ID_IR[24:21]}),
    .\dist (5'b00001), .out(shifter_2_out));
  Comparator #(.width(32), .mode("twosComplement")) comparator_1 (
    .a(R2), .b(32'h22), .eq(comparator_1_eq));  // open: gt, lt
  not not_4 (not_4_out, comparator_1_eq);
  Comparator #(.width(32), .mode("twosComplement")) comparator_2 (
    .a(R2), .b(32'h22), .eq(comparator_2_eq));  // open: gt, lt
  // Probe on M_PC[11:0]
  D_Flip_Flop #(.trigger("high"), .Pre_Clr_Positions("LEGACY"), .NegatePresetClear("false"), .enable("true"), .NewFFLayout("false")) d_ff_1 (.Q(d_ff_1_q));  // open: clk, D, Qn, preset, en, reset
  // Probe on 13'hc
  Multiplexer #(.select(1), .width(5), .disabled("Z"), .enable("false")) multiplexer_4 (
    .in0(ID_IR[19:15]), .in1(5'b01010), .out(ID_R1_num), .sel(ecall));
  assign bit_extender_1_out = {{20{shifter_1_out[11]}}, shifter_1_out};  // Bit_Extender bit_extender_1
  assign bit_extender_2_out = {{12{shifter_2_out[19]}}, shifter_2_out};  // Bit_Extender bit_extender_2
  and and_3 (and_3_out, ecall, not_4_out);
  and and_4 (and_4_out, ecall, comparator_2_eq);
  // Probe on WB_PC[11:0]
  Comparator #(.width(13), .mode("twosComplement")) comparator_3 (
    .a(CNT_num), .b(13'hc), .eq(comparator_3_eq), .lt(comparator_3_lt));  // open: gt
  Clock #(.highDuration(1), .lowDuration(1)) clock_1 (.out(clock_1_out));
  Adder #(.width(16)) adder_2 (.a(\条件分支成功数 ), .b(\无条件分支数 ), .out(adder_2_out));  // open: cin, cout
  Shifter #(.width(16), .shift("ll")) shifter_3 (.in(adder_2_out), .\dist (4'b0001), .out(shifter_3_out));
  not not_5 (not_5_out, halt);
  and and_5 (and_5_out, not_5_out, DataHazzard);
  Multiplexer #(.select(1), .width(5), .disabled("Z"), .enable("false")) multiplexer_5 (
    .in0(ID_IR[24:20]), .in1(5'b10001), .out(ID_R2_num), .sel(ecall));
  Register #(.width(32), .trigger("rising"), .Select("low")) register_1 (
    .D(R1), .en(and_4_out), .Q(LedData), .clk(CLK));  // open: clr
  nand nand_1 (nand_1_out, d_ff_1_q, comparator_3_eq);
  Counter #(.width(13), .max('h1fff), .ongoal("stay"), .trigger("rising"), .behavior("old")) counter_4 (
    .count(comparator_3_lt), .Q(CNT_num), .clk(clock_1_out));  // open: load, D, carry, clr, preset
  Adder #(.width(16)) adder_3 (.a(shifter_3_out), .b(counter_5_q), .out(\插入气泡数 ));  // open: cin, cout
  Counter #(.width(16), .max('hffff), .ongoal("wrap"), .trigger("rising"), .behavior("new")) counter_5 (
    .count(and_5_out), .Q(counter_5_q), .clk(CLK), .clr(RST));  // open: load, D, carry, preset, down
  not not_6 (not_6_out, CLK);
  Regifile regifile_1 (
    .Din(RDin), .Clk(not_6_out), .R1(R1), .R2(R2), .WE(RegWrite), .W_num(W_num), .R1_num(ID_R1_num),
    .R2_num(ID_R2_num));
  assign CLK = nand_1_out ? clock_1_out : 1'bz;  // Controlled_Buffer controlled_buffer_1
  Pull_Resistor #(.pull(1)) pull_resistor_1 (.node(CLK));
  ID_EX id_ex_1 (
    .MemToRegin(\单周期硬布线控制器_1_memtoreg ), .MemWritein(\单周期硬布线控制器_1_memwrite ),
    .AluSrcBin(\单周期硬布线控制器_1_alu_src ), .RegWritein(\单周期硬布线控制器_1_regwrite ), .S_typein(S_Type),
    .W_in(ID_IR[11:7]), .MemToRegout(id_ex_1_memtoregout), .MemWriteout(id_ex_1_memwriteout),
    .AluSrcBout(id_ex_1_alusrcbout), .RegWriteout(EX_RegWrite_num), .S_Typeout(id_ex_1_s_typeout),
    .W_out(EX_W_num), .CLK(CLK), .EN_H(en), .RST(or_3_out), .Sbin(Sb), .Sbout(id_ex_1_sbout),
    .AluOpin(\单周期硬布线控制器_1_alu_op ), .AluOpout(id_ex_1_aluopout), .Jalin(\单周期硬布线控制器_1_jal ), .Jalout(JAL),
    .Jalrin(\单周期硬布线控制器_1_jalr ), .Jalrout(JALR), .R1in(R1), .R1out(id_ex_1_r1out), .R2in(R2), .R2out(R2Sel),
    .Imm_I_in({ID_IR[31], ID_Funct[4], ID_IR[29:26], ID_Funct[3], ID_IR[24:20]}),
    .Imm_I_out(id_ex_1_imm_i_out),
    .Imm_S_in({ID_IR[31], ID_Funct[4], ID_IR[29:26], ID_Funct[3], ID_IR[11:7]}),
    .Imm_S_out(id_ex_1_imm_s_out), .Imm_B_in(bit_extender_1_out), .Imm_B_out(id_ex_1_imm_b_out),
    .Imm_J_in(bit_extender_2_out), .Imm_J_out(id_ex_1_imm_j_out), .PCin(ID_PC), .PCout(EX_PC),
    .Beqin(\单周期硬布线控制器_1_beq ), .Beqout(id_ex_1_beqout), .Bnein(\单周期硬布线控制器_1_bne ), .Bneout(id_ex_1_bneout),
    .Bltin(\单周期硬布线控制器_1_blt ), .Bltout(id_ex_1_bltout),
    .IRin({ID_IR[31], ID_Funct[4], ID_IR[29:26], ID_Funct[3], ID_IR[24:15], ID_Funct[2:0], ID_IR[11:0]}),
    .IRout(EX_IR), .Haltin(and_3_out), .Haltout(id_ex_1_haltout));  // open: R1Forwardin, R1Forwardout, R2Forwardout, R2Forwardin, PredictJumpin, PredictJumpout
  or or_3 (or_3_out, JALR, JAL, DataHazzard, B, RST);
  Multiplexer #(.select(1), .width(12), .disabled("Z"), .enable("false")) multiplexer_6 (
    .in0(id_ex_1_imm_i_out), .in1(id_ex_1_imm_s_out), .out(multiplexer_6_out), .sel(id_ex_1_s_typeout));
  Multiplexer #(.select(2), .width(4), .disabled("Z"), .enable("false")) multiplexer_7 (
    .in0(4'b0001), .in1(4'b0010), .in2(4'b0100), .in3(4'b1000), .out(multiplexer_7_out), .sel(Result[1:0]));
  Multiplexer #(.select(2), .width(5), .disabled("Z"), .enable("false")) multiplexer_8 (
    .in0({5{1'b0}}), .in1(5'b01000), .in2(5'b10000), .in3(5'b11000), .out(multiplexer_8_out),
    .sel(Result[1:0]));
  not not_7 (not_7_out, equal);
  Multiplexer #(.select(1), .width(32), .disabled("Z"), .enable("false")) multiplexer_9 (
    .in0(R2Sel), .in1(bit_extender_3_out), .out(multiplexer_9_out), .sel(id_ex_1_alusrcbout));
  assign bit_extender_3_out = {{20{multiplexer_6_out[11]}}, multiplexer_6_out};  // Bit_Extender bit_extender_3
  Multiplexer #(.select(1), .width(4), .disabled("Z"), .enable("false")) multiplexer_10 (
    .in0(4'b1111), .in1(multiplexer_7_out), .out(ByteSelect), .sel(id_ex_1_sbout));
  and and_6 (and_6_out, id_ex_1_beqout, equal);
  and and_7 (and_7_out, not_7_out, id_ex_1_bneout);
  and and_8 (and_8_out, less, id_ex_1_bltout);
  ALU alu_1 (
    .X(id_ex_1_r1out), .Y(multiplexer_9_out), .AluOP(id_ex_1_aluopout), .Equal(equal), .Result(Result),
    .out_6(less));  // open: Result_2, out_4
  Adder #(.width(32)) adder_4 (.a(EX_PC), .b(id_ex_1_imm_b_out), .out(BPC));  // open: cin, cout
  Adder #(.width(32)) adder_5 (.a(EX_PC), .b(id_ex_1_imm_j_out), .out(JPC));  // open: cin, cout
  Shifter #(.width(32), .shift("ll")) shifter_4 (.in(R2Sel), .\dist (multiplexer_8_out), .out(shifter_4_out));
  or or_4 (B, and_6_out, and_7_out, and_8_out);
  // Probe on Result
  Multiplexer #(.select(1), .width(32), .disabled("Z"), .enable("false")) multiplexer_11 (
    .in0(R2Sel), .in1(shifter_4_out), .out(multiplexer_11_out), .sel(id_ex_1_sbout));
  or or_5 (or_5_out, JAL, JALR);
  EX_MEM ex_mem_1 (
    .MemToRegin(id_ex_1_memtoregout), .MemWritein(id_ex_1_memwriteout), .Jin(or_5_out),
    .RegWritein(EX_RegWrite_num), .ByteSelectin(ByteSelect), .MDin(multiplexer_11_out), .W_in(EX_W_num),
    .PCin(EX_PC), .MemToRegout(ex_mem_1_memtoregout), .MemWriteout(MemWrite), .Jout(ex_mem_1_jout),
    .RegWriteout(MEM_RegWrite_num), .ByteSelectout(ex_mem_1_byteselectout), .MDout(MDin), .W_out(MEM_W_num),
    .PCout(M_PC), .RST(RST), .EN_H(en), .CLK(CLK), .Resultin(Result), .Rrsultout(ex_mem_1_rrsultout),
    .IRin(EX_IR), .IRout(MEM_IR), .Haltout(ex_mem_1_haltout), .Haltin(id_ex_1_haltout));
  // Probe on ex_mem_1_rrsultout
  not not_8 (not_8_out, MemWrite);
  // MIPS_RAM mips_ram_1: pin names not known; wires that end beside it: ex_mem_1_rrsultout[11:2], MDin, MemWrite, ex_mem_1_byteselectout, CLK, not_8_out, MemWrite, mips_ram_1_p8
  MEM_WB mem_wb_1 (
    .MemToRegin(ex_mem_1_memtoregout), .Jin(ex_mem_1_jout), .RegWritein(MEM_RegWrite_num), .W_in(MEM_W_num),
    .IRin(MEM_IR), .PCin(M_PC), .MemToRegout(mem_wb_1_memtoregout), .Jout(J), .RegWriteout(RegWrite),
    .W_out(W_num), .IRout(WB_IR), .PCout(WB_PC), .RST(RST), .EN_H(en), .CLK(CLK), .Memdatein(mips_ram_1_p8),
    .Memdateout(mem_wb_1_memdateout), .Resultin(ex_mem_1_rrsultout), .Resultout(mem_wb_1_resultout),
    .Haltin(ex_mem_1_haltout), .Haltout(mem_wb_1_haltout));
  Multiplexer #(.select(1), .width(32), .disabled("Z"), .enable("false")) multiplexer_12 (
    .in0(mem_wb_1_resultout), .in1(mem_wb_1_memdateout), .out(multiplexer_12_out), .sel(mem_wb_1_memtoregout));
  and and_9 (halt, mem_wb_1_haltout, ~Go);  // AND_Gate
  not not_9 (en, halt);
  Multiplexer #(.select(1), .width(32), .disabled("Z"), .enable("false")) multiplexer_13 (
    .in0(multiplexer_12_out), .in1(adder_6_out), .out(RDin), .sel(J));
  Adder #(.width(32)) adder_6 (.a(32'h4), .b(WB_PC), .out(adder_6_out));  // open: cin, cout

  // Other names for the same wires on the sheet: IR[31:0] = {ID_IR[31], ID_Funct[4], ID_IR[29:26], ID_Funct[3], ID_IR[24:15], ID_Funct[2:0], ID_IR[11:0]};
  //   ID_IR (some bits) = ID_Funct; ID_OP[4:0] = ID_IR[6:2]; MEM_PC[31:0] = M_PC

  // Notes on the sheet:
  //   中断源
  //   时空图监测，可删除
  //   中断等待指示
  //   数码管输出
  //   指令存储器
  //   IR
  //   contents of rom_1 (hex, n*v repeats v):
  //   100493 100006f 100493 200913 300993 100006f 100493 200913 300993 100006f 100493 200913 300993
  //   100006f 100493 200913 300993 3b8000ef 100413 100493 1f49493 900533 2200893 73 24d493 48463 fedff06f
  //   900533 2200893 73 100493 249493 900533 2200893 73 48463 fedff06f 100493 1f49493 900533 2200893 73
  //   4034d493 900533 2200893 73 4044d493 900533 2200893 73 4044d493 900533 2200893 73 4044d493 900533
  //   2200893 73 4044d493 900533 2200893 73 4044d493 900533 2200893 73 4044d493 900533 2200893 73 4044d493
  //   900533 2200893 73 100413 1f41993 41f9d993 433 c00913 300b13 140413 f47413 800293 100313 499993
  //   89e9b3 1300533 2200893 73 406282b3 fe0294e3 140413 f00f93 1f47433 1c41413 800293 100313 49d993
  //   89e9b3 1300533 2200893 73 406282b3 fe0294e3 1c45413 406b0b33 b0463 f95ff06f 2b3 fff2c293 829293
  //   ff2e293 500533 2200893 73 fff00413 493 84a023 140413 448493 84a023 140413 448493 84a023 140413
  //   448493 84a023 140413 448493 84a023 140413 448493 84a023 140413 448493 84a023 140413 448493 84a023
  //   140413 448493 84a023 140413 448493 84a023 140413 448493 84a023 140413 448493 84a023 140413 448493
  //   84a023 140413 448493 84a023 140413 448493 84a023 140413 448493 84a023 140413 448493 140413 433
  //   3c00493 42983 4aa03 149a2b3 28663 134a023 1442023 ffc48493 fe9412e3 800533 2200893 73 440413 3c00493
  //   fc9416e3 a00893 73 100293 300313 800493 849493 7648493 1449493 900533 2200893 73 800e13 54d4b3
  //   64d4b3 900533 2200893 73 fffe0e13 fe0e14e3 a00893 73 100293 300313 800493 849493 7648493 1449493
  //   900533 2200893 73 800e13 4054d4b3 4064d4b3 900533 2200893 73 fffe0e13 fe0e14e3 a00893 73 313 2000e13
  //   493 100913 930023 900533 2200893 73 12484b3 130313 fffe0e13 fe0e12e3 800e13 313 32483 900533 2200893
  //   73 430313 fffe0e13 fe0e14e3 a00893 73 ff100493 900533 2200893 73 148493 fe04c8e3 a00893 73 a00893 73
  //   413 140413 800533 2200893 73 240413 800533 2200893 73 340413 800533 2200893 73 440413 800533 2200893
  //   73 540413 800533 2200893 73 640413 800533 2200893 73 740413 800533 2200893 73 840413 800533 2200893
  //   2200893 73 8067
  //   PC
  //   指令探针
  //   JAL
  //   JALR
  //   URET
  //   func
  //   rs1
  //   rs2
  //   指令字
  //   rd
  //   I型imm
  //   s型imm
  //   b型imm
  //   j型imm
  //   控制位
  //   Beq
  //   Bne
  //   Blt
  //   AluOP
  //   AluSrcB
  //   RegWrite
  //   S_Type
  //   流水调试日志用
  //   暂停节拍，不能为0
  //   MemWrite
  //   可计数暂停的时钟源
  //   为方便自动评测，需要输出流水线各段保存的PC值，注意是PC不是PC+4，另外ID段寄存器写入信息，Mem段内存写入信息也要输出
  //   数据存储器
endmodule

module \重定向流水线  (
  output RegWrite,
  output MemWrite,
  output [31:0] IF_PC,
  output [31:0] ID_PC,
  output [31:0] EX_PC,
  output [31:0] M_PC,
  output [31:0] WB_PC,
  output [31:0] RDin,
  output [31:0] MDin,
  output [31:0] LedData
);

  wire AluSrcB, and_1_out, and_2_out, and_3_out, and_4_out, and_5_out, and_6_out, and_7_out, and_8_out, B,
       Beq, Blt, Bne, CLK, clock_1_out, comparator_1_eq, comparator_1_lt, comparator_2_eq, comparator_3_eq,
       d_ff_1_q, DataHazzard, ecall, en, equal, ex_mem_1_haltout, ex_mem_1_jout, ex_mem_1_memtoregout,
       EX_MemToReg, EX_RegWrite, Go, halt, id_ex_1_p1, id_ex_1_p2, id_ex_1_p26, id_ex_1_p33, id_ex_1_p34,
       id_ex_1_p35, id_ex_1_p36, id_ex_1_p37, id_ex_1_p39, id_ex_1_p41, id_ex_1_p43, id_ex_1_p48,
       id_ex_1_p57, id_ex_1_p61, IR1, IR2, IR3, J, JAL, JALR, less, Load_Use, MEM_RegWrite, mem_wb_1_haltout,
       mem_wb_1_memtoregout, MemToReg, mips_ram_1_p6, nand_1_out, not_1_out, not_2_out, not_3_out, not_4_out,
       not_5_out, not_6_out, not_7_out, or_1_out, or_2_out, or_5_out, riscv_probe_5_p3, RST, S_Type, Sb, W1,
       W2, W3, \单周期硬布线控制器_1_jal , \单周期硬布线控制器_1_jalr , \单周期硬布线控制器_1_memwrite , \单周期硬布线控制器_1_regwrite ;
  wire [1:0] id_ex_1_p44, id_ex_1_p45, R1Forward, R2Forward;
  wire [3:0] AluOP, ByteSelect, ex_mem_1_byteselectout, id_ex_1_p40, multiplexer_7_out;
  wire [4:0] EX_W_num, ID_Funct, ID_R1_num, ID_R2_num, MEM_W_num, multiplexer_8_out, W_num;
  wire [11:0] id_ex_1_p52, id_ex_1_p53, multiplexer_6_out, shifter_2_out;
  wire [12:0] CNT_num;
  wire [15:0] adder_1_out, \LoadUse次数 , shifter_1_out, \总周期数 , \插入气泡数 , \无条件分支数 , \条件分支成功数 ;
  wire [19:0] shifter_3_out;
  wire [31:0] adder_2_out, adder_6_out, bit_extender_1_out, bit_extender_2_out, bit_extender_3_out, BPC,
       EX_IR, EX_R1, EX_R2, EX_Result, id_ex_1_p46, id_ex_1_p47, id_ex_1_p55, id_ex_1_p59, ID_IR, IF_IR, JPC,
       MEM_F, MEM_IR, mem_wb_1_memdateout, mem_wb_1_resultout, mips_ram_1_p8, multiplexer_1_out,
       multiplexer_2_out, multiplexer_12_out, multiplexer_13_out, multiplexer_14_out, PCin, R1, R2,
       shifter_4_out, WB_IR;

  Button \u_总复位  (.out(RST));
  Button _1 (.out(IR1));
  Button _2 (.out(IR2));
  Button _3 (.out(IR3));
  // Probe on \总周期数 
  // Probe on \总周期数 
  Button \u_继续运行  (.out(Go));
  LED #(.active("true")) led_1 (.in(W1));
  LED #(.active("true")) led_2 (.in(W2));
  LED #(.active("true")) led_3 (.in(W3));
  not not_1 (not_1_out, halt);
  Counter #(.width(16), .max('hffff), .ongoal("wrap"), .trigger("rising"), .behavior("new")) counter_1 (
    .count(not_1_out), .Q(\总周期数 ), .clk(CLK));  // open: load, D, carry, clr, preset, down
  not not_2 (not_2_out, Load_Use);
  Hex_Digit_Display hex_digit_display_1 (.value(LedData[31:28]));  // open: dp
  // Probe on IF_PC[19:0]
  // RiscV_Probe riscv_probe_1: pin names not known; wires that end beside it: IF_IR
  Counter #(.width(16), .max('hffff), .ongoal("wrap"), .trigger("rising"), .behavior("new")) counter_2 (
    .count(B), .Q(\条件分支成功数 ), .clk(CLK), .clr(RST));  // open: load, D, carry, preset, down
  Adder #(.width(16)) adder_1 (.a(\条件分支成功数 ), .b(\无条件分支数 ), .out(adder_1_out));  // open: cin, cout
  not not_3 (not_3_out, halt);
  Register #(.width(32), .trigger("rising"), .Select("low")) PC (
    .D(PCin), .en(and_1_out), .Q(IF_PC), .clk(CLK));  // open: clr
  and and_1 (and_1_out, not_2_out, en);
  Hex_Digit_Display hex_digit_display_2 (.value(LedData[27:24]));  // open: dp
  Hex_Digit_Display hex_digit_display_3 (.value(LedData[23:20]));  // open: dp
  // Probe on ID_PC[19:0]
  // RiscV_Probe riscv_probe_2: pin names not known; wires that end beside it: {ID_IR[31], ID_Funct[4], ID_IR[29:26], ID_Funct[3], ID_IR[24:15], ID_Funct[2:0], ID_IR[11:0]}
  Shifter #(.width(16), .shift("ll")) shifter_1 (.in(adder_1_out), .\dist (4'b0001), .out(shifter_1_out));
  and and_2 (and_2_out, not_3_out, Load_Use);
  Counter #(.width(16), .max('hffff), .ongoal("wrap"), .trigger("rising"), .behavior("new")) counter_3 (
    .count(and_2_out), .Q(\LoadUse次数 ), .clk(CLK), .clr(RST));  // open: load, D, carry, preset, down
  Adder #(.width(32)) adder_2 (.a(IF_PC), .b(32'h4), .out(adder_2_out));  // open: cin, cout
  Hex_Digit_Display hex_digit_display_4 (.value(LedData[19:16]));  // open: dp
  Hex_Digit_Display hex_digit_display_5 (.value(LedData[15:12]));  // open: dp
  Adder #(.width(16)) adder_3 (.a(shifter_1_out), .b(\LoadUse次数 ), .out(\插入气泡数 ));  // open: cin, cout
  Multiplexer #(.select(1), .width(32), .disabled("Z"), .enable("false")) multiplexer_1 (
    .in0(adder_2_out), .in1(BPC), .out(multiplexer_1_out), .sel(B));
  Hex_Digit_Display hex_digit_display_6 (.value(LedData[7:4]));  // open: dp
  Hex_Digit_Display hex_digit_display_7 (.value(LedData[11:8]));  // open: dp
  // Probe on EX_PC[19:0]
  // RiscV_Probe riscv_probe_3: pin names not known; wires that end beside it: EX_IR
  or or_1 (or_1_out, JAL, JALR);
  Counter #(.width(16), .max('hffff), .ongoal("wrap"), .trigger("rising"), .behavior("new")) counter_4 (
    .count(or_1_out), .Q(\无条件分支数 ), .clk(CLK), .clr(RST));  // open: load, D, carry, preset, down
  ROM #(.addrWidth(10), .dataWidth(32), .Select("high")) rom_1 (.addr(IF_PC[11:2]), .data(IF_IR));
  Multiplexer #(.select(1), .width(32), .disabled("Z"), .enable("false")) multiplexer_2 (
    .in0(multiplexer_1_out), .in1(JPC), .out(multiplexer_2_out), .sel(JAL));
  Multiplexer #(.select(1), .width(32), .disabled("Z"), .enable("false")) multiplexer_3 (
    .in0(multiplexer_2_out), .in1(EX_Result), .out(PCin), .sel(JALR));
  not not_4 (not_4_out, Load_Use);
  and and_3 (and_3_out, not_4_out, en);
  Hex_Digit_Display hex_digit_display_8 (.value(LedData[3:0]));  // open: dp
  IF_ID if_id_1 (
    .IRin(IF_IR), .PCin(IF_PC), .RST(or_2_out), .EN(and_3_out), .CLK(CLK),
    .IRout({ID_IR[31], ID_Funct[4], ID_IR[29:26], ID_Funct[3], ID_IR[24:15], ID_Funct[2:0], ID_IR[11:0]}),
    .PCout(ID_PC));  // open: PredictJumpin, PredictJumpout
  or or_2 (or_2_out, JALR, JAL, B, RST);
  // Probe on \总周期数 
  // Probe on M_PC[19:0]
  // RiscV_Probe riscv_probe_4: pin names not known; wires that end beside it: MEM_IR
  // Probe on \总周期数 
  // Probe on \无条件分支数 
  // Probe on \条件分支成功数 
  // Probe on \插入气泡数 
  // Probe on \LoadUse次数 
  // RiscV_Probe riscv_probe_5: pin names not known; wires that end beside it: {ID_IR[31], ID_Funct[4], ID_IR[29:26], ID_Funct[3], ID_IR[24:15], ID_Funct[2:0], ID_IR[11:0]}, {ID_IR[31], ID_Funct[4], ID_IR[29:26], ID_Funct[3], ID_IR[11:7]}, riscv_probe_5_p3
  // Probe on IF_PC[11:0]
  // Probe on WB_PC[19:0]
  // RiscV_Probe riscv_probe_6: pin names not known; wires that end beside it: WB_IR
  // Probe on ID_PC[11:0]
  // Probe on EX_PC[11:0]
  \单周期硬布线控制器  \u_单周期硬布线控制器_1  (
    .Funct(ID_Funct), .OP(ID_IR[6:2]), .ALU_OP(AluOP), .MemToReg(MemToReg),
    .MemWrite(\单周期硬布线控制器_1_memwrite ), .ALU_SRC(AluSrcB), .RegWrite(\单周期硬布线控制器_1_regwrite ), .ecall(ecall),
    .S_type(S_Type), .Jalr(\单周期硬布线控制器_1_jalr ), .Beq(Beq), .JAL(\单周期硬布线控制器_1_jal ), .Bne(Bne),
    .in_3(ID_IR[21]), .uret(riscv_probe_5_p3), .Blt(Blt), .Sb(Sb));  // open: CSRRCI, CSRRSI
  // Probe on M_PC[11:0]
  D_Flip_Flop #(.trigger("high"), .Pre_Clr_Positions("LEGACY"), .NegatePresetClear("false"), .enable("true"), .NewFFLayout("false")) d_ff_1 (.Q(d_ff_1_q));  // open: clk, D, Qn, preset, en, reset
  // Probe on 13'hc
  Shifter #(.width(12), .shift("ll")) shifter_2 (
    .in({ID_IR[31], ID_IR[7], ID_Funct[4], ID_IR[29:26], ID_Funct[3], ID_IR[11:8]}), .\dist (4'b0001),
    .out(shifter_2_out));
  assign bit_extender_1_out = {{20{shifter_2_out[11]}}, shifter_2_out};  // Bit_Extender bit_extender_1
  assign bit_extender_2_out = {{12{shifter_3_out[19]}}, shifter_3_out};  // Bit_Extender bit_extender_2
  Shifter #(.width(20), .shift("ll")) shifter_3 (
    .in({ID_IR[31], ID_IR[19:15], ID_Funct[2:0], ID_IR[20], ID_Funct[4], ID_IR[29:26], ID_Funct[3], ID_IR[24:21]}),
    .\dist (5'b00001), .out(shifter_3_out));
  // Probe on WB_PC[11:0]
  Comparator #(.width(13), .mode("twosComplement")) comparator_1 (
    .a(CNT_num), .b(13'hc), .eq(comparator_1_eq), .lt(comparator_1_lt));  // open: gt
  Clock #(.highDuration(1), .lowDuration(1)) clock_1 (.out(clock_1_out));
  Multiplexer #(.select(1), .width(5), .disabled("Z"), .enable("false")) multiplexer_4 (
    .in0(ID_IR[19:15]), .in1(5'b01010), .out(ID_R1_num), .sel(ecall));
  Multiplexer #(.select(1), .width(5), .disabled("Z"), .enable("false")) multiplexer_5 (
    .in0(ID_IR[24:20]), .in1(5'b10001), .out(ID_R2_num), .sel(ecall));
  nand nand_1 (nand_1_out, d_ff_1_q, comparator_1_eq);
  Counter #(.width(13), .max('h1fff), .ongoal("stay"), .trigger("rising"), .behavior("old")) counter_5 (
    .count(comparator_1_lt), .Q(CNT_num), .clk(clock_1_out));  // open: load, D, carry, clr, preset
  \数据相关检测逻辑_重定向  \u_数据相关检测逻辑_重定向_1  (
    .ID_R1_num(ID_R1_num), .EX_W_num(EX_W_num), .EX_RegWrite(EX_RegWrite), .ID_R2_num(ID_R2_num),
    .MEM_W_num(MEM_W_num), .MEM_RegWrite(MEM_RegWrite), .EX_MemToReg(EX_MemToReg), .OP(ID_IR[6:2]),
    .Funct(ID_Funct), .R1Forward(R1Forward), .DataHazzard(DataHazzard), .R2Forward(R2Forward),
    .Load_Use(Load_Use));
  not not_5 (not_5_out, CLK);
  assign CLK = nand_1_out ? clock_1_out : 1'bz;  // Controlled_Buffer controlled_buffer_1
  Regifile regifile_1 (
    .Din(RDin), .Clk(not_5_out), .R1(R1), .R2(R2), .WE(RegWrite), .W_num(W_num), .R1_num(ID_R1_num),
    .R2_num(ID_R2_num));
  Pull_Resistor #(.pull(1)) pull_resistor_1 (.node(CLK));
  // ID_EX id_ex_1: pin names not known; wires that end beside it: id_ex_1_p1, id_ex_1_p2, Sb, id_ex_1_p1, Beq, id_ex_1_p2, Bne, Blt, MemToReg, \单周期硬布线控制器_1_memwrite , AluOP, AluSrcB, \单周期硬布线控制器_1_regwrite , S_Type, R1Forward, R2Forward, R1, R2, ID_IR[11:7], {ID_IR[31], ID_Funct[4], ID_IR[29:26], ID_Funct[3], ID_IR[24:15], ID_Funct[2:0], ID_IR[11:0]}, {ID_IR[31], ID_Funct[4], ID_IR[29:26], ID_Funct[3], ID_IR[24:20]}, {ID_IR[31], ID_Funct[4], ID_IR[29:26], ID_Funct[3], ID_IR[11:7]}, ID_PC, bit_extender_1_out, \单周期硬布线控制器_1_jal , id_ex_1_p26, id_ex_1_p26, bit_extender_2_out, \单周期硬布线控制器_1_jalr , ecall, CLK, en, id_ex_1_p33, id_ex_1_p34, id_ex_1_p35, id_ex_1_p36, id_ex_1_p37, EX_MemToReg, id_ex_1_p39, id_ex_1_p40, id_ex_1_p41, EX_RegWrite, id_ex_1_p43, id_ex_1_p44, id_ex_1_p45, id_ex_1_p46, id_ex_1_p47, id_ex_1_p48, id_ex_1_p48, EX_W_num, EX_IR, id_ex_1_p52, id_ex_1_p53, EX_PC, id_ex_1_p55, JAL, id_ex_1_p57, id_ex_1_p57, id_ex_1_p59, JALR, id_ex_1_p61
  Multiplexer #(.select(1), .width(12), .disabled("Z"), .enable("false")) multiplexer_6 (
    .in0(id_ex_1_p52), .in1(id_ex_1_p53), .out(multiplexer_6_out), .sel(id_ex_1_p43));
  or or_3 (id_ex_1_p33, JALR, JAL, Load_Use, B, RST);
  Multiplexer #(.select(2), .width(4), .disabled("Z"), .enable("false")) multiplexer_7 (
    .in0(4'b0001), .in1(4'b0010), .in2(4'b0100), .in3(4'b1000), .out(multiplexer_7_out), .sel(EX_Result[1:0]));
  Multiplexer #(.select(2), .width(5), .disabled("Z"), .enable("false")) multiplexer_8 (
    .in0({5{1'b0}}), .in1(5'b01000), .in2(5'b10000), .in3(5'b11000), .out(multiplexer_8_out),
    .sel(EX_Result[1:0]));
  not not_6 (not_6_out, equal);
  Multiplexer #(.select(2), .width(32), .disabled("Z"), .enable("false")) multiplexer_9 (
    .in0(id_ex_1_p47), .in1(RDin), .in2(MEM_F), .out(EX_R2), .sel(id_ex_1_p45));  // open: in3
  assign bit_extender_3_out = {{20{multiplexer_6_out[11]}}, multiplexer_6_out};  // Bit_Extender bit_extender_3
  Multiplexer #(.select(1), .width(4), .disabled("Z"), .enable("false")) multiplexer_10 (
    .in0(4'b1111), .in1(multiplexer_7_out), .out(ByteSelect), .sel(id_ex_1_p34));
  and and_4 (and_4_out, id_ex_1_p35, equal);
  and and_5 (and_5_out, not_6_out, id_ex_1_p36);
  and and_6 (and_6_out, less, id_ex_1_p37);
  Multiplexer #(.select(2), .width(32), .disabled("Z"), .enable("false")) multiplexer_11 (
    .in0(id_ex_1_p46), .in1(RDin), .in2(MEM_F), .out(EX_R1), .sel(id_ex_1_p44));  // open: in3
  Multiplexer #(.select(1), .width(32), .disabled("Z"), .enable("false")) multiplexer_12 (
    .in0(EX_R2), .in1(bit_extender_3_out), .out(multiplexer_12_out), .sel(id_ex_1_p41));
  Adder #(.width(32)) adder_4 (.a(EX_PC), .b(id_ex_1_p55), .out(BPC));  // open: cin, cout
  Adder #(.width(32)) adder_5 (.a(EX_PC), .b(id_ex_1_p59), .out(JPC));  // open: cin, cout
  not not_7 (not_7_out, comparator_2_eq);
  Comparator #(.width(32), .mode("twosComplement")) comparator_2 (
    .a(EX_R2), .b(32'h22), .eq(comparator_2_eq));  // open: gt, lt
  Comparator #(.width(32), .mode("twosComplement")) comparator_3 (
    .a(EX_R2), .b(32'h22), .eq(comparator_3_eq));  // open: gt, lt
  Shifter #(.width(32), .shift("ll")) shifter_4 (.in(EX_R2), .\dist (multiplexer_8_out), .out(shifter_4_out));
  or or_4 (B, and_4_out, and_5_out, and_6_out);
  ALU alu_1 (
    .X(EX_R1), .Y(multiplexer_12_out), .AluOP(id_ex_1_p40), .Equal(equal), .Result(EX_Result), .out_6(less));  // open: Result_2, out_4
  and and_7 (and_7_out, id_ex_1_p61, not_7_out);
  and and_8 (and_8_out, id_ex_1_p61, comparator_3_eq);
  Multiplexer #(.select(1), .width(32), .disabled("Z"), .enable("false")) multiplexer_13 (
    .in0(EX_R2), .in1(shifter_4_out), .out(multiplexer_13_out), .sel(id_ex_1_p34));
  or or_5 (or_5_out, JAL, JALR);
  Register #(.width(32), .trigger("rising"), .Select("low")) register_1 (
    .D(EX_R1), .en(and_8_out), .Q(LedData), .clk(CLK));  // open: clr
  EX_MEM ex_mem_1 (
    .MemToRegin(EX_MemToReg), .MemWritein(id_ex_1_p39), .Jin(or_5_out), .RegWritein(EX_RegWrite),
    .ByteSelectin(ByteSelect), .MDin(multiplexer_13_out), .W_in(EX_W_num), .PCin(EX_PC),
    .MemToRegout(ex_mem_1_memtoregout), .MemWriteout(MemWrite), .Jout(ex_mem_1_jout),
    .RegWriteout(MEM_RegWrite), .ByteSelectout(ex_mem_1_byteselectout), .MDout(MDin), .W_out(MEM_W_num),
    .PCout(M_PC), .RST(RST), .EN_H(en), .CLK(CLK), .Resultin(EX_Result), .Rrsultout(MEM_F), .IRin(EX_IR),
    .IRout(MEM_IR), .Haltout(ex_mem_1_haltout), .Haltin(and_7_out));
  // MIPS_RAM mips_ram_1: pin names not known; wires that end beside it: MEM_F[11:2], MDin, MemWrite, ex_mem_1_byteselectout, CLK, mips_ram_1_p6, MemWrite, mips_ram_1_p8
  not not_8 (mips_ram_1_p6, MemWrite);
  MEM_WB mem_wb_1 (
    .MemToRegin(ex_mem_1_memtoregout), .Jin(ex_mem_1_jout), .RegWritein(MEM_RegWrite), .W_in(MEM_W_num),
    .IRin(MEM_IR), .PCin(M_PC), .MemToRegout(mem_wb_1_memtoregout), .Jout(J), .RegWriteout(RegWrite),
    .W_out(W_num), .IRout(WB_IR), .PCout(WB_PC), .RST(RST), .EN_H(en), .CLK(CLK), .Memdatein(mips_ram_1_p8),
    .Memdateout(mem_wb_1_memdateout), .Resultin(MEM_F), .Resultout(mem_wb_1_resultout),
    .Haltin(ex_mem_1_haltout), .Haltout(mem_wb_1_haltout));
  and and_9 (halt, mem_wb_1_haltout, ~Go);  // AND_Gate
  not not_9 (en, halt);
  Multiplexer #(.select(1), .width(32), .disabled("Z"), .enable("false")) multiplexer_14 (
    .in0(mem_wb_1_resultout), .in1(mem_wb_1_memdateout), .out(multiplexer_14_out), .sel(mem_wb_1_memtoregout));
  Multiplexer #(.select(1), .width(32), .disabled("Z"), .enable("false")) multiplexer_15 (
    .in0(multiplexer_14_out), .in1(adder_6_out), .out(RDin), .sel(J));
  Adder #(.width(32)) adder_6 (.a(32'h4), .b(WB_PC), .out(adder_6_out));  // open: cin, cout

  // Other names for the same wires on the sheet: IR[31:0] = {ID_IR[31], ID_Funct[4], ID_IR[29:26], ID_Funct[3], ID_IR[24:15], ID_Funct[2:0], ID_IR[11:0]};
  //   ID_IR (some bits) = ID_Funct; ID_OP[4:0] = ID_IR[6:2]; MEM_PC[31:0] = M_PC; WB_F[31:0] = RDin

  // Notes on the sheet:
  //   中断源
  //   时空图监测，可删除
  //   中断等待指示
  //   数码管输出
  //   指令存储器
  //   contents of rom_1 (hex, n*v repeats v):
  //   100493 100006f 100493 200913 300993 100006f 100493 200913 300993 100006f 100493 200913 300993
  //   100006f 100493 200913 300993 3b8000ef 100413 100493 1f49493 900533 2200893 73 24d493 48463 fedff06f
  //   900533 2200893 73 100493 249493 900533 2200893 73 48463 fedff06f 100493 1f49493 900533 2200893 73
  //   4034d493 900533 2200893 73 4044d493 900533 2200893 73 4044d493 900533 2200893 73 4044d493 900533
  //   2200893 73 4044d493 900533 2200893 73 4044d493 900533 2200893 73 4044d493 900533 2200893 73 4044d493
  //   900533 2200893 73 100413 1f41993 41f9d993 433 c00913 300b13 140413 f47413 800293 100313 499993
  //   89e9b3 1300533 2200893 73 406282b3 fe0294e3 140413 f00f93 1f47433 1c41413 800293 100313 49d993
  //   89e9b3 1300533 2200893 73 406282b3 fe0294e3 1c45413 406b0b33 b0463 f95ff06f 2b3 fff2c293 829293
  //   ff2e293 500533 2200893 73 fff00413 493 84a023 140413 448493 84a023 140413 448493 84a023 140413
  //   448493 84a023 140413 448493 84a023 140413 448493 84a023 140413 448493 84a023 140413 448493 84a023
  //   140413 448493 84a023 140413 448493 84a023 140413 448493 84a023 140413 448493 84a023 140413 448493
  //   84a023 140413 448493 84a023 140413 448493 84a023 140413 448493 84a023 140413 448493 140413 433
  //   3c00493 42983 4aa03 149a2b3 28663 134a023 1442023 ffc48493 fe9412e3 800533 2200893 73 440413 3c00493
  //   fc9416e3 3200893 73 100293 300313 800493 849493 7648493 1449493 900533 2200893 73 800e13 54d4b3
  //   64d4b3 900533 2200893 73 fffe0e13 fe0e14e3 a00893 73 100293 300313 800493 849493 7648493 1449493
  //   900533 2200893 73 800e13 4054d4b3 4064d4b3 900533 2200893 73 fffe0e13 fe0e14e3 a00893 73 313 2000e13
  //   493 100913 930023 900533 2200893 73 12484b3 130313 fffe0e13 fe0e12e3 800e13 313 32483 900533 2200893
  //   73 430313 fffe0e13 fe0e14e3 a00893 73 ff100493 900533 2200893 73 148493 fe04c8e3 a00893 73 a00893 73
  //   413 140413 800533 2200893 73 240413 800533 2200893 73 340413 800533 2200893 73 440413 800533 2200893
  //   73 540413 800533 2200893 73 640413 800533 2200893 73 740413 800533 2200893 73 840413 800533 2200893
  //   2200893 73 8067
  //   IR
  //   PC
  //   指令探针
  //   func
  //   rs1
  //   rs2
  //   指令字
  //   rd
  //   b型imm
  //   j型imm
  //   控制位
  //   JAL
  //   JALR
  //   URET
  //   I型imm
  //   s型imm
  //   流水调试日志用
  //   暂停节拍，不能为0
  //   Beq
  //   Bne
  //   Blt
  //   MemWrite
  //   AluOP
  //   AluSrcB
  //   RegWrite
  //   S_Type
  //   戳工具置1进入计数暂停模式，ctrl+k时钟自动运行到对应节拍暂停
  //   ctrl+k关闭时钟连续运行，将控制位置零，进入单步调试模式调试
  //   可计数暂停的时钟源
  //   为方便自动评测，需要输出流水线各段保存的PC值，注意是PC不是PC+4，另外ID段寄存器写入信息，Mem段内存写入信息也要输出
  //   数据存储器
endmodule

module \中断按键参考电路  (
  input  \同步清零信号 ,
  output \与中断屏蔽位与 
);

  wire \_1号中断_out , and_1_out, clock_1_out, d_ff_1_q, or_1_out, or_2_out;

  Clock #(.highDuration(1), .lowDuration(1)) clock_1 (.out(clock_1_out));
  Button \_1号中断  (.out(\_1号中断_out ));
  or or_1 (or_1_out, \与中断屏蔽位与 , d_ff_1_q);
  LED #(.active("true")) \_1号中断等待指示灯  (.in(or_1_out));
  D_Flip_Flop #(.trigger("rising"), .Pre_Clr_Positions("LEGACY"), .NegatePresetClear("false"), .enable("true"), .NewFFLayout("false")) d_ff_1 (
    .clk(\_1号中断_out ), .D(1'b1), .Q(d_ff_1_q), .reset(\与中断屏蔽位与 ));  // open: Qn, preset, en
  or or_2 (or_2_out, d_ff_1_q, \与中断屏蔽位与 );
  and and_1 (and_1_out, or_2_out, ~\同步清零信号 );  // AND_Gate
  D_Flip_Flop #(.trigger("rising"), .Pre_Clr_Positions("LEGACY"), .NegatePresetClear("false"), .enable("true"), .NewFFLayout("false")) IR1 (
    .clk(clock_1_out), .D(and_1_out), .Q(\与中断屏蔽位与 ));  // open: Qn, preset, en, reset

  // Notes on the sheet:
  //   中断信号采样参考电路
  //   Reset 
endmodule
module \单周期_单级中断  (
  input  IR1,
  input  IR2,
  input  IR3,
  output RegWrite,
  output MemWrite,
  output [31:0] PC,
  output [31:0] IR,
  output [31:0] RDin,
  output [31:0] MDin,
  output [31:0] LedData
);

  wire AluSrcB, and_1_out, and_2_out, and_3_out, and_4_out, and_5_out, and_6_out, and_7_out, and_8_out, B,
       Beq, Blt, Bne, CLK, clock_1_out, comparator_1_eq, comparator_2_eq, comparator_3_eq, comparator_3_lt,
       d_ff_1_q, d_ff_2_q, d_ff_3_q, d_ff_4_q, decoder_1_out1, decoder_1_out2, decoder_1_out3, ecall, equal,
       Go, halt, IE, Int, Intq, IR1_q, IR1_t, IR2_q, IR2_t, IR3_q, IR3_t, IRA, IRB, IRC, J, JAL, JALR, less,
       MemToReg, nand_1_out, not_1_out, not_2_out, not_3_out, not_4_out, not_5_out, not_6_out, or_9_out,
       or_10_out, or_11_out, or_12_out, Ret1, Ret2, Ret3, S_Type, Sb, uret, W1, W2, W3;
  wire [1:0] priority_encoder_1_out, \中断号_q ;
  wire [3:0] AluOP, ByteSelect, multiplexer_12_out;
  wire [4:0] multiplexer_4_out, multiplexer_5_out, multiplexer_13_out;
  wire [11:0] multiplexer_7_out, shifter_1_out;
  wire [12:0] CNT_num;
  wire [15:0] \总周期数 ;
  wire [19:0] shifter_2_out;
  wire [31:0] adder_2_out, adder_3_out, bit_extender_1_out, bit_extender_2_out, bit_extender_3_out, EPC,
       InterAddr, mips_ram_1_p7, multiplexer_1_out, multiplexer_2_out, multiplexer_6_out, multiplexer_9_out,
       multiplexer_11_out, nextPC, PC_4, PCin, R1, R2, Result, shifter_3_out;

  Button \u_继续运行  (.out(Go));
  Button _1 (.out(IRA));
  Button _2 (.out(IRB));
  Button _3 (.out(IRC));
  LED #(.active("true")) led_1 (.in(W1));
  LED #(.active("true")) led_2 (.in(W2));
  LED #(.active("true")) led_3 (.in(W3));
  Comparator #(.width(32), .mode("twosComplement")) comparator_1 (
    .a(R2), .b(32'h22), .eq(comparator_1_eq));  // open: gt, lt
  Comparator #(.width(32), .mode("twosComplement")) comparator_2 (
    .a(R2), .b(32'h22), .eq(comparator_2_eq));  // open: gt, lt
  Hex_Digit_Display hex_digit_display_1 (.value(LedData[31:28]));  // open: dp
  and and_1 (and_1_out, ecall, not_1_out);
  not not_1 (not_1_out, comparator_2_eq);
  not not_2 (not_2_out, halt);
  Register #(.width(32), .trigger("rising"), .Select("low")) u_PC (
    .D(PCin), .en(not_3_out), .Q(PC), .clk(CLK));  // open: clr
  not not_3 (not_3_out, halt);
  Hex_Digit_Display hex_digit_display_2 (.value(LedData[27:24]));  // open: dp
  Hex_Digit_Display hex_digit_display_3 (.value(LedData[23:20]));  // open: dp
  and and_2 (and_2_out, ecall, comparator_1_eq);
  Register #(.width(1), .trigger("falling"), .Select("low")) register_1 (
    .D(and_1_out), .en(not_2_out), .Q(halt), .clk(CLK), .clr(Go));
  Shifter #(.width(12), .shift("ll")) shifter_1 (
    .in({IR[31], IR[7], IR[30:25], IR[11:8]}), .\dist (4'b0001), .out(shifter_1_out));
  Shifter #(.width(20), .shift("ll")) shifter_2 (
    .in({IR[31], IR[19:12], IR[20], IR[30:21]}), .\dist (5'b00001), .out(shifter_2_out));
  Hex_Digit_Display hex_digit_display_4 (.value(LedData[19:16]));  // open: dp
  Hex_Digit_Display hex_digit_display_5 (.value(LedData[15:12]));  // open: dp
  Register #(.width(32), .trigger("rising"), .Select("low")) register_2 (
    .D(R1), .en(and_2_out), .Q(LedData), .clk(CLK));  // open: clr
  and and_3 (and_3_out, Beq, equal);
  not not_4 (not_4_out, equal);
  and and_4 (and_4_out, not_4_out, Bne);
  and and_5 (and_5_out, less, Blt);
  Adder #(.width(32)) adder_1 (.a(PC), .b(32'h4), .out(PC_4));  // open: cin, cout
  assign bit_extender_1_out = {{20{shifter_1_out[11]}}, shifter_1_out};  // Bit_Extender bit_extender_1
  Adder #(.width(32)) adder_2 (.a(bit_extender_1_out), .b(PC), .out(adder_2_out));  // open: cin, cout
  assign bit_extender_2_out = {{12{shifter_2_out[19]}}, shifter_2_out};  // Bit_Extender bit_extender_2
  Adder #(.width(32)) adder_3 (.a(bit_extender_2_out), .b(PC), .out(adder_3_out));  // open: cin, cout
  Hex_Digit_Display hex_digit_display_6 (.value(LedData[11:8]));  // open: dp
  Hex_Digit_Display hex_digit_display_7 (.value(LedData[7:4]));  // open: dp
  // Probe on \总周期数 
  not not_5 (not_5_out, halt);
  Counter #(.width(16), .max('hffff), .ongoal("wrap"), .trigger("rising"), .behavior("new")) counter_1 (
    .count(not_5_out), .Q(\总周期数 ), .clk(CLK));  // open: load, D, carry, clr, preset, down
  // RiscV_Probe riscv_probe_1: pin names not known; wires that end beside it: IR, ecall, IR[24:20]
  ROM #(.addrWidth(10), .dataWidth(32), .Select("high")) rom_1 (.addr(PC[11:2]), .data(IR));
  or or_1 (B, and_3_out, and_4_out, and_5_out);
  Multiplexer #(.select(1), .width(32), .disabled("Z"), .enable("false")) multiplexer_1 (
    .in0(PC_4), .in1(adder_2_out), .out(multiplexer_1_out), .sel(B));
  Hex_Digit_Display hex_digit_display_8 (.value(LedData[3:0]));  // open: dp
  Multiplexer #(.select(1), .width(32), .disabled("Z"), .enable("false")) multiplexer_2 (
    .in0(multiplexer_1_out), .in1(adder_3_out), .out(multiplexer_2_out), .sel(JAL));
  Multiplexer #(.select(1), .width(32), .disabled("Z"), .enable("false")) multiplexer_3 (
    .in0(multiplexer_2_out), .in1(Result), .out(nextPC), .sel(JALR));
  or or_2 (IR1_t, IR1, IRA);
  \单周期硬布线控制器  \u_单周期硬布线控制器_1  (
    .Funct({IR[30], IR[25], IR[14:12]}), .OP(IR[6:2]), .ALU_OP(AluOP), .MemToReg(MemToReg),
    .MemWrite(MemWrite), .ALU_SRC(AluSrcB), .RegWrite(RegWrite), .ecall(ecall), .S_type(S_Type), .Jalr(JALR),
    .Beq(Beq), .JAL(JAL), .Bne(Bne), .in_3(IR[21]), .uret(uret), .Blt(Blt), .Sb(Sb));  // open: CSRRCI, CSRRSI
  Multiplexer #(.select(1), .width(5), .disabled("Z"), .enable("false")) multiplexer_4 (
    .in0(IR[19:15]), .in1(5'b01010), .out(multiplexer_4_out), .sel(ecall));
  Multiplexer #(.select(1), .width(5), .disabled("Z"), .enable("false")) multiplexer_5 (
    .in0(IR[24:20]), .in1(5'b10001), .out(multiplexer_5_out), .sel(ecall));
  Multiplexer #(.select(1), .width(32), .disabled("Z"), .enable("false")) multiplexer_6 (
    .in0(nextPC), .in1(InterAddr), .out(multiplexer_6_out), .sel(Int));
  or or_3 (IR2_t, IR2, IRB);
  Multiplexer #(.select(1), .width(12), .disabled("Z"), .enable("false")) multiplexer_7 (
    .in0(IR[31:20]), .in1({IR[31:25], IR[11:7]}), .out(multiplexer_7_out), .sel(S_Type));
  Multiplexer #(.select(1), .width(32), .disabled("Z"), .enable("false")) multiplexer_8 (
    .in0(multiplexer_6_out), .in1(EPC), .out(PCin), .sel(uret));
  Regifile regifile_1 (
    .Din(RDin), .Clk(CLK), .R1(R1), .R2(R2), .WE(RegWrite), .W_num(IR[11:7]), .R1_num(multiplexer_4_out),
    .R2_num(multiplexer_5_out));
  assign bit_extender_3_out = {{20{multiplexer_7_out[11]}}, multiplexer_7_out};  // Bit_Extender bit_extender_3
  or or_4 (IR3_t, IR3, IRC);
  Multiplexer #(.select(1), .width(32), .disabled("Z"), .enable("false")) multiplexer_9 (
    .in0(R2), .in1(bit_extender_3_out), .out(multiplexer_9_out), .sel(AluSrcB));
  Multiplexer #(.select(1), .width(32), .disabled("Z"), .enable("false")) multiplexer_10 (
    .in0(multiplexer_11_out), .in1(PC_4), .out(RDin), .sel(J));
  or or_5 (J, JAL, JALR);
  Multiplexer #(.select(1), .width(32), .disabled("Z"), .enable("false")) multiplexer_11 (
    .in0(Result), .in1(mips_ram_1_p7), .out(multiplexer_11_out), .sel(MemToReg));
  Multiplexer #(.select(2), .width(4), .disabled("Z"), .enable("false")) multiplexer_12 (
    .in0(4'b0001), .in1(4'b0010), .in2(4'b0100), .in3(4'b1000), .out(multiplexer_12_out), .sel(Result[1:0]));
  Multiplexer #(.select(2), .width(5), .disabled("Z"), .enable("false")) multiplexer_13 (
    .in0({5{1'b0}}), .in1(5'b01000), .in2(5'b10000), .in3(5'b11000), .out(multiplexer_13_out),
    .sel(Result[1:0]));
  ALU alu_1 (
    .X(R1), .Y(multiplexer_9_out), .AluOP(AluOP), .Equal(equal), .Result(Result), .out_6(less));  // open: Result_2, out_4
  or or_6 (W1, IR1_q, d_ff_1_q);
  or or_7 (W2, IR2_q, d_ff_2_q);
  or or_8 (W3, IR3_q, d_ff_3_q);
  Multiplexer #(.select(1), .width(4), .disabled("Z"), .enable("false")) multiplexer_14 (
    .in0(4'b1111), .in1(multiplexer_12_out), .out(ByteSelect), .sel(Sb));
  Multiplexer #(.select(1), .width(32), .disabled("Z"), .enable("false")) multiplexer_15 (
    .in0(R2), .in1(shifter_3_out), .out(MDin), .sel(Sb));
  Shifter #(.width(32), .shift("ll")) shifter_3 (.in(R2), .\dist (multiplexer_13_out), .out(shifter_3_out));
  D_Flip_Flop #(.trigger("rising"), .Pre_Clr_Positions("LEGACY"), .NegatePresetClear("false"), .enable("true"), .NewFFLayout("false")) d_ff_1 (
    .clk(IR1_t), .D(1'b1), .Q(d_ff_1_q), .reset(IR1_q));  // open: Qn, preset, en
  D_Flip_Flop #(.trigger("rising"), .Pre_Clr_Positions("LEGACY"), .NegatePresetClear("false"), .enable("true"), .NewFFLayout("false")) d_ff_2 (
    .clk(IR2_t), .D(1'b1), .Q(d_ff_2_q), .reset(IR2_q));  // open: Qn, preset, en
  D_Flip_Flop #(.trigger("rising"), .Pre_Clr_Positions("LEGACY"), .NegatePresetClear("false"), .enable("true"), .NewFFLayout("false")) d_ff_3 (
    .clk(IR3_t), .D(1'b1), .Q(d_ff_3_q), .reset(IR3_q));  // open: Qn, preset, en
  or or_9 (or_9_out, d_ff_1_q, IR1_q);
  or or_10 (or_10_out, d_ff_2_q, IR2_q);
  or or_11 (or_11_out, d_ff_3_q, IR3_q);
  and and_6 (and_6_out, or_9_out, ~Ret1);  // AND_Gate
  and and_7 (and_7_out, or_10_out, ~Ret2);  // AND_Gate
  and and_8 (and_8_out, or_11_out, ~Ret3);  // AND_Gate
  D_Flip_Flop #(.trigger("high"), .Pre_Clr_Positions("LEGACY"), .NegatePresetClear("false"), .enable("true"), .NewFFLayout("false")) d_ff_4 (.Q(d_ff_4_q));  // open: clk, D, Qn, preset, en, reset
  // Probe on 13'hc
  D_Flip_Flop #(.trigger("rising"), .Pre_Clr_Positions("LEGACY"), .NegatePresetClear("false"), .enable("true"), .NewFFLayout("false")) u_IR1 (
    .clk(CLK), .D(and_6_out), .Q(IR1_q));  // open: Qn, preset, en, reset
  D_Flip_Flop #(.trigger("rising"), .Pre_Clr_Positions("LEGACY"), .NegatePresetClear("false"), .enable("true"), .NewFFLayout("false")) u_IR2 (
    .clk(CLK), .D(and_7_out), .Q(IR2_q));  // open: Qn, preset, en, reset
  D_Flip_Flop #(.trigger("rising"), .Pre_Clr_Positions("LEGACY"), .NegatePresetClear("false"), .enable("true"), .NewFFLayout("false")) u_IR3 (
    .clk(CLK), .D(and_8_out), .Q(IR3_q));  // open: Qn, preset, en, reset
  Comparator #(.width(13), .mode("twosComplement")) comparator_3 (
    .a(CNT_num), .b(13'hc), .eq(comparator_3_eq), .lt(comparator_3_lt));  // open: gt
  Clock #(.highDuration(1), .lowDuration(1)) clock_1 (.out(clock_1_out));
  not not_6 (not_6_out, MemWrite);
  Counter #(.width(13), .max('h1fff), .ongoal("stay"), .trigger("rising"), .behavior("old")) counter_2 (
    .count(comparator_3_lt), .Q(CNT_num), .clk(clock_1_out));  // open: load, D, carry, clr, preset
  // MIPS_RAM mips_ram_1: pin names not known; wires that end beside it: Result[11:2], MDin, MemWrite, ByteSelect, CLK, not_6_out, mips_ram_1_p7
  nand nand_1 (nand_1_out, d_ff_4_q, comparator_3_eq);
  Priority_Encoder #(.select(2), .disabled("Z")) priority_encoder_1 (
    .in1(IR1_q), .in2(IR2_q), .in3(IR3_q), .out(priority_encoder_1_out), .gs(Intq));  // open: in0, en_out, en_in
  and and_9 (Int, IE, Intq);
  or or_12 (or_12_out, Int, uret);
  assign CLK = nand_1_out ? clock_1_out : 1'bz;  // Controlled_Buffer controlled_buffer_1
  Pull_Resistor #(.pull(1)) pull_resistor_1 (.node(CLK));
  D_Flip_Flop #(.trigger("rising"), .Pre_Clr_Positions("LEGACY"), .NegatePresetClear("false"), .enable("true"), .NewFFLayout("false")) u_IE (
    .clk(CLK), .D(Int), .Qn(IE), .en(or_12_out));  // open: Q, preset, reset
  Register #(.width(32), .trigger("rising"), .Select("low")) u_EPC (
    .D(nextPC), .en(Int), .Q(EPC), .clk(CLK));  // open: clr
  Multiplexer #(.select(2), .width(32), .disabled("Z"), .enable("false")) multiplexer_16 (
    .in1(32'h30ac), .in2(32'h3150), .in3(32'h31f4), .out(InterAddr), .sel(priority_encoder_1_out));  // open: in0
  Register #(.width(2), .trigger("rising"), .Select("low")) \u_中断号  (
    .D(priority_encoder_1_out), .en(Int), .Q(\中断号_q ), .clk(CLK));  // open: clr
  Decoder #(.select(2), .tristate("false"), .disabled("Z"), .enable("false")) decoder_1 (
    .out1(decoder_1_out1), .out2(decoder_1_out2), .out3(decoder_1_out3), .sel(\中断号_q ));  // open: out0
  and and_10 (Ret1, uret, decoder_1_out1);
  and and_11 (Ret2, decoder_1_out2, uret);
  and and_12 (Ret3, uret, decoder_1_out3);

  // Notes on the sheet:
  //   中断源
  //   中断等待指示
  //   总复位信号应将除ROM以外所有存储组件全部清零
  //   b型imm
  //   j型imm
  //   数码管输出
  //   指令存储器
  //   数码管输出应该用寄存器锁存，否则显示数据只能一闪而过
  //   指令探针
  //   contents of rom_1 (hex, n*v repeats v):
  //   7d000113 100413 1f41993 41f9d993 433 c00913 800b13 140413 f47413 800293 100313 499993 89e9b3 1300533
  //   2200893 73 406282b3 fe0294e3 140413 f00f93 1f47433 1c41413 800293 100313 49d993 89e9b3 1300533
  //   2200893 73 406282b3 fe0294e3 1c45413 406b0b33 b0463 f95ff06f 2b3 fff2c293 1029293 fff2e293 500533
  //   2200893 73 f5dff06f 1112023 410113 a12023 410113 812023 410113 1312023 410113 1412023 410113 1512023
  //   410113 1612023 410113 100b13 300a13 100a93 1600433 441413 14469b3 1300533 2200893 73 fe0416e3
  //   415a0a33 fe0a10e3 ffc10113 12b03 ffc10113 12a83 ffc10113 12a03 ffc10113 12983 ffc10113 12403
  //   ffc10113 12503 ffc10113 12883 200073 1112023 410113 a12023 410113 812023 410113 1312023 410113
  //   1412023 410113 1512023 410113 1612023 410113 200b13 300a13 100a93 1600433 441413 14469b3 1300533
  //   2200893 73 fe0416e3 415a0a33 fe0a10e3 ffc10113 12b03 ffc10113 12a83 ffc10113 12a03 ffc10113 12983
  //   ffc10113 12403 ffc10113 12503 ffc10113 12883 200073 1112023 410113 a12023 410113 812023 410113
  //   1312023 410113 1412023 410113 1512023 410113 1612023 410113 300b13 300a13 100a93 1600433 441413
  //   14469b3 1300533 2200893 73 fe0416e3 415a0a33 fe0a10e3 ffc10113 12b03 ffc10113 12a83 ffc10113 12a03
  //   ffc10113 12983 ffc10113 12403 ffc10113 12503 ffc10113 12883 200073
  //   指令字
  //   JAL
  //   JALR
  //   URET
  //   func
  //   rs1
  //   rs2
  //   rd
  //   I型imm
  //   s型imm
  //   Beq
  //   Bne
  //   MemToReg
  //   MemWrite
  //   AluOP
  //   AluSrcB
  //   RegWrite
  //   S_Type
  //   为方便自动评测，需要输出PC，IR，寄存器堆写如数据RDin
  //   RAM写使能MemWrite、RAM写入数据MDin等信号
  //   Reset 
  //   Reset 
  //   Reset 
  //   控制位
  //   暂停节拍，不能为0
  //   戳工具置1进入计数暂停模式，ctrl+k时钟自动运行到对应节拍暂停
  //   ctrl+k关闭时钟连续运行，将控制位置零，进入单步调试模式调试
  //   数据存储器
  //   可计数暂停的时钟源
endmodule

module \单周期_多级中断  (
  input  IR1,
  input  IR2,
  input  IR3,
  output RegWrite,
  output MemWrite,
  output [31:0] PC,
  output [31:0] IR,
  output [31:0] RDin,
  output [31:0] MDin,
  output [31:0] LedData
);

  wire AluSrcB, and_1_out, and_2_out, and_3_out, and_4_out, and_5_out, and_6_out, and_7_out, and_8_out, B,
       Beq, Blt, Bne, CLK, clock_1_out, comparator_1_eq, comparator_2_eq, comparator_3_eq, comparator_3_lt,
       csrrci, csrrsi, d_ff_1_q, d_ff_2_q, d_ff_3_q, d_ff_4_q, decoder_1_out1, decoder_1_out2,
       decoder_1_out3, demultiplexer_1_out0, demultiplexer_1_out1, demultiplexer_1_out2,
       demultiplexer_2_out0, demultiplexer_2_out1, demultiplexer_2_out2, ecall, equal, Go, halt, IE,
       Interrupt, IR1_q, IR1_t, IR2_q, IR2_t, IR3_q, IR3_t, IRA, IRB, IRC, J, JAL, JALR, less, MemToReg,
       mips_ram_1_p6, nand_1_out, not_1_out, not_2_out, not_3_out, not_4_out, not_5_out, or_9_out, or_10_out,
       or_11_out, or_12_out, or_13_out, or_14_out, priority_encoder_1_gs, Ret1, Ret2, Ret3, S_Type, Sb,
       shield, uret, W1, W2, W3;
  wire [1:0] Inter_Num, Inter_Num_Pri, IR1_2_q, IR2_2_q, IR3_2_q, stack;
  wire [3:0] AluOP, ByteSelect, multiplexer_11_out;
  wire [4:0] multiplexer_5_out, multiplexer_6_out, multiplexer_12_out;
  wire [11:0] multiplexer_7_out, shifter_1_out;
  wire [12:0] CNT_num;
  wire [15:0] \总周期数 ;
  wire [19:0] shifter_2_out;
  wire [31:0] adder_2_out, adder_3_out, bit_extender_1_out, bit_extender_2_out, bit_extender_3_out, EPC,
       EPC1_q, EPC2_q, EPC3_q, InterAddr, mips_ram_1_p7, multiplexer_1_out, multiplexer_2_out,
       multiplexer_4_out, multiplexer_10_out, multiplexer_13_out, nextPC, PC_4, PCin, R1, R2, Result,
       shifter_3_out;

  Button \u_继续运行  (.out(Go));
  Button _1 (.out(IRA));
  Button _2 (.out(IRB));
  Button _3 (.out(IRC));
  LED #(.active("true")) led_1 (.in(W1));
  LED #(.active("true")) led_2 (.in(W2));
  LED #(.active("true")) led_3 (.in(W3));
  Comparator #(.width(32), .mode("twosComplement")) comparator_1 (
    .a(R2), .b(32'h22), .eq(comparator_1_eq));  // open: gt, lt
  Comparator #(.width(32), .mode("twosComplement")) comparator_2 (
    .a(R2), .b(32'h22), .eq(comparator_2_eq));  // open: gt, lt
  Hex_Digit_Display hex_digit_display_1 (.value(LedData[31:28]));  // open: dp
  and and_1 (and_1_out, ecall, not_1_out);
  not not_1 (not_1_out, comparator_2_eq);
  not not_2 (not_2_out, halt);
  not not_3 (not_3_out, halt);
  Hex_Digit_Display hex_digit_display_2 (.value(LedData[27:24]));  // open: dp
  Hex_Digit_Display hex_digit_display_3 (.value(LedData[23:20]));  // open: dp
  and and_2 (and_2_out, ecall, comparator_1_eq);
  Register #(.width(1), .trigger("falling"), .Select("low")) register_1 (
    .D(and_1_out), .en(not_2_out), .Q(halt), .clk(CLK), .clr(Go));
  Register #(.width(32), .trigger("rising"), .Select("low")) u_PC (
    .D(PCin), .en(not_3_out), .Q(PC), .clk(CLK));  // open: clr
  Shifter #(.width(12), .shift("ll")) shifter_1 (
    .in({IR[31], IR[7], IR[30:25], IR[11:8]}), .\dist (4'b0001), .out(shifter_1_out));
  Shifter #(.width(20), .shift("ll")) shifter_2 (
    .in({IR[31], IR[19:12], IR[20], IR[30:21]}), .\dist (5'b00001), .out(shifter_2_out));
  Hex_Digit_Display hex_digit_display_4 (.value(LedData[15:12]));  // open: dp
  Hex_Digit_Display hex_digit_display_5 (.value(LedData[19:16]));  // open: dp
  Register #(.width(32), .trigger("rising"), .Select("low")) register_2 (
    .D(R1), .en(and_2_out), .Q(LedData), .clk(CLK));  // open: clr
  not not_4 (not_4_out, equal);
  assign bit_extender_1_out = {{20{shifter_1_out[11]}}, shifter_1_out};  // Bit_Extender bit_extender_1
  assign bit_extender_2_out = {{12{shifter_2_out[19]}}, shifter_2_out};  // Bit_Extender bit_extender_2
  Hex_Digit_Display hex_digit_display_6 (.value(LedData[7:4]));  // open: dp
  Hex_Digit_Display hex_digit_display_7 (.value(LedData[11:8]));  // open: dp
  // Probe on \总周期数 
  not not_5 (not_5_out, halt);
  Counter #(.width(16), .max('hffff), .ongoal("wrap"), .trigger("rising"), .behavior("new")) counter_1 (
    .count(not_5_out), .Q(\总周期数 ), .clk(CLK));  // open: load, D, carry, clr, preset, down
  ROM #(.addrWidth(10), .dataWidth(32), .Select("high")) rom_1 (.addr(PC[11:2]), .data(IR));
  and and_3 (and_3_out, Beq, equal);
  and and_4 (and_4_out, not_4_out, Bne);
  and and_5 (and_5_out, less, Blt);
  Adder #(.width(32)) adder_1 (.a(PC), .b(32'h4), .out(PC_4));  // open: cin, cout
  Adder #(.width(32)) adder_2 (.a(bit_extender_1_out), .b(PC), .out(adder_2_out));  // open: cin, cout
  Adder #(.width(32)) adder_3 (.a(bit_extender_2_out), .b(PC), .out(adder_3_out));  // open: cin, cout
  Hex_Digit_Display hex_digit_display_8 (.value(LedData[3:0]));  // open: dp
  // RiscV_Probe riscv_probe_1: pin names not known; wires that end beside it: IR, ecall, IR[24:20]
  or or_1 (B, and_3_out, and_4_out, and_5_out);
  Multiplexer #(.select(1), .width(32), .disabled("Z"), .enable("false")) multiplexer_1 (
    .in0(PC_4), .in1(adder_2_out), .out(multiplexer_1_out), .sel(B));
  Multiplexer #(.select(1), .width(32), .disabled("Z"), .enable("false")) multiplexer_2 (
    .in0(multiplexer_1_out), .in1(adder_3_out), .out(multiplexer_2_out), .sel(JAL));
  Multiplexer #(.select(1), .width(32), .disabled("Z"), .enable("false")) multiplexer_3 (
    .in0(multiplexer_2_out), .in1(Result), .out(nextPC), .sel(JALR));
  or or_2 (IR1_t, IR1, IRA);
  Multiplexer #(.select(1), .width(32), .disabled("Z"), .enable("false")) multiplexer_4 (
    .in0(nextPC), .in1(InterAddr), .out(multiplexer_4_out), .sel(Interrupt));
  or or_3 (IR2_t, IR2, IRB);
  \单周期硬布线控制器  \u_单周期硬布线控制器_1  (
    .Funct({IR[30], IR[25], IR[14:12]}), .OP(IR[6:2]), .ALU_OP(AluOP), .MemToReg(MemToReg),
    .MemWrite(MemWrite), .ALU_SRC(AluSrcB), .RegWrite(RegWrite), .ecall(ecall), .S_type(S_Type), .Jalr(JALR),
    .Beq(Beq), .JAL(JAL), .Bne(Bne), .in_3(IR[21]), .uret(uret), .Blt(Blt), .Sb(Sb), .CSRRCI(csrrci),
    .CSRRSI(csrrsi));
  Multiplexer #(.select(1), .width(5), .disabled("Z"), .enable("false")) multiplexer_5 (
    .in0(IR[19:15]), .in1(5'b01010), .out(multiplexer_5_out), .sel(ecall));
  Multiplexer #(.select(1), .width(5), .disabled("Z"), .enable("false")) multiplexer_6 (
    .in0(IR[24:20]), .in1(5'b10001), .out(multiplexer_6_out), .sel(ecall));
  Multiplexer #(.select(1), .width(12), .disabled("Z"), .enable("false")) multiplexer_7 (
    .in0(IR[31:20]), .in1({IR[31:25], IR[11:7]}), .out(multiplexer_7_out), .sel(S_Type));
  Multiplexer #(.select(1), .width(32), .disabled("Z"), .enable("false")) multiplexer_8 (
    .in0(multiplexer_4_out), .in1(EPC), .out(PCin), .sel(uret));
  or or_4 (IR3_t, IR3, IRC);
  Regifile regifile_1 (
    .Din(RDin), .Clk(CLK), .R1(R1), .R2(R2), .WE(RegWrite), .W_num(IR[11:7]), .R1_num(multiplexer_5_out),
    .R2_num(multiplexer_6_out));
  assign bit_extender_3_out = {{20{multiplexer_7_out[11]}}, multiplexer_7_out};  // Bit_Extender bit_extender_3
  Multiplexer #(.select(1), .width(32), .disabled("Z"), .enable("false")) multiplexer_9 (
    .in0(multiplexer_13_out), .in1(PC_4), .out(RDin), .sel(J));
  Multiplexer #(.select(1), .width(32), .disabled("Z"), .enable("false")) multiplexer_10 (
    .in0(R2), .in1(bit_extender_3_out), .out(multiplexer_10_out), .sel(AluSrcB));
  or or_5 (J, JAL, JALR);
  Multiplexer #(.select(2), .width(4), .disabled("Z"), .enable("false")) multiplexer_11 (
    .in0(4'b0001), .in1(4'b0010), .in2(4'b0100), .in3(4'b1000), .out(multiplexer_11_out), .sel(Result[1:0]));
  Multiplexer #(.select(2), .width(5), .disabled("Z"), .enable("false")) multiplexer_12 (
    .in0({5{1'b0}}), .in1(5'b01000), .in2(5'b10000), .in3(5'b11000), .out(multiplexer_12_out),
    .sel(Result[1:0]));
  Multiplexer #(.select(1), .width(32), .disabled("Z"), .enable("false")) multiplexer_13 (
    .in0(Result), .in1(mips_ram_1_p7), .out(multiplexer_13_out), .sel(MemToReg));
  Multiplexer #(.select(1), .width(4), .disabled("Z"), .enable("false")) multiplexer_14 (
    .in0(4'b1111), .in1(multiplexer_11_out), .out(ByteSelect), .sel(Sb));
  Shifter #(.width(32), .shift("ll")) shifter_3 (.in(R2), .\dist (multiplexer_12_out), .out(shifter_3_out));
  ALU alu_1 (
    .X(R1), .Y(multiplexer_10_out), .AluOP(AluOP), .Equal(equal), .Result(Result), .out_6(less));  // open: Result_2, out_4
  Multiplexer #(.select(1), .width(32), .disabled("Z"), .enable("false")) multiplexer_15 (
    .in0(R2), .in1(shifter_3_out), .out(MDin), .sel(Sb));
  D_Flip_Flop #(.trigger("rising"), .Pre_Clr_Positions("LEGACY"), .NegatePresetClear("false"), .enable("true"), .NewFFLayout("false")) d_ff_1 (
    .clk(IR1_t), .D(1'b1), .Q(d_ff_1_q), .reset(IR1_q));  // open: Qn, preset, en
  or or_6 (W1, IR1_q, d_ff_1_q);
  D_Flip_Flop #(.trigger("rising"), .Pre_Clr_Positions("LEGACY"), .NegatePresetClear("false"), .enable("true"), .NewFFLayout("false")) d_ff_2 (
    .clk(IR2_t), .D(1'b1), .Q(d_ff_2_q), .reset(IR2_q));  // open: Qn, preset, en
  or or_7 (W2, IR2_q, d_ff_2_q);
  D_Flip_Flop #(.trigger("rising"), .Pre_Clr_Positions("LEGACY"), .NegatePresetClear("false"), .enable("true"), .NewFFLayout("false")) d_ff_3 (
    .clk(IR3_t), .D(1'b1), .Q(d_ff_3_q), .reset(IR3_q));  // open: Qn, preset, en
  or or_8 (W3, IR3_q, d_ff_3_q);
  D_Flip_Flop #(.trigger("high"), .Pre_Clr_Positions("LEGACY"), .NegatePresetClear("false"), .enable("true"), .NewFFLayout("false")) d_ff_4 (.Q(d_ff_4_q));  // open: clk, D, Qn, preset, en, reset
  // Probe on 13'hc
  Comparator #(.width(13), .mode("twosComplement")) comparator_3 (
    .a(CNT_num), .b(13'hc), .eq(comparator_3_eq), .lt(comparator_3_lt));  // open: gt
  Clock #(.highDuration(1), .lowDuration(1)) clock_1 (.out(clock_1_out));
  or or_9 (or_9_out, d_ff_1_q, IR1_q);
  and and_6 (and_6_out, or_9_out, ~Ret1);  // AND_Gate
  or or_10 (or_10_out, d_ff_2_q, IR2_q);
  and and_7 (and_7_out, or_10_out, ~Ret2);  // AND_Gate
  or or_11 (or_11_out, d_ff_3_q, IR3_q);
  and and_8 (and_8_out, or_11_out, ~Ret3);  // AND_Gate
  Counter #(.width(13), .max('h1fff), .ongoal("stay"), .trigger("rising"), .behavior("old")) counter_2 (
    .count(comparator_3_lt), .Q(CNT_num), .clk(clock_1_out));  // open: load, D, carry, clr, preset
  // MIPS_RAM mips_ram_1: pin names not known; wires that end beside it: Result[11:2], MDin, MemWrite, ByteSelect, CLK, mips_ram_1_p6, mips_ram_1_p7
  not not_6 (mips_ram_1_p6, MemWrite);
  D_Flip_Flop #(.trigger("rising"), .Pre_Clr_Positions("LEGACY"), .NegatePresetClear("false"), .enable("true"), .NewFFLayout("false")) u_IR1 (
    .clk(CLK), .D(and_6_out), .Q(IR1_q));  // open: Qn, preset, en, reset
  D_Flip_Flop #(.trigger("rising"), .Pre_Clr_Positions("LEGACY"), .NegatePresetClear("false"), .enable("true"), .NewFFLayout("false")) u_IR2 (
    .clk(CLK), .D(and_7_out), .Q(IR2_q));  // open: Qn, preset, en, reset
  D_Flip_Flop #(.trigger("rising"), .Pre_Clr_Positions("LEGACY"), .NegatePresetClear("false"), .enable("true"), .NewFFLayout("false")) u_IR3 (
    .clk(CLK), .D(and_8_out), .Q(IR3_q));  // open: Qn, preset, en, reset
  nand nand_1 (nand_1_out, d_ff_4_q, comparator_3_eq);
  assign CLK = nand_1_out ? clock_1_out : 1'bz;  // Controlled_Buffer controlled_buffer_1
  Pull_Resistor #(.pull(1)) pull_resistor_1 (.node(CLK));
  Demultiplexer #(.select(2), .width(1), .tristate("false"), .disabled("Z"), .enable("false")) demultiplexer_1 (
    .out0(demultiplexer_1_out0), .out1(demultiplexer_1_out1), .out2(demultiplexer_1_out2), .in(Interrupt),
    .sel(stack));  // open: out3
  Priority_Encoder #(.select(2), .disabled("Z")) priority_encoder_1 (
    .in0(1'b0), .in1(IR1_q), .in2(IR2_q), .in3(IR3_q), .out(Inter_Num), .gs(priority_encoder_1_gs));  // open: en_out, en_in
  Register #(.width(32), .trigger("rising"), .Select("low")) EPC1 (
    .D(nextPC), .en(demultiplexer_1_out0), .Q(EPC1_q), .clk(CLK));  // open: clr
  Register #(.width(32), .trigger("rising"), .Select("low")) EPC2 (
    .D(nextPC), .en(demultiplexer_1_out1), .Q(EPC2_q), .clk(CLK));  // open: clr
  Register #(.width(32), .trigger("rising"), .Select("low")) EPC3 (
    .D(nextPC), .en(demultiplexer_1_out2), .Q(EPC3_q), .clk(CLK));  // open: clr
  and and_9 (Interrupt, priority_encoder_1_gs, shield, IE);
  or or_12 (or_12_out, Interrupt, csrrci);
  or or_13 (or_13_out, Interrupt, csrrci, csrrsi, uret);
  Comparator #(.width(2), .mode("unsigned")) comparator_4 (
    .a(Inter_Num_Pri), .b(Inter_Num), .lt(shield));  // open: gt, eq
  Pull_Resistor #(.pull(1)) pull_resistor_2 (.node(shield));
  D_Flip_Flop #(.trigger("rising"), .Pre_Clr_Positions("LEGACY"), .NegatePresetClear("false"), .enable("true"), .NewFFLayout("false")) d_ff_5 (
    .clk(CLK), .D(or_12_out), .Qn(IE), .en(or_13_out));  // open: Q, preset, reset
  Multiplexer #(.select(2), .width(32), .disabled("Z"), .enable("false")) multiplexer_16 (
    .in1(EPC1_q), .in2(EPC2_q), .in3(EPC3_q), .out(EPC), .sel(stack));  // open: in0
  or or_14 (or_14_out, uret, Interrupt);
  Counter #(.width(2), .max('h3), .ongoal("wrap"), .trigger("rising"), .behavior("new")) counter_3 (
    .count(or_14_out), .Q(stack), .clk(CLK), .down(uret));  // open: load, D, carry, clr, preset
  Multiplexer #(.select(2), .width(32), .disabled("Z"), .enable("false")) multiplexer_17 (
    .in1(32'h30ac), .in2(32'h3158), .in3(32'h3204), .out(InterAddr), .sel(Inter_Num));  // open: in0
  Demultiplexer #(.select(2), .width(1), .tristate("false"), .disabled("Z"), .enable("false")) demultiplexer_2 (
    .out0(demultiplexer_2_out0), .out1(demultiplexer_2_out1), .out2(demultiplexer_2_out2), .in(Interrupt),
    .sel(stack));  // open: out3
  Register #(.width(2), .trigger("rising"), .Select("low")) IR1_2 (
    .D(Inter_Num), .en(demultiplexer_2_out0), .Q(IR1_2_q), .clk(CLK));  // open: clr
  Register #(.width(2), .trigger("rising"), .Select("low")) IR2_2 (
    .D(Inter_Num), .en(demultiplexer_2_out1), .Q(IR2_2_q), .clk(CLK));  // open: clr
  Register #(.width(2), .trigger("rising"), .Select("low")) IR3_2 (
    .D(Inter_Num), .en(demultiplexer_2_out2), .Q(IR3_2_q), .clk(CLK));  // open: clr
  Multiplexer #(.select(2), .width(2), .disabled("Z"), .enable("false")) multiplexer_18 (
    .in1(IR1_2_q), .in2(IR2_2_q), .in3(IR3_2_q), .out(Inter_Num_Pri), .sel(stack));  // open: in0
  Decoder #(.select(2), .tristate("false"), .disabled("Z"), .enable("false")) decoder_1 (
    .out1(decoder_1_out1), .out2(decoder_1_out2), .out3(decoder_1_out3), .sel(Inter_Num_Pri));  // open: out0
  and and_10 (Ret1, uret, decoder_1_out1);
  and and_11 (Ret2, decoder_1_out2, uret);
  and and_12 (Ret3, decoder_1_out3, uret);

  // Notes on the sheet:
  //   中断源
  //   中断等待指示
  //   总复位信号应将除ROM以外所有存储组件全部清零
  //   b型imm
  //   j型imm
  //   数码管输出
  //   数码管输出应该用寄存器锁存，否则显示数据只能一闪而过
  //   指令存储器
  //   contents of rom_1 (hex, n*v repeats v):
  //   7d000113 100413 1f41993 41f9d993 433 c00913 800b13 140413 f47413 800293 100313 499993 89e9b3 1300533
  //   2200893 73 406282b3 fe0294e3 140413 f00f93 1f47433 1c41413 800293 100313 49d993 89e9b3 1300533
  //   2200893 73 406282b3 fe0294e3 1c45413 406b0b33 b0463 f95ff06f 2b3 fff2c293 1029293 fff2e293 500533
  //   2200893 73 f5dff06f 1112023 410113 a12023 410113 812023 410113 1312023 410113 1412023 410113 1512023
  //   410113 1612023 410113 40e073 100b13 300a13 100a93 1600433 441413 14469b3 1300533 2200893 73 fe0416e3
  //   415a0a33 fe0a10e3 40f073 ffc10113 12b03 ffc10113 12a83 ffc10113 12a03 ffc10113 12983 ffc10113 12403
  //   ffc10113 12503 ffc10113 12883 200073 1112023 410113 a12023 410113 812023 410113 1312023 410113
  //   1412023 410113 1512023 410113 1612023 410113 40e073 200b13 300a13 100a93 1600433 441413 14469b3
  //   1300533 2200893 73 fe0416e3 415a0a33 fe0a10e3 40f073 ffc10113 12b03 ffc10113 12a83 ffc10113 12a03
  //   ffc10113 12983 ffc10113 12403 ffc10113 12503 ffc10113 12883 200073 1112023 410113 a12023 410113
  //   812023 410113 1312023 410113 1412023 410113 1512023 410113 1612023 410113 40e073 300b13 300a13
  //   100a93 1600433 441413 14469b3 1300533 2200893 73 fe0416e3 415a0a33 fe0a10e3 40f073 ffc10113 12b03
  //   ffc10113 12a83 ffc10113 12a03 ffc10113 12983 ffc10113 12403 ffc10113 12503 ffc10113 12883 200073
  //   指令探针
  //   rs2
  //   指令字
  //   JAL
  //   JALR
  //   URET
  //   func
  //   rs1
  //   rd
  //   I型imm
  //   s型imm
  //   Beq
  //   Bne
  //   MemToReg
  //   MemWrite
  //   AluOP
  //   AluSrcB
  //   RegWrite
  //   S_Type
  //   为方便自动评测，需要输出PC，IR，寄存器堆写如数据RDin
  //   RAM写使能MemWrite、RAM写入数据MDin等信号
  //   控制位
  //   暂停节拍，不能为0
  //   戳工具置1进入计数暂停模式，ctrl+k时钟自动运行到对应节拍暂停
  //   ctrl+k关闭时钟连续运行，将控制位置零，进入单步调试模式调试
  //   Reset 
  //   Reset 
  //   Reset 
  //   可计数暂停的时钟源
endmodule

module \封装正确性测试  (
);

  wire IR1, IR2, IR3, MemW, RegW;
  wire [31:0] EX_PC, ID_PC, IF_PC, IR, LED, MDin, MDinr, MEM_PC, PC, RDin, RDinr, WB_PC;

  \单周期RISC_V  \u_单周期risc_v_1  (
    .IR1(IR1), .IR2(IR2), .IR3(IR3), .RegWrite(RegW), .MemWrite(MemW), .PC(PC), .IR(IR), .RDin(RDin),
    .MDin(MDin), .LedData(LED));
  \气泡流水线  \u_气泡流水线_1  (
    .RegWrite(RegW), .MemWrite(MemW), .IF_PC(IF_PC), .ID_PC(ID_PC), .EX_PC(EX_PC), .M_PC(MEM_PC),
    .WB_PC(WB_PC), .RDin(RDinr), .MDin(MDinr), .LedData(LED));
  \单周期_单级中断  \u_单周期_单级中断_1  (
    .IR1(IR1), .IR2(IR2), .IR3(IR3), .RegWrite(RegW), .MemWrite(MemW), .PC(PC), .IR(IR), .RDin(RDin),
    .MDin(MDin), .LedData(LED));
  \理想流水线  \u_理想流水线_1  (
    .RegWrite(RegW), .MemWrite(MemW), .IF_PC(IF_PC), .ID_PC(ID_PC), .EX_PC(EX_PC), .M_PC(MEM_PC),
    .WB_PC(WB_PC), .RDin(RDinr), .MDin(MDinr), .LedData(LED));
  \重定向流水线  \u_重定向流水线_1  (
    .RegWrite(RegW), .MemWrite(MemW), .IF_PC(IF_PC), .ID_PC(ID_PC), .EX_PC(EX_PC), .M_PC(MEM_PC),
    .WB_PC(WB_PC), .RDin(RDinr), .MDin(MDinr), .LedData(LED));
  \单周期_多级中断  \u_单周期_多级中断_1  (
    .IR1(IR1), .IR2(IR2), .IR3(IR3), .RegWrite(RegW), .MemWrite(MemW), .PC(PC), .IR(IR), .RDin(RDin),
    .MDin(MDin), .LedData(LED));

  // Notes on the sheet:
  //   单周期封装测试
  //   气泡流水封装测试
  //   单周期+单级中断封装测试
  //   请检查上面封装有无位宽不匹配，引脚标签是否和连接的标签相对应，否则无法在educoder平台上正确测试
  //   理想流水封装测试
  //   重定向流水封装测试
  //   单周期+多级中断封装测试
endmodule

module IF_ID (
  input  PredictJumpin,
  input  [31:0] IRin,
  input  [31:0] PCin,
  input  RST,
  input  EN,
  input  CLK,
  output PredictJumpout,
  output [31:0] IRout,
  output [31:0] PCout
);

  wire multiplexer_1_out;
  wire [31:0] multiplexer_2_out, multiplexer_3_out;

  Multiplexer #(.select(1), .width(1), .disabled("Z"), .enable("false")) multiplexer_1 (
    .in0(PredictJumpin), .in1(1'b0), .out(multiplexer_1_out), .sel(RST));
  Multiplexer #(.select(1), .width(32), .disabled("Z"), .enable("false")) multiplexer_2 (
    .in0(IRin), .in1({32{1'b0}}), .out(multiplexer_2_out), .sel(RST));
  Multiplexer #(.select(1), .width(32), .disabled("Z"), .enable("false")) multiplexer_3 (
    .in0(PCin), .in1({32{1'b0}}), .out(multiplexer_3_out), .sel(RST));
  Register #(.width(1), .trigger("rising"), .Select("low")) register_1 (
    .D(multiplexer_1_out), .en(EN), .Q(PredictJumpout), .clk(CLK));  // open: clr
  Register #(.width(32), .trigger("rising"), .Select("high")) register_2 (
    .D(multiplexer_2_out), .en(EN), .Q(IRout), .clk(CLK));  // open: clr
  Register #(.width(32), .trigger("rising"), .Select("high")) register_3 (
    .D(multiplexer_3_out), .en(EN), .Q(PCout), .clk(CLK));  // open: clr
endmodule

module ID_EX (
  input  Jalin,
  input  Jalrin,
  input  Bltin,
  input  Sbin,
  input  Beqin,
  input  Bnein,
  input  MemToRegin,
  input  MemWritein,
  input  [3:0] AluOpin,
  input  AluSrcBin,
  input  RegWritein,
  input  S_typein,
  input  [1:0] R1Forwardin,
  input  [1:0] R2Forwardin,
  input  Haltin,
  input  PredictJumpin,
  input  [31:0] R1in,
  input  [31:0] R2in,
  input  [4:0] W_in,
  input  [11:0] Imm_I_in,
  input  [11:0] Imm_S_in,
  input  [31:0] Imm_B_in,
  input  [31:0] Imm_J_in,
  input  [31:0] PCin,
  input  [31:0] IRin,
  input  RST,
  input  EN_H,
  input  CLK,
  output Jalout,
  output Jalrout,
  output Bltout,
  output Sbout,
  output Beqout,
  output Bneout,
  output MemToRegout,
  output MemWriteout,
  output [3:0] AluOpout,
  output AluSrcBout,
  output RegWriteout,
  output S_Typeout,
  output [1:0] R1Forwardout,
  output [1:0] R2Forwardout,
  output Haltout,
  output PredictJumpout,
  output [31:0] R1out,
  output [31:0] R2out,
  output [4:0] W_out,
  output [11:0] Imm_I_out,
  output [11:0] Imm_S_out,
  output [31:0] Imm_B_out,
  output [31:0] Imm_J_out,
  output [31:0] PCout,
  output [31:0] IRout
);

  wire multiplexer_1_out, multiplexer_2_out, multiplexer_3_out, multiplexer_4_out, multiplexer_5_out,
       multiplexer_6_out, multiplexer_7_out, multiplexer_8_out, multiplexer_10_out, multiplexer_11_out,
       multiplexer_12_out, multiplexer_15_out, multiplexer_16_out;
  wire [1:0] multiplexer_13_out, multiplexer_14_out;
  wire [3:0] multiplexer_9_out;
  wire [4:0] multiplexer_19_out;
  wire [11:0] multiplexer_20_out, multiplexer_21_out;
  wire [31:0] multiplexer_17_out, multiplexer_18_out, multiplexer_22_out, multiplexer_23_out,
       multiplexer_24_out, multiplexer_25_out;

  Multiplexer #(.select(1), .width(1), .disabled("Z"), .enable("false")) multiplexer_1 (
    .in0(Jalin), .in1(1'b0), .out(multiplexer_1_out), .sel(RST));
  Multiplexer #(.select(1), .width(1), .disabled("Z"), .enable("false")) multiplexer_2 (
    .in0(Jalrin), .in1(1'b0), .out(multiplexer_2_out), .sel(RST));
  Multiplexer #(.select(1), .width(1), .disabled("Z"), .enable("false")) multiplexer_3 (
    .in0(Bltin), .in1(1'b0), .out(multiplexer_3_out), .sel(RST));
  Multiplexer #(.select(1), .width(1), .disabled("Z"), .enable("false")) multiplexer_4 (
    .in0(Sbin), .in1(1'b0), .out(multiplexer_4_out), .sel(RST));
  Multiplexer #(.select(1), .width(1), .disabled("Z"), .enable("false")) multiplexer_5 (
    .in0(Beqin), .in1(1'b0), .out(multiplexer_5_out), .sel(RST));
  Multiplexer #(.select(1), .width(1), .disabled("Z"), .enable("false")) multiplexer_6 (
    .in0(Bnein), .in1(1'b0), .out(multiplexer_6_out), .sel(RST));
  Multiplexer #(.select(1), .width(1), .disabled("Z"), .enable("false")) multiplexer_7 (
    .in0(MemToRegin), .in1(1'b0), .out(multiplexer_7_out), .sel(RST));
  Multiplexer #(.select(1), .width(1), .disabled("Z"), .enable("false")) multiplexer_8 (
    .in0(MemWritein), .in1(1'b0), .out(multiplexer_8_out), .sel(RST));
  Multiplexer #(.select(1), .width(4), .disabled("Z"), .enable("false")) multiplexer_9 (
    .in0(AluOpin), .in1(4'b0000), .out(multiplexer_9_out), .sel(RST));
  Multiplexer #(.select(1), .width(1), .disabled("Z"), .enable("false")) multiplexer_10 (
    .in0(AluSrcBin), .in1(1'b0), .out(multiplexer_10_out), .sel(RST));
  Multiplexer #(.select(1), .width(1), .disabled("Z"), .enable("false")) multiplexer_11 (
    .in0(RegWritein), .in1(1'b0), .out(multiplexer_11_out), .sel(RST));
  Multiplexer #(.select(1), .width(1), .disabled("Z"), .enable("false")) multiplexer_12 (
    .in0(S_typein), .in1(1'b0), .out(multiplexer_12_out), .sel(RST));
  Multiplexer #(.select(1), .width(2), .disabled("Z"), .enable("false")) multiplexer_13 (
    .in0(R1Forwardin), .in1(2'b00), .out(multiplexer_13_out), .sel(RST));
  Multiplexer #(.select(1), .width(2), .disabled("Z"), .enable("false")) multiplexer_14 (
    .in0(R2Forwardin), .in1(2'b00), .out(multiplexer_14_out), .sel(RST));
  Multiplexer #(.select(1), .width(1), .disabled("Z"), .enable("false")) multiplexer_15 (
    .in0(Haltin), .in1(1'b0), .out(multiplexer_15_out), .sel(RST));
  Multiplexer #(.select(1), .width(1), .disabled("Z"), .enable("false")) multiplexer_16 (
    .in0(PredictJumpin), .in1(1'b0), .out(multiplexer_16_out), .sel(RST));
  Multiplexer #(.select(1), .width(32), .disabled("Z"), .enable("false")) multiplexer_17 (
    .in0(R1in), .in1({32{1'b0}}), .out(multiplexer_17_out), .sel(RST));
  Multiplexer #(.select(1), .width(32), .disabled("Z"), .enable("false")) multiplexer_18 (
    .in0(R2in), .in1({32{1'b0}}), .out(multiplexer_18_out), .sel(RST));
  Multiplexer #(.select(1), .width(5), .disabled("Z"), .enable("false")) multiplexer_19 (
    .in0(W_in), .in1({5{1'b0}}), .out(multiplexer_19_out), .sel(RST));
  Multiplexer #(.select(1), .width(12), .disabled("Z"), .enable("false")) multiplexer_20 (
    .in0(Imm_I_in), .in1({12{1'b0}}), .out(multiplexer_20_out), .sel(RST));
  Multiplexer #(.select(1), .width(12), .disabled("Z"), .enable("false")) multiplexer_21 (
    .in0(Imm_S_in), .in1({12{1'b0}}), .out(multiplexer_21_out), .sel(RST));
  Multiplexer #(.select(1), .width(32), .disabled("Z"), .enable("false")) multiplexer_22 (
    .in0(Imm_B_in), .in1({32{1'b0}}), .out(multiplexer_22_out), .sel(RST));
  Multiplexer #(.select(1), .width(32), .disabled("Z"), .enable("false")) multiplexer_23 (
    .in0(Imm_J_in), .in1({32{1'b0}}), .out(multiplexer_23_out), .sel(RST));
  Multiplexer #(.select(1), .width(32), .disabled("Z"), .enable("false")) multiplexer_24 (
    .in0(PCin), .in1({32{1'b0}}), .out(multiplexer_24_out), .sel(RST));
  Multiplexer #(.select(1), .width(32), .disabled("Z"), .enable("false")) multiplexer_25 (
    .in0(IRin), .in1({32{1'b0}}), .out(multiplexer_25_out), .sel(RST));
  Register #(.width(1), .trigger("rising"), .Select("low")) register_1 (
    .D(multiplexer_1_out), .en(EN_H), .Q(Jalout), .clk(CLK));  // open: clr
  Register #(.width(1), .trigger("rising"), .Select("low")) register_2 (
    .D(multiplexer_2_out), .en(EN_H), .Q(Jalrout), .clk(CLK));  // open: clr
  Register #(.width(1), .trigger("rising"), .Select("low")) register_3 (
    .D(multiplexer_3_out), .en(EN_H), .Q(Bltout), .clk(CLK));  // open: clr
  Register #(.width(1), .trigger("rising"), .Select("low")) register_4 (
    .D(multiplexer_4_out), .en(EN_H), .Q(Sbout), .clk(CLK));  // open: clr
  Register #(.width(1), .trigger("rising"), .Select("low")) register_5 (
    .D(multiplexer_5_out), .en(EN_H), .Q(Beqout), .clk(CLK));  // open: clr
  Register #(.width(1), .trigger("rising"), .Select("low")) register_6 (
    .D(multiplexer_6_out), .en(EN_H), .Q(Bneout), .clk(CLK));  // open: clr
  Register #(.width(1), .trigger("rising"), .Select("low")) register_7 (
    .D(multiplexer_7_out), .en(EN_H), .Q(MemToRegout), .clk(CLK));  // open: clr
  Register #(.width(1), .trigger("rising"), .Select("low")) register_8 (
    .D(multiplexer_8_out), .en(EN_H), .Q(MemWriteout), .clk(CLK));  // open: clr
  Register #(.width(4), .trigger("rising"), .Select("low")) register_9 (
    .D(multiplexer_9_out), .en(EN_H), .Q(AluOpout), .clk(CLK));  // open: clr
  Register #(.width(1), .trigger("rising"), .Select("low")) register_10 (
    .D(multiplexer_10_out), .en(EN_H), .Q(AluSrcBout), .clk(CLK));  // open: clr
  Register #(.width(1), .trigger("rising"), .Select("low")) register_11 (
    .D(multiplexer_11_out), .en(EN_H), .Q(RegWriteout), .clk(CLK));  // open: clr
  Register #(.width(1), .trigger("rising"), .Select("low")) register_12 (
    .D(multiplexer_12_out), .en(EN_H), .Q(S_Typeout), .clk(CLK));  // open: clr
  Register #(.width(2), .trigger("rising"), .Select("low")) register_13 (
    .D(multiplexer_13_out), .en(EN_H), .Q(R1Forwardout), .clk(CLK));  // open: clr
  Register #(.width(2), .trigger("rising"), .Select("low")) register_14 (
    .D(multiplexer_14_out), .en(EN_H), .Q(R2Forwardout), .clk(CLK));  // open: clr
  Register #(.width(1), .trigger("rising"), .Select("low")) register_15 (
    .D(multiplexer_15_out), .en(EN_H), .Q(Haltout), .clk(CLK));  // open: clr
  Register #(.width(1), .trigger("rising"), .Select("low")) register_16 (
    .D(multiplexer_16_out), .en(EN_H), .Q(PredictJumpout), .clk(CLK));  // open: clr
  Register #(.width(32), .trigger("rising"), .Select("low")) register_17 (
    .D(multiplexer_17_out), .en(EN_H), .Q(R1out), .clk(CLK));  // open: clr
  Register #(.width(32), .trigger("rising"), .Select("low")) register_18 (
    .D(multiplexer_18_out), .en(EN_H), .Q(R2out), .clk(CLK));  // open: clr
  Register #(.width(5), .trigger("rising"), .Select("low")) register_19 (
    .D(multiplexer_19_out), .en(EN_H), .Q(W_out), .clk(CLK));  // open: clr
  Register #(.width(12), .trigger("rising"), .Select("low")) register_20 (
    .D(multiplexer_20_out), .en(EN_H), .Q(Imm_I_out), .clk(CLK));  // open: clr
  Register #(.width(12), .trigger("rising"), .Select("low")) register_21 (
    .D(multiplexer_21_out), .en(EN_H), .Q(Imm_S_out), .clk(CLK));  // open: clr
  Register #(.width(32), .trigger("rising"), .Select("low")) register_22 (
    .D(multiplexer_22_out), .en(EN_H), .Q(Imm_B_out), .clk(CLK));  // open: clr
  Register #(.width(32), .trigger("rising"), .Select("low")) register_23 (
    .D(multiplexer_23_out), .en(EN_H), .Q(Imm_J_out), .clk(CLK));  // open: clr
  Register #(.width(32), .trigger("rising"), .Select("low")) register_24 (
    .D(multiplexer_24_out), .en(EN_H), .Q(PCout), .clk(CLK));  // open: clr
  Register #(.width(32), .trigger("rising"), .Select("low")) register_25 (
    .D(multiplexer_25_out), .en(EN_H), .Q(IRout), .clk(CLK));  // open: clr
endmodule

module EX_MEM (
  input  MemToRegin,
  input  MemWritein,
  input  Jin,
  input  Haltin,
  input  RegWritein,
  input  [3:0] ByteSelectin,
  input  [31:0] Resultin,
  input  [31:0] MDin,
  input  [4:0] W_in,
  input  [31:0] IRin,
  input  [31:0] PCin,
  input  RST,
  input  EN_H,
  input  CLK,
  output MemToRegout,
  output MemWriteout,
  output Jout,
  output Haltout,
  output RegWriteout,
  output [3:0] ByteSelectout,
  output [31:0] Rrsultout,
  output [31:0] MDout,
  output [4:0] W_out,
  output [31:0] IRout,
  output [31:0] PCout
);

  wire multiplexer_1_out, multiplexer_2_out, multiplexer_3_out, multiplexer_4_out, multiplexer_5_out;
  wire [3:0] multiplexer_6_out;
  wire [4:0] multiplexer_9_out;
  wire [31:0] multiplexer_7_out, multiplexer_8_out, multiplexer_10_out, multiplexer_11_out;

  Multiplexer #(.select(1), .width(1), .disabled("Z"), .enable("false")) multiplexer_1 (
    .in0(MemToRegin), .in1(1'b0), .out(multiplexer_1_out), .sel(RST));
  Multiplexer #(.select(1), .width(1), .disabled("Z"), .enable("false")) multiplexer_2 (
    .in0(MemWritein), .in1(1'b0), .out(multiplexer_2_out), .sel(RST));
  Multiplexer #(.select(1), .width(1), .disabled("Z"), .enable("false")) multiplexer_3 (
    .in0(Jin), .in1(1'b0), .out(multiplexer_3_out), .sel(RST));
  Multiplexer #(.select(1), .width(1), .disabled("Z"), .enable("false")) multiplexer_4 (
    .in0(Haltin), .in1(1'b0), .out(multiplexer_4_out), .sel(RST));
  Multiplexer #(.select(1), .width(1), .disabled("Z"), .enable("false")) multiplexer_5 (
    .in0(RegWritein), .in1(1'b0), .out(multiplexer_5_out), .sel(RST));
  Multiplexer #(.select(1), .width(4), .disabled("Z"), .enable("false")) multiplexer_6 (
    .in0(ByteSelectin), .in1(4'b0000), .out(multiplexer_6_out), .sel(RST));
  Multiplexer #(.select(1), .width(32), .disabled("Z"), .enable("false")) multiplexer_7 (
    .in0(Resultin), .in1({32{1'b0}}), .out(multiplexer_7_out), .sel(RST));
  Multiplexer #(.select(1), .width(32), .disabled("Z"), .enable("false")) multiplexer_8 (
    .in0(MDin), .in1({32{1'b0}}), .out(multiplexer_8_out), .sel(RST));
  Multiplexer #(.select(1), .width(5), .disabled("Z"), .enable("false")) multiplexer_9 (
    .in0(W_in), .in1({5{1'b0}}), .out(multiplexer_9_out), .sel(RST));
  Multiplexer #(.select(1), .width(32), .disabled("Z"), .enable("false")) multiplexer_10 (
    .in0(IRin), .in1({32{1'b0}}), .out(multiplexer_10_out), .sel(RST));
  Multiplexer #(.select(1), .width(32), .disabled("Z"), .enable("false")) multiplexer_11 (
    .in0(PCin), .in1({32{1'b0}}), .out(multiplexer_11_out), .sel(RST));
  Register #(.width(1), .trigger("rising"), .Select("high")) register_1 (
    .D(multiplexer_1_out), .en(EN_H), .Q(MemToRegout), .clk(CLK));  // open: clr
  Register #(.width(1), .trigger("rising"), .Select("high")) register_2 (
    .D(multiplexer_2_out), .en(EN_H), .Q(MemWriteout), .clk(CLK));  // open: clr
  Register #(.width(1), .trigger("rising"), .Select("high")) register_3 (
    .D(multiplexer_3_out), .en(EN_H), .Q(Jout), .clk(CLK));  // open: clr
  Register #(.width(1), .trigger("rising"), .Select("low")) register_4 (
    .D(multiplexer_4_out), .en(EN_H), .Q(Haltout), .clk(CLK));  // open: clr
  Register #(.width(1), .trigger("rising"), .Select("high")) register_5 (
    .D(multiplexer_5_out), .en(EN_H), .Q(RegWriteout), .clk(CLK));  // open: clr
  Register #(.width(4), .trigger("rising"), .Select("high")) register_6 (
    .D(multiplexer_6_out), .en(EN_H), .Q(ByteSelectout), .clk(CLK));  // open: clr
  Register #(.width(32), .trigger("rising"), .Select("high")) register_7 (
    .D(multiplexer_7_out), .en(EN_H), .Q(Rrsultout), .clk(CLK));  // open: clr
  Register #(.width(32), .trigger("rising"), .Select("high")) register_8 (
    .D(multiplexer_8_out), .en(EN_H), .Q(MDout), .clk(CLK));  // open: clr
  Register #(.width(5), .trigger("rising"), .Select("high")) register_9 (
    .D(multiplexer_9_out), .en(EN_H), .Q(W_out), .clk(CLK));  // open: clr
  Register #(.width(32), .trigger("rising"), .Select("high")) register_10 (
    .D(multiplexer_10_out), .en(EN_H), .Q(IRout), .clk(CLK));  // open: clr
  Register #(.width(32), .trigger("rising"), .Select("high")) register_11 (
    .D(multiplexer_11_out), .en(EN_H), .Q(PCout), .clk(CLK));  // open: clr
endmodule

module MEM_WB (
  input  MemToRegin,
  input  Jin,
  input  Haltin,
  input  RegWritein,
  input  [31:0] Memdatein,
  input  [31:0] Resultin,
  input  [4:0] W_in,
  input  [31:0] IRin,
  input  [31:0] PCin,
  input  RST,
  input  EN_H,
  input  CLK,
  output MemToRegout,
  output Jout,
  output Haltout,
  output RegWriteout,
  output [31:0] Memdateout,
  output [31:0] Resultout,
  output [4:0] W_out,
  output [31:0] IRout,
  output [31:0] PCout
);

  wire multiplexer_1_out, multiplexer_2_out, multiplexer_3_out, multiplexer_4_out;
  wire [4:0] multiplexer_7_out;
  wire [31:0] multiplexer_5_out, multiplexer_6_out, multiplexer_8_out, multiplexer_9_out;

  Multiplexer #(.select(1), .width(1), .disabled("Z"), .enable("false")) multiplexer_1 (
    .in0(MemToRegin), .in1(1'b0), .out(multiplexer_1_out), .sel(RST));
  Multiplexer #(.select(1), .width(1), .disabled("Z"), .enable("false")) multiplexer_2 (
    .in0(Jin), .in1(1'b0), .out(multiplexer_2_out), .sel(RST));
  Multiplexer #(.select(1), .width(1), .disabled("Z"), .enable("false")) multiplexer_3 (
    .in0(Haltin), .in1(1'b0), .out(multiplexer_3_out), .sel(RST));
  Multiplexer #(.select(1), .width(1), .disabled("Z"), .enable("false")) multiplexer_4 (
    .in0(RegWritein), .in1(1'b0), .out(multiplexer_4_out), .sel(RST));
  Multiplexer #(.select(1), .width(32), .disabled("Z"), .enable("false")) multiplexer_5 (
    .in0(Memdatein), .in1({32{1'b0}}), .out(multiplexer_5_out), .sel(RST));
  Multiplexer #(.select(1), .width(32), .disabled("Z"), .enable("false")) multiplexer_6 (
    .in0(Resultin), .in1({32{1'b0}}), .out(multiplexer_6_out), .sel(RST));
  Multiplexer #(.select(1), .width(5), .disabled("Z"), .enable("false")) multiplexer_7 (
    .in0(W_in), .in1({5{1'b0}}), .out(multiplexer_7_out), .sel(RST));
  Multiplexer #(.select(1), .width(32), .disabled("Z"), .enable("false")) multiplexer_8 (
    .in0(IRin), .in1({32{1'b0}}), .out(multiplexer_8_out), .sel(RST));
  Multiplexer #(.select(1), .width(32), .disabled("Z"), .enable("false")) multiplexer_9 (
    .in0(PCin), .in1({32{1'b0}}), .out(multiplexer_9_out), .sel(RST));
  Register #(.width(1), .trigger("rising"), .Select("low")) register_1 (
    .D(multiplexer_1_out), .en(EN_H), .Q(MemToRegout), .clk(CLK));  // open: clr
  Register #(.width(1), .trigger("rising"), .Select("low")) register_2 (
    .D(multiplexer_2_out), .en(EN_H), .Q(Jout), .clk(CLK));  // open: clr
  Register #(.width(1), .trigger("rising"), .Select("low")) register_3 (
    .D(multiplexer_3_out), .en(EN_H), .Q(Haltout), .clk(CLK));  // open: clr
  Register #(.width(1), .trigger("rising"), .Select("low")) register_4 (
    .D(multiplexer_4_out), .en(EN_H), .Q(RegWriteout), .clk(CLK));  // open: clr
  Register #(.width(32), .trigger("rising"), .Select("low")) register_5 (
    .D(multiplexer_5_out), .en(EN_H), .Q(Memdateout), .clk(CLK));  // open: clr
  Register #(.width(32), .trigger("rising"), .Select("low")) register_6 (
    .D(multiplexer_6_out), .en(EN_H), .Q(Resultout), .clk(CLK));  // open: clr
  Register #(.width(5), .trigger("rising"), .Select("low")) register_7 (
    .D(multiplexer_7_out), .en(EN_H), .Q(W_out), .clk(CLK));  // open: clr
  Register #(.width(32), .trigger("rising"), .Select("low")) register_8 (
    .D(multiplexer_8_out), .en(EN_H), .Q(IRout), .clk(CLK));  // open: clr
  Register #(.width(32), .trigger("rising"), .Select("low")) register_9 (
    .D(multiplexer_9_out), .en(EN_H), .Q(PCout), .clk(CLK));  // open: clr
endmodule

module \数据相关检测逻辑  (
  input  [4:0] ID_R1_num,
  input  [4:0] EX_W_num,
  input  EX_RegWrite,
  input  [4:0] ID_R2_num,
  input  [4:0] MEM_W_num,
  input  MEM_RegWrite,
  input  [4:0] OP,
  input  [4:0] Funct,
  output DataHazzard
);

  wire and_1_out, and_2_out, and_3_out, and_4_out, and_5_out, and_6_out, comparator_1_eq, comparator_2_eq,
       comparator_3_eq, comparator_4_eq, comparator_5_eq, comparator_6_eq, comparator_7_eq, comparator_8_eq,
       or_1_out, or_2_out, \寄存器有效逻辑_1_r1 , \寄存器有效逻辑_1_r2 ;

  \寄存器有效逻辑  \u_寄存器有效逻辑_1  (
    .OP2(OP[0]), .OP3(OP[1]), .OP4(OP[2]), .OP5(OP[3]), .OP6(OP[4]), .F12(Funct[0]), .F13(Funct[1]),
    .F14(Funct[2]), .F25(Funct[3]), .F30(Funct[4]), .R1(\寄存器有效逻辑_1_r1 ), .R2(\寄存器有效逻辑_1_r2 ));
  Comparator #(.width(5), .mode("twosComplement")) comparator_1 (
    .a(ID_R1_num), .b(EX_W_num), .eq(comparator_1_eq));  // open: gt, lt
  Comparator #(.width(5), .mode("twosComplement")) comparator_2 (
    .a(ID_R1_num), .b({5{1'b0}}), .eq(comparator_2_eq));  // open: gt, lt
  Comparator #(.width(5), .mode("twosComplement")) comparator_3 (
    .a(ID_R2_num), .b(EX_W_num), .eq(comparator_3_eq));  // open: gt, lt
  Comparator #(.width(5), .mode("twosComplement")) comparator_4 (
    .a(ID_R2_num), .b({5{1'b0}}), .eq(comparator_4_eq));  // open: gt, lt
  and and_1 (and_1_out, comparator_1_eq, EX_RegWrite, ~comparator_2_eq);  // AND_Gate
  and and_2 (and_2_out, comparator_3_eq, EX_RegWrite, ~comparator_4_eq);  // AND_Gate
  Comparator #(.width(5), .mode("twosComplement")) comparator_5 (
    .a(ID_R1_num), .b(MEM_W_num), .eq(comparator_5_eq));  // open: gt, lt
  Comparator #(.width(5), .mode("twosComplement")) comparator_6 (
    .a(ID_R1_num), .b({5{1'b0}}), .eq(comparator_6_eq));  // open: gt, lt
  Comparator #(.width(5), .mode("twosComplement")) comparator_7 (
    .a(ID_R2_num), .b(MEM_W_num), .eq(comparator_7_eq));  // open: gt, lt
  Comparator #(.width(5), .mode("twosComplement")) comparator_8 (
    .a(ID_R2_num), .b({5{1'b0}}), .eq(comparator_8_eq));  // open: gt, lt
  and and_3 (and_3_out, comparator_5_eq, MEM_RegWrite, ~comparator_6_eq);  // AND_Gate
  and and_4 (and_4_out, comparator_7_eq, MEM_RegWrite, ~comparator_8_eq);  // AND_Gate
  or or_1 (or_1_out, and_3_out, and_1_out);
  or or_2 (or_2_out, and_2_out, and_4_out);
  and and_5 (and_5_out, or_1_out, \寄存器有效逻辑_1_r1 );
  and and_6 (and_6_out, \寄存器有效逻辑_1_r2 , or_2_out);
  or or_3 (DataHazzard, and_5_out, and_6_out);
endmodule

module \寄存器有效逻辑  (
  input  OP2,
  input  OP3,
  input  OP4,
  input  OP5,
  input  OP6,
  input  F12,
  input  F13,
  input  F14,
  input  F25,
  input  F30,
  output R1,
  output R2
);

  wire and_1_out, and_2_out, and_3_out, and_4_out, and_5_out, and_6_out, and_7_out, and_8_out, and_9_out,
       and_10_out, and_11_out, and_12_out, and_13_out, and_14_out, and_15_out, and_16_out, and_17_out,
       and_18_out, and_19_out, and_20_out, and_21_out, and_22_out, and_23_out, and_24_out, and_25_out,
       and_26_out, and_27_out, and_28_out, and_29_out, and_30_out, and_31_out, and_32_out, and_33_out,
       and_34_out, and_35_out, and_36_out, and_37_out, and_38_out, not_1_out, not_2_out, not_3_out,
       not_4_out, not_5_out, not_6_out, not_7_out, not_8_out, not_9_out, not_10_out, not_11_out, not_12_out,
       not_13_out, not_14_out, not_15_out, not_16_out, not_17_out, not_18_out, not_19_out, not_20_out,
       not_21_out, not_22_out, not_23_out, not_24_out, not_25_out, not_26_out, not_27_out, not_28_out,
       not_29_out, not_30_out, not_31_out, not_32_out, not_33_out, not_34_out, not_35_out, not_36_out,
       not_37_out, not_38_out, not_39_out, not_40_out, not_41_out, not_42_out, not_43_out, not_44_out,
       not_45_out, not_46_out, not_47_out, not_48_out, not_49_out, not_50_out, not_51_out, not_52_out,
       not_53_out, not_54_out, not_55_out, not_56_out, not_57_out, not_58_out, not_59_out, not_60_out,
       not_61_out, not_62_out, not_63_out, not_64_out, not_65_out, not_66_out, not_67_out, not_68_out,
       not_69_out, not_70_out, not_71_out, not_72_out, not_73_out, not_74_out, not_75_out, not_76_out,
       not_77_out, not_78_out, not_79_out, not_80_out, not_81_out, not_82_out, not_83_out, not_84_out,
       not_85_out, not_86_out, not_87_out, not_88_out, not_89_out, not_90_out, not_91_out, not_92_out,
       not_93_out, not_94_out, not_95_out, not_96_out, not_97_out, not_98_out, not_99_out, not_100_out,
       not_101_out, not_102_out, not_103_out, not_104_out, not_105_out, not_106_out, not_107_out,
       not_108_out, not_109_out, not_110_out, not_111_out, not_112_out, not_113_out, not_114_out,
       not_115_out, not_116_out, not_117_out, not_118_out, not_119_out, not_120_out, not_121_out,
       not_122_out, not_123_out, not_124_out, not_125_out, not_126_out, not_127_out, not_128_out,
       not_129_out, not_130_out, not_131_out, not_132_out, not_133_out, not_134_out, not_135_out,
       not_136_out, not_137_out, not_138_out, not_139_out, not_140_out, not_141_out, not_142_out,
       not_143_out, not_144_out, not_145_out, not_146_out, not_147_out, not_148_out, not_149_out,
       not_150_out, not_151_out, not_152_out, not_153_out, not_154_out, not_155_out, not_156_out,
       not_157_out, not_158_out, not_159_out, not_160_out, not_161_out, not_162_out, not_163_out,
       not_164_out, not_165_out, not_166_out, not_167_out, not_168_out, not_169_out, not_170_out,
       not_171_out, not_172_out, not_173_out, not_174_out, not_175_out, not_176_out, not_177_out,
       not_178_out, not_179_out, not_180_out, not_181_out, not_182_out, not_183_out, not_184_out,
       not_185_out, not_186_out, not_187_out, not_188_out, not_189_out, not_190_out, not_191_out,
       not_192_out, not_193_out, not_194_out, not_195_out, not_196_out, not_197_out, not_198_out,
       not_199_out, not_200_out, not_201_out, not_202_out, not_203_out, not_204_out, not_205_out,
       not_206_out, not_207_out, not_208_out, not_209_out, not_210_out, not_211_out, not_212_out,
       not_213_out, not_214_out, not_215_out, not_216_out, not_217_out, not_218_out, not_219_out,
       not_220_out, not_221_out, not_222_out, not_223_out, not_224_out, not_225_out, not_226_out,
       not_227_out, not_228_out, not_229_out, not_230_out, not_231_out, not_232_out, not_233_out,
       not_234_out, not_235_out;

  not not_1 (not_1_out, F30);
  not not_2 (not_2_out, F25);
  not not_3 (not_3_out, F14);
  not not_4 (not_4_out, F13);
  not not_5 (not_5_out, F12);
  not not_6 (not_6_out, OP6);
  not not_7 (not_7_out, OP3);
  not not_8 (not_8_out, OP2);
  not not_9 (not_9_out, F25);
  not not_10 (not_10_out, F14);
  not not_11 (not_11_out, F13);
  not not_12 (not_12_out, F12);
  not not_13 (not_13_out, OP6);
  not not_14 (not_14_out, OP3);
  not not_15 (not_15_out, OP2);
  not not_16 (not_16_out, F30);
  not not_17 (not_17_out, F25);
  not not_18 (not_18_out, OP6);
  not not_19 (not_19_out, OP3);
  not not_20 (not_20_out, OP2);
  not not_21 (not_21_out, F30);
  not not_22 (not_22_out, F25);
  not not_23 (not_23_out, F12);
  not not_24 (not_24_out, OP6);
  not not_25 (not_25_out, OP3);
  not not_26 (not_26_out, OP2);
  not not_27 (not_27_out, F30);
  not not_28 (not_28_out, F25);
  not not_29 (not_29_out, F14);
  not not_30 (not_30_out, F12);
  not not_31 (not_31_out, OP6);
  not not_32 (not_32_out, OP3);
  not not_33 (not_33_out, OP2);
  not not_34 (not_34_out, F30);
  not not_35 (not_35_out, F25);
  not not_36 (not_36_out, F14);
  not not_37 (not_37_out, OP6);
  not not_38 (not_38_out, OP3);
  not not_39 (not_39_out, OP2);
  not not_40 (not_40_out, F14);
  not not_41 (not_41_out, F13);
  not not_42 (not_42_out, F12);
  not not_43 (not_43_out, OP6);
  not not_44 (not_44_out, OP5);
  not not_45 (not_45_out, OP3);
  not not_46 (not_46_out, OP2);
  not not_47 (not_47_out, OP6);
  not not_48 (not_48_out, OP5);
  not not_49 (not_49_out, OP3);
  not not_50 (not_50_out, OP2);
  not not_51 (not_51_out, F12);
  not not_52 (not_52_out, OP6);
  not not_53 (not_53_out, OP5);
  not not_54 (not_54_out, OP3);
  not not_55 (not_55_out, OP2);
  not not_56 (not_56_out, F13);
  not not_57 (not_57_out, F12);
  not not_58 (not_58_out, OP6);
  not not_59 (not_59_out, OP5);
  not not_60 (not_60_out, OP3);
  not not_61 (not_61_out, OP2);
  not not_62 (not_62_out, F30);
  not not_63 (not_63_out, F25);
  not not_64 (not_64_out, F14);
  not not_65 (not_65_out, F12);
  not not_66 (not_66_out, OP6);
  not not_67 (not_67_out, OP5);
  not not_68 (not_68_out, OP3);
  not not_69 (not_69_out, OP2);
  not not_70 (not_70_out, F30);
  not not_71 (not_71_out, F25);
  not not_72 (not_72_out, F14);
  not not_73 (not_73_out, F13);
  not not_74 (not_74_out, OP6);
  not not_75 (not_75_out, OP5);
  not not_76 (not_76_out, OP3);
  not not_77 (not_77_out, OP2);
  not not_78 (not_78_out, F30);
  not not_79 (not_79_out, F25);
  not not_80 (not_80_out, F13);
  not not_81 (not_81_out, OP6);
  not not_82 (not_82_out, OP5);
  not not_83 (not_83_out, OP3);
  not not_84 (not_84_out, OP2);
  not not_85 (not_85_out, F25);
  not not_86 (not_86_out, F13);
  not not_87 (not_87_out, OP6);
  not not_88 (not_88_out, OP5);
  not not_89 (not_89_out, OP3);
  not not_90 (not_90_out, OP2);
  not not_91 (not_91_out, F14);
  not not_92 (not_92_out, F12);
  not not_93 (not_93_out, OP6);
  not not_94 (not_94_out, OP5);
  not not_95 (not_95_out, OP4);
  not not_96 (not_96_out, OP3);
  not not_97 (not_97_out, OP2);
  not not_98 (not_98_out, F14);
  not not_99 (not_99_out, F12);
  not not_100 (not_100_out, OP6);
  not not_101 (not_101_out, OP4);
  not not_102 (not_102_out, OP3);
  not not_103 (not_103_out, OP2);
  not not_104 (not_104_out, F30);
  not not_105 (not_105_out, F25);
  not not_106 (not_106_out, F14);
  not not_107 (not_107_out, F13);
  not not_108 (not_108_out, F12);
  not not_109 (not_109_out, OP3);
  not not_110 (not_110_out, OP2);
  not not_111 (not_111_out, F14);
  not not_112 (not_112_out, F13);
  not not_113 (not_113_out, F12);
  not not_114 (not_114_out, OP4);
  not not_115 (not_115_out, OP3);
  not not_116 (not_116_out, OP2);
  not not_117 (not_117_out, F14);
  not not_118 (not_118_out, F13);
  not not_119 (not_119_out, OP4);
  not not_120 (not_120_out, OP3);
  not not_121 (not_121_out, OP2);
  not not_122 (not_122_out, F14);
  not not_123 (not_123_out, F13);
  not not_124 (not_124_out, F12);
  not not_125 (not_125_out, OP4);
  not not_126 (not_126_out, OP3);
  not not_127 (not_127_out, F30);
  not not_128 (not_128_out, F25);
  not not_129 (not_129_out, F13);
  not not_130 (not_130_out, OP6);
  not not_131 (not_131_out, OP3);
  not not_132 (not_132_out, OP2);
  not not_133 (not_133_out, F25);
  not not_134 (not_134_out, F13);
  not not_135 (not_135_out, OP6);
  not not_136 (not_136_out, OP3);
  not not_137 (not_137_out, OP2);
  not not_138 (not_138_out, F14);
  not not_139 (not_139_out, F13);
  not not_140 (not_140_out, F12);
  not not_141 (not_141_out, OP6);
  not not_142 (not_142_out, OP4);
  not not_143 (not_143_out, OP3);
  not not_144 (not_144_out, OP2);
  not not_145 (not_145_out, F13);
  not not_146 (not_146_out, F12);
  not not_147 (not_147_out, OP4);
  not not_148 (not_148_out, OP3);
  not not_149 (not_149_out, OP2);
  not not_150 (not_150_out, F30);
  not not_151 (not_151_out, F25);
  not not_152 (not_152_out, F14);
  not not_153 (not_153_out, F13);
  not not_154 (not_154_out, F12);
  not not_155 (not_155_out, OP6);
  not not_156 (not_156_out, OP3);
  not not_157 (not_157_out, OP2);
  not not_158 (not_158_out, F25);
  not not_159 (not_159_out, F14);
  not not_160 (not_160_out, F13);
  not not_161 (not_161_out, F12);
  not not_162 (not_162_out, OP6);
  not not_163 (not_163_out, OP3);
  not not_164 (not_164_out, OP2);
  not not_165 (not_165_out, F30);
  not not_166 (not_166_out, F25);
  not not_167 (not_167_out, OP6);
  not not_168 (not_168_out, OP3);
  not not_169 (not_169_out, OP2);
  not not_170 (not_170_out, F30);
  not not_171 (not_171_out, F25);
  not not_172 (not_172_out, F12);
  not not_173 (not_173_out, OP6);
  not not_174 (not_174_out, OP3);
  not not_175 (not_175_out, OP2);
  not not_176 (not_176_out, F30);
  not not_177 (not_177_out, F25);
  not not_178 (not_178_out, F14);
  not not_179 (not_179_out, F12);
  not not_180 (not_180_out, OP6);
  not not_181 (not_181_out, OP3);
  not not_182 (not_182_out, OP2);
  not not_183 (not_183_out, F30);
  not not_184 (not_184_out, F25);
  not not_185 (not_185_out, F14);
  not not_186 (not_186_out, OP6);
  not not_187 (not_187_out, OP3);
  not not_188 (not_188_out, OP2);
  not not_189 (not_189_out, F14);
  not not_190 (not_190_out, F12);
  not not_191 (not_191_out, OP6);
  not not_192 (not_192_out, OP4);
  not not_193 (not_193_out, OP3);
  not not_194 (not_194_out, OP2);
  not not_195 (not_195_out, F30);
  not not_196 (not_196_out, F25);
  not not_197 (not_197_out, F14);
  not not_198 (not_198_out, F13);
  not not_199 (not_199_out, F12);
  not not_200 (not_200_out, OP3);
  not not_201 (not_201_out, OP2);
  not not_202 (not_202_out, F14);
  not not_203 (not_203_out, F13);
  not not_204 (not_204_out, F12);
  not not_205 (not_205_out, OP4);
  not not_206 (not_206_out, OP3);
  not not_207 (not_207_out, OP2);
  not not_208 (not_208_out, F14);
  not not_209 (not_209_out, F13);
  not not_210 (not_210_out, OP4);
  not not_211 (not_211_out, OP3);
  not not_212 (not_212_out, OP2);
  not not_213 (not_213_out, F30);
  not not_214 (not_214_out, F25);
  not not_215 (not_215_out, F13);
  not not_216 (not_216_out, OP6);
  not not_217 (not_217_out, OP3);
  not not_218 (not_218_out, OP2);
  not not_219 (not_219_out, F25);
  not not_220 (not_220_out, F13);
  not not_221 (not_221_out, OP6);
  not not_222 (not_222_out, OP3);
  not not_223 (not_223_out, OP2);
  not not_224 (not_224_out, F14);
  not not_225 (not_225_out, F13);
  not not_226 (not_226_out, F12);
  not not_227 (not_227_out, OP6);
  not not_228 (not_228_out, OP4);
  not not_229 (not_229_out, OP3);
  not not_230 (not_230_out, OP2);
  not not_231 (not_231_out, F13);
  not not_232 (not_232_out, F12);
  not not_233 (not_233_out, OP4);
  not not_234 (not_234_out, OP3);
  not not_235 (not_235_out, OP2);
  and and_1 (and_1_out, not_1_out, not_2_out, not_3_out, not_4_out, not_5_out, not_6_out, OP5, OP4, not_7_out, not_8_out);
  and and_2 (and_2_out, F30, not_9_out, not_10_out, not_11_out, not_12_out, not_13_out, OP5, OP4, not_14_out, not_15_out);
  and and_3 (and_3_out, not_16_out, not_17_out, F14, F13, F12, not_18_out, OP5, OP4, not_19_out, not_20_out);
  and and_4 (and_4_out, not_21_out, not_22_out, F14, F13, not_23_out, not_24_out, OP5, OP4, not_25_out, not_26_out);
  and and_5 (and_5_out, not_27_out, not_28_out, not_29_out, F13, not_30_out, not_31_out, OP5, OP4, not_32_out, not_33_out);
  and and_6 (and_6_out, not_34_out, not_35_out, not_36_out, F13, F12, not_37_out, OP5, OP4, not_38_out, not_39_out);
  and and_7 (and_7_out, not_40_out, not_41_out, not_42_out, not_43_out, not_44_out, OP4, not_45_out, not_46_out);
  and and_8 (and_8_out, F14, F13, F12, not_47_out, not_48_out, OP4, not_49_out, not_50_out);
  and and_9 (and_9_out, F14, F13, not_51_out, not_52_out, not_53_out, OP4, not_54_out, not_55_out);
  and and_10 (and_10_out, F14, not_56_out, not_57_out, not_58_out, not_59_out, OP4, not_60_out, not_61_out);
  and and_11 (and_11_out, not_62_out, not_63_out, not_64_out, F13, not_65_out, not_66_out, not_67_out, OP4, not_68_out, not_69_out);
  and and_12 (and_12_out, not_70_out, not_71_out, not_72_out, not_73_out, F12, not_74_out, not_75_out, OP4, not_76_out, not_77_out);
  and and_13 (and_13_out, not_78_out, not_79_out, F14, not_80_out, F12, not_81_out, not_82_out, OP4, not_83_out, not_84_out);
  and and_14 (and_14_out, F30, not_85_out, F14, not_86_out, F12, not_87_out, not_88_out, OP4, not_89_out, not_90_out);
  and and_15 (and_15_out, not_91_out, F13, not_92_out, not_93_out, not_94_out, not_95_out, not_96_out, not_97_out);
  and and_16 (and_16_out, not_98_out, F13, not_99_out, not_100_out, OP5, not_101_out, not_102_out, not_103_out);
  and and_17 (and_17_out, not_104_out, not_105_out, not_106_out, not_107_out, not_108_out, OP6, OP5, OP4, not_109_out, not_110_out);
  and and_18 (and_18_out, not_111_out, not_112_out, not_113_out, OP6, OP5, not_114_out, not_115_out, not_116_out);
  and and_19 (and_19_out, not_117_out, not_118_out, F12, OP6, OP5, not_119_out, not_120_out, not_121_out);
  and and_20 (and_20_out, not_122_out, not_123_out, not_124_out, OP6, OP5, not_125_out, not_126_out, OP2);
  and and_21 (and_21_out, not_127_out, not_128_out, F14, not_129_out, F12, not_130_out, OP5, OP4, not_131_out, not_132_out);
  and and_22 (and_22_out, F30, not_133_out, F14, not_134_out, F12, not_135_out, OP5, OP4, not_136_out, not_137_out);
  and and_23 (and_23_out, not_138_out, not_139_out, not_140_out, not_141_out, OP5, not_142_out, not_143_out, not_144_out);
  and and_24 (and_24_out, F14, not_145_out, not_146_out, OP6, OP5, not_147_out, not_148_out, not_149_out);
  and and_25 (and_25_out, not_150_out, not_151_out, not_152_out, not_153_out, not_154_out, not_155_out, OP5, OP4, not_156_out, not_157_out);
  and and_26 (and_26_out, F30, not_158_out, not_159_out, not_160_out, not_161_out, not_162_out, OP5, OP4, not_163_out, not_164_out);
  and and_27 (and_27_out, not_165_out, not_166_out, F14, F13, F12, not_167_out, OP5, OP4, not_168_out, not_169_out);
  and and_28 (and_28_out, not_170_out, not_171_out, F14, F13, not_172_out, not_173_out, OP5, OP4, not_174_out, not_175_out);
  and and_29 (and_29_out, not_176_out, not_177_out, not_178_out, F13, not_179_out, not_180_out, OP5, OP4, not_181_out, not_182_out);
  and and_30 (and_30_out, not_183_out, not_184_out, not_185_out, F13, F12, not_186_out, OP5, OP4, not_187_out, not_188_out);
  and and_31 (and_31_out, not_189_out, F13, not_190_out, not_191_out, OP5, not_192_out, not_193_out, not_194_out);
  and and_32 (and_32_out, not_195_out, not_196_out, not_197_out, not_198_out, not_199_out, OP6, OP5, OP4, not_200_out, not_201_out);
  and and_33 (and_33_out, not_202_out, not_203_out, not_204_out, OP6, OP5, not_205_out, not_206_out, not_207_out);
  and and_34 (and_34_out, not_208_out, not_209_out, F12, OP6, OP5, not_210_out, not_211_out, not_212_out);
  and and_35 (and_35_out, not_213_out, not_214_out, F14, not_215_out, F12, not_216_out, OP5, OP4, not_217_out, not_218_out);
  and and_36 (and_36_out, F30, not_219_out, F14, not_220_out, F12, not_221_out, OP5, OP4, not_222_out, not_223_out);
  and and_37 (and_37_out, not_224_out, not_225_out, not_226_out, not_227_out, OP5, not_228_out, not_229_out, not_230_out);
  and and_38 (and_38_out, F14, not_231_out, not_232_out, OP6, OP5, not_233_out, not_234_out, not_235_out);
  or or_1 (R2, and_25_out, and_26_out, and_27_out, and_28_out, and_29_out, and_30_out, and_31_out, and_32_out, and_33_out, and_34_out, and_35_out, and_36_out, and_37_out, and_38_out);
  or or_2 (R1, and_1_out, and_2_out, and_3_out, and_4_out, and_5_out, and_6_out, and_7_out, and_8_out, and_9_out, and_10_out, and_11_out, and_12_out, and_13_out, and_14_out, and_15_out, and_16_out, and_17_out, and_18_out, and_19_out, and_20_out, and_21_out, and_22_out, and_23_out, and_24_out);
endmodule

module \流水线中断  (
  output RegWrite,
  output MemWrite,
  output [31:0] IF_PC,
  output [31:0] ID_PC,
  output [31:0] EX_PC,
  output [31:0] M_PC,
  output [31:0] WB_PC,
  output [31:0] RDin,
  output [31:0] MDin,
  output [31:0] LedData
);

  wire AluSrcB, and_1_out, and_2_out, and_3_out, and_4_out, and_5_out, and_6_out, and_7_out, and_8_out,
       and_9_out, and_10_out, B, Beq, Blt, Bne, Bubble1, Bubble2, CLK, clock_1_out, comparator_1_eq,
       comparator_1_lt, comparator_2_eq, comparator_3_eq, comparator_4_eq, comparator_5_eq, d_ff_1_q,
       d_ff_2_q, d_ff_3_q, d_ff_4_q, DataHazzard, decoder_1_out1, decoder_1_out2, decoder_1_out3, ecall, en,
       equal, ex_mem_1_haltout, ex_mem_1_jout, ex_mem_1_memtoregout, EX_MemToReg, EX_RegWrite, Go, halt,
       id_ex_1_p1, id_ex_1_p2, id_ex_1_p26, id_ex_1_p33, id_ex_1_p34, id_ex_1_p35, id_ex_1_p36, id_ex_1_p37,
       id_ex_1_p39, id_ex_1_p41, id_ex_1_p43, id_ex_1_p48, id_ex_1_p57, id_ex_1_p61, IE, Int, Intq, IR1,
       IR1_q, IR2, IR2_q, IR3, IR3_q, J, JAL, JALR, less, Load_Use, MEM_RegWrite, mem_wb_1_haltout,
       mem_wb_1_memtoregout, MemToReg, nand_1_out, not_1_out, not_2_out, not_3_out, not_4_out, not_5_out,
       not_6_out, not_7_out, or_1_out, or_7_out, or_8_out, or_9_out, or_10_out, or_11_out, Ret1, Ret2, Ret3,
       RST, S_Type, Sb, uret, W1, W2, W3, \单周期硬布线控制器_1_jal , \单周期硬布线控制器_1_jalr , \单周期硬布线控制器_1_memwrite ,
       \单周期硬布线控制器_1_regwrite ;
  wire [1:0] id_ex_1_p44, id_ex_1_p45, priority_encoder_1_out, R1Forward, R2Forward, \中断号_q ;
  wire [3:0] AluOP, ByteSelect, ex_mem_1_byteselectout, id_ex_1_p40, multiplexer_9_out;
  wire [4:0] EX_W_num, ID_Funct, ID_R1_num, ID_R2_num, MEM_W_num, multiplexer_10_out, W_num;
  wire [11:0] id_ex_1_p52, id_ex_1_p53, multiplexer_8_out, shifter_1_out;
  wire [12:0] CNT_num;
  wire [15:0] \LoadUse次数 , \总周期数 , \插入气泡数 , \无条件分支数 , \条件分支成功数 ;
  wire [19:0] shifter_2_out;
  wire [31:0] adder_1_out, adder_4_out, bit_extender_1_out, bit_extender_2_out, bit_extender_3_out, BPC, EPC,
       EX_IR, EX_R1, EX_R2, EX_Result, id_ex_1_p46, id_ex_1_p47, id_ex_1_p55, id_ex_1_p59, ID_IR, IF_IR,
       InterAddr, JPC, MEM_F, MEM_IR, mem_wb_1_memdateout, mem_wb_1_resultout, mips_ram_1_p8,
       multiplexer_1_out, multiplexer_2_out, multiplexer_3_out, multiplexer_4_out, multiplexer_13_out,
       multiplexer_15_out, multiplexer_16_out, multiplexer_19_out, multiplexer_20_out, PCin, R1, R2,
       shifter_3_out, WB_IR;

  Button \u_总复位  (.out(RST));
  Button _1 (.out(IR1));
  Button _2 (.out(IR2));
  Button _3 (.out(IR3));
  // Probe on \总周期数 
  // Probe on \总周期数 
  Button \u_继续运行  (.out(Go));
  LED #(.active("true")) led_1 (.in(W1));
  LED #(.active("true")) led_2 (.in(W2));
  LED #(.active("true")) led_3 (.in(W3));
  Hex_Digit_Display hex_digit_display_1 (.value(LedData[31:28]));  // open: dp
  // Probe on IF_PC[19:0]
  // RiscV_Probe riscv_probe_1: pin names not known; wires that end beside it: IF_IR
  not not_1 (not_1_out, Load_Use);
  and and_1 (and_1_out, not_1_out, en);
  Adder #(.width(32)) adder_1 (.a(IF_PC), .b(32'h4), .out(adder_1_out));  // open: cin, cout
  Multiplexer #(.select(1), .width(32), .disabled("Z"), .enable("false")) multiplexer_1 (
    .in0(adder_1_out), .in1(BPC), .out(multiplexer_1_out), .sel(B));
  Hex_Digit_Display hex_digit_display_2 (.value(LedData[23:20]));  // open: dp
  Hex_Digit_Display hex_digit_display_3 (.value(LedData[27:24]));  // open: dp
  // Probe on ID_PC[19:0]
  // RiscV_Probe riscv_probe_2: pin names not known; wires that end beside it: {ID_IR[31], ID_Funct[4], ID_IR[29:26], ID_Funct[3], ID_IR[24:15], ID_Funct[2:0], ID_IR[11:0]}
  Register #(.width(32), .trigger("rising"), .Select("low")) PC (
    .D(PCin), .en(and_1_out), .Q(IF_PC), .clk(CLK));  // open: clr
  Multiplexer #(.select(1), .width(32), .disabled("Z"), .enable("false")) multiplexer_2 (
    .in0(multiplexer_1_out), .in1(JPC), .out(multiplexer_2_out), .sel(JAL));
  Hex_Digit_Display hex_digit_display_4 (.value(LedData[15:12]));  // open: dp
  Hex_Digit_Display hex_digit_display_5 (.value(LedData[19:16]));  // open: dp
  Multiplexer #(.select(1), .width(32), .disabled("Z"), .enable("false")) multiplexer_3 (
    .in0(multiplexer_2_out), .in1(EX_Result), .out(multiplexer_3_out), .sel(JALR));
  Hex_Digit_Display hex_digit_display_6 (.value(LedData[11:8]));  // open: dp
  Hex_Digit_Display hex_digit_display_7 (.value(LedData[7:4]));  // open: dp
  // Probe on EX_PC[19:0]
  // RiscV_Probe riscv_probe_3: pin names not known; wires that end beside it: EX_IR
  Multiplexer #(.select(1), .width(32), .disabled("Z"), .enable("false")) multiplexer_4 (
    .in0(multiplexer_3_out), .in1(InterAddr), .out(multiplexer_4_out), .sel(Int));
  Multiplexer #(.select(1), .width(32), .disabled("Z"), .enable("false")) multiplexer_5 (
    .in0(multiplexer_4_out), .in1(EPC), .out(PCin), .sel(uret));
  Hex_Digit_Display hex_digit_display_8 (.value(LedData[3:0]));  // open: dp
  not not_2 (not_2_out, halt);
  ROM #(.addrWidth(10), .dataWidth(32), .Select("high")) rom_1 (.addr(IF_PC[11:2]), .data(IF_IR));
  not not_3 (not_3_out, Load_Use);
  and and_2 (and_2_out, not_3_out, en);
  // Probe on \总周期数 
  // Probe on M_PC[19:0]
  // RiscV_Probe riscv_probe_4: pin names not known; wires that end beside it: MEM_IR
  Counter #(.width(16), .max('hffff), .ongoal("wrap"), .trigger("rising"), .behavior("new")) counter_1 (
    .count(not_2_out), .Q(\总周期数 ), .clk(CLK));  // open: load, D, carry, clr, preset, down
  IF_ID if_id_1 (
    .IRin(IF_IR), .PCin(IF_PC), .RST(or_1_out), .EN(and_2_out), .CLK(CLK),
    .IRout({ID_IR[31], ID_Funct[4], ID_IR[29:26], ID_Funct[3], ID_IR[24:15], ID_Funct[2:0], ID_IR[11:0]}),
    .PCout(ID_PC));  // open: PredictJumpin, PredictJumpout
  or or_1 (or_1_out, JALR, uret, JAL, B, Int, RST);
  // Probe on \总周期数 
  // Probe on \无条件分支数 
  // Probe on \条件分支成功数 
  // Probe on \插入气泡数 
  // Probe on \LoadUse次数 
  // Probe on IF_PC[11:0]
  // Probe on WB_PC[19:0]
  // RiscV_Probe riscv_probe_5: pin names not known; wires that end beside it: WB_IR
  // RiscV_Probe riscv_probe_6: pin names not known; wires that end beside it: {ID_IR[31], ID_Funct[4], ID_IR[29:26], ID_Funct[3], ID_IR[24:15], ID_Funct[2:0], ID_IR[11:0]}, {ID_IR[31], ID_Funct[4], ID_IR[29:26], ID_Funct[3], ID_IR[11:7]}
  // Probe on ID_PC[11:0]
  // Probe on EX_PC[11:0]
  // Probe on M_PC[11:0]
  D_Flip_Flop #(.trigger("high"), .Pre_Clr_Positions("LEGACY"), .NegatePresetClear("false"), .enable("true"), .NewFFLayout("false")) d_ff_1 (.Q(d_ff_1_q));  // open: clk, D, Qn, preset, en, reset
  // Probe on 13'hc
  \单周期硬布线控制器  \u_单周期硬布线控制器_1  (
    .Funct(ID_Funct), .OP(ID_IR[6:2]), .ALU_OP(AluOP), .MemToReg(MemToReg),
    .MemWrite(\单周期硬布线控制器_1_memwrite ), .ALU_SRC(AluSrcB), .RegWrite(\单周期硬布线控制器_1_regwrite ), .ecall(ecall),
    .S_type(S_Type), .Jalr(\单周期硬布线控制器_1_jalr ), .Beq(Beq), .JAL(\单周期硬布线控制器_1_jal ), .Bne(Bne),
    .in_3(ID_IR[21]), .uret(uret), .Blt(Blt), .Sb(Sb));  // open: CSRRCI, CSRRSI
  Shifter #(.width(12), .shift("ll")) shifter_1 (
    .in({ID_IR[31], ID_IR[7], ID_Funct[4], ID_IR[29:26], ID_Funct[3], ID_IR[11:8]}), .\dist (4'b0001),
    .out(shifter_1_out));
  Shifter #(.width(20), .shift("ll")) shifter_2 (
    .in({ID_IR[31], ID_IR[19:15], ID_Funct[2:0], ID_IR[20], ID_Funct[4], ID_IR[29:26], ID_Funct[3], ID_IR[24:21]}),
    .\dist (5'b00001), .out(shifter_2_out));
  // Probe on WB_PC[11:0]
  Comparator #(.width(13), .mode("twosComplement")) comparator_1 (
    .a(CNT_num), .b(13'hc), .eq(comparator_1_eq), .lt(comparator_1_lt));  // open: gt
  Clock #(.highDuration(1), .lowDuration(1)) clock_1 (.out(clock_1_out));
  Multiplexer #(.select(1), .width(5), .disabled("Z"), .enable("false")) multiplexer_6 (
    .in0(ID_IR[19:15]), .in1(5'b01010), .out(ID_R1_num), .sel(ecall));
  assign bit_extender_1_out = {{20{shifter_1_out[11]}}, shifter_1_out};  // Bit_Extender bit_extender_1
  assign bit_extender_2_out = {{12{shifter_2_out[19]}}, shifter_2_out};  // Bit_Extender bit_extender_2
  nand nand_1 (nand_1_out, d_ff_1_q, comparator_1_eq);
  Counter #(.width(13), .max('h1fff), .ongoal("stay"), .trigger("rising"), .behavior("old")) counter_2 (
    .count(comparator_1_lt), .Q(CNT_num), .clk(clock_1_out));  // open: load, D, carry, clr, preset
  Multiplexer #(.select(1), .width(5), .disabled("Z"), .enable("false")) multiplexer_7 (
    .in0(ID_IR[24:20]), .in1(5'b10001), .out(ID_R2_num), .sel(ecall));
  assign CLK = nand_1_out ? clock_1_out : 1'bz;  // Controlled_Buffer controlled_buffer_1
  \数据相关检测逻辑_重定向  \u_数据相关检测逻辑_重定向_1  (
    .ID_R1_num(ID_R1_num), .EX_W_num(EX_W_num), .EX_RegWrite(EX_RegWrite), .ID_R2_num(ID_R2_num),
    .MEM_W_num(MEM_W_num), .MEM_RegWrite(MEM_RegWrite), .EX_MemToReg(EX_MemToReg), .OP(ID_IR[6:2]),
    .Funct(ID_Funct), .R1Forward(R1Forward), .DataHazzard(DataHazzard), .R2Forward(R2Forward),
    .Load_Use(Load_Use));
  not not_4 (not_4_out, CLK);
  Regifile regifile_1 (
    .Din(RDin), .Clk(not_4_out), .R1(R1), .R2(R2), .WE(RegWrite), .W_num(W_num), .R1_num(ID_R1_num),
    .R2_num(ID_R2_num));
  Pull_Resistor #(.pull(1)) pull_resistor_1 (.node(CLK));
  // ID_EX id_ex_1: pin names not known; wires that end beside it: id_ex_1_p1, id_ex_1_p2, Sb, id_ex_1_p1, Beq, id_ex_1_p2, Bne, Blt, MemToReg, \单周期硬布线控制器_1_memwrite , AluOP, AluSrcB, \单周期硬布线控制器_1_regwrite , S_Type, R1Forward, R2Forward, R1, R2, ID_IR[11:7], {ID_IR[31], ID_Funct[4], ID_IR[29:26], ID_Funct[3], ID_IR[24:15], ID_Funct[2:0], ID_IR[11:0]}, {ID_IR[31], ID_Funct[4], ID_IR[29:26], ID_Funct[3], ID_IR[24:20]}, {ID_IR[31], ID_Funct[4], ID_IR[29:26], ID_Funct[3], ID_IR[11:7]}, ID_PC, bit_extender_1_out, \单周期硬布线控制器_1_jal , id_ex_1_p26, id_ex_1_p26, bit_extender_2_out, \单周期硬布线控制器_1_jalr , ecall, CLK, en, id_ex_1_p33, id_ex_1_p34, id_ex_1_p35, id_ex_1_p36, id_ex_1_p37, EX_MemToReg, id_ex_1_p39, id_ex_1_p40, id_ex_1_p41, EX_RegWrite, id_ex_1_p43, id_ex_1_p44, id_ex_1_p45, id_ex_1_p46, id_ex_1_p47, id_ex_1_p48, id_ex_1_p48, EX_W_num, EX_IR, id_ex_1_p52, id_ex_1_p53, EX_PC, id_ex_1_p55, JAL, id_ex_1_p57, id_ex_1_p57, id_ex_1_p59, JALR, id_ex_1_p61
  or or_2 (id_ex_1_p33, JALR, uret, JAL, Load_Use, B, Int, RST);
  Multiplexer #(.select(1), .width(12), .disabled("Z"), .enable("false")) multiplexer_8 (
    .in0(id_ex_1_p52), .in1(id_ex_1_p53), .out(multiplexer_8_out), .sel(id_ex_1_p43));
  Multiplexer #(.select(2), .width(4), .disabled("Z"), .enable("false")) multiplexer_9 (
    .in0(4'b0001), .in1(4'b0010), .in2(4'b0100), .in3(4'b1000), .out(multiplexer_9_out), .sel(EX_Result[1:0]));
  Multiplexer #(.select(2), .width(5), .disabled("Z"), .enable("false")) multiplexer_10 (
    .in0({5{1'b0}}), .in1(5'b01000), .in2(5'b10000), .in3(5'b11000), .out(multiplexer_10_out),
    .sel(EX_Result[1:0]));
  not not_5 (not_5_out, equal);
  Multiplexer #(.select(2), .width(32), .disabled("Z"), .enable("false")) multiplexer_11 (
    .in0(id_ex_1_p46), .in1(RDin), .in2(MEM_F), .out(EX_R1), .sel(id_ex_1_p44));  // open: in3
  Multiplexer #(.select(2), .width(32), .disabled("Z"), .enable("false")) multiplexer_12 (
    .in0(id_ex_1_p47), .in1(RDin), .in2(MEM_F), .out(EX_R2), .sel(id_ex_1_p45));  // open: in3
  Multiplexer #(.select(1), .width(32), .disabled("Z"), .enable("false")) multiplexer_13 (
    .in0(EX_R2), .in1(bit_extender_3_out), .out(multiplexer_13_out), .sel(id_ex_1_p41));
  assign bit_extender_3_out = {{20{multiplexer_8_out[11]}}, multiplexer_8_out};  // Bit_Extender bit_extender_3
  Multiplexer #(.select(1), .width(4), .disabled("Z"), .enable("false")) multiplexer_14 (
    .in0(4'b1111), .in1(multiplexer_9_out), .out(ByteSelect), .sel(id_ex_1_p34));
  and and_3 (and_3_out, id_ex_1_p35, equal);
  and and_4 (and_4_out, not_5_out, id_ex_1_p36);
  and and_5 (and_5_out, less, id_ex_1_p37);
  ALU alu_1 (
    .X(EX_R1), .Y(multiplexer_13_out), .AluOP(id_ex_1_p40), .Equal(equal), .Result(EX_Result), .out_6(less));  // open: Result_2, out_4
  Adder #(.width(32)) adder_2 (.a(EX_PC), .b(id_ex_1_p55), .out(BPC));  // open: cin, cout
  Adder #(.width(32)) adder_3 (.a(EX_PC), .b(id_ex_1_p59), .out(JPC));  // open: cin, cout
  and and_6 (and_6_out, id_ex_1_p61, not_6_out);
  not not_6 (not_6_out, comparator_2_eq);
  Comparator #(.width(32), .mode("twosComplement")) comparator_2 (
    .a(EX_R2), .b(32'h22), .eq(comparator_2_eq));  // open: gt, lt
  Comparator #(.width(32), .mode("twosComplement")) comparator_3 (
    .a(EX_R2), .b(32'h22), .eq(comparator_3_eq));  // open: gt, lt
  or or_3 (W1, IR1_q, d_ff_2_q);
  or or_4 (W2, IR2_q, d_ff_3_q);
  or or_5 (W3, IR3_q, d_ff_4_q);
  Shifter #(.width(32), .shift("ll")) shifter_3 (.in(EX_R2), .\dist (multiplexer_10_out), .out(shifter_3_out));
  or or_6 (B, and_3_out, and_4_out, and_5_out);
  and and_7 (and_7_out, id_ex_1_p61, comparator_3_eq);
  D_Flip_Flop #(.trigger("rising"), .Pre_Clr_Positions("LEGACY"), .NegatePresetClear("false"), .enable("true"), .NewFFLayout("false")) d_ff_2 (
    .clk(IR1), .D(1'b1), .Q(d_ff_2_q), .reset(IR1_q));  // open: Qn, preset, en
  D_Flip_Flop #(.trigger("rising"), .Pre_Clr_Positions("LEGACY"), .NegatePresetClear("false"), .enable("true"), .NewFFLayout("false")) d_ff_3 (
    .clk(IR2), .D(1'b1), .Q(d_ff_3_q), .reset(IR2_q));  // open: Qn, preset, en
  D_Flip_Flop #(.trigger("rising"), .Pre_Clr_Positions("LEGACY"), .NegatePresetClear("false"), .enable("true"), .NewFFLayout("false")) d_ff_4 (
    .clk(IR3), .D(1'b1), .Q(d_ff_4_q), .reset(IR3_q));  // open: Qn, preset, en
  Multiplexer #(.select(1), .width(32), .disabled("Z"), .enable("false")) multiplexer_15 (
    .in0(EX_R2), .in1(shifter_3_out), .out(multiplexer_15_out), .sel(id_ex_1_p34));
  or or_7 (or_7_out, JAL, JALR);
  Register #(.width(32), .trigger("rising"), .Select("low")) register_1 (
    .D(EX_R1), .en(and_7_out), .Q(LedData), .clk(CLK));  // open: clr
  or or_8 (or_8_out, d_ff_2_q, IR1_q);
  or or_9 (or_9_out, d_ff_3_q, IR2_q);
  or or_10 (or_10_out, d_ff_4_q, IR3_q);
  EX_MEM ex_mem_1 (
    .MemToRegin(EX_MemToReg), .MemWritein(id_ex_1_p39), .Jin(or_7_out), .RegWritein(EX_RegWrite),
    .ByteSelectin(ByteSelect), .MDin(multiplexer_15_out), .W_in(EX_W_num), .PCin(EX_PC),
    .MemToRegout(ex_mem_1_memtoregout), .MemWriteout(MemWrite), .Jout(ex_mem_1_jout),
    .RegWriteout(MEM_RegWrite), .ByteSelectout(ex_mem_1_byteselectout), .MDout(MDin), .W_out(MEM_W_num),
    .PCout(M_PC), .RST(RST), .EN_H(en), .CLK(CLK), .Resultin(EX_Result), .Rrsultout(MEM_F), .IRin(EX_IR),
    .IRout(MEM_IR), .Haltout(ex_mem_1_haltout), .Haltin(and_6_out));
  and and_8 (and_8_out, or_8_out, ~Ret1);  // AND_Gate
  and and_9 (and_9_out, or_9_out, ~Ret2);  // AND_Gate
  and and_10 (and_10_out, or_10_out, ~Ret3);  // AND_Gate
  D_Flip_Flop #(.trigger("rising"), .Pre_Clr_Positions("LEGACY"), .NegatePresetClear("false"), .enable("true"), .NewFFLayout("false")) u_IR1 (
    .clk(CLK), .D(and_8_out), .Q(IR1_q));  // open: Qn, preset, en, reset
  D_Flip_Flop #(.trigger("rising"), .Pre_Clr_Positions("LEGACY"), .NegatePresetClear("false"), .enable("true"), .NewFFLayout("false")) u_IR2 (
    .clk(CLK), .D(and_9_out), .Q(IR2_q));  // open: Qn, preset, en, reset
  D_Flip_Flop #(.trigger("rising"), .Pre_Clr_Positions("LEGACY"), .NegatePresetClear("false"), .enable("true"), .NewFFLayout("false")) u_IR3 (
    .clk(CLK), .D(and_10_out), .Q(IR3_q));  // open: Qn, preset, en, reset
  not not_7 (not_7_out, MemWrite);
  and and_11 (Int, IE, Intq);
  // MIPS_RAM mips_ram_1: pin names not known; wires that end beside it: MEM_F[11:2], MDin, MemWrite, ex_mem_1_byteselectout, CLK, not_7_out, MemWrite, mips_ram_1_p8
  Priority_Encoder #(.select(2), .disabled("Z")) priority_encoder_1 (
    .in1(IR1_q), .in2(IR2_q), .in3(IR3_q), .out(priority_encoder_1_out), .gs(Intq));  // open: in0, en_out, en_in
  D_Flip_Flop #(.trigger("rising"), .Pre_Clr_Positions("LEGACY"), .NegatePresetClear("false"), .enable("true"), .NewFFLayout("false")) u_IE (
    .clk(CLK), .D(Int), .Qn(IE), .en(or_11_out));  // open: Q, preset, reset
  or or_11 (or_11_out, Int, uret);
  MEM_WB mem_wb_1 (
    .MemToRegin(ex_mem_1_memtoregout), .Jin(ex_mem_1_jout), .RegWritein(MEM_RegWrite), .W_in(MEM_W_num),
    .IRin(MEM_IR), .PCin(M_PC), .MemToRegout(mem_wb_1_memtoregout), .Jout(J), .RegWriteout(RegWrite),
    .W_out(W_num), .IRout(WB_IR), .PCout(WB_PC), .RST(RST), .EN_H(en), .CLK(CLK), .Memdatein(mips_ram_1_p8),
    .Memdateout(mem_wb_1_memdateout), .Resultin(MEM_F), .Resultout(mem_wb_1_resultout),
    .Haltin(ex_mem_1_haltout), .Haltout(mem_wb_1_haltout));
  Multiplexer #(.select(1), .width(32), .disabled("Z"), .enable("false")) multiplexer_16 (
    .in0(mem_wb_1_resultout), .in1(mem_wb_1_memdateout), .out(multiplexer_16_out), .sel(mem_wb_1_memtoregout));
  and and_12 (halt, mem_wb_1_haltout, ~Go);  // AND_Gate
  not not_8 (en, halt);
  Multiplexer #(.select(2), .width(32), .disabled("Z"), .enable("false")) multiplexer_17 (
    .in1(32'h30ac), .in2(32'h3150), .in3(32'h31f4), .out(InterAddr), .sel(priority_encoder_1_out));  // open: in0
  Register #(.width(2), .trigger("rising"), .Select("low")) \u_中断号  (
    .D(priority_encoder_1_out), .en(Int), .Q(\中断号_q ), .clk(CLK));  // open: clr
  Multiplexer #(.select(1), .width(32), .disabled("Z"), .enable("false")) multiplexer_18 (
    .in0(multiplexer_16_out), .in1(adder_4_out), .out(RDin), .sel(J));
  Adder #(.width(32)) adder_4 (.a(32'h4), .b(WB_PC), .out(adder_4_out));  // open: cin, cout
  Decoder #(.select(2), .tristate("false"), .disabled("Z"), .enable("false")) decoder_1 (
    .out1(decoder_1_out1), .out2(decoder_1_out2), .out3(decoder_1_out3), .sel(\中断号_q ));  // open: out0
  Comparator #(.width(32), .mode("twosComplement")) comparator_4 (
    .a(ID_PC), .b({32{1'b0}}), .eq(comparator_4_eq));  // open: gt, lt
  Multiplexer #(.select(1), .width(32), .disabled("Z"), .enable("false")) multiplexer_19 (
    .in0(ID_PC), .in1(IF_PC), .out(multiplexer_19_out), .sel(Bubble2));
  and and_13 (Ret1, uret, decoder_1_out1);
  and and_14 (Ret2, decoder_1_out2, uret);
  and and_15 (Ret3, uret, decoder_1_out3);
  Comparator #(.width(32), .mode("twosComplement")) comparator_5 (
    .a(EX_PC), .b({32{1'b0}}), .eq(comparator_5_eq));  // open: gt, lt
  not not_9 (Bubble1, comparator_5_eq);
  not not_10 (Bubble2, comparator_4_eq);
  Multiplexer #(.select(1), .width(32), .disabled("Z"), .enable("false")) multiplexer_20 (
    .in0(EX_PC), .in1(multiplexer_19_out), .out(multiplexer_20_out), .sel(Bubble1));
  Register #(.width(32), .trigger("rising"), .Select("low")) u_EPC (
    .D(multiplexer_20_out), .en(Int), .Q(EPC), .clk(CLK));  // open: clr

  // Other names for the same wires on the sheet: IR[31:0] = {ID_IR[31], ID_Funct[4], ID_IR[29:26], ID_Funct[3], ID_IR[24:15], ID_Funct[2:0], ID_IR[11:0]};
  //   ID_IR (some bits) = ID_Funct; ID_OP[4:0] = ID_IR[6:2]; MEM_PC[31:0] = M_PC; WB_F[31:0] = RDin

  // Notes on the sheet:
  //   中断源
  //   时空图监测，可删除
  //   中断等待指示
  //   数码管输出
  //   指令存储器
  //   IR
  //   contents of rom_1 (hex, n*v repeats v):
  //   7d000113 100413 1f41993 41f9d993 433 c00913 800b13 140413 f47413 800293 100313 499993 89e9b3 1300533
  //   2200893 73 406282b3 fe0294e3 140413 f00f93 1f47433 1c41413 800293 100313 49d993 89e9b3 1300533
  //   2200893 73 406282b3 fe0294e3 1c45413 406b0b33 b0463 f95ff06f 2b3 fff2c293 1029293 fff2e293 500533
  //   2200893 73 f5dff06f 1112023 410113 a12023 410113 812023 410113 1312023 410113 1412023 410113 1512023
  //   410113 1612023 410113 100b13 300a13 100a93 1600433 441413 14469b3 1300533 2200893 73 fe0416e3
  //   415a0a33 fe0a10e3 ffc10113 12b03 ffc10113 12a83 ffc10113 12a03 ffc10113 12983 ffc10113 12403
  //   ffc10113 12503 ffc10113 12883 200073 1112023 410113 a12023 410113 812023 410113 1312023 410113
  //   1412023 410113 1512023 410113 1612023 410113 200b13 300a13 100a93 1600433 441413 14469b3 1300533
  //   2200893 73 fe0416e3 415a0a33 fe0a10e3 ffc10113 12b03 ffc10113 12a83 ffc10113 12a03 ffc10113 12983
  //   ffc10113 12403 ffc10113 12503 ffc10113 12883 200073 1112023 410113 a12023 410113 812023 410113
  //   1312023 410113 1412023 410113 1512023 410113 1612023 410113 300b13 300a13 100a93 1600433 441413
  //   14469b3 1300533 2200893 73 fe0416e3 415a0a33 fe0a10e3 ffc10113 12b03 ffc10113 12a83 ffc10113 12a03
  //   ffc10113 12983 ffc10113 12403 ffc10113 12503 ffc10113 12883 200073
  //   PC
  //   指令探针
  //   控制位
  //   JAL
  //   JALR
  //   URET
  //   func
  //   rs1
  //   rs2
  //   指令字
  //   rd
  //   I型imm
  //   s型imm
  //   b型imm
  //   j型imm
  //   流水调试日志用
  //   暂停节拍，不能为0
  //   Beq
  //   Bne
  //   Blt
  //   AluOP
  //   AluSrcB
  //   RegWrite
  //   S_Type
  //   戳工具置1进入计数暂停模式，ctrl+k时钟自动运行到对应节拍暂停
  //   ctrl+k关闭时钟连续运行，将控制位置零，进入单步调试模式调试
  //   MemWrite
  //   可计数暂停的时钟源
  //   为方便自动评测，需要输出流水线各段保存的PC值，注意是PC不是PC+4，另外ID段寄存器写入信息，Mem段内存写入信息也要输出
  //   Reset 
  //   Reset 
  //   Reset 
  //   数据存储器
endmodule

module \数据相关检测逻辑_重定向  (
  input  [4:0] ID_R1_num,
  input  [4:0] EX_W_num,
  input  EX_RegWrite,
  input  [4:0] ID_R2_num,
  input  [4:0] MEM_W_num,
  input  MEM_RegWrite,
  input  EX_MemToReg,
  input  [4:0] OP,
  input  [4:0] Funct,
  output [1:0] R1Forward,
  output DataHazzard,
  output [1:0] R2Forward,
  output Load_Use
);

  wire and_1_out, and_2_out, and_4_out, and_5_out, and_6_out, and_7_out, and_8_out, and_9_out, and_10_out,
       and_11_out, and_12_out, and_13_out, comparator_1_eq, comparator_2_eq, comparator_3_eq,
       comparator_4_eq, comparator_5_eq, comparator_6_eq, comparator_7_eq, comparator_8_eq, comparator_9_eq,
       comparator_10_eq, comparator_11_eq, comparator_12_eq, or_1_out, or_2_out, or_3_out, R1Used, R2Used;

  Comparator #(.width(5), .mode("twosComplement")) comparator_1 (
    .a({5{1'b0}}), .b(ID_R2_num), .eq(comparator_1_eq));  // open: gt, lt
  Comparator #(.width(5), .mode("twosComplement")) comparator_2 (
    .a(ID_R2_num), .b(EX_W_num), .eq(comparator_2_eq));  // open: gt, lt
  Comparator #(.width(5), .mode("twosComplement")) comparator_3 (
    .a(EX_W_num), .b(ID_R2_num), .eq(comparator_3_eq));  // open: gt, lt
  Comparator #(.width(5), .mode("twosComplement")) comparator_4 (
    .a(ID_R2_num), .b({5{1'b0}}), .eq(comparator_4_eq));  // open: gt, lt
  \寄存器有效逻辑  \u_寄存器有效逻辑_1  (
    .OP2(OP[0]), .OP3(OP[1]), .OP4(OP[2]), .OP5(OP[3]), .OP6(OP[4]), .F12(Funct[0]), .F13(Funct[1]),
    .F14(Funct[2]), .F25(Funct[3]), .F30(Funct[4]), .R1(R1Used), .R2(R2Used));
  and and_1 (and_1_out, ~comparator_1_eq, comparator_2_eq, R1Used);  // AND_Gate
  and and_2 (and_2_out, R2Used, comparator_3_eq, ~comparator_4_eq);  // AND_Gate
  or or_1 (or_1_out, and_1_out, and_2_out);
  Comparator #(.width(5), .mode("twosComplement")) comparator_5 (
    .a(ID_R1_num), .b(EX_W_num), .eq(comparator_5_eq));  // open: gt, lt
  Comparator #(.width(5), .mode("twosComplement")) comparator_6 (
    .a(ID_R1_num), .b({5{1'b0}}), .eq(comparator_6_eq));  // open: gt, lt
  Comparator #(.width(5), .mode("twosComplement")) comparator_7 (
    .a(ID_R2_num), .b(EX_W_num), .eq(comparator_7_eq));  // open: gt, lt
  Comparator #(.width(5), .mode("twosComplement")) comparator_8 (
    .a(ID_R2_num), .b({5{1'b0}}), .eq(comparator_8_eq));  // open: gt, lt
  and and_3 (Load_Use, or_1_out, EX_MemToReg);
  and and_4 (and_4_out, comparator_5_eq, EX_RegWrite, ~comparator_6_eq);  // AND_Gate
  and and_5 (and_5_out, comparator_7_eq, EX_RegWrite, ~comparator_8_eq);  // AND_Gate
  Comparator #(.width(5), .mode("twosComplement")) comparator_9 (
    .a(ID_R1_num), .b(MEM_W_num), .eq(comparator_9_eq));  // open: gt, lt
  Comparator #(.width(5), .mode("twosComplement")) comparator_10 (
    .a(ID_R1_num), .b({5{1'b0}}), .eq(comparator_10_eq));  // open: gt, lt
  Comparator #(.width(5), .mode("twosComplement")) comparator_11 (
    .a(ID_R2_num), .b(MEM_W_num), .eq(comparator_11_eq));  // open: gt, lt
  Comparator #(.width(5), .mode("twosComplement")) comparator_12 (
    .a(ID_R2_num), .b({5{1'b0}}), .eq(comparator_12_eq));  // open: gt, lt
  and and_6 (and_6_out, comparator_9_eq, MEM_RegWrite, ~comparator_10_eq);  // AND_Gate
  and and_7 (and_7_out, comparator_11_eq, MEM_RegWrite, ~comparator_12_eq);  // AND_Gate
  and and_8 (and_8_out, R1Used, and_6_out);
  and and_9 (and_9_out, R1Used, and_4_out);
  or or_2 (or_2_out, and_6_out, and_4_out);
  and and_10 (and_10_out, or_2_out, R1Used);
  and and_11 (and_11_out, R2Used, or_3_out);
  or or_3 (or_3_out, and_5_out, and_7_out);
  and and_12 (and_12_out, R2Used, and_7_out);
  and and_13 (and_13_out, R2Used, and_5_out);
  Priority_Encoder #(.select(2), .disabled("Z")) priority_encoder_1 (
    .in0(1'b1), .in1(and_8_out), .in2(and_9_out), .out(R1Forward));  // open: in3, gs, en_out, en_in
  or or_4 (DataHazzard, and_10_out, and_11_out);
  Priority_Encoder #(.select(2), .disabled("Z")) priority_encoder_2 (
    .in0(1'b1), .in1(and_12_out), .in2(and_13_out), .out(R2Forward));  // open: in3, gs, en_out, en_in
endmodule
// BTB
module \动态分支预测  (
  output RegWrite,
  output MemWrite,
  output [31:0] IF_PC,
  output [31:0] ID_PC,
  output [31:0] EX_PC,
  output [31:0] M_PC,
  output [31:0] WB_PC,
  output [31:0] RDin,
  output [31:0] MDin,
  output [31:0] LedData
);

  wire AluSrcB, and_1_out, and_2_out, and_3_out, and_4_out, and_5_out, and_6_out, and_7_out, and_8_out, B,
       Beq, Blt, Bne, Branch, BranchTaken, CLK, clock_1_out, comparator_1_eq, comparator_2_eq,
       comparator_2_lt, comparator_3_eq, comparator_4_eq, d_ff_1_q, DataHazzard, ecall, en, equal,
       ex_mem_1_haltout, ex_mem_1_jout, ex_mem_1_memtoregout, EX_MemToReg, EX_PredictErr, EX_PredictJump,
       EX_RegWrite, Go, halt, id_ex_1_alusrcbout, id_ex_1_beqout, id_ex_1_bltout, id_ex_1_bneout,
       id_ex_1_haltout, id_ex_1_memwriteout, id_ex_1_s_typeout, id_ex_1_sbout, if_id_1_predictjumpout, IR1,
       IR2, IR3, J, JAL, JALR, less, Load_Use, MEM_RegWrite, mem_wb_1_haltout, mem_wb_1_memtoregout,
       MemToReg, mips_ram_1_p6, nand_1_out, not_1_out, not_2_out, not_3_out, not_4_out, not_6_out, not_7_out,
       not_8_out, or_1_out, or_2_out, or_5_out, or_7_out, PredictJump, riscv_probe_5_p3, RST, S_Type, Sb, W1,
       W2, W3, \单周期硬布线控制器_1_jal , \单周期硬布线控制器_1_jalr , \单周期硬布线控制器_1_memwrite , \单周期硬布线控制器_1_regwrite ;
  wire [1:0] id_ex_1_r1forwardout, id_ex_1_r2forwardout, R1Forward, R2Forward;
  wire [3:0] AluOP, ByteSelect, ex_mem_1_byteselectout, id_ex_1_aluopout, multiplexer_10_out;
  wire [4:0] EX_W_num, ID_Funct, ID_R1_num, ID_R2_num, MEM_W_num, multiplexer_11_out, W_num;
  wire [11:0] id_ex_1_imm_i_out, id_ex_1_imm_s_out, multiplexer_9_out, shifter_2_out;
  wire [12:0] CNT_num;
  wire [15:0] adder_1_out, \LoadUse次数 , shifter_1_out, \总周期数 , \插入气泡数 , \无条件分支数 , \条件分支成功数 ;
  wire [19:0] shifter_3_out;
  wire [31:0] adder_2_out, adder_3_out, adder_7_out, bit_extender_1_out, bit_extender_2_out,
       bit_extender_3_out, BPC, BranchAddr, EX_IR, EX_R1, EX_R2, EX_Result, id_ex_1_imm_b_out,
       id_ex_1_imm_j_out, id_ex_1_r1out, id_ex_1_r2out, ID_IR, IF_IR, JPC, JumpAddr, MEM_F, MEM_IR,
       mem_wb_1_memdateout, mem_wb_1_resultout, mips_ram_1_p8, multiplexer_1_out, multiplexer_2_out,
       multiplexer_4_out, multiplexer_5_out, multiplexer_15_out, multiplexer_16_out, multiplexer_17_out,
       PCin, R1, R2, shifter_4_out, WB_IR;

  Button \u_总复位  (.out(RST));
  Button _1 (.out(IR1));
  Button _2 (.out(IR2));
  Button _3 (.out(IR3));
  // Probe on \总周期数 
  // Probe on \总周期数 
  not not_1 (not_1_out, halt);
  Button \u_继续运行  (.out(Go));
  LED #(.active("true")) led_1 (.in(W1));
  LED #(.active("true")) led_2 (.in(W2));
  LED #(.active("true")) led_3 (.in(W3));
  Counter #(.width(16), .max('hffff), .ongoal("wrap"), .trigger("rising"), .behavior("new")) counter_1 (
    .count(not_1_out), .Q(\总周期数 ), .clk(CLK));  // open: load, D, carry, clr, preset, down
  not not_2 (not_2_out, Load_Use);
  Multiplexer #(.select(1), .width(32), .disabled("Z"), .enable("false")) multiplexer_1 (
    .in1(BPC), .out(multiplexer_1_out), .sel(B));  // open: in0
  Hex_Digit_Display hex_digit_display_1 (.value(LedData[31:28]));  // open: dp
  // Probe on IF_PC[19:0]
  // RiscV_Probe riscv_probe_1: pin names not known; wires that end beside it: IF_IR
  Counter #(.width(16), .max('hffff), .ongoal("wrap"), .trigger("rising"), .behavior("new")) counter_2 (
    .count(B), .Q(\条件分支成功数 ), .clk(CLK), .clr(RST));  // open: load, D, carry, preset, down
  Adder #(.width(16)) adder_1 (.a(\条件分支成功数 ), .b(\无条件分支数 ), .out(adder_1_out));  // open: cin, cout
  not not_3 (not_3_out, halt);
  and and_1 (and_1_out, not_3_out, Load_Use);
  Register #(.width(32), .trigger("rising"), .Select("low")) PC (
    .D(PCin), .en(and_2_out), .Q(IF_PC), .clk(CLK));  // open: clr
  and and_2 (and_2_out, not_2_out, en);
  Multiplexer #(.select(1), .width(32), .disabled("Z"), .enable("false")) multiplexer_2 (
    .in0(multiplexer_1_out), .in1(JPC), .out(multiplexer_2_out), .sel(JAL));
  Hex_Digit_Display hex_digit_display_2 (.value(LedData[27:24]));  // open: dp
  Hex_Digit_Display hex_digit_display_3 (.value(LedData[23:20]));  // open: dp
  // Probe on ID_PC[19:0]
  // RiscV_Probe riscv_probe_2: pin names not known; wires that end beside it: {ID_IR[31], ID_Funct[4], ID_IR[29:26], ID_Funct[3], ID_IR[24:15], ID_Funct[2:0], ID_IR[11:0]}
  Shifter #(.width(16), .shift("ll")) shifter_1 (.in(adder_1_out), .\dist (4'b0001), .out(shifter_1_out));
  Counter #(.width(16), .max('hffff), .ongoal("wrap"), .trigger("rising"), .behavior("new")) counter_3 (
    .count(and_1_out), .Q(\LoadUse次数 ), .clk(CLK), .clr(RST));  // open: load, D, carry, preset, down
  Adder #(.width(32)) adder_2 (.a(IF_PC), .b(32'h4), .out(adder_2_out));  // open: cin, cout
  Adder #(.width(32)) adder_3 (.a(EX_PC), .b(32'h4), .out(adder_3_out));  // open: cin, cout
  Multiplexer #(.select(1), .width(32), .disabled("Z"), .enable("false")) multiplexer_3 (
    .in0(multiplexer_2_out), .in1(EX_Result), .out(BranchAddr), .sel(JALR));
  Hex_Digit_Display hex_digit_display_4 (.value(LedData[19:16]));  // open: dp
  Hex_Digit_Display hex_digit_display_5 (.value(LedData[15:12]));  // open: dp
  or or_1 (or_1_out, JAL, JALR);
  Adder #(.width(16)) adder_4 (.a(shifter_1_out), .b(\LoadUse次数 ), .out(\插入气泡数 ));  // open: cin, cout
  Multiplexer #(.select(1), .width(32), .disabled("Z"), .enable("false")) multiplexer_4 (
    .in0(adder_2_out), .in1(JumpAddr), .out(multiplexer_4_out), .sel(PredictJump));
  Multiplexer #(.select(1), .width(32), .disabled("Z"), .enable("false")) multiplexer_5 (
    .in0(adder_3_out), .in1(BranchAddr), .out(multiplexer_5_out), .sel(BranchTaken));
  Hex_Digit_Display hex_digit_display_6 (.value(LedData[11:8]));  // open: dp
  Hex_Digit_Display hex_digit_display_7 (.value(LedData[7:4]));  // open: dp
  // Probe on EX_PC[19:0]
  // RiscV_Probe riscv_probe_3: pin names not known; wires that end beside it: EX_IR, RST
  Counter #(.width(16), .max('hffff), .ongoal("wrap"), .trigger("rising"), .behavior("new")) counter_4 (
    .count(or_1_out), .Q(\无条件分支数 ), .clk(CLK), .clr(RST));  // open: load, D, carry, preset, down
  ROM #(.addrWidth(10), .dataWidth(32), .Select("high")) rom_1 (.addr(IF_PC[11:2]), .data(IF_IR));
  \BTB表  \btb表_1  (
    .CLK(CLK), .EX_Branch(BranchTaken), .EX_PC(EX_PC), .EX_BranchAddr(BranchAddr), .PC(IF_PC),
    .EX_BranchTaken(Branch), .PredictJump(PredictJump), .JumpAddr(JumpAddr));
  Multiplexer #(.select(1), .width(32), .disabled("Z"), .enable("false")) multiplexer_6 (
    .in0(multiplexer_4_out), .in1(multiplexer_5_out), .out(PCin), .sel(EX_PredictErr));
  not not_4 (not_4_out, Load_Use);
  and and_3 (and_3_out, not_4_out, en);
  Hex_Digit_Display hex_digit_display_8 (.value(LedData[3:0]));  // open: dp
  IF_ID if_id_1 (
    .IRin(IF_IR), .PCin(IF_PC), .RST(or_2_out), .EN(and_3_out), .CLK(CLK),
    .IRout({ID_IR[31], ID_Funct[4], ID_IR[29:26], ID_Funct[3], ID_IR[24:15], ID_Funct[2:0], ID_IR[11:0]}),
    .PCout(ID_PC), .PredictJumpin(PredictJump), .PredictJumpout(if_id_1_predictjumpout));
  or or_2 (or_2_out, EX_PredictErr, RST);
  // Probe on \总周期数 
  // Probe on M_PC[19:0]
  // RiscV_Probe riscv_probe_4: pin names not known; wires that end beside it: MEM_IR
  // Probe on \总周期数 
  // Probe on \无条件分支数 
  // Probe on \条件分支成功数 
  // Probe on \插入气泡数 
  // Probe on \LoadUse次数 
  // RiscV_Probe riscv_probe_5: pin names not known; wires that end beside it: {ID_IR[31], ID_Funct[4], ID_IR[29:26], ID_Funct[3], ID_IR[24:15], ID_Funct[2:0], ID_IR[11:0]}, {ID_IR[31], ID_Funct[4], ID_IR[29:26], ID_Funct[3], ID_IR[11:7]}, riscv_probe_5_p3
  // Probe on IF_PC[11:0]
  // Probe on WB_PC[19:0]
  // RiscV_Probe riscv_probe_6: pin names not known; wires that end beside it: WB_IR
  Comparator #(.width(1), .mode("twosComplement")) comparator_1 (
    .a(BranchTaken), .b(EX_PredictJump), .eq(comparator_1_eq));  // open: gt, lt
  not not_5 (EX_PredictErr, comparator_1_eq);
  // Probe on ID_PC[11:0]
  // Probe on EX_PC[11:0]
  \单周期硬布线控制器  \u_单周期硬布线控制器_1  (
    .Funct(ID_Funct), .OP(ID_IR[6:2]), .ALU_OP(AluOP), .MemToReg(MemToReg),
    .MemWrite(\单周期硬布线控制器_1_memwrite ), .ALU_SRC(AluSrcB), .RegWrite(\单周期硬布线控制器_1_regwrite ), .ecall(ecall),
    .S_type(S_Type), .Jalr(\单周期硬布线控制器_1_jalr ), .Beq(Beq), .JAL(\单周期硬布线控制器_1_jal ), .Bne(Bne),
    .in_3(ID_IR[21]), .uret(riscv_probe_5_p3), .Blt(Blt), .Sb(Sb));  // open: CSRRCI, CSRRSI
  // Probe on M_PC[11:0]
  D_Flip_Flop #(.trigger("high"), .Pre_Clr_Positions("LEGACY"), .NegatePresetClear("false"), .enable("true"), .NewFFLayout("false")) d_ff_1 (.Q(d_ff_1_q));  // open: clk, D, Qn, preset, en, reset
  // Probe on 13'hc
  assign bit_extender_1_out = {{20{shifter_2_out[11]}}, shifter_2_out};  // Bit_Extender bit_extender_1
  Shifter #(.width(12), .shift("ll")) shifter_2 (
    .in({ID_IR[31], ID_IR[7], ID_Funct[4], ID_IR[29:26], ID_Funct[3], ID_IR[11:8]}), .\dist (4'b0001),
    .out(shifter_2_out));
  assign bit_extender_2_out = {{12{shifter_3_out[19]}}, shifter_3_out};  // Bit_Extender bit_extender_2
  Shifter #(.width(20), .shift("ll")) shifter_3 (
    .in({ID_IR[31], ID_IR[19:15], ID_Funct[2:0], ID_IR[20], ID_Funct[4], ID_IR[29:26], ID_Funct[3], ID_IR[24:21]}),
    .\dist (5'b00001), .out(shifter_3_out));
  \数据相关检测逻辑_重定向  \u_数据相关检测逻辑_重定向_1  (
    .ID_R1_num(ID_R1_num), .EX_W_num(EX_W_num), .EX_RegWrite(EX_RegWrite), .ID_R2_num(ID_R2_num),
    .MEM_W_num(MEM_W_num), .MEM_RegWrite(MEM_RegWrite), .EX_MemToReg(EX_MemToReg), .OP(ID_IR[6:2]),
    .Funct(ID_Funct), .R1Forward(R1Forward), .DataHazzard(DataHazzard), .R2Forward(R2Forward),
    .Load_Use(Load_Use));
  // Probe on WB_PC[11:0]
  Comparator #(.width(13), .mode("twosComplement")) comparator_2 (
    .a(CNT_num), .b(13'hc), .eq(comparator_2_eq), .lt(comparator_2_lt));  // open: gt
  Clock #(.highDuration(1), .lowDuration(1)) clock_1 (.out(clock_1_out));
  Multiplexer #(.select(1), .width(5), .disabled("Z"), .enable("false")) multiplexer_7 (
    .in0(ID_IR[19:15]), .in1(5'b01010), .out(ID_R1_num), .sel(ecall));
  Multiplexer #(.select(1), .width(5), .disabled("Z"), .enable("false")) multiplexer_8 (
    .in0(ID_IR[24:20]), .in1(5'b10001), .out(ID_R2_num), .sel(ecall));
  nand nand_1 (nand_1_out, d_ff_1_q, comparator_2_eq);
  Counter #(.width(13), .max('h1fff), .ongoal("stay"), .trigger("rising"), .behavior("old")) counter_5 (
    .count(comparator_2_lt), .Q(CNT_num), .clk(clock_1_out));  // open: load, D, carry, clr, preset
  not not_6 (not_6_out, CLK);
  assign CLK = nand_1_out ? clock_1_out : 1'bz;  // Controlled_Buffer controlled_buffer_1
  or or_3 (BranchTaken, JALR, JAL, B);
  Regifile regifile_1 (
    .Din(RDin), .Clk(not_6_out), .R1(R1), .R2(R2), .WE(RegWrite), .W_num(W_num), .R1_num(ID_R1_num),
    .R2_num(ID_R2_num));
  Pull_Resistor #(.pull(1)) pull_resistor_1 (.node(CLK));
  or or_4 (Branch, JALR, JAL, id_ex_1_bneout, id_ex_1_beqout, id_ex_1_bltout);
  ID_EX id_ex_1 (
    .MemToRegin(MemToReg), .MemWritein(\单周期硬布线控制器_1_memwrite ), .AluSrcBin(AluSrcB),
    .RegWritein(\单周期硬布线控制器_1_regwrite ), .S_typein(S_Type), .W_in(ID_IR[11:7]), .MemToRegout(EX_MemToReg),
    .MemWriteout(id_ex_1_memwriteout), .AluSrcBout(id_ex_1_alusrcbout), .RegWriteout(EX_RegWrite),
    .S_Typeout(id_ex_1_s_typeout), .W_out(EX_W_num), .CLK(CLK), .EN_H(en), .RST(or_5_out), .Sbin(Sb),
    .Sbout(id_ex_1_sbout), .AluOpin(AluOP), .AluOpout(id_ex_1_aluopout), .Jalin(\单周期硬布线控制器_1_jal ),
    .Jalout(JAL), .Jalrin(\单周期硬布线控制器_1_jalr ), .Jalrout(JALR), .R1in(R1), .R1out(id_ex_1_r1out), .R2in(R2),
    .R2out(id_ex_1_r2out), .Imm_I_in({ID_IR[31], ID_Funct[4], ID_IR[29:26], ID_Funct[3], ID_IR[24:20]}),
    .Imm_I_out(id_ex_1_imm_i_out),
    .Imm_S_in({ID_IR[31], ID_Funct[4], ID_IR[29:26], ID_Funct[3], ID_IR[11:7]}),
    .Imm_S_out(id_ex_1_imm_s_out), .Imm_B_in(bit_extender_1_out), .Imm_B_out(id_ex_1_imm_b_out),
    .Imm_J_in(bit_extender_2_out), .Imm_J_out(id_ex_1_imm_j_out), .PCin(ID_PC), .PCout(EX_PC), .Beqin(Beq),
    .Beqout(id_ex_1_beqout), .Bnein(Bne), .Bneout(id_ex_1_bneout), .Bltin(Blt), .Bltout(id_ex_1_bltout),
    .IRin({ID_IR[31], ID_Funct[4], ID_IR[29:26], ID_Funct[3], ID_IR[24:15], ID_Funct[2:0], ID_IR[11:0]}),
    .IRout(EX_IR), .Haltin(ecall), .Haltout(id_ex_1_haltout), .R1Forwardin(R1Forward),
    .R1Forwardout(id_ex_1_r1forwardout), .R2Forwardout(id_ex_1_r2forwardout), .R2Forwardin(R2Forward),
    .PredictJumpin(if_id_1_predictjumpout), .PredictJumpout(EX_PredictJump));
  Multiplexer #(.select(1), .width(12), .disabled("Z"), .enable("false")) multiplexer_9 (
    .in0(id_ex_1_imm_i_out), .in1(id_ex_1_imm_s_out), .out(multiplexer_9_out), .sel(id_ex_1_s_typeout));
  or or_5 (or_5_out, EX_PredictErr, Load_Use, RST);
  Multiplexer #(.select(2), .width(4), .disabled("Z"), .enable("false")) multiplexer_10 (
    .in0(4'b0001), .in1(4'b0010), .in2(4'b0100), .in3(4'b1000), .out(multiplexer_10_out), .sel(EX_Result[1:0]));
  Multiplexer #(.select(2), .width(5), .disabled("Z"), .enable("false")) multiplexer_11 (
    .in0({5{1'b0}}), .in1(5'b01000), .in2(5'b10000), .in3(5'b11000), .out(multiplexer_11_out),
    .sel(EX_Result[1:0]));
  not not_7 (not_7_out, equal);
  Multiplexer #(.select(2), .width(32), .disabled("Z"), .enable("false")) multiplexer_12 (
    .in0(id_ex_1_r2out), .in1(RDin), .in2(MEM_F), .out(EX_R2), .sel(id_ex_1_r2forwardout));  // open: in3
  assign bit_extender_3_out = {{20{multiplexer_9_out[11]}}, multiplexer_9_out};  // Bit_Extender bit_extender_3
  Multiplexer #(.select(1), .width(4), .disabled("Z"), .enable("false")) multiplexer_13 (
    .in0(4'b1111), .in1(multiplexer_10_out), .out(ByteSelect), .sel(id_ex_1_sbout));
  and and_4 (and_4_out, id_ex_1_beqout, equal);
  and and_5 (and_5_out, not_7_out, id_ex_1_bneout);
  and and_6 (and_6_out, less, id_ex_1_bltout);
  Multiplexer #(.select(2), .width(32), .disabled("Z"), .enable("false")) multiplexer_14 (
    .in0(id_ex_1_r1out), .in1(RDin), .in2(MEM_F), .out(EX_R1), .sel(id_ex_1_r1forwardout));  // open: in3
  Multiplexer #(.select(1), .width(32), .disabled("Z"), .enable("false")) multiplexer_15 (
    .in0(EX_R2), .in1(bit_extender_3_out), .out(multiplexer_15_out), .sel(id_ex_1_alusrcbout));
  Adder #(.width(32)) adder_5 (.a(EX_PC), .b(id_ex_1_imm_b_out), .out(BPC));  // open: cin, cout
  Adder #(.width(32)) adder_6 (.a(EX_PC), .b(id_ex_1_imm_j_out), .out(JPC));  // open: cin, cout
  not not_8 (not_8_out, comparator_3_eq);
  Comparator #(.width(32), .mode("twosComplement")) comparator_3 (
    .a(EX_R2), .b(32'h22), .eq(comparator_3_eq));  // open: gt, lt
  Comparator #(.width(32), .mode("twosComplement")) comparator_4 (
    .a(EX_R2), .b(32'h22), .eq(comparator_4_eq));  // open: gt, lt
  Shifter #(.width(32), .shift("ll")) shifter_4 (.in(EX_R2), .\dist (multiplexer_11_out), .out(shifter_4_out));
  or or_6 (B, and_4_out, and_5_out, and_6_out);
  ALU alu_1 (
    .X(EX_R1), .Y(multiplexer_15_out), .AluOP(id_ex_1_aluopout), .Equal(equal), .Result(EX_Result),
    .out_6(less));  // open: Result_2, out_4
  and and_7 (and_7_out, id_ex_1_haltout, not_8_out);
  and and_8 (and_8_out, id_ex_1_haltout, comparator_4_eq);
  Multiplexer #(.select(1), .width(32), .disabled("Z"), .enable("false")) multiplexer_16 (
    .in0(EX_R2), .in1(shifter_4_out), .out(multiplexer_16_out), .sel(id_ex_1_sbout));
  or or_7 (or_7_out, JAL, JALR);
  Register #(.width(32), .trigger("rising"), .Select("low")) register_1 (
    .D(EX_R1), .en(and_8_out), .Q(LedData), .clk(CLK));  // open: clr
  EX_MEM ex_mem_1 (
    .MemToRegin(EX_MemToReg), .MemWritein(id_ex_1_memwriteout), .Jin(or_7_out), .RegWritein(EX_RegWrite),
    .ByteSelectin(ByteSelect), .MDin(multiplexer_16_out), .W_in(EX_W_num), .PCin(EX_PC),
    .MemToRegout(ex_mem_1_memtoregout), .MemWriteout(MemWrite), .Jout(ex_mem_1_jout),
    .RegWriteout(MEM_RegWrite), .ByteSelectout(ex_mem_1_byteselectout), .MDout(MDin), .W_out(MEM_W_num),
    .PCout(M_PC), .RST(RST), .EN_H(en), .CLK(CLK), .Resultin(EX_Result), .Rrsultout(MEM_F), .IRin(EX_IR),
    .IRout(MEM_IR), .Haltout(ex_mem_1_haltout), .Haltin(and_7_out));
  // MIPS_RAM mips_ram_1: pin names not known; wires that end beside it: MEM_F[11:2], MDin, MemWrite, ex_mem_1_byteselectout, CLK, mips_ram_1_p6, MemWrite, mips_ram_1_p8
  not not_9 (mips_ram_1_p6, MemWrite);
  MEM_WB mem_wb_1 (
    .MemToRegin(ex_mem_1_memtoregout), .Jin(ex_mem_1_jout), .RegWritein(MEM_RegWrite), .W_in(MEM_W_num),
    .IRin(MEM_IR), .PCin(M_PC), .MemToRegout(mem_wb_1_memtoregout), .Jout(J), .RegWriteout(RegWrite),
    .W_out(W_num), .IRout(WB_IR), .PCout(WB_PC), .RST(RST), .EN_H(en), .CLK(CLK), .Memdatein(mips_ram_1_p8),
    .Memdateout(mem_wb_1_memdateout), .Resultin(MEM_F), .Resultout(mem_wb_1_resultout),
    .Haltin(ex_mem_1_haltout), .Haltout(mem_wb_1_haltout));
  and and_9 (halt, mem_wb_1_haltout, ~Go);  // AND_Gate
  not not_10 (en, halt);
  Multiplexer #(.select(1), .width(32), .disabled("Z"), .enable("false")) multiplexer_17 (
    .in0(mem_wb_1_resultout), .in1(mem_wb_1_memdateout), .out(multiplexer_17_out), .sel(mem_wb_1_memtoregout));
  Multiplexer #(.select(1), .width(32), .disabled("Z"), .enable("false")) multiplexer_18 (
    .in0(multiplexer_17_out), .in1(adder_7_out), .out(RDin), .sel(J));
  Adder #(.width(32)) adder_7 (.a(32'h4), .b(WB_PC), .out(adder_7_out));  // open: cin, cout

  // Other names for the same wires on the sheet: IR[31:0] = {ID_IR[31], ID_Funct[4], ID_IR[29:26], ID_Funct[3], ID_IR[24:15], ID_Funct[2:0], ID_IR[11:0]};
  //   ID_IR (some bits) = ID_Funct; ID_OP[4:0] = ID_IR[6:2]; MEM_PC[31:0] = M_PC; WB_F[31:0] = RDin

  // Notes on the sheet:
  //   中断源
  //   中断等待指示
  //   数码管输出
  //   指令存储器
  //   contents of rom_1 (hex, n*v repeats v):
  //   100493 100006f 100493 200913 300993 100006f 100493 200913 300993 100006f 100493 200913 300993
  //   100006f 100493 200913 300993 29c000ef 100413 100493 1f49493 900533 2200893 73 24d493 48463 fedff06f
  //   900533 2200893 73 100493 249493 900533 2200893 73 48463 fedff06f 100493 1f49493 900533 2200893 73
  //   4034d493 900533 2200893 73 4044d493 900533 2200893 73 4044d493 900533 2200893 73 4044d493 900533
  //   2200893 73 4044d493 900533 2200893 73 4044d493 900533 2200893 73 4044d493 900533 2200893 73 4044d493
  //   900533 2200893 73 100413 1f41993 41f9d993 433 c00913 300b13 140413 f47413 800293 100313 499993
  //   89e9b3 1300533 2200893 73 406282b3 fe0294e3 140413 f00f93 1f47433 1c41413 800293 100313 49d993
  //   89e9b3 1300533 2200893 73 406282b3 fe0294e3 1c45413 406b0b33 b0463 f95ff06f 2b3 fff2c293 829293
  //   ff2e293 500533 2200893 73 fff00413 493 84a023 140413 448493 84a023 140413 448493 84a023 140413
  //   448493 84a023 140413 448493 84a023 140413 448493 84a023 140413 448493 84a023 140413 448493 84a023
  //   140413 448493 84a023 140413 448493 84a023 140413 448493 84a023 140413 448493 84a023 140413 448493
  //   84a023 140413 448493 84a023 140413 448493 84a023 140413 448493 84a023 140413 448493 140413 433
  //   3c00493 42983 4aa03 149a2b3 28663 134a023 1442023 ffc48493 fe9412e3 800533 2200893 73 440413 3c00493
  //   fc9416e3 a00893 73 413 140413 800533 2200893 73 240413 800533 2200893 73 340413 800533 2200893 73
  //   440413 800533 2200893 73 540413 800533 2200893 73 640413 800533 2200893 73 740413 800533 2200893 73
  //   840413 800533 2200893 2200893 73 8067
  //   IR
  //   PC
  //   指令探针
  //   func
  //   rs1
  //   rs2
  //   指令字
  //   rd
  //   b型imm
  //   j型imm
  //   控制位
  //   JAL
  //   JALR
  //   URET
  //   I型imm
  //   s型imm
  //   流水调试日志用
  //   暂停节拍，不能为0
  //   Beq
  //   Bne
  //   Blt
  //   MemWrite
  //   AluOP
  //   AluSrcB
  //   RegWrite
  //   S_Type
  //   戳工具置1进入计数暂停模式，ctrl+k时钟自动运行到对应节拍暂停
  //   ctrl+k关闭时钟连续运行，将控制位置零，进入单步调试模式调试
  //   可计数暂停的时钟源
  //   为方便自动评测，需要输出流水线各段保存的PC值，注意是PC不是PC+4，另外ID段寄存器写入信息，Mem段内存写入信息也要输出
  //   数据存储器
endmodule

// BTB
module \BTB表  (
  input  CLK,
  input  EX_Branch,
  input  [31:0] EX_PC,
  input  [31:0] EX_BranchAddr,
  input  [31:0] PC,
  input  EX_BranchTaken,
  output PredictJump,
  output [31:0] JumpAddr
);

  wire and_1_out, and_2_out, and_3_out, and_4_out, and_5_out, and_6_out, and_7_out, and_8_out, and_25_out,
       comparator_1_eq, comparator_2_eq, comparator_3_eq, comparator_4_eq, comparator_5_eq, comparator_6_eq,
       comparator_7_eq, comparator_8_eq, comparator_9_eq, comparator_10_eq, comparator_11_eq,
       comparator_12_eq, comparator_13_eq, comparator_14_eq, comparator_15_eq, comparator_16_eq,
       comparator_17_eq, comparator_18_eq, comparator_19_eq, comparator_20_eq, comparator_21_eq,
       comparator_22_eq, comparator_23_eq, comparator_24_eq, d_ff_1_q, d_ff_2_q, d_ff_3_q, d_ff_4_q,
       d_ff_5_q, d_ff_6_q, d_ff_7_q, d_ff_8_q, EX_Hit, EX_Miss, full, L0, L1, L2, L3, L4, L5, L6, L7, M0, M1,
       M2, M3, M4, M5, M6, M7, not_1_out, not_2_out, not_3_out, not_4_out, not_5_out, not_6_out, not_7_out,
       not_8_out, or_1_out, or_2_out, or_3_out, or_4_out, or_5_out, or_6_out, or_7_out, or_8_out, V0, V1, V2,
       V3, V4, V5, V6, V7, Write0, Write1, Write2, Write3, Write4, Write5, Write6, Write7;
  wire [0:0] controlled_buffer_9_out, controlled_buffer_10_out, controlled_buffer_11_out,
       controlled_buffer_12_out, controlled_buffer_13_out, controlled_buffer_14_out,
       controlled_buffer_15_out, controlled_buffer_16_out;
  wire [1:0] JumpState0, JumpState1, JumpState2, JumpState3, JumpState4, JumpState5, JumpState6, JumpState7,
       multiplexer_1_out, multiplexer_2_out, multiplexer_3_out, multiplexer_4_out, multiplexer_5_out,
       multiplexer_6_out, multiplexer_7_out, multiplexer_8_out, multiplexer_9_out, multiplexer_10_out,
       multiplexer_11_out, multiplexer_12_out, multiplexer_13_out, multiplexer_14_out, multiplexer_15_out,
       multiplexer_16_out, multiplexer_17_out, multiplexer_18_out, multiplexer_19_out, multiplexer_20_out,
       multiplexer_21_out, multiplexer_22_out, multiplexer_23_out, multiplexer_24_out, multiplexer_25_out,
       multiplexer_26_out, multiplexer_27_out, multiplexer_28_out, multiplexer_29_out, multiplexer_30_out,
       multiplexer_31_out, multiplexer_32_out, multiplexer_33_out, multiplexer_34_out, multiplexer_35_out,
       multiplexer_36_out, multiplexer_37_out, multiplexer_38_out, multiplexer_39_out, multiplexer_40_out;
  wire [2:0] max2_1_max_num, max2_2_max_num, max2_3_max_num, max2_4_max_num, max2_5_max_num, max2_6_max_num,
       max2_7_max_num, multiplexer_41_out, priority_encoder_1_out;
  wire [15:0] C0, C1, C2, C3, C4, C5, C6, C7, max2_1_max, max2_2_max, max2_3_max, max2_4_max, max2_5_max,
       max2_6_max;
  wire [31:0] JumpAddr0, JumpAddr1, JumpAddr2, JumpAddr3, JumpAddr4, JumpAddr5, JumpAddr6, JumpAddr7, Tag0,
       Tag1, Tag2, Tag3, Tag4, Tag5, Tag6, Tag7;

  Register #(.width(1), .trigger("rising"), .Select("low")) Valid (
    .D(1'b1), .en(Write0), .Q(V0), .clk(CLK));  // open: clr
  Register #(.width(1), .trigger("rising"), .Select("low")) Valid_2 (
    .D(1'b1), .en(Write1), .Q(V1), .clk(CLK));  // open: clr
  Register #(.width(1), .trigger("rising"), .Select("low")) Valid_3 (
    .D(1'b1), .en(Write2), .Q(V2), .clk(CLK));  // open: clr
  Register #(.width(1), .trigger("rising"), .Select("low")) Valid_4 (
    .D(1'b1), .en(Write3), .Q(V3), .clk(CLK));  // open: clr
  Register #(.width(1), .trigger("rising"), .Select("low")) Valid_5 (
    .D(1'b1), .en(Write4), .Q(V4), .clk(CLK));  // open: clr
  Register #(.width(1), .trigger("rising"), .Select("low")) Valid_6 (
    .D(1'b1), .en(Write5), .Q(V5), .clk(CLK));  // open: clr
  Register #(.width(1), .trigger("rising"), .Select("low")) Valid_7 (
    .D(1'b1), .en(Write6), .Q(V6), .clk(CLK));  // open: clr
  Register #(.width(1), .trigger("rising"), .Select("low")) Valid_8 (
    .D(1'b1), .en(Write7), .Q(V7), .clk(CLK));  // open: clr
  Register #(.width(32), .trigger("rising"), .Select("low")) \u_分支指令地址  (
    .D(EX_PC), .en(Write0), .Q(Tag0), .clk(CLK));  // open: clr
  Register #(.width(32), .trigger("rising"), .Select("low")) \u_分支指令地址_2  (
    .D(EX_PC), .en(Write1), .Q(Tag1), .clk(CLK));  // open: clr
  Register #(.width(32), .trigger("rising"), .Select("low")) \u_分支指令地址_3  (
    .D(EX_PC), .en(Write2), .Q(Tag2), .clk(CLK));  // open: clr
  Register #(.width(32), .trigger("rising"), .Select("low")) \u_分支指令地址_4  (
    .D(EX_PC), .en(Write3), .Q(Tag3), .clk(CLK));  // open: clr
  Register #(.width(32), .trigger("rising"), .Select("low")) \u_分支指令地址_5  (
    .D(EX_PC), .en(Write4), .Q(Tag4), .clk(CLK));  // open: clr
  Register #(.width(32), .trigger("rising"), .Select("low")) \u_分支指令地址_6  (
    .D(EX_PC), .en(Write5), .Q(Tag5), .clk(CLK));  // open: clr
  Register #(.width(32), .trigger("rising"), .Select("low")) \u_分支指令地址_7  (
    .D(EX_PC), .en(Write6), .Q(Tag6), .clk(CLK));  // open: clr
  Register #(.width(32), .trigger("rising"), .Select("low")) \u_分支指令地址_8  (
    .D(EX_PC), .en(Write7), .Q(Tag7), .clk(CLK));  // open: clr
  Register #(.width(32), .trigger("rising"), .Select("low")) \u_分支目标地址  (
    .D(EX_BranchAddr), .en(Write0), .Q(JumpAddr0), .clk(CLK));  // open: clr
  Register #(.width(32), .trigger("rising"), .Select("low")) \u_分支目标地址_2  (
    .D(EX_BranchAddr), .en(Write1), .Q(JumpAddr1), .clk(CLK));  // open: clr
  Register #(.width(32), .trigger("rising"), .Select("low")) \u_分支目标地址_3  (
    .D(EX_BranchAddr), .en(Write2), .Q(JumpAddr2), .clk(CLK));  // open: clr
  Register #(.width(32), .trigger("rising"), .Select("low")) \u_分支目标地址_4  (
    .D(EX_BranchAddr), .en(Write3), .Q(JumpAddr3), .clk(CLK));  // open: clr
  Register #(.width(32), .trigger("rising"), .Select("low")) \u_分支目标地址_5  (
    .D(EX_BranchAddr), .en(Write4), .Q(JumpAddr4), .clk(CLK));  // open: clr
  Register #(.width(32), .trigger("rising"), .Select("low")) \u_分支目标地址_6  (
    .D(EX_BranchAddr), .en(Write5), .Q(JumpAddr5), .clk(CLK));  // open: clr
  Register #(.width(32), .trigger("rising"), .Select("low")) \u_分支目标地址_7  (
    .D(EX_BranchAddr), .en(Write6), .Q(JumpAddr6), .clk(CLK));  // open: clr
  Register #(.width(32), .trigger("rising"), .Select("low")) \u_分支目标地址_8  (
    .D(EX_BranchAddr), .en(Write7), .Q(JumpAddr7), .clk(CLK));  // open: clr
  assign JumpAddr = L0 ? JumpAddr0 : 32'bz;  // Controlled_Buffer controlled_buffer_1
  assign JumpAddr = L1 ? JumpAddr1 : 32'bz;  // Controlled_Buffer controlled_buffer_2
  assign JumpAddr = L2 ? JumpAddr2 : 32'bz;  // Controlled_Buffer controlled_buffer_3
  assign JumpAddr = L3 ? JumpAddr3 : 32'bz;  // Controlled_Buffer controlled_buffer_4
  assign JumpAddr = L4 ? JumpAddr4 : 32'bz;  // Controlled_Buffer controlled_buffer_5
  assign JumpAddr = L5 ? JumpAddr5 : 32'bz;  // Controlled_Buffer controlled_buffer_6
  assign JumpAddr = L6 ? JumpAddr6 : 32'bz;  // Controlled_Buffer controlled_buffer_7
  assign JumpAddr = L7 ? JumpAddr7 : 32'bz;  // Controlled_Buffer controlled_buffer_8
  assign {PredictJump, controlled_buffer_9_out[0]} = L0 ? JumpState0 : 2'bz;  // Controlled_Buffer controlled_buffer_9
  or or_1 (or_1_out, Write0, L0);
  assign {PredictJump, controlled_buffer_10_out[0]} = L1 ? JumpState1 : 2'bz;  // Controlled_Buffer controlled_buffer_10
  or or_2 (or_2_out, Write1, L1);
  assign {PredictJump, controlled_buffer_11_out[0]} = L2 ? JumpState2 : 2'bz;  // Controlled_Buffer controlled_buffer_11
  or or_3 (or_3_out, Write2, L2);
  assign {PredictJump, controlled_buffer_12_out[0]} = L3 ? JumpState3 : 2'bz;  // Controlled_Buffer controlled_buffer_12
  or or_4 (or_4_out, Write3, L3);
  assign {PredictJump, controlled_buffer_13_out[0]} = L4 ? JumpState4 : 2'bz;  // Controlled_Buffer controlled_buffer_13
  or or_5 (or_5_out, Write4, L4);
  assign {PredictJump, controlled_buffer_14_out[0]} = L5 ? JumpState5 : 2'bz;  // Controlled_Buffer controlled_buffer_14
  or or_6 (or_6_out, Write5, L5);
  assign {PredictJump, controlled_buffer_15_out[0]} = L6 ? JumpState6 : 2'bz;  // Controlled_Buffer controlled_buffer_15
  or or_7 (or_7_out, Write6, L6);
  assign {PredictJump, controlled_buffer_16_out[0]} = L7 ? JumpState7 : 2'bz;  // Controlled_Buffer controlled_buffer_16
  or or_8 (or_8_out, Write7, L7);
  D_Flip_Flop #(.trigger("rising"), .Pre_Clr_Positions("ABOVE_BELOW"), .NegatePresetClear("false"), .enable("false"), .NewFFLayout("false")) d_ff_1 (
    .clk(CLK), .D(or_1_out), .Q(d_ff_1_q));  // open: Qn, preset, reset
  D_Flip_Flop #(.trigger("rising"), .Pre_Clr_Positions("ABOVE_BELOW"), .NegatePresetClear("false"), .enable("false"), .NewFFLayout("false")) d_ff_2 (
    .clk(CLK), .D(or_2_out), .Q(d_ff_2_q));  // open: Qn, preset, reset
  D_Flip_Flop #(.trigger("rising"), .Pre_Clr_Positions("ABOVE_BELOW"), .NegatePresetClear("false"), .enable("false"), .NewFFLayout("false")) d_ff_3 (
    .clk(CLK), .D(or_3_out), .Q(d_ff_3_q));  // open: Qn, preset, reset
  D_Flip_Flop #(.trigger("rising"), .Pre_Clr_Positions("ABOVE_BELOW"), .NegatePresetClear("false"), .enable("false"), .NewFFLayout("false")) d_ff_4 (
    .clk(CLK), .D(or_4_out), .Q(d_ff_4_q));  // open: Qn, preset, reset
  D_Flip_Flop #(.trigger("rising"), .Pre_Clr_Positions("ABOVE_BELOW"), .NegatePresetClear("false"), .enable("false"), .NewFFLayout("false")) d_ff_5 (
    .clk(CLK), .D(or_5_out), .Q(d_ff_5_q));  // open: Qn, preset, reset
  D_Flip_Flop #(.trigger("rising"), .Pre_Clr_Positions("ABOVE_BELOW"), .NegatePresetClear("false"), .enable("false"), .NewFFLayout("false")) d_ff_6 (
    .clk(CLK), .D(or_6_out), .Q(d_ff_6_q));  // open: Qn, preset, reset
  D_Flip_Flop #(.trigger("rising"), .Pre_Clr_Positions("ABOVE_BELOW"), .NegatePresetClear("false"), .enable("false"), .NewFFLayout("false")) d_ff_7 (
    .clk(CLK), .D(or_7_out), .Q(d_ff_7_q));  // open: Qn, preset, reset
  D_Flip_Flop #(.trigger("rising"), .Pre_Clr_Positions("ABOVE_BELOW"), .NegatePresetClear("false"), .enable("false"), .NewFFLayout("false")) d_ff_8 (
    .clk(CLK), .D(or_8_out), .Q(d_ff_8_q));  // open: Qn, preset, reset
  Pull_Resistor #(.pull(0)) pull_resistor_1 (.node(PredictJump));
  Counter #(.width(16), .max('hffff), .ongoal("wrap"), .trigger("rising"), .behavior("new")) \u_淘汰记数  (
    .Q(C0), .clk(CLK), .clr(d_ff_1_q));  // open: load, D, count, carry, preset, down
  Counter #(.width(16), .max('hffff), .ongoal("wrap"), .trigger("rising"), .behavior("new")) \u_淘汰记数_2  (
    .Q(C1), .clk(CLK), .clr(d_ff_2_q));  // open: load, D, count, carry, preset, down
  Counter #(.width(16), .max('hffff), .ongoal("wrap"), .trigger("rising"), .behavior("new")) \u_淘汰记数_3  (
    .Q(C2), .clk(CLK), .clr(d_ff_3_q));  // open: load, D, count, carry, preset, down
  Counter #(.width(16), .max('hffff), .ongoal("wrap"), .trigger("rising"), .behavior("new")) \u_淘汰记数_4  (
    .Q(C3), .clk(CLK), .clr(d_ff_4_q));  // open: load, D, count, carry, preset, down
  Counter #(.width(16), .max('hffff), .ongoal("wrap"), .trigger("rising"), .behavior("new")) \u_淘汰记数_5  (
    .Q(C4), .clk(CLK), .clr(d_ff_5_q));  // open: load, D, count, carry, preset, down
  Counter #(.width(16), .max('hffff), .ongoal("wrap"), .trigger("rising"), .behavior("new")) \u_淘汰记数_6  (
    .Q(C5), .clk(CLK), .clr(d_ff_6_q));  // open: load, D, count, carry, preset, down
  Counter #(.width(16), .max('hffff), .ongoal("wrap"), .trigger("rising"), .behavior("new")) \u_淘汰记数_7  (
    .Q(C6), .clk(CLK), .clr(d_ff_7_q));  // open: load, D, count, carry, preset, down
  Counter #(.width(16), .max('hffff), .ongoal("wrap"), .trigger("rising"), .behavior("new")) \u_淘汰记数_8  (
    .Q(C7), .clk(CLK), .clr(d_ff_8_q));  // open: load, D, count, carry, preset, down
  Multiplexer #(.select(1), .width(2), .disabled("Z"), .enable("false")) multiplexer_1 (
    .in0(2'b00), .in1(2'b01), .out(multiplexer_1_out), .sel(EX_BranchTaken));
  Multiplexer #(.select(1), .width(2), .disabled("Z"), .enable("false")) multiplexer_2 (
    .in0(2'b00), .in1(2'b10), .out(multiplexer_2_out), .sel(EX_BranchTaken));
  Multiplexer #(.select(1), .width(2), .disabled("Z"), .enable("false")) multiplexer_3 (
    .in0(2'b11), .in1(2'b10), .out(multiplexer_3_out), .sel(EX_BranchTaken));
  Multiplexer #(.select(1), .width(2), .disabled("Z"), .enable("false")) multiplexer_4 (
    .in0(2'b00), .in1(2'b10), .out(multiplexer_4_out), .sel(EX_BranchTaken));
  Multiplexer #(.select(1), .width(2), .disabled("Z"), .enable("false")) multiplexer_5 (
    .in0(2'b00), .in1(2'b01), .out(multiplexer_5_out), .sel(EX_BranchTaken));
  Multiplexer #(.select(1), .width(2), .disabled("Z"), .enable("false")) multiplexer_6 (
    .in0(2'b00), .in1(2'b10), .out(multiplexer_6_out), .sel(EX_BranchTaken));
  Multiplexer #(.select(1), .width(2), .disabled("Z"), .enable("false")) multiplexer_7 (
    .in0(2'b11), .in1(2'b10), .out(multiplexer_7_out), .sel(EX_BranchTaken));
  Multiplexer #(.select(1), .width(2), .disabled("Z"), .enable("false")) multiplexer_8 (
    .in0(2'b00), .in1(2'b10), .out(multiplexer_8_out), .sel(EX_BranchTaken));
  Multiplexer #(.select(1), .width(2), .disabled("Z"), .enable("false")) multiplexer_9 (
    .in0(2'b00), .in1(2'b01), .out(multiplexer_9_out), .sel(EX_BranchTaken));
  Multiplexer #(.select(1), .width(2), .disabled("Z"), .enable("false")) multiplexer_10 (
    .in0(2'b00), .in1(2'b10), .out(multiplexer_10_out), .sel(EX_BranchTaken));
  Multiplexer #(.select(1), .width(2), .disabled("Z"), .enable("false")) multiplexer_11 (
    .in0(2'b11), .in1(2'b10), .out(multiplexer_11_out), .sel(EX_BranchTaken));
  Multiplexer #(.select(1), .width(2), .disabled("Z"), .enable("false")) multiplexer_12 (
    .in0(2'b00), .in1(2'b10), .out(multiplexer_12_out), .sel(EX_BranchTaken));
  Multiplexer #(.select(1), .width(2), .disabled("Z"), .enable("false")) multiplexer_13 (
    .in0(2'b00), .in1(2'b01), .out(multiplexer_13_out), .sel(EX_BranchTaken));
  Multiplexer #(.select(1), .width(2), .disabled("Z"), .enable("false")) multiplexer_14 (
    .in0(2'b00), .in1(2'b10), .out(multiplexer_14_out), .sel(EX_BranchTaken));
  Multiplexer #(.select(1), .width(2), .disabled("Z"), .enable("false")) multiplexer_15 (
    .in0(2'b11), .in1(2'b10), .out(multiplexer_15_out), .sel(EX_BranchTaken));
  Multiplexer #(.select(1), .width(2), .disabled("Z"), .enable("false")) multiplexer_16 (
    .in0(2'b00), .in1(2'b10), .out(multiplexer_16_out), .sel(EX_BranchTaken));
  Multiplexer #(.select(1), .width(2), .disabled("Z"), .enable("false")) multiplexer_17 (
    .in0(2'b00), .in1(2'b01), .out(multiplexer_17_out), .sel(EX_BranchTaken));
  Multiplexer #(.select(1), .width(2), .disabled("Z"), .enable("false")) multiplexer_18 (
    .in0(2'b00), .in1(2'b10), .out(multiplexer_18_out), .sel(EX_BranchTaken));
  Multiplexer #(.select(1), .width(2), .disabled("Z"), .enable("false")) multiplexer_19 (
    .in0(2'b11), .in1(2'b10), .out(multiplexer_19_out), .sel(EX_BranchTaken));
  Multiplexer #(.select(1), .width(2), .disabled("Z"), .enable("false")) multiplexer_20 (
    .in0(2'b00), .in1(2'b10), .out(multiplexer_20_out), .sel(EX_BranchTaken));
  Multiplexer #(.select(1), .width(2), .disabled("Z"), .enable("false")) multiplexer_21 (
    .in0(2'b00), .in1(2'b01), .out(multiplexer_21_out), .sel(EX_BranchTaken));
  Multiplexer #(.select(1), .width(2), .disabled("Z"), .enable("false")) multiplexer_22 (
    .in0(2'b00), .in1(2'b10), .out(multiplexer_22_out), .sel(EX_BranchTaken));
  Multiplexer #(.select(1), .width(2), .disabled("Z"), .enable("false")) multiplexer_23 (
    .in0(2'b11), .in1(2'b10), .out(multiplexer_23_out), .sel(EX_BranchTaken));
  Multiplexer #(.select(1), .width(2), .disabled("Z"), .enable("false")) multiplexer_24 (
    .in0(2'b00), .in1(2'b10), .out(multiplexer_24_out), .sel(EX_BranchTaken));
  Multiplexer #(.select(1), .width(2), .disabled("Z"), .enable("false")) multiplexer_25 (
    .in0(2'b00), .in1(2'b01), .out(multiplexer_25_out), .sel(EX_BranchTaken));
  Multiplexer #(.select(1), .width(2), .disabled("Z"), .enable("false")) multiplexer_26 (
    .in0(2'b00), .in1(2'b10), .out(multiplexer_26_out), .sel(EX_BranchTaken));
  Multiplexer #(.select(1), .width(2), .disabled("Z"), .enable("false")) multiplexer_27 (
    .in0(2'b11), .in1(2'b10), .out(multiplexer_27_out), .sel(EX_BranchTaken));
  Multiplexer #(.select(1), .width(2), .disabled("Z"), .enable("false")) multiplexer_28 (
    .in0(2'b00), .in1(2'b10), .out(multiplexer_28_out), .sel(EX_BranchTaken));
  Multiplexer #(.select(1), .width(2), .disabled("Z"), .enable("false")) multiplexer_29 (
    .in0(2'b00), .in1(2'b01), .out(multiplexer_29_out), .sel(EX_BranchTaken));
  Multiplexer #(.select(1), .width(2), .disabled("Z"), .enable("false")) multiplexer_30 (
    .in0(2'b00), .in1(2'b10), .out(multiplexer_30_out), .sel(EX_BranchTaken));
  Multiplexer #(.select(1), .width(2), .disabled("Z"), .enable("false")) multiplexer_31 (
    .in0(2'b11), .in1(2'b10), .out(multiplexer_31_out), .sel(EX_BranchTaken));
  Multiplexer #(.select(1), .width(2), .disabled("Z"), .enable("false")) multiplexer_32 (
    .in0(2'b00), .in1(2'b10), .out(multiplexer_32_out), .sel(EX_BranchTaken));
  Multiplexer #(.select(2), .width(2), .disabled("Z"), .enable("false")) multiplexer_33 (
    .in0(multiplexer_5_out), .in1(multiplexer_6_out), .in2(multiplexer_7_out), .in3(multiplexer_8_out),
    .out(multiplexer_33_out), .sel(JumpState1));
  Multiplexer #(.select(2), .width(2), .disabled("Z"), .enable("false")) multiplexer_34 (
    .in0(multiplexer_13_out), .in1(multiplexer_14_out), .in2(multiplexer_15_out), .in3(multiplexer_16_out),
    .out(multiplexer_34_out), .sel(JumpState3));
  Multiplexer #(.select(2), .width(2), .disabled("Z"), .enable("false")) multiplexer_35 (
    .in0(multiplexer_21_out), .in1(multiplexer_22_out), .in2(multiplexer_23_out), .in3(multiplexer_24_out),
    .out(multiplexer_35_out), .sel(JumpState5));
  Multiplexer #(.select(2), .width(2), .disabled("Z"), .enable("false")) multiplexer_36 (
    .in0(multiplexer_29_out), .in1(multiplexer_30_out), .in2(multiplexer_31_out), .in3(multiplexer_32_out),
    .out(multiplexer_36_out), .sel(JumpState7));
  Multiplexer #(.select(2), .width(2), .disabled("Z"), .enable("false")) multiplexer_37 (
    .in0(multiplexer_1_out), .in1(multiplexer_2_out), .in2(multiplexer_3_out), .in3(multiplexer_4_out),
    .out(multiplexer_37_out), .sel(JumpState0));
  Multiplexer #(.select(2), .width(2), .disabled("Z"), .enable("false")) multiplexer_38 (
    .in0(multiplexer_9_out), .in1(multiplexer_10_out), .in2(multiplexer_11_out), .in3(multiplexer_12_out),
    .out(multiplexer_38_out), .sel(JumpState2));
  and and_1 (and_1_out, EX_Branch, M3);
  Multiplexer #(.select(2), .width(2), .disabled("Z"), .enable("false")) multiplexer_39 (
    .in0(multiplexer_17_out), .in1(multiplexer_18_out), .in2(multiplexer_19_out), .in3(multiplexer_20_out),
    .out(multiplexer_39_out), .sel(JumpState4));
  and and_2 (and_2_out, EX_Branch, M4);
  and and_3 (and_3_out, EX_Branch, M5);
  Multiplexer #(.select(2), .width(2), .disabled("Z"), .enable("false")) multiplexer_40 (
    .in0(multiplexer_25_out), .in1(multiplexer_26_out), .in2(multiplexer_27_out), .in3(multiplexer_28_out),
    .out(multiplexer_40_out), .sel(JumpState6));
  and and_4 (and_4_out, EX_Branch, M6);
  and and_5 (and_5_out, EX_Branch, M7);
  and and_6 (and_6_out, EX_Branch, M0);
  Register #(.width(2), .trigger("rising"), .Select("low")) \u_双位预测状态_2位  (
    .D(multiplexer_33_out), .en(and_7_out), .Q(JumpState1), .clk(CLK));  // open: clr
  and and_7 (and_7_out, EX_Branch, M1);
  Register #(.width(2), .trigger("rising"), .Select("low")) \u_双位预测状态_2位_2  (
    .D(multiplexer_38_out), .en(and_8_out), .Q(JumpState2), .clk(CLK));  // open: clr
  and and_8 (and_8_out, EX_Branch, M2);
  Register #(.width(2), .trigger("rising"), .Select("low")) \u_双位预测状态_2位_3  (
    .D(multiplexer_34_out), .en(and_1_out), .Q(JumpState3), .clk(CLK));  // open: clr
  Register #(.width(2), .trigger("rising"), .Select("low")) \u_双位预测状态_2位_4  (
    .D(multiplexer_39_out), .en(and_2_out), .Q(JumpState4), .clk(CLK));  // open: clr
  Register #(.width(2), .trigger("rising"), .Select("low")) \u_双位预测状态_2位_5  (
    .D(multiplexer_35_out), .en(and_3_out), .Q(JumpState5), .clk(CLK));  // open: clr
  Register #(.width(2), .trigger("rising"), .Select("low")) \u_双位预测状态_2位_6  (
    .D(multiplexer_40_out), .en(and_4_out), .Q(JumpState6), .clk(CLK));  // open: clr
  Register #(.width(2), .trigger("rising"), .Select("low")) \u_双位预测状态_2位_7  (
    .D(multiplexer_36_out), .en(and_5_out), .Q(JumpState7), .clk(CLK));  // open: clr
  Register #(.width(2), .trigger("rising"), .Select("low")) \u_双位预测状态_2位_8  (
    .D(multiplexer_37_out), .en(and_6_out), .Q(JumpState0), .clk(CLK));  // open: clr
  Comparator #(.width(32), .mode("unsigned")) comparator_1 (
    .a(EX_BranchAddr), .b(JumpAddr0), .eq(comparator_1_eq));  // open: gt, lt
  Comparator #(.width(32), .mode("unsigned")) comparator_2 (
    .a(EX_BranchAddr), .b(JumpAddr1), .eq(comparator_2_eq));  // open: gt, lt
  Comparator #(.width(32), .mode("unsigned")) comparator_3 (
    .a(EX_BranchAddr), .b(JumpAddr2), .eq(comparator_3_eq));  // open: gt, lt
  Comparator #(.width(32), .mode("unsigned")) comparator_4 (
    .a(EX_BranchAddr), .b(JumpAddr3), .eq(comparator_4_eq));  // open: gt, lt
  Comparator #(.width(32), .mode("unsigned")) comparator_5 (
    .a(EX_BranchAddr), .b(JumpAddr4), .eq(comparator_5_eq));  // open: gt, lt
  Comparator #(.width(32), .mode("unsigned")) comparator_6 (
    .a(EX_BranchAddr), .b(JumpAddr5), .eq(comparator_6_eq));  // open: gt, lt
  Comparator #(.width(32), .mode("unsigned")) comparator_7 (
    .a(EX_BranchAddr), .b(JumpAddr6), .eq(comparator_7_eq));  // open: gt, lt
  Comparator #(.width(32), .mode("unsigned")) comparator_8 (
    .a(EX_BranchAddr), .b(JumpAddr7), .eq(comparator_8_eq));  // open: gt, lt
  MAX2 max2_1 (.X(C0), .Y(C1), .X_num(3'b000), .Y_num(3'b001), .MAX(max2_1_max), .MAX_num(max2_1_max_num));
  MAX2 max2_2 (.X(C2), .Y(C3), .X_num(3'b010), .Y_num(3'b011), .MAX(max2_2_max), .MAX_num(max2_2_max_num));
  MAX2 max2_3 (.X(C4), .Y(C5), .X_num(3'b100), .Y_num(3'b101), .MAX(max2_3_max), .MAX_num(max2_3_max_num));
  MAX2 max2_4 (.X(C6), .Y(C7), .X_num(3'b110), .Y_num(3'b111), .MAX(max2_4_max), .MAX_num(max2_4_max_num));
  not not_1 (not_1_out, V0);
  not not_2 (not_2_out, V1);
  not not_3 (not_3_out, V2);
  not not_4 (not_4_out, V3);
  not not_5 (not_5_out, V4);
  not not_6 (not_6_out, V5);
  not not_7 (not_7_out, V6);
  not not_8 (not_8_out, V7);
  MAX2 max2_5 (
    .X(max2_1_max), .Y(max2_2_max), .X_num(max2_1_max_num), .Y_num(max2_2_max_num), .MAX(max2_5_max),
    .MAX_num(max2_5_max_num));
  MAX2 max2_6 (
    .X(max2_3_max), .Y(max2_4_max), .X_num(max2_3_max_num), .Y_num(max2_4_max_num), .MAX(max2_6_max),
    .MAX_num(max2_6_max_num));
  Priority_Encoder #(.select(3), .disabled("Z")) priority_encoder_1 (
    .in0(not_1_out), .in1(not_2_out), .in2(not_3_out), .in3(not_4_out), .in4(not_5_out), .in5(not_6_out),
    .in6(not_7_out), .in7(not_8_out), .out(priority_encoder_1_out), .en_out(full), .en_in(1'b1));  // open: gs
  MAX2 max2_7 (
    .X(max2_5_max), .Y(max2_6_max), .X_num(max2_5_max_num), .Y_num(max2_6_max_num), .MAX_num(max2_7_max_num));  // open: MAX
  Comparator #(.width(32), .mode("unsigned")) comparator_9 (.a(PC), .b(Tag0), .eq(comparator_9_eq));  // open: gt, lt
  Comparator #(.width(32), .mode("unsigned")) comparator_10 (.a(PC), .b(Tag1), .eq(comparator_10_eq));  // open: gt, lt
  Comparator #(.width(32), .mode("unsigned")) comparator_11 (.a(PC), .b(Tag2), .eq(comparator_11_eq));  // open: gt, lt
  Comparator #(.width(32), .mode("unsigned")) comparator_12 (.a(PC), .b(Tag3), .eq(comparator_12_eq));  // open: gt, lt
  Comparator #(.width(32), .mode("unsigned")) comparator_13 (.a(PC), .b(Tag4), .eq(comparator_13_eq));  // open: gt, lt
  Comparator #(.width(32), .mode("unsigned")) comparator_14 (.a(PC), .b(Tag5), .eq(comparator_14_eq));  // open: gt, lt
  Comparator #(.width(32), .mode("unsigned")) comparator_15 (.a(PC), .b(Tag6), .eq(comparator_15_eq));  // open: gt, lt
  Comparator #(.width(32), .mode("unsigned")) comparator_16 (.a(PC), .b(Tag7), .eq(comparator_16_eq));  // open: gt, lt
  Comparator #(.width(32), .mode("unsigned")) comparator_17 (
    .a(EX_PC), .b(Tag0), .eq(comparator_17_eq));  // open: gt, lt
  Comparator #(.width(32), .mode("unsigned")) comparator_18 (
    .a(EX_PC), .b(Tag1), .eq(comparator_18_eq));  // open: gt, lt
  Comparator #(.width(32), .mode("unsigned")) comparator_19 (
    .a(EX_PC), .b(Tag2), .eq(comparator_19_eq));  // open: gt, lt
  Comparator #(.width(32), .mode("unsigned")) comparator_20 (
    .a(EX_PC), .b(Tag3), .eq(comparator_20_eq));  // open: gt, lt
  Comparator #(.width(32), .mode("unsigned")) comparator_21 (
    .a(EX_PC), .b(Tag4), .eq(comparator_21_eq));  // open: gt, lt
  Comparator #(.width(32), .mode("unsigned")) comparator_22 (
    .a(EX_PC), .b(Tag5), .eq(comparator_22_eq));  // open: gt, lt
  Comparator #(.width(32), .mode("unsigned")) comparator_23 (
    .a(EX_PC), .b(Tag6), .eq(comparator_23_eq));  // open: gt, lt
  Comparator #(.width(32), .mode("unsigned")) comparator_24 (
    .a(EX_PC), .b(Tag7), .eq(comparator_24_eq));  // open: gt, lt
  and and_9 (L0, comparator_9_eq, V0);
  and and_10 (L1, comparator_10_eq, V1);
  and and_11 (L2, comparator_11_eq, V2);
  and and_12 (L3, comparator_12_eq, V3);
  and and_13 (L4, comparator_13_eq, V4);
  and and_14 (L5, comparator_14_eq, V5);
  and and_15 (L6, comparator_15_eq, V6);
  and and_16 (L7, comparator_16_eq, V7);
  and and_17 (M0, comparator_17_eq, V0, comparator_1_eq);
  and and_18 (M1, comparator_18_eq, V1, comparator_2_eq);
  and and_19 (M2, comparator_19_eq, V2, comparator_3_eq);
  and and_20 (M3, comparator_20_eq, V3, comparator_4_eq);
  and and_21 (M4, comparator_21_eq, V4, comparator_5_eq);
  and and_22 (M5, comparator_22_eq, V5, comparator_6_eq);
  and and_23 (M6, comparator_23_eq, V6, comparator_7_eq);
  and and_24 (M7, comparator_24_eq, V7, comparator_8_eq);
  and and_25 (and_25_out, EX_Branch, EX_Miss);
  Multiplexer #(.select(1), .width(3), .disabled("Z"), .enable("false")) multiplexer_41 (
    .in0(priority_encoder_1_out), .in1(max2_7_max_num), .out(multiplexer_41_out), .sel(full));
  Demultiplexer #(.select(3), .width(1), .tristate("false"), .disabled("Z"), .enable("false")) demultiplexer_1 (
    .out0(Write0), .out1(Write1), .out2(Write2), .out3(Write3), .out4(Write4), .out5(Write5), .out6(Write6),
    .out7(Write7), .in(and_25_out), .sel(multiplexer_41_out));
  or or_9 (EX_Hit, M0, M1, M2, M3, M4, M5, M6, M7);
  not not_9 (EX_Miss, EX_Hit);
endmodule

module MAX2 (
  input  [15:0] X,
  input  [15:0] Y,
  input  [2:0] X_num,
  input  [2:0] Y_num,
  output [15:0] MAX,
  output [2:0] MAX_num
);

  wire comparator_1_eq, comparator_1_gt, or_1_out;

  Comparator #(.width(16), .mode("unsigned")) comparator_1 (
    .a(Y), .b(X), .gt(comparator_1_gt), .eq(comparator_1_eq));  // open: lt
  Multiplexer #(.select(1), .width(16), .disabled("Z"), .enable("false")) multiplexer_1 (
    .in0(X), .in1(Y), .out(MAX), .sel(or_1_out));
  or or_1 (or_1_out, comparator_1_gt, comparator_1_eq);
  Multiplexer #(.select(1), .width(3), .disabled("Z"), .enable("false")) multiplexer_2 (
    .in0(X_num), .in1(Y_num), .out(MAX_num), .sel(or_1_out));
endmodule
