// Logisim project cpu21-riscv - 动态分支预测.circ as structural Verilog: 24 circuits, main circuit ◇单周期RISC-V
// 单周期硬布线控制器
module \单周期硬布线控制器  (
  input  [4:0] OP,
  input  [4:0] Funct,
  input  in_3,
  output [3:0] ALU_OP,
  output uret,
  output u1,
  output u2,
  output MemToReg,
  output ecall,
  output MemWrite,
  output ALU_SRC,
  output RegWrite,
  output S_type,
  output Beq,
  output Bne,
  output Jalr,
  output JAL,
  output csr,
  output LBU,
  output U_type,
  output bge
);

  wire \控制信号自动生成_1_ecall ;

  \运算控制器自动生成  \u_运算控制器自动生成_1  (
    .OP2(OP[0]), .OP3(OP[1]), .OP4(OP[2]), .OP5(OP[3]), .OP6(OP[4]), .F12(Funct[0]), .F13(Funct[1]),
    .F14(Funct[2]), .F25(Funct[3]), .F30(Funct[4]), .S0(ALU_OP[0]), .S1(ALU_OP[1]), .S2(ALU_OP[2]),
    .S3(ALU_OP[3]));
  \控制信号自动生成  \u_控制信号自动生成_1  (
    .OP2(OP[0]), .OP3(OP[1]), .OP4(OP[2]), .OP5(OP[3]), .OP6(OP[4]), .MemToReg(MemToReg), .F12(Funct[0]),
    .F13(Funct[1]), .F14(Funct[2]), .F25(Funct[3]), .F30(Funct[4]), .MemWrite(MemWrite), .ALU_SRC(ALU_SRC),
    .RegWrite(RegWrite), .ecall(\控制信号自动生成_1_ecall ), .S_Type(S_type), .BEQ(Beq), .BNE(Bne), .JALR(Jalr),
    .JAL(JAL), .csr(csr), .bge(bge), .U_Type(U_type), .u1(u1), .u2(u2), .LBU(LBU));
  and and_1 (uret, in_3, \控制信号自动生成_1_ecall );
  and and_2 (ecall, ~in_3, \控制信号自动生成_1_ecall );  // AND_Gate
  \运算控制器自动生成  \u_运算控制器自动生成_2  ();  // open: OP2, OP3, OP4, OP5, OP6, F12, F13, F14, F25, F30, S0, S1, S2, S3

  // Other names for the same wires on the sheet: IR21 = in_3; OP_CODE[4:0] = OP

  // Notes on the sheet:
  //   运算器控制器，根据指令生成运算器功能选择信号
  //   控制信号生成，产生数据通路需要的其他控制信号
endmodule

module \单周期RISC_V  (
  input  IR1,
  input  IR2,
  input  IR3,
  output RegWrite,
  output MemWrite,
  output [31:0] PC,
  output [31:0] IR,
  output [31:0] RDin,
  output [31:0] MDin,
  output [31:0] LedData
);

  wire ALUequal, ALUge, and_1_out, and_2_out, and_3_out, and_5_out, Beq, Bne, CLK, clock_1_out,
       comparator_1_eq, comparator_2_eq, comparator_2_lt, d_ff_1_q, ecall, Go, halt, IR1_t, IR2_t, IR3_t,
       IRA, IRB, IRC, jal, jalr, LBU, MemToReg, nand_1_out, not_1_out, not_2_out, not_3_out, not_4_out,
       or_1_out, or_2_out, riscv_probe_1_p2, Stype, Utype, W1, W2, W3, \单周期硬布线控制器_1_alu_src ,
       \单周期硬布线控制器_1_bge ;
  wire [1:0] or_6_out, priority_encoder_1_out;
  wire [3:0] \单周期硬布线控制器_1_alu_op ;
  wire [4:0] multiplexer_2_out, multiplexer_3_out;
  wire [7:0] multiplexer_8_out;
  wire [11:0] multiplexer_4_out;
  wire [12:0] CNT_num;
  wire [15:0] \总周期数 ;
  wire [31:0] adder_2_out, adder_3_out, adder_4_out, ALUresult, bit_extender_1_out, bit_extender_2_out,
       bit_extender_3_out, bit_extender_4_out, LBUData, multiplexer_1_out, multiplexer_5_out,
       multiplexer_6_out, PC_4, ram_1_data, regifile_1_r1, shifter_1_out, shifter_2_out, shifter_3_out;

  Button \u_继续运行  (.out(Go));
  Button _1 (.out(IRA));
  Button _2 (.out(IRB));
  Button _3 (.out(IRC));
  LED #(.active("true")) led_1 (.in(W1));
  LED #(.active("true")) led_2 (.in(W2));
  LED #(.active("true")) led_3 (.in(W3));
  Priority_Encoder #(.select(2), .disabled("Z")) priority_encoder_1 (
    .in0(1'b1), .in1(jalr), .in2(jal), .in3(or_1_out), .out(priority_encoder_1_out), .en_in(1'b1));  // open: gs, en_out
  Multiplexer #(.select(2), .width(32), .disabled("Z"), .enable("false")) multiplexer_1 (
    .in0(PC_4), .in1(ALUresult), .in2(adder_3_out), .in3(adder_2_out), .out(multiplexer_1_out),
    .sel(priority_encoder_1_out));
  not not_1 (not_1_out, halt);
  Hex_Digit_Display hex_digit_display_1 (.value(LedData[31:28]));  // open: dp
  not not_2 (not_2_out, ALUequal);
  and and_1 (and_1_out, Beq, ALUequal);
  or or_1 (or_1_out, and_1_out, and_2_out, and_3_out);
  Register #(.width(32), .trigger("rising"), .Select("low")) u_PC (
    .D(multiplexer_1_out), .en(or_2_out), .Q(PC), .clk(CLK));  // open: clr
  or or_2 (or_2_out, not_1_out, Go);
  Hex_Digit_Display hex_digit_display_2 (.value(LedData[27:24]));  // open: dp
  Hex_Digit_Display hex_digit_display_3 (.value(LedData[23:20]));  // open: dp
  and and_2 (and_2_out, not_2_out, Bne);
  Hex_Digit_Display hex_digit_display_4 (.value(LedData[15:12]));  // open: dp
  Hex_Digit_Display hex_digit_display_5 (.value(LedData[19:16]));  // open: dp
  and and_3 (and_3_out, ALUge, \单周期硬布线控制器_1_bge );
  // RiscV_Probe riscv_probe_1: pin names not known; wires that end beside it: IR, riscv_probe_1_p2
  Adder #(.width(32)) adder_1 (.a(PC), .b(32'h4), .out(PC_4));  // open: cin, cout
  Hex_Digit_Display hex_digit_display_6 (.value(LedData[11:8]));  // open: dp
  Hex_Digit_Display hex_digit_display_7 (.value(LedData[7:4]));  // open: dp
  // Probe on \总周期数 
  ROM #(.addrWidth(10), .dataWidth(32), .Select("high")) rom_1 (.addr(PC[11:2]), .data(IR));
  Hex_Digit_Display hex_digit_display_8 (.value(LedData[3:0]));  // open: dp
  \单周期硬布线控制器  \u_单周期硬布线控制器_1  (
    .Funct({IR[30], IR[25], IR[14:12]}), .OP(IR[6:2]), .ALU_OP(\单周期硬布线控制器_1_alu_op ), .MemToReg(MemToReg),
    .MemWrite(MemWrite), .ALU_SRC(\单周期硬布线控制器_1_alu_src ), .RegWrite(RegWrite), .ecall(ecall), .S_type(Stype),
    .Jalr(jalr), .Beq(Beq), .JAL(jal), .Bne(Bne), .in_3(IR[21]), .uret(riscv_probe_1_p2), .U_type(Utype),
    .bge(\单周期硬布线控制器_1_bge ), .LBU(LBU));  // open: u2, u1, csr
  Multiplexer #(.select(1), .width(5), .disabled("Z"), .enable("false")) multiplexer_2 (
    .in0(IR[19:15]), .in1(5'b10001), .out(multiplexer_2_out), .sel(ecall));
  Multiplexer #(.select(1), .width(5), .disabled("Z"), .enable("false")) multiplexer_3 (
    .in0(IR[24:20]), .in1(5'b01010), .out(multiplexer_3_out), .sel(ecall));
  Multiplexer #(.select(1), .width(12), .disabled("Z"), .enable("false")) multiplexer_4 (
    .in0(IR[31:20]), .in1({IR[31:25], IR[11:7]}), .out(multiplexer_4_out), .sel(Stype));
  or or_3 (IR1_t, IR1, IRA);
  assign bit_extender_1_out = {{20{multiplexer_4_out[11]}}, multiplexer_4_out};  // Bit_Extender bit_extender_1
  assign bit_extender_2_out = {{12{IR[31]}}, IR[31:12]};  // Bit_Extender bit_extender_2
  assign bit_extender_3_out = {{20{IR[31]}}, {IR[31], IR[7], IR[30:25], IR[11:8]}};  // Bit_Extender bit_extender_3
  assign bit_extender_4_out = {{12{IR[31]}}, {IR[31], IR[19:12], IR[20], IR[30:21]}};  // Bit_Extender bit_extender_4
  or or_4 (IR2_t, IR2, IRB);
  Regifile regifile_1 (
    .Din(RDin), .Clk(CLK), .R1(regifile_1_r1), .R2(MDin), .WE(RegWrite), .W_num(IR[11:7]),
    .R1_num(multiplexer_2_out), .R2_num(multiplexer_3_out));
  Shifter #(.width(32), .shift("ll")) shifter_1 (.in(bit_extender_2_out), .\dist (5'b01100), .out(shifter_1_out));
  Shifter #(.width(32), .shift("ll")) shifter_2 (.in(bit_extender_3_out), .\dist (5'b00001), .out(shifter_2_out));
  Shifter #(.width(32), .shift("ll")) shifter_3 (.in(bit_extender_4_out), .\dist (5'b00001), .out(shifter_3_out));
  Multiplexer #(.select(1), .width(32), .disabled("Z"), .enable("false")) multiplexer_5 (
    .in0(MDin), .in1(bit_extender_1_out), .out(multiplexer_5_out), .sel(\单周期硬布线控制器_1_alu_src ));
  Adder #(.width(32)) adder_2 (.a(shifter_2_out), .b(PC), .out(adder_2_out));  // open: cin, cout
  Adder #(.width(32)) adder_3 (.a(shifter_3_out), .b(PC), .out(adder_3_out));  // open: cin, cout
  or or_5 (IR3_t, IR3, IRC);
  ALU alu_1 (
    .X(regifile_1_r1), .Y(multiplexer_5_out), .AluOP(\单周期硬布线控制器_1_alu_op ), .Equal(ALUequal),
    .Result(ALUresult), .out_4(ALUge));  // open: Result_2, out_6
  not not_3 (not_3_out, halt);
  Adder #(.width(32)) adder_4 (.a(shifter_1_out), .b(PC), .out(adder_4_out));  // open: cin, cout
  not not_4 (not_4_out, comparator_1_eq);
  Comparator #(.width(32), .mode("twosComplement")) comparator_1 (
    .a(regifile_1_r1), .b(32'h22), .eq(comparator_1_eq));  // open: gt, lt
  Counter #(.width(16), .max('hffff), .ongoal("wrap"), .trigger("rising"), .behavior("new")) counter_1 (
    .load(1'b0), .D({16{1'b0}}), .count(not_3_out), .Q(\总周期数 ), .clk(CLK), .clr(1'b0), .down(1'b0));  // open: carry, preset
  and and_4 (halt, ecall, not_4_out);
  and and_5 (and_5_out, comparator_1_eq, ecall);
  RAM #(.addrWidth(10), .dataWidth(32), .bus("separate"), .Select("high")) ram_1 (
    .addr(ALUresult[11:2]), .din(MDin), .data(ram_1_data), .str(MemWrite), .sel(1'b1), .clk(CLK), .ld(1'b1));  // open: clr
  Register #(.width(32), .trigger("rising"), .Select("low")) register_1 (
    .D(MDin), .en(and_5_out), .Q(LedData), .clk(CLK));  // open: clr
  Multiplexer #(.select(1), .width(32), .disabled("Z"), .enable("false")) multiplexer_6 (
    .in0(ram_1_data), .in1(LBUData), .out(multiplexer_6_out), .sel(LBU));
  D_Flip_Flop #(.trigger("high"), .Pre_Clr_Positions("LEGACY"), .NegatePresetClear("false"), .enable("true"), .NewFFLayout("false")) d_ff_1 (.Q(d_ff_1_q));  // open: clk, D, Qn, preset, en, reset
  // Probe on 13'h609
  or or_6 (or_6_out[0], Utype, MemToReg);
  Comparator #(.width(13), .mode("twosComplement")) comparator_2 (
    .a(CNT_num), .b(13'h609), .eq(comparator_2_eq), .lt(comparator_2_lt));  // open: gt
  Clock #(.highDuration(1), .lowDuration(1)) clock_1 (.out(clock_1_out));
  or or_7 (or_6_out[1], Utype, jal, jalr);
  Multiplexer #(.select(2), .width(32), .disabled("Z"), .enable("false")) multiplexer_7 (
    .in0(ALUresult), .in1(multiplexer_6_out), .in2(PC_4), .in3(adder_4_out), .out(RDin), .sel(or_6_out));
  Multiplexer #(.select(2), .width(8), .disabled("Z"), .enable("false")) multiplexer_8 (
    .in0(ram_1_data[7:0]), .in1(ram_1_data[15:8]), .in2(ram_1_data[23:16]), .in3(ram_1_data[31:24]),
    .out(multiplexer_8_out), .sel(ALUresult[1:0]));
  Counter #(.width(13), .max('h1fff), .ongoal("stay"), .trigger("rising"), .behavior("old")) counter_2 (
    .count(comparator_2_lt), .Q(CNT_num), .clk(clock_1_out));  // open: load, D, carry, clr, preset
  assign LBUData = {{24{1'b0}}, multiplexer_8_out};  // Bit_Extender bit_extender_5
  nand nand_1 (nand_1_out, d_ff_1_q, comparator_2_eq);
  assign CLK = nand_1_out ? clock_1_out : 1'bz;  // Controlled_Buffer controlled_buffer_1
  Pull_Resistor #(.pull(1)) pull_resistor_1 (.node(CLK));

  // Notes on the sheet:
  //   中断源
  //   中断等待指示
  //   数码管输出应该用寄存器锁存，否则显示数据只能一闪而过
  //   数码管输出
  //   指令探针
  //   指令存储器
  //   指令字
  //   contents of rom_1 (hex, n*v repeats v):
  //   100493 100006f 100493 200913 300993 100006f 100493 200913 300993 100006f 100493 200913 300993
  //   100006f 100493 200913 300993 3fc000ef 100413 100493 1f49493 900533 2200893 73 24d493 48463 fedff06f
  //   900533 2200893 73 100493 249493 900533 2200893 73 48463 fedff06f 100493 1f49493 900533 2200893 73
  //   4034d493 900533 2200893 73 4044d493 900533 2200893 73 4044d493 900533 2200893 73 4044d493 900533
  //   2200893 73 4044d493 900533 2200893 73 4044d493 900533 2200893 73 4044d493 900533 2200893 73 4044d493
  //   900533 2200893 73 100413 1f41993 41f9d993 433 c00913 300b13 140413 f47413 800293 100313 499993
  //   89e9b3 1300533 2200893 73 406282b3 fe0294e3 140413 f00f93 1f47433 1c41413 800293 100313 49d993
  //   89e9b3 1300533 2200893 73 406282b3 fe0294e3 1c45413 406b0b33 b0463 f95ff06f 2b3 fff2c293 829293
  //   ff2e293 500533 2200893 73 fff00413 493 84a023 140413 448493 84a023 140413 448493 84a023 140413
  //   448493 84a023 140413 448493 84a023 140413 448493 84a023 140413 448493 84a023 140413 448493 84a023
  //   140413 448493 84a023 140413 448493 84a023 140413 448493 84a023 140413 448493 84a023 140413 448493
  //   84a023 140413 448493 84a023 140413 448493 84a023 140413 448493 84a023 140413 448493 140413 433
  //   3c00493 42983 4aa03 149a2b3 28663 134a023 1442023 ffc48493 fe9412e3 800533 2200893 73 440413 3c00493
  //   fc9416e3 a00893 73 13 430497 900533 2200893 73 430497 900533 2200893 73 430497 900533 2200893 73
  //   430497 900533 2200893 73 430497 900533 2200893 73 430497 900533 2200893 73 430497 900533 2200893 73
  //   430497 900533 2200893 73 a00893 73 fff00293 313 1900413 841413 9700493 940533 2200893 73 5484b3
  //   494b313 fe0306e3 a00893 73 313 1000e13 8400493 849493 8348493 400913 891913 490913 849493 8248493
  //   849493 8148493 891913 490913 891913 490913 932023 12484b3 430313 fffe0e13 fe0e18e3 2000e13 313 34483
  //   900533 2200893 73 130313 fffe0e13 fe0e14e3 a00893 73 f00493 900533 2200893 73 fff48493 fe04d8e3
  //   a00893 73 413 140413 800533 2200893 73 240413 800533 2200893 73 340413 800533 2200893 73 440413
  //   800533 2200893 73 540413 800533 2200893 73 640413 800533 2200893 73 740413 800533 2200893 73 840413
  //   800533 2200893 2200893 73 8067
  //   JAL
  //   JALR
  //   URET
  //   BGE
  //   CSR
  //   rs1
  //   rs2
  //   rd
  //   I指令
  //   S指令
  //   U指令
  //   B指令
  //   J指令
  //   Beq
  //   Bne
  //   MemToReg
  //   MemWrite
  //   AluOP
  //   AluSrcB
  //   RegWrite
  //   为方便自动评测，需要输出PC，IR，寄存器堆写如数据RDin
  //   RAM写使能MemWrite、RAM写入数据MDin等信号
  //   数据存储器
  //   控制位
  //   暂停节拍，不能为0
  //   戳工具置1进入计数暂停模式，ctrl+k时钟自动运行到对应节拍暂停
  //   ctrl+k关闭时钟连续运行，将控制位置零，进入单步调试模式调试
  //   用这个时钟源需要去掉电路中的其他时钟源
  //   可计数暂停的时钟源
endmodule

// 运算器控制器
module \运算控制器自动生成  (
  input  OP2,
  input  OP3,
  input  OP4,
  input  OP5,
  input  OP6,
  input  F12,
  input  F13,
  input  F14,
  input  F25,
  input  F30,
  output S0,
  output S1,
  output S2,
  output S3
);

  wire and_1_out, and_2_out, and_3_out, and_4_out, and_5_out, and_6_out, and_7_out, and_8_out, and_9_out,
       and_10_out, and_11_out, and_12_out, and_13_out, and_14_out, and_15_out, and_16_out, and_17_out,
       and_18_out, and_19_out, and_20_out, and_21_out, and_22_out, and_23_out, and_24_out, and_25_out,
       and_26_out, and_27_out, and_28_out, and_29_out, and_30_out, and_31_out, and_32_out, and_33_out,
       and_34_out, and_35_out, and_36_out, and_37_out, and_38_out, and_39_out, and_40_out, and_41_out,
       and_42_out, and_43_out, and_44_out, and_45_out, and_46_out, and_47_out, and_48_out, and_49_out,
       not_1_out, not_2_out, not_3_out, not_4_out, not_5_out, not_6_out, not_7_out, not_8_out, not_9_out,
       not_10_out, not_11_out, not_12_out, not_13_out, not_14_out, not_15_out, not_16_out, not_17_out,
       not_18_out, not_19_out, not_20_out, not_21_out, not_22_out, not_23_out, not_24_out, not_25_out,
       not_26_out, not_27_out, not_28_out, not_29_out, not_30_out, not_31_out, not_32_out, not_33_out,
       not_34_out, not_35_out, not_36_out, not_37_out, not_38_out, not_39_out, not_40_out, not_41_out,
       not_42_out, not_43_out, not_44_out, not_45_out, not_46_out, not_47_out, not_48_out, not_49_out,
       not_50_out, not_51_out, not_52_out, not_53_out, not_54_out, not_55_out, not_56_out, not_57_out,
       not_58_out, not_59_out, not_60_out, not_61_out, not_62_out, not_63_out, not_64_out, not_65_out,
       not_66_out, not_67_out, not_68_out, not_69_out, not_70_out, not_71_out, not_72_out, not_73_out,
       not_74_out, not_75_out, not_76_out, not_77_out, not_78_out, not_79_out, not_80_out, not_81_out,
       not_82_out, not_83_out, not_84_out, not_85_out, not_86_out, not_87_out, not_88_out, not_89_out,
       not_90_out, not_91_out, not_92_out, not_93_out, not_94_out, not_95_out, not_96_out, not_97_out,
       not_98_out, not_99_out, not_100_out, not_101_out, not_102_out, not_103_out, not_104_out, not_105_out,
       not_106_out, not_107_out, not_108_out, not_109_out, not_110_out, not_111_out, not_112_out,
       not_113_out, not_114_out, not_115_out, not_116_out, not_117_out, not_118_out, not_119_out,
       not_120_out, not_121_out, not_122_out, not_123_out, not_124_out, not_125_out, not_126_out,
       not_127_out, not_128_out, not_129_out, not_130_out, not_131_out, not_132_out, not_133_out,
       not_134_out, not_135_out, not_136_out, not_137_out, not_138_out, not_139_out, not_140_out,
       not_141_out, not_142_out, not_143_out, not_144_out, not_145_out, not_146_out, not_147_out,
       not_148_out, not_149_out, not_150_out, not_151_out, not_152_out, not_153_out, not_154_out,
       not_155_out, not_156_out, not_157_out, not_158_out, not_159_out, not_160_out, not_161_out,
       not_162_out, not_163_out, not_164_out, not_165_out, not_166_out, not_167_out, not_168_out,
       not_169_out, not_170_out, not_171_out, not_172_out, not_173_out, not_174_out, not_175_out,
       not_176_out, not_177_out, not_178_out, not_179_out, not_180_out, not_181_out, not_182_out,
       not_183_out, not_184_out, not_185_out, not_186_out, not_187_out, not_188_out, not_189_out,
       not_190_out, not_191_out, not_192_out, not_193_out, not_194_out, not_195_out, not_196_out,
       not_197_out, not_198_out, not_199_out, not_200_out, not_201_out, not_202_out, not_203_out,
       not_204_out, not_205_out, not_206_out, not_207_out, not_208_out, not_209_out, not_210_out,
       not_211_out, not_212_out, not_213_out, not_214_out, not_215_out, not_216_out, not_217_out,
       not_218_out, not_219_out, not_220_out, not_221_out, not_222_out, not_223_out, not_224_out,
       not_225_out, not_226_out, not_227_out, not_228_out, not_229_out, not_230_out, not_231_out,
       not_232_out, not_233_out, not_234_out, not_235_out, not_236_out, not_237_out, not_238_out,
       not_239_out, not_240_out, not_241_out, not_242_out, not_243_out, not_244_out, not_245_out,
       not_246_out, not_247_out, not_248_out, not_249_out, not_250_out, not_251_out, not_252_out,
       not_253_out, not_254_out, not_255_out, not_256_out, not_257_out, not_258_out, not_259_out,
       not_260_out, not_261_out, not_262_out, not_263_out, not_264_out, not_265_out, not_266_out, not_267_out;

  not not_1 (not_1_out, F30);
  not not_2 (not_2_out, F25);
  not not_3 (not_3_out, F14);
  not not_4 (not_4_out, F13);
  not not_5 (not_5_out, F12);
  not not_6 (not_6_out, OP6);
  not not_7 (not_7_out, OP3);
  not not_8 (not_8_out, OP2);
  not not_9 (not_9_out, F30);
  not not_10 (not_10_out, F25);
  not not_11 (not_11_out, OP6);
  not not_12 (not_12_out, OP3);
  not not_13 (not_13_out, OP2);
  not not_14 (not_14_out, F30);
  not not_15 (not_15_out, F25);
  not not_16 (not_16_out, F14);
  not not_17 (not_17_out, F12);
  not not_18 (not_18_out, OP6);
  not not_19 (not_19_out, OP3);
  not not_20 (not_20_out, OP2);
  not not_21 (not_21_out, F14);
  not not_22 (not_22_out, F13);
  not not_23 (not_23_out, F12);
  not not_24 (not_24_out, OP6);
  not not_25 (not_25_out, OP5);
  not not_26 (not_26_out, OP3);
  not not_27 (not_27_out, OP2);
  not not_28 (not_28_out, OP6);
  not not_29 (not_29_out, OP5);
  not not_30 (not_30_out, OP3);
  not not_31 (not_31_out, OP2);
  not not_32 (not_32_out, F13);
  not not_33 (not_33_out, F12);
  not not_34 (not_34_out, OP6);
  not not_35 (not_35_out, OP5);
  not not_36 (not_36_out, OP3);
  not not_37 (not_37_out, OP2);
  not not_38 (not_38_out, F14);
  not not_39 (not_39_out, F12);
  not not_40 (not_40_out, OP6);
  not not_41 (not_41_out, OP5);
  not not_42 (not_42_out, OP3);
  not not_43 (not_43_out, OP2);
  not not_44 (not_44_out, F25);
  not not_45 (not_45_out, F13);
  not not_46 (not_46_out, OP6);
  not not_47 (not_47_out, OP5);
  not not_48 (not_48_out, OP3);
  not not_49 (not_49_out, OP2);
  not not_50 (not_50_out, F14);
  not not_51 (not_51_out, F12);
  not not_52 (not_52_out, OP6);
  not not_53 (not_53_out, OP5);
  not not_54 (not_54_out, OP4);
  not not_55 (not_55_out, OP3);
  not not_56 (not_56_out, OP2);
  not not_57 (not_57_out, F14);
  not not_58 (not_58_out, F12);
  not not_59 (not_59_out, OP6);
  not not_60 (not_60_out, OP4);
  not not_61 (not_61_out, OP3);
  not not_62 (not_62_out, OP2);
  not not_63 (not_63_out, OP3);
  not not_64 (not_64_out, OP2);
  not not_65 (not_65_out, OP6);
  not not_66 (not_66_out, OP5);
  not not_67 (not_67_out, OP3);
  not not_68 (not_68_out, F13);
  not not_69 (not_69_out, F12);
  not not_70 (not_70_out, OP6);
  not not_71 (not_71_out, OP5);
  not not_72 (not_72_out, OP4);
  not not_73 (not_73_out, OP3);
  not not_74 (not_74_out, OP2);
  not not_75 (not_75_out, F13);
  not not_76 (not_76_out, OP4);
  not not_77 (not_77_out, OP3);
  not not_78 (not_78_out, OP2);
  not not_79 (not_79_out, F25);
  not not_80 (not_80_out, F14);
  not not_81 (not_81_out, F13);
  not not_82 (not_82_out, F12);
  not not_83 (not_83_out, OP6);
  not not_84 (not_84_out, OP3);
  not not_85 (not_85_out, OP2);
  not not_86 (not_86_out, F30);
  not not_87 (not_87_out, F25);
  not not_88 (not_88_out, OP6);
  not not_89 (not_89_out, OP3);
  not not_90 (not_90_out, OP2);
  not not_91 (not_91_out, F30);
  not not_92 (not_92_out, F25);
  not not_93 (not_93_out, F14);
  not not_94 (not_94_out, F12);
  not not_95 (not_95_out, OP6);
  not not_96 (not_96_out, OP3);
  not not_97 (not_97_out, OP2);
  not not_98 (not_98_out, OP6);
  not not_99 (not_99_out, OP5);
  not not_100 (not_100_out, OP3);
  not not_101 (not_101_out, OP2);
  not not_102 (not_102_out, F14);
  not not_103 (not_103_out, F12);
  not not_104 (not_104_out, OP6);
  not not_105 (not_105_out, OP5);
  not not_106 (not_106_out, OP3);
  not not_107 (not_107_out, OP2);
  not not_108 (not_108_out, F30);
  not not_109 (not_109_out, F25);
  not not_110 (not_110_out, F13);
  not not_111 (not_111_out, OP6);
  not not_112 (not_112_out, OP5);
  not not_113 (not_113_out, OP3);
  not not_114 (not_114_out, OP2);
  not not_115 (not_115_out, F14);
  not not_116 (not_116_out, F13);
  not not_117 (not_117_out, F12);
  not not_118 (not_118_out, OP4);
  not not_119 (not_119_out, OP3);
  not not_120 (not_120_out, OP2);
  not not_121 (not_121_out, F14);
  not not_122 (not_122_out, F13);
  not not_123 (not_123_out, OP4);
  not not_124 (not_124_out, OP3);
  not not_125 (not_125_out, OP2);
  not not_126 (not_126_out, F14);
  not not_127 (not_127_out, F13);
  not not_128 (not_128_out, F12);
  not not_129 (not_129_out, OP4);
  not not_130 (not_130_out, OP3);
  not not_131 (not_131_out, OP3);
  not not_132 (not_132_out, OP2);
  not not_133 (not_133_out, F13);
  not not_134 (not_134_out, OP4);
  not not_135 (not_135_out, OP3);
  not not_136 (not_136_out, OP2);
  not not_137 (not_137_out, F30);
  not not_138 (not_138_out, F25);
  not not_139 (not_139_out, F14);
  not not_140 (not_140_out, F13);
  not not_141 (not_141_out, F12);
  not not_142 (not_142_out, OP6);
  not not_143 (not_143_out, OP3);
  not not_144 (not_144_out, OP2);
  not not_145 (not_145_out, F25);
  not not_146 (not_146_out, F14);
  not not_147 (not_147_out, F13);
  not not_148 (not_148_out, F12);
  not not_149 (not_149_out, OP6);
  not not_150 (not_150_out, OP3);
  not not_151 (not_151_out, OP2);
  not not_152 (not_152_out, F30);
  not not_153 (not_153_out, F25);
  not not_154 (not_154_out, OP6);
  not not_155 (not_155_out, OP3);
  not not_156 (not_156_out, OP2);
  not not_157 (not_157_out, F30);
  not not_158 (not_158_out, F25);
  not not_159 (not_159_out, F14);
  not not_160 (not_160_out, OP6);
  not not_161 (not_161_out, OP3);
  not not_162 (not_162_out, OP2);
  not not_163 (not_163_out, F14);
  not not_164 (not_164_out, F13);
  not not_165 (not_165_out, F12);
  not not_166 (not_166_out, OP6);
  not not_167 (not_167_out, OP5);
  not not_168 (not_168_out, OP3);
  not not_169 (not_169_out, OP2);
  not not_170 (not_170_out, OP6);
  not not_171 (not_171_out, OP5);
  not not_172 (not_172_out, OP3);
  not not_173 (not_173_out, OP2);
  not not_174 (not_174_out, F14);
  not not_175 (not_175_out, F12);
  not not_176 (not_176_out, OP6);
  not not_177 (not_177_out, OP5);
  not not_178 (not_178_out, OP4);
  not not_179 (not_179_out, OP3);
  not not_180 (not_180_out, OP2);
  not not_181 (not_181_out, F14);
  not not_182 (not_182_out, F12);
  not not_183 (not_183_out, OP6);
  not not_184 (not_184_out, OP4);
  not not_185 (not_185_out, OP3);
  not not_186 (not_186_out, OP2);
  not not_187 (not_187_out, F14);
  not not_188 (not_188_out, F13);
  not not_189 (not_189_out, F12);
  not not_190 (not_190_out, OP4);
  not not_191 (not_191_out, OP3);
  not not_192 (not_192_out, OP2);
  not not_193 (not_193_out, F14);
  not not_194 (not_194_out, F13);
  not not_195 (not_195_out, OP4);
  not not_196 (not_196_out, OP3);
  not not_197 (not_197_out, OP2);
  not not_198 (not_198_out, F14);
  not not_199 (not_199_out, F13);
  not not_200 (not_200_out, F12);
  not not_201 (not_201_out, OP4);
  not not_202 (not_202_out, OP3);
  not not_203 (not_203_out, OP3);
  not not_204 (not_204_out, OP2);
  not not_205 (not_205_out, OP6);
  not not_206 (not_206_out, OP5);
  not not_207 (not_207_out, OP3);
  not not_208 (not_208_out, F14);
  not not_209 (not_209_out, OP6);
  not not_210 (not_210_out, OP5);
  not not_211 (not_211_out, OP3);
  not not_212 (not_212_out, OP2);
  not not_213 (not_213_out, F13);
  not not_214 (not_214_out, F12);
  not not_215 (not_215_out, OP6);
  not not_216 (not_216_out, OP5);
  not not_217 (not_217_out, OP4);
  not not_218 (not_218_out, OP3);
  not not_219 (not_219_out, OP2);
  not not_220 (not_220_out, F30);
  not not_221 (not_221_out, F25);
  not not_222 (not_222_out, F12);
  not not_223 (not_223_out, OP6);
  not not_224 (not_224_out, OP3);
  not not_225 (not_225_out, OP2);
  not not_226 (not_226_out, F30);
  not not_227 (not_227_out, F25);
  not not_228 (not_228_out, F14);
  not not_229 (not_229_out, F12);
  not not_230 (not_230_out, OP6);
  not not_231 (not_231_out, OP3);
  not not_232 (not_232_out, OP2);
  not not_233 (not_233_out, F30);
  not not_234 (not_234_out, F25);
  not not_235 (not_235_out, F14);
  not not_236 (not_236_out, OP6);
  not not_237 (not_237_out, OP3);
  not not_238 (not_238_out, OP2);
  not not_239 (not_239_out, F12);
  not not_240 (not_240_out, OP6);
  not not_241 (not_241_out, OP5);
  not not_242 (not_242_out, OP3);
  not not_243 (not_243_out, OP2);
  not not_244 (not_244_out, F13);
  not not_245 (not_245_out, F12);
  not not_246 (not_246_out, OP6);
  not not_247 (not_247_out, OP5);
  not not_248 (not_248_out, OP3);
  not not_249 (not_249_out, OP2);
  not not_250 (not_250_out, F14);
  not not_251 (not_251_out, F12);
  not not_252 (not_252_out, OP6);
  not not_253 (not_253_out, OP5);
  not not_254 (not_254_out, OP3);
  not not_255 (not_255_out, OP2);
  not not_256 (not_256_out, F12);
  not not_257 (not_257_out, OP3);
  not not_258 (not_258_out, OP2);
  not not_259 (not_259_out, F14);
  not not_260 (not_260_out, OP6);
  not not_261 (not_261_out, OP5);
  not not_262 (not_262_out, OP3);
  not not_263 (not_263_out, OP2);
  not not_264 (not_264_out, F13);
  not not_265 (not_265_out, OP4);
  not not_266 (not_266_out, OP3);
  not not_267 (not_267_out, OP2);
  and and_1 (and_1_out, not_1_out, not_2_out, not_3_out, not_4_out, not_5_out, not_6_out, OP5, OP4, not_7_out, not_8_out);
  and and_2 (and_2_out, not_9_out, not_10_out, F14, F13, F12, not_11_out, OP5, OP4, not_12_out, not_13_out);
  and and_3 (and_3_out, not_14_out, not_15_out, not_16_out, F13, not_17_out, not_18_out, OP5, OP4, not_19_out, not_20_out);
  and and_4 (and_4_out, not_21_out, not_22_out, not_23_out, not_24_out, not_25_out, OP4, not_26_out, not_27_out);
  and and_5 (and_5_out, F14, F13, F12, not_28_out, not_29_out, OP4, not_30_out, not_31_out);
  and and_6 (and_6_out, F14, not_32_out, not_33_out, not_34_out, not_35_out, OP4, not_36_out, not_37_out);
  and and_7 (and_7_out, not_38_out, F13, not_39_out, not_40_out, not_41_out, OP4, not_42_out, not_43_out);
  and and_8 (and_8_out, F30, not_44_out, F14, not_45_out, F12, not_46_out, not_47_out, OP4, not_48_out, not_49_out);
  and and_9 (and_9_out, not_50_out, F13, not_51_out, not_52_out, not_53_out, not_54_out, not_55_out, not_56_out);
  and and_10 (and_10_out, not_57_out, F13, not_58_out, not_59_out, OP5, not_60_out, not_61_out, not_62_out);
  and and_11 (and_11_out, F14, F13, F12, OP6, OP5, OP4, not_63_out, not_64_out);
  and and_12 (and_12_out, not_65_out, not_66_out, OP4, not_67_out, OP2);
  and and_13 (and_13_out, F14, not_68_out, not_69_out, not_70_out, not_71_out, not_72_out, not_73_out, not_74_out);
  and and_14 (and_14_out, F14, not_75_out, F12, OP6, OP5, not_76_out, not_77_out, not_78_out);
  and and_15 (and_15_out, F30, not_79_out, not_80_out, not_81_out, not_82_out, not_83_out, OP5, OP4, not_84_out, not_85_out);
  and and_16 (and_16_out, not_86_out, not_87_out, F14, F13, F12, not_88_out, OP5, OP4, not_89_out, not_90_out);
  and and_17 (and_17_out, not_91_out, not_92_out, not_93_out, F13, not_94_out, not_95_out, OP5, OP4, not_96_out, not_97_out);
  and and_18 (and_18_out, F14, F13, F12, not_98_out, not_99_out, OP4, not_100_out, not_101_out);
  and and_19 (and_19_out, not_102_out, F13, not_103_out, not_104_out, not_105_out, OP4, not_106_out, not_107_out);
  and and_20 (and_20_out, not_108_out, not_109_out, F14, not_110_out, F12, not_111_out, not_112_out, OP4, not_113_out, not_114_out);
  and and_21 (and_21_out, not_115_out, not_116_out, not_117_out, OP6, OP5, not_118_out, not_119_out, not_120_out);
  and and_22 (and_22_out, not_121_out, not_122_out, F12, OP6, OP5, not_123_out, not_124_out, not_125_out);
  and and_23 (and_23_out, not_126_out, not_127_out, not_128_out, OP6, OP5, not_129_out, not_130_out, OP2);
  and and_24 (and_24_out, F14, F13, F12, OP6, OP5, OP4, not_131_out, not_132_out);
  and and_25 (and_25_out, F14, not_133_out, F12, OP6, OP5, not_134_out, not_135_out, not_136_out);
  and and_26 (and_26_out, not_137_out, not_138_out, not_139_out, not_140_out, not_141_out, not_142_out, OP5, OP4, not_143_out, not_144_out);
  and and_27 (and_27_out, F30, not_145_out, not_146_out, not_147_out, not_148_out, not_149_out, OP5, OP4, not_150_out, not_151_out);
  and and_28 (and_28_out, not_152_out, not_153_out, F14, F13, F12, not_154_out, OP5, OP4, not_155_out, not_156_out);
  and and_29 (and_29_out, not_157_out, not_158_out, not_159_out, F13, F12, not_160_out, OP5, OP4, not_161_out, not_162_out);
  and and_30 (and_30_out, not_163_out, not_164_out, not_165_out, not_166_out, not_167_out, OP4, not_168_out, not_169_out);
  and and_31 (and_31_out, F14, F13, F12, not_170_out, not_171_out, OP4, not_172_out, not_173_out);
  and and_32 (and_32_out, not_174_out, F13, not_175_out, not_176_out, not_177_out, not_178_out, not_179_out, not_180_out);
  and and_33 (and_33_out, not_181_out, F13, not_182_out, not_183_out, OP5, not_184_out, not_185_out, not_186_out);
  and and_34 (and_34_out, not_187_out, not_188_out, not_189_out, OP6, OP5, not_190_out, not_191_out, not_192_out);
  and and_35 (and_35_out, not_193_out, not_194_out, F12, OP6, OP5, not_195_out, not_196_out, not_197_out);
  and and_36 (and_36_out, not_198_out, not_199_out, not_200_out, OP6, OP5, not_201_out, not_202_out, OP2);
  and and_37 (and_37_out, F14, F13, F12, OP6, OP5, OP4, not_203_out, not_204_out);
  and and_38 (and_38_out, not_205_out, not_206_out, OP4, not_207_out, OP2);
  and and_39 (and_39_out, not_208_out, F13, F12, not_209_out, not_210_out, OP4, not_211_out, not_212_out);
  and and_40 (and_40_out, F14, not_213_out, not_214_out, not_215_out, not_216_out, not_217_out, not_218_out, not_219_out);
  and and_41 (and_41_out, not_220_out, not_221_out, F14, F13, not_222_out, not_223_out, OP5, OP4, not_224_out, not_225_out);
  and and_42 (and_42_out, not_226_out, not_227_out, not_228_out, F13, not_229_out, not_230_out, OP5, OP4, not_231_out, not_232_out);
  and and_43 (and_43_out, not_233_out, not_234_out, not_235_out, F13, F12, not_236_out, OP5, OP4, not_237_out, not_238_out);
  and and_44 (and_44_out, F14, F13, not_239_out, not_240_out, not_241_out, OP4, not_242_out, not_243_out);
  and and_45 (and_45_out, F14, not_244_out, not_245_out, not_246_out, not_247_out, OP4, not_248_out, not_249_out);
  and and_46 (and_46_out, not_250_out, F13, not_251_out, not_252_out, not_253_out, OP4, not_254_out, not_255_out);
  and and_47 (and_47_out, F14, F13, not_256_out, OP6, OP5, OP4, not_257_out, not_258_out);
  and and_48 (and_48_out, not_259_out, F13, F12, not_260_out, not_261_out, OP4, not_262_out, not_263_out);
  and and_49 (and_49_out, F14, not_264_out, F12, OP6, OP5, not_265_out, not_266_out, not_267_out);
  or or_1 (S0, and_1_out, and_2_out, and_3_out, and_4_out, and_5_out, and_6_out, and_7_out, and_8_out, and_9_out, and_10_out, and_11_out, and_12_out, and_13_out, and_14_out);
  or or_2 (S1, and_15_out, and_16_out, and_17_out, and_18_out, and_19_out, and_20_out, and_21_out, and_22_out, and_23_out, and_24_out, and_25_out);
  or or_3 (S2, and_26_out, and_27_out, and_28_out, and_29_out, and_30_out, and_31_out, and_32_out, and_33_out, and_34_out, and_35_out, and_36_out, and_37_out, and_38_out, and_39_out, and_40_out);
  or or_4 (S3, and_41_out, and_42_out, and_43_out, and_44_out, and_45_out, and_46_out, and_47_out, and_48_out, and_49_out);
endmodule

// 控制信号生成
module \控制信号自动生成  (
  input  OP2,
  input  OP3,
  input  OP4,
  input  OP5,
  input  OP6,
  input  F12,
  input  F13,
  input  F14,
  input  F25,
  input  F30,
  output MemToReg,
  output MemWrite,
  output ALU_SRC,
  output RegWrite,
  output ecall,
  output S_Type,
  output BEQ,
  output BNE,
  output JALR,
  output JAL,
  output csr,
  output bge,
  output U_Type,
  output u1,
  output u2,
  output LBU
);

  wire and_1_out, and_2_out, and_4_out, and_5_out, and_6_out, and_7_out, and_8_out, and_9_out, and_10_out,
       and_11_out, and_12_out, and_13_out, and_14_out, and_15_out, and_16_out, and_17_out, and_18_out,
       and_19_out, and_20_out, and_21_out, and_22_out, and_23_out, and_33_out, and_34_out, and_35_out,
       and_36_out, and_37_out, and_38_out, and_39_out, and_40_out, and_41_out, and_42_out, and_43_out,
       and_44_out, and_45_out, and_46_out, and_47_out, and_48_out, not_1_out, not_2_out, not_3_out,
       not_4_out, not_5_out, not_6_out, not_7_out, not_8_out, not_9_out, not_10_out, not_11_out, not_12_out,
       not_13_out, not_14_out, not_15_out, not_16_out, not_17_out, not_18_out, not_19_out, not_20_out,
       not_21_out, not_22_out, not_23_out, not_24_out, not_25_out, not_26_out, not_27_out, not_28_out,
       not_29_out, not_30_out, not_31_out, not_32_out, not_33_out, not_34_out, not_35_out, not_36_out,
       not_37_out, not_38_out, not_39_out, not_40_out, not_41_out, not_42_out, not_43_out, not_44_out,
       not_45_out, not_46_out, not_47_out, not_48_out, not_49_out, not_50_out, not_51_out, not_52_out,
       not_53_out, not_54_out, not_55_out, not_56_out, not_57_out, not_58_out, not_59_out, not_60_out,
       not_61_out, not_62_out, not_63_out, not_64_out, not_65_out, not_66_out, not_67_out, not_68_out,
       not_69_out, not_70_out, not_71_out, not_72_out, not_73_out, not_74_out, not_75_out, not_76_out,
       not_77_out, not_78_out, not_79_out, not_80_out, not_81_out, not_82_out, not_83_out, not_84_out,
       not_85_out, not_86_out, not_87_out, not_88_out, not_89_out, not_90_out, not_91_out, not_92_out,
       not_93_out, not_94_out, not_95_out, not_96_out, not_97_out, not_98_out, not_99_out, not_100_out,
       not_101_out, not_102_out, not_103_out, not_104_out, not_105_out, not_106_out, not_107_out,
       not_108_out, not_109_out, not_110_out, not_111_out, not_112_out, not_113_out, not_114_out,
       not_115_out, not_116_out, not_117_out, not_118_out, not_119_out, not_120_out, not_121_out,
       not_122_out, not_123_out, not_124_out, not_125_out, not_126_out, not_127_out, not_128_out,
       not_129_out, not_130_out, not_131_out, not_132_out, not_133_out, not_134_out, not_135_out,
       not_136_out, not_137_out, not_138_out, not_139_out, not_140_out, not_141_out, not_142_out,
       not_143_out, not_144_out, not_145_out, not_146_out, not_147_out, not_148_out, not_149_out,
       not_150_out, not_151_out, not_152_out, not_153_out, not_154_out, not_155_out, not_156_out,
       not_157_out, not_158_out, not_159_out, not_160_out, not_161_out, not_162_out, not_163_out,
       not_164_out, not_165_out, not_166_out, not_167_out, not_168_out, not_169_out, not_170_out,
       not_171_out, not_172_out, not_173_out, not_174_out, not_175_out, not_176_out, not_177_out,
       not_178_out, not_179_out, not_180_out, not_181_out, not_182_out, not_183_out, not_184_out,
       not_185_out, not_186_out, not_187_out, not_188_out, not_189_out, not_190_out, not_191_out,
       not_192_out, not_193_out, not_194_out, not_195_out, not_196_out, not_197_out, not_198_out,
       not_199_out, not_200_out, not_201_out, not_202_out, not_203_out, not_204_out, not_205_out,
       not_206_out, not_207_out, not_208_out, not_209_out, not_210_out, not_211_out, not_212_out,
       not_213_out, not_214_out, not_215_out, not_216_out, not_217_out, not_218_out, not_219_out,
       not_220_out, not_221_out, not_222_out, not_223_out, not_224_out, not_225_out, not_226_out,
       not_227_out, not_228_out, not_229_out, not_230_out, not_231_out;

  not not_1 (not_1_out, OP2);
  not not_2 (not_2_out, OP3);
  not not_3 (not_3_out, OP4);
  not not_4 (not_4_out, OP5);
  not not_5 (not_5_out, OP6);
  not not_6 (not_6_out, F12);
  not not_7 (not_7_out, F13);
  not not_8 (not_8_out, OP2);
  not not_9 (not_9_out, OP3);
  not not_10 (not_10_out, OP4);
  not not_11 (not_11_out, OP5);
  not not_12 (not_12_out, OP6);
  not not_13 (not_13_out, F12);
  not not_14 (not_14_out, F14);
  not not_15 (not_15_out, OP2);
  not not_16 (not_16_out, OP3);
  not not_17 (not_17_out, OP4);
  not not_18 (not_18_out, OP6);
  not not_19 (not_19_out, F12);
  not not_20 (not_20_out, F14);
  not not_21 (not_21_out, OP2);
  not not_22 (not_22_out, OP3);
  not not_23 (not_23_out, OP5);
  not not_24 (not_24_out, OP6);
  not not_25 (not_25_out, F12);
  not not_26 (not_26_out, F13);
  not not_27 (not_27_out, OP2);
  not not_28 (not_28_out, OP3);
  not not_29 (not_29_out, OP4);
  not not_30 (not_30_out, OP6);
  not not_31 (not_31_out, F12);
  not not_32 (not_32_out, F14);
  not not_33 (not_33_out, OP3);
  not not_34 (not_34_out, OP5);
  not not_35 (not_35_out, OP6);
  not not_36 (not_36_out, F12);
  not not_37 (not_37_out, OP3);
  not not_38 (not_38_out, OP5);
  not not_39 (not_39_out, OP6);
  not not_40 (not_40_out, F25);
  not not_41 (not_41_out, F30);
  not not_42 (not_42_out, OP3);
  not not_43 (not_43_out, OP5);
  not not_44 (not_44_out, OP6);
  not not_45 (not_45_out, F25);
  not not_46 (not_46_out, OP3);
  not not_47 (not_47_out, OP5);
  not not_48 (not_48_out, OP6);
  not not_49 (not_49_out, OP2);
  not not_50 (not_50_out, OP3);
  not not_51 (not_51_out, OP3);
  not not_52 (not_52_out, OP4);
  not not_53 (not_53_out, F12);
  not not_54 (not_54_out, F13);
  not not_55 (not_55_out, F14);
  not not_56 (not_56_out, OP3);
  not not_57 (not_57_out, OP5);
  not not_58 (not_58_out, OP6);
  not not_59 (not_59_out, OP2);
  not not_60 (not_60_out, OP3);
  not not_61 (not_61_out, OP5);
  not not_62 (not_62_out, OP6);
  not not_63 (not_63_out, F12);
  not not_64 (not_64_out, F13);
  not not_65 (not_65_out, OP2);
  not not_66 (not_66_out, OP3);
  not not_67 (not_67_out, OP5);
  not not_68 (not_68_out, OP6);
  not not_69 (not_69_out, F12);
  not not_70 (not_70_out, F14);
  not not_71 (not_71_out, OP2);
  not not_72 (not_72_out, OP3);
  not not_73 (not_73_out, OP6);
  not not_74 (not_74_out, F12);
  not not_75 (not_75_out, F13);
  not not_76 (not_76_out, F14);
  not not_77 (not_77_out, F25);
  not not_78 (not_78_out, OP3);
  not not_79 (not_79_out, OP5);
  not not_80 (not_80_out, OP6);
  not not_81 (not_81_out, F12);
  not not_82 (not_82_out, OP3);
  not not_83 (not_83_out, OP5);
  not not_84 (not_84_out, OP6);
  not not_85 (not_85_out, F25);
  not not_86 (not_86_out, F30);
  not not_87 (not_87_out, OP3);
  not not_88 (not_88_out, OP5);
  not not_89 (not_89_out, OP6);
  not not_90 (not_90_out, F25);
  not not_91 (not_91_out, OP2);
  not not_92 (not_92_out, OP3);
  not not_93 (not_93_out, OP6);
  not not_94 (not_94_out, F25);
  not not_95 (not_95_out, F30);
  not not_96 (not_96_out, OP3);
  not not_97 (not_97_out, OP5);
  not not_98 (not_98_out, OP6);
  not not_99 (not_99_out, OP4);
  not not_100 (not_100_out, F12);
  not not_101 (not_101_out, F13);
  not not_102 (not_102_out, F14);
  not not_103 (not_103_out, OP3);
  not not_104 (not_104_out, OP5);
  not not_105 (not_105_out, OP6);
  not not_106 (not_106_out, OP4);
  not not_107 (not_107_out, OP2);
  not not_108 (not_108_out, OP3);
  not not_109 (not_109_out, F12);
  not not_110 (not_110_out, F13);
  not not_111 (not_111_out, F14);
  not not_112 (not_112_out, F25);
  not not_113 (not_113_out, F30);
  not not_114 (not_114_out, OP2);
  not not_115 (not_115_out, OP3);
  not not_116 (not_116_out, OP4);
  not not_117 (not_117_out, OP6);
  not not_118 (not_118_out, F12);
  not not_119 (not_119_out, F14);
  not not_120 (not_120_out, OP2);
  not not_121 (not_121_out, OP3);
  not not_122 (not_122_out, OP4);
  not not_123 (not_123_out, F12);
  not not_124 (not_124_out, F13);
  not not_125 (not_125_out, F14);
  not not_126 (not_126_out, OP2);
  not not_127 (not_127_out, OP3);
  not not_128 (not_128_out, OP4);
  not not_129 (not_129_out, F13);
  not not_130 (not_130_out, F14);
  not not_131 (not_131_out, OP3);
  not not_132 (not_132_out, OP4);
  not not_133 (not_133_out, F12);
  not not_134 (not_134_out, F13);
  not not_135 (not_135_out, F14);
  not not_136 (not_136_out, OP4);
  not not_137 (not_137_out, OP2);
  not not_138 (not_138_out, OP3);
  not not_139 (not_139_out, OP2);
  not not_140 (not_140_out, OP3);
  not not_141 (not_141_out, OP4);
  not not_142 (not_142_out, F13);
  not not_143 (not_143_out, OP3);
  not not_144 (not_144_out, OP5);
  not not_145 (not_145_out, OP6);
  not not_146 (not_146_out, OP2);
  not not_147 (not_147_out, OP3);
  not not_148 (not_148_out, OP5);
  not not_149 (not_149_out, OP6);
  not not_150 (not_150_out, F12);
  not not_151 (not_151_out, F13);
  not not_152 (not_152_out, OP2);
  not not_153 (not_153_out, OP3);
  not not_154 (not_154_out, OP4);
  not not_155 (not_155_out, OP6);
  not not_156 (not_156_out, F12);
  not not_157 (not_157_out, F14);
  not not_158 (not_158_out, OP3);
  not not_159 (not_159_out, OP4);
  not not_160 (not_160_out, F12);
  not not_161 (not_161_out, F13);
  not not_162 (not_162_out, F14);
  not not_163 (not_163_out, OP2);
  not not_164 (not_164_out, OP3);
  not not_165 (not_165_out, OP4);
  not not_166 (not_166_out, F13);
  not not_167 (not_167_out, OP2);
  not not_168 (not_168_out, OP3);
  not not_169 (not_169_out, OP6);
  not not_170 (not_170_out, F12);
  not not_171 (not_171_out, F13);
  not not_172 (not_172_out, F14);
  not not_173 (not_173_out, F25);
  not not_174 (not_174_out, OP3);
  not not_175 (not_175_out, OP5);
  not not_176 (not_176_out, OP6);
  not not_177 (not_177_out, F12);
  not not_178 (not_178_out, OP3);
  not not_179 (not_179_out, OP5);
  not not_180 (not_180_out, OP6);
  not not_181 (not_181_out, F25);
  not not_182 (not_182_out, F30);
  not not_183 (not_183_out, OP3);
  not not_184 (not_184_out, OP5);
  not not_185 (not_185_out, OP6);
  not not_186 (not_186_out, F25);
  not not_187 (not_187_out, OP2);
  not not_188 (not_188_out, OP3);
  not not_189 (not_189_out, OP6);
  not not_190 (not_190_out, F25);
  not not_191 (not_191_out, F30);
  not not_192 (not_192_out, OP3);
  not not_193 (not_193_out, OP5);
  not not_194 (not_194_out, OP6);
  not not_195 (not_195_out, OP3);
  not not_196 (not_196_out, OP5);
  not not_197 (not_197_out, OP6);
  not not_198 (not_198_out, OP2);
  not not_199 (not_199_out, OP3);
  not not_200 (not_200_out, OP4);
  not not_201 (not_201_out, OP6);
  not not_202 (not_202_out, F12);
  not not_203 (not_203_out, F14);
  not not_204 (not_204_out, OP2);
  not not_205 (not_205_out, OP3);
  not not_206 (not_206_out, OP4);
  not not_207 (not_207_out, F13);
  not not_208 (not_208_out, F14);
  not not_209 (not_209_out, OP2);
  not not_210 (not_210_out, OP3);
  not not_211 (not_211_out, OP4);
  not not_212 (not_212_out, F13);
  not not_213 (not_213_out, OP2);
  not not_214 (not_214_out, OP3);
  not not_215 (not_215_out, OP6);
  not not_216 (not_216_out, F12);
  not not_217 (not_217_out, F13);
  not not_218 (not_218_out, F14);
  not not_219 (not_219_out, F25);
  not not_220 (not_220_out, OP2);
  not not_221 (not_221_out, OP3);
  not not_222 (not_222_out, OP6);
  not not_223 (not_223_out, F25);
  not not_224 (not_224_out, F30);
  not not_225 (not_225_out, F13);
  not not_226 (not_226_out, F12);
  not not_227 (not_227_out, OP6);
  not not_228 (not_228_out, OP5);
  not not_229 (not_229_out, OP4);
  not not_230 (not_230_out, OP3);
  not not_231 (not_231_out, OP2);
  and and_1 (and_1_out, not_1_out, not_2_out, not_3_out, not_4_out, not_5_out, not_6_out, not_7_out, F14);
  and and_2 (and_2_out, not_8_out, not_9_out, not_10_out, not_11_out, not_12_out, not_13_out, F13, not_14_out);
  and and_3 (MemWrite, not_15_out, not_16_out, not_17_out, OP5, not_18_out, not_19_out, F13, not_20_out);
  and and_4 (and_4_out, not_21_out, not_22_out, not_23_out, not_24_out, not_25_out, not_26_out, F14);
  and and_5 (and_5_out, not_27_out, not_28_out, not_29_out, not_30_out, not_31_out, F13, not_32_out);
  and and_6 (and_6_out, not_33_out, OP4, not_34_out, not_35_out, not_36_out);
  and and_7 (and_7_out, not_37_out, OP4, not_38_out, not_39_out, not_40_out, not_41_out);
  and and_8 (and_8_out, not_42_out, OP4, not_43_out, not_44_out, F14, not_45_out);
  and and_9 (and_9_out, not_46_out, OP4, not_47_out, not_48_out, F13);
  and and_10 (and_10_out, not_49_out, not_50_out, OP4, OP5, OP6, F13, F14);
  and and_11 (and_11_out, OP2, not_51_out, not_52_out, OP5, OP6, not_53_out, not_54_out, not_55_out);
  and and_12 (and_12_out, OP2, not_56_out, OP4, not_57_out, not_58_out);
  and and_13 (and_13_out, not_59_out, not_60_out, not_61_out, not_62_out, not_63_out, not_64_out, F14);
  and and_14 (and_14_out, not_65_out, not_66_out, not_67_out, not_68_out, not_69_out, F13, not_70_out);
  and and_15 (and_15_out, not_71_out, not_72_out, OP4, not_73_out, not_74_out, not_75_out, not_76_out, not_77_out);
  and and_16 (and_16_out, not_78_out, OP4, not_79_out, not_80_out, not_81_out);
  and and_17 (and_17_out, not_82_out, OP4, not_83_out, not_84_out, not_85_out, not_86_out);
  and and_18 (and_18_out, not_87_out, OP4, not_88_out, not_89_out, F14, not_90_out);
  and and_19 (and_19_out, not_91_out, not_92_out, OP4, not_93_out, F13, not_94_out, not_95_out);
  and and_20 (and_20_out, not_96_out, OP4, not_97_out, not_98_out, F13);
  and and_21 (and_21_out, OP2, not_99_out, OP5, OP6, not_100_out, not_101_out, not_102_out);
  and and_22 (and_22_out, OP2, not_103_out, OP4, not_104_out, not_105_out);
  and and_23 (and_23_out, OP2, OP3, not_106_out, OP5, OP6);
  and and_24 (ecall, not_107_out, not_108_out, OP4, OP5, OP6, not_109_out, not_110_out, not_111_out, not_112_out, not_113_out);
  and and_25 (S_Type, not_114_out, not_115_out, not_116_out, OP5, not_117_out, not_118_out, F13, not_119_out);
  and and_26 (BEQ, not_120_out, not_121_out, not_122_out, OP5, OP6, not_123_out, not_124_out, not_125_out);
  and and_27 (BNE, not_126_out, not_127_out, not_128_out, OP5, OP6, F12, not_129_out, not_130_out);
  and and_28 (JALR, OP2, not_131_out, not_132_out, OP5, OP6, not_133_out, not_134_out, not_135_out);
  and and_29 (JAL, OP2, OP3, not_136_out, OP5, OP6);
  and and_30 (csr, not_137_out, not_138_out, OP4, OP5, OP6, F13, F14);
  and and_31 (bge, not_139_out, not_140_out, not_141_out, OP5, OP6, F12, not_142_out, F14);
  and and_32 (U_Type, OP2, not_143_out, OP4, not_144_out, not_145_out);
  and and_33 (and_33_out, not_146_out, not_147_out, not_148_out, not_149_out, not_150_out, not_151_out, F14);
  and and_34 (and_34_out, not_152_out, not_153_out, not_154_out, not_155_out, not_156_out, F13, not_157_out);
  and and_35 (and_35_out, not_158_out, not_159_out, OP5, OP6, not_160_out, not_161_out, not_162_out);
  and and_36 (and_36_out, not_163_out, not_164_out, not_165_out, OP5, OP6, F12, not_166_out);
  and and_37 (and_37_out, not_167_out, not_168_out, OP4, not_169_out, not_170_out, not_171_out, not_172_out, not_173_out);
  and and_38 (and_38_out, not_174_out, OP4, not_175_out, not_176_out, not_177_out);
  and and_39 (and_39_out, not_178_out, OP4, not_179_out, not_180_out, not_181_out, not_182_out);
  and and_40 (and_40_out, not_183_out, OP4, not_184_out, not_185_out, F14, not_186_out);
  and and_41 (and_41_out, not_187_out, not_188_out, OP4, not_189_out, F13, not_190_out, not_191_out);
  and and_42 (and_42_out, not_192_out, OP4, not_193_out, not_194_out, F13);
  and and_43 (and_43_out, OP2, not_195_out, OP4, not_196_out, not_197_out);
  and and_44 (and_44_out, not_198_out, not_199_out, not_200_out, OP5, not_201_out, not_202_out, F13, not_203_out);
  and and_45 (and_45_out, not_204_out, not_205_out, not_206_out, OP5, OP6, not_207_out, not_208_out);
  and and_46 (and_46_out, not_209_out, not_210_out, not_211_out, OP5, OP6, F12, not_212_out);
  and and_47 (and_47_out, not_213_out, not_214_out, OP4, OP5, not_215_out, not_216_out, not_217_out, not_218_out, not_219_out);
  and and_48 (and_48_out, not_220_out, not_221_out, OP4, OP5, not_222_out, F13, not_223_out, not_224_out);
  and and_49 (LBU, F14, not_225_out, not_226_out, not_227_out, not_228_out, not_229_out, not_230_out, not_231_out);
  or or_1 (MemToReg, and_1_out, and_2_out);
  or or_2 (u2, and_44_out, and_45_out, and_46_out, and_47_out, and_48_out);
  or or_3 (ALU_SRC, and_4_out, and_5_out, and_6_out, and_7_out, and_8_out, and_9_out, and_10_out, and_11_out, and_12_out);
  or or_4 (RegWrite, and_13_out, and_14_out, and_15_out, and_16_out, and_17_out, and_18_out, and_19_out, and_20_out, and_21_out, and_22_out, and_23_out);
  or or_5 (u1, and_33_out, and_34_out, and_35_out, and_36_out, and_37_out, and_38_out, and_39_out, and_40_out, and_41_out, and_42_out, and_43_out);
endmodule

// ALU
module ALU (
  input  [31:0] X,
  input  [31:0] Y,
  input  [3:0] AluOP,
  output out_4,
  output Equal,
  output out_6,
  output [31:0] Result,
  output [31:0] Result_2
);

  wire [0:0] comparator_1_lt, comparator_2_lt;
  wire [31:0] adder_1_out, AND_out, divider_1_out, divider_1_rem, multiplier_1_cout, multiplier_1_out,
       NOR_out, OR_out, shifter_1_out, shifter_2_out, shifter_3_out, subtractor_1_out, XOR_out;

  assign AND_out = X & Y;  // AND_Gate AND, 32 bits wide
  assign OR_out = X | Y;  // OR_Gate OR, 32 bits wide
  Shifter #(.width(32), .shift("ll")) shifter_1 (.in(X), .\dist (Y[4:0]), .out(shifter_1_out));
  Shifter #(.width(32), .shift("ar")) shifter_2 (.in(X), .\dist (Y[4:0]), .out(shifter_2_out));
  Shifter #(.width(32), .shift("lr")) shifter_3 (.in(X), .\dist (Y[4:0]), .out(shifter_3_out));
  Multiplier #(.width(32)) multiplier_1 (.a(X), .b(Y), .out(multiplier_1_out), .cout(multiplier_1_cout));  // open: cin
  Divider #(.width(32)) divider_1 (.a(X), .b(Y), .out(divider_1_out), .rem(divider_1_rem));  // open: upper
  Adder #(.width(32)) adder_1 (.a(X), .b(Y), .out(adder_1_out));  // open: cin, cout
  Subtractor #(.width(32)) subtractor_1 (.a(X), .b(Y), .out(subtractor_1_out));  // open: bin, bout
  assign XOR_out = X ^ Y;  // XOR_Gate XOR, 32 bits wide
  assign NOR_out = ~(X | Y);  // NOR_Gate NOR, 32 bits wide
  Comparator #(.width(32), .mode("twosComplement")) comparator_1 (
    .a(X), .b(Y), .eq(Equal), .lt(comparator_1_lt[0]));  // open: gt
  Comparator #(.width(32), .mode("unsigned")) comparator_2 (.a(X), .b(Y), .lt(comparator_2_lt[0]));  // open: gt, eq
  Multiplexer #(.select(4), .width(32), .disabled("Z"), .enable("false")) multiplexer_1 (
    .in0(shifter_1_out), .in1(shifter_2_out), .in2(shifter_3_out), .in3(multiplier_1_out),
    .in4(divider_1_out), .in5(adder_1_out), .in6(subtractor_1_out), .in7(AND_out), .in8(OR_out),
    .in9(XOR_out), .in10(NOR_out), .in11({{31{1'b0}}, comparator_1_lt[0]}),
    .in12({{31{1'b0}}, comparator_2_lt[0]}), .in13({32{1'b0}}), .in14({32{1'b0}}), .in15({32{1'b0}}),
    .out(Result), .sel(AluOP));
  Multiplexer #(.select(4), .width(32), .disabled("Z"), .enable("false")) multiplexer_2 (
    .in0({32{1'b0}}), .in1({32{1'b0}}), .in2({32{1'b0}}), .in3(multiplier_1_cout), .in4(divider_1_rem),
    .in5({32{1'b0}}), .in6({32{1'b0}}), .in7({32{1'b0}}), .in8({32{1'b0}}), .in9({32{1'b0}}),
    .in10({32{1'b0}}), .in11({32{1'b0}}), .in12({32{1'b0}}), .in13({32{1'b0}}), .in14({32{1'b0}}),
    .in15({32{1'b0}}), .out(Result_2), .sel(AluOP));
  Multiplexer #(.select(4), .width(1), .disabled("Z"), .enable("false")) multiplexer_3 (
    .in0(1'b0), .in1(1'b0), .in2(1'b0), .in3(1'b0), .in4(1'b0), .in5(1'b0), .in6(1'b0), .in7(1'b0),
    .in8(1'b0), .in9(1'b0), .in10(1'b0), .in11(comparator_1_lt[0]), .in12(comparator_2_lt[0]), .in13(1'b0),
    .in14(1'b0), .in15(1'b0), .out(out_6), .sel(AluOP));
  not not_1 (out_4, out_6);

  // Other names for the same wires on the sheet: Result2[31:0] = Result_2; S[3:0] = AluOP; tunnel = out_6;
  //   tunnel_t = out_4

  // Notes on the sheet:
  //   不要改变此引脚区域内容，也不要改变ALU封装形式
  //   输入引脚
  //   输出引脚
endmodule

module Regifile (
  input  [31:0] Din,
  input  Clk,
  input  WE,
  input  [4:0] R1_num,
  input  [4:0] W_num,
  input  [4:0] R2_num,
  output [31:0] R1,
  output [31:0] R2
);

  // RegisterFile registerfile_1: pin names not known; wires that end beside it: Din, Clk, WE, W_num, R1_num, R2_num, R1, R2
endmodule

module \理想流水线  (
  output RegWrite,
  output MemWrite,
  output [31:0] IF_PC,
  output [31:0] ID_PC,
  output [31:0] EX_PC,
  output [31:0] M_PC,
  output [31:0] WB_PC,
  output [31:0] RDin,
  output [31:0] MDin,
  output [31:0] LedData
);

  wire ALUequal, ALUge, and_1_out, and_2_out, and_3_out, and_4_out, CLK, clock_1_out, comparator_1_eq,
       comparator_1_lt, comparator_2_eq, d_ff_1_q, EX_ecall, ex_mem_1_halt_2, ex_mem_1_jal_2,
       ex_mem_1_jalr_2, ex_mem_1_lbu_2, ex_mem_1_memtoreg_2, ex_mem_1_regwrite_2, ex_mem_1_uret_2, exhalt,
       Go, halt, ID_ecall, id_ex_1_alusrcb_2, id_ex_1_beq_2, id_ex_1_bge_2, id_ex_1_bne_2, id_ex_1_jal_2,
       id_ex_1_lbu_2, id_ex_1_memtoreg_2, id_ex_1_memwrite_2, id_ex_1_regwrite_2, id_ex_1_uret_2, IR1, IR2,
       IR3, jal, mem_wb_1_halt_2, mem_wb_1_jal_2, mem_wb_1_jalr_2, nand_1_out, not_1_out, not_2_out,
       not_3_out, or_1_out, or_2_out, RST, Stype, Utype, W1, W2, W3, \单周期硬布线控制器_1_alu_src ,
       \单周期硬布线控制器_1_beq , \单周期硬布线控制器_1_bge , \单周期硬布线控制器_1_bne , \单周期硬布线控制器_1_csr , \单周期硬布线控制器_1_jalr ,
       \单周期硬布线控制器_1_lbu , \单周期硬布线控制器_1_memtoreg , \单周期硬布线控制器_1_memwrite , \单周期硬布线控制器_1_regwrite ,
       \单周期硬布线控制器_1_uret ;
  wire [1:0] id_ex_1_jalr_2, mem_wb_1_memtoreg_2;
  wire [3:0] id_ex_1_aluop_2, \单周期硬布线控制器_1_alu_op ;
  wire [4:0] ex_mem_1_rd_2, id_ex_1_rd_2, multiplexer_2_out, multiplexer_3_out, \WB地址 ;
  wire [11:0] multiplexer_4_out;
  wire [12:0] CNT_num;
  wire [15:0] \LoadUse次数 , \总周期数 , \插入气泡数 , \无条件分支数 , \条件分支成功数 ;
  wire [31:0] ALUresult, bit_extender_1_out, bit_extender_2_out, bit_extender_3_out, EX_IR, ex_mem_1_pc_4_2,
       ex_mem_1_result_2, id_ex_1_imm_1_2, id_ex_1_imm_2_2, id_ex_1_pc_4_2, id_ex_1_r1_2, id_ex_1_r2_2,
       ID_IR, if_id_1_pc_4_2, IF_IR, IR, Jaddress, MEM_IR, mem_wb_1_aluresult_2, mem_wb_1_memdata_2,
       mem_wb_1_pc_4_2, multiplexer_1_out, multiplexer_5_out, multiplexer_6_out, PC_4, ram_1_data,
       regifile_1_r1, regifile_1_r2, shifter_1_out, WB_IR;

  Button \u_总复位  (.out(RST));
  Button _1 (.out(IR1));
  Button _2 (.out(IR2));
  Button _3 (.out(IR3));
  // Probe on \总周期数 
  // Probe on \总周期数 
  Button \u_继续运行  (.out(Go));
  LED #(.active("true")) led_1 (.in(W1));
  LED #(.active("true")) led_2 (.in(W2));
  LED #(.active("true")) led_3 (.in(W3));
  Multiplexer #(.select(2), .width(32), .disabled("Z"), .enable("false")) multiplexer_1 (
    .in0(PC_4), .in1(ALUresult), .in2(Jaddress), .out(multiplexer_1_out), .sel(id_ex_1_jalr_2));  // open: in3
  not not_1 (not_1_out, halt);
  Hex_Digit_Display hex_digit_display_1 (.value(LedData[31:28]));  // open: dp
  // Probe on IF_PC[19:0]
  // RiscV_Probe riscv_probe_1: pin names not known; wires that end beside it: IF_IR
  Register #(.width(32), .trigger("rising"), .Select("low")) PC (
    .D(multiplexer_1_out), .en(or_1_out), .Q(IF_PC), .clk(CLK), .clr(RST));
  or or_1 (or_1_out, not_1_out, Go);
  Hex_Digit_Display hex_digit_display_2 (.value(LedData[23:20]));  // open: dp
  Hex_Digit_Display hex_digit_display_3 (.value(LedData[27:24]));  // open: dp
  // Probe on ID_PC[19:0]
  // RiscV_Probe riscv_probe_2: pin names not known; wires that end beside it: ID_IR
  Hex_Digit_Display hex_digit_display_4 (.value(LedData[19:16]));  // open: dp
  Hex_Digit_Display hex_digit_display_5 (.value(LedData[15:12]));  // open: dp
  Adder #(.width(32)) adder_1 (.a(IF_PC), .b(32'h4), .out(PC_4));  // open: cin, cout
  Hex_Digit_Display hex_digit_display_6 (.value(LedData[7:4]));  // open: dp
  Hex_Digit_Display hex_digit_display_7 (.value(LedData[11:8]));  // open: dp
  // Probe on EX_PC[19:0]
  // RiscV_Probe riscv_probe_3: pin names not known; wires that end beside it: EX_IR
  // RiscV_Probe riscv_probe_4: pin names not known; wires that end beside it: IR
  ROM #(.addrWidth(10), .dataWidth(32), .Select("high")) rom_1 (.addr(IF_PC[11:2]), .data(IR));
  Hex_Digit_Display hex_digit_display_8 (.value(LedData[3:0]));  // open: dp
  or or_2 (or_2_out, id_ex_1_jalr_2[0], id_ex_1_jalr_2[1]);
  // Probe on \总周期数 
  // Probe on M_PC[19:0]
  // RiscV_Probe riscv_probe_5: pin names not known; wires that end beside it: MEM_IR
  IF_ID if_id_1 (
    .PC(IF_PC), .PC_4(PC_4), .IR(IR), .PC_2(ID_PC), .PC_4_2(if_id_1_pc_4_2), .IR_2(ID_IR), .reset(1'b0),
    .flush(or_2_out), .en(1'b1), .CLK(CLK));  // open: 预测跳转, 预测跳转_2
  // Probe on \总周期数 
  // Probe on \无条件分支数 
  // Probe on \条件分支成功数 
  // Probe on \插入气泡数 
  // Probe on \LoadUse次数 
  // Probe on IF_PC[11:0]
  // Probe on WB_PC[19:0]
  // RiscV_Probe riscv_probe_6: pin names not known; wires that end beside it: WB_IR
  \单周期硬布线控制器  \u_单周期硬布线控制器_1  (
    .Funct({ID_IR[30], ID_IR[25], ID_IR[14:12]}), .OP(ID_IR[6:2]), .ALU_OP(\单周期硬布线控制器_1_alu_op ),
    .MemToReg(\单周期硬布线控制器_1_memtoreg ), .MemWrite(\单周期硬布线控制器_1_memwrite ), .ALU_SRC(\单周期硬布线控制器_1_alu_src ),
    .RegWrite(\单周期硬布线控制器_1_regwrite ), .ecall(ID_ecall), .S_type(Stype), .Jalr(\单周期硬布线控制器_1_jalr ),
    .Beq(\单周期硬布线控制器_1_beq ), .JAL(jal), .Bne(\单周期硬布线控制器_1_bne ), .in_3(ID_IR[21]), .uret(\单周期硬布线控制器_1_uret ),
    .csr(\单周期硬布线控制器_1_csr ), .U_type(Utype), .bge(\单周期硬布线控制器_1_bge ), .LBU(\单周期硬布线控制器_1_lbu ));  // open: u2, u1
  Multiplexer #(.select(1), .width(5), .disabled("Z"), .enable("false")) multiplexer_2 (
    .in0(ID_IR[19:15]), .in1(5'b10001), .out(multiplexer_2_out), .sel(ID_ecall));
  Multiplexer #(.select(1), .width(5), .disabled("Z"), .enable("false")) multiplexer_3 (
    .in0(ID_IR[24:20]), .in1(5'b01010), .out(multiplexer_3_out), .sel(ID_ecall));
  Multiplexer #(.select(1), .width(12), .disabled("Z"), .enable("false")) multiplexer_4 (
    .in0(ID_IR[31:20]), .in1({ID_IR[31:25], ID_IR[11:7]}), .out(multiplexer_4_out), .sel(Stype));
  assign bit_extender_1_out = {{20{ID_IR[31]}}, {ID_IR[31], ID_IR[7], ID_IR[30:25], ID_IR[11:8]}};  // Bit_Extender bit_extender_1
  assign bit_extender_2_out = {{12{ID_IR[31]}}, {ID_IR[31], ID_IR[19:12], ID_IR[20], ID_IR[30:21]}};  // Bit_Extender bit_extender_2
  // Probe on ID_PC[11:0]
  // Probe on EX_PC[11:0]
  assign bit_extender_3_out = {{20{multiplexer_4_out[11]}}, multiplexer_4_out};  // Bit_Extender bit_extender_3
  Multiplexer #(.select(1), .width(32), .disabled("Z"), .enable("false")) multiplexer_5 (
    .in0(bit_extender_1_out), .in1(bit_extender_2_out), .out(multiplexer_5_out), .sel(jal));
  // Probe on M_PC[11:0]
  D_Flip_Flop #(.trigger("high"), .Pre_Clr_Positions("LEGACY"), .NegatePresetClear("false"), .enable("true"), .NewFFLayout("false")) d_ff_1 (.Q(d_ff_1_q));  // open: clk, D, Qn, preset, en, reset
  // Probe on 13'hccc
  Regifile regifile_1 (
    .Din(RDin), .Clk(CLK), .R1(regifile_1_r1), .R2(regifile_1_r2), .WE(RegWrite), .W_num(\WB地址 ),
    .R1_num(multiplexer_2_out), .R2_num(multiplexer_3_out));
  // Probe on WB_PC[11:0]
  Comparator #(.width(13), .mode("twosComplement")) comparator_1 (
    .a(CNT_num), .b(13'hccc), .eq(comparator_1_eq), .lt(comparator_1_lt));  // open: gt
  Clock #(.highDuration(1), .lowDuration(1)) clock_1 (.out(clock_1_out));
  ID_EX id_ex_1 (
    .Beq(\单周期硬布线控制器_1_beq ), .Bne(\单周期硬布线控制器_1_bne ), .MemToReg(\单周期硬布线控制器_1_memtoreg ),
    .MemWrite(\单周期硬布线控制器_1_memwrite ), .RegWrite(\单周期硬布线控制器_1_regwrite ), .JAL(jal),
    .JALR(\单周期硬布线控制器_1_jalr ), .URET(\单周期硬布线控制器_1_uret ), .S_type(Stype), .U_type(Utype),
    .bge(\单周期硬布线控制器_1_bge ), .csr(\单周期硬布线控制器_1_csr ), .LBU(\单周期硬布线控制器_1_lbu ), .ecall(ID_ecall),
    .AluOP(\单周期硬布线控制器_1_alu_op ), .rd(ID_IR[11:7]), .R1(regifile_1_r1), .R2(regifile_1_r2),
    .imm_1(bit_extender_3_out), .imm_2(multiplexer_5_out), .PC(ID_PC), .PC_4(if_id_1_pc_4_2), .IR(ID_IR),
    .Beq_2(id_ex_1_beq_2), .Bne_2(id_ex_1_bne_2), .MemToReg_2(id_ex_1_memtoreg_2),
    .MemWrite_2(id_ex_1_memwrite_2), .RegWrite_2(id_ex_1_regwrite_2), .JAL_2(id_ex_1_jal_2),
    .JALR_2(id_ex_1_jalr_2[0]), .URET_2(id_ex_1_uret_2), .bge_2(id_ex_1_bge_2), .LBU_2(id_ex_1_lbu_2),
    .ecall_2(EX_ecall), .AluOP_2(id_ex_1_aluop_2), .rd_2(id_ex_1_rd_2), .R1_2(id_ex_1_r1_2),
    .R2_2(id_ex_1_r2_2), .imm_1_2(id_ex_1_imm_1_2), .imm_2_2(id_ex_1_imm_2_2), .PC_2(EX_PC),
    .PC_4_2(id_ex_1_pc_4_2), .IR_2(EX_IR), .reset(1'b0), .flush(1'b0), .en(1'b1), .CLK(CLK),
    .AluSrcB(\单周期硬布线控制器_1_alu_src ), .AluSrcB_2(id_ex_1_alusrcb_2));  // open: rs1f, rs2f, S_type_2, U_type_2, csr_2, rs1f_2, rs2f_2, imm_3, imm_3_2, 预测跳转_2, 预测跳转
  nand nand_1 (nand_1_out, d_ff_1_q, comparator_1_eq);
  Counter #(.width(13), .max('h1fff), .ongoal("stay"), .trigger("rising"), .behavior("old")) counter_1 (
    .count(comparator_1_lt), .Q(CNT_num), .clk(clock_1_out));  // open: load, D, carry, clr, preset
  assign CLK = nand_1_out ? clock_1_out : 1'bz;  // Controlled_Buffer controlled_buffer_1
  or or_3 (id_ex_1_jalr_2[1], and_1_out, and_3_out, and_2_out);
  and and_1 (and_1_out, id_ex_1_beq_2, ALUequal);
  Multiplexer #(.select(1), .width(32), .disabled("Z"), .enable("false")) multiplexer_6 (
    .in0(id_ex_1_r2_2), .in1(id_ex_1_imm_1_2), .out(multiplexer_6_out), .sel(id_ex_1_alusrcb_2));
  Pull_Resistor #(.pull(1)) pull_resistor_1 (.node(CLK));
  and and_2 (and_2_out, id_ex_1_bne_2, ~ALUequal);  // AND_Gate
  Shifter #(.width(32), .shift("ll")) shifter_1 (.in(id_ex_1_imm_2_2), .\dist (5'b00001), .out(shifter_1_out));
  Comparator #(.width(32), .mode("twosComplement")) comparator_2 (
    .a(id_ex_1_r1_2), .b(32'h22), .eq(comparator_2_eq));  // open: gt, lt
  and and_3 (and_3_out, id_ex_1_bge_2, ALUge);
  ALU alu_1 (
    .X(id_ex_1_r1_2), .Y(multiplexer_6_out), .AluOP(id_ex_1_aluop_2), .Equal(ALUequal), .Result(ALUresult),
    .out_4(ALUge));  // open: Result_2, out_6
  Adder #(.width(32)) adder_2 (.a(shifter_1_out), .b(EX_PC), .out(Jaddress), .cin(1'b0));  // open: cout
  not not_2 (not_2_out, comparator_2_eq);
  and and_4 (and_4_out, comparator_2_eq, EX_ecall);
  not not_3 (not_3_out, halt);
  and and_5 (exhalt, EX_ecall, not_2_out);
  Register #(.width(32), .trigger("rising"), .Select("low")) register_1 (
    .D(id_ex_1_r2_2), .en(and_4_out), .Q(LedData), .clk(CLK));  // open: clr
  Counter #(.width(16), .max('hffff), .ongoal("wrap"), .trigger("rising"), .behavior("new")) counter_2 (
    .load(1'b0), .D({16{1'b0}}), .count(not_3_out), .Q(\总周期数 ), .clk(CLK), .clr(1'b0), .down(1'b0));  // open: carry, preset
  EX_MEM ex_mem_1 (
    .MemToReg(id_ex_1_memtoreg_2), .MemWrite(id_ex_1_memwrite_2), .RegWrite(id_ex_1_regwrite_2),
    .JAL(id_ex_1_jal_2), .JALR(id_ex_1_jalr_2[0]), .URET(id_ex_1_uret_2), .LBU(id_ex_1_lbu_2), .halt(exhalt),
    .rd(id_ex_1_rd_2), .result(ALUresult), .R2(id_ex_1_r2_2), .PC(EX_PC), .PC_4(id_ex_1_pc_4_2), .IR(EX_IR),
    .MemToReg_2(ex_mem_1_memtoreg_2), .MemWrite_2(MemWrite), .RegWrite_2(ex_mem_1_regwrite_2),
    .JAL_2(ex_mem_1_jal_2), .JALR_2(ex_mem_1_jalr_2), .URET_2(ex_mem_1_uret_2), .LBU_2(ex_mem_1_lbu_2),
    .halt_2(ex_mem_1_halt_2), .rd_2(ex_mem_1_rd_2), .result_2(ex_mem_1_result_2), .R2_2(MDin), .PC_2(M_PC),
    .PC_4_2(ex_mem_1_pc_4_2), .IR_2(MEM_IR), .reset(1'b0), .flush(1'b0), .en(1'b1), .CLK(CLK));  // open: U_type, U_type_2, Uimm, Uimm_2
  RAM #(.addrWidth(10), .dataWidth(32), .bus("separate"), .Select("high")) ram_1 (
    .addr(ex_mem_1_result_2[11:2]), .din(MDin), .data(ram_1_data), .str(MemWrite), .sel(1'b1), .clk(CLK),
    .ld(1'b1));  // open: clr
  MEM_WB mem_wb_1 (
    .LBU(ex_mem_1_lbu_2), .MemToReg(ex_mem_1_memtoreg_2), .RegWrite(ex_mem_1_regwrite_2),
    .JAL(ex_mem_1_jal_2), .JALR(ex_mem_1_jalr_2), .URET(ex_mem_1_uret_2), .halt(ex_mem_1_halt_2),
    .rd(ex_mem_1_rd_2), .ALUresult(ex_mem_1_result_2), .MemData(ram_1_data), .PC(M_PC),
    .PC_4(ex_mem_1_pc_4_2), .IR(MEM_IR), .MemToReg_2(mem_wb_1_memtoreg_2[0]), .RegWrite_2(RegWrite),
    .JAL_2(mem_wb_1_jal_2), .JALR_2(mem_wb_1_jalr_2), .halt_2(mem_wb_1_halt_2), .rd_2(\WB地址 ),
    .ALUresult_2(mem_wb_1_aluresult_2), .MemData_2(mem_wb_1_memdata_2), .PC_2(WB_PC),
    .PC_4_2(mem_wb_1_pc_4_2), .IR_2(WB_IR), .reset(1'b0), .flush(1'b0), .en(1'b1), .CLK(CLK));  // open: LBU_2, URET_2, U_type, U_type_2, Uimm, Uimm_2
  or or_4 (mem_wb_1_memtoreg_2[1], mem_wb_1_jal_2, mem_wb_1_jalr_2);
  Multiplexer #(.select(2), .width(32), .disabled("Z"), .enable("false")) multiplexer_7 (
    .in0(mem_wb_1_aluresult_2), .in1(mem_wb_1_memdata_2), .in2(mem_wb_1_pc_4_2), .out(RDin),
    .sel(mem_wb_1_memtoreg_2));  // open: in3
  D_Flip_Flop #(.trigger("rising"), .Pre_Clr_Positions("ABOVE_BELOW"), .NegatePresetClear("false"), .enable("true"), .NewFFLayout("true")) d_ff_2 (
    .clk(mem_wb_1_halt_2), .D(1'b1), .Q(halt), .preset(1'b0), .en(1'b1), .reset(Go));  // open: Qn

  // Other names for the same wires on the sheet: MEM_PC[31:0] = M_PC

  // Notes on the sheet:
  //   中断源
  //   时空图监测，可删除
  //   中断等待指示
  //   数码管输出
  //   IF
  //   指令探针
  //   指令存储器
  //   contents of rom_1 (hex, n*v repeats v):
  //   413 493 913 993 46413 14e493 296913 39e993 842023 942223 1242423 1342623 a00893 493 913 993 73
  //   rs1
  //   rs2
  //   rd
  //   JAL
  //   JALR
  //   CSR
  //   I指令
  //   S指令
  //   B指令
  //   J指令
  //   ID
  //   Beq
  //   Bne
  //   MemToReg
  //   MemWrite
  //   AluOP
  //   AluSrcB
  //   RegWrite
  //   控制位
  //   流水调试日志用
  //   暂停节拍，不能为0
  //   戳工具置1进入计数暂停模式，ctrl+k时钟自动运行到对应节拍暂停
  //   ctrl+k关闭时钟连续运行，将控制位置零，进入单步调试模式调试
  //   用这个时钟源需要去掉电路中的其他时钟源
  //   R1
  //   imm1
  //   R2
  //   rd
  //   imm2
  //   可计数暂停的时钟源
  //   EX
  //   ALUresult
  //   为方便自动评测，需要输出流水线各段保存的PC值，注意是PC不是PC+4，另外ID段寄存器写入信息，Mem段内存写入信息也要输出
  //   ReegWrite
  //   MEM
  //   数据存储器
  //   MemtoReg
  //   JAL
  //   JALR
  //   LBU
  //   WB
endmodule

module \气泡流水线  (
  output RegWrite,
  output MemWrite,
  output [31:0] IF_PC,
  output [31:0] ID_PC,
  output [31:0] EX_PC,
  output [31:0] M_PC,
  output [31:0] WB_PC,
  output [31:0] RDin,
  output [31:0] MDin,
  output [31:0] LedData
);

  wire ALUequal, ALUge, and_1_out, and_2_out, and_3_out, and_4_out, and_5_out, and_6_out, branch, CLK,
       clock_1_out, comparator_1_eq, comparator_1_lt, comparator_2_eq, d_ff_1_q, EX_ecall, ex_mem_1_halt_2,
       ex_mem_1_jal_2, ex_mem_1_jalr_2, ex_mem_1_lbu_2, ex_mem_1_memtoreg_2, ex_mem_1_regwrite_2,
       ex_mem_1_uret_2, exhalt, flush, Go, halt, ID_ecall, id_ex_1_alusrcb_2, id_ex_1_beq_2, id_ex_1_bge_2,
       id_ex_1_bne_2, id_ex_1_jal_2, id_ex_1_lbu_2, id_ex_1_memtoreg_2, id_ex_1_memwrite_2,
       id_ex_1_regwrite_2, id_ex_1_uret_2, IR1, IR2, IR3, jal, mem_wb_1_halt_2, mem_wb_1_jal_2,
       mem_wb_1_jalr_2, nand_1_out, not_1_out, not_2_out, not_3_out, not_4_out, not_5_out, not_6_out,
       not_7_out, or_1_out, or_3_out, or_5_out, RST, Stype, Utype, W1, W2, W3, \冲突 , \单周期硬布线控制器_1_alu_src ,
       \单周期硬布线控制器_1_beq , \单周期硬布线控制器_1_bge , \单周期硬布线控制器_1_bne , \单周期硬布线控制器_1_csr , \单周期硬布线控制器_1_jalr ,
       \单周期硬布线控制器_1_lbu , \单周期硬布线控制器_1_memtoreg , \单周期硬布线控制器_1_memwrite , \单周期硬布线控制器_1_regwrite ,
       \单周期硬布线控制器_1_u1 , \单周期硬布线控制器_1_u2 , \单周期硬布线控制器_1_uret ;
  wire [1:0] id_ex_1_jalr_2, mem_wb_1_memtoreg_2;
  wire [3:0] id_ex_1_aluop_2, \单周期硬布线控制器_1_alu_op ;
  wire [4:0] EX_rd, MEM_rd, multiplexer_2_out, multiplexer_3_out, \WB地址 ;
  wire [11:0] multiplexer_4_out;
  wire [12:0] CNT_num;
  wire [15:0] \LoadUse次数 , \总周期数 , \插入气泡数 , \无条件分支数 , \条件分支成功数 ;
  wire [31:0] ALUresult, bit_extender_1_out, bit_extender_2_out, bit_extender_3_out, EX_IR, ex_mem_1_pc_4_2,
       ex_mem_1_result_2, id_ex_1_imm_1_2, id_ex_1_imm_2_2, id_ex_1_pc_4_2, id_ex_1_r1_2, id_ex_1_r2_2,
       ID_IR, if_id_1_pc_4_2, IF_IR, Jaddress, MEM_IR, mem_wb_1_aluresult_2, mem_wb_1_memdata_2,
       mem_wb_1_pc_4_2, multiplexer_1_out, multiplexer_5_out, multiplexer_6_out, PC_4, ram_1_data,
       regifile_1_r1, regifile_1_r2, shifter_1_out, WB_IR;

  Button \u_总复位  (.out(RST));
  Button _1 (.out(IR1));
  Button _2 (.out(IR2));
  Button _3 (.out(IR3));
  // Probe on \总周期数 
  // Probe on \总周期数 
  Button \u_继续运行  (.out(Go));
  LED #(.active("true")) led_1 (.in(W1));
  LED #(.active("true")) led_2 (.in(W2));
  LED #(.active("true")) led_3 (.in(W3));
  not not_1 (not_1_out, halt);
  Hex_Digit_Display hex_digit_display_1 (.value(LedData[31:28]));  // open: dp
  // Probe on IF_PC[19:0]
  // RiscV_Probe riscv_probe_1: pin names not known; wires that end beside it: IF_IR
  and and_1 (and_1_out, or_1_out, not_2_out);
  Multiplexer #(.select(2), .width(32), .disabled("Z"), .enable("false")) multiplexer_1 (
    .in0(PC_4), .in1(ALUresult), .in2(Jaddress), .out(multiplexer_1_out), .sel(id_ex_1_jalr_2));  // open: in3
  or or_1 (or_1_out, not_1_out, Go);
  not not_2 (not_2_out, \冲突 );
  Hex_Digit_Display hex_digit_display_2 (.value(LedData[27:24]));  // open: dp
  Hex_Digit_Display hex_digit_display_3 (.value(LedData[23:20]));  // open: dp
  // Probe on ID_PC[19:0]
  // RiscV_Probe riscv_probe_2: pin names not known; wires that end beside it: ID_IR
  Register #(.width(32), .trigger("rising"), .Select("low")) PC (
    .D(multiplexer_1_out), .en(and_1_out), .Q(IF_PC), .clk(CLK), .clr(RST));
  Hex_Digit_Display hex_digit_display_4 (.value(LedData[19:16]));  // open: dp
  Hex_Digit_Display hex_digit_display_5 (.value(LedData[15:12]));  // open: dp
  Adder #(.width(32)) adder_1 (.a(IF_PC), .b(32'h4), .out(PC_4));  // open: cin, cout
  Hex_Digit_Display hex_digit_display_6 (.value(LedData[11:8]));  // open: dp
  Hex_Digit_Display hex_digit_display_7 (.value(LedData[7:4]));  // open: dp
  // Probe on EX_PC[19:0]
  // RiscV_Probe riscv_probe_3: pin names not known; wires that end beside it: EX_IR
  // RiscV_Probe riscv_probe_4: pin names not known; wires that end beside it: IF_IR
  Hex_Digit_Display hex_digit_display_8 (.value(LedData[3:0]));  // open: dp
  ROM #(.addrWidth(10), .dataWidth(32), .Select("high")) rom_1 (.addr(IF_PC[11:2]), .data(IF_IR));
  not not_3 (not_3_out, halt);
  // Probe on \总周期数 
  // Probe on M_PC[19:0]
  // RiscV_Probe riscv_probe_5: pin names not known; wires that end beside it: MEM_IR
  or or_2 (branch, id_ex_1_jalr_2[0], id_ex_1_jalr_2[1]);
  IF_ID if_id_1 (
    .PC(IF_PC), .PC_4(PC_4), .IR(IF_IR), .PC_2(ID_PC), .PC_4_2(if_id_1_pc_4_2), .IR_2(ID_IR), .reset(1'b0),
    .flush(branch), .en(and_2_out), .CLK(CLK));  // open: 预测跳转, 预测跳转_2
  and and_2 (and_2_out, or_3_out, not_4_out);
  not not_4 (not_4_out, \冲突 );
  or or_3 (or_3_out, not_3_out, Go);
  // Probe on \总周期数 
  // Probe on \无条件分支数 
  // Probe on \条件分支成功数 
  // Probe on \插入气泡数 
  // Probe on \LoadUse次数 
  // Probe on IF_PC[11:0]
  // Probe on WB_PC[19:0]
  // RiscV_Probe riscv_probe_6: pin names not known; wires that end beside it: WB_IR
  \气泡流水线处理  \u_气泡流水线处理_1  (
    .IR(ID_IR), .u1(\单周期硬布线控制器_1_u1 ), .EX_RegWrite(id_ex_1_regwrite_2), .u2(\单周期硬布线控制器_1_u2 ),
    .MEM_RegWrite(ex_mem_1_regwrite_2), .EX_rd(EX_rd), .branch(branch), .MEM_rd(MEM_rd), .ecall(ID_ecall),
    .\冲突 (\冲突 ), .flush(flush));
  \单周期硬布线控制器  \u_单周期硬布线控制器_1  (
    .Funct({ID_IR[30], ID_IR[25], ID_IR[14:12]}), .OP(ID_IR[6:2]), .ALU_OP(\单周期硬布线控制器_1_alu_op ),
    .MemToReg(\单周期硬布线控制器_1_memtoreg ), .MemWrite(\单周期硬布线控制器_1_memwrite ), .ALU_SRC(\单周期硬布线控制器_1_alu_src ),
    .RegWrite(\单周期硬布线控制器_1_regwrite ), .ecall(ID_ecall), .S_type(Stype), .Jalr(\单周期硬布线控制器_1_jalr ),
    .Beq(\单周期硬布线控制器_1_beq ), .JAL(jal), .Bne(\单周期硬布线控制器_1_bne ), .in_3(ID_IR[21]), .uret(\单周期硬布线控制器_1_uret ),
    .u2(\单周期硬布线控制器_1_u2 ), .u1(\单周期硬布线控制器_1_u1 ), .csr(\单周期硬布线控制器_1_csr ), .U_type(Utype),
    .bge(\单周期硬布线控制器_1_bge ), .LBU(\单周期硬布线控制器_1_lbu ));
  Multiplexer #(.select(1), .width(5), .disabled("Z"), .enable("false")) multiplexer_2 (
    .in0(ID_IR[19:15]), .in1(5'b10001), .out(multiplexer_2_out), .sel(ID_ecall));
  Multiplexer #(.select(1), .width(5), .disabled("Z"), .enable("false")) multiplexer_3 (
    .in0(ID_IR[24:20]), .in1(5'b01010), .out(multiplexer_3_out), .sel(ID_ecall));
  Multiplexer #(.select(1), .width(12), .disabled("Z"), .enable("false")) multiplexer_4 (
    .in0(ID_IR[31:20]), .in1({ID_IR[31:25], ID_IR[11:7]}), .out(multiplexer_4_out), .sel(Stype));
  // Probe on EX_PC[11:0]
  // Probe on ID_PC[11:0]
  assign bit_extender_1_out = {{20{multiplexer_4_out[11]}}, multiplexer_4_out};  // Bit_Extender bit_extender_1
  assign bit_extender_2_out = {{20{ID_IR[31]}}, {ID_IR[31], ID_IR[7], ID_IR[30:25], ID_IR[11:8]}};  // Bit_Extender bit_extender_2
  assign bit_extender_3_out = {{12{ID_IR[31]}}, {ID_IR[31], ID_IR[19:12], ID_IR[20], ID_IR[30:21]}};  // Bit_Extender bit_extender_3
  // Probe on M_PC[11:0]
  D_Flip_Flop #(.trigger("high"), .Pre_Clr_Positions("LEGACY"), .NegatePresetClear("false"), .enable("true"), .NewFFLayout("false")) d_ff_1 (.Q(d_ff_1_q));  // open: clk, D, Qn, preset, en, reset
  // Probe on 13'h1a
  Regifile regifile_1 (
    .Din(RDin), .Clk(not_5_out), .R1(regifile_1_r1), .R2(regifile_1_r2), .WE(RegWrite), .W_num(\WB地址 ),
    .R1_num(multiplexer_2_out), .R2_num(multiplexer_3_out));
  not not_5 (not_5_out, CLK);
  Multiplexer #(.select(1), .width(32), .disabled("Z"), .enable("false")) multiplexer_5 (
    .in0(bit_extender_2_out), .in1(bit_extender_3_out), .out(multiplexer_5_out), .sel(jal));
  // Probe on WB_PC[11:0]
  Comparator #(.width(13), .mode("twosComplement")) comparator_1 (
    .a(CNT_num), .b(13'h1a), .eq(comparator_1_eq), .lt(comparator_1_lt));  // open: gt
  Clock #(.highDuration(1), .lowDuration(1)) clock_1 (.out(clock_1_out));
  nand nand_1 (nand_1_out, d_ff_1_q, comparator_1_eq);
  Counter #(.width(13), .max('h1fff), .ongoal("stay"), .trigger("rising"), .behavior("old")) counter_1 (
    .count(comparator_1_lt), .Q(CNT_num), .clk(clock_1_out));  // open: load, D, carry, clr, preset
  ID_EX id_ex_1 (
    .Beq(\单周期硬布线控制器_1_beq ), .Bne(\单周期硬布线控制器_1_bne ), .MemToReg(\单周期硬布线控制器_1_memtoreg ),
    .MemWrite(\单周期硬布线控制器_1_memwrite ), .RegWrite(\单周期硬布线控制器_1_regwrite ), .JAL(jal),
    .JALR(\单周期硬布线控制器_1_jalr ), .URET(\单周期硬布线控制器_1_uret ), .S_type(Stype), .U_type(Utype),
    .bge(\单周期硬布线控制器_1_bge ), .csr(\单周期硬布线控制器_1_csr ), .LBU(\单周期硬布线控制器_1_lbu ), .ecall(ID_ecall),
    .AluOP(\单周期硬布线控制器_1_alu_op ), .rd(ID_IR[11:7]), .R1(regifile_1_r1), .R2(regifile_1_r2),
    .imm_1(bit_extender_1_out), .imm_2(multiplexer_5_out), .PC(ID_PC), .PC_4(if_id_1_pc_4_2), .IR(ID_IR),
    .Beq_2(id_ex_1_beq_2), .Bne_2(id_ex_1_bne_2), .MemToReg_2(id_ex_1_memtoreg_2),
    .MemWrite_2(id_ex_1_memwrite_2), .RegWrite_2(id_ex_1_regwrite_2), .JAL_2(id_ex_1_jal_2),
    .JALR_2(id_ex_1_jalr_2[0]), .URET_2(id_ex_1_uret_2), .bge_2(id_ex_1_bge_2), .LBU_2(id_ex_1_lbu_2),
    .ecall_2(EX_ecall), .AluOP_2(id_ex_1_aluop_2), .rd_2(EX_rd), .R1_2(id_ex_1_r1_2), .R2_2(id_ex_1_r2_2),
    .imm_1_2(id_ex_1_imm_1_2), .imm_2_2(id_ex_1_imm_2_2), .PC_2(EX_PC), .PC_4_2(id_ex_1_pc_4_2),
    .IR_2(EX_IR), .reset(1'b0), .flush(flush), .en(or_3_out), .CLK(CLK), .AluSrcB(\单周期硬布线控制器_1_alu_src ),
    .AluSrcB_2(id_ex_1_alusrcb_2));  // open: rs1f, rs2f, S_type_2, U_type_2, csr_2, rs1f_2, rs2f_2, imm_3, imm_3_2, 预测跳转_2, 预测跳转
  assign CLK = nand_1_out ? clock_1_out : 1'bz;  // Controlled_Buffer controlled_buffer_1
  or or_4 (id_ex_1_jalr_2[1], id_ex_1_jal_2, or_5_out);
  and and_3 (and_3_out, id_ex_1_beq_2, ALUequal);
  Pull_Resistor #(.pull(1)) pull_resistor_1 (.node(CLK));
  or or_5 (or_5_out, and_3_out, and_5_out, and_4_out);
  and and_4 (and_4_out, id_ex_1_bne_2, ~ALUequal);  // AND_Gate
  Multiplexer #(.select(1), .width(32), .disabled("Z"), .enable("false")) multiplexer_6 (
    .in0(id_ex_1_r2_2), .in1(id_ex_1_imm_1_2), .out(multiplexer_6_out), .sel(id_ex_1_alusrcb_2));
  Shifter #(.width(32), .shift("ll")) shifter_1 (.in(id_ex_1_imm_2_2), .\dist (5'b00001), .out(shifter_1_out));
  Comparator #(.width(32), .mode("twosComplement")) comparator_2 (
    .a(id_ex_1_r1_2), .b(32'h22), .eq(comparator_2_eq));  // open: gt, lt
  and and_5 (and_5_out, id_ex_1_bge_2, ALUge);
  ALU alu_1 (
    .X(id_ex_1_r1_2), .Y(multiplexer_6_out), .AluOP(id_ex_1_aluop_2), .Equal(ALUequal), .Result(ALUresult),
    .out_4(ALUge));  // open: Result_2, out_6
  Adder #(.width(32)) adder_2 (.a(shifter_1_out), .b(EX_PC), .out(Jaddress), .cin(1'b0));  // open: cout
  not not_6 (not_6_out, comparator_2_eq);
  and and_6 (and_6_out, comparator_2_eq, EX_ecall);
  not not_7 (not_7_out, halt);
  and and_7 (exhalt, EX_ecall, not_6_out);
  Counter #(.width(16), .max('hffff), .ongoal("wrap"), .trigger("rising"), .behavior("new")) counter_2 (
    .load(1'b0), .D({16{1'b0}}), .count(not_7_out), .Q(\总周期数 ), .clk(CLK), .clr(1'b0), .down(1'b0));  // open: carry, preset
  Register #(.width(32), .trigger("rising"), .Select("low")) register_1 (
    .D(id_ex_1_r2_2), .en(and_6_out), .Q(LedData), .clk(CLK));  // open: clr
  EX_MEM ex_mem_1 (
    .MemToReg(id_ex_1_memtoreg_2), .MemWrite(id_ex_1_memwrite_2), .RegWrite(id_ex_1_regwrite_2),
    .JAL(id_ex_1_jal_2), .JALR(id_ex_1_jalr_2[0]), .URET(id_ex_1_uret_2), .LBU(id_ex_1_lbu_2), .halt(exhalt),
    .rd(EX_rd), .result(ALUresult), .R2(id_ex_1_r2_2), .PC(EX_PC), .PC_4(id_ex_1_pc_4_2), .IR(EX_IR),
    .MemToReg_2(ex_mem_1_memtoreg_2), .MemWrite_2(MemWrite), .RegWrite_2(ex_mem_1_regwrite_2),
    .JAL_2(ex_mem_1_jal_2), .JALR_2(ex_mem_1_jalr_2), .URET_2(ex_mem_1_uret_2), .LBU_2(ex_mem_1_lbu_2),
    .halt_2(ex_mem_1_halt_2), .rd_2(MEM_rd), .result_2(ex_mem_1_result_2), .R2_2(MDin), .PC_2(M_PC),
    .PC_4_2(ex_mem_1_pc_4_2), .IR_2(MEM_IR), .reset(1'b0), .flush(1'b0), .en(or_3_out), .CLK(CLK));  // open: U_type, U_type_2, Uimm, Uimm_2
  RAM #(.addrWidth(10), .dataWidth(32), .bus("separate"), .Select("high")) ram_1 (
    .addr(ex_mem_1_result_2[11:2]), .din(MDin), .data(ram_1_data), .str(MemWrite), .sel(1'b1), .clk(CLK),
    .ld(1'b1));  // open: clr
  MEM_WB mem_wb_1 (
    .LBU(ex_mem_1_lbu_2), .MemToReg(ex_mem_1_memtoreg_2), .RegWrite(ex_mem_1_regwrite_2),
    .JAL(ex_mem_1_jal_2), .JALR(ex_mem_1_jalr_2), .URET(ex_mem_1_uret_2), .halt(ex_mem_1_halt_2),
    .rd(MEM_rd), .ALUresult(ex_mem_1_result_2), .MemData(ram_1_data), .PC(M_PC), .PC_4(ex_mem_1_pc_4_2),
    .IR(MEM_IR), .MemToReg_2(mem_wb_1_memtoreg_2[0]), .RegWrite_2(RegWrite), .JAL_2(mem_wb_1_jal_2),
    .JALR_2(mem_wb_1_jalr_2), .halt_2(mem_wb_1_halt_2), .rd_2(\WB地址 ), .ALUresult_2(mem_wb_1_aluresult_2),
    .MemData_2(mem_wb_1_memdata_2), .PC_2(WB_PC), .PC_4_2(mem_wb_1_pc_4_2), .IR_2(WB_IR), .reset(1'b0),
    .flush(1'b0), .en(or_3_out), .CLK(CLK));  // open: LBU_2, URET_2, U_type, U_type_2, Uimm, Uimm_2
  or or_6 (mem_wb_1_memtoreg_2[1], mem_wb_1_jal_2, mem_wb_1_jalr_2);
  Multiplexer #(.select(2), .width(32), .disabled("Z"), .enable("false")) multiplexer_7 (
    .in0(mem_wb_1_aluresult_2), .in1(mem_wb_1_memdata_2), .in2(mem_wb_1_pc_4_2), .out(RDin),
    .sel(mem_wb_1_memtoreg_2));  // open: in3
  D_Flip_Flop #(.trigger("rising"), .Pre_Clr_Positions("ABOVE_BELOW"), .NegatePresetClear("false"), .enable("true"), .NewFFLayout("true")) d_ff_2 (
    .clk(mem_wb_1_halt_2), .D(1'b1), .Q(halt), .preset(1'b0), .en(1'b1), .reset(Go));  // open: Qn

  // Other names for the same wires on the sheet: MEM_PC[31:0] = M_PC

  // Notes on the sheet:
  //   中断源
  //   时空图监测，可删除
  //   中断等待指示
  //   数码管输出
  //   IF
  //   指令探针
  //   指令存储器
  //   contents of rom_1 (hex, n*v repeats v):
  //   100493 100006f 100493 200913 300993 100006f 100493 200913 300993 100006f 100493 200913 300993
  //   100006f 100493 200913 300993 29c000ef 100413 100493 1f49493 900533 2200893 73 24d493 48463 fedff06f
  //   900533 2200893 73 100493 249493 900533 2200893 73 48463 fedff06f 100493 1f49493 900533 2200893 73
  //   4034d493 900533 2200893 73 4044d493 900533 2200893 73 4044d493 900533 2200893 73 4044d493 900533
  //   2200893 73 4044d493 900533 2200893 73 4044d493 900533 2200893 73 4044d493 900533 2200893 73 4044d493
  //   900533 2200893 73 100413 1f41993 41f9d993 433 c00913 300b13 140413 f47413 800293 100313 499993
  //   89e9b3 1300533 2200893 73 406282b3 fe0294e3 140413 f00f93 1f47433 1c41413 800293 100313 49d993
  //   89e9b3 1300533 2200893 73 406282b3 fe0294e3 1c45413 406b0b33 b0463 f95ff06f 2b3 fff2c293 829293
  //   ff2e293 500533 2200893 73 fff00413 493 84a023 140413 448493 84a023 140413 448493 84a023 140413
  //   448493 84a023 140413 448493 84a023 140413 448493 84a023 140413 448493 84a023 140413 448493 84a023
  //   140413 448493 84a023 140413 448493 84a023 140413 448493 84a023 140413 448493 84a023 140413 448493
  //   84a023 140413 448493 84a023 140413 448493 84a023 140413 448493 84a023 140413 448493 140413 433
  //   3c00493 42983 4aa03 149a2b3 28663 134a023 1442023 ffc48493 fe9412e3 800533 2200893 73 440413 3c00493
  //   fc9416e3 a00893 73 413 140413 800533 2200893 73 240413 800533 2200893 73 340413 800533 2200893 73
  //   440413 800533 2200893 73 540413 800533 2200893 73 640413 800533 2200893 73 740413 800533 2200893 73
  //   840413 800533 2200893 2200893 73 8067
  //   JAL
  //   JALR
  //   CSR
  //   rs1
  //   rs2
  //   rd
  //   I指令
  //   S指令
  //   B指令
  //   J指令
  //   ID
  //   Beq
  //   Bne
  //   MemToReg
  //   MemWrite
  //   AluOP
  //   AluSrcB
  //   RegWrite
  //   控制位
  //   流水调试日志用
  //   暂停节拍，不能为0
  //   戳工具置1进入计数暂停模式，ctrl+k时钟自动运行到对应节拍暂停
  //   ctrl+k关闭时钟连续运行，将控制位置零，进入单步调试模式调试
  //   R1
  //   R2
  //   rd
  //   imm1
  //   imm2
  //   可计数暂停的时钟源
  //   EX
  //   为方便自动评测，需要输出流水线各段保存的PC值，注意是PC不是PC+4，另外ID段寄存器写入信息，Mem段内存写入信息也要输出
  //   ALUresult
  //   RegWrite
  //   MEM
  //   数据存储器
  //   MemtoReg
  //   JAL
  //   JALR
  //   LBU
  //   WB
endmodule
module \重定向流水线  (
  output RegWrite,
  output MemWrite,
  output [31:0] IF_PC,
  output [31:0] ID_PC,
  output [31:0] EX_PC,
  output [31:0] M_PC,
  output [31:0] WB_PC,
  output [31:0] RDin,
  output [31:0] MDin,
  output [31:0] LedData
);

  wire ALUequal, ALUge, and_1_out, and_2_out, and_3_out, and_4_out, and_5_out, and_6_out, branch, CLK,
       clock_1_out, comparator_1_eq, comparator_1_lt, comparator_2_eq, d_ff_1_q, EX_ecall, ex_mem_1_halt_2,
       ex_mem_1_jal_2, ex_mem_1_jalr_2, ex_mem_1_lbu_2, ex_mem_1_memtoreg_2, ex_mem_1_regwrite_2,
       ex_mem_1_uret_2, exhalt, flush, Go, halt, ID_ecall, id_ex_1_alusrcb_2, id_ex_1_beq_2, id_ex_1_bge_2,
       id_ex_1_bne_2, id_ex_1_jal_2, id_ex_1_lbu_2, id_ex_1_memtoreg_2, id_ex_1_memwrite_2,
       id_ex_1_regwrite_2, id_ex_1_u_type_2, id_ex_1_uret_2, IR1, IR2, IR3, jal, mem_wb_1_halt_2,
       mem_wb_1_jal_2, mem_wb_1_jalr_2, mem_wb_1_lbu_2, mem_wb_1_memtoreg_2, mem_wb_1_u_type_2, MemUtype,
       nand_1_out, not_1_out, not_2_out, not_3_out, not_4_out, not_5_out, not_6_out, not_7_out, or_1_out,
       or_3_out, or_5_out, RST, Stype, Utype, W1, W2, W3, \冲突 , \单周期硬布线控制器_1_alu_src , \单周期硬布线控制器_1_beq ,
       \单周期硬布线控制器_1_bge , \单周期硬布线控制器_1_bne , \单周期硬布线控制器_1_csr , \单周期硬布线控制器_1_jalr , \单周期硬布线控制器_1_lbu ,
       \单周期硬布线控制器_1_memtoreg , \单周期硬布线控制器_1_memwrite , \单周期硬布线控制器_1_regwrite , \单周期硬布线控制器_1_u1 ,
       \单周期硬布线控制器_1_u2 , \单周期硬布线控制器_1_uret ;
  wire [1:0] id_ex_1_jalr_2, id_ex_1_rs1f_2, id_ex_1_rs2f_2, multiplexer_8_out, or_7_out, r1_forward,
       r2_forward;
  wire [3:0] id_ex_1_aluop_2, \单周期硬布线控制器_1_alu_op ;
  wire [4:0] EX_rd, MEM_rd, multiplexer_2_out, multiplexer_3_out, \WB地址 ;
  wire [7:0] multiplexer_12_out;
  wire [11:0] multiplexer_4_out;
  wire [12:0] CNT_num;
  wire [15:0] \LoadUse次数 , \总周期数 , \插入气泡数 , \无条件分支数 , \条件分支成功数 ;
  wire [31:0] adder_2_out, ALUresult, bit_extender_1_out, bit_extender_2_out, bit_extender_3_out,
       bit_extender_4_out, EX_IR, ex_mem_1_pc_4_2, EX_R1, EX_R2, id_ex_1_imm_1_2, id_ex_1_imm_2_2,
       id_ex_1_imm_3_2, id_ex_1_pc_4_2, ID_IR, if_id_1_pc_4_2, IF_IR, Jaddress, LBUData, MEM_AluResult,
       MEM_IR, MEM_Uimm, mem_wb_1_aluresult_2, mem_wb_1_memdata_2, mem_wb_1_pc_4_2, mem_wb_1_uimm_2,
       multiplexer_1_out, multiplexer_5_out, multiplexer_7_out, multiplexer_10_out, newr1, newr2, PC_4,
       ram_1_data, regifile_1_r1, regifile_1_r2, shifter_1_out, shifter_2_out, WB_IR;

  Button \u_总复位  (.out(RST));
  Button _1 (.out(IR1));
  Button _2 (.out(IR2));
  Button _3 (.out(IR3));
  // Probe on \总周期数 
  // Probe on \总周期数 
  Button \u_继续运行  (.out(Go));
  LED #(.active("true")) led_1 (.in(W1));
  LED #(.active("true")) led_2 (.in(W2));
  LED #(.active("true")) led_3 (.in(W3));
  not not_1 (not_1_out, halt);
  Hex_Digit_Display hex_digit_display_1 (.value(LedData[31:28]));  // open: dp
  // Probe on IF_PC[19:0]
  // RiscV_Probe riscv_probe_1: pin names not known; wires that end beside it: IF_IR
  and and_1 (and_1_out, or_1_out, not_2_out);
  Multiplexer #(.select(2), .width(32), .disabled("Z"), .enable("false")) multiplexer_1 (
    .in0(PC_4), .in1(ALUresult), .in2(Jaddress), .out(multiplexer_1_out), .sel(id_ex_1_jalr_2));  // open: in3
  or or_1 (or_1_out, not_1_out, Go);
  not not_2 (not_2_out, \冲突 );
  Hex_Digit_Display hex_digit_display_2 (.value(LedData[27:24]));  // open: dp
  Hex_Digit_Display hex_digit_display_3 (.value(LedData[23:20]));  // open: dp
  // Probe on ID_PC[19:0]
  // RiscV_Probe riscv_probe_2: pin names not known; wires that end beside it: ID_IR
  Register #(.width(32), .trigger("rising"), .Select("low")) PC (
    .D(multiplexer_1_out), .en(and_1_out), .Q(IF_PC), .clk(CLK), .clr(RST));
  Hex_Digit_Display hex_digit_display_4 (.value(LedData[19:16]));  // open: dp
  Hex_Digit_Display hex_digit_display_5 (.value(LedData[15:12]));  // open: dp
  Adder #(.width(32)) adder_1 (.a(IF_PC), .b(32'h4), .out(PC_4));  // open: cin, cout
  Hex_Digit_Display hex_digit_display_6 (.value(LedData[7:4]));  // open: dp
  Hex_Digit_Display hex_digit_display_7 (.value(LedData[11:8]));  // open: dp
  // Probe on EX_PC[19:0]
  // RiscV_Probe riscv_probe_3: pin names not known; wires that end beside it: EX_IR
  // RiscV_Probe riscv_probe_4: pin names not known; wires that end beside it: IF_IR
  Hex_Digit_Display hex_digit_display_8 (.value(LedData[3:0]));  // open: dp
  ROM #(.addrWidth(10), .dataWidth(32), .Select("high")) rom_1 (.addr(IF_PC[11:2]), .data(IF_IR));
  not not_3 (not_3_out, halt);
  // Probe on \总周期数 
  // Probe on M_PC[19:0]
  // RiscV_Probe riscv_probe_5: pin names not known; wires that end beside it: MEM_IR
  or or_2 (branch, id_ex_1_jalr_2[0], id_ex_1_jalr_2[1]);
  IF_ID if_id_1 (
    .PC(IF_PC), .PC_4(PC_4), .IR(IF_IR), .PC_2(ID_PC), .PC_4_2(if_id_1_pc_4_2), .IR_2(ID_IR), .reset(1'b0),
    .flush(branch), .en(and_2_out), .CLK(CLK));  // open: 预测跳转, 预测跳转_2
  and and_2 (and_2_out, or_3_out, not_4_out);
  or or_3 (or_3_out, not_3_out, Go);
  not not_4 (not_4_out, \冲突 );
  // Probe on \总周期数 
  // Probe on \无条件分支数 
  // Probe on \条件分支成功数 
  // Probe on \插入气泡数 
  // Probe on \LoadUse次数 
  // Probe on IF_PC[11:0]
  // Probe on WB_PC[19:0]
  // RiscV_Probe riscv_probe_6: pin names not known; wires that end beside it: WB_IR
  \单周期硬布线控制器  \u_单周期硬布线控制器_1  (
    .Funct({ID_IR[30], ID_IR[25], ID_IR[14:12]}), .OP(ID_IR[6:2]), .ALU_OP(\单周期硬布线控制器_1_alu_op ),
    .MemToReg(\单周期硬布线控制器_1_memtoreg ), .MemWrite(\单周期硬布线控制器_1_memwrite ), .ALU_SRC(\单周期硬布线控制器_1_alu_src ),
    .RegWrite(\单周期硬布线控制器_1_regwrite ), .ecall(ID_ecall), .S_type(Stype), .Jalr(\单周期硬布线控制器_1_jalr ),
    .Beq(\单周期硬布线控制器_1_beq ), .JAL(jal), .Bne(\单周期硬布线控制器_1_bne ), .in_3(ID_IR[21]), .uret(\单周期硬布线控制器_1_uret ),
    .u2(\单周期硬布线控制器_1_u2 ), .u1(\单周期硬布线控制器_1_u1 ), .csr(\单周期硬布线控制器_1_csr ), .U_type(Utype),
    .bge(\单周期硬布线控制器_1_bge ), .LBU(\单周期硬布线控制器_1_lbu ));
  Multiplexer #(.select(1), .width(5), .disabled("Z"), .enable("false")) multiplexer_2 (
    .in0(ID_IR[19:15]), .in1(5'b10001), .out(multiplexer_2_out), .sel(ID_ecall));
  Multiplexer #(.select(1), .width(5), .disabled("Z"), .enable("false")) multiplexer_3 (
    .in0(ID_IR[24:20]), .in1(5'b01010), .out(multiplexer_3_out), .sel(ID_ecall));
  Multiplexer #(.select(1), .width(12), .disabled("Z"), .enable("false")) multiplexer_4 (
    .in0(ID_IR[31:20]), .in1({ID_IR[31:25], ID_IR[11:7]}), .out(multiplexer_4_out), .sel(Stype));
  assign bit_extender_1_out = {{12{ID_IR[31]}}, ID_IR[31:12]};  // Bit_Extender bit_extender_1
  Shifter #(.width(32), .shift("ll")) shifter_1 (.in(bit_extender_1_out), .\dist (5'b01100), .out(shifter_1_out));
  // Probe on ID_PC[11:0]
  // Probe on EX_PC[11:0]
  assign bit_extender_2_out = {{20{multiplexer_4_out[11]}}, multiplexer_4_out};  // Bit_Extender bit_extender_2
  assign bit_extender_3_out = {{20{ID_IR[31]}}, {ID_IR[31], ID_IR[7], ID_IR[30:25], ID_IR[11:8]}};  // Bit_Extender bit_extender_3
  assign bit_extender_4_out = {{12{ID_IR[31]}}, {ID_IR[31], ID_IR[19:12], ID_IR[20], ID_IR[30:21]}};  // Bit_Extender bit_extender_4
  // Probe on M_PC[11:0]
  D_Flip_Flop #(.trigger("high"), .Pre_Clr_Positions("LEGACY"), .NegatePresetClear("false"), .enable("true"), .NewFFLayout("false")) d_ff_1 (.Q(d_ff_1_q));  // open: clk, D, Qn, preset, en, reset
  // Probe on 13'hc
  Regifile regifile_1 (
    .Din(RDin), .Clk(not_5_out), .R1(regifile_1_r1), .R2(regifile_1_r2), .WE(RegWrite), .W_num(\WB地址 ),
    .R1_num(multiplexer_2_out), .R2_num(multiplexer_3_out));
  not not_5 (not_5_out, CLK);
  Multiplexer #(.select(1), .width(32), .disabled("Z"), .enable("false")) multiplexer_5 (
    .in0(bit_extender_3_out), .in1(bit_extender_4_out), .out(multiplexer_5_out), .sel(jal));
  // Probe on WB_PC[11:0]
  Comparator #(.width(13), .mode("twosComplement")) comparator_1 (
    .a(CNT_num), .b(13'hc), .eq(comparator_1_eq), .lt(comparator_1_lt));  // open: gt
  Clock #(.highDuration(1), .lowDuration(1)) clock_1 (.out(clock_1_out));
  nand nand_1 (nand_1_out, d_ff_1_q, comparator_1_eq);
  Counter #(.width(13), .max('h1fff), .ongoal("stay"), .trigger("rising"), .behavior("old")) counter_1 (
    .count(comparator_1_lt), .Q(CNT_num), .clk(clock_1_out));  // open: load, D, carry, clr, preset
  ID_EX id_ex_1 (
    .Beq(\单周期硬布线控制器_1_beq ), .Bne(\单周期硬布线控制器_1_bne ), .MemToReg(\单周期硬布线控制器_1_memtoreg ),
    .MemWrite(\单周期硬布线控制器_1_memwrite ), .RegWrite(\单周期硬布线控制器_1_regwrite ), .JAL(jal),
    .JALR(\单周期硬布线控制器_1_jalr ), .URET(\单周期硬布线控制器_1_uret ), .S_type(Stype), .U_type(Utype),
    .bge(\单周期硬布线控制器_1_bge ), .csr(\单周期硬布线控制器_1_csr ), .LBU(\单周期硬布线控制器_1_lbu ), .ecall(ID_ecall),
    .AluOP(\单周期硬布线控制器_1_alu_op ), .rd(ID_IR[11:7]), .R1(regifile_1_r1), .R2(regifile_1_r2),
    .imm_1(bit_extender_2_out), .imm_2(multiplexer_5_out), .PC(ID_PC), .PC_4(if_id_1_pc_4_2), .IR(ID_IR),
    .rs1f(r1_forward), .rs2f(r2_forward), .Beq_2(id_ex_1_beq_2), .Bne_2(id_ex_1_bne_2),
    .MemToReg_2(id_ex_1_memtoreg_2), .MemWrite_2(id_ex_1_memwrite_2), .RegWrite_2(id_ex_1_regwrite_2),
    .JAL_2(id_ex_1_jal_2), .JALR_2(id_ex_1_jalr_2[0]), .URET_2(id_ex_1_uret_2), .U_type_2(id_ex_1_u_type_2),
    .bge_2(id_ex_1_bge_2), .LBU_2(id_ex_1_lbu_2), .ecall_2(EX_ecall), .AluOP_2(id_ex_1_aluop_2),
    .rd_2(EX_rd), .R1_2(EX_R1), .R2_2(EX_R2), .imm_1_2(id_ex_1_imm_1_2), .imm_2_2(id_ex_1_imm_2_2),
    .PC_2(EX_PC), .PC_4_2(id_ex_1_pc_4_2), .IR_2(EX_IR), .rs1f_2(id_ex_1_rs1f_2), .rs2f_2(id_ex_1_rs2f_2),
    .reset(1'b0), .flush(flush), .en(or_3_out), .CLK(CLK), .AluSrcB(\单周期硬布线控制器_1_alu_src ),
    .AluSrcB_2(id_ex_1_alusrcb_2), .imm_3(shifter_1_out), .imm_3_2(id_ex_1_imm_3_2));  // open: S_type_2, csr_2, 预测跳转_2, 预测跳转
  Multiplexer #(.select(2), .width(32), .disabled("Z"), .enable("false")) multiplexer_6 (
    .in0(EX_R1), .in1(RDin), .in2(MEM_AluResult), .out(newr1), .sel(id_ex_1_rs1f_2));  // open: in3
  assign CLK = nand_1_out ? clock_1_out : 1'bz;  // Controlled_Buffer controlled_buffer_1
  \重定向流水线处理  \u_重定向流水线处理_1  (
    .IR(ID_IR), .u1(\单周期硬布线控制器_1_u1 ), .EX_RegWrite(id_ex_1_regwrite_2), .u2(\单周期硬布线控制器_1_u2 ),
    .MEM_RegWrite(ex_mem_1_regwrite_2), .EX_rd(EX_rd), .branch(branch), .EX_MemToReg(id_ex_1_memtoreg_2),
    .MEM_rd(MEM_rd), .ecall(ID_ecall), .\冲突 (\冲突 ), .flush(flush), .RS1_Forward(r1_forward),
    .RS2_Forward(r2_forward));
  or or_4 (id_ex_1_jalr_2[1], id_ex_1_jal_2, or_5_out);
  and and_3 (and_3_out, id_ex_1_beq_2, ALUequal);
  Pull_Resistor #(.pull(1)) pull_resistor_1 (.node(CLK));
  or or_5 (or_5_out, and_3_out, and_5_out, and_4_out);
  and and_4 (and_4_out, id_ex_1_bne_2, ~ALUequal);  // AND_Gate
  Multiplexer #(.select(1), .width(32), .disabled("Z"), .enable("false")) multiplexer_7 (
    .in0(newr2), .in1(id_ex_1_imm_1_2), .out(multiplexer_7_out), .sel(id_ex_1_alusrcb_2));
  Shifter #(.width(32), .shift("ll")) shifter_2 (.in(id_ex_1_imm_2_2), .\dist (5'b00001), .out(shifter_2_out));
  Comparator #(.width(32), .mode("twosComplement")) comparator_2 (
    .a(newr1), .b(32'h22), .eq(comparator_2_eq));  // open: gt, lt
  Multiplexer #(.select(1), .width(2), .disabled("Z"), .enable("false")) multiplexer_8 (
    .in0(id_ex_1_rs2f_2), .in1(2'b11), .out(multiplexer_8_out), .sel(MemUtype));
  Multiplexer #(.select(2), .width(32), .disabled("Z"), .enable("false")) multiplexer_9 (
    .in0(EX_R2), .in1(RDin), .in2(MEM_AluResult), .in3(MEM_Uimm), .out(newr2), .sel(multiplexer_8_out));
  and and_5 (and_5_out, id_ex_1_bge_2, ALUge);
  ALU alu_1 (
    .X(newr1), .Y(multiplexer_7_out), .AluOP(id_ex_1_aluop_2), .Equal(ALUequal), .Result(ALUresult),
    .out_4(ALUge));  // open: Result_2, out_6
  Adder #(.width(32)) adder_2 (.a(id_ex_1_imm_3_2), .b(EX_PC), .out(adder_2_out));  // open: cin, cout
  Adder #(.width(32)) adder_3 (.a(shifter_2_out), .b(EX_PC), .out(Jaddress), .cin(1'b0));  // open: cout
  not not_6 (not_6_out, comparator_2_eq);
  and and_6 (and_6_out, comparator_2_eq, EX_ecall);
  not not_7 (not_7_out, halt);
  and and_7 (exhalt, EX_ecall, not_6_out);
  Counter #(.width(16), .max('hffff), .ongoal("wrap"), .trigger("rising"), .behavior("new")) counter_2 (
    .load(1'b0), .D({16{1'b0}}), .count(not_7_out), .Q(\总周期数 ), .clk(CLK), .clr(1'b0), .down(1'b0));  // open: carry, preset
  Register #(.width(32), .trigger("rising"), .Select("low")) register_1 (
    .D(newr2), .en(and_6_out), .Q(LedData), .clk(CLK));  // open: clr
  EX_MEM ex_mem_1 (
    .MemToReg(id_ex_1_memtoreg_2), .MemWrite(id_ex_1_memwrite_2), .RegWrite(id_ex_1_regwrite_2),
    .JAL(id_ex_1_jal_2), .JALR(id_ex_1_jalr_2[0]), .URET(id_ex_1_uret_2), .LBU(id_ex_1_lbu_2), .halt(exhalt),
    .rd(EX_rd), .result(ALUresult), .R2(newr2), .PC(EX_PC), .PC_4(id_ex_1_pc_4_2), .IR(EX_IR),
    .MemToReg_2(ex_mem_1_memtoreg_2), .MemWrite_2(MemWrite), .RegWrite_2(ex_mem_1_regwrite_2),
    .JAL_2(ex_mem_1_jal_2), .JALR_2(ex_mem_1_jalr_2), .URET_2(ex_mem_1_uret_2), .LBU_2(ex_mem_1_lbu_2),
    .halt_2(ex_mem_1_halt_2), .rd_2(MEM_rd), .result_2(MEM_AluResult), .R2_2(MDin), .PC_2(M_PC),
    .PC_4_2(ex_mem_1_pc_4_2), .IR_2(MEM_IR), .reset(1'b0), .flush(1'b0), .en(or_3_out), .CLK(CLK),
    .U_type(id_ex_1_u_type_2), .U_type_2(MemUtype), .Uimm(adder_2_out), .Uimm_2(MEM_Uimm));
  RAM #(.addrWidth(10), .dataWidth(32), .bus("separate"), .Select("high")) ram_1 (
    .addr(MEM_AluResult[11:2]), .din(MDin), .data(ram_1_data), .str(MemWrite), .sel(1'b1), .clk(CLK),
    .ld(1'b1));  // open: clr
  MEM_WB mem_wb_1 (
    .LBU(ex_mem_1_lbu_2), .MemToReg(ex_mem_1_memtoreg_2), .RegWrite(ex_mem_1_regwrite_2),
    .JAL(ex_mem_1_jal_2), .JALR(ex_mem_1_jalr_2), .URET(ex_mem_1_uret_2), .halt(ex_mem_1_halt_2),
    .rd(MEM_rd), .ALUresult(MEM_AluResult), .MemData(ram_1_data), .PC(M_PC), .PC_4(ex_mem_1_pc_4_2),
    .IR(MEM_IR), .LBU_2(mem_wb_1_lbu_2), .MemToReg_2(mem_wb_1_memtoreg_2), .RegWrite_2(RegWrite),
    .JAL_2(mem_wb_1_jal_2), .JALR_2(mem_wb_1_jalr_2), .halt_2(mem_wb_1_halt_2), .rd_2(\WB地址 ),
    .ALUresult_2(mem_wb_1_aluresult_2), .MemData_2(mem_wb_1_memdata_2), .PC_2(WB_PC),
    .PC_4_2(mem_wb_1_pc_4_2), .IR_2(WB_IR), .reset(1'b0), .flush(1'b0), .en(or_3_out), .CLK(CLK),
    .U_type(MemUtype), .U_type_2(mem_wb_1_u_type_2), .Uimm(MEM_Uimm), .Uimm_2(mem_wb_1_uimm_2));  // open: URET_2
  or or_6 (or_7_out[1], mem_wb_1_jal_2, mem_wb_1_u_type_2, mem_wb_1_jalr_2);
  or or_7 (or_7_out[0], mem_wb_1_memtoreg_2, mem_wb_1_u_type_2);
  Multiplexer #(.select(1), .width(32), .disabled("Z"), .enable("false")) multiplexer_10 (
    .in0(mem_wb_1_memdata_2), .in1(LBUData), .out(multiplexer_10_out), .sel(mem_wb_1_lbu_2));
  Multiplexer #(.select(2), .width(32), .disabled("Z"), .enable("false")) multiplexer_11 (
    .in0(mem_wb_1_aluresult_2), .in1(multiplexer_10_out), .in2(mem_wb_1_pc_4_2), .in3(mem_wb_1_uimm_2),
    .out(RDin), .sel(or_7_out));
  D_Flip_Flop #(.trigger("rising"), .Pre_Clr_Positions("ABOVE_BELOW"), .NegatePresetClear("false"), .enable("true"), .NewFFLayout("true")) d_ff_2 (
    .clk(mem_wb_1_halt_2), .D(1'b1), .Q(halt), .preset(1'b0), .en(1'b1), .reset(Go));  // open: Qn
  Multiplexer #(.select(2), .width(8), .disabled("Z"), .enable("false")) multiplexer_12 (
    .in0(mem_wb_1_memdata_2[7:0]), .in1(mem_wb_1_memdata_2[15:8]), .in2(mem_wb_1_memdata_2[23:16]),
    .in3(mem_wb_1_memdata_2[31:24]), .out(multiplexer_12_out), .sel(mem_wb_1_aluresult_2[1:0]));
  assign LBUData = {{24{1'b0}}, multiplexer_12_out};  // Bit_Extender bit_extender_5

  // Other names for the same wires on the sheet: MEM_PC[31:0] = M_PC

  // Notes on the sheet:
  //   中断源
  //   时空图监测，可删除
  //   中断等待指示
  //   数码管输出
  //   IF
  //   指令探针
  //   指令存储器
  //   contents of rom_1 (hex, n*v repeats v):
  //   100493 100006f 100493 200913 300993 100006f 100493 200913 300993 100006f 100493 200913 300993
  //   100006f 100493 200913 300993 3fc000ef 100413 100493 1f49493 900533 2200893 73 24d493 48463 fedff06f
  //   900533 2200893 73 100493 249493 900533 2200893 73 48463 fedff06f 100493 1f49493 900533 2200893 73
  //   4034d493 900533 2200893 73 4044d493 900533 2200893 73 4044d493 900533 2200893 73 4044d493 900533
  //   2200893 73 4044d493 900533 2200893 73 4044d493 900533 2200893 73 4044d493 900533 2200893 73 4044d493
  //   900533 2200893 73 100413 1f41993 41f9d993 433 c00913 300b13 140413 f47413 800293 100313 499993
  //   89e9b3 1300533 2200893 73 406282b3 fe0294e3 140413 f00f93 1f47433 1c41413 800293 100313 49d993
  //   89e9b3 1300533 2200893 73 406282b3 fe0294e3 1c45413 406b0b33 b0463 f95ff06f 2b3 fff2c293 829293
  //   ff2e293 500533 2200893 73 fff00413 493 84a023 140413 448493 84a023 140413 448493 84a023 140413
  //   448493 84a023 140413 448493 84a023 140413 448493 84a023 140413 448493 84a023 140413 448493 84a023
  //   140413 448493 84a023 140413 448493 84a023 140413 448493 84a023 140413 448493 84a023 140413 448493
  //   84a023 140413 448493 84a023 140413 448493 84a023 140413 448493 84a023 140413 448493 140413 433
  //   3c00493 42983 4aa03 149a2b3 28663 134a023 1442023 ffc48493 fe9412e3 800533 2200893 73 440413 3c00493
  //   fc9416e3 a00893 73 13 430497 900533 2200893 73 430497 900533 2200893 73 430497 900533 2200893 73
  //   430497 900533 2200893 73 430497 900533 2200893 73 430497 900533 2200893 73 430497 900533 2200893 73
  //   430497 900533 2200893 73 a00893 73 fff00293 313 1900413 841413 9700493 940533 2200893 73 5484b3
  //   494b313 fe0306e3 a00893 73 313 1000e13 8400493 849493 8348493 400913 891913 490913 849493 8248493
  //   849493 8148493 891913 490913 891913 490913 932023 12484b3 430313 fffe0e13 fe0e18e3 2000e13 313 34483
  //   900533 2200893 73 130313 fffe0e13 fe0e14e3 a00893 73 f00493 900533 2200893 73 fff48493 fe04d8e3
  //   a00893 73 413 140413 800533 2200893 73 240413 800533 2200893 73 340413 800533 2200893 73 440413
  //   800533 2200893 73 540413 800533 2200893 73 640413 800533 2200893 73 740413 800533 2200893 73 840413
  //   800533 2200893 2200893 73 8067
  //   JAL
  //   JALR
  //   CSR
  //   rs1
  //   rs2
  //   rd
  //   I指令
  //   S指令
  //   B指令
  //   U指令
  //   J指令
  //   ID
  //   Beq
  //   Bne
  //   MemToReg
  //   MemWrite
  //   AluOP
  //   AluSrcB
  //   RegWrite
  //   控制位
  //   流水调试日志用
  //   暂停节拍，不能为0
  //   戳工具置1进入计数暂停模式，ctrl+k时钟自动运行到对应节拍暂停
  //   ctrl+k关闭时钟连续运行，将控制位置零，进入单步调试模式调试
  //   R1
  //   R2
  //   rd
  //   imm1
  //   imm2
  //   可计数暂停的时钟源
  //   EX
  //   为方便自动评测，需要输出流水线各段保存的PC值，注意是PC不是PC+4，另外ID段寄存器写入信息，Mem段内存写入信息也要输出
  //   ALUresult
  //   RegWrite
  //   MEM
  //   数据存储器
  //   MemtoReg
  //   JAL
  //   JALR
  //   LBU
  //   WB
endmodule

module \中断按键参考电路  (
  input  \同步清零信号 ,
  output \与中断屏蔽位与 
);

  wire \_1号中断_out , and_1_out, clock_1_out, d_ff_1_q, or_1_out, or_2_out;

  Clock #(.highDuration(1), .lowDuration(1)) clock_1 (.out(clock_1_out));
  Button \_1号中断  (.out(\_1号中断_out ));
  or or_1 (or_1_out, \与中断屏蔽位与 , d_ff_1_q);
  LED #(.active("true")) \_1号中断等待指示灯  (.in(or_1_out));
  D_Flip_Flop #(.trigger("rising"), .Pre_Clr_Positions("LEGACY"), .NegatePresetClear("false"), .enable("true"), .NewFFLayout("false")) d_ff_1 (
    .clk(\_1号中断_out ), .D(1'b1), .Q(d_ff_1_q), .reset(\与中断屏蔽位与 ));  // open: Qn, preset, en
  or or_2 (or_2_out, d_ff_1_q, \与中断屏蔽位与 );
  and and_1 (and_1_out, or_2_out, ~\同步清零信号 );  // AND_Gate
  D_Flip_Flop #(.trigger("rising"), .Pre_Clr_Positions("LEGACY"), .NegatePresetClear("false"), .enable("true"), .NewFFLayout("false")) IR1 (
    .clk(clock_1_out), .D(and_1_out), .Q(\与中断屏蔽位与 ));  // open: Qn, preset, en, reset

  // Notes on the sheet:
  //   中断信号采样参考电路
  //   Reset 
endmodule

module \单周期_单级中断  (
  input  IR1,
  input  IR2,
  input  IR3,
  output RegWrite,
  output MemWrite,
  output [31:0] PC,
  output [31:0] IR,
  output [31:0] RDin,
  output [31:0] MDin,
  output [31:0] LedData
);

  wire ALUequal, ALUge, and_1_out, and_2_out, and_3_out, and_4_out, and_5_out, and_6_out, and_8_out, Beq,
       Bne, CLK, clock_1_out, comparator_1_eq, comparator_2_eq, comparator_3_eq, comparator_4_eq,
       comparator_5_eq, comparator_6_eq, comparator_6_lt, csr, d_ff_1_q, d_ff_2_q, d_ff_3_q, d_ff_8_q, ecall,
       Go, halt, IE, IR1_t, IR2_t, IR3_t, IRA, IRB, IRC, jal, jalr, LBU, MemToReg, nand_1_out, not_1_out,
       not_2_out, not_3_out, not_4_out, or_4_out, or_5_out, or_6_out, or_7_out, or_8_out, or_9_out,
       or_13_out, RESET1, RESET2, RESET3, RST, Stype, uret, Utype, W1, W2, W3, \中断 , \中断1 , \中断2 , \中断3 ,
       \中断产生 , \单周期硬布线控制器_1_alu_src , \单周期硬布线控制器_1_bge ;
  wire [1:0] or_14_out, priority_encoder_1_out, \中断号 , \中断号_q ;
  wire [3:0] \单周期硬布线控制器_1_alu_op ;
  wire [4:0] multiplexer_2_out, multiplexer_3_out;
  wire [7:0] multiplexer_10_out;
  wire [11:0] multiplexer_4_out;
  wire [12:0] CNT_num;
  wire [15:0] \总周期数 ;
  wire [31:0] adder_2_out, adder_3_out, adder_4_out, ALUresult, bit_extender_1_out, bit_extender_2_out,
       bit_extender_3_out, bit_extender_4_out, EPC, LBUData, multiplexer_6_out, multiplexer_8_out, PC_4,
       ram_1_data, regifile_1_r1, shifter_1_out, shifter_2_out, shifter_3_out, \中断地址 , \新PC , \老PC ;

  Button \u_继续运行  (.out(Go));
  Button _1 (.out(IRA));
  Button _2 (.out(IRB));
  Button _3 (.out(IRC));
  LED #(.active("true")) led_1 (.in(W1));
  LED #(.active("true")) led_2 (.in(W2));
  LED #(.active("true")) led_3 (.in(W3));
  Priority_Encoder #(.select(2), .disabled("Z")) priority_encoder_1 (
    .in0(1'b1), .in1(jalr), .in2(jal), .in3(or_9_out), .out(priority_encoder_1_out), .en_in(1'b1));  // open: gs, en_out
  Hex_Digit_Display hex_digit_display_1 (.value(LedData[31:28]));  // open: dp
  Comparator #(.width(16), .mode("twosComplement")) comparator_1 (
    .a(16'h23b), .b(\总周期数 ), .eq(comparator_1_eq));  // open: gt, lt
  Comparator #(.width(16), .mode("twosComplement")) comparator_2 (
    .a(\总周期数 ), .b(16'h1), .eq(comparator_2_eq));  // open: gt, lt
  Comparator #(.width(16), .mode("twosComplement")) comparator_3 (
    .a(\总周期数 ), .b(16'h4), .eq(comparator_3_eq));  // open: gt, lt
  Comparator #(.width(16), .mode("twosComplement")) comparator_4 (
    .a(\总周期数 ), .b(16'h7), .eq(comparator_4_eq));  // open: gt, lt
  D_Flip_Flop #(.trigger("rising"), .Pre_Clr_Positions("LEGACY"), .NegatePresetClear("false"), .enable("true"), .NewFFLayout("false")) d_ff_1 (
    .clk(IR1_t), .D(1'b1), .Q(d_ff_1_q), .en(1'b1), .reset(\中断1 ));  // open: Qn, preset
  or or_1 (W1, \中断1 , d_ff_1_q);
  D_Flip_Flop #(.trigger("rising"), .Pre_Clr_Positions("LEGACY"), .NegatePresetClear("false"), .enable("true"), .NewFFLayout("false")) d_ff_2 (
    .clk(IR2_t), .D(1'b1), .Q(d_ff_2_q), .en(1'b1), .reset(\中断2 ));  // open: Qn, preset
  or or_2 (W2, \中断2 , d_ff_2_q);
  D_Flip_Flop #(.trigger("rising"), .Pre_Clr_Positions("LEGACY"), .NegatePresetClear("false"), .enable("true"), .NewFFLayout("false")) d_ff_3 (
    .clk(IR3_t), .D(1'b1), .Q(d_ff_3_q), .en(1'b1), .reset(\中断3 ));  // open: Qn, preset
  or or_3 (W3, \中断3 , d_ff_3_q);
  and and_1 (and_1_out, Beq, ALUequal);
  Multiplexer #(.select(2), .width(32), .disabled("Z"), .enable("false")) multiplexer_1 (
    .in0(PC_4), .in1(ALUresult), .in2(adder_3_out), .in3(adder_2_out), .out(\老PC ),
    .sel(priority_encoder_1_out));
  or or_4 (or_4_out, not_1_out, Go);
  not not_1 (not_1_out, halt);
  Hex_Digit_Display hex_digit_display_2 (.value(LedData[27:24]));  // open: dp
  Hex_Digit_Display hex_digit_display_3 (.value(LedData[23:20]));  // open: dp
  or or_5 (or_5_out, comparator_1_eq, comparator_2_eq);
  assign IRA = or_5_out ? ~CLK : 1'bz;  // Controlled_Inverter controlled_inverter_1
  assign IRB = comparator_3_eq ? ~CLK : 1'bz;  // Controlled_Inverter controlled_inverter_2
  assign IRC = comparator_4_eq ? ~CLK : 1'bz;  // Controlled_Inverter controlled_inverter_3
  or or_6 (or_6_out, d_ff_1_q, \中断1 );
  or or_7 (or_7_out, d_ff_2_q, \中断2 );
  or or_8 (or_8_out, d_ff_3_q, \中断3 );
  not not_2 (not_2_out, ALUequal);
  and and_2 (and_2_out, not_2_out, Bne);
  or or_9 (or_9_out, and_1_out, and_2_out, and_6_out);
  Register #(.width(32), .trigger("rising"), .Select("low")) u_PC (
    .D(\新PC ), .en(or_4_out), .Q(PC), .clk(CLK), .clr(RST));
  Hex_Digit_Display hex_digit_display_4 (.value(LedData[15:12]));  // open: dp
  Hex_Digit_Display hex_digit_display_5 (.value(LedData[19:16]));  // open: dp
  Pull_Resistor #(.pull(0)) pull_resistor_1 (.node(IRA));
  Pull_Resistor #(.pull(0)) pull_resistor_2 (.node(IRB));
  Pull_Resistor #(.pull(0)) pull_resistor_3 (.node(IRC));
  and and_3 (and_3_out, or_6_out, ~RESET1);  // AND_Gate
  and and_4 (and_4_out, or_7_out, ~RESET2);  // AND_Gate
  and and_5 (and_5_out, or_8_out, ~RESET3);  // AND_Gate
  and and_6 (and_6_out, ALUge, \单周期硬布线控制器_1_bge );
  Adder #(.width(32)) adder_1 (.a(PC), .b(32'h4), .out(PC_4));  // open: cin, cout
  Hex_Digit_Display hex_digit_display_6 (.value(LedData[7:4]));  // open: dp
  Hex_Digit_Display hex_digit_display_7 (.value(LedData[11:8]));  // open: dp
  // Probe on \总周期数 
  D_Flip_Flop #(.trigger("rising"), .Pre_Clr_Positions("LEGACY"), .NegatePresetClear("false"), .enable("true"), .NewFFLayout("false")) d_ff_4 (
    .clk(CLK), .D(and_3_out), .Q(\中断1 ), .en(1'b1));  // open: Qn, preset, reset
  D_Flip_Flop #(.trigger("rising"), .Pre_Clr_Positions("LEGACY"), .NegatePresetClear("false"), .enable("true"), .NewFFLayout("false")) d_ff_5 (
    .clk(CLK), .D(and_4_out), .Q(\中断2 ), .en(1'b1));  // open: Qn, preset, reset
  D_Flip_Flop #(.trigger("rising"), .Pre_Clr_Positions("LEGACY"), .NegatePresetClear("false"), .enable("true"), .NewFFLayout("false")) d_ff_6 (
    .clk(CLK), .D(and_5_out), .Q(\中断3 ), .en(1'b1));  // open: Qn, preset, reset
  // RiscV_Probe riscv_probe_1: pin names not known; wires that end beside it: IR
  Hex_Digit_Display hex_digit_display_8 (.value(LedData[3:0]));  // open: dp
  ROM #(.addrWidth(10), .dataWidth(32), .Select("high")) rom_1 (.addr(PC[11:2]), .data(IR));
  Multiplexer #(.select(1), .width(5), .disabled("Z"), .enable("false")) multiplexer_2 (
    .in0(IR[19:15]), .in1(5'b10001), .out(multiplexer_2_out), .sel(ecall));
  Multiplexer #(.select(1), .width(5), .disabled("Z"), .enable("false")) multiplexer_3 (
    .in0(IR[24:20]), .in1(5'b01010), .out(multiplexer_3_out), .sel(ecall));
  or or_10 (IR1_t, IR1, IRA);
  \单周期硬布线控制器  \u_单周期硬布线控制器_1  (
    .Funct({IR[30], IR[25], IR[14:12]}), .OP(IR[6:2]), .ALU_OP(\单周期硬布线控制器_1_alu_op ), .MemToReg(MemToReg),
    .MemWrite(MemWrite), .ALU_SRC(\单周期硬布线控制器_1_alu_src ), .RegWrite(RegWrite), .ecall(ecall), .S_type(Stype),
    .Jalr(jalr), .Beq(Beq), .JAL(jal), .Bne(Bne), .in_3(IR[21]), .uret(uret), .csr(csr), .U_type(Utype),
    .bge(\单周期硬布线控制器_1_bge ), .LBU(LBU));  // open: u2, u1
  Multiplexer #(.select(1), .width(12), .disabled("Z"), .enable("false")) multiplexer_4 (
    .in0(IR[31:20]), .in1({IR[31:25], IR[11:7]}), .out(multiplexer_4_out), .sel(Stype));
  assign bit_extender_1_out = {{12{IR[31]}}, IR[31:12]};  // Bit_Extender bit_extender_1
  or or_11 (IR2_t, IR2, IRB);
  assign bit_extender_2_out = {{20{multiplexer_4_out[11]}}, multiplexer_4_out};  // Bit_Extender bit_extender_2
  Shifter #(.width(32), .shift("ll")) shifter_1 (.in(bit_extender_1_out), .\dist (5'b01100), .out(shifter_1_out));
  assign bit_extender_3_out = {{20{IR[31]}}, {IR[31], IR[7], IR[30:25], IR[11:8]}};  // Bit_Extender bit_extender_3
  assign bit_extender_4_out = {{12{IR[31]}}, {IR[31], IR[19:12], IR[20], IR[30:21]}};  // Bit_Extender bit_extender_4
  Multiplexer #(.select(2), .width(32), .disabled("Z"), .enable("false")) multiplexer_5 (
    .in0(\老PC ), .in1(EPC), .in2(\中断地址 ), .in3(EPC), .out(\新PC ), .sel({\中断 , uret}));
  Priority_Encoder #(.select(2), .disabled("Z")) priority_encoder_2 (
    .in1(\中断1 ), .in2(\中断2 ), .in3(\中断3 ), .out(\中断号 ), .gs(\中断产生 ));  // open: in0, en_out, en_in
  Regifile regifile_1 (
    .Din(RDin), .Clk(CLK), .R1(regifile_1_r1), .R2(MDin), .WE(RegWrite), .W_num(IR[11:7]),
    .R1_num(multiplexer_2_out), .R2_num(multiplexer_3_out));
  Shifter #(.width(32), .shift("ll")) shifter_2 (.in(bit_extender_3_out), .\dist (5'b00001), .out(shifter_2_out));
  Shifter #(.width(32), .shift("ll")) shifter_3 (.in(bit_extender_4_out), .\dist (5'b00001), .out(shifter_3_out));
  or or_12 (IR3_t, IR3, IRC);
  Multiplexer #(.select(1), .width(32), .disabled("Z"), .enable("false")) multiplexer_6 (
    .in0(MDin), .in1(bit_extender_2_out), .out(multiplexer_6_out), .sel(\单周期硬布线控制器_1_alu_src ));
  Adder #(.width(32)) adder_2 (.a(shifter_2_out), .b(PC), .out(adder_2_out));  // open: cin, cout
  Adder #(.width(32)) adder_3 (.a(shifter_3_out), .b(PC), .out(adder_3_out));  // open: cin, cout
  ALU alu_1 (
    .X(regifile_1_r1), .Y(multiplexer_6_out), .AluOP(\单周期硬布线控制器_1_alu_op ), .Equal(ALUequal),
    .Result(ALUresult), .out_4(ALUge));  // open: Result_2, out_6
  Register #(.width(32), .trigger("rising"), .Select("low")) u_EPC (
    .D(\老PC ), .en(\中断 ), .Q(EPC), .clk(CLK));  // open: clr
  Multiplexer #(.select(2), .width(32), .disabled("Z"), .enable("false")) multiplexer_7 (
    .in1(32'h30ac), .in2(32'h3150), .in3(32'h31f4), .out(\中断地址 ), .sel(\中断号 ));  // open: in0
  Adder #(.width(32)) adder_4 (.a(shifter_1_out), .b(PC), .out(adder_4_out));  // open: cin, cout
  Demultiplexer #(.select(2), .width(1), .tristate("false"), .disabled("Z"), .enable("false")) demultiplexer_1 (
    .out1(RESET1), .out2(RESET2), .out3(RESET3), .in(uret), .sel(\中断号_q ));  // open: out0
  Register #(.width(2), .trigger("rising"), .Select("low")) \u_中断号  (
    .D(\中断号 ), .en(\中断 ), .Q(\中断号_q ), .clk(CLK));  // open: clr
  not not_3 (not_3_out, halt);
  Comparator #(.width(32), .mode("twosComplement")) comparator_5 (
    .a(regifile_1_r1), .b(32'h22), .eq(comparator_5_eq));  // open: gt, lt
  and and_7 (\中断 , \中断产生 , IE);
  Counter #(.width(16), .max('hffff), .ongoal("wrap"), .trigger("rising"), .behavior("new")) counter_1 (
    .load(1'b0), .D({16{1'b0}}), .count(not_3_out), .Q(\总周期数 ), .clk(CLK), .clr(1'b0), .down(1'b0));  // open: carry, preset
  not not_4 (not_4_out, comparator_5_eq);
  and and_8 (and_8_out, comparator_5_eq, ecall);
  D_Flip_Flop #(.trigger("rising"), .Pre_Clr_Positions("LEGACY"), .NegatePresetClear("false"), .enable("true"), .NewFFLayout("false")) d_ff_7 (
    .clk(CLK), .D(\中断 ), .Qn(IE), .en(or_13_out));  // open: Q, preset, reset
  or or_13 (or_13_out, \中断 , uret);
  Pull_Resistor #(.pull(0)) pull_resistor_4 (.node(RESET1));
  and and_9 (halt, ecall, not_4_out);
  Pull_Resistor #(.pull(0)) pull_resistor_5 (.node(RESET2));
  RAM #(.addrWidth(10), .dataWidth(32), .bus("separate"), .Select("high")) ram_1 (
    .addr(ALUresult[11:2]), .din(MDin), .data(ram_1_data), .str(MemWrite), .sel(1'b1), .clk(CLK), .ld(1'b1));  // open: clr
  Register #(.width(32), .trigger("rising"), .Select("low")) register_1 (
    .D(MDin), .en(and_8_out), .Q(LedData), .clk(CLK));  // open: clr
  D_Flip_Flop #(.trigger("high"), .Pre_Clr_Positions("LEGACY"), .NegatePresetClear("false"), .enable("true"), .NewFFLayout("false")) d_ff_8 (.Q(d_ff_8_q));  // open: clk, D, Qn, preset, en, reset
  // Probe on 13'hbb
  or or_14 (or_14_out[0], Utype, MemToReg);
  Multiplexer #(.select(1), .width(32), .disabled("Z"), .enable("false")) multiplexer_8 (
    .in0(ram_1_data), .in1(LBUData), .out(multiplexer_8_out), .sel(LBU));
  Comparator #(.width(13), .mode("twosComplement")) comparator_6 (
    .a(CNT_num), .b(13'hbb), .eq(comparator_6_eq), .lt(comparator_6_lt));  // open: gt
  Clock #(.highDuration(1), .lowDuration(1)) clock_1 (.out(clock_1_out));
  Pull_Resistor #(.pull(0)) pull_resistor_6 (.node(RESET3));
  Multiplexer #(.select(2), .width(32), .disabled("Z"), .enable("false")) multiplexer_9 (
    .in0(ALUresult), .in1(multiplexer_8_out), .in2(PC_4), .in3(adder_4_out), .out(RDin), .sel(or_14_out));
  Counter #(.width(13), .max('h1fff), .ongoal("stay"), .trigger("rising"), .behavior("old")) counter_2 (
    .count(comparator_6_lt), .Q(CNT_num), .clk(clock_1_out));  // open: load, D, carry, clr, preset
  or or_15 (or_14_out[1], Utype, jal, jalr);
  Multiplexer #(.select(2), .width(8), .disabled("Z"), .enable("false")) multiplexer_10 (
    .in0(ram_1_data[7:0]), .in1(ram_1_data[15:8]), .in2(ram_1_data[23:16]), .in3(ram_1_data[31:24]),
    .out(multiplexer_10_out), .sel(ALUresult[1:0]));
  nand nand_1 (nand_1_out, d_ff_8_q, comparator_6_eq);
  assign LBUData = {{24{1'b0}}, multiplexer_10_out};  // Bit_Extender bit_extender_5
  assign CLK = nand_1_out ? clock_1_out : 1'bz;  // Controlled_Buffer controlled_buffer_1
  Pull_Resistor #(.pull(1)) pull_resistor_7 (.node(CLK));

  // Notes on the sheet:
  //   中断源
  //   中断等待指示
  //   总复位信号应将除ROM以外所有存储组件全部清零
  //   单级中断测试信号模拟器
  //   数码管输出
  //   数码管输出应该用寄存器锁存，否则显示数据只能一闪而过
  //   指令探针
  //   指令存储器
  //   rs1
  //   rs2
  //   指令字
  //   contents of rom_1 (hex, n*v repeats v):
  //   7d000113 100413 1f41993 41f9d993 433 c00913 800b13 140413 f47413 800293 100313 499993 89e9b3 1300533
  //   2200893 73 406282b3 fe0294e3 140413 f00f93 1f47433 1c41413 800293 100313 49d993 89e9b3 1300533
  //   2200893 73 406282b3 fe0294e3 1c45413 406b0b33 b0463 f95ff06f 2b3 fff2c293 1029293 fff2e293 500533
  //   2200893 73 f5dff06f 1112023 410113 a12023 410113 812023 410113 1312023 410113 1412023 410113 1512023
  //   410113 1612023 410113 100b13 300a13 100a93 1600433 441413 14469b3 1300533 2200893 73 fe0416e3
  //   415a0a33 fe0a10e3 ffc10113 12b03 ffc10113 12a83 ffc10113 12a03 ffc10113 12983 ffc10113 12403
  //   ffc10113 12503 ffc10113 12883 200073 1112023 410113 a12023 410113 812023 410113 1312023 410113
  //   1412023 410113 1512023 410113 1612023 410113 200b13 300a13 100a93 1600433 441413 14469b3 1300533
  //   2200893 73 fe0416e3 415a0a33 fe0a10e3 ffc10113 12b03 ffc10113 12a83 ffc10113 12a03 ffc10113 12983
  //   ffc10113 12403 ffc10113 12503 ffc10113 12883 200073 1112023 410113 a12023 410113 812023 410113
  //   1312023 410113 1412023 410113 1512023 410113 1612023 410113 300b13 300a13 100a93 1600433 441413
  //   14469b3 1300533 2200893 73 fe0416e3 415a0a33 fe0a10e3 ffc10113 12b03 ffc10113 12a83 ffc10113 12a03
  //   ffc10113 12983 ffc10113 12403 ffc10113 12503 ffc10113 12883 200073
  //   rd
  //   I指令
  //   S指令
  //   JAL
  //   JALR
  //   URET
  //   BGE
  //   CSR
  //   U指令
  //   B指令
  //   J指令
  //   Beq
  //   Bne
  //   MemToReg
  //   MemWrite
  //   AluOP
  //   AluSrcB
  //   RegWrite
  //   为方便自动评测，需要输出PC，IR，寄存器堆写如数据RDin
  //   RAM写使能MemWrite、RAM写入数据MDin等信号
  //   数据存储器
  //   控制位
  //   暂停节拍，不能为0
  //   戳工具置1进入计数暂停模式，ctrl+k时钟自动运行到对应节拍暂停
  //   ctrl+k关闭时钟连续运行，将控制位置零，进入单步调试模式调试
  //   可计数暂停的时钟源
endmodule

module \单周期_多级中断  (
  input  IR1,
  input  IR2,
  input  IR3,
  output RegWrite,
  output MemWrite,
  output [31:0] PC,
  output [31:0] IR,
  output [31:0] RDin,
  output [31:0] MDin,
  output [31:0] LedData
);

  wire ALUequal, ALUge, and_1_out, and_2_out, and_3_out, and_4_out, and_5_out, and_6_out, and_11_out, Beq,
       Bne, CLK, clock_1_out, comparator_1_eq, comparator_2_eq, comparator_3_eq, comparator_4_eq,
       comparator_5_eq, comparator_7_eq, comparator_8_eq, comparator_9_eq, comparator_10_eq,
       comparator_10_lt, csr, csrrci, csrrsi, d_ff_1_q, d_ff_2_q, d_ff_3_q, d_ff_8_q, demultiplexer_1_out0,
       demultiplexer_1_out1, demultiplexer_1_out2, demultiplexer_2_out0, demultiplexer_2_out1,
       demultiplexer_2_out2, ecall, Go, halt, IE, IR1_t, IR2_t, IR3_t, IRA, IRB, IRC, jal, jalr, LBU,
       MemToReg, nand_1_out, not_1_out, not_2_out, not_3_out, not_4_out, or_4_out, or_5_out, or_6_out,
       or_7_out, or_8_out, or_9_out, or_10_out, or_14_out, or_15_out, or_16_out, priority_encoder_2_gs,
       RESET1, RESET2, RESET3, RST, Stype, uret, Utype, W1, W2, W3, \中断 , \中断1 , \中断2 , \中断3 , \中断优先 ,
       \单周期硬布线控制器_1_alu_src , \单周期硬布线控制器_1_bge ;
  wire [1:0] EPC_4_q, EPC_5_q, EPC_6_q, or_17_out, priority_encoder_1_out, \中断号 , \中断计数 , \前中断号 ;
  wire [3:0] \单周期硬布线控制器_1_alu_op ;
  wire [4:0] multiplexer_2_out, multiplexer_3_out;
  wire [7:0] multiplexer_10_out;
  wire [11:0] multiplexer_4_out;
  wire [12:0] CNT_num;
  wire [15:0] \总周期数 ;
  wire [31:0] adder_2_out, adder_3_out, adder_4_out, ALUresult, bit_extender_1_out, bit_extender_2_out,
       bit_extender_3_out, bit_extender_4_out, EPC, EPC_2_q, EPC_3_q, EPC_q, LBUData, multiplexer_6_out,
       multiplexer_8_out, PC_4, ram_1_data, regifile_1_r1, shifter_1_out, shifter_2_out, shifter_3_out,
       \中断地址 , \新PC , \老PC ;

  Button \u_继续运行  (.out(Go));
  Button _1 (.out(IRA));
  Button _2 (.out(IRB));
  Button _3 (.out(IRC));
  LED #(.active("true")) led_1 (.in(W1));
  LED #(.active("true")) led_2 (.in(W2));
  LED #(.active("true")) led_3 (.in(W3));
  Hex_Digit_Display hex_digit_display_1 (.value(LedData[31:28]));  // open: dp
  or or_1 (W1, \中断1 , d_ff_1_q);
  or or_2 (W2, \中断2 , d_ff_2_q);
  or or_3 (W3, \中断3 , d_ff_3_q);
  Priority_Encoder #(.select(2), .disabled("Z")) priority_encoder_1 (
    .in0(1'b1), .in1(jalr), .in2(jal), .in3(or_4_out), .out(priority_encoder_1_out), .en_in(1'b1));  // open: gs, en_out
  Multiplexer #(.select(2), .width(32), .disabled("Z"), .enable("false")) multiplexer_1 (
    .in0(PC_4), .in1(ALUresult), .in2(adder_3_out), .in3(adder_2_out), .out(\老PC ),
    .sel(priority_encoder_1_out));
  not not_1 (not_1_out, halt);
  Hex_Digit_Display hex_digit_display_2 (.value(LedData[27:24]));  // open: dp
  Hex_Digit_Display hex_digit_display_3 (.value(LedData[23:20]));  // open: dp
  D_Flip_Flop #(.trigger("rising"), .Pre_Clr_Positions("LEGACY"), .NegatePresetClear("false"), .enable("true"), .NewFFLayout("false")) d_ff_1 (
    .clk(IR1_t), .D(1'b1), .Q(d_ff_1_q), .en(1'b1), .reset(\中断1 ));  // open: Qn, preset
  D_Flip_Flop #(.trigger("rising"), .Pre_Clr_Positions("LEGACY"), .NegatePresetClear("false"), .enable("true"), .NewFFLayout("false")) d_ff_2 (
    .clk(IR2_t), .D(1'b1), .Q(d_ff_2_q), .en(1'b1), .reset(\中断2 ));  // open: Qn, preset
  D_Flip_Flop #(.trigger("rising"), .Pre_Clr_Positions("LEGACY"), .NegatePresetClear("false"), .enable("true"), .NewFFLayout("false")) d_ff_3 (
    .clk(IR3_t), .D(1'b1), .Q(d_ff_3_q), .en(1'b1), .reset(\中断3 ));  // open: Qn, preset
  and and_1 (and_1_out, Beq, ALUequal);
  or or_4 (or_4_out, and_1_out, and_2_out, and_6_out);
  Register #(.width(32), .trigger("rising"), .Select("low")) u_PC (
    .D(\新PC ), .en(or_5_out), .Q(PC), .clk(CLK), .clr(RST));
  or or_5 (or_5_out, not_1_out, Go);
  Hex_Digit_Display hex_digit_display_4 (.value(LedData[15:12]));  // open: dp
  Hex_Digit_Display hex_digit_display_5 (.value(LedData[19:16]));  // open: dp
  Comparator #(.width(16), .mode("twosComplement")) comparator_1 (
    .a(16'h258), .b(\总周期数 ), .eq(comparator_1_eq));  // open: gt, lt
  Comparator #(.width(16), .mode("twosComplement")) comparator_2 (
    .a(\总周期数 ), .b(16'h1), .eq(comparator_2_eq));  // open: gt, lt
  Comparator #(.width(16), .mode("twosComplement")) comparator_3 (
    .a(\总周期数 ), .b(16'h4), .eq(comparator_3_eq));  // open: gt, lt
  Comparator #(.width(16), .mode("twosComplement")) comparator_4 (
    .a(\总周期数 ), .b(16'h7), .eq(comparator_4_eq));  // open: gt, lt
  or or_6 (or_6_out, comparator_4_eq, comparator_5_eq);
  Comparator #(.width(16), .mode("twosComplement")) comparator_5 (
    .a(\总周期数 ), .b(16'h241), .eq(comparator_5_eq));  // open: gt, lt
  or or_7 (or_7_out, d_ff_1_q, \中断1 );
  or or_8 (or_8_out, d_ff_2_q, \中断2 );
  or or_9 (or_9_out, d_ff_3_q, \中断3 );
  not not_2 (not_2_out, ALUequal);
  and and_2 (and_2_out, not_2_out, Bne);
  Hex_Digit_Display hex_digit_display_6 (.value(LedData[11:8]));  // open: dp
  Hex_Digit_Display hex_digit_display_7 (.value(LedData[7:4]));  // open: dp
  // Probe on \总周期数 
  or or_10 (or_10_out, comparator_1_eq, comparator_2_eq);
  Pull_Resistor #(.pull(0)) pull_resistor_1 (.node(IRA));
  assign IRA = or_10_out ? ~CLK : 1'bz;  // Controlled_Inverter controlled_inverter_1
  Pull_Resistor #(.pull(0)) pull_resistor_2 (.node(IRB));
  assign IRB = comparator_3_eq ? ~CLK : 1'bz;  // Controlled_Inverter controlled_inverter_2
  Pull_Resistor #(.pull(0)) pull_resistor_3 (.node(IRC));
  assign IRC = or_6_out ? ~CLK : 1'bz;  // Controlled_Inverter controlled_inverter_3
  D_Flip_Flop #(.trigger("rising"), .Pre_Clr_Positions("LEGACY"), .NegatePresetClear("false"), .enable("true"), .NewFFLayout("false")) d_ff_4 (
    .clk(CLK), .D(and_3_out), .Q(\中断1 ), .en(1'b1));  // open: Qn, preset, reset
  and and_3 (and_3_out, or_7_out, ~RESET1);  // AND_Gate
  D_Flip_Flop #(.trigger("rising"), .Pre_Clr_Positions("LEGACY"), .NegatePresetClear("false"), .enable("true"), .NewFFLayout("false")) d_ff_5 (
    .clk(CLK), .D(and_4_out), .Q(\中断2 ), .en(1'b1));  // open: Qn, preset, reset
  and and_4 (and_4_out, or_8_out, ~RESET2);  // AND_Gate
  D_Flip_Flop #(.trigger("rising"), .Pre_Clr_Positions("LEGACY"), .NegatePresetClear("false"), .enable("true"), .NewFFLayout("false")) d_ff_6 (
    .clk(CLK), .D(and_5_out), .Q(\中断3 ), .en(1'b1));  // open: Qn, preset, reset
  and and_5 (and_5_out, or_9_out, ~RESET3);  // AND_Gate
  and and_6 (and_6_out, ALUge, \单周期硬布线控制器_1_bge );
  Adder #(.width(32)) adder_1 (.a(PC), .b(32'h4), .out(PC_4));  // open: cin, cout
  Hex_Digit_Display hex_digit_display_8 (.value(LedData[3:0]));  // open: dp
  // RiscV_Probe riscv_probe_1: pin names not known; wires that end beside it: IR
  ROM #(.addrWidth(10), .dataWidth(32), .Select("high")) rom_1 (.addr(PC[11:2]), .data(IR));
  or or_11 (IR1_t, IR1, IRA);
  \单周期硬布线控制器  \u_单周期硬布线控制器_1  (
    .Funct({IR[30], IR[25], IR[14:12]}), .OP(IR[6:2]), .ALU_OP(\单周期硬布线控制器_1_alu_op ), .MemToReg(MemToReg),
    .MemWrite(MemWrite), .ALU_SRC(\单周期硬布线控制器_1_alu_src ), .RegWrite(RegWrite), .ecall(ecall), .S_type(Stype),
    .Jalr(jalr), .Beq(Beq), .JAL(jal), .Bne(Bne), .in_3(IR[21]), .uret(uret), .csr(csr), .U_type(Utype),
    .bge(\单周期硬布线控制器_1_bge ), .LBU(LBU));  // open: u2, u1
  Multiplexer #(.select(1), .width(5), .disabled("Z"), .enable("false")) multiplexer_2 (
    .in0(IR[19:15]), .in1(5'b10001), .out(multiplexer_2_out), .sel(ecall));
  Multiplexer #(.select(1), .width(5), .disabled("Z"), .enable("false")) multiplexer_3 (
    .in0(IR[24:20]), .in1(5'b01010), .out(multiplexer_3_out), .sel(ecall));
  Multiplexer #(.select(1), .width(12), .disabled("Z"), .enable("false")) multiplexer_4 (
    .in0(IR[31:20]), .in1({IR[31:25], IR[11:7]}), .out(multiplexer_4_out), .sel(Stype));
  or or_12 (IR2_t, IR2, IRB);
  assign bit_extender_1_out = {{20{multiplexer_4_out[11]}}, multiplexer_4_out};  // Bit_Extender bit_extender_1
  assign bit_extender_2_out = {{12{IR[31]}}, IR[31:12]};  // Bit_Extender bit_extender_2
  assign bit_extender_3_out = {{20{IR[31]}}, {IR[31], IR[7], IR[30:25], IR[11:8]}};  // Bit_Extender bit_extender_3
  assign bit_extender_4_out = {{12{IR[31]}}, {IR[31], IR[19:12], IR[20], IR[30:21]}};  // Bit_Extender bit_extender_4
  Multiplexer #(.select(2), .width(32), .disabled("Z"), .enable("false")) multiplexer_5 (
    .in0(\老PC ), .in1(EPC), .in2(\中断地址 ), .in3(EPC), .out(\新PC ), .sel({\中断 , uret}));
  Priority_Encoder #(.select(2), .disabled("Z")) priority_encoder_2 (
    .in1(\中断1 ), .in2(\中断2 ), .in3(\中断3 ), .out(\中断号 ), .gs(priority_encoder_2_gs));  // open: in0, en_out, en_in
  Shifter #(.width(32), .shift("ll")) shifter_1 (.in(bit_extender_2_out), .\dist (5'b01100), .out(shifter_1_out));
  Shifter #(.width(32), .shift("ll")) shifter_2 (.in(bit_extender_3_out), .\dist (5'b00001), .out(shifter_2_out));
  Shifter #(.width(32), .shift("ll")) shifter_3 (.in(bit_extender_4_out), .\dist (5'b00001), .out(shifter_3_out));
  or or_13 (IR3_t, IR3, IRC);
  Regifile regifile_1 (
    .Din(RDin), .Clk(CLK), .R1(regifile_1_r1), .R2(MDin), .WE(RegWrite), .W_num(IR[11:7]),
    .R1_num(multiplexer_2_out), .R2_num(multiplexer_3_out));
  Multiplexer #(.select(1), .width(32), .disabled("Z"), .enable("false")) multiplexer_6 (
    .in0(MDin), .in1(bit_extender_1_out), .out(multiplexer_6_out), .sel(\单周期硬布线控制器_1_alu_src ));
  Adder #(.width(32)) adder_2 (.a(shifter_2_out), .b(PC), .out(adder_2_out));  // open: cin, cout
  and and_7 (\中断 , priority_encoder_2_gs, \中断优先 , IE);
  Comparator #(.width(2), .mode("unsigned")) comparator_6 (.a(\前中断号 ), .b(\中断号 ), .lt(\中断优先 ));  // open: gt, eq
  Pull_Resistor #(.pull(1)) pull_resistor_4 (.node(\中断优先 ));
  Comparator #(.width(3), .mode("twosComplement")) comparator_7 (
    .a(3'b110), .b(IR[14:12]), .eq(comparator_7_eq));  // open: gt, lt
  Comparator #(.width(3), .mode("twosComplement")) comparator_8 (
    .a(IR[14:12]), .b(3'b111), .eq(comparator_8_eq));  // open: gt, lt
  Adder #(.width(32)) adder_3 (.a(shifter_3_out), .b(PC), .out(adder_3_out));  // open: cin, cout
  and and_8 (csrrsi, comparator_7_eq, csr);
  and and_9 (csrrci, csr, comparator_8_eq);
  ALU alu_1 (
    .X(regifile_1_r1), .Y(multiplexer_6_out), .AluOP(\单周期硬布线控制器_1_alu_op ), .Equal(ALUequal),
    .Result(ALUresult), .out_4(ALUge));  // open: Result_2, out_6
  or or_14 (or_14_out, \中断 , uret);
  Multiplexer #(.select(2), .width(32), .disabled("Z"), .enable("false")) multiplexer_7 (
    .in1(32'h30ac), .in2(32'h3158), .in3(32'h3204), .out(\中断地址 ), .sel(\中断号 ));  // open: in0
  Adder #(.width(32)) adder_4 (.a(shifter_1_out), .b(PC), .out(adder_4_out));  // open: cin, cout
  Counter #(.width(2), .max('h3), .ongoal("wrap"), .trigger("rising"), .behavior("new")) counter_1 (
    .count(or_14_out), .Q(\中断计数 ), .clk(CLK), .down(uret));  // open: load, D, carry, clr, preset
  or or_15 (or_15_out, \中断 , csrrci);
  not not_3 (not_3_out, halt);
  Comparator #(.width(32), .mode("twosComplement")) comparator_9 (
    .a(regifile_1_r1), .b(32'h22), .eq(comparator_9_eq));  // open: gt, lt
  not not_4 (not_4_out, comparator_9_eq);
  or or_16 (or_16_out, \中断 , csrrci, csrrsi, uret);
  Counter #(.width(16), .max('hffff), .ongoal("wrap"), .trigger("rising"), .behavior("new")) counter_2 (
    .load(1'b0), .D({16{1'b0}}), .count(not_3_out), .Q(\总周期数 ), .clk(CLK), .clr(1'b0), .down(1'b0));  // open: carry, preset
  and and_10 (halt, ecall, not_4_out);
  and and_11 (and_11_out, comparator_9_eq, ecall);
  D_Flip_Flop #(.trigger("rising"), .Pre_Clr_Positions("LEGACY"), .NegatePresetClear("false"), .enable("true"), .NewFFLayout("false")) d_ff_7 (
    .clk(CLK), .D(or_15_out), .Qn(IE), .en(or_16_out));  // open: Q, preset, reset
  RAM #(.addrWidth(10), .dataWidth(32), .bus("separate"), .Select("high")) ram_1 (
    .addr(ALUresult[11:2]), .din(MDin), .data(ram_1_data), .str(MemWrite), .sel(1'b1), .clk(CLK), .ld(1'b1));  // open: clr
  Register #(.width(32), .trigger("rising"), .Select("low")) register_1 (
    .D(MDin), .en(and_11_out), .Q(LedData), .clk(CLK));  // open: clr
  D_Flip_Flop #(.trigger("high"), .Pre_Clr_Positions("LEGACY"), .NegatePresetClear("false"), .enable("true"), .NewFFLayout("false")) d_ff_8 (.Q(d_ff_8_q));  // open: clk, D, Qn, preset, en, reset
  // Probe on 13'hc
  Demultiplexer #(.select(2), .width(1), .tristate("false"), .disabled("Z"), .enable("false")) demultiplexer_1 (
    .out0(demultiplexer_1_out0), .out1(demultiplexer_1_out1), .out2(demultiplexer_1_out2), .in(\中断 ),
    .sel(\中断计数 ));  // open: out3
  Multiplexer #(.select(1), .width(32), .disabled("Z"), .enable("false")) multiplexer_8 (
    .in0(ram_1_data), .in1(LBUData), .out(multiplexer_8_out), .sel(LBU));
  Comparator #(.width(13), .mode("twosComplement")) comparator_10 (
    .a(CNT_num), .b(13'hc), .eq(comparator_10_eq), .lt(comparator_10_lt));  // open: gt
  Clock #(.highDuration(1), .lowDuration(1)) clock_1 (.out(clock_1_out));
  Demultiplexer #(.select(2), .width(1), .tristate("false"), .disabled("Z"), .enable("false")) demultiplexer_2 (
    .out0(demultiplexer_2_out0), .out1(demultiplexer_2_out1), .out2(demultiplexer_2_out2), .in(\中断 ),
    .sel(\中断计数 ));  // open: out3
  or or_17 (or_17_out[0], Utype, MemToReg);
  Counter #(.width(13), .max('h1fff), .ongoal("stay"), .trigger("rising"), .behavior("old")) counter_3 (
    .count(comparator_10_lt), .Q(CNT_num), .clk(clock_1_out));  // open: load, D, carry, clr, preset
  Demultiplexer #(.select(2), .width(1), .tristate("false"), .disabled("Z"), .enable("false")) demultiplexer_3 (
    .out1(RESET1), .out2(RESET2), .out3(RESET3), .in(uret), .sel(\前中断号 ));  // open: out0
  or or_18 (or_17_out[1], Utype, jal, jalr);
  Multiplexer #(.select(2), .width(32), .disabled("Z"), .enable("false")) multiplexer_9 (
    .in0(ALUresult), .in1(multiplexer_8_out), .in2(PC_4), .in3(adder_4_out), .out(RDin), .sel(or_17_out));
  nand nand_1 (nand_1_out, d_ff_8_q, comparator_10_eq);
  Register #(.width(32), .trigger("rising"), .Select("low")) u_EPC (
    .D(\老PC ), .en(demultiplexer_1_out0), .Q(EPC_q), .clk(CLK));  // open: clr
  Register #(.width(32), .trigger("rising"), .Select("low")) EPC_2 (
    .D(\老PC ), .en(demultiplexer_1_out1), .Q(EPC_2_q), .clk(CLK));  // open: clr
  Register #(.width(32), .trigger("rising"), .Select("low")) EPC_3 (
    .D(\老PC ), .en(demultiplexer_1_out2), .Q(EPC_3_q), .clk(CLK));  // open: clr
  Pull_Resistor #(.pull(0)) pull_resistor_5 (.node(RESET1));
  assign LBUData = {{24{1'b0}}, multiplexer_10_out};  // Bit_Extender bit_extender_5
  Multiplexer #(.select(2), .width(8), .disabled("Z"), .enable("false")) multiplexer_10 (
    .in0(ram_1_data[7:0]), .in1(ram_1_data[15:8]), .in2(ram_1_data[23:16]), .in3(ram_1_data[31:24]),
    .out(multiplexer_10_out), .sel(ALUresult[1:0]));
  assign CLK = nand_1_out ? clock_1_out : 1'bz;  // Controlled_Buffer controlled_buffer_1
  Pull_Resistor #(.pull(1)) pull_resistor_6 (.node(CLK));
  Register #(.width(2), .trigger("rising"), .Select("low")) EPC_4 (
    .D(\中断号 ), .en(demultiplexer_2_out0), .Q(EPC_4_q), .clk(CLK));  // open: clr
  Register #(.width(2), .trigger("rising"), .Select("low")) EPC_5 (
    .D(\中断号 ), .en(demultiplexer_2_out1), .Q(EPC_5_q), .clk(CLK));  // open: clr
  Register #(.width(2), .trigger("rising"), .Select("low")) EPC_6 (
    .D(\中断号 ), .en(demultiplexer_2_out2), .Q(EPC_6_q), .clk(CLK));  // open: clr
  Multiplexer #(.select(2), .width(32), .disabled("Z"), .enable("false")) multiplexer_11 (
    .in1(EPC_q), .in2(EPC_2_q), .in3(EPC_3_q), .out(EPC), .sel(\中断计数 ));  // open: in0
  Multiplexer #(.select(2), .width(2), .disabled("Z"), .enable("false")) multiplexer_12 (
    .in1(EPC_4_q), .in2(EPC_5_q), .in3(EPC_6_q), .out(\前中断号 ), .sel(\中断计数 ));  // open: in0
  Pull_Resistor #(.pull(0)) pull_resistor_7 (.node(RESET2));
  Pull_Resistor #(.pull(0)) pull_resistor_8 (.node(RESET3));

  // Notes on the sheet:
  //   中断源
  //   中断等待指示
  //   总复位信号应将除ROM以外所有存储组件全部清零
  //   多级中断测试信号模拟器
  //   数码管输出
  //   数码管输出应该用寄存器锁存，否则显示数据只能一闪而过
  //   指令探针
  //   指令存储器
  //   指令字
  //   contents of rom_1 (hex, n*v repeats v):
  //   7d000113 100413 1f41993 41f9d993 433 c00913 800b13 140413 f47413 800293 100313 499993 89e9b3 1300533
  //   2200893 73 406282b3 fe0294e3 140413 f00f93 1f47433 1c41413 800293 100313 49d993 89e9b3 1300533
  //   2200893 73 406282b3 fe0294e3 1c45413 406b0b33 b0463 f95ff06f 2b3 fff2c293 1029293 fff2e293 500533
  //   2200893 73 f5dff06f 1112023 410113 a12023 410113 812023 410113 1312023 410113 1412023 410113 1512023
  //   410113 1612023 410113 40e073 100b13 300a13 100a93 1600433 441413 14469b3 1300533 2200893 73 fe0416e3
  //   415a0a33 fe0a10e3 40f073 ffc10113 12b03 ffc10113 12a83 ffc10113 12a03 ffc10113 12983 ffc10113 12403
  //   ffc10113 12503 ffc10113 12883 200073 1112023 410113 a12023 410113 812023 410113 1312023 410113
  //   1412023 410113 1512023 410113 1612023 410113 40e073 200b13 300a13 100a93 1600433 441413 14469b3
  //   1300533 2200893 73 fe0416e3 415a0a33 fe0a10e3 40f073 ffc10113 12b03 ffc10113 12a83 ffc10113 12a03
  //   ffc10113 12983 ffc10113 12403 ffc10113 12503 ffc10113 12883 200073 1112023 410113 a12023 410113
  //   812023 410113 1312023 410113 1412023 410113 1512023 410113 1612023 410113 40e073 300b13 300a13
  //   100a93 1600433 441413 14469b3 1300533 2200893 73 fe0416e3 415a0a33 fe0a10e3 40f073 ffc10113 12b03
  //   ffc10113 12a83 ffc10113 12a03 ffc10113 12983 ffc10113 12403 ffc10113 12503 ffc10113 12883 200073
  //   JAL
  //   JALR
  //   URET
  //   BGE
  //   CSR
  //   rs1
  //   rs2
  //   rd
  //   I指令
  //   S指令
  //   U指令
  //   B指令
  //   J指令
  //   Beq
  //   Bne
  //   AluOP
  //   AluSrcB
  //   RegWrite
  //   PC更新
  //   MemToReg
  //   MemWrite
  //   中断使能
  //   为方便自动评测，需要输出PC，IR，寄存器堆写如数据RDin
  //   RAM写使能MemWrite、RAM写入数据MDin等信号
  //   中断计数
  //   数据存储器
  //   控制位
  //   暂停节拍，不能为0
  //   戳工具置1进入计数暂停模式，ctrl+k时钟自动运行到对应节拍暂停
  //   ctrl+k关闭时钟连续运行，将控制位置零，进入单步调试模式调试
  //   保存中断号
  //   堆栈保存EPC
  //   可计数暂停的时钟源
endmodule

module \封装正确性测试  (
);

  wire IR1, IR2, IR3, MemW, RegW;
  wire [31:0] EX_PC, ID_PC, IF_PC, IR, LED, MDin, MDinr, MEM_PC, PC, RDin, RDinr, WB_PC;

  \单周期RISC_V  \u_单周期risc_v_1  (
    .IR1(IR1), .IR2(IR2), .IR3(IR3), .RegWrite(RegW), .MemWrite(MemW), .PC(PC), .IR(IR), .RDin(RDin),
    .MDin(MDin), .LedData(LED));
  \气泡流水线  \u_气泡流水线_1  (
    .RegWrite(RegW), .MemWrite(MemW), .IF_PC(IF_PC), .ID_PC(ID_PC), .EX_PC(EX_PC), .M_PC(MEM_PC),
    .WB_PC(WB_PC), .RDin(RDinr), .MDin(MDinr), .LedData(LED));
  \单周期_单级中断  \u_单周期_单级中断_1  (
    .IR1(IR1), .IR2(IR2), .IR3(IR3), .RegWrite(RegW), .MemWrite(MemW), .PC(PC), .IR(IR), .RDin(RDin),
    .MDin(MDin), .LedData(LED));
  \理想流水线  \u_理想流水线_1  (
    .RegWrite(RegW), .MemWrite(MemW), .IF_PC(IF_PC), .ID_PC(ID_PC), .EX_PC(EX_PC), .M_PC(MEM_PC),
    .WB_PC(WB_PC), .RDin(RDinr), .MDin(MDinr), .LedData(LED));
  \重定向流水线  \u_重定向流水线_1  (
    .RegWrite(RegW), .MemWrite(MemW), .IF_PC(IF_PC), .ID_PC(ID_PC), .EX_PC(EX_PC), .M_PC(MEM_PC),
    .WB_PC(WB_PC), .RDin(RDinr), .MDin(MDinr), .LedData(LED));
  \单周期_多级中断  \u_单周期_多级中断_1  (
    .IR1(IR1), .IR2(IR2), .IR3(IR3), .RegWrite(RegW), .MemWrite(MemW), .PC(PC), .IR(IR), .RDin(RDin),
    .MDin(MDin), .LedData(LED));

  // Notes on the sheet:
  //   单周期封装测试
  //   气泡流水封装测试
  //   单周期+单级中断封装测试
  //   请检查上面封装有无位宽不匹配，引脚标签是否和连接的标签相对应，否则无法在educoder平台上正确测试
  //   理想流水封装测试
  //   重定向流水封装测试
  //   单周期+多级中断封装测试
endmodule

module IF_ID (
  input  [31:0] PC,
  input  [31:0] PC_4,
  input  [31:0] IR,
  input  \预测跳转 ,
  input  en,
  input  CLK,
  input  reset,
  input  flush,
  output [31:0] PC_2,
  output [31:0] PC_4_2,
  output [31:0] IR_2,
  output \预测跳转_2 
);

  wire and_1_out, not_1_out, or_1_out;
  wire [31:0] multiplexer_1_out, multiplexer_2_out, multiplexer_3_out;

  Multiplexer #(.select(1), .width(32), .disabled("Z"), .enable("false")) multiplexer_1 (
    .in0(PC), .in1({32{1'b0}}), .out(multiplexer_1_out), .sel(or_1_out));
  Multiplexer #(.select(1), .width(32), .disabled("Z"), .enable("false")) multiplexer_2 (
    .in0(PC_4), .in1({32{1'b0}}), .out(multiplexer_2_out), .sel(or_1_out));
  Multiplexer #(.select(1), .width(32), .disabled("Z"), .enable("false")) multiplexer_3 (
    .in0(IR), .in1({32{1'b0}}), .out(multiplexer_3_out), .sel(or_1_out));
  or or_1 (or_1_out, reset, flush);
  not not_1 (not_1_out, or_1_out);
  and and_1 (and_1_out, \预测跳转 , not_1_out);
  Register #(.width(32), .trigger("rising"), .Select("low")) register_1 (
    .D(multiplexer_1_out), .en(en), .Q(PC_2), .clk(CLK));  // open: clr
  Register #(.width(32), .trigger("rising"), .Select("low")) register_2 (
    .D(multiplexer_2_out), .en(en), .Q(PC_4_2), .clk(CLK));  // open: clr
  Register #(.width(32), .trigger("rising"), .Select("low")) register_3 (
    .D(multiplexer_3_out), .en(en), .Q(IR_2), .clk(CLK));  // open: clr
  Register #(.width(1), .trigger("rising"), .Select("low")) register_4 (
    .D(and_1_out), .en(en), .Q(\预测跳转_2 ), .clk(CLK));  // open: clr
endmodule

module ID_EX (
  input  Beq,
  input  Bne,
  input  MemToReg,
  input  MemWrite,
  input  AluSrcB,
  input  RegWrite,
  input  JAL,
  input  JALR,
  input  URET,
  input  S_type,
  input  U_type,
  input  bge,
  input  csr,
  input  LBU,
  input  ecall,
  input  [3:0] AluOP,
  input  [4:0] rd,
  input  [31:0] R1,
  input  [31:0] R2,
  input  [31:0] imm_1,
  input  [31:0] imm_2,
  input  [31:0] imm_3,
  input  [31:0] PC,
  input  [31:0] PC_4,
  input  [31:0] IR,
  input  [1:0] rs1f,
  input  [1:0] rs2f,
  input  \预测跳转 ,
  input  reset,
  input  flush,
  input  en,
  input  CLK,
  output Beq_2,
  output Bne_2,
  output MemToReg_2,
  output MemWrite_2,
  output AluSrcB_2,
  output RegWrite_2,
  output JAL_2,
  output JALR_2,
  output URET_2,
  output S_type_2,
  output U_type_2,
  output bge_2,
  output csr_2,
  output LBU_2,
  output ecall_2,
  output [3:0] AluOP_2,
  output [4:0] rd_2,
  output [31:0] R1_2,
  output [31:0] R2_2,
  output [31:0] imm_1_2,
  output [31:0] imm_2_2,
  output [31:0] imm_3_2,
  output [31:0] PC_2,
  output [31:0] PC_4_2,
  output [31:0] IR_2,
  output [1:0] rs1f_2,
  output [1:0] rs2f_2,
  output \预测跳转_2 
);

  wire and_1_out, multiplexer_1_out, multiplexer_2_out, multiplexer_3_out, multiplexer_4_out,
       multiplexer_5_out, multiplexer_6_out, multiplexer_7_out, multiplexer_8_out, multiplexer_9_out,
       multiplexer_10_out, multiplexer_11_out, multiplexer_12_out, multiplexer_13_out, multiplexer_14_out,
       multiplexer_15_out, not_1_out, or_1_out;
  wire [1:0] multiplexer_26_out, multiplexer_27_out;
  wire [3:0] multiplexer_16_out;
  wire [4:0] multiplexer_17_out;
  wire [31:0] multiplexer_18_out, multiplexer_19_out, multiplexer_20_out, multiplexer_21_out,
       multiplexer_22_out, multiplexer_23_out, multiplexer_24_out, multiplexer_25_out;

  Multiplexer #(.select(1), .width(1), .disabled("Z"), .enable("false")) multiplexer_1 (
    .in0(Beq), .in1(1'b0), .out(multiplexer_1_out), .sel(or_1_out));
  Multiplexer #(.select(1), .width(1), .disabled("Z"), .enable("false")) multiplexer_2 (
    .in0(Bne), .in1(1'b0), .out(multiplexer_2_out), .sel(or_1_out));
  Multiplexer #(.select(1), .width(1), .disabled("Z"), .enable("false")) multiplexer_3 (
    .in0(MemToReg), .in1(1'b0), .out(multiplexer_3_out), .sel(or_1_out));
  Multiplexer #(.select(1), .width(1), .disabled("Z"), .enable("false")) multiplexer_4 (
    .in0(MemWrite), .in1(1'b0), .out(multiplexer_4_out), .sel(or_1_out));
  Multiplexer #(.select(1), .width(1), .disabled("Z"), .enable("false")) multiplexer_5 (
    .in0(AluSrcB), .in1(1'b0), .out(multiplexer_5_out), .sel(or_1_out));
  Multiplexer #(.select(1), .width(1), .disabled("Z"), .enable("false")) multiplexer_6 (
    .in0(RegWrite), .in1(1'b0), .out(multiplexer_6_out), .sel(or_1_out));
  Multiplexer #(.select(1), .width(1), .disabled("Z"), .enable("false")) multiplexer_7 (
    .in0(JAL), .in1(1'b0), .out(multiplexer_7_out), .sel(or_1_out));
  Multiplexer #(.select(1), .width(1), .disabled("Z"), .enable("false")) multiplexer_8 (
    .in0(JALR), .in1(1'b0), .out(multiplexer_8_out), .sel(or_1_out));
  Multiplexer #(.select(1), .width(1), .disabled("Z"), .enable("false")) multiplexer_9 (
    .in0(URET), .in1(1'b0), .out(multiplexer_9_out), .sel(or_1_out));
  Multiplexer #(.select(1), .width(1), .disabled("Z"), .enable("false")) multiplexer_10 (
    .in0(S_type), .in1(1'b0), .out(multiplexer_10_out), .sel(or_1_out));
  Multiplexer #(.select(1), .width(1), .disabled("Z"), .enable("false")) multiplexer_11 (
    .in0(U_type), .in1(1'b0), .out(multiplexer_11_out), .sel(or_1_out));
  Multiplexer #(.select(1), .width(1), .disabled("Z"), .enable("false")) multiplexer_12 (
    .in0(bge), .in1(1'b0), .out(multiplexer_12_out), .sel(or_1_out));
  Multiplexer #(.select(1), .width(1), .disabled("Z"), .enable("false")) multiplexer_13 (
    .in0(csr), .in1(1'b0), .out(multiplexer_13_out), .sel(or_1_out));
  Multiplexer #(.select(1), .width(1), .disabled("Z"), .enable("false")) multiplexer_14 (
    .in0(LBU), .in1(1'b0), .out(multiplexer_14_out), .sel(or_1_out));
  Multiplexer #(.select(1), .width(1), .disabled("Z"), .enable("false")) multiplexer_15 (
    .in0(ecall), .in1(1'b0), .out(multiplexer_15_out), .sel(or_1_out));
  Multiplexer #(.select(1), .width(4), .disabled("Z"), .enable("false")) multiplexer_16 (
    .in0(AluOP), .in1(4'b0000), .out(multiplexer_16_out), .sel(or_1_out));
  Multiplexer #(.select(1), .width(5), .disabled("Z"), .enable("false")) multiplexer_17 (
    .in0(rd), .in1({5{1'b0}}), .out(multiplexer_17_out), .sel(or_1_out));
  Multiplexer #(.select(1), .width(32), .disabled("Z"), .enable("false")) multiplexer_18 (
    .in0(R1), .in1({32{1'b0}}), .out(multiplexer_18_out), .sel(or_1_out));
  Multiplexer #(.select(1), .width(32), .disabled("Z"), .enable("false")) multiplexer_19 (
    .in0(R2), .in1({32{1'b0}}), .out(multiplexer_19_out), .sel(or_1_out));
  Multiplexer #(.select(1), .width(32), .disabled("Z"), .enable("false")) multiplexer_20 (
    .in0(imm_1), .in1({32{1'b0}}), .out(multiplexer_20_out), .sel(or_1_out));
  Multiplexer #(.select(1), .width(32), .disabled("Z"), .enable("false")) multiplexer_21 (
    .in0(imm_2), .in1({32{1'b0}}), .out(multiplexer_21_out), .sel(or_1_out));
  Multiplexer #(.select(1), .width(32), .disabled("Z"), .enable("false")) multiplexer_22 (
    .in0(imm_3), .in1({32{1'b0}}), .out(multiplexer_22_out), .sel(or_1_out));
  Multiplexer #(.select(1), .width(32), .disabled("Z"), .enable("false")) multiplexer_23 (
    .in0(PC), .in1({32{1'b0}}), .out(multiplexer_23_out), .sel(or_1_out));
  Multiplexer #(.select(1), .width(32), .disabled("Z"), .enable("false")) multiplexer_24 (
    .in0(PC_4), .in1({32{1'b0}}), .out(multiplexer_24_out), .sel(or_1_out));
  Multiplexer #(.select(1), .width(32), .disabled("Z"), .enable("false")) multiplexer_25 (
    .in0(IR), .in1({32{1'b0}}), .out(multiplexer_25_out), .sel(or_1_out));
  Multiplexer #(.select(1), .width(2), .disabled("Z"), .enable("false")) multiplexer_26 (
    .in0(rs1f), .in1(2'b00), .out(multiplexer_26_out), .sel(or_1_out));
  Multiplexer #(.select(1), .width(2), .disabled("Z"), .enable("false")) multiplexer_27 (
    .in0(rs2f), .in1(2'b00), .out(multiplexer_27_out), .sel(or_1_out));
  or or_1 (or_1_out, reset, flush);
  not not_1 (not_1_out, or_1_out);
  and and_1 (and_1_out, \预测跳转 , not_1_out);
  Register #(.width(1), .trigger("rising"), .Select("low")) register_1 (
    .D(multiplexer_1_out), .en(en), .Q(Beq_2), .clk(CLK));  // open: clr
  Register #(.width(1), .trigger("rising"), .Select("low")) register_2 (
    .D(multiplexer_2_out), .en(en), .Q(Bne_2), .clk(CLK));  // open: clr
  Register #(.width(1), .trigger("rising"), .Select("low")) register_3 (
    .D(multiplexer_3_out), .en(en), .Q(MemToReg_2), .clk(CLK));  // open: clr
  Register #(.width(1), .trigger("rising"), .Select("low")) register_4 (
    .D(multiplexer_4_out), .en(en), .Q(MemWrite_2), .clk(CLK));  // open: clr
  Register #(.width(1), .trigger("rising"), .Select("low")) register_5 (
    .D(multiplexer_5_out), .en(en), .Q(AluSrcB_2), .clk(CLK));  // open: clr
  Register #(.width(1), .trigger("rising"), .Select("low")) register_6 (
    .D(multiplexer_6_out), .en(en), .Q(RegWrite_2), .clk(CLK));  // open: clr
  Register #(.width(1), .trigger("rising"), .Select("low")) register_7 (
    .D(multiplexer_7_out), .en(en), .Q(JAL_2), .clk(CLK));  // open: clr
  Register #(.width(1), .trigger("rising"), .Select("low")) register_8 (
    .D(multiplexer_8_out), .en(en), .Q(JALR_2), .clk(CLK));  // open: clr
  Register #(.width(1), .trigger("rising"), .Select("low")) register_9 (
    .D(multiplexer_9_out), .en(en), .Q(URET_2), .clk(CLK));  // open: clr
  Register #(.width(1), .trigger("rising"), .Select("low")) register_10 (
    .D(multiplexer_10_out), .en(en), .Q(S_type_2), .clk(CLK));  // open: clr
  Register #(.width(1), .trigger("rising"), .Select("low")) register_11 (
    .D(multiplexer_11_out), .en(en), .Q(U_type_2), .clk(CLK));  // open: clr
  Register #(.width(1), .trigger("rising"), .Select("low")) register_12 (
    .D(multiplexer_12_out), .en(en), .Q(bge_2), .clk(CLK));  // open: clr
  Register #(.width(1), .trigger("rising"), .Select("low")) register_13 (
    .D(multiplexer_13_out), .en(en), .Q(csr_2), .clk(CLK));  // open: clr
  Register #(.width(1), .trigger("rising"), .Select("low")) register_14 (
    .D(multiplexer_14_out), .en(en), .Q(LBU_2), .clk(CLK));  // open: clr
  Register #(.width(1), .trigger("rising"), .Select("low")) register_15 (
    .D(multiplexer_15_out), .en(en), .Q(ecall_2), .clk(CLK));  // open: clr
  Register #(.width(4), .trigger("rising"), .Select("low")) register_16 (
    .D(multiplexer_16_out), .en(en), .Q(AluOP_2), .clk(CLK));  // open: clr
  Register #(.width(5), .trigger("rising"), .Select("low")) register_17 (
    .D(multiplexer_17_out), .en(en), .Q(rd_2), .clk(CLK));  // open: clr
  Register #(.width(32), .trigger("rising"), .Select("low")) register_18 (
    .D(multiplexer_18_out), .en(en), .Q(R1_2), .clk(CLK));  // open: clr
  Register #(.width(32), .trigger("rising"), .Select("low")) register_19 (
    .D(multiplexer_19_out), .en(en), .Q(R2_2), .clk(CLK));  // open: clr
  Register #(.width(32), .trigger("rising"), .Select("low")) register_20 (
    .D(multiplexer_20_out), .en(en), .Q(imm_1_2), .clk(CLK));  // open: clr
  Register #(.width(32), .trigger("rising"), .Select("low")) register_21 (
    .D(multiplexer_21_out), .en(en), .Q(imm_2_2), .clk(CLK));  // open: clr
  Register #(.width(32), .trigger("rising"), .Select("low")) register_22 (
    .D(multiplexer_22_out), .en(en), .Q(imm_3_2), .clk(CLK));  // open: clr
  Register #(.width(32), .trigger("rising"), .Select("low")) register_23 (
    .D(multiplexer_23_out), .en(en), .Q(PC_2), .clk(CLK));  // open: clr
  Register #(.width(32), .trigger("rising"), .Select("low")) register_24 (
    .D(multiplexer_24_out), .en(en), .Q(PC_4_2), .clk(CLK));  // open: clr
  Register #(.width(32), .trigger("rising"), .Select("low")) register_25 (
    .D(multiplexer_25_out), .en(en), .Q(IR_2), .clk(CLK));  // open: clr
  Register #(.width(2), .trigger("rising"), .Select("low")) register_26 (
    .D(multiplexer_26_out), .en(en), .Q(rs1f_2), .clk(CLK));  // open: clr
  Register #(.width(2), .trigger("rising"), .Select("low")) register_27 (
    .D(multiplexer_27_out), .en(en), .Q(rs2f_2), .clk(CLK));  // open: clr
  Register #(.width(1), .trigger("rising"), .Select("low")) register_28 (
    .D(and_1_out), .en(en), .Q(\预测跳转_2 ), .clk(CLK));  // open: clr
endmodule

module EX_MEM (
  input  U_type,
  input  MemToReg,
  input  MemWrite,
  input  RegWrite,
  input  JAL,
  input  JALR,
  input  URET,
  input  LBU,
  input  halt,
  input  [4:0] rd,
  input  [31:0] result,
  input  [31:0] R2,
  input  [31:0] Uimm,
  input  [31:0] PC,
  input  [31:0] PC_4,
  input  [31:0] IR,
  input  reset,
  input  flush,
  input  en,
  input  CLK,
  output U_type_2,
  output MemToReg_2,
  output MemWrite_2,
  output RegWrite_2,
  output JAL_2,
  output JALR_2,
  output URET_2,
  output LBU_2,
  output halt_2,
  output [4:0] rd_2,
  output [31:0] result_2,
  output [31:0] R2_2,
  output [31:0] Uimm_2,
  output [31:0] PC_2,
  output [31:0] PC_4_2,
  output [31:0] IR_2
);

  wire multiplexer_1_out, multiplexer_2_out, multiplexer_3_out, multiplexer_4_out, multiplexer_5_out,
       multiplexer_6_out, multiplexer_7_out, multiplexer_8_out, multiplexer_9_out, or_1_out;
  wire [4:0] multiplexer_10_out;
  wire [31:0] multiplexer_11_out, multiplexer_12_out, multiplexer_13_out, multiplexer_14_out,
       multiplexer_15_out, multiplexer_16_out;

  Multiplexer #(.select(1), .width(1), .disabled("Z"), .enable("false")) multiplexer_1 (
    .in0(U_type), .in1(1'b0), .out(multiplexer_1_out), .sel(or_1_out));
  Multiplexer #(.select(1), .width(1), .disabled("Z"), .enable("false")) multiplexer_2 (
    .in0(MemToReg), .in1(1'b0), .out(multiplexer_2_out), .sel(or_1_out));
  Multiplexer #(.select(1), .width(1), .disabled("Z"), .enable("false")) multiplexer_3 (
    .in0(MemWrite), .in1(1'b0), .out(multiplexer_3_out), .sel(or_1_out));
  Multiplexer #(.select(1), .width(1), .disabled("Z"), .enable("false")) multiplexer_4 (
    .in0(RegWrite), .in1(1'b0), .out(multiplexer_4_out), .sel(or_1_out));
  Multiplexer #(.select(1), .width(1), .disabled("Z"), .enable("false")) multiplexer_5 (
    .in0(JAL), .in1(1'b0), .out(multiplexer_5_out), .sel(or_1_out));
  Multiplexer #(.select(1), .width(1), .disabled("Z"), .enable("false")) multiplexer_6 (
    .in0(JALR), .in1(1'b0), .out(multiplexer_6_out), .sel(or_1_out));
  Multiplexer #(.select(1), .width(1), .disabled("Z"), .enable("false")) multiplexer_7 (
    .in0(URET), .in1(1'b0), .out(multiplexer_7_out));  // open: sel
  Multiplexer #(.select(1), .width(1), .disabled("Z"), .enable("false")) multiplexer_8 (
    .in0(LBU), .in1(1'b0), .out(multiplexer_8_out), .sel(or_1_out));
  Multiplexer #(.select(1), .width(1), .disabled("Z"), .enable("false")) multiplexer_9 (
    .in0(halt), .in1(1'b0), .out(multiplexer_9_out), .sel(or_1_out));
  Multiplexer #(.select(1), .width(5), .disabled("Z"), .enable("false")) multiplexer_10 (
    .in0(rd), .in1({5{1'b0}}), .out(multiplexer_10_out), .sel(or_1_out));
  Multiplexer #(.select(1), .width(32), .disabled("Z"), .enable("false")) multiplexer_11 (
    .in0(result), .in1({32{1'b0}}), .out(multiplexer_11_out), .sel(or_1_out));
  Multiplexer #(.select(1), .width(32), .disabled("Z"), .enable("false")) multiplexer_12 (
    .in0(R2), .in1({32{1'b0}}), .out(multiplexer_12_out), .sel(or_1_out));
  Multiplexer #(.select(1), .width(32), .disabled("Z"), .enable("false")) multiplexer_13 (
    .in0(Uimm), .in1({32{1'b0}}), .out(multiplexer_13_out), .sel(or_1_out));
  Multiplexer #(.select(1), .width(32), .disabled("Z"), .enable("false")) multiplexer_14 (
    .in0(PC), .in1({32{1'b0}}), .out(multiplexer_14_out), .sel(or_1_out));
  Multiplexer #(.select(1), .width(32), .disabled("Z"), .enable("false")) multiplexer_15 (
    .in0(PC_4), .in1({32{1'b0}}), .out(multiplexer_15_out), .sel(or_1_out));
  Multiplexer #(.select(1), .width(32), .disabled("Z"), .enable("false")) multiplexer_16 (
    .in0(IR), .in1({32{1'b0}}), .out(multiplexer_16_out), .sel(or_1_out));
  or or_1 (or_1_out, reset, flush);
  Register #(.width(1), .trigger("rising"), .Select("low")) register_1 (
    .D(multiplexer_1_out), .en(en), .Q(U_type_2), .clk(CLK));  // open: clr
  Register #(.width(1), .trigger("rising"), .Select("low")) register_2 (
    .D(multiplexer_2_out), .en(en), .Q(MemToReg_2), .clk(CLK));  // open: clr
  Register #(.width(1), .trigger("rising"), .Select("low")) register_3 (
    .D(multiplexer_3_out), .en(en), .Q(MemWrite_2), .clk(CLK));  // open: clr
  Register #(.width(1), .trigger("rising"), .Select("low")) register_4 (
    .D(multiplexer_4_out), .en(en), .Q(RegWrite_2), .clk(CLK));  // open: clr
  Register #(.width(1), .trigger("rising"), .Select("low")) register_5 (
    .D(multiplexer_5_out), .en(en), .Q(JAL_2), .clk(CLK));  // open: clr
  Register #(.width(1), .trigger("rising"), .Select("low")) register_6 (
    .D(multiplexer_6_out), .en(en), .Q(JALR_2), .clk(CLK));  // open: clr
  Register #(.width(1), .trigger("rising"), .Select("low")) register_7 (
    .D(multiplexer_7_out), .en(en), .Q(URET_2));  // open: clk, clr
  Register #(.width(1), .trigger("rising"), .Select("low")) register_8 (
    .D(multiplexer_8_out), .en(en), .Q(LBU_2), .clk(CLK));  // open: clr
  Register #(.width(1), .trigger("rising"), .Select("low")) register_9 (
    .D(multiplexer_9_out), .en(en), .Q(halt_2), .clk(CLK));  // open: clr
  Register #(.width(5), .trigger("rising"), .Select("low")) register_10 (
    .D(multiplexer_10_out), .en(en), .Q(rd_2), .clk(CLK));  // open: clr
  Register #(.width(32), .trigger("rising"), .Select("low")) register_11 (
    .D(multiplexer_11_out), .en(en), .Q(result_2), .clk(CLK));  // open: clr
  Register #(.width(32), .trigger("rising"), .Select("low")) register_12 (
    .D(multiplexer_12_out), .en(en), .Q(R2_2), .clk(CLK));  // open: clr
  Register #(.width(32), .trigger("rising"), .Select("low")) register_13 (
    .D(multiplexer_13_out), .en(en), .Q(Uimm_2), .clk(CLK));  // open: clr
  Register #(.width(32), .trigger("rising"), .Select("low")) register_14 (
    .D(multiplexer_14_out), .en(en), .Q(PC_2), .clk(CLK));  // open: clr
  Register #(.width(32), .trigger("rising"), .Select("low")) register_15 (
    .D(multiplexer_15_out), .en(en), .Q(PC_4_2), .clk(CLK));  // open: clr
  Register #(.width(32), .trigger("rising"), .Select("low")) register_16 (
    .D(multiplexer_16_out), .en(en), .Q(IR_2), .clk(CLK));  // open: clr
endmodule

module MEM_WB (
  input  U_type,
  input  LBU,
  input  MemToReg,
  input  RegWrite,
  input  JAL,
  input  JALR,
  input  URET,
  input  halt,
  input  [4:0] rd,
  input  [31:0] ALUresult,
  input  [31:0] MemData,
  input  [31:0] Uimm,
  input  [31:0] PC,
  input  [31:0] PC_4,
  input  [31:0] IR,
  input  reset,
  input  flush,
  input  en,
  input  CLK,
  output U_type_2,
  output LBU_2,
  output MemToReg_2,
  output RegWrite_2,
  output JAL_2,
  output JALR_2,
  output URET_2,
  output halt_2,
  output [4:0] rd_2,
  output [31:0] ALUresult_2,
  output [31:0] MemData_2,
  output [31:0] Uimm_2,
  output [31:0] PC_2,
  output [31:0] PC_4_2,
  output [31:0] IR_2
);

  wire multiplexer_1_out, multiplexer_2_out, multiplexer_3_out, multiplexer_4_out, multiplexer_5_out,
       multiplexer_6_out, multiplexer_7_out, multiplexer_8_out, or_1_out;
  wire [4:0] multiplexer_9_out;
  wire [31:0] multiplexer_10_out, multiplexer_11_out, multiplexer_12_out, multiplexer_13_out,
       multiplexer_14_out, multiplexer_15_out;

  Multiplexer #(.select(1), .width(1), .disabled("Z"), .enable("false")) multiplexer_1 (
    .in0(U_type), .in1(1'b0), .out(multiplexer_1_out), .sel(or_1_out));
  Multiplexer #(.select(1), .width(1), .disabled("Z"), .enable("false")) multiplexer_2 (
    .in0(LBU), .in1(1'b0), .out(multiplexer_2_out), .sel(or_1_out));
  Multiplexer #(.select(1), .width(1), .disabled("Z"), .enable("false")) multiplexer_3 (
    .in0(MemToReg), .in1(1'b0), .out(multiplexer_3_out), .sel(or_1_out));
  Multiplexer #(.select(1), .width(1), .disabled("Z"), .enable("false")) multiplexer_4 (
    .in0(RegWrite), .in1(1'b0), .out(multiplexer_4_out), .sel(or_1_out));
  Multiplexer #(.select(1), .width(1), .disabled("Z"), .enable("false")) multiplexer_5 (
    .in0(JAL), .in1(1'b0), .out(multiplexer_5_out), .sel(or_1_out));
  Multiplexer #(.select(1), .width(1), .disabled("Z"), .enable("false")) multiplexer_6 (
    .in0(JALR), .in1(1'b0), .out(multiplexer_6_out), .sel(or_1_out));
  Multiplexer #(.select(1), .width(1), .disabled("Z"), .enable("false")) multiplexer_7 (
    .in0(URET), .in1(1'b0), .out(multiplexer_7_out), .sel(or_1_out));
  Multiplexer #(.select(1), .width(1), .disabled("Z"), .enable("false")) multiplexer_8 (
    .in0(halt), .in1(1'b0), .out(multiplexer_8_out), .sel(or_1_out));
  Multiplexer #(.select(1), .width(5), .disabled("Z"), .enable("false")) multiplexer_9 (
    .in0(rd), .in1({5{1'b0}}), .out(multiplexer_9_out), .sel(or_1_out));
  Multiplexer #(.select(1), .width(32), .disabled("Z"), .enable("false")) multiplexer_10 (
    .in0(ALUresult), .in1({32{1'b0}}), .out(multiplexer_10_out), .sel(or_1_out));
  Multiplexer #(.select(1), .width(32), .disabled("Z"), .enable("false")) multiplexer_11 (
    .in0(MemData), .in1({32{1'b0}}), .out(multiplexer_11_out), .sel(or_1_out));
  Multiplexer #(.select(1), .width(32), .disabled("Z"), .enable("false")) multiplexer_12 (
    .in0(Uimm), .in1({32{1'b0}}), .out(multiplexer_12_out), .sel(or_1_out));
  Multiplexer #(.select(1), .width(32), .disabled("Z"), .enable("false")) multiplexer_13 (
    .in0(PC), .in1({32{1'b0}}), .out(multiplexer_13_out), .sel(or_1_out));
  Multiplexer #(.select(1), .width(32), .disabled("Z"), .enable("false")) multiplexer_14 (
    .in0(PC_4), .in1({32{1'b0}}), .out(multiplexer_14_out), .sel(or_1_out));
  Multiplexer #(.select(1), .width(32), .disabled("Z"), .enable("false")) multiplexer_15 (
    .in0(IR), .in1({32{1'b0}}), .out(multiplexer_15_out), .sel(or_1_out));
  or or_1 (or_1_out, reset, flush);
  Register #(.width(1), .trigger("rising"), .Select("low")) register_1 (
    .D(multiplexer_1_out), .en(en), .Q(U_type_2), .clk(CLK));  // open: clr
  Register #(.width(1), .trigger("rising"), .Select("low")) register_2 (
    .D(multiplexer_2_out), .en(en), .Q(LBU_2), .clk(CLK));  // open: clr
  Register #(.width(1), .trigger("rising"), .Select("low")) register_3 (
    .D(multiplexer_3_out), .en(en), .Q(MemToReg_2), .clk(CLK));  // open: clr
  Register #(.width(1), .trigger("rising"), .Select("low")) register_4 (
    .D(multiplexer_4_out), .en(en), .Q(RegWrite_2), .clk(CLK));  // open: clr
  Register #(.width(1), .trigger("rising"), .Select("low")) register_5 (
    .D(multiplexer_5_out), .en(en), .Q(JAL_2), .clk(CLK));  // open: clr
  Register #(.width(1), .trigger("rising"), .Select("low")) register_6 (
    .D(multiplexer_6_out), .en(en), .Q(JALR_2), .clk(CLK));  // open: clr
  Register #(.width(1), .trigger("rising"), .Select("low")) register_7 (
    .D(multiplexer_7_out), .en(en), .Q(URET_2));  // open: clk, clr
  Register #(.width(1), .trigger("rising"), .Select("low")) register_8 (
    .D(multiplexer_8_out), .en(en), .Q(halt_2), .clk(CLK));  // open: clr
  Register #(.width(5), .trigger("rising"), .Select("low")) register_9 (
    .D(multiplexer_9_out), .en(en), .Q(rd_2), .clk(CLK));  // open: clr
  Register #(.width(32), .trigger("rising"), .Select("low")) register_10 (
    .D(multiplexer_10_out), .en(en), .Q(ALUresult_2), .clk(CLK));  // open: clr
  Register #(.width(32), .trigger("rising"), .Select("low")) register_11 (
    .D(multiplexer_11_out), .en(en), .Q(MemData_2), .clk(CLK));  // open: clr
  Register #(.width(32), .trigger("rising"), .Select("low")) register_12 (
    .D(multiplexer_12_out), .en(en), .Q(Uimm_2), .clk(CLK));  // open: clr
  Register #(.width(32), .trigger("rising"), .Select("low")) register_13 (
    .D(multiplexer_13_out), .en(en), .Q(PC_2), .clk(CLK));  // open: clr
  Register #(.width(32), .trigger("rising"), .Select("low")) register_14 (
    .D(multiplexer_14_out), .en(en), .Q(PC_4_2), .clk(CLK));  // open: clr
  Register #(.width(32), .trigger("rising"), .Select("low")) register_15 (
    .D(multiplexer_15_out), .en(en), .Q(IR_2), .clk(CLK));  // open: clr
endmodule

module \气泡流水线处理  (
  input  [31:0] IR,
  input  u1,
  input  EX_RegWrite,
  input  u2,
  input  MEM_RegWrite,
  input  [4:0] EX_rd,
  input  branch,
  input  [4:0] MEM_rd,
  input  ecall,
  output \冲突 ,
  output flush
);

  wire and_1_out, and_2_out, and_3_out, and_4_out, and_5_out, comparator_1_eq, comparator_2_eq,
       comparator_3_eq, comparator_4_eq, comparator_5_eq, comparator_6_eq, comparator_7_eq, comparator_8_eq,
       comparator_9_eq, comparator_10_eq, comparator_11_eq, comparator_12_eq, not_1_out, not_2_out,
       not_3_out, not_4_out, or_1_out;

  Comparator #(.width(5), .mode("twosComplement")) comparator_1 (
    .a(5'b10001), .b(EX_rd), .eq(comparator_1_eq));  // open: gt, lt
  Comparator #(.width(5), .mode("twosComplement")) comparator_2 (
    .a(EX_rd), .b(5'b01010), .eq(comparator_2_eq));  // open: gt, lt
  Comparator #(.width(5), .mode("twosComplement")) comparator_3 (
    .a(5'b10001), .b(MEM_rd), .eq(comparator_3_eq));  // open: gt, lt
  Comparator #(.width(5), .mode("twosComplement")) comparator_4 (
    .a(MEM_rd), .b(5'b01010), .eq(comparator_4_eq));  // open: gt, lt
  Comparator #(.width(5), .mode("twosComplement")) comparator_5 (
    .a(EX_rd), .b(IR[24:20]), .eq(comparator_5_eq));  // open: gt, lt
  Comparator #(.width(5), .mode("twosComplement")) comparator_6 (
    .a(IR[24:20]), .b({5{1'b0}}), .eq(comparator_6_eq));  // open: gt, lt
  not not_1 (not_1_out, comparator_6_eq);
  Comparator #(.width(5), .mode("twosComplement")) comparator_7 (
    .a(EX_rd), .b(IR[19:15]), .eq(comparator_7_eq));  // open: gt, lt
  Comparator #(.width(5), .mode("twosComplement")) comparator_8 (
    .a(IR[19:15]), .b({5{1'b0}}), .eq(comparator_8_eq));  // open: gt, lt
  Comparator #(.width(5), .mode("twosComplement")) comparator_9 (
    .a(MEM_rd), .b(IR[24:20]), .eq(comparator_9_eq));  // open: gt, lt
  Comparator #(.width(5), .mode("twosComplement")) comparator_10 (
    .a(IR[24:20]), .b({5{1'b0}}), .eq(comparator_10_eq));  // open: gt, lt
  Comparator #(.width(5), .mode("twosComplement")) comparator_11 (
    .a(MEM_rd), .b(IR[19:15]), .eq(comparator_11_eq));  // open: gt, lt
  Comparator #(.width(5), .mode("twosComplement")) comparator_12 (
    .a(IR[19:15]), .b({5{1'b0}}), .eq(comparator_12_eq));  // open: gt, lt
  not not_2 (not_2_out, comparator_8_eq);
  not not_3 (not_3_out, comparator_10_eq);
  not not_4 (not_4_out, comparator_12_eq);
  or or_1 (or_1_out, comparator_1_eq, comparator_2_eq, comparator_3_eq, comparator_4_eq);
  and and_1 (and_1_out, EX_RegWrite, u2, comparator_5_eq, not_1_out);
  and and_2 (and_2_out, EX_RegWrite, u1, comparator_7_eq, not_2_out);
  and and_3 (and_3_out, MEM_RegWrite, u2, comparator_9_eq, not_3_out);
  and and_4 (and_4_out, MEM_RegWrite, u1, comparator_11_eq, not_4_out);
  and and_5 (and_5_out, or_1_out, ecall);
  or or_2 (\冲突 , and_5_out, and_1_out, and_2_out, and_3_out, and_4_out);
  or or_3 (flush, \冲突 , branch);

  // Other names for the same wires on the sheet: RS1[4:0] = IR[19:15]; RS2[4:0] = IR[24:20]
endmodule

module \重定向流水线处理  (
  input  [31:0] IR,
  input  u1,
  input  EX_RegWrite,
  input  u2,
  input  MEM_RegWrite,
  input  [4:0] EX_rd,
  input  branch,
  input  EX_MemToReg,
  input  [4:0] MEM_rd,
  input  ecall,
  output \冲突 ,
  output flush,
  output [1:0] RS1_Forward,
  output [1:0] RS2_Forward
);

  wire and_1_out, and_2_out, and_3_out, and_4_out, and_5_out, and_6_out, and_8_out, and_9_out, and_10_out,
       and_11_out, comparator_1_eq, comparator_2_eq, comparator_3_eq, comparator_4_eq, comparator_5_eq,
       comparator_6_eq, comparator_7_eq, comparator_8_eq, comparator_9_eq, comparator_10_eq,
       comparator_11_eq, comparator_12_eq, comparator_13_eq, comparator_14_eq, comparator_15_eq,
       comparator_16_eq, not_1_out, not_2_out, not_3_out, not_4_out, not_5_out, not_6_out, not_7_out,
       not_8_out, or_3_out, or_6_out;

  Comparator #(.width(5), .mode("twosComplement")) comparator_1 (
    .a(EX_rd), .b(IR[24:20]), .eq(comparator_1_eq));  // open: gt, lt
  Comparator #(.width(5), .mode("twosComplement")) comparator_2 (
    .a(IR[24:20]), .b({5{1'b0}}), .eq(comparator_2_eq));  // open: gt, lt
  not not_1 (not_1_out, comparator_2_eq);
  Comparator #(.width(5), .mode("twosComplement")) comparator_3 (
    .a(EX_rd), .b(IR[19:15]), .eq(comparator_3_eq));  // open: gt, lt
  not not_2 (not_2_out, comparator_4_eq);
  Comparator #(.width(5), .mode("twosComplement")) comparator_4 (
    .a(IR[19:15]), .b({5{1'b0}}), .eq(comparator_4_eq));  // open: gt, lt
  Comparator #(.width(5), .mode("twosComplement")) comparator_5 (
    .a(EX_rd), .b(IR[19:15]), .eq(comparator_5_eq));  // open: gt, lt
  not not_3 (not_3_out, comparator_6_eq);
  Comparator #(.width(5), .mode("twosComplement")) comparator_6 (
    .a(IR[19:15]), .b({5{1'b0}}), .eq(comparator_6_eq));  // open: gt, lt
  Comparator #(.width(5), .mode("twosComplement")) comparator_7 (
    .a(EX_rd), .b(5'b10001), .eq(comparator_7_eq));  // open: gt, lt
  Comparator #(.width(5), .mode("twosComplement")) comparator_8 (
    .a(MEM_rd), .b(IR[19:15]), .eq(comparator_8_eq));  // open: gt, lt
  Comparator #(.width(5), .mode("twosComplement")) comparator_9 (
    .a(IR[19:15]), .b({5{1'b0}}), .eq(comparator_9_eq));  // open: gt, lt
  not not_4 (not_4_out, comparator_9_eq);
  Comparator #(.width(5), .mode("twosComplement")) comparator_10 (
    .a(MEM_rd), .b(5'b10001), .eq(comparator_10_eq));  // open: gt, lt
  and and_1 (and_1_out, comparator_7_eq, EX_RegWrite, ecall);
  and and_2 (and_2_out, comparator_10_eq, MEM_RegWrite, ecall);
  and and_3 (and_3_out, EX_MemToReg, u2, comparator_1_eq, not_1_out);
  and and_4 (and_4_out, EX_MemToReg, u1, comparator_3_eq, not_2_out);
  and and_5 (and_5_out, EX_RegWrite, u1, comparator_5_eq, not_3_out);
  and and_6 (and_6_out, MEM_RegWrite, u1, comparator_8_eq, not_4_out);
  or or_1 (\冲突 , and_3_out, and_4_out);
  or or_2 (RS1_Forward[1], and_5_out, and_1_out);
  or or_3 (or_3_out, and_6_out, and_2_out);
  or or_4 (flush, \冲突 , branch);
  not not_5 (not_5_out, RS1_Forward[1]);
  and and_7 (RS1_Forward[0], not_5_out, or_3_out);
  Comparator #(.width(5), .mode("twosComplement")) comparator_11 (
    .a(EX_rd), .b(IR[24:20]), .eq(comparator_11_eq));  // open: gt, lt
  Comparator #(.width(5), .mode("twosComplement")) comparator_12 (
    .a(IR[24:20]), .b({5{1'b0}}), .eq(comparator_12_eq));  // open: gt, lt
  not not_6 (not_6_out, comparator_12_eq);
  Comparator #(.width(5), .mode("twosComplement")) comparator_13 (
    .a(EX_rd), .b(5'b01010), .eq(comparator_13_eq));  // open: gt, lt
  Comparator #(.width(5), .mode("twosComplement")) comparator_14 (
    .a(MEM_rd), .b(IR[24:20]), .eq(comparator_14_eq));  // open: gt, lt
  not not_7 (not_7_out, comparator_15_eq);
  Comparator #(.width(5), .mode("twosComplement")) comparator_15 (
    .a(IR[24:20]), .b({5{1'b0}}), .eq(comparator_15_eq));  // open: gt, lt
  Comparator #(.width(5), .mode("twosComplement")) comparator_16 (
    .a(MEM_rd), .b(5'b01010), .eq(comparator_16_eq));  // open: gt, lt
  and and_8 (and_8_out, comparator_13_eq, EX_RegWrite, ecall);
  and and_9 (and_9_out, comparator_16_eq, MEM_RegWrite, ecall);
  and and_10 (and_10_out, EX_RegWrite, u2, comparator_11_eq, not_6_out);
  and and_11 (and_11_out, MEM_RegWrite, u2, comparator_14_eq, not_7_out);
  or or_5 (RS2_Forward[1], and_10_out, and_8_out);
  or or_6 (or_6_out, and_11_out, and_9_out);
  not not_8 (not_8_out, RS2_Forward[1]);
  and and_12 (RS2_Forward[0], not_8_out, or_6_out);

  // Other names for the same wires on the sheet: RS1[4:0] = IR[19:15]; RS2[4:0] = IR[24:20]
endmodule
module \流水线中断  (
  output RegWrite,
  output MemWrite,
  output [31:0] IF_PC,
  output [31:0] ID_PC,
  output [31:0] EX_PC,
  output [31:0] M_PC,
  output [31:0] WB_PC,
  output [31:0] RDin,
  output [31:0] MDin,
  output [31:0] LedData
);

  wire ALUequal, ALUge, and_1_out, and_2_out, and_3_out, and_4_out, and_5_out, and_6_out, and_8_out,
       and_11_out, and_12_out, branch, CLK, clock_1_out, comparator_1_eq, comparator_2_eq, comparator_3_eq,
       comparator_4_eq, comparator_5_eq, comparator_6_eq, comparator_6_lt, comparator_8_eq, comparator_9_eq,
       comparator_10_eq, csr, csrrci, csrrsi, d_ff_1_q, d_ff_2_q, d_ff_3_q, d_ff_7_q, demultiplexer_1_out0,
       demultiplexer_1_out1, demultiplexer_1_out2, demultiplexer_2_out0, demultiplexer_2_out1,
       demultiplexer_2_out2, EX_ecall, ex_mem_1_halt_2, ex_mem_1_jal_2, ex_mem_1_jalr_2, ex_mem_1_lbu_2,
       ex_mem_1_memtoreg_2, ex_mem_1_regwrite_2, ex_mem_1_uret_2, exhalt, flush, Go, halt, ID_ecall,
       id_ex_1_alusrcb_2, id_ex_1_beq_2, id_ex_1_bge_2, id_ex_1_bne_2, id_ex_1_jal_2, id_ex_1_lbu_2,
       id_ex_1_memtoreg_2, id_ex_1_memwrite_2, id_ex_1_regwrite_2, id_ex_1_u_type_2, IE, IR1, IR2, IR3, IRA,
       IRB, IRC, jal, mem_wb_1_halt_2, mem_wb_1_jal_2, mem_wb_1_jalr_2, mem_wb_1_lbu_2, mem_wb_1_memtoreg_2,
       mem_wb_1_u_type_2, MemUtype, nand_1_out, not_1_out, not_2_out, not_3_out, not_4_out, not_5_out,
       not_6_out, not_7_out, or_1_out, or_5_out, or_6_out, or_7_out, or_8_out, or_10_out, or_11_out,
       or_13_out, or_14_out, or_15_out, or_16_out, priority_encoder_1_gs, RESET1, RESET2, RESET3, RST, Stype,
       uret, Utype, W1, W2, W3, \中断 , \中断1 , \中断2 , \中断3 , \中断优先 , \冲突 , \单周期硬布线控制器_1_alu_src ,
       \单周期硬布线控制器_1_beq , \单周期硬布线控制器_1_bge , \单周期硬布线控制器_1_bne , \单周期硬布线控制器_1_csr , \单周期硬布线控制器_1_jalr ,
       \单周期硬布线控制器_1_lbu , \单周期硬布线控制器_1_memtoreg , \单周期硬布线控制器_1_memwrite , \单周期硬布线控制器_1_regwrite ,
       \单周期硬布线控制器_1_u1 , \单周期硬布线控制器_1_u2 , \单周期硬布线控制器_1_uret ;
  wire [1:0] EPC_4_q, EPC_5_q, EPC_6_q, id_ex_1_jalr_2, id_ex_1_rs1f_2, id_ex_1_rs2f_2, multiplexer_9_out,
       or_18_out, r1_forward, r2_forward, \中断号 , \中断计数 , \前中断号 ;
  wire [3:0] id_ex_1_aluop_2, \单周期硬布线控制器_1_alu_op ;
  wire [4:0] EX_rd, MEM_rd, multiplexer_2_out, multiplexer_3_out, \WB地址 ;
  wire [7:0] multiplexer_16_out;
  wire [11:0] multiplexer_4_out;
  wire [12:0] CNT_num;
  wire [15:0] \LoadUse次数 , \总周期数 , \插入气泡数 , \无条件分支数 , \条件分支成功数 ;
  wire [31:0] adder_2_out, ALUresult, bit_extender_1_out, bit_extender_2_out, bit_extender_3_out,
       bit_extender_4_out, EPC, EPC_2_q, EPC_3_q, EPC_q, EX_IR, ex_mem_1_pc_4_2, EX_R1, EX_R2,
       id_ex_1_imm_1_2, id_ex_1_imm_2_2, id_ex_1_imm_3_2, id_ex_1_pc_4_2, ID_IR, if_id_1_pc_4_2, IF_IR,
       Jaddress, LBUData, MEM_AluResult, MEM_IR, MEM_Uimm, mem_wb_1_aluresult_2, mem_wb_1_memdata_2,
       mem_wb_1_pc_4_2, mem_wb_1_uimm_2, multiplexer_5_out, multiplexer_8_out, multiplexer_14_out, newr1,
       newr2, PC_4, ram_1_data, regifile_1_r1, regifile_1_r2, shifter_1_out, shifter_2_out, WB_IR, \中断地址 ,
       \新PC , \老PC ;

  Button \u_总复位  (.out(RST));
  Button _1 (.out(IR1));
  Button _2 (.out(IR2));
  Button _3 (.out(IR3));
  // Probe on \总周期数 
  // Probe on \总周期数 
  Button \u_继续运行  (.out(Go));
  LED #(.active("true")) led_1 (.in(W1));
  LED #(.active("true")) led_2 (.in(W2));
  LED #(.active("true")) led_3 (.in(W3));
  not not_1 (not_1_out, halt);
  Hex_Digit_Display hex_digit_display_1 (.value(LedData[31:28]));  // open: dp
  // Probe on IF_PC[19:0]
  // RiscV_Probe riscv_probe_1: pin names not known; wires that end beside it: IF_IR
  and and_1 (and_1_out, or_1_out, not_2_out);
  Multiplexer #(.select(2), .width(32), .disabled("Z"), .enable("false")) multiplexer_1 (
    .in0(PC_4), .in1(ALUresult), .in2(Jaddress), .out(\老PC ), .sel(id_ex_1_jalr_2));  // open: in3
  or or_1 (or_1_out, not_1_out, Go);
  not not_2 (not_2_out, \冲突 );
  Hex_Digit_Display hex_digit_display_2 (.value(LedData[27:24]));  // open: dp
  Hex_Digit_Display hex_digit_display_3 (.value(LedData[23:20]));  // open: dp
  // Probe on ID_PC[19:0]
  // RiscV_Probe riscv_probe_2: pin names not known; wires that end beside it: ID_IR
  Register #(.width(32), .trigger("rising"), .Select("low")) PC (
    .D(\新PC ), .en(and_1_out), .Q(IF_PC), .clk(CLK), .clr(RST));
  Hex_Digit_Display hex_digit_display_4 (.value(LedData[19:16]));  // open: dp
  Hex_Digit_Display hex_digit_display_5 (.value(LedData[15:12]));  // open: dp
  Adder #(.width(32)) adder_1 (.a(IF_PC), .b(32'h4), .out(PC_4));  // open: cin, cout
  or or_2 (W1, \中断1 , d_ff_1_q);
  or or_3 (W2, \中断2 , d_ff_2_q);
  or or_4 (W3, \中断3 , d_ff_3_q);
  Hex_Digit_Display hex_digit_display_6 (.value(LedData[11:8]));  // open: dp
  Hex_Digit_Display hex_digit_display_7 (.value(LedData[7:4]));  // open: dp
  // Probe on EX_PC[19:0]
  // RiscV_Probe riscv_probe_3: pin names not known; wires that end beside it: EX_IR
  // RiscV_Probe riscv_probe_4: pin names not known; wires that end beside it: IF_IR
  D_Flip_Flop #(.trigger("rising"), .Pre_Clr_Positions("LEGACY"), .NegatePresetClear("false"), .enable("true"), .NewFFLayout("false")) d_ff_1 (
    .clk(IR1), .D(1'b1), .Q(d_ff_1_q), .en(1'b1), .reset(\中断1 ));  // open: Qn, preset
  D_Flip_Flop #(.trigger("rising"), .Pre_Clr_Positions("LEGACY"), .NegatePresetClear("false"), .enable("true"), .NewFFLayout("false")) d_ff_2 (
    .clk(IR2), .D(1'b1), .Q(d_ff_2_q), .en(1'b1), .reset(\中断2 ));  // open: Qn, preset
  D_Flip_Flop #(.trigger("rising"), .Pre_Clr_Positions("LEGACY"), .NegatePresetClear("false"), .enable("true"), .NewFFLayout("false")) d_ff_3 (
    .clk(IR3), .D(1'b1), .Q(d_ff_3_q), .en(1'b1), .reset(\中断3 ));  // open: Qn, preset
  Hex_Digit_Display hex_digit_display_8 (.value(LedData[3:0]));  // open: dp
  ROM #(.addrWidth(10), .dataWidth(32), .Select("high")) rom_1 (.addr(IF_PC[11:2]), .data(IF_IR));
  not not_3 (not_3_out, halt);
  Comparator #(.width(16), .mode("twosComplement")) comparator_1 (
    .a(16'h258), .b(\总周期数 ), .eq(comparator_1_eq));  // open: gt, lt
  Comparator #(.width(16), .mode("twosComplement")) comparator_2 (
    .a(\总周期数 ), .b(16'h1), .eq(comparator_2_eq));  // open: gt, lt
  Comparator #(.width(16), .mode("twosComplement")) comparator_3 (
    .a(\总周期数 ), .b(16'h4), .eq(comparator_3_eq));  // open: gt, lt
  Comparator #(.width(16), .mode("twosComplement")) comparator_4 (
    .a(\总周期数 ), .b(16'h7), .eq(comparator_4_eq));  // open: gt, lt
  or or_5 (or_5_out, comparator_4_eq, comparator_5_eq);
  Comparator #(.width(16), .mode("twosComplement")) comparator_5 (
    .a(\总周期数 ), .b(16'h241), .eq(comparator_5_eq));  // open: gt, lt
  or or_6 (or_6_out, d_ff_1_q, \中断1 );
  or or_7 (or_7_out, d_ff_2_q, \中断2 );
  or or_8 (or_8_out, d_ff_3_q, \中断3 );
  // Probe on \总周期数 
  // Probe on M_PC[19:0]
  // RiscV_Probe riscv_probe_5: pin names not known; wires that end beside it: MEM_IR
  or or_9 (branch, id_ex_1_jalr_2[0], id_ex_1_jalr_2[1]);
  IF_ID if_id_1 (
    .PC(IF_PC), .PC_4(PC_4), .IR(IF_IR), .PC_2(ID_PC), .PC_4_2(if_id_1_pc_4_2), .IR_2(ID_IR), .reset(1'b0),
    .flush(branch), .en(and_2_out), .CLK(CLK));  // open: 预测跳转, 预测跳转_2
  and and_2 (and_2_out, or_10_out, not_4_out);
  not not_4 (not_4_out, \冲突 );
  or or_10 (or_10_out, not_3_out, Go);
  or or_11 (or_11_out, comparator_1_eq, comparator_2_eq);
  Pull_Resistor #(.pull(0)) pull_resistor_1 (.node(IRA));
  assign IRA = or_11_out ? ~CLK : 1'bz;  // Controlled_Inverter controlled_inverter_1
  Pull_Resistor #(.pull(0)) pull_resistor_2 (.node(IRB));
  assign IRB = comparator_3_eq ? ~CLK : 1'bz;  // Controlled_Inverter controlled_inverter_2
  Pull_Resistor #(.pull(0)) pull_resistor_3 (.node(IRC));
  assign IRC = or_5_out ? ~CLK : 1'bz;  // Controlled_Inverter controlled_inverter_3
  D_Flip_Flop #(.trigger("rising"), .Pre_Clr_Positions("LEGACY"), .NegatePresetClear("false"), .enable("true"), .NewFFLayout("false")) d_ff_4 (
    .clk(CLK), .D(and_3_out), .Q(\中断1 ), .en(1'b1));  // open: Qn, preset, reset
  and and_3 (and_3_out, or_6_out, ~RESET1);  // AND_Gate
  D_Flip_Flop #(.trigger("rising"), .Pre_Clr_Positions("LEGACY"), .NegatePresetClear("false"), .enable("true"), .NewFFLayout("false")) d_ff_5 (
    .clk(CLK), .D(and_4_out), .Q(\中断2 ), .en(1'b1));  // open: Qn, preset, reset
  and and_4 (and_4_out, or_7_out, ~RESET2);  // AND_Gate
  D_Flip_Flop #(.trigger("rising"), .Pre_Clr_Positions("LEGACY"), .NegatePresetClear("false"), .enable("true"), .NewFFLayout("false")) d_ff_6 (
    .clk(CLK), .D(and_5_out), .Q(\中断3 ), .en(1'b1));  // open: Qn, preset, reset
  and and_5 (and_5_out, or_8_out, ~RESET3);  // AND_Gate
  // Probe on \总周期数 
  // Probe on \无条件分支数 
  // Probe on \条件分支成功数 
  // Probe on \插入气泡数 
  // Probe on \LoadUse次数 
  // Probe on IF_PC[11:0]
  // Probe on WB_PC[19:0]
  // RiscV_Probe riscv_probe_6: pin names not known; wires that end beside it: WB_IR
  \单周期硬布线控制器  \u_单周期硬布线控制器_1  (
    .Funct({ID_IR[30], ID_IR[25], ID_IR[14:12]}), .OP(ID_IR[6:2]), .ALU_OP(\单周期硬布线控制器_1_alu_op ),
    .MemToReg(\单周期硬布线控制器_1_memtoreg ), .MemWrite(\单周期硬布线控制器_1_memwrite ), .ALU_SRC(\单周期硬布线控制器_1_alu_src ),
    .RegWrite(\单周期硬布线控制器_1_regwrite ), .ecall(ID_ecall), .S_type(Stype), .Jalr(\单周期硬布线控制器_1_jalr ),
    .Beq(\单周期硬布线控制器_1_beq ), .JAL(jal), .Bne(\单周期硬布线控制器_1_bne ), .in_3(ID_IR[21]), .uret(\单周期硬布线控制器_1_uret ),
    .u2(\单周期硬布线控制器_1_u2 ), .u1(\单周期硬布线控制器_1_u1 ), .csr(\单周期硬布线控制器_1_csr ), .U_type(Utype),
    .bge(\单周期硬布线控制器_1_bge ), .LBU(\单周期硬布线控制器_1_lbu ));
  Multiplexer #(.select(1), .width(5), .disabled("Z"), .enable("false")) multiplexer_2 (
    .in0(ID_IR[19:15]), .in1(5'b10001), .out(multiplexer_2_out), .sel(ID_ecall));
  Multiplexer #(.select(1), .width(5), .disabled("Z"), .enable("false")) multiplexer_3 (
    .in0(ID_IR[24:20]), .in1(5'b01010), .out(multiplexer_3_out), .sel(ID_ecall));
  Multiplexer #(.select(1), .width(12), .disabled("Z"), .enable("false")) multiplexer_4 (
    .in0(ID_IR[31:20]), .in1({ID_IR[31:25], ID_IR[11:7]}), .out(multiplexer_4_out), .sel(Stype));
  assign bit_extender_1_out = {{12{ID_IR[31]}}, ID_IR[31:12]};  // Bit_Extender bit_extender_1
  Shifter #(.width(32), .shift("ll")) shifter_1 (.in(bit_extender_1_out), .\dist (5'b01100), .out(shifter_1_out));
  // Probe on EX_PC[11:0]
  // Probe on ID_PC[11:0]
  assign bit_extender_2_out = {{20{multiplexer_4_out[11]}}, multiplexer_4_out};  // Bit_Extender bit_extender_2
  assign bit_extender_3_out = {{20{ID_IR[31]}}, {ID_IR[31], ID_IR[7], ID_IR[30:25], ID_IR[11:8]}};  // Bit_Extender bit_extender_3
  assign bit_extender_4_out = {{12{ID_IR[31]}}, {ID_IR[31], ID_IR[19:12], ID_IR[20], ID_IR[30:21]}};  // Bit_Extender bit_extender_4
  // Probe on M_PC[11:0]
  D_Flip_Flop #(.trigger("high"), .Pre_Clr_Positions("LEGACY"), .NegatePresetClear("false"), .enable("true"), .NewFFLayout("false")) d_ff_7 (.Q(d_ff_7_q));  // open: clk, D, Qn, preset, en, reset
  // Probe on 13'hc
  Regifile regifile_1 (
    .Din(RDin), .Clk(not_5_out), .R1(regifile_1_r1), .R2(regifile_1_r2), .WE(RegWrite), .W_num(\WB地址 ),
    .R1_num(multiplexer_2_out), .R2_num(multiplexer_3_out));
  not not_5 (not_5_out, CLK);
  Multiplexer #(.select(1), .width(32), .disabled("Z"), .enable("false")) multiplexer_5 (
    .in0(bit_extender_3_out), .in1(bit_extender_4_out), .out(multiplexer_5_out), .sel(jal));
  // Probe on WB_PC[11:0]
  Comparator #(.width(13), .mode("twosComplement")) comparator_6 (
    .a(CNT_num), .b(13'hc), .eq(comparator_6_eq), .lt(comparator_6_lt));  // open: gt
  Clock #(.highDuration(1), .lowDuration(1)) clock_1 (.out(clock_1_out));
  Multiplexer #(.select(2), .width(32), .disabled("Z"), .enable("false")) multiplexer_6 (
    .in0(\老PC ), .in1(EPC), .in2(\中断地址 ), .in3(EPC), .out(\新PC ), .sel({\中断 , uret}));
  Priority_Encoder #(.select(2), .disabled("Z")) priority_encoder_1 (
    .in1(\中断1 ), .in2(\中断2 ), .in3(\中断3 ), .out(\中断号 ), .gs(priority_encoder_1_gs));  // open: in0, en_out, en_in
  nand nand_1 (nand_1_out, d_ff_7_q, comparator_6_eq);
  Counter #(.width(13), .max('h1fff), .ongoal("stay"), .trigger("rising"), .behavior("old")) counter_1 (
    .count(comparator_6_lt), .Q(CNT_num), .clk(clock_1_out));  // open: load, D, carry, clr, preset
  ID_EX id_ex_1 (
    .Beq(\单周期硬布线控制器_1_beq ), .Bne(\单周期硬布线控制器_1_bne ), .MemToReg(\单周期硬布线控制器_1_memtoreg ),
    .MemWrite(\单周期硬布线控制器_1_memwrite ), .RegWrite(\单周期硬布线控制器_1_regwrite ), .JAL(jal),
    .JALR(\单周期硬布线控制器_1_jalr ), .URET(\单周期硬布线控制器_1_uret ), .S_type(Stype), .U_type(Utype),
    .bge(\单周期硬布线控制器_1_bge ), .csr(\单周期硬布线控制器_1_csr ), .LBU(\单周期硬布线控制器_1_lbu ), .ecall(ID_ecall),
    .AluOP(\单周期硬布线控制器_1_alu_op ), .rd(ID_IR[11:7]), .R1(regifile_1_r1), .R2(regifile_1_r2),
    .imm_1(bit_extender_2_out), .imm_2(multiplexer_5_out), .PC(ID_PC), .PC_4(if_id_1_pc_4_2), .IR(ID_IR),
    .rs1f(r1_forward), .rs2f(r2_forward), .Beq_2(id_ex_1_beq_2), .Bne_2(id_ex_1_bne_2),
    .MemToReg_2(id_ex_1_memtoreg_2), .MemWrite_2(id_ex_1_memwrite_2), .RegWrite_2(id_ex_1_regwrite_2),
    .JAL_2(id_ex_1_jal_2), .JALR_2(id_ex_1_jalr_2[0]), .URET_2(uret), .U_type_2(id_ex_1_u_type_2),
    .bge_2(id_ex_1_bge_2), .csr_2(csr), .LBU_2(id_ex_1_lbu_2), .ecall_2(EX_ecall), .AluOP_2(id_ex_1_aluop_2),
    .rd_2(EX_rd), .R1_2(EX_R1), .R2_2(EX_R2), .imm_1_2(id_ex_1_imm_1_2), .imm_2_2(id_ex_1_imm_2_2),
    .PC_2(EX_PC), .PC_4_2(id_ex_1_pc_4_2), .IR_2(EX_IR), .rs1f_2(id_ex_1_rs1f_2), .rs2f_2(id_ex_1_rs2f_2),
    .reset(1'b0), .flush(flush), .en(or_10_out), .CLK(CLK), .AluSrcB(\单周期硬布线控制器_1_alu_src ),
    .AluSrcB_2(id_ex_1_alusrcb_2), .imm_3(shifter_1_out), .imm_3_2(id_ex_1_imm_3_2));  // open: S_type_2, 预测跳转_2, 预测跳转
  Multiplexer #(.select(2), .width(32), .disabled("Z"), .enable("false")) multiplexer_7 (
    .in0(EX_R1), .in1(RDin), .in2(MEM_AluResult), .out(newr1), .sel(id_ex_1_rs1f_2));  // open: in3
  assign CLK = nand_1_out ? clock_1_out : 1'bz;  // Controlled_Buffer controlled_buffer_1
  \重定向流水线处理  \u_重定向流水线处理_1  (
    .IR(ID_IR), .u1(\单周期硬布线控制器_1_u1 ), .EX_RegWrite(id_ex_1_regwrite_2), .u2(\单周期硬布线控制器_1_u2 ),
    .MEM_RegWrite(ex_mem_1_regwrite_2), .EX_rd(EX_rd), .branch(branch), .EX_MemToReg(id_ex_1_memtoreg_2),
    .MEM_rd(MEM_rd), .ecall(ID_ecall), .\冲突 (\冲突 ), .flush(flush), .RS1_Forward(r1_forward),
    .RS2_Forward(r2_forward));
  or or_12 (id_ex_1_jalr_2[1], id_ex_1_jal_2, or_13_out);
  and and_6 (and_6_out, id_ex_1_beq_2, ALUequal);
  and and_7 (\中断 , priority_encoder_1_gs, \中断优先 , IE);
  Comparator #(.width(2), .mode("unsigned")) comparator_7 (.a(\前中断号 ), .b(\中断号 ), .lt(\中断优先 ));  // open: gt, eq
  Pull_Resistor #(.pull(1)) pull_resistor_4 (.node(\中断优先 ));
  Comparator #(.width(3), .mode("twosComplement")) comparator_8 (
    .a(3'b110), .b(EX_IR[14:12]), .eq(comparator_8_eq));  // open: gt, lt
  Comparator #(.width(3), .mode("twosComplement")) comparator_9 (
    .a(EX_IR[14:12]), .b(3'b111), .eq(comparator_9_eq));  // open: gt, lt
  Pull_Resistor #(.pull(1)) pull_resistor_5 (.node(CLK));
  or or_13 (or_13_out, and_6_out, and_11_out, and_8_out);
  and and_8 (and_8_out, id_ex_1_bne_2, ~ALUequal);  // AND_Gate
  Multiplexer #(.select(1), .width(32), .disabled("Z"), .enable("false")) multiplexer_8 (
    .in0(newr2), .in1(id_ex_1_imm_1_2), .out(multiplexer_8_out), .sel(id_ex_1_alusrcb_2));
  Shifter #(.width(32), .shift("ll")) shifter_2 (.in(id_ex_1_imm_2_2), .\dist (5'b00001), .out(shifter_2_out));
  Comparator #(.width(32), .mode("twosComplement")) comparator_10 (
    .a(newr1), .b(32'h22), .eq(comparator_10_eq));  // open: gt, lt
  Multiplexer #(.select(1), .width(2), .disabled("Z"), .enable("false")) multiplexer_9 (
    .in0(id_ex_1_rs2f_2), .in1(2'b11), .out(multiplexer_9_out), .sel(MemUtype));
  Multiplexer #(.select(2), .width(32), .disabled("Z"), .enable("false")) multiplexer_10 (
    .in0(EX_R2), .in1(RDin), .in2(MEM_AluResult), .in3(MEM_Uimm), .out(newr2), .sel(multiplexer_9_out));
  and and_9 (csrrsi, comparator_8_eq, csr);
  and and_10 (csrrci, csr, comparator_9_eq);
  and and_11 (and_11_out, id_ex_1_bge_2, ALUge);
  ALU alu_1 (
    .X(newr1), .Y(multiplexer_8_out), .AluOP(id_ex_1_aluop_2), .Equal(ALUequal), .Result(ALUresult),
    .out_4(ALUge));  // open: Result_2, out_6
  Adder #(.width(32)) adder_2 (.a(id_ex_1_imm_3_2), .b(EX_PC), .out(adder_2_out));  // open: cin, cout
  Adder #(.width(32)) adder_3 (.a(shifter_2_out), .b(EX_PC), .out(Jaddress), .cin(1'b0));  // open: cout
  not not_6 (not_6_out, comparator_10_eq);
  and and_12 (and_12_out, comparator_10_eq, EX_ecall);
  or or_14 (or_14_out, \中断 , uret);
  Multiplexer #(.select(2), .width(32), .disabled("Z"), .enable("false")) multiplexer_11 (
    .in1(32'h30ac), .in2(32'h3158), .in3(32'h3204), .out(\中断地址 ), .sel(\中断号 ));  // open: in0
  not not_7 (not_7_out, halt);
  and and_13 (exhalt, EX_ecall, not_6_out);
  Counter #(.width(2), .max('h3), .ongoal("wrap"), .trigger("rising"), .behavior("new")) counter_2 (
    .count(or_14_out), .Q(\中断计数 ), .clk(CLK), .down(uret));  // open: load, D, carry, clr, preset
  Counter #(.width(16), .max('hffff), .ongoal("wrap"), .trigger("rising"), .behavior("new")) counter_3 (
    .load(1'b0), .D({16{1'b0}}), .count(not_7_out), .Q(\总周期数 ), .clk(CLK), .clr(1'b0), .down(1'b0));  // open: carry, preset
  Register #(.width(32), .trigger("rising"), .Select("low")) register_1 (
    .D(newr2), .en(and_12_out), .Q(LedData), .clk(CLK));  // open: clr
  or or_15 (or_15_out, \中断 , csrrci);
  or or_16 (or_16_out, \中断 , csrrci, csrrsi, uret);
  EX_MEM ex_mem_1 (
    .MemToReg(id_ex_1_memtoreg_2), .MemWrite(id_ex_1_memwrite_2), .RegWrite(id_ex_1_regwrite_2),
    .JAL(id_ex_1_jal_2), .JALR(id_ex_1_jalr_2[0]), .URET(uret), .LBU(id_ex_1_lbu_2), .halt(exhalt),
    .rd(EX_rd), .result(ALUresult), .R2(newr2), .PC(EX_PC), .PC_4(id_ex_1_pc_4_2), .IR(EX_IR),
    .MemToReg_2(ex_mem_1_memtoreg_2), .MemWrite_2(MemWrite), .RegWrite_2(ex_mem_1_regwrite_2),
    .JAL_2(ex_mem_1_jal_2), .JALR_2(ex_mem_1_jalr_2), .URET_2(ex_mem_1_uret_2), .LBU_2(ex_mem_1_lbu_2),
    .halt_2(ex_mem_1_halt_2), .rd_2(MEM_rd), .result_2(MEM_AluResult), .R2_2(MDin), .PC_2(M_PC),
    .PC_4_2(ex_mem_1_pc_4_2), .IR_2(MEM_IR), .reset(1'b0), .flush(1'b0), .en(or_10_out), .CLK(CLK),
    .U_type(id_ex_1_u_type_2), .U_type_2(MemUtype), .Uimm(adder_2_out), .Uimm_2(MEM_Uimm));
  D_Flip_Flop #(.trigger("rising"), .Pre_Clr_Positions("LEGACY"), .NegatePresetClear("false"), .enable("true"), .NewFFLayout("false")) d_ff_8 (
    .clk(CLK), .D(or_15_out), .Qn(IE), .en(or_16_out));  // open: Q, preset, reset
  Demultiplexer #(.select(2), .width(1), .tristate("false"), .disabled("Z"), .enable("false")) demultiplexer_1 (
    .out0(demultiplexer_1_out0), .out1(demultiplexer_1_out1), .out2(demultiplexer_1_out2), .in(\中断 ),
    .sel(\中断计数 ));  // open: out3
  Demultiplexer #(.select(2), .width(1), .tristate("false"), .disabled("Z"), .enable("false")) demultiplexer_2 (
    .out0(demultiplexer_2_out0), .out1(demultiplexer_2_out1), .out2(demultiplexer_2_out2), .in(\中断 ),
    .sel(\中断计数 ));  // open: out3
  RAM #(.addrWidth(10), .dataWidth(32), .bus("separate"), .Select("high")) ram_1 (
    .addr(MEM_AluResult[11:2]), .din(MDin), .data(ram_1_data), .str(MemWrite), .sel(1'b1), .clk(CLK),
    .ld(1'b1));  // open: clr
  Demultiplexer #(.select(2), .width(1), .tristate("false"), .disabled("Z"), .enable("false")) demultiplexer_3 (
    .out1(RESET1), .out2(RESET2), .out3(RESET3), .in(uret), .sel(\前中断号 ));  // open: out0
  Register #(.width(32), .trigger("rising"), .Select("low")) u_EPC (
    .D(\老PC ), .en(demultiplexer_1_out0), .Q(EPC_q), .clk(CLK));  // open: clr
  Register #(.width(32), .trigger("rising"), .Select("low")) EPC_2 (
    .D(\老PC ), .en(demultiplexer_1_out1), .Q(EPC_2_q), .clk(CLK));  // open: clr
  Register #(.width(32), .trigger("rising"), .Select("low")) EPC_3 (
    .D(\老PC ), .en(demultiplexer_1_out2), .Q(EPC_3_q), .clk(CLK));  // open: clr
  Register #(.width(2), .trigger("rising"), .Select("low")) EPC_4 (
    .D(\中断号 ), .en(demultiplexer_2_out0), .Q(EPC_4_q), .clk(CLK));  // open: clr
  Register #(.width(2), .trigger("rising"), .Select("low")) EPC_5 (
    .D(\中断号 ), .en(demultiplexer_2_out1), .Q(EPC_5_q), .clk(CLK));  // open: clr
  Register #(.width(2), .trigger("rising"), .Select("low")) EPC_6 (
    .D(\中断号 ), .en(demultiplexer_2_out2), .Q(EPC_6_q), .clk(CLK));  // open: clr
  Pull_Resistor #(.pull(0)) pull_resistor_6 (.node(RESET1));
  MEM_WB mem_wb_1 (
    .LBU(ex_mem_1_lbu_2), .MemToReg(ex_mem_1_memtoreg_2), .RegWrite(ex_mem_1_regwrite_2),
    .JAL(ex_mem_1_jal_2), .JALR(ex_mem_1_jalr_2), .URET(ex_mem_1_uret_2), .halt(ex_mem_1_halt_2),
    .rd(MEM_rd), .ALUresult(MEM_AluResult), .MemData(ram_1_data), .PC(M_PC), .PC_4(ex_mem_1_pc_4_2),
    .IR(MEM_IR), .LBU_2(mem_wb_1_lbu_2), .MemToReg_2(mem_wb_1_memtoreg_2), .RegWrite_2(RegWrite),
    .JAL_2(mem_wb_1_jal_2), .JALR_2(mem_wb_1_jalr_2), .halt_2(mem_wb_1_halt_2), .rd_2(\WB地址 ),
    .ALUresult_2(mem_wb_1_aluresult_2), .MemData_2(mem_wb_1_memdata_2), .PC_2(WB_PC),
    .PC_4_2(mem_wb_1_pc_4_2), .IR_2(WB_IR), .reset(1'b0), .flush(1'b0), .en(or_10_out), .CLK(CLK),
    .U_type(MemUtype), .U_type_2(mem_wb_1_u_type_2), .Uimm(MEM_Uimm), .Uimm_2(mem_wb_1_uimm_2));  // open: URET_2
  Multiplexer #(.select(2), .width(32), .disabled("Z"), .enable("false")) multiplexer_12 (
    .in1(EPC_q), .in2(EPC_2_q), .in3(EPC_3_q), .out(EPC), .sel(\中断计数 ));  // open: in0
  Multiplexer #(.select(2), .width(2), .disabled("Z"), .enable("false")) multiplexer_13 (
    .in1(EPC_4_q), .in2(EPC_5_q), .in3(EPC_6_q), .out(\前中断号 ), .sel(\中断计数 ));  // open: in0
  Pull_Resistor #(.pull(0)) pull_resistor_7 (.node(RESET2));
  or or_17 (or_18_out[1], mem_wb_1_jal_2, mem_wb_1_u_type_2, mem_wb_1_jalr_2);
  Pull_Resistor #(.pull(0)) pull_resistor_8 (.node(RESET3));
  or or_18 (or_18_out[0], mem_wb_1_memtoreg_2, mem_wb_1_u_type_2);
  Multiplexer #(.select(1), .width(32), .disabled("Z"), .enable("false")) multiplexer_14 (
    .in0(mem_wb_1_memdata_2), .in1(LBUData), .out(multiplexer_14_out), .sel(mem_wb_1_lbu_2));
  Multiplexer #(.select(2), .width(32), .disabled("Z"), .enable("false")) multiplexer_15 (
    .in0(mem_wb_1_aluresult_2), .in1(multiplexer_14_out), .in2(mem_wb_1_pc_4_2), .in3(mem_wb_1_uimm_2),
    .out(RDin), .sel(or_18_out));
  D_Flip_Flop #(.trigger("rising"), .Pre_Clr_Positions("ABOVE_BELOW"), .NegatePresetClear("false"), .enable("true"), .NewFFLayout("true")) d_ff_9 (
    .clk(mem_wb_1_halt_2), .D(1'b1), .Q(halt), .preset(1'b0), .en(1'b1), .reset(Go));  // open: Qn
  Multiplexer #(.select(2), .width(8), .disabled("Z"), .enable("false")) multiplexer_16 (
    .in0(mem_wb_1_memdata_2[7:0]), .in1(mem_wb_1_memdata_2[15:8]), .in2(mem_wb_1_memdata_2[23:16]),
    .in3(mem_wb_1_memdata_2[31:24]), .out(multiplexer_16_out), .sel(mem_wb_1_aluresult_2[1:0]));
  assign LBUData = {{24{1'b0}}, multiplexer_16_out};  // Bit_Extender bit_extender_5

  // Other names for the same wires on the sheet: MEM_PC[31:0] = M_PC

  // Notes on the sheet:
  //   中断源
  //   时空图监测，可删除
  //   中断等待指示
  //   数码管输出
  //   IF
  //   指令探针
  //   指令存储器
  //   多级中断测试信号模拟器
  //   contents of rom_1 (hex, n*v repeats v):
  //   7d000113 100413 1f41993 41f9d993 433 c00913 800b13 140413 f47413 800293 100313 499993 89e9b3 1300533
  //   2200893 73 406282b3 fe0294e3 140413 f00f93 1f47433 1c41413 800293 100313 49d993 89e9b3 1300533
  //   2200893 73 406282b3 fe0294e3 1c45413 406b0b33 b0463 f95ff06f 2b3 fff2c293 1029293 fff2e293 500533
  //   2200893 73 f5dff06f 1112023 410113 a12023 410113 812023 410113 1312023 410113 1412023 410113 1512023
  //   410113 1612023 410113 40e073 100b13 300a13 100a93 1600433 441413 14469b3 1300533 2200893 73 fe0416e3
  //   415a0a33 fe0a10e3 40f073 ffc10113 12b03 ffc10113 12a83 ffc10113 12a03 ffc10113 12983 ffc10113 12403
  //   ffc10113 12503 ffc10113 12883 200073 1112023 410113 a12023 410113 812023 410113 1312023 410113
  //   1412023 410113 1512023 410113 1612023 410113 40e073 200b13 300a13 100a93 1600433 441413 14469b3
  //   1300533 2200893 73 fe0416e3 415a0a33 fe0a10e3 40f073 ffc10113 12b03 ffc10113 12a83 ffc10113 12a03
  //   ffc10113 12983 ffc10113 12403 ffc10113 12503 ffc10113 12883 200073 1112023 410113 a12023 410113
  //   812023 410113 1312023 410113 1412023 410113 1512023 410113 1612023 410113 40e073 300b13 300a13
  //   100a93 1600433 441413 14469b3 1300533 2200893 73 fe0416e3 415a0a33 fe0a10e3 40f073 ffc10113 12b03
  //   ffc10113 12a83 ffc10113 12a03 ffc10113 12983 ffc10113 12403 ffc10113 12503 ffc10113 12883 200073
  //   JAL
  //   JALR
  //   CSR
  //   rs1
  //   rs2
  //   rd
  //   I指令
  //   S指令
  //   B指令
  //   U指令
  //   J指令
  //   ID
  //   Beq
  //   Bne
  //   MemToReg
  //   MemWrite
  //   AluOP
  //   AluSrcB
  //   RegWrite
  //   控制位
  //   流水调试日志用
  //   暂停节拍，不能为0
  //   PC更新
  //   戳工具置1进入计数暂停模式，ctrl+k时钟自动运行到对应节拍暂停
  //   ctrl+k关闭时钟连续运行，将控制位置零，进入单步调试模式调试
  //   R1
  //   R2
  //   rd
  //   imm1
  //   imm2
  //   可计数暂停的时钟源
  //   中断使能
  //   EX
  //   中断计数
  //   为方便自动评测，需要输出流水线各段保存的PC值，注意是PC不是PC+4，另外ID段寄存器写入信息，Mem段内存写入信息也要输出
  //   ALUresult
  //   RegWrite
  //   MEM
  //   数据存储器
  //   保存中断号
  //   堆栈保存EPC
  //   MemtoReg
  //   JAL
  //   JALR
  //   LBU
  //   WB
endmodule

module \cache归并比较  (
  input  [15:0] Y,
  input  [15:0] X,
  input  [2:0] Y_num,
  input  [2:0] X_num,
  output [15:0] MAX,
  output [2:0] Max_num
);

  wire comparator_1_eq, comparator_1_gt, or_1_out;

  Multiplexer #(.select(1), .width(16), .disabled("Z"), .enable("false")) multiplexer_1 (
    .in0(Y), .in1(X), .out(MAX), .sel(or_1_out));
  Comparator #(.width(16), .mode("unsigned")) comparator_1 (
    .a(X), .b(Y), .gt(comparator_1_gt), .eq(comparator_1_eq));  // open: lt
  or or_1 (or_1_out, comparator_1_gt, comparator_1_eq);
  Multiplexer #(.select(1), .width(3), .disabled("Z"), .enable("false")) multiplexer_2 (
    .in0(Y_num), .in1(X_num), .out(Max_num), .sel(or_1_out));

  // Notes on the sheet:
  //   输出两个输入中的较大值，并输出较大值的3位编号
endmodule

module \分支历史表  (
  input  [31:0] exbranch_ad,
  input  [31:0] exPC,
  input  exbranch,
  input  CLK,
  input  [31:0] ifPC,
  input  \是否跳转 ,
  output [31:0] \预测结果 ,
  output \预测跳转 
);

  wire and_1_out, and_2_out, and_3_out, and_4_out, and_5_out, and_6_out, and_7_out, and_8_out, and_9_out,
       and_10_out, and_11_out, and_12_out, and_13_out, and_14_out, and_15_out, and_16_out, and_17_out,
       and_18_out, and_19_out, and_20_out, and_21_out, and_22_out, and_23_out, and_26_out, and_27_out,
       and_30_out, and_31_out, and_34_out, and_35_out, and_36_out, and_37_out, and_40_out, and_41_out,
       and_42_out, and_43_out, and_44_out, and_45_out, and_46_out, and_47_out, comparator_1_eq,
       comparator_2_eq, comparator_3_eq, comparator_4_eq, comparator_5_eq, comparator_6_eq, comparator_7_eq,
       comparator_8_eq, comparator_9_eq, comparator_10_eq, comparator_11_eq, comparator_12_eq,
       comparator_13_eq, comparator_14_eq, comparator_15_eq, comparator_16_eq, decoder_1_out0,
       decoder_1_out1, decoder_1_out2, decoder_1_out3, decoder_1_out4, decoder_1_out5, decoder_1_out6,
       decoder_1_out7, nor_2_out, not_1_out, not_2_out, not_3_out, not_4_out, not_5_out, not_6_out,
       not_7_out, not_8_out, or_1_out, or_2_out, or_3_out, or_4_out, or_5_out, or_6_out, or_7_out, or_8_out,
       or_9_out, or_10_out, or_11_out, or_12_out, or_13_out, or_14_out, or_15_out, or_16_out, undriven, WE0,
       WE1, WE2, WE3, WE4, WE5, WE6, WE7, \已满 , \有效位_2_q , \有效位_3_q , \有效位_4_q , \有效位_5_q , \有效位_6_q ,
       \有效位_7_q , \有效位_8_q , \有效位_q ;
  wire [0:0] controlled_buffer_9_out, controlled_buffer_10_out, controlled_buffer_11_out,
       controlled_buffer_12_out, controlled_buffer_13_out, controlled_buffer_14_out,
       controlled_buffer_15_out, controlled_buffer_16_out;
  wire [1:0] register_1_q, register_2_q, register_3_q, register_4_q, register_5_q, register_6_q,
       register_7_q, register_8_q, \双位预测状态转换_1_z0 , \双位预测状态转换_2_z0 , \双位预测状态转换_3_z0 , \双位预测状态转换_4_z0 ,
       \双位预测状态转换_5_z0 , \双位预测状态转换_6_z0 , \双位预测状态转换_7_z0 , \双位预测状态转换_8_z0 ;
  wire [2:0] \cache归并比较_1_max_num , \cache归并比较_2_max_num , \cache归并比较_3_max_num , \cache归并比较_4_max_num ,
       \cache归并比较_5_max_num , \cache归并比较_6_max_num , \cache归并比较_7_max_num ;
  wire [15:0] \cache归并比较_1_max , \cache归并比较_2_max , \cache归并比较_3_max , \cache归并比较_4_max , \cache归并比较_5_max ,
       \cache归并比较_6_max , \淘汰计数器_2_q , \淘汰计数器_3_q , \淘汰计数器_4_q , \淘汰计数器_5_q , \淘汰计数器_6_q , \淘汰计数器_7_q ,
       \淘汰计数器_8_q , \淘汰计数器_q ;
  wire [31:0] \区地址_2_q , \区地址_3_q , \区地址_4_q , \区地址_5_q , \区地址_6_q , \区地址_7_q , \区地址_8_q , \区地址_q ,
       \数据缓存_2_q , \数据缓存_3_q , \数据缓存_4_q , \数据缓存_5_q , \数据缓存_6_q , \数据缓存_7_q , \数据缓存_8_q , \数据缓存_q ;

  and and_1 (and_1_out, exbranch, WE7);
  and and_2 (and_2_out, exbranch, WE0);
  and and_3 (and_3_out, exbranch, WE1);
  and and_4 (and_4_out, exbranch, WE2);
  and and_5 (and_5_out, exbranch, WE3);
  and and_6 (and_6_out, exbranch, WE4);
  and and_7 (and_7_out, exbranch, WE5);
  and and_8 (and_8_out, exbranch, WE6);
  Register #(.width(1), .trigger("rising"), .Select("low")) \u_有效位  (
    .D(1'b1), .en(and_2_out), .Q(\有效位_q ), .clk(CLK), .clr(1'b0), .cs(1'b0), .preset(1'b0));
  Register #(.width(1), .trigger("rising"), .Select("low")) \u_有效位_2  (
    .D(1'b1), .en(and_3_out), .Q(\有效位_2_q ), .clk(CLK), .clr(1'b0), .cs(1'b0), .preset(1'b0));
  Register #(.width(1), .trigger("rising"), .Select("low")) \u_有效位_3  (
    .D(1'b1), .en(and_4_out), .Q(\有效位_3_q ), .clk(CLK), .clr(1'b0), .cs(1'b0), .preset(1'b0));
  Register #(.width(1), .trigger("rising"), .Select("low")) \u_有效位_4  (
    .D(1'b1), .en(and_5_out), .Q(\有效位_4_q ), .clk(CLK), .clr(1'b0), .cs(1'b0), .preset(1'b0));
  Register #(.width(1), .trigger("rising"), .Select("low")) \u_有效位_5  (
    .D(1'b1), .en(and_6_out), .Q(\有效位_5_q ), .clk(CLK), .clr(1'b0), .cs(1'b0), .preset(1'b0));
  Register #(.width(1), .trigger("rising"), .Select("low")) \u_有效位_6  (
    .D(1'b1), .en(and_7_out), .Q(\有效位_6_q ), .clk(CLK), .clr(1'b0), .cs(1'b0), .preset(1'b0));
  Register #(.width(1), .trigger("rising"), .Select("low")) \u_有效位_7  (
    .D(1'b1), .en(and_8_out), .Q(\有效位_7_q ), .clk(CLK), .clr(1'b0), .cs(1'b0), .preset(1'b0));
  Register #(.width(1), .trigger("rising"), .Select("low")) \u_有效位_8  (
    .D(1'b1), .en(and_1_out), .Q(\有效位_8_q ), .clk(CLK), .clr(1'b0), .cs(1'b0), .preset(1'b0));
  not not_1 (not_1_out, \有效位_8_q );
  not not_2 (not_2_out, \有效位_7_q );
  not not_3 (not_3_out, \有效位_6_q );
  not not_4 (not_4_out, \有效位_5_q );
  not not_5 (not_5_out, \有效位_4_q );
  not not_6 (not_6_out, \有效位_3_q );
  not not_7 (not_7_out, \有效位_2_q );
  not not_8 (not_8_out, \有效位_q );
  Register #(.width(32), .trigger("rising"), .Select("low")) \u_区地址  (
    .D(exPC), .en(and_2_out), .Q(\区地址_q ), .clk(CLK), .clr(1'b0), .cs(1'b0), .preset(1'b0));
  Register #(.width(32), .trigger("rising"), .Select("low")) \u_区地址_2  (
    .D(exPC), .en(and_3_out), .Q(\区地址_2_q ), .clk(CLK), .clr(1'b0), .cs(1'b0), .preset(1'b0));
  Register #(.width(32), .trigger("rising"), .Select("low")) \u_区地址_3  (
    .D(exPC), .en(and_4_out), .Q(\区地址_3_q ), .clk(CLK), .clr(1'b0), .cs(1'b0), .preset(1'b0));
  Register #(.width(32), .trigger("rising"), .Select("low")) \u_区地址_4  (
    .D(exPC), .en(and_5_out), .Q(\区地址_4_q ), .clk(CLK), .clr(1'b0), .cs(1'b0), .preset(1'b0));
  Register #(.width(32), .trigger("rising"), .Select("low")) \u_区地址_5  (
    .D(exPC), .en(and_6_out), .Q(\区地址_5_q ), .clk(CLK), .clr(1'b0), .cs(1'b0), .preset(1'b0));
  Register #(.width(32), .trigger("rising"), .Select("low")) \u_区地址_6  (
    .D(exPC), .en(and_7_out), .Q(\区地址_6_q ), .clk(CLK), .clr(1'b0), .cs(1'b0), .preset(1'b0));
  Register #(.width(32), .trigger("rising"), .Select("low")) \u_区地址_7  (
    .D(exPC), .en(and_8_out), .Q(\区地址_7_q ), .clk(CLK), .clr(1'b0), .cs(1'b0), .preset(1'b0));
  Register #(.width(32), .trigger("rising"), .Select("low")) \u_区地址_8  (
    .D(exPC), .en(and_1_out), .Q(\区地址_8_q ), .clk(CLK), .clr(1'b0), .cs(1'b0), .preset(1'b0));
  Comparator #(.width(32), .mode("twosComplement")) comparator_1 (
    .a(\区地址_8_q ), .b(exPC), .eq(comparator_1_eq));  // open: gt, lt
  Comparator #(.width(32), .mode("twosComplement")) comparator_2 (
    .a(\区地址_8_q ), .b(ifPC), .eq(comparator_2_eq));  // open: gt, lt
  and and_9 (and_9_out, not_1_out, \有效位_7_q );
  and and_10 (and_10_out, not_2_out, \有效位_6_q );
  and and_11 (and_11_out, not_3_out, \有效位_5_q );
  and and_12 (and_12_out, not_4_out, \有效位_4_q );
  and and_13 (and_13_out, not_5_out, \有效位_3_q );
  and and_14 (and_14_out, not_6_out, \有效位_2_q );
  and and_15 (and_15_out, not_7_out, \有效位_q );
  and and_16 (and_16_out, \有效位_8_q , comparator_1_eq);
  and and_17 (and_17_out, \有效位_8_q , comparator_2_eq);
  Comparator #(.width(32), .mode("twosComplement")) comparator_3 (
    .a(\区地址_7_q ), .b(exPC), .eq(comparator_3_eq));  // open: gt, lt
  Comparator #(.width(32), .mode("twosComplement")) comparator_4 (
    .a(\区地址_7_q ), .b(ifPC), .eq(comparator_4_eq));  // open: gt, lt
  nor nor_1 (\已满 , not_8_out, and_15_out, and_14_out, and_13_out, and_12_out, and_11_out, and_10_out, and_9_out);
  and and_18 (and_18_out, \有效位_7_q , comparator_3_eq);
  and and_19 (and_19_out, \有效位_7_q , comparator_4_eq);
  Comparator #(.width(32), .mode("twosComplement")) comparator_5 (
    .a(\区地址_6_q ), .b(exPC), .eq(comparator_5_eq));  // open: gt, lt
  Comparator #(.width(32), .mode("twosComplement")) comparator_6 (
    .a(\区地址_6_q ), .b(ifPC), .eq(comparator_6_eq));  // open: gt, lt
  and and_20 (and_20_out, \有效位_6_q , comparator_5_eq);
  and and_21 (and_21_out, \有效位_6_q , comparator_6_eq);
  and and_22 (and_22_out, \有效位_5_q , comparator_7_eq);
  Comparator #(.width(32), .mode("twosComplement")) comparator_7 (
    .a(\区地址_5_q ), .b(exPC), .eq(comparator_7_eq));  // open: gt, lt
  and and_23 (and_23_out, \有效位_5_q , comparator_8_eq);
  Comparator #(.width(32), .mode("twosComplement")) comparator_8 (
    .a(\区地址_5_q ), .b(ifPC), .eq(comparator_8_eq));  // open: gt, lt
  Comparator #(.width(32), .mode("twosComplement")) comparator_9 (
    .a(\区地址_4_q ), .b(exPC), .eq(comparator_9_eq));  // open: gt, lt
  Comparator #(.width(32), .mode("twosComplement")) comparator_10 (
    .a(\区地址_4_q ), .b(ifPC), .eq(comparator_10_eq));  // open: gt, lt
  or or_1 (or_1_out, and_15_out, decoder_1_out1);
  or or_2 (or_2_out, not_8_out, decoder_1_out0);
  and and_24 (WE0, nor_2_out, or_2_out);
  and and_25 (WE1, nor_2_out, or_1_out);
  and and_26 (and_26_out, \有效位_4_q , comparator_9_eq);
  and and_27 (and_27_out, \有效位_4_q , comparator_10_eq);
  Comparator #(.width(32), .mode("twosComplement")) comparator_11 (
    .a(\区地址_3_q ), .b(exPC), .eq(comparator_11_eq));  // open: gt, lt
  Comparator #(.width(32), .mode("twosComplement")) comparator_12 (
    .a(\区地址_3_q ), .b(ifPC), .eq(comparator_12_eq));  // open: gt, lt
  or or_3 (or_3_out, and_13_out, decoder_1_out3);
  or or_4 (or_4_out, and_14_out, decoder_1_out2);
  and and_28 (WE3, nor_2_out, or_3_out);
  and and_29 (WE2, nor_2_out, or_4_out);
  and and_30 (and_30_out, \有效位_3_q , comparator_11_eq);
  and and_31 (and_31_out, \有效位_3_q , comparator_12_eq);
  Comparator #(.width(32), .mode("twosComplement")) comparator_13 (
    .a(\区地址_2_q ), .b(exPC), .eq(comparator_13_eq));  // open: gt, lt
  Comparator #(.width(32), .mode("twosComplement")) comparator_14 (
    .a(\区地址_2_q ), .b(ifPC), .eq(comparator_14_eq));  // open: gt, lt
  or or_5 (or_5_out, and_11_out, decoder_1_out5);
  or or_6 (or_6_out, and_12_out, decoder_1_out4);
  and and_32 (WE4, nor_2_out, or_6_out);
  and and_33 (WE5, nor_2_out, or_5_out);
  or or_7 (or_7_out, and_2_out, and_37_out);
  or or_8 (or_8_out, and_3_out, and_35_out);
  or or_9 (or_9_out, and_4_out, and_31_out);
  or or_10 (or_10_out, and_5_out, and_27_out);
  or or_11 (or_11_out, and_6_out, and_23_out);
  or or_12 (or_12_out, and_7_out, and_21_out);
  or or_13 (or_13_out, and_8_out, and_19_out);
  or or_14 (or_14_out, and_1_out, and_17_out);
  and and_34 (and_34_out, \有效位_2_q , comparator_13_eq);
  and and_35 (and_35_out, \有效位_2_q , comparator_14_eq);
  and and_36 (and_36_out, \有效位_q , comparator_15_eq);
  Comparator #(.width(32), .mode("twosComplement")) comparator_15 (
    .a(\区地址_q ), .b(exPC), .eq(comparator_15_eq));  // open: gt, lt
  and and_37 (and_37_out, \有效位_q , comparator_16_eq);
  Comparator #(.width(32), .mode("twosComplement")) comparator_16 (
    .a(\区地址_q ), .b(ifPC), .eq(comparator_16_eq));  // open: gt, lt
  or or_15 (or_15_out, and_9_out, decoder_1_out7);
  or or_16 (or_16_out, and_10_out, decoder_1_out6);
  and and_38 (WE6, nor_2_out, or_16_out);
  and and_39 (WE7, nor_2_out, or_15_out);
  Counter #(.width(16), .max('hffff), .ongoal("wrap"), .trigger("rising"), .behavior("new")) \u_淘汰计数器  (
    .load(or_7_out), .D({16{1'b0}}), .count(\有效位_q ), .Q(\淘汰计数器_q ), .clk(CLK), .clr(1'b0), .preset(1'b0),
    .down(1'b0));  // open: carry
  Counter #(.width(16), .max('hffff), .ongoal("wrap"), .trigger("rising"), .behavior("new")) \u_淘汰计数器_2  (
    .load(or_8_out), .D({16{1'b0}}), .count(\有效位_2_q ), .Q(\淘汰计数器_2_q ), .clk(CLK), .clr(1'b0),
    .preset(1'b0), .down(1'b0));  // open: carry
  Counter #(.width(16), .max('hffff), .ongoal("wrap"), .trigger("rising"), .behavior("new")) \u_淘汰计数器_3  (
    .load(or_9_out), .D({16{1'b0}}), .count(\有效位_3_q ), .Q(\淘汰计数器_3_q ), .clk(CLK), .clr(1'b0),
    .preset(1'b0), .down(1'b0));  // open: carry
  Counter #(.width(16), .max('hffff), .ongoal("wrap"), .trigger("rising"), .behavior("new")) \u_淘汰计数器_4  (
    .load(or_10_out), .D({16{1'b0}}), .count(\有效位_4_q ), .Q(\淘汰计数器_4_q ), .clk(CLK), .clr(1'b0),
    .preset(1'b0), .down(1'b0));  // open: carry
  Counter #(.width(16), .max('hffff), .ongoal("wrap"), .trigger("rising"), .behavior("new")) \u_淘汰计数器_5  (
    .load(or_11_out), .D({16{1'b0}}), .count(\有效位_5_q ), .Q(\淘汰计数器_5_q ), .clk(CLK), .clr(1'b0),
    .preset(1'b0), .down(1'b0));  // open: carry
  Counter #(.width(16), .max('hffff), .ongoal("wrap"), .trigger("rising"), .behavior("new")) \u_淘汰计数器_6  (
    .load(or_12_out), .D({16{1'b0}}), .count(\有效位_6_q ), .Q(\淘汰计数器_6_q ), .clk(CLK), .clr(1'b0),
    .preset(1'b0), .down(1'b0));  // open: carry
  Counter #(.width(16), .max('hffff), .ongoal("wrap"), .trigger("rising"), .behavior("new")) \u_淘汰计数器_7  (
    .load(or_13_out), .D({16{1'b0}}), .count(\有效位_7_q ), .Q(\淘汰计数器_7_q ), .clk(CLK), .clr(1'b0),
    .preset(1'b0), .down(1'b0));  // open: carry
  Counter #(.width(16), .max('hffff), .ongoal("wrap"), .trigger("rising"), .behavior("new")) \u_淘汰计数器_8  (
    .load(or_14_out), .D({16{1'b0}}), .count(\有效位_8_q ), .Q(\淘汰计数器_8_q ), .clk(CLK), .clr(1'b0),
    .preset(1'b0), .down(1'b0));  // open: carry
  \cache归并比较  \cache归并比较_1  (
    .Y(\淘汰计数器_7_q ), .X(\淘汰计数器_8_q ), .Y_num(3'b110), .X_num(3'b111), .MAX(\cache归并比较_1_max ),
    .Max_num(\cache归并比较_1_max_num ));
  \cache归并比较  \cache归并比较_2  (
    .Y(\淘汰计数器_5_q ), .X(\淘汰计数器_6_q ), .Y_num(3'b100), .X_num(3'b101), .MAX(\cache归并比较_2_max ),
    .Max_num(\cache归并比较_2_max_num ));
  \cache归并比较  \cache归并比较_3  (
    .Y(\淘汰计数器_3_q ), .X(\淘汰计数器_4_q ), .Y_num(3'b010), .X_num(3'b011), .MAX(\cache归并比较_3_max ),
    .Max_num(\cache归并比较_3_max_num ));
  \cache归并比较  \cache归并比较_4  (
    .Y(\cache归并比较_2_max ), .X(\cache归并比较_1_max ), .Y_num(\cache归并比较_2_max_num ),
    .X_num(\cache归并比较_1_max_num ), .MAX(\cache归并比较_4_max ), .Max_num(\cache归并比较_4_max_num ));
  \cache归并比较  \cache归并比较_5  (
    .Y(\淘汰计数器_q ), .X(\淘汰计数器_2_q ), .Y_num(3'b000), .X_num(3'b001), .MAX(\cache归并比较_5_max ),
    .Max_num(\cache归并比较_5_max_num ));
  Register #(.width(32), .trigger("rising"), .Select("low")) \u_数据缓存  (
    .D(exbranch_ad), .en(and_2_out), .Q(\数据缓存_q ), .clk(CLK), .clr(1'b0), .cs(1'b0), .preset(1'b0));
  Register #(.width(32), .trigger("rising"), .Select("low")) \u_数据缓存_2  (
    .D(exbranch_ad), .en(and_3_out), .Q(\数据缓存_2_q ), .clk(CLK), .clr(1'b0), .cs(1'b0), .preset(1'b0));
  Register #(.width(32), .trigger("rising"), .Select("low")) \u_数据缓存_3  (
    .D(exbranch_ad), .en(and_4_out), .Q(\数据缓存_3_q ), .clk(CLK), .clr(1'b0), .cs(1'b0), .preset(1'b0));
  Register #(.width(32), .trigger("rising"), .Select("low")) \u_数据缓存_4  (
    .D(exbranch_ad), .en(and_5_out), .Q(\数据缓存_4_q ), .clk(CLK), .clr(1'b0), .cs(undriven), .preset(1'b0));
  assign \预测结果  = and_23_out ? \数据缓存_5_q  : 32'bz;  // Controlled_Buffer controlled_buffer_1
  Register #(.width(32), .trigger("rising"), .Select("low")) \u_数据缓存_5  (
    .D(exbranch_ad), .en(and_6_out), .Q(\数据缓存_5_q ), .clk(CLK), .clr(1'b0), .cs(1'b0), .preset(1'b0));
  assign \预测结果  = and_21_out ? \数据缓存_6_q  : 32'bz;  // Controlled_Buffer controlled_buffer_2
  Register #(.width(32), .trigger("rising"), .Select("low")) \u_数据缓存_6  (
    .D(exbranch_ad), .en(and_7_out), .Q(\数据缓存_6_q ), .clk(CLK), .clr(1'b0), .cs(1'b0), .preset(1'b0));
  Register #(.width(32), .trigger("rising"), .Select("low")) \u_数据缓存_7  (
    .D(exbranch_ad), .en(and_8_out), .Q(\数据缓存_7_q ), .clk(CLK), .clr(1'b0), .cs(1'b0), .preset(1'b0));
  assign \预测结果  = and_19_out ? \数据缓存_7_q  : 32'bz;  // Controlled_Buffer controlled_buffer_3
  assign \预测结果  = and_17_out ? \数据缓存_8_q  : 32'bz;  // Controlled_Buffer controlled_buffer_4
  Register #(.width(32), .trigger("rising"), .Select("low")) \u_数据缓存_8  (
    .D(exbranch_ad), .en(and_1_out), .Q(\数据缓存_8_q ), .clk(CLK), .clr(1'b0), .cs(1'b0), .preset(1'b0));
  \cache归并比较  \cache归并比较_6  (
    .Y(\cache归并比较_5_max ), .X(\cache归并比较_3_max ), .Y_num(\cache归并比较_5_max_num ),
    .X_num(\cache归并比较_3_max_num ), .MAX(\cache归并比较_6_max ), .Max_num(\cache归并比较_6_max_num ));
  Decoder #(.select(3), .tristate("false"), .disabled(0), .enable("true")) decoder_1 (
    .out0(decoder_1_out0), .out1(decoder_1_out1), .out2(decoder_1_out2), .out3(decoder_1_out3),
    .out4(decoder_1_out4), .out5(decoder_1_out5), .out6(decoder_1_out6), .out7(decoder_1_out7),
    .sel(\cache归并比较_7_max_num ), .en(\已满 ));
  assign \预测结果  = and_37_out ? \数据缓存_q  : 32'bz;  // Controlled_Buffer controlled_buffer_5
  assign \预测结果  = and_35_out ? \数据缓存_2_q  : 32'bz;  // Controlled_Buffer controlled_buffer_6
  assign \预测结果  = and_31_out ? \数据缓存_3_q  : 32'bz;  // Controlled_Buffer controlled_buffer_7
  assign \预测结果  = and_27_out ? \数据缓存_4_q  : 32'bz;  // Controlled_Buffer controlled_buffer_8
  nor nor_2 (nor_2_out, and_36_out, and_34_out, and_30_out, and_26_out, and_22_out, and_20_out, and_18_out, and_16_out);
  \cache归并比较  \cache归并比较_7  (
    .Y(\cache归并比较_6_max ), .X(\cache归并比较_4_max ), .Y_num(\cache归并比较_6_max_num ),
    .X_num(\cache归并比较_4_max_num ), .Max_num(\cache归并比较_7_max_num ));  // open: MAX
  \双位预测状态转换  \u_双位预测状态转换_1  (
    .Y1(register_1_q[1]), .Y0(register_1_q[0]), .\跳转 (\是否跳转 ), .Z1(\双位预测状态转换_1_z0 [1]),
    .Z0(\双位预测状态转换_1_z0 [0]));
  \双位预测状态转换  \u_双位预测状态转换_2  (
    .Y1(register_2_q[1]), .Y0(register_2_q[0]), .\跳转 (\是否跳转 ), .Z1(\双位预测状态转换_2_z0 [1]),
    .Z0(\双位预测状态转换_2_z0 [0]));
  \双位预测状态转换  \u_双位预测状态转换_3  (
    .Y1(register_3_q[1]), .Y0(register_3_q[0]), .\跳转 (\是否跳转 ), .Z1(\双位预测状态转换_3_z0 [1]),
    .Z0(\双位预测状态转换_3_z0 [0]));
  \双位预测状态转换  \u_双位预测状态转换_4  (
    .Y1(register_4_q[1]), .Y0(register_4_q[0]), .\跳转 (\是否跳转 ), .Z1(\双位预测状态转换_4_z0 [1]),
    .Z0(\双位预测状态转换_4_z0 [0]));
  \双位预测状态转换  \u_双位预测状态转换_5  (
    .Y1(register_5_q[1]), .Y0(register_5_q[0]), .\跳转 (\是否跳转 ), .Z1(\双位预测状态转换_5_z0 [1]),
    .Z0(\双位预测状态转换_5_z0 [0]));
  \双位预测状态转换  \u_双位预测状态转换_6  (
    .Y1(register_6_q[1]), .Y0(register_6_q[0]), .\跳转 (\是否跳转 ), .Z1(\双位预测状态转换_6_z0 [1]),
    .Z0(\双位预测状态转换_6_z0 [0]));
  \双位预测状态转换  \u_双位预测状态转换_7  (
    .Y1(register_7_q[1]), .Y0(register_7_q[0]), .\跳转 (\是否跳转 ), .Z1(\双位预测状态转换_7_z0 [1]),
    .Z0(\双位预测状态转换_7_z0 [0]));
  \双位预测状态转换  \u_双位预测状态转换_8  (
    .Y1(register_8_q[1]), .Y0(register_8_q[0]), .\跳转 (\是否跳转 ), .Z1(\双位预测状态转换_8_z0 [1]),
    .Z0(\双位预测状态转换_8_z0 [0]));
  and and_40 (and_40_out, exbranch, and_16_out);
  and and_41 (and_41_out, exbranch, and_18_out);
  and and_42 (and_42_out, exbranch, and_20_out);
  and and_43 (and_43_out, exbranch, and_22_out);
  and and_44 (and_44_out, exbranch, and_26_out);
  and and_45 (and_45_out, exbranch, and_30_out);
  and and_46 (and_46_out, exbranch, and_34_out);
  and and_47 (and_47_out, exbranch, and_36_out);
  Register #(.width(2), .trigger("rising"), .Select("low")) register_1 (
    .D(\双位预测状态转换_1_z0 ), .en(and_40_out), .Q(register_1_q), .clk(CLK), .clr(1'b0), .cs(1'b0), .preset(1'b0));
  Register #(.width(2), .trigger("rising"), .Select("low")) register_2 (
    .D(\双位预测状态转换_2_z0 ), .en(and_41_out), .Q(register_2_q), .clk(CLK), .clr(1'b0), .cs(1'b0), .preset(1'b0));
  Register #(.width(2), .trigger("rising"), .Select("low")) register_3 (
    .D(\双位预测状态转换_3_z0 ), .en(and_42_out), .Q(register_3_q), .clk(CLK), .clr(1'b0), .cs(1'b0), .preset(1'b0));
  Register #(.width(2), .trigger("rising"), .Select("low")) register_4 (
    .D(\双位预测状态转换_4_z0 ), .en(and_43_out), .Q(register_4_q), .clk(CLK), .clr(1'b0), .cs(1'b0), .preset(1'b0));
  Register #(.width(2), .trigger("rising"), .Select("low")) register_5 (
    .D(\双位预测状态转换_5_z0 ), .en(and_44_out), .Q(register_5_q), .clk(CLK), .cs(1'b0), .preset(1'b0));  // open: clr
  Register #(.width(2), .trigger("rising"), .Select("low")) register_6 (
    .D(\双位预测状态转换_6_z0 ), .en(and_45_out), .Q(register_6_q), .clk(CLK), .clr(1'b0), .cs(1'b0), .preset(1'b0));
  Register #(.width(2), .trigger("rising"), .Select("low")) register_7 (
    .D(\双位预测状态转换_7_z0 ), .en(and_46_out), .Q(register_7_q), .clk(CLK), .clr(1'b0), .cs(1'b0), .preset(1'b0));
  Register #(.width(2), .trigger("rising"), .Select("low")) register_8 (
    .D(\双位预测状态转换_8_z0 ), .en(and_47_out), .Q(register_8_q), .clk(CLK), .clr(1'b0), .cs(1'b0), .preset(1'b0));
  assign {\预测跳转 , controlled_buffer_9_out[0]} = and_17_out ? register_1_q : 2'bz;  // Controlled_Buffer controlled_buffer_9
  assign {\预测跳转 , controlled_buffer_10_out[0]} = and_19_out ? register_2_q : 2'bz;  // Controlled_Buffer controlled_buffer_10
  assign {\预测跳转 , controlled_buffer_11_out[0]} = and_21_out ? register_3_q : 2'bz;  // Controlled_Buffer controlled_buffer_11
  assign {\预测跳转 , controlled_buffer_12_out[0]} = and_23_out ? register_4_q : 2'bz;  // Controlled_Buffer controlled_buffer_12
  assign {\预测跳转 , controlled_buffer_13_out[0]} = and_27_out ? register_5_q : 2'bz;  // Controlled_Buffer controlled_buffer_13
  assign {\预测跳转 , controlled_buffer_14_out[0]} = and_31_out ? register_6_q : 2'bz;  // Controlled_Buffer controlled_buffer_14
  assign {\预测跳转 , controlled_buffer_15_out[0]} = and_35_out ? register_7_q : 2'bz;  // Controlled_Buffer controlled_buffer_15
  assign {\预测跳转 , controlled_buffer_16_out[0]} = and_37_out ? register_8_q : 2'bz;  // Controlled_Buffer controlled_buffer_16
  Pull_Resistor #(.pull(0)) pull_resistor_1 (.node(\预测跳转 ));

  // Other names for the same wires on the sheet: 分支指令地址[31:0] = exPC; 分支目标地址[31:0] = exbranch_ad; 查询地址[31:0] = ifPC;
  //   表更新 = exbranch

  // Notes on the sheet:
  //   输入引脚区
  //   输出引脚区
endmodule

module \双位预测状态转换  (
  input  Y1,
  input  Y0,
  input  \跳转 ,
  output Z1,
  output Z0
);

  wire and_1_out, and_2_out, and_3_out, and_4_out, not_1_out, not_2_out, not_3_out, not_4_out, not_5_out;

  not not_1 (not_1_out, Y0);
  not not_2 (not_2_out, Y1);
  not not_3 (not_3_out, Y0);
  not not_4 (not_4_out, Y0);
  not not_5 (not_5_out, \跳转 );
  and and_1 (and_1_out, Y0, \跳转 );
  and and_2 (and_2_out, Y1, not_1_out);
  and and_3 (and_3_out, not_2_out, not_3_out, \跳转 );
  and and_4 (and_4_out, Y1, not_4_out, not_5_out);
  or or_1 (Z1, and_1_out, and_2_out);
  or or_2 (Z0, and_3_out, and_4_out);
endmodule

module \动态分支预测  (
  output RegWrite,
  output MemWrite,
  output [31:0] IF_PC,
  output [31:0] ID_PC,
  output [31:0] EX_PC,
  output [31:0] M_PC,
  output [31:0] WB_PC,
  output [31:0] RDin,
  output [31:0] MDin,
  output [31:0] LedData
);

  wire ALUequal, ALUge, and_1_out, and_2_out, and_3_out, and_4_out, and_5_out, and_6_out, and_8_out,
       and_11_out, and_12_out, branch, BranchOK, BS, CLK, clock_1_out, comparator_1_eq, comparator_2_eq,
       comparator_3_eq, comparator_4_eq, comparator_5_eq, comparator_6_eq, comparator_6_lt, comparator_8_eq,
       comparator_9_eq, comparator_10_eq, csr, csrrci, csrrsi, d_ff_1_q, d_ff_2_q, d_ff_3_q, d_ff_7_q,
       demultiplexer_1_out0, demultiplexer_1_out1, demultiplexer_1_out2, demultiplexer_2_out0,
       demultiplexer_2_out1, demultiplexer_2_out2, EX_ecall, EX_jal, EX_jalr, ex_mem_1_halt_2,
       ex_mem_1_jal_2, ex_mem_1_jalr_2, ex_mem_1_lbu_2, ex_mem_1_memtoreg_2, ex_mem_1_regwrite_2,
       ex_mem_1_uret_2, exhalt, flush, Go, halt, ID_ecall, id_ex_1_alusrcb_2, id_ex_1_beq_2, id_ex_1_bge_2,
       id_ex_1_bne_2, id_ex_1_lbu_2, id_ex_1_memtoreg_2, id_ex_1_memwrite_2, id_ex_1_regwrite_2,
       id_ex_1_u_type_2, \id_ex_1_预测跳转_2 , IE, \if_id_1_预测跳转_2 , IR1, IR2, IR3, IRA, IRB, IRC, jal,
       mem_wb_1_halt_2, mem_wb_1_jal_2, mem_wb_1_jalr_2, mem_wb_1_lbu_2, mem_wb_1_memtoreg_2,
       mem_wb_1_u_type_2, MemUtype, nand_1_out, not_1_out, not_2_out, not_3_out, not_4_out, not_5_out,
       not_6_out, not_7_out, or_1_out, or_2_out, or_7_out, or_8_out, or_9_out, or_10_out, or_11_out,
       or_12_out, or_13_out, or_14_out, or_18_out, or_19_out, or_20_out, priority_encoder_1_gs, RESET1,
       RESET2, RESET3, RST, Stype, uret, Utype, W1, W2, W3, \中断 , \中断1 , \中断2 , \中断3 , \中断优先 , \冲突 ,
       \分支历史表_1_预测跳转 , \单周期硬布线控制器_1_alu_src , \单周期硬布线控制器_1_beq , \单周期硬布线控制器_1_bge , \单周期硬布线控制器_1_bne ,
       \单周期硬布线控制器_1_csr , \单周期硬布线控制器_1_jalr , \单周期硬布线控制器_1_lbu , \单周期硬布线控制器_1_memtoreg ,
       \单周期硬布线控制器_1_memwrite , \单周期硬布线控制器_1_regwrite , \单周期硬布线控制器_1_u1 , \单周期硬布线控制器_1_u2 ,
       \单周期硬布线控制器_1_uret , \预测出错 ;
  wire [1:0] EPC_4_q, EPC_5_q, EPC_6_q, id_ex_1_rs1f_2, id_ex_1_rs2f_2, multiplexer_12_out, or_22_out,
       r1_forward, r2_forward, \中断号 , \中断计数 , \前中断号 ;
  wire [1:1] or_16_out;
  wire [3:0] id_ex_1_aluop_2, \单周期硬布线控制器_1_alu_op ;
  wire [4:0] EX_rd, MEM_rd, multiplexer_5_out, multiplexer_6_out, \WB地址 ;
  wire [7:0] multiplexer_19_out;
  wire [11:0] multiplexer_7_out;
  wire [12:0] CNT_num;
  wire [15:0] \LoadUse次数 , \总周期数 , \插入气泡数 , \无条件分支数 , \条件分支成功数 ;
  wire [31:0] adder_1_out, adder_3_out, ALUresult, bit_extender_1_out, bit_extender_2_out,
       bit_extender_3_out, bit_extender_4_out, EPC, EPC_2_q, EPC_3_q, EPC_q, EX_IR, ex_mem_1_pc_4_2, EX_R1,
       EX_R2, id_ex_1_imm_1_2, id_ex_1_imm_2_2, id_ex_1_imm_3_2, id_ex_1_pc_4_2, ID_IR, if_id_1_pc_4_2,
       IF_IR, Jaddress, LBUData, MEM_AluResult, MEM_IR, MEM_Uimm, mem_wb_1_aluresult_2, mem_wb_1_memdata_2,
       mem_wb_1_pc_4_2, mem_wb_1_uimm_2, multiplexer_1_out, multiplexer_2_out, multiplexer_8_out,
       multiplexer_11_out, multiplexer_17_out, newr1, newr2, PC_4, ram_1_data, regifile_1_r1, regifile_1_r2,
       shifter_1_out, shifter_2_out, WB_IR, \中断地址 , \分支历史表_1_预测结果 , \新PC , \老PC , \预测地址 ;

  Button \u_总复位  (.out(RST));
  Button _1 (.out(IR1));
  Button _2 (.out(IR2));
  Button _3 (.out(IR3));
  // Probe on \总周期数 
  // Probe on \总周期数 
  Button \u_继续运行  (.out(Go));
  LED #(.active("true")) led_1 (.in(W1));
  LED #(.active("true")) led_2 (.in(W2));
  LED #(.active("true")) led_3 (.in(W3));
  Adder #(.width(32)) adder_1 (.a(32'h4), .b(EX_PC), .out(adder_1_out), .cin(1'b0));  // open: cout
  Multiplexer #(.select(2), .width(32), .disabled("Z"), .enable("false")) multiplexer_1 (
    .in0(adder_1_out), .in1(ALUresult), .in2(Jaddress), .out(multiplexer_1_out), .sel({or_16_out[1], EX_jalr}));  // open: in3
  not not_1 (not_1_out, halt);
  Multiplexer #(.select(3), .width(32), .disabled("Z"), .enable("false")) multiplexer_2 (
    .in0(IF_PC), .in1(ALUresult), .in2(Jaddress), .in3(Jaddress), .in4(Jaddress), .in5(Jaddress),
    .in6(Jaddress), .in7(Jaddress), .out(multiplexer_2_out), .sel({BS, EX_jal, EX_jalr}));
  or or_1 (or_1_out, EX_jalr, EX_jal, BS);
  Hex_Digit_Display hex_digit_display_1 (.value(LedData[31:28]));  // open: dp
  // Probe on IF_PC[19:0]
  // RiscV_Probe riscv_probe_1: pin names not known; wires that end beside it: IF_IR
  Multiplexer #(.select(1), .width(32), .disabled("Z"), .enable("false")) multiplexer_3 (
    .in0(\预测地址 ), .in1(multiplexer_1_out), .out(\老PC ), .sel(\预测出错 ));
  and and_1 (and_1_out, or_2_out, not_2_out);
  or or_2 (or_2_out, not_1_out, Go);
  not not_2 (not_2_out, \冲突 );
  \分支历史表  \u_分支历史表_1  (
    .exbranch_ad(multiplexer_2_out), .exPC(EX_PC), .exbranch(or_1_out), .CLK(CLK), .ifPC(IF_PC),
    .\是否跳转 (branch), .\预测结果 (\分支历史表_1_预测结果 ), .\预测跳转 (\分支历史表_1_预测跳转 ));
  Hex_Digit_Display hex_digit_display_2 (.value(LedData[23:20]));  // open: dp
  Hex_Digit_Display hex_digit_display_3 (.value(LedData[27:24]));  // open: dp
  // Probe on ID_PC[19:0]
  // RiscV_Probe riscv_probe_2: pin names not known; wires that end beside it: ID_IR
  Register #(.width(32), .trigger("rising"), .Select("low")) PC (
    .D(\新PC ), .en(and_1_out), .Q(IF_PC), .clk(CLK), .clr(RST), .cs(1'b0), .preset(1'b0));
  Multiplexer #(.select(1), .width(32), .disabled("Z"), .enable("false")) multiplexer_4 (
    .in0(PC_4), .in1(\分支历史表_1_预测结果 ), .out(\预测地址 ), .sel(\分支历史表_1_预测跳转 ));
  Hex_Digit_Display hex_digit_display_4 (.value(LedData[19:16]));  // open: dp
  Hex_Digit_Display hex_digit_display_5 (.value(LedData[15:12]));  // open: dp
  Adder #(.width(32)) adder_2 (.a(IF_PC), .b(32'h4), .out(PC_4));  // open: cin, cout
  or or_3 (W1, \中断1 , d_ff_1_q);
  or or_4 (W2, \中断2 , d_ff_2_q);
  or or_5 (W3, \中断3 , d_ff_3_q);
  Hex_Digit_Display hex_digit_display_6 (.value(LedData[11:8]));  // open: dp
  Hex_Digit_Display hex_digit_display_7 (.value(LedData[7:4]));  // open: dp
  // Probe on EX_PC[19:0]
  // RiscV_Probe riscv_probe_3: pin names not known; wires that end beside it: EX_IR
  or or_6 (branch, EX_jalr, or_16_out[1]);
  or or_7 (or_7_out, \预测出错 , uret, \中断 );
  // RiscV_Probe riscv_probe_4: pin names not known; wires that end beside it: IF_IR
  D_Flip_Flop #(.trigger("rising"), .Pre_Clr_Positions("LEGACY"), .NegatePresetClear("false"), .enable("true"), .NewFFLayout("false")) d_ff_1 (
    .clk(IR1), .D(1'b1), .Q(d_ff_1_q), .en(1'b1), .reset(\中断1 ));  // open: Qn, preset
  D_Flip_Flop #(.trigger("rising"), .Pre_Clr_Positions("LEGACY"), .NegatePresetClear("false"), .enable("true"), .NewFFLayout("false")) d_ff_2 (
    .clk(IR2), .D(1'b1), .Q(d_ff_2_q), .en(1'b1), .reset(\中断2 ));  // open: Qn, preset
  D_Flip_Flop #(.trigger("rising"), .Pre_Clr_Positions("LEGACY"), .NegatePresetClear("false"), .enable("true"), .NewFFLayout("false")) d_ff_3 (
    .clk(IR3), .D(1'b1), .Q(d_ff_3_q), .en(1'b1), .reset(\中断3 ));  // open: Qn, preset
  Hex_Digit_Display hex_digit_display_8 (.value(LedData[3:0]));  // open: dp
  ROM #(.addrWidth(10), .dataWidth(32), .Select("high")) rom_1 (.addr(IF_PC[11:2]), .data(IF_IR), .sel(1'b1));
  not not_3 (not_3_out, halt);
  Comparator #(.width(16), .mode("twosComplement")) comparator_1 (
    .a(16'h258), .b(\总周期数 ), .eq(comparator_1_eq));  // open: gt, lt
  Comparator #(.width(16), .mode("twosComplement")) comparator_2 (
    .a(\总周期数 ), .b(16'h1), .eq(comparator_2_eq));  // open: gt, lt
  Comparator #(.width(16), .mode("twosComplement")) comparator_3 (
    .a(\总周期数 ), .b(16'h4), .eq(comparator_3_eq));  // open: gt, lt
  Comparator #(.width(16), .mode("twosComplement")) comparator_4 (
    .a(\总周期数 ), .b(16'h7), .eq(comparator_4_eq));  // open: gt, lt
  or or_8 (or_8_out, comparator_4_eq, comparator_5_eq);
  Comparator #(.width(16), .mode("twosComplement")) comparator_5 (
    .a(\总周期数 ), .b(16'h241), .eq(comparator_5_eq));  // open: gt, lt
  or or_9 (or_9_out, d_ff_1_q, \中断1 );
  or or_10 (or_10_out, d_ff_2_q, \中断2 );
  or or_11 (or_11_out, d_ff_3_q, \中断3 );
  // Probe on \总周期数 
  // Probe on M_PC[19:0]
  // RiscV_Probe riscv_probe_5: pin names not known; wires that end beside it: MEM_IR
  IF_ID if_id_1 (
    .PC(IF_PC), .PC_4(PC_4), .IR(IF_IR), .PC_2(ID_PC), .PC_4_2(if_id_1_pc_4_2), .IR_2(ID_IR), .reset(1'b0),
    .flush(or_7_out), .en(and_2_out), .CLK(CLK), .\预测跳转 (\分支历史表_1_预测跳转 ), .\预测跳转_2 (\if_id_1_预测跳转_2 ));
  and and_2 (and_2_out, or_12_out, not_4_out);
  not not_4 (not_4_out, \冲突 );
  or or_12 (or_12_out, not_3_out, Go);
  or or_13 (or_13_out, comparator_1_eq, comparator_2_eq);
  Pull_Resistor #(.pull(0)) pull_resistor_1 (.node(IRA));
  assign IRA = or_13_out ? ~CLK : 1'bz;  // Controlled_Inverter controlled_inverter_1
  Pull_Resistor #(.pull(0)) pull_resistor_2 (.node(IRB));
  assign IRB = comparator_3_eq ? ~CLK : 1'bz;  // Controlled_Inverter controlled_inverter_2
  Pull_Resistor #(.pull(0)) pull_resistor_3 (.node(IRC));
  assign IRC = or_8_out ? ~CLK : 1'bz;  // Controlled_Inverter controlled_inverter_3
  D_Flip_Flop #(.trigger("rising"), .Pre_Clr_Positions("LEGACY"), .NegatePresetClear("false"), .enable("true"), .NewFFLayout("false")) d_ff_4 (
    .clk(CLK), .D(and_3_out), .Q(\中断1 ), .en(1'b1));  // open: Qn, preset, reset
  and and_3 (and_3_out, or_9_out, ~RESET1);  // AND_Gate
  D_Flip_Flop #(.trigger("rising"), .Pre_Clr_Positions("LEGACY"), .NegatePresetClear("false"), .enable("true"), .NewFFLayout("false")) d_ff_5 (
    .clk(CLK), .D(and_4_out), .Q(\中断2 ), .en(1'b1));  // open: Qn, preset, reset
  and and_4 (and_4_out, or_10_out, ~RESET2);  // AND_Gate
  D_Flip_Flop #(.trigger("rising"), .Pre_Clr_Positions("LEGACY"), .NegatePresetClear("false"), .enable("true"), .NewFFLayout("false")) d_ff_6 (
    .clk(CLK), .D(and_5_out), .Q(\中断3 ), .en(1'b1));  // open: Qn, preset, reset
  and and_5 (and_5_out, or_11_out, ~RESET3);  // AND_Gate
  // Probe on \总周期数 
  // Probe on \无条件分支数 
  // Probe on \条件分支成功数 
  // Probe on \插入气泡数 
  // Probe on \LoadUse次数 
  // Probe on IF_PC[11:0]
  // Probe on WB_PC[19:0]
  // RiscV_Probe riscv_probe_6: pin names not known; wires that end beside it: WB_IR
  \单周期硬布线控制器  \u_单周期硬布线控制器_1  (
    .Funct({ID_IR[30], ID_IR[25], ID_IR[14:12]}), .OP(ID_IR[6:2]), .ALU_OP(\单周期硬布线控制器_1_alu_op ),
    .MemToReg(\单周期硬布线控制器_1_memtoreg ), .MemWrite(\单周期硬布线控制器_1_memwrite ), .ALU_SRC(\单周期硬布线控制器_1_alu_src ),
    .RegWrite(\单周期硬布线控制器_1_regwrite ), .ecall(ID_ecall), .S_type(Stype), .Jalr(\单周期硬布线控制器_1_jalr ),
    .Beq(\单周期硬布线控制器_1_beq ), .JAL(jal), .Bne(\单周期硬布线控制器_1_bne ), .in_3(ID_IR[21]), .uret(\单周期硬布线控制器_1_uret ),
    .u2(\单周期硬布线控制器_1_u2 ), .u1(\单周期硬布线控制器_1_u1 ), .csr(\单周期硬布线控制器_1_csr ), .U_type(Utype),
    .bge(\单周期硬布线控制器_1_bge ), .LBU(\单周期硬布线控制器_1_lbu ));
  Multiplexer #(.select(1), .width(5), .disabled("Z"), .enable("false")) multiplexer_5 (
    .in0(ID_IR[19:15]), .in1(5'b10001), .out(multiplexer_5_out), .sel(ID_ecall));
  Multiplexer #(.select(1), .width(5), .disabled("Z"), .enable("false")) multiplexer_6 (
    .in0(ID_IR[24:20]), .in1(5'b01010), .out(multiplexer_6_out), .sel(ID_ecall));
  Multiplexer #(.select(1), .width(12), .disabled("Z"), .enable("false")) multiplexer_7 (
    .in0(ID_IR[31:20]), .in1({ID_IR[31:25], ID_IR[11:7]}), .out(multiplexer_7_out), .sel(Stype));
  assign bit_extender_1_out = {{12{ID_IR[31]}}, ID_IR[31:12]};  // Bit_Extender bit_extender_1
  Shifter #(.width(32), .shift("ll")) shifter_1 (.in(bit_extender_1_out), .\dist (5'b01100), .out(shifter_1_out));
  // Probe on ID_PC[11:0]
  // Probe on EX_PC[11:0]
  assign bit_extender_2_out = {{20{multiplexer_7_out[11]}}, multiplexer_7_out};  // Bit_Extender bit_extender_2
  assign bit_extender_3_out = {{20{ID_IR[31]}}, {ID_IR[31], ID_IR[7], ID_IR[30:25], ID_IR[11:8]}};  // Bit_Extender bit_extender_3
  assign bit_extender_4_out = {{12{ID_IR[31]}}, {ID_IR[31], ID_IR[19:12], ID_IR[20], ID_IR[30:21]}};  // Bit_Extender bit_extender_4
  xor xor_1 (\预测出错 , \id_ex_1_预测跳转_2 , branch);
  // Probe on M_PC[11:0]
  D_Flip_Flop #(.trigger("high"), .Pre_Clr_Positions("LEGACY"), .NegatePresetClear("false"), .enable("true"), .NewFFLayout("false")) d_ff_7 (.Q(d_ff_7_q));  // open: clk, D, Qn, preset, en, reset
  // Probe on 13'h150
  Regifile regifile_1 (
    .Din(RDin), .Clk(not_5_out), .R1(regifile_1_r1), .R2(regifile_1_r2), .WE(RegWrite), .W_num(\WB地址 ),
    .R1_num(multiplexer_5_out), .R2_num(multiplexer_6_out));
  not not_5 (not_5_out, CLK);
  Multiplexer #(.select(1), .width(32), .disabled("Z"), .enable("false")) multiplexer_8 (
    .in0(bit_extender_3_out), .in1(bit_extender_4_out), .out(multiplexer_8_out), .sel(jal));
  // Probe on WB_PC[11:0]
  Comparator #(.width(13), .mode("twosComplement")) comparator_6 (
    .a(CNT_num), .b(13'h150), .eq(comparator_6_eq), .lt(comparator_6_lt));  // open: gt
  Clock #(.highDuration(1), .lowDuration(1)) clock_1 (.out(clock_1_out));
  or or_14 (or_14_out, \预测出错 , \中断 , \冲突 , uret);
  Multiplexer #(.select(2), .width(32), .disabled("Z"), .enable("false")) multiplexer_9 (
    .in0(\老PC ), .in1(EPC), .in2(\中断地址 ), .in3(EPC), .out(\新PC ), .sel({\中断 , uret}));
  Priority_Encoder #(.select(2), .disabled("Z")) priority_encoder_1 (
    .in1(\中断1 ), .in2(\中断2 ), .in3(\中断3 ), .out(\中断号 ), .gs(priority_encoder_1_gs));  // open: in0, en_out, en_in
  nand nand_1 (nand_1_out, d_ff_7_q, comparator_6_eq);
  Counter #(.width(13), .max('h1fff), .ongoal("stay"), .trigger("rising"), .behavior("old")) counter_1 (
    .count(comparator_6_lt), .Q(CNT_num), .clk(clock_1_out));  // open: load, D, carry, clr, preset
  or or_15 (BS, id_ex_1_bne_2, id_ex_1_memtoreg_2, id_ex_1_bge_2);
  ID_EX id_ex_1 (
    .Beq(\单周期硬布线控制器_1_beq ), .Bne(\单周期硬布线控制器_1_bne ), .MemToReg(\单周期硬布线控制器_1_memtoreg ),
    .MemWrite(\单周期硬布线控制器_1_memwrite ), .RegWrite(\单周期硬布线控制器_1_regwrite ), .JAL(jal),
    .JALR(\单周期硬布线控制器_1_jalr ), .URET(\单周期硬布线控制器_1_uret ), .S_type(Stype), .U_type(Utype),
    .bge(\单周期硬布线控制器_1_bge ), .csr(\单周期硬布线控制器_1_csr ), .LBU(\单周期硬布线控制器_1_lbu ), .ecall(ID_ecall),
    .AluOP(\单周期硬布线控制器_1_alu_op ), .rd(ID_IR[11:7]), .R1(regifile_1_r1), .R2(regifile_1_r2),
    .imm_1(bit_extender_2_out), .imm_2(multiplexer_8_out), .PC(ID_PC), .PC_4(if_id_1_pc_4_2), .IR(ID_IR),
    .rs1f(r1_forward), .rs2f(r2_forward), .Beq_2(id_ex_1_beq_2), .Bne_2(id_ex_1_bne_2),
    .MemToReg_2(id_ex_1_memtoreg_2), .MemWrite_2(id_ex_1_memwrite_2), .RegWrite_2(id_ex_1_regwrite_2),
    .JAL_2(EX_jal), .JALR_2(EX_jalr), .URET_2(uret), .U_type_2(id_ex_1_u_type_2), .bge_2(id_ex_1_bge_2),
    .csr_2(csr), .LBU_2(id_ex_1_lbu_2), .ecall_2(EX_ecall), .AluOP_2(id_ex_1_aluop_2), .rd_2(EX_rd),
    .R1_2(EX_R1), .R2_2(EX_R2), .imm_1_2(id_ex_1_imm_1_2), .imm_2_2(id_ex_1_imm_2_2), .PC_2(EX_PC),
    .PC_4_2(id_ex_1_pc_4_2), .IR_2(EX_IR), .rs1f_2(id_ex_1_rs1f_2), .rs2f_2(id_ex_1_rs2f_2), .reset(1'b0),
    .flush(or_14_out), .en(or_12_out), .CLK(CLK), .AluSrcB(\单周期硬布线控制器_1_alu_src ),
    .AluSrcB_2(id_ex_1_alusrcb_2), .imm_3(shifter_1_out), .imm_3_2(id_ex_1_imm_3_2),
    .\预测跳转_2 (\id_ex_1_预测跳转_2 ), .\预测跳转 (\if_id_1_预测跳转_2 ));  // open: S_type_2
  Multiplexer #(.select(2), .width(32), .disabled("Z"), .enable("false")) multiplexer_10 (
    .in0(EX_R1), .in1(RDin), .in2(MEM_AluResult), .out(newr1), .sel(id_ex_1_rs1f_2));  // open: in3
  assign CLK = nand_1_out ? clock_1_out : 1'bz;  // Controlled_Buffer controlled_buffer_1
  \重定向流水线处理  \u_重定向流水线处理_1  (
    .IR(ID_IR), .u1(\单周期硬布线控制器_1_u1 ), .EX_RegWrite(id_ex_1_regwrite_2), .u2(\单周期硬布线控制器_1_u2 ),
    .MEM_RegWrite(ex_mem_1_regwrite_2), .EX_rd(EX_rd), .branch(branch), .EX_MemToReg(id_ex_1_memtoreg_2),
    .MEM_rd(MEM_rd), .ecall(ID_ecall), .\冲突 (\冲突 ), .flush(flush), .RS1_Forward(r1_forward),
    .RS2_Forward(r2_forward));
  or or_16 (or_16_out[1], EX_jal, BranchOK);
  and and_6 (and_6_out, id_ex_1_beq_2, ALUequal);
  and and_7 (\中断 , priority_encoder_1_gs, \中断优先 , IE);
  Comparator #(.width(2), .mode("unsigned")) comparator_7 (.a(\前中断号 ), .b(\中断号 ), .lt(\中断优先 ));  // open: gt, eq
  Pull_Resistor #(.pull(1)) pull_resistor_4 (.node(\中断优先 ));
  Comparator #(.width(3), .mode("twosComplement")) comparator_8 (
    .a(3'b110), .b(EX_IR[14:12]), .eq(comparator_8_eq));  // open: gt, lt
  Comparator #(.width(3), .mode("twosComplement")) comparator_9 (
    .a(EX_IR[14:12]), .b(3'b111), .eq(comparator_9_eq));  // open: gt, lt
  Pull_Resistor #(.pull(1)) pull_resistor_5 (.node(CLK));
  or or_17 (BranchOK, and_6_out, and_11_out, and_8_out);
  and and_8 (and_8_out, id_ex_1_bne_2, ~ALUequal);  // AND_Gate
  Multiplexer #(.select(1), .width(32), .disabled("Z"), .enable("false")) multiplexer_11 (
    .in0(newr2), .in1(id_ex_1_imm_1_2), .out(multiplexer_11_out), .sel(id_ex_1_alusrcb_2));
  Shifter #(.width(32), .shift("ll")) shifter_2 (.in(id_ex_1_imm_2_2), .\dist (5'b00001), .out(shifter_2_out));
  Comparator #(.width(32), .mode("twosComplement")) comparator_10 (
    .a(newr1), .b(32'h22), .eq(comparator_10_eq));  // open: gt, lt
  Multiplexer #(.select(1), .width(2), .disabled("Z"), .enable("false")) multiplexer_12 (
    .in0(id_ex_1_rs2f_2), .in1(2'b11), .out(multiplexer_12_out), .sel(MemUtype));
  Multiplexer #(.select(2), .width(32), .disabled("Z"), .enable("false")) multiplexer_13 (
    .in0(EX_R2), .in1(RDin), .in2(MEM_AluResult), .in3(MEM_Uimm), .out(newr2), .sel(multiplexer_12_out));
  and and_9 (csrrsi, comparator_8_eq, csr);
  and and_10 (csrrci, csr, comparator_9_eq);
  and and_11 (and_11_out, id_ex_1_bge_2, ALUge);
  ALU alu_1 (
    .X(newr1), .Y(multiplexer_11_out), .AluOP(id_ex_1_aluop_2), .Equal(ALUequal), .Result(ALUresult),
    .out_4(ALUge));  // open: Result_2, out_6
  Adder #(.width(32)) adder_3 (.a(id_ex_1_imm_3_2), .b(EX_PC), .out(adder_3_out));  // open: cin, cout
  Adder #(.width(32)) adder_4 (.a(shifter_2_out), .b(EX_PC), .out(Jaddress), .cin(1'b0));  // open: cout
  not not_6 (not_6_out, comparator_10_eq);
  and and_12 (and_12_out, comparator_10_eq, EX_ecall);
  or or_18 (or_18_out, \中断 , uret);
  Multiplexer #(.select(2), .width(32), .disabled("Z"), .enable("false")) multiplexer_14 (
    .in1(32'h30ac), .in2(32'h3158), .in3(32'h3204), .out(\中断地址 ), .sel(\中断号 ));  // open: in0
  not not_7 (not_7_out, halt);
  and and_13 (exhalt, EX_ecall, not_6_out);
  Counter #(.width(2), .max('h3), .ongoal("wrap"), .trigger("rising"), .behavior("new")) counter_2 (
    .count(or_18_out), .Q(\中断计数 ), .clk(CLK), .down(uret));  // open: load, D, carry, clr, preset
  Counter #(.width(16), .max('hffff), .ongoal("wrap"), .trigger("rising"), .behavior("new")) counter_3 (
    .load(1'b0), .D({16{1'b0}}), .count(not_7_out), .Q(\总周期数 ), .clk(CLK), .clr(1'b0), .down(1'b0));  // open: carry, preset
  Register #(.width(32), .trigger("rising"), .Select("low")) register_1 (
    .D(newr2), .en(and_12_out), .Q(LedData), .clk(CLK));  // open: clr
  or or_19 (or_19_out, \中断 , csrrci);
  or or_20 (or_20_out, \中断 , csrrci, csrrsi, uret);
  EX_MEM ex_mem_1 (
    .MemToReg(id_ex_1_memtoreg_2), .MemWrite(id_ex_1_memwrite_2), .RegWrite(id_ex_1_regwrite_2),
    .JAL(EX_jal), .JALR(EX_jalr), .URET(uret), .LBU(id_ex_1_lbu_2), .halt(exhalt), .rd(EX_rd),
    .result(ALUresult), .R2(newr2), .PC(EX_PC), .PC_4(id_ex_1_pc_4_2), .IR(EX_IR),
    .MemToReg_2(ex_mem_1_memtoreg_2), .MemWrite_2(MemWrite), .RegWrite_2(ex_mem_1_regwrite_2),
    .JAL_2(ex_mem_1_jal_2), .JALR_2(ex_mem_1_jalr_2), .URET_2(ex_mem_1_uret_2), .LBU_2(ex_mem_1_lbu_2),
    .halt_2(ex_mem_1_halt_2), .rd_2(MEM_rd), .result_2(MEM_AluResult), .R2_2(MDin), .PC_2(M_PC),
    .PC_4_2(ex_mem_1_pc_4_2), .IR_2(MEM_IR), .reset(1'b0), .flush(1'b0), .en(or_12_out), .CLK(CLK),
    .U_type(id_ex_1_u_type_2), .U_type_2(MemUtype), .Uimm(adder_3_out), .Uimm_2(MEM_Uimm));
  D_Flip_Flop #(.trigger("rising"), .Pre_Clr_Positions("LEGACY"), .NegatePresetClear("false"), .enable("true"), .NewFFLayout("false")) d_ff_8 (
    .clk(CLK), .D(or_19_out), .Qn(IE), .en(or_20_out));  // open: Q, preset, reset
  Demultiplexer #(.select(2), .width(1), .tristate("false"), .disabled("Z"), .enable("false")) demultiplexer_1 (
    .out0(demultiplexer_1_out0), .out1(demultiplexer_1_out1), .out2(demultiplexer_1_out2), .in(\中断 ),
    .sel(\中断计数 ));  // open: out3
  Demultiplexer #(.select(2), .width(1), .tristate("false"), .disabled("Z"), .enable("false")) demultiplexer_2 (
    .out0(demultiplexer_2_out0), .out1(demultiplexer_2_out1), .out2(demultiplexer_2_out2), .in(\中断 ),
    .sel(\中断计数 ));  // open: out3
  RAM #(.addrWidth(10), .dataWidth(32), .bus("separate"), .Select("high")) ram_1 (
    .addr(MEM_AluResult[11:2]), .din(MDin), .data(ram_1_data), .str(MemWrite), .sel(1'b1), .clk(CLK),
    .ld(1'b1));  // open: clr
  Demultiplexer #(.select(2), .width(1), .tristate("false"), .disabled("Z"), .enable("false")) demultiplexer_3 (
    .out1(RESET1), .out2(RESET2), .out3(RESET3), .in(uret), .sel(\前中断号 ));  // open: out0
  Register #(.width(32), .trigger("rising"), .Select("low")) u_EPC (
    .D(\老PC ), .en(demultiplexer_1_out0), .Q(EPC_q), .clk(CLK));  // open: clr
  Register #(.width(32), .trigger("rising"), .Select("low")) EPC_2 (
    .D(\老PC ), .en(demultiplexer_1_out1), .Q(EPC_2_q), .clk(CLK));  // open: clr
  Register #(.width(32), .trigger("rising"), .Select("low")) EPC_3 (
    .D(\老PC ), .en(demultiplexer_1_out2), .Q(EPC_3_q), .clk(CLK));  // open: clr
  Register #(.width(2), .trigger("rising"), .Select("low")) EPC_4 (
    .D(\中断号 ), .en(demultiplexer_2_out0), .Q(EPC_4_q), .clk(CLK));  // open: clr
  Register #(.width(2), .trigger("rising"), .Select("low")) EPC_5 (
    .D(\中断号 ), .en(demultiplexer_2_out1), .Q(EPC_5_q), .clk(CLK));  // open: clr
  Register #(.width(2), .trigger("rising"), .Select("low")) EPC_6 (
    .D(\中断号 ), .en(demultiplexer_2_out2), .Q(EPC_6_q), .clk(CLK));  // open: clr
  Pull_Resistor #(.pull(0)) pull_resistor_6 (.node(RESET1));
  MEM_WB mem_wb_1 (
    .LBU(ex_mem_1_lbu_2), .MemToReg(ex_mem_1_memtoreg_2), .RegWrite(ex_mem_1_regwrite_2),
    .JAL(ex_mem_1_jal_2), .JALR(ex_mem_1_jalr_2), .URET(ex_mem_1_uret_2), .halt(ex_mem_1_halt_2),
    .rd(MEM_rd), .ALUresult(MEM_AluResult), .MemData(ram_1_data), .PC(M_PC), .PC_4(ex_mem_1_pc_4_2),
    .IR(MEM_IR), .LBU_2(mem_wb_1_lbu_2), .MemToReg_2(mem_wb_1_memtoreg_2), .RegWrite_2(RegWrite),
    .JAL_2(mem_wb_1_jal_2), .JALR_2(mem_wb_1_jalr_2), .halt_2(mem_wb_1_halt_2), .rd_2(\WB地址 ),
    .ALUresult_2(mem_wb_1_aluresult_2), .MemData_2(mem_wb_1_memdata_2), .PC_2(WB_PC),
    .PC_4_2(mem_wb_1_pc_4_2), .IR_2(WB_IR), .reset(1'b0), .flush(1'b0), .en(or_12_out), .CLK(CLK),
    .U_type(MemUtype), .U_type_2(mem_wb_1_u_type_2), .Uimm(MEM_Uimm), .Uimm_2(mem_wb_1_uimm_2));  // open: URET_2
  Multiplexer #(.select(2), .width(32), .disabled("Z"), .enable("false")) multiplexer_15 (
    .in1(EPC_q), .in2(EPC_2_q), .in3(EPC_3_q), .out(EPC), .sel(\中断计数 ));  // open: in0
  Multiplexer #(.select(2), .width(2), .disabled("Z"), .enable("false")) multiplexer_16 (
    .in1(EPC_4_q), .in2(EPC_5_q), .in3(EPC_6_q), .out(\前中断号 ), .sel(\中断计数 ));  // open: in0
  Pull_Resistor #(.pull(0)) pull_resistor_7 (.node(RESET2));
  or or_21 (or_22_out[1], mem_wb_1_jal_2, mem_wb_1_u_type_2, mem_wb_1_jalr_2);
  Pull_Resistor #(.pull(0)) pull_resistor_8 (.node(RESET3));
  or or_22 (or_22_out[0], mem_wb_1_memtoreg_2, mem_wb_1_u_type_2);
  Multiplexer #(.select(1), .width(32), .disabled("Z"), .enable("false")) multiplexer_17 (
    .in0(mem_wb_1_memdata_2), .in1(LBUData), .out(multiplexer_17_out), .sel(mem_wb_1_lbu_2));
  Multiplexer #(.select(2), .width(32), .disabled("Z"), .enable("false")) multiplexer_18 (
    .in0(mem_wb_1_aluresult_2), .in1(multiplexer_17_out), .in2(mem_wb_1_pc_4_2), .in3(mem_wb_1_uimm_2),
    .out(RDin), .sel(or_22_out));
  D_Flip_Flop #(.trigger("rising"), .Pre_Clr_Positions("ABOVE_BELOW"), .NegatePresetClear("false"), .enable("true"), .NewFFLayout("true")) d_ff_9 (
    .clk(mem_wb_1_halt_2), .D(1'b1), .Q(halt), .preset(1'b0), .en(1'b1), .reset(Go));  // open: Qn
  Multiplexer #(.select(2), .width(8), .disabled("Z"), .enable("false")) multiplexer_19 (
    .in0(mem_wb_1_memdata_2[7:0]), .in1(mem_wb_1_memdata_2[15:8]), .in2(mem_wb_1_memdata_2[23:16]),
    .in3(mem_wb_1_memdata_2[31:24]), .out(multiplexer_19_out), .sel(mem_wb_1_aluresult_2[1:0]));
  assign LBUData = {{24{1'b0}}, multiplexer_19_out};  // Bit_Extender bit_extender_5

  // Other names for the same wires on the sheet: MEM_PC[31:0] = M_PC

  // Notes on the sheet:
  //   中断源
  //   时空图监测，可删除
  //   中断等待指示
  //   数码管输出
  //   IF
  //   指令探针
  //   指令存储器
  //   多级中断测试信号模拟器
  //   contents of rom_1 (hex, n*v repeats v):
  //   100493 100006f 100493 200913 300993 100006f 100493 200913 300993 100006f 100493 200913 300993
  //   100006f 100493 200913 300993 3ec000ef 100413 100493 1f49493 900533 2200893 73 24d493 48463 fedff06f
  //   900533 2200893 73 100493 249493 900533 2200893 73 48463 fedff06f 100493 1f49493 900533 2200893 73
  //   4034d493 900533 2200893 73 4044d493 900533 2200893 73 4044d493 900533 2200893 73 4044d493 900533
  //   2200893 73 4044d493 900533 2200893 73 4044d493 900533 2200893 73 4044d493 900533 2200893 73 4044d493
  //   900533 2200893 73 100413 1f41993 41f9d993 433 c00913 300b13 140413 f47413 800293 100313 499993
  //   89e9b3 1300533 2200893 73 406282b3 fe0294e3 140413 f00f93 1f47433 1c41413 800293 100313 49d993
  //   89e9b3 1300533 2200893 73 406282b3 fe0294e3 1c45413 406b0b33 b0463 f95ff06f 2b3 fff2c293 829293
  //   ff2e293 500533 2200893 73 fff00413 493 84a023 140413 448493 84a023 140413 448493 84a023 140413
  //   448493 84a023 140413 448493 84a023 140413 448493 84a023 140413 448493 84a023 140413 448493 84a023
  //   140413 448493 84a023 140413 448493 84a023 140413 448493 84a023 140413 448493 84a023 140413 448493
  //   84a023 140413 448493 84a023 140413 448493 84a023 140413 448493 84a023 140413 448493 140413 433
  //   3c00493 42983 4aa03 149a2b3 28663 134a023 1442023 ffc48493 fe9412e3 800533 2200893 73 440413 3c00493
  //   fc9416e3 a00893 73 100293 300313 800493 849493 7648493 1449493 900533 2200893 73 800e13 4054d4b3
  //   4064d4b3 900533 2200893 73 fffe0e13 fe0e14e3 a00893 73 800e13 fedc04b7 fff00413 1045413 84e4b3
  //   900533 2200893 73 ba984b7 900533 73 76544b7 900533 73 32104b7 900533 73 fffe0e13 fa0e1ee3 a00893 73
  //   313 1000e13 13 8400493 849493 8348493 400913 891913 490913 849493 8248493 849493 8148493 891913
  //   490913 891913 490913 932023 12484b3 430313 fffe0e13 fe0e18e3 2000e13 313 30483 900533 2200893 73
  //   130313 fffe0e13 fe0e14e3 a00893 73 ff100493 900533 2200893 73 148493 fe9068e3 900533 2200893 73
  //   a00893 73 413 140413 800533 2200893 73 240413 800533 2200893 73 340413 800533 2200893 73 440413
  //   800533 2200893 73 540413 800533 2200893 73 640413 800533 2200893 73 740413 800533 2200893 73 840413
  //   800533 2200893 2200893 73 8067
  //   JAL
  //   JALR
  //   CSR
  //   rs1
  //   rs2
  //   rd
  //   I指令
  //   S指令
  //   B指令
  //   U指令
  //   J指令
  //   ID
  //   Beq
  //   Bne
  //   MemToReg
  //   MemWrite
  //   AluOP
  //   AluSrcB
  //   RegWrite
  //   控制位
  //   流水调试日志用
  //   暂停节拍，不能为0
  //   PC更新
  //   戳工具置1进入计数暂停模式，ctrl+k时钟自动运行到对应节拍暂停
  //   ctrl+k关闭时钟连续运行，将控制位置零，进入单步调试模式调试
  //   R1
  //   R2
  //   rd
  //   imm1
  //   imm2
  //   可计数暂停的时钟源
  //   中断使能
  //   EX
  //   中断计数
  //   为方便自动评测，需要输出流水线各段保存的PC值，注意是PC不是PC+4，另外ID段寄存器写入信息，Mem段内存写入信息也要输出
  //   ALUresult
  //   RegWrite
  //   MEM
  //   数据存储器
  //   保存中断号
  //   堆栈保存EPC
  //   MemtoReg
  //   JAL
  //   JALR
  //   LBU
  //   WB
endmodule
